// Digital circuit LCG-32.dig as structural Verilog
module LCG_32 (
  input  C_n,
  input  [31:0] P,
  input  [31:0] G,
  output G_o,
  output P_o,
  output C_o,
  output [31:0] C
);

  wire and_2_out, and_3_out, and_5_out, and_6_out, and_8_out, and_9_out, and_11_out, and_12_out, G0, G1, G2,
       G3, lcg_4_1_g, lcg_4_1_p, lcg_4_2_g, lcg_4_2_p, lcg_4_3_g, lcg_4_3_p, lcg_4_4_g, lcg_4_4_p, lcg_4_5_g,
       lcg_4_5_p, lcg_4_6_g, lcg_4_6_p, lcg_4_7_g, lcg_4_7_p, lcg_4_8_g, lcg_4_8_p, P0, P1, P2, P3;

  LCG_4C lcg_4c_1 (
    .G0(G0), .G1(G1), .G2(G2), .G3(G3), .P0(P0), .P1(P1), .P2(P2), .P3(P3), .C_n(C_n), .C_O(C_o), .G(G_o),
    .P(P_o), .C1(C[8]), .C2(C[16]), .C3(C[24]));
  LCG_4 lcg_4_1 (
    .G0(G[28]), .G1(G[29]), .G2(G[30]), .G3(G[31]), .P0(P[28]), .P1(P[29]), .P2(P[30]), .P3(P[31]),
    .C_n(C[28]), .G(lcg_4_1_g), .P(lcg_4_1_p), .C1(C[29]), .C2(C[30]), .C3(C[31]));
  LCG_4 lcg_4_2 (
    .G0(G[24]), .G1(G[25]), .G2(G[26]), .G3(G[27]), .P0(P[24]), .P1(P[25]), .P2(P[26]), .P3(P[27]),
    .C_n(C[24]), .G(lcg_4_2_g), .P(lcg_4_2_p), .C1(C[25]), .C2(C[26]), .C3(C[27]));
  LCG_4 lcg_4_3 (
    .G0(G[20]), .G1(G[21]), .G2(G[22]), .G3(G[23]), .P0(P[20]), .P1(P[21]), .P2(P[22]), .P3(P[23]),
    .C_n(C[20]), .G(lcg_4_3_g), .P(lcg_4_3_p), .C1(C[21]), .C2(C[22]), .C3(C[23]));
  LCG_4 lcg_4_4 (
    .G0(G[16]), .G1(G[17]), .G2(G[18]), .G3(G[19]), .P0(P[16]), .P1(P[17]), .P2(P[18]), .P3(P[19]),
    .C_n(C[16]), .G(lcg_4_4_g), .P(lcg_4_4_p), .C1(C[17]), .C2(C[18]), .C3(C[19]));
  LCG_4 lcg_4_5 (
    .G0(G[12]), .G1(G[13]), .G2(G[14]), .G3(G[15]), .P0(P[12]), .P1(P[13]), .P2(P[14]), .P3(P[15]),
    .C_n(C[12]), .G(lcg_4_5_g), .P(lcg_4_5_p), .C1(C[13]), .C2(C[14]), .C3(C[15]));
  LCG_4 lcg_4_6 (
    .G0(G[8]), .G1(G[9]), .G2(G[10]), .G3(G[11]), .P0(P[8]), .P1(P[9]), .P2(P[10]), .P3(P[11]), .C_n(C[8]),
    .G(lcg_4_6_g), .P(lcg_4_6_p), .C1(C[9]), .C2(C[10]), .C3(C[11]));
  LCG_4 lcg_4_7 (
    .G0(G[4]), .G1(G[5]), .G2(G[6]), .G3(G[7]), .P0(P[4]), .P1(P[5]), .P2(P[6]), .P3(P[7]), .C_n(C[4]),
    .G(lcg_4_7_g), .P(lcg_4_7_p), .C1(C[5]), .C2(C[6]), .C3(C[7]));
  LCG_4 lcg_4_8 (
    .G0(G[0]), .G1(G[1]), .G2(G[2]), .G3(G[3]), .P0(P[0]), .P1(P[1]), .P2(P[2]), .P3(P[3]), .C_n(C_n),
    .G(lcg_4_8_g), .P(lcg_4_8_p), .C1(C[1]), .C2(C[2]), .C3(C[3]));
  and and_1 (P3, lcg_4_2_p, lcg_4_1_p);
  and and_2 (and_2_out, lcg_4_1_p, lcg_4_2_g);
  and and_3 (and_3_out, lcg_4_2_p, C[24]);
  and and_4 (P2, lcg_4_4_p, lcg_4_3_p);
  and and_5 (and_5_out, lcg_4_3_p, lcg_4_4_g);
  and and_6 (and_6_out, lcg_4_4_p, C[16]);
  and and_7 (P1, lcg_4_6_p, lcg_4_5_p);
  and and_8 (and_8_out, lcg_4_5_p, lcg_4_6_g);
  and and_9 (and_9_out, lcg_4_6_p, C[8]);
  and and_10 (P0, lcg_4_8_p, lcg_4_7_p);
  and and_11 (and_11_out, lcg_4_7_p, lcg_4_8_g);
  and and_12 (and_12_out, lcg_4_8_p, C_n);
  or or_1 (G3, lcg_4_1_g, and_2_out);
  or or_2 (C[28], lcg_4_2_g, and_3_out);
  or or_3 (G2, lcg_4_3_g, and_5_out);
  or or_4 (C[20], lcg_4_4_g, and_6_out);
  or or_5 (G1, lcg_4_5_g, and_8_out);
  or or_6 (C[12], lcg_4_6_g, and_9_out);
  or or_7 (G0, lcg_4_7_g, and_11_out);
  or or_8 (C[4], lcg_4_8_g, and_12_out);

  assign C[0] = C_n;
endmodule
