// Digital circuit LCG-4C.dig as structural Verilog
module LCG_4C (
  input  G1,
  input  P1,
  input  G2,
  input  G3,
  input  G0,
  input  P2,
  input  P3,
  input  P0,
  input  C_n,
  output G,
  output P,
  output C2,
  output C3,
  output C1,
  output C_O
);

  wire or_1_out, or_2_out, or_3_out, or_4_out, or_5_out, or_6_out, or_7_out, or_8_out, or_9_out, or_10_out,
       or_11_out, or_12_out, or_13_out, or_14_out, or_15_out, or_16_out, or_17_out, or_18_out;

  or or_1 (or_1_out, C_n, G0, G1, G2, G3);
  or or_2 (or_2_out, G0, G1, P0, G2, G3);
  or or_3 (or_3_out, P1, G3, G2, G1);
  or or_4 (or_4_out, P2, G3, G2);
  or or_5 (or_5_out, P3, G3);
  and and_1 (P, P0, P1, P2, P3);
  or or_6 (or_6_out, G0, G1, G2, G3);
  or or_7 (or_7_out, P1, G3, G2, G1);
  or or_8 (or_8_out, P2, G3, G2);
  or or_9 (or_9_out, P3, G3);
  or or_10 (or_10_out, G2, G1, G0, C_n);
  or or_11 (or_11_out, P0, G2, G1, G0);
  or or_12 (or_12_out, P1, G2, G1);
  or or_13 (or_13_out, P2, G2);
  or or_14 (or_14_out, G1, G0, C_n);
  or or_15 (or_15_out, P0, G1, G0);
  or or_16 (or_16_out, P1, G1);
  or or_17 (or_17_out, G0, C_n);
  or or_18 (or_18_out, P0, G0);
  and and_2 (C_O, or_1_out, or_2_out, or_3_out, or_4_out, or_5_out);
  and and_3 (G, or_6_out, or_7_out, or_8_out, or_9_out);
  and and_4 (C3, or_10_out, or_11_out, or_12_out, or_13_out);
  and and_5 (C2, or_14_out, or_15_out, or_16_out);
  and and_6 (C1, or_17_out, or_18_out);
endmodule
