// Digital circuit LCGP-16.dig as structural Verilog
module LCGP_16 (
  input  C_n,
  input  [15:0] P,
  output P_o,
  output C_o,
  output [15:0] C
);

  wire P0, P1, P2, P3;

  LCGP_4C lcgp_4c_1 (
    .P0(P0), .P1(P1), .P2(P2), .P3(P3), .C_n(C_n), .C_O(C_o), .P(P_o), .C1(C[4]), .C2(C[8]), .C3(C[12]));
  LCGP_4 lcgp_4_1 (
    .P0(P[12]), .P1(P[13]), .P2(P[14]), .P3(P[15]), .C_n(C[12]), .P(P3), .C1(C[13]), .C2(C[14]), .C3(C[15]));
  LCGP_4 lcgp_4_2 (.P0(P[8]), .P1(P[9]), .P2(P[10]), .P3(P[11]), .C_n(C[8]), .P(P2), .C1(C[9]), .C2(C[10]), .C3(C[11]));
  LCGP_4 lcgp_4_3 (.P0(P[4]), .P1(P[5]), .P2(P[6]), .P3(P[7]), .C_n(C[4]), .P(P1), .C1(C[5]), .C2(C[6]), .C3(C[7]));
  LCGP_4 lcgp_4_4 (.P0(P[0]), .P1(P[1]), .P2(P[2]), .P3(P[3]), .C_n(C_n), .P(P0), .C1(C[1]), .C2(C[2]), .C3(C[3]));

  assign C[0] = C_n;
endmodule
