// Digital circuit LCGP-4.dig as structural Verilog
module LCGP_4 (
  input  P1,
  input  P2,
  input  P3,
  input  P0,
  input  C_n,
  output P,
  output C2,
  output C3,
  output C1
);

  and and_1 (P, P0, P1, P2, P3);
  and and_2 (C3, C_n, P0, P1, P2);
  and and_3 (C2, C_n, P0, P1);
  and and_4 (C1, C_n, P0);
endmodule
