// Digital circuit LCGP-4C.dig as structural Verilog
module LCGP_4C (
  input  P1,
  input  P2,
  input  P3,
  input  P0,
  input  C_n,
  output P,
  output C2,
  output C3,
  output C1,
  output C_O
);

  and and_1 (C_O, P3, P0, P1, P2, C_n);
  and and_2 (P, P0, P1, P2, P3);
  and and_3 (C3, C_n, P0, P1, P2);
  and and_4 (C2, C_n, P0, P1);
  and and_5 (C1, C_n, P0);
endmodule
