// Digital circuit ROB-PC.dig as structural Verilog
module ROB_PC (
  input  [31:0] D,
  input  [3:0] inst,
  input  [3:0] com_id,
  input  E,
  input  C,
  input  [3:0] read_id,
  output [31:0] D1,
  output [31:0] D2
);

  RegisterFile #(.AddrBits(4), .Bits(32)) registerfile_1 (
    .Din(D), .we(E), .Rw(inst), .C(C), .Ra(com_id), .Rb(read_id), .Da(D1), .Db(D2));
endmodule
