// Digital circuit add-4c32.dig as structural Verilog
module add_4c32 (
  input  [3:0] b,
  input  [31:0] a,
  output [31:0] s,
  output c
);

  wire add_1_c_o;
  wire [27:0] lcgp_28_1_c;

  Add #(.Bits(4)) add_1 (.a(a[3:0]), .b(b), .c_i(1'b0), .s(s[3:0]), .c_o(add_1_c_o));
  LCGP_28 lcgp_28_1 (.P(a[31:4]), .C_n(add_1_c_o), .C_o(c), .C(lcgp_28_1_c));  // open: P_o
  assign s[31:4] = lcgp_28_1_c ^ a[31:4];  // XOr xor_1, 28 bits wide

  // Notes on the sheet:
  //   b: second input to add
  //   a: first input to add
  //   s: the result of the addition
  //   c: carry output. If set there was an overflow.
endmodule
