// Digital circuit add-s16c32.dig as structural Verilog
module add_s16c32 (
  input  [15:0] b,
  input  [31:0] a,
  output [31:0] s,
  output c
);

  wire lcg_16_1_c_o, xor_3_out;
  wire [15:0] and_1_out, bitextender_1_out, lcg_16_1_c, lcgp_16_1_c, xor_1_out, xor_2_out;

  BitExtender #(.inputBits(1)) bitextender_1 (.in(b[15]), .out(bitextender_1_out));
  assign and_1_out = a[15:0] & b;  // And and_1, 16 bits wide
  assign xor_1_out = a[15:0] ^ b;  // XOr xor_1, 16 bits wide
  assign xor_2_out = a[31:16] ^ bitextender_1_out;  // XOr xor_2, 16 bits wide
  xor xor_3 (xor_3_out, lcg_16_1_c_o, b[15]);
  LCGP_16 lcgp_16_1 (.P(xor_2_out), .C_n(xor_3_out), .C_o(c), .C(lcgp_16_1_c));  // open: P_o
  LCG_16 lcg_16_1 (.G(and_1_out), .P(xor_1_out), .C_n(1'b0), .C_o(lcg_16_1_c_o), .C(lcg_16_1_c));  // open: G_o, P_o
  assign s[31:16] = lcgp_16_1_c ^ a[31:16];  // XOr xor_4, 16 bits wide
  assign s[15:0] = lcg_16_1_c ^ xor_1_out;  // XOr xor_5, 16 bits wide

  // Notes on the sheet:
  //   b: second input to add
  //   a: first input to add
  //   s: the result of the addition
  //   c: carry output. If set there was an overflow.
endmodule
