// Digital circuit BTB-buff.dig as structural Verilog
module BTB_buff (
  input  C,
  input  [3:0] inst,
  input  [3:0] rd_id,
  input  [35:0] BTB_I,
  input  rd,
  input  E,
  output [35:0] BTB_O,
  output full
);

  wire and_1_out, and_3_out, and_4_out, and_5_out, CMP_M1, CMP_M2, CMP_M3, CMP_M4, E_M1, E_M2, E_M3, E_M4,
       priority_4_1_v, V_M1, V_M2, V_M3, V_M4;
  wire [1:0] priorityencoder_1_num;
  wire [3:0] and_2_out, not_1_out, register_2_q, register_4_q, register_6_q, register_8_q;
  wire [35:0] D_M1, D_M2, D_M3, D_M4;

  and and_1 (and_1_out, ~E_M1, rd, CMP_M1);  // And
  RS_FF rs_ff_1 (.S(E_M1), .C(C), .R(and_1_out), .Q(V_M1));  // open: nQ
  Register #(.Bits(36)) register_1 (.D(BTB_I), .C(C), .en(E_M1), .Q(D_M1));
  Register #(.Bits(4)) register_2 (.D(inst), .C(C), .en(E_M1), .Q(register_2_q));
  Comparator #(.Bits(4)) comparator_1 (.a(register_2_q), .b(rd_id), .eq(CMP_M1));  // open: gt, lt
  assign and_2_out = {V_M4, V_M3, V_M2, V_M1} & {CMP_M4, CMP_M3, CMP_M2, CMP_M1};  // And and_2, 4 bits wide
  assign not_1_out = ~{V_M4, V_M3, V_M2, V_M1};  // Not not_1, 4 bits wide
  and and_3 (and_3_out, ~E_M2, rd, CMP_M2);  // And
  priority_4 priority_4_1 (
    .on(E), .in1(not_1_out[0]), .in2(not_1_out[1]), .in3(not_1_out[2]), .in4(not_1_out[3]), .out1(E_M1),
    .out2(E_M2), .out3(E_M3), .out4(E_M4), .v(priority_4_1_v));
  PriorityEncoder #(.Selector_Bits(2)) priorityencoder_1 (
    .in0(and_2_out[0]), .in1(and_2_out[1]), .in2(and_2_out[2]), .in3(and_2_out[3]),
    .num(priorityencoder_1_num));  // open: any
  RS_FF rs_ff_2 (.S(E_M2), .C(C), .R(and_3_out), .Q(V_M2));  // open: nQ
  Register #(.Bits(36)) register_3 (.D(BTB_I), .C(C), .en(E_M2), .Q(D_M2));
  Register #(.Bits(4)) register_4 (.D(inst), .C(C), .en(E_M2), .Q(register_4_q));
  Comparator #(.Bits(4)) comparator_2 (.a(register_4_q), .b(rd_id), .eq(CMP_M2));  // open: gt, lt
  not not_2 (full, priority_4_1_v);
  Multiplexer #(.Selector_Bits(2), .Bits(36)) multiplexer_1 (
    .sel(priorityencoder_1_num), .in_0(D_M1), .in_1(D_M2), .in_2(D_M3), .in_3(D_M4), .out(BTB_O));
  and and_4 (and_4_out, ~E_M3, rd, CMP_M3);  // And
  RS_FF rs_ff_3 (.S(E_M3), .C(C), .R(and_4_out), .Q(V_M3));  // open: nQ
  Register #(.Bits(36)) register_5 (.D(BTB_I), .C(C), .en(E_M3), .Q(D_M3));
  Register #(.Bits(4)) register_6 (.D(inst), .C(C), .en(E_M3), .Q(register_6_q));
  Comparator #(.Bits(4)) comparator_3 (.a(register_6_q), .b(rd_id), .eq(CMP_M3));  // open: gt, lt
  and and_5 (and_5_out, ~E_M4, rd, CMP_M4);  // And
  RS_FF rs_ff_4 (.S(E_M4), .C(C), .R(and_5_out), .Q(V_M4));  // open: nQ
  Register #(.Bits(36)) register_7 (.D(BTB_I), .C(C), .en(E_M4), .Q(D_M4));
  Register #(.Bits(4)) register_8 (.D(inst), .C(C), .en(E_M4), .Q(register_8_q));
  Comparator #(.Bits(4)) comparator_4 (.a(register_8_q), .b(rd_id), .eq(CMP_M4));  // open: gt, lt

  // Other names for the same wires on the sheet: CMP = rd; CMP_ID[3:0] = rd_id

  // Notes on the sheet:
  //   BTB_I: inst data
  //   E: inst data
endmodule
