// Digital circuit BTB.dig as structural Verilog
module BTB (
  input  [3:0] id,
  input  [11:0] tag,
  input  E,
  input  C,
  input  [1:0] pred,
  input  [31:0] tar,
  input  [3:0] R1_id,
  input  [11:0] R1_tag,
  input  [3:0] R2_id,
  input  [11:0] R2_tag,
  input  V_in,
  output [31:0] tar_O1,
  output J_1,
  output [31:0] tar_O2,
  output [1:0] pred_O2,
  output V_2,
  output J_2
);

  wire comparator_1_eq, comparator_2_eq, F_V1, F_V2;
  wire [1:0] predict_O1;
  wire [11:0] tag_O1, tag_O2;

  Comparator #(.Bits(12)) comparator_1 (.a(tag_O1), .b(R1_tag), .eq(comparator_1_eq));  // open: gt, lt
  Comparator #(.Bits(12)) comparator_2 (.a(tag_O2), .b(R2_tag), .eq(comparator_2_eq));  // open: gt, lt
  RegisterFile #(.AddrBits(4), .Bits(47)) registerfile_1 (
    .Din({V_in, pred, tag, tar}), .we(E), .Rw(id), .C(C), .Ra(R1_id), .Rb(R2_id),
    .Da({F_V1, predict_O1, tag_O1, tar_O1}), .Db({F_V2, pred_O2, tag_O2, tar_O2}));
  and and_1 (J_1, F_V1, predict_O1[1], comparator_1_eq);
  and and_2 (V_2, F_V2, comparator_2_eq);
  and and_3 (J_2, comparator_2_eq, pred_O2[1], F_V2);

  // Other names for the same wires on the sheet: target_O1[31:0] = tar_O1; target_O2[31:0] = tar_O2;
  //   predict_O2[1:0] = pred_O2; index[3:0] = id; predict[1:0] = pred; target[31:0] = tar
endmodule
