// Digital circuit cpu-32-scalar.dig as structural Verilog
module cpu_32_scalar (
  input  C,
  input  bus_e,
  input  E,
  input  [31:0] I_D__bus,
  input  [31:0] D_D__bus,
  input  [31:0] I_A__bus,
  input  [31:0] D_A__bus,
  input  INT_nor,
  input  INT_nmk,
  input  run,
  input  I_valid,
  input  D_valid,
  output I_LD,
  output D_LD,
  output D_ST,
  output [1:0] MMU_sel,
  output MMU_str,
  output [2:0] DMA_sel,
  output DMA_str,
  output INT_str,
  output CLK_str,
  output [1:0] CSH_mode,
  output CSH_run,
  output INT_out,
  output [1:0] D_MD
);

  wire add_4c32_1_c, alu_32_1_p6, alu_32_1_p8, alu_e, and_2_out, and_3_out, and_4_out, and_9_out, and_10_out,
       and_11_out, and_12_out, and_13_out, and_14_out, and_15_out, and_19_out, and_20_out, and_21_out,
       and_22_out, and_23_out, and_25_out, and_26_out, and_27_out, and_28_out, and_29_out, and_30_out,
       and_31_out, and_32_out, and_33_out, and_34_out, and_35_out, and_36_out, and_37_out, and_38_out,
       and_39_out, and_40_out, and_41_out, and_43_out, and_45_out, and_47_out, and_48_out, and_49_out,
       and_50_out, and_51_out, and_53_out, and_56_out, and_62_out, and_63_out, and_64_out, and_65_out, C_ct,
       cm_e, cm_e__bf, com1, com1_M, com2, comparator_1_gt, comparator_2_eq, CT_ALU__M2, CT_block,
       CT_BUS__DAG, CT_BUS__DAM, CT_BUS__DAR, CT_BUS__DDG, CT_BUS__DDM, CT_BUS__DDR, CT_BUS__IAG,
       CT_BUS__IAR, CT_BUS__IDM, CT_BUS__IDR, CT_DEP__EA, CT_DEP__EB, CT_DEP__EOA, CT_DEP__OFLE,
       CT_DEP__OFLS, CT_DEP__OSCE, CT_DEP__OSCS, CT_DEP__STA, CT_DEP__STB, CT_DISP, CT_haz, CT_MVR, CT_RAW,
       CT_RF__DM, CT_RF__E, CT_RF__FLS, CT_RF__PCH, CT_RF__PCJ, CT_RF__PCR, CT_RF__PCSE, CT_RF__SCAE,
       CT_RF__SCD, CT_RF__SCS, CT_RF__SCSE, DC_B_q, dc_e, DC_q, dispatch, dp_e, dp_e__bf, ecm_e__bf,
       ex_e__bf, ex_nop, ft_e, FT_q, H_full, hlt, id_full, id_gen_1_v, int_run, kernel_inst, mode,
       multiplexer_4_out, multiplexer_7_out, multiplexer_8_out, multiplexer_10_out, multiplexer_12_out,
       multiplexer_14_out, multiplexer_16_out, multiplexer_17_out, multiplexer_18_out, nand_1_out,
       nand_2_out, nand_3_out, nor_2_out, nor_4_out, nor_6_out, nor_7_out, nor_8_out, not_1_out, not_2_out,
       not_4_out, not_6_out, not_7_out, not_8_out, not_9_out, or_7_out, or_8_out, or_9_out, or_10_out,
       or_23_out, or_24_out, or_25_out, or_26_out, register_8_q, register_9_q, register_12_q, register_13_q,
       register_14_q, register_15_q, register_16_q, register_17_q, register_21_q, register_22_q,
       register_25_q, register_27_q, register_28_q, register_29_q, register_30_q, register_31_q,
       register_35_q, register_36_q, register_37_q, register_38_q, register_39_q, register_40_q,
       register_41_q, register_42_q, register_43_q, register_44_q, register_45_q, rf_e, rollback, st_e__bf,
       xor_1_out, xor_2_out, xor_3_out, xor_4_out, xor_5_out;
  wire [0:0] and_59_out;
  wire [1:0] and_42_out, CT_ALU__M, register_11_q;
  wire [1:1] and_44_out;
  wire [2:0] and_1_out, and_5_out, and_6_out, and_7_out, and_8_out, and_55_out, and_58_out,
       bitextender_1_out, CT_BUS__DASDN, CT_DEP__OFL, CT_DEP__OMA, CT_DEP__OMB, CT_DEP__OSC, CT_DEP__UFL,
       CT_DEP__UMA, CT_DEP__UMB, CT_DEP__USC, CT_RF__MA, CT_RF__MB, CT_RF__SCN, CT_RF__WM, EOB_p15, EOB_p16,
       EOB_p17, EOB_p18, multiplexer_11_out, multiplexer_13_out, or_1_out, or_4_out, or_6_out, register_18_q,
       register_20_q, register_23_q, register_24_q, register_26_q, register_32_q;
  wire [2:1] and_57_out;
  wire [3:0] CT_RF__FLE;
  wire [3:3] register_20_q_2;
  wire [4:0] com1_inst, com2_inst, CT_DEP__ORA, CT_DEP__ORB, CT_DEP__URA, CT_DEP__URB, CT_RF__RA, CT_RF__RB,
       CT_RF__WS, EXT_CM_q, FL_inst, PC_inst, SC_inst;
  wire [7:0] ALU_F, ALU_T__F, and_52_out, bitextender_3_out, bitextender_4_out, byte0, byte0_iv, byte1,
       byte1_ex, byte1_st, byte2, byte2_ex, byte3, byte3_ex, register_19_q, xor_6_out;
  wire [8:0] CT_ALU__A;
  wire [9:8] fl_i;
  wire [10:0] and_24_out, multiplexer_6_out, register_10_q;
  wire [23:0] inst_iv;
  wire [31:0] add_1_s, add_4c32_1_s, alu_32_1_p10, ALU_R, ALU_T__R, bitextender_2_out, bitextender_5_out,
       D_A__R_q, FL, I_A__R_q, I_D__R_q, multiplexer_2_out, multiplexer_3_out, multiplexer_9_out,
       multiplexer_15_out, mVec, OD_D__R_q, pca_i, PCS, PCS_d1, PCS_d2, pcs_i, R_A, R_B, SCS, scs_i,
       sub_4c32_1_s;

  nor nor_1 (or_1_out[0], CT_DEP__OMA[0], CT_DEP__OMA[1]);
  nor nor_2 (nor_2_out, CT_DEP__OMA[0], CT_DEP__OMA[1], CT_DEP__OMA[2]);
  xor xor_1 (xor_1_out, CT_DEP__OMA[0], CT_DEP__OMA[1]);
  BitExtender #(.inputBits(1), .outputBits(3)) bitextender_1 (.in(CT_DEP__EOA), .out(bitextender_1_out));
  or or_1 (or_1_out[1], CT_DEP__OMA[0], nor_2_out);
  or or_2 (or_1_out[2], nor_2_out, xor_1_out);
  not not_1 (not_1_out, ex_nop);
  assign and_1_out = bitextender_1_out & or_1_out;  // And and_1, 3 bits wide
  nor nor_3 (or_4_out[0], CT_DEP__UMA[0], CT_DEP__UMA[1]);
  nor nor_4 (nor_4_out, CT_DEP__UMA[0], CT_DEP__UMA[1], CT_DEP__UMA[2]);
  xor xor_2 (xor_2_out, CT_DEP__UMA[0], CT_DEP__UMA[1]);
  nor nor_5 (or_6_out[0], CT_DEP__UMB[0], CT_DEP__UMB[1]);
  nor nor_6 (nor_6_out, CT_DEP__UMB[0], CT_DEP__UMB[1], CT_DEP__UMB[2]);
  xor xor_3 (xor_3_out, CT_DEP__UMB[0], CT_DEP__UMB[1]);
  and and_2 (and_2_out, not_1_out, CT_DEP__STA, dp_e);
  or or_3 (or_4_out[1], CT_DEP__UMA[0], nor_4_out);
  or or_4 (or_4_out[2], nor_4_out, xor_2_out);
  or or_5 (or_6_out[1], CT_DEP__UMB[0], nor_6_out);
  or or_6 (or_6_out[2], nor_6_out, xor_3_out);
  // reg_scoreboard EOB: pin names not known; wires that end beside it: C_ct, and_2_out, CT_DEP__STB, and_1_out, CT_DEP__ORA, CT_DEP__ORB, CT_DEP__URA, CT_DEP__URB, CT_DEP__OSC, CT_DEP__OSCS, CT_DEP__OSCE, CT_DEP__OFL, CT_DEP__OFLS, CT_DEP__OFLE, EOB_p15, EOB_p16, EOB_p17, EOB_p18
  and and_3 (and_3_out, CT_DEP__URA[0], CT_DEP__URA[1]);
  xor xor_4 (xor_4_out, CT_DEP__URA[2], CT_DEP__URA[3]);
  and and_4 (and_4_out, CT_DEP__URB[0], CT_DEP__URB[1]);
  xor xor_5 (xor_5_out, CT_DEP__URB[2], CT_DEP__URB[3]);
  assign and_5_out = EOB_p15 & or_4_out;  // And and_5, 3 bits wide
  assign and_6_out = EOB_p16 & or_6_out;  // And and_6, 3 bits wide
  assign and_7_out = EOB_p17 & CT_DEP__USC;  // And and_7, 3 bits wide
  assign and_8_out = EOB_p18 & CT_DEP__UFL;  // And and_8, 3 bits wide
  nand nand_1 (nand_1_out, and_3_out, xor_4_out);
  nand nand_2 (nand_2_out, and_4_out, xor_5_out);
  or or_7 (or_7_out, and_5_out[0], and_5_out[1], and_5_out[2]);
  or or_8 (or_8_out, and_6_out[0], and_6_out[1], and_6_out[2]);
  or or_9 (or_9_out, and_7_out[0], and_7_out[1], and_7_out[2]);
  or or_10 (or_10_out, and_8_out[0], and_8_out[1], and_8_out[2]);
  and and_9 (and_9_out, nand_1_out, CT_DEP__EA);
  and and_10 (and_10_out, nand_2_out, CT_DEP__EB);
  and and_11 (and_11_out, or_7_out, and_9_out);
  and and_12 (and_12_out, or_8_out, and_10_out);
  Comparator #(.Bits(32)) comparator_1 (.a(PCS), .b(mVec), .gt(comparator_1_gt));  // open: eq, lt
  or or_11 (CT_haz, CT_RAW, CT_block);
  DipSwitch dipswitch_1 (.out(CT_block));
  or or_12 (CT_RAW, and_11_out, and_12_out, or_9_out, or_10_out);
  BitExtender #(.inputBits(16), .outputBits(32)) bitextender_2 (.in({byte2_ex, byte3_ex}), .out(bitextender_2_out));
  and and_13 (and_13_out, FL[14], INT_nor);
  and and_14 (and_14_out, 1'b0, ~comparator_1_gt);  // And
  Add #(.Bits(32)) add_1 (.a(R_A), .b(bitextender_2_out), .c_i(1'b0), .s(add_1_s));  // open: c_o
  or or_13 (int_run, and_13_out, INT_nmk);
  RS_FF u_mode (.S(and_14_out), .C(C), .R(comparator_1_gt), .Q(mode));  // open: nQ
  Register #(.Bits(32)) MVR (.D(add_1_s), .C(C), .en(CT_MVR), .Q(mVec));
  and and_15 (and_15_out, CT_haz, dp_e);
  assign CT_RF__PCSE = ft_e ? 1'b1 : 1'bz;  // Driver driver_1
  assign CT_BUS__IAR = ft_e ? 1'b1 : 1'bz;  // Driver driver_2
  assign CT_BUS__IAG = ft_e ? 1'b1 : 1'bz;  // Driver driver_3
  assign I_LD = ft_e ? 1'b1 : 1'bz;  // Driver driver_4
  id_gen id_gen_1 (
    .C(C), .\use (dispatch), .com1(com1), .com1_id(com1_inst), .com2(com2), .com2_id(com2_inst),
    .id(PC_inst), .V(id_gen_1_v));
  RS_FF FT (.S(run), .C(C_ct), .R(hlt), .Q(FT_q));  // open: nQ
  not not_2 (not_2_out, and_15_out);
  assign ex_nop = and_15_out ? 1'b1 : 1'bz;  // Driver driver_5
  not not_3 (id_full, id_gen_1_v);
  and and_16 (dispatch, CT_DISP, dp_e__bf);
  and and_17 (ft_e, FT_q, not_2_out);
  Register DC_B (.D(FT_q), .C(C), .en(1'b1), .Q(DC_B_q));
  Register #(.Bits(32)) register_1 (.D(PCS), .C(C), .en(CT_RF__PCSE), .Q(PCS_d1));
  Register DC (.D(FT_q), .C(C_ct), .en(1'b1), .Q(DC_q));
  not not_4 (not_4_out, I_valid);
  DipSwitch dipswitch_2 (.out(rollback));
  and and_18 (dc_e, DC_q, not_2_out);
  Register DP_B (.D(DC_B_q), .C(C), .en(1'b1), .Q(dp_e__bf));
  Register #(.Bits(32)) register_2 (.D(PCS_d1), .C(C), .en(CT_RF__PCSE), .Q(PCS_d2));
  assign CT_BUS__IDM = not_4_out ? 1'b1 : 1'bz;  // Driver driver_6
  Register #(.Bits(5)) EX (.D(PC_inst), .C(C), .en(dp_e), .Q(SC_inst));
  Register DP (.D(DC_q), .C(C_ct), .en(1'b1), .Q(dp_e));
  Register #(.Bits(5)) ST (.D(SC_inst), .C(C), .en(alu_e), .Q(FL_inst));
  Register EX_B (.D(dp_e__bf), .C(C), .en(1'b1), .Q(ex_e__bf));
  Register #(.Bits(32)) register_3 (.D(PCS_d2), .C(C), .en(CT_RF__PCSE), .Q(pca_i));
  Register EX_2 (.D(dp_e), .C(C_ct), .en(1'b1), .Q(alu_e));
  Register #(.Bits(5)) CM (.D(FL_inst), .C(C), .en(rf_e), .Q(com2_inst));
  PullDown pulldown_1 (.out(com2));
  PullDown #(.Bits(5)) pulldown_2 (.out(com2_inst));
  PullDown pulldown_3 (.out(com1));
  PullDown #(.Bits(5)) pulldown_4 (.out(com1_inst));
  PullDown pulldown_5 (.out(rollback));
  Register ST_B (.D(ex_e__bf), .C(C), .en(1'b1), .Q(st_e__bf));
  not not_5 (C_ct, C);
  Register ST_2 (.D(alu_e), .C(C_ct), .en(1'b1), .Q(rf_e));
  Register #(.Bits(5)) EXT_CM (.D(com2_inst), .C(C), .en(rf_e), .Q(EXT_CM_q));
  PullDown pulldown_6 (.out(com1_M));
  Register CM_B___EXT_B (.D(st_e__bf), .C(C), .en(1'b1), .Q(cm_e__bf));
  Multiplexer #(.Bits(5)) multiplexer_1 (.sel(com1_M), .in_0(com2_inst), .in_1(EXT_CM_q), .out(com1_inst));
  Register CM___EXT (.D(rf_e), .C(C_ct), .en(1'b1), .Q(cm_e));
  Register EXT_CM_B (.D(cm_e__bf), .C(C), .en(1'b1), .Q(ecm_e__bf));
  Register #(.Bits(8)) register_4 (.D(byte1), .C(C_ct), .en(ex_e__bf), .Q(byte1_ex));
  Register #(.Bits(8)) register_5 (.D(byte2), .C(C_ct), .en(ex_e__bf), .Q(byte2_ex));
  Register #(.Bits(8)) register_6 (.D(byte3), .C(C_ct), .en(ex_e__bf), .Q(byte3_ex));
  PullDown pulldown_7 (.out(CT_DISP));
  Register #(.Bits(8)) register_7 (.D(byte1_ex), .C(C_ct), .en(st_e__bf), .Q(byte1_st));
  sub_4c32 sub_4c32_1 (.a(SCS), .b({1'b0, CT_BUS__DASDN}), .s(sub_4c32_1_s));
  and and_19 (and_19_out, byte0[3], byte0[0]);
  and and_20 (and_20_out, byte0[2], byte0[0]);
  and and_21 (and_21_out, byte0_iv[3], byte0_iv[2], byte0[1], byte0_iv[0]);
  and and_22 (and_22_out, byte0_iv[4], byte0[3], byte0[2], byte0[1]);
  and and_23 (and_23_out, byte0[4], byte0_iv[3], byte0_iv[2], byte0[1], byte0[0]);
  and and_24 (and_24_out[7], byte0_iv[4], byte0[3], byte0[2]);
  and and_25 (and_25_out, byte0[4], byte0[2], byte0_iv[1]);
  and and_26 (and_26_out, byte0[4], byte0_iv[3], byte0_iv[2]);
  and and_27 (and_27_out, byte0_iv[4], byte0_iv[3], byte0_iv[2]);
  and and_28 (and_28_out, byte0_iv[4], byte0_iv[3]);
  and and_29 (and_29_out, byte0_iv[4], byte0[3], byte0_iv[2], byte0_iv[1]);
  and and_30 (and_30_out, byte0_iv[4], byte0[3], byte0_iv[2]);
  and and_31 (and_31_out, byte0[4], byte0[3]);
  and and_32 (and_32_out, byte0_iv[4], byte0_iv[3], byte0[2], byte0_iv[1]);
  and and_33 (and_33_out, byte0[4], byte0[2], byte0[1]);
  and and_34 (and_34_out, byte0_iv[4], byte0_iv[3], byte0_iv[2], byte0[1], byte0[0]);
  and and_35 (and_35_out, byte0_iv[2], byte0_iv[0]);
  and and_36 (and_36_out, byte0[2], byte0[0]);
  and and_37 (and_37_out, byte0[1], byte0[2], byte0[4]);
  and and_38 (and_38_out, byte0[3], byte0[4]);
  Multiplexer #(.Bits(32)) multiplexer_2 (
    .sel(CT_BUS__DAM), .in_0(ALU_R), .in_1(sub_4c32_1_s), .out(multiplexer_2_out));
  or or_14 (and_24_out[10], and_19_out, and_20_out, and_21_out);
  or or_15 (and_24_out[6], and_25_out, and_22_out, and_23_out);
  or or_16 (and_24_out[5], and_24_out[7], and_25_out, and_26_out);
  or or_17 (and_24_out[4], and_32_out, and_33_out, and_27_out);
  or or_18 (and_24_out[3], and_28_out, and_33_out, and_29_out);
  or or_19 (and_24_out[2], and_30_out, and_31_out);
  or or_20 (and_24_out[1], and_32_out, and_33_out, and_34_out);
  or or_21 (and_24_out[0], byte0[3], byte0[1], and_35_out, and_36_out);
  nor nor_7 (nor_7_out, and_37_out, and_38_out);
  and and_39 (and_39_out, ft_e, CT_BUS__IAR);
  Multiplexer #(.Bits(32)) multiplexer_3 (
    .sel(CT_BUS__IDM), .in_0(I_D__bus), .in_1(32'h72000000), .out(multiplexer_3_out));
  and and_40 (and_40_out, alu_e, CT_BUS__DAR);
  and and_41 (and_41_out, alu_e, CT_BUS__DDR);
  or or_22 (and_42_out[1], CT_RF__PCH, CT_RF__PCR);
  and and_42 (and_42_out[0], ~CT_RF__PCH, CT_RF__PCJ);  // And
  nor nor_8 (nor_8_out, CT_RF__PCR, CT_RF__PCJ);
  and and_43 (and_43_out, byte0_iv[0], byte0_iv[1], byte0[2], byte0[3], byte0[4], byte0_iv[5], byte0_iv[6], byte0_iv[7]);
  and and_44 (and_44_out[1], byte0[1], byte0_iv[2], byte0[3], byte0[4], byte0_iv[5], byte0_iv[6], byte0_iv[7]);
  add_4c32 add_4c32_1 (.a(PCS), .b(4'b0100), .s(add_4c32_1_s), .c(add_4c32_1_c));
  Register #(.Bits(32)) I_A__R (.D(PCS), .C(C), .en(and_39_out), .Q(I_A__R_q));
  Register #(.Bits(32)) I_D__R (.D(multiplexer_3_out), .C(C), .en(dc_e), .Q(I_D__R_q));
  Register #(.Bits(32)) D_A__R (.D(multiplexer_2_out), .C(C), .en(and_40_out), .Q(D_A__R_q));
  Register #(.Bits(32)) OD_D__R (.D(R_B), .C(C), .en(and_41_out), .Q(OD_D__R_q));
  and and_45 (and_45_out, byte0[4], byte0[3], byte0_iv[1], byte0_iv[2], byte0_iv[5], byte0_iv[6], byte0_iv[7]);
  Multiplexer multiplexer_4 (.sel(ex_nop), .in_0(nor_7_out), .in_1(1'b0), .out(multiplexer_4_out));
  Register register_8 (.D(multiplexer_4_out), .C(C_ct), .en(ex_e__bf), .Q(register_8_q));
  Register register_9 (.D(register_8_q), .C(C_ct), .en(st_e__bf), .Q(register_9_q));
  Multiplexer #(.Selector_Bits(2), .Bits(32)) multiplexer_5 (
    .sel(and_42_out), .in_0(add_4c32_1_s), .in_1(ALU_T__R), .in_2(pca_i), .in_3(D_D__bus), .out(pcs_i));
  and and_46 (fl_i[8], add_4c32_1_c, nor_8_out);
  assign I_A__bus = and_47_out ? I_A__R_q : 32'bz;  // Driver driver_7
  D_FF #(.Bits(32)) INST (.D(I_D__R_q), .C(C_ct), .Q({byte0, byte1, byte2, byte3}), .nQ({byte0_iv, inst_iv}));
  assign D_A__bus = and_48_out ? D_A__R_q : 32'bz;  // Driver driver_8
  assign D_D__bus = and_49_out ? OD_D__R_q : 32'bz;  // Driver driver_9
  Multiplexer #(.Bits(11)) multiplexer_6 (
    .sel(ex_nop), .in_0({and_24_out[10], 2'b00, and_24_out[7:0]}), .in_1({11{1'b0}}), .out(multiplexer_6_out));
  BitExtender #(.inputBits(1), .outputBits(8)) bitextender_3 (.in(register_9_q), .out(bitextender_3_out));
  or or_23 (or_23_out, and_43_out, and_44_out[1]);
  and and_47 (and_47_out, CT_BUS__IAG, bus_e);
  and and_48 (and_48_out, CT_BUS__DAG, bus_e);
  and and_49 (and_49_out, CT_BUS__DDG, bus_e);
  and and_50 (and_50_out, byte0_iv[7], byte0_iv[6], byte0_iv[5], byte0_iv[4]);
  and and_51 (and_51_out, byte0_iv[7], byte0_iv[6], byte0_iv[5], byte0[4], byte0_iv[3]);
  Multiplexer multiplexer_7 (.sel(ex_nop), .in_0(or_24_out), .in_1(1'b0), .out(multiplexer_7_out));
  Register #(.Bits(11)) register_10 (.D(multiplexer_6_out), .C(C_ct), .en(ex_e__bf), .Q(register_10_q));
  assign and_52_out = byte1_st & bitextender_3_out;  // And and_52, 8 bits wide
  Register #(.Bits(2)) register_11 (.D({and_44_out[1], byte0[0]}), .C(C_ct), .en(ex_e__bf), .Q(register_11_q));
  not not_6 (not_6_out, and_24_out[10]);
  Multiplexer multiplexer_8 (.sel(ex_nop), .in_0(or_23_out), .in_1(1'b0), .out(multiplexer_8_out));
  or or_24 (or_24_out, and_50_out, and_45_out, and_51_out);
  assign CT_DEP__STA = or_24_out ? nor_7_out : 1'bz;  // Driver driver_10
  assign CT_DEP__EA = or_24_out ? 1'b1 : 1'bz;  // Driver driver_11
  assign CT_DEP__EB = or_24_out ? not_6_out : 1'bz;  // Driver driver_12
  assign CT_DEP__EOA = or_24_out ? 1'b1 : 1'bz;  // Driver driver_13
  assign {CT_DEP__URA, CT_DEP__UMA} = or_24_out ? byte1 : 8'bz;  // Driver driver_14
  assign {CT_DEP__URB, CT_DEP__UMB} = or_24_out ? byte2 : 8'bz;  // Driver driver_15
  assign {CT_DEP__ORA, CT_DEP__OMA} = or_24_out ? byte1 : 8'bz;  // Driver driver_16
  assign CT_DEP__OFL = or_24_out ? 3'b001 : 3'bz;  // Driver driver_17
  assign CT_DEP__OFLS = or_24_out ? 1'b1 : 1'bz;  // Driver driver_18
  assign CT_DEP__OFLE = or_24_out ? 1'b1 : 1'bz;  // Driver driver_19
  assign CT_DISP = multiplexer_7_out ? 1'b1 : 1'bz;  // Driver driver_20
  Register register_12 (.D(multiplexer_7_out), .C(C_ct), .en(ex_e__bf), .Q(register_12_q));
  assign {CT_RF__RA, CT_RF__MA} = register_12_q ? byte1_ex : 8'bz;  // Driver driver_21
  assign {CT_RF__RB, CT_RF__MB} = register_12_q ? byte2_ex : 8'bz;  // Driver driver_22
  assign CT_ALU__A = register_12_q ? register_10_q[8:0] : 9'bz;  // Driver driver_23
  assign CT_ALU__M = register_12_q ? register_10_q[10:9] : 2'bz;  // Driver driver_24
  assign CT_DEP__STB = register_12_q ? register_8_q : 1'bz;  // Driver driver_25
  assign {CT_DEP__ORB, CT_DEP__OMB} = register_12_q ? byte1_ex : 8'bz;  // Driver driver_26
  assign CT_DEP__OFLS = register_12_q ? 1'b1 : 1'bz;  // Driver driver_27
  assign CT_DEP__OFLE = register_12_q ? 1'b1 : 1'bz;  // Driver driver_28
  Register register_13 (.D(register_12_q), .C(C_ct), .en(st_e__bf), .Q(register_13_q));
  assign {CT_RF__WS, CT_RF__WM} = register_13_q ? and_52_out : 8'bz;  // Driver driver_29
  assign CT_RF__E = register_13_q ? register_9_q : 1'bz;  // Driver driver_30
  assign CT_RF__FLS = register_13_q ? 1'b1 : 1'bz;  // Driver driver_31
  assign CT_RF__FLE = register_13_q ? 4'b0001 : 4'bz;  // Driver driver_32
  Register register_14 (.D(register_13_q), .C(C_ct), .en(cm_e__bf), .Q(register_14_q));
  assign com1 = register_14_q ? 1'b1 : 1'bz;  // Driver driver_33
  assign CT_DEP__EA = and_43_out ? 1'b1 : 1'bz;  // Driver driver_34
  assign CT_DEP__STA = or_23_out ? 1'b1 : 1'bz;  // Driver driver_35
  assign CT_DEP__EOA = or_23_out ? 1'b1 : 1'bz;  // Driver driver_36
  assign {CT_DEP__URA, CT_DEP__UMA} = or_23_out ? byte2 : 8'bz;  // Driver driver_37
  assign {CT_DEP__ORA, CT_DEP__OMA} = or_23_out ? byte1 : 8'bz;  // Driver driver_38
  assign CT_DISP = multiplexer_8_out ? 1'b1 : 1'bz;  // Driver driver_39
  Register register_15 (.D(multiplexer_8_out), .C(C_ct), .en(ex_e__bf), .Q(register_15_q));
  assign CT_ALU__M = register_15_q ? register_11_q : 2'bz;  // Driver driver_40
  assign {CT_RF__RA, CT_RF__MA} = register_15_q ? 8'hd0 : 8'bz;  // Driver driver_41
  assign {CT_RF__RB, CT_RF__MB} = register_15_q ? byte2_ex : 8'bz;  // Driver driver_42
  assign CT_ALU__A = register_15_q ? 9'h9 : 9'bz;  // Driver driver_43
  assign CT_DEP__STB = register_15_q ? 1'b1 : 1'bz;  // Driver driver_44
  assign {CT_DEP__ORB, CT_DEP__OMB} = register_15_q ? byte1_ex : 8'bz;  // Driver driver_45
  Register register_16 (.D(register_15_q), .C(C_ct), .en(st_e__bf), .Q(register_16_q));
  assign {CT_RF__WS, CT_RF__WM} = register_16_q ? byte1_st : 8'bz;  // Driver driver_46
  assign CT_RF__E = register_16_q ? 1'b1 : 1'bz;  // Driver driver_47
  Register register_17 (.D(register_16_q), .C(C_ct), .en(cm_e__bf), .Q(register_17_q));
  assign com1 = register_17_q ? 1'b1 : 1'bz;  // Driver driver_48
  and and_53 (and_53_out, rf_e, CT_RF__E);
  PullDown pulldown_8 (.out(CT_RF__SCAE));
  Multiplexer #(.Bits(32)) multiplexer_9 (.sel(CT_RF__DM), .in_0(ALU_T__R), .in_1(D_D__bus), .out(multiplexer_9_out));
  BitExtender #(.inputBits(1), .outputBits(8)) bitextender_4 (.in(register_20_q_2[3]), .out(bitextender_4_out));
  // regFile3 regfile3_1: pin names not known; wires that end beside it: C, and_53_out, multiplexer_9_out, CT_RF__WS, CT_RF__WM, CT_RF__RA, CT_RF__MA, CT_RF__RB, CT_RF__MB, pcs_i, CT_RF__PCSE, scs_i, CT_RF__SCS, CT_RF__SCSE, {FL[31:10], fl_i, ALU_T__F}, CT_RF__FLS, CT_RF__FLE, R_A, R_B, PCS, SCS, FL, FL_inst, PC_inst, SC_inst, FL_inst, rollback, com2, com2_inst, com1, com1_inst, H_full
  assign xor_6_out = FL[7:0] ^ bitextender_4_out;  // XOr xor_6, 8 bits wide
  not not_7 (not_7_out, byte1_ex[1]);
  or or_25 (or_25_out, byte1_ex[2], byte1_ex[0]);
  and and_54 (and_55_out[2], byte0_iv[7], byte0_iv[6], byte0[5]);
  and and_55 (and_55_out[1], byte0_iv[7], byte0[6], byte0_iv[5]);
  or or_26 (or_26_out, byte1_ex[0], byte1_ex[2]);
  and and_56 (and_56_out, byte0_iv[4], byte0[5], byte0[6], byte0_iv[7]);
  Multiplexer #(.Selector_Bits(3)) multiplexer_10 (
    .sel(register_20_q), .in_0(xor_6_out[0]), .in_1(xor_6_out[1]), .in_2(xor_6_out[2]), .in_3(xor_6_out[3]),
    .in_4(xor_6_out[4]), .in_5(xor_6_out[5]), .in_6(xor_6_out[6]), .in_7(xor_6_out[7]),
    .out(multiplexer_10_out));
  and and_57 (and_57_out[1], not_7_out, or_25_out);
  nor nor_9 (and_57_out[2], byte1_ex[2], byte1_ex[1], byte1_ex[0]);
  not not_8 (not_8_out, byte1_ex[1]);
  Comparator #(.Bits(3)) comparator_2 (.a(byte0[2:0]), .b(3'b110), .eq(comparator_2_eq));  // open: gt, lt
  not not_9 (not_9_out, byte0[0]);
  and and_58 (and_58_out[0], byte0[1], byte0[2], byte0[3], byte0[4], byte0_iv[5], byte0_iv[6], byte0_iv[7]);
  Register #(.Bits(3)) register_18 (.D({and_57_out, byte1_ex[1]}), .C(C_ct), .en(st_e__bf), .Q(register_18_q));
  or or_27 (and_55_out[0], and_55_out[2], and_55_out[1]);
  Register #(.Bits(8)) register_19 (.D({byte0[4:0], 3'b000}), .C(C_ct), .en(ex_e__bf), .Q(register_19_q));
  and and_59 (and_59_out[0], or_26_out, not_8_out);
  Register #(.Bits(4)) register_20 (.D(byte0[3:0]), .C(C_ct), .en(ex_e__bf), .Q({register_20_q_2[3], register_20_q}));
  Register register_21 (.D(and_62_out), .C(C_ct), .en(st_e__bf), .Q(register_21_q));
  Register register_22 (.D(register_21_q), .C(C_ct), .en(cm_e__bf), .Q(register_22_q));
  and and_60 (and_58_out[1], and_58_out[0], byte0[0]);
  and and_61 (and_58_out[2], not_9_out, and_58_out[0]);
  Multiplexer #(.Bits(3)) multiplexer_11 (.sel(ex_nop), .in_0(and_58_out), .in_1(3'b000), .out(multiplexer_11_out));
  nand nand_3 (nand_3_out, and_56_out, comparator_2_eq);
  Multiplexer multiplexer_12 (.sel(ex_nop), .in_0(and_56_out), .in_1(1'b0), .out(multiplexer_12_out));
  assign com1 = register_22_q ? 1'b1 : 1'bz;  // Driver driver_49
  Multiplexer #(.Bits(3)) multiplexer_13 (.sel(ex_nop), .in_0(and_55_out), .in_1(3'b000), .out(multiplexer_13_out));
  and and_62 (and_62_out, register_28_q, ~multiplexer_10_out);  // And
  assign CT_DEP__EA = and_58_out[0] ? 1'b1 : 1'bz;  // Driver driver_50
  assign CT_DEP__EOA = and_58_out[0] ? 1'b1 : 1'bz;  // Driver driver_51
  assign {CT_DEP__ORA, CT_DEP__OMA} = and_58_out[0] ? byte1 : 8'bz;  // Driver driver_52
  assign {CT_DEP__URA, CT_DEP__UMA} = and_58_out[0] ? 8'hf0 : 8'bz;  // Driver driver_53
  assign CT_DEP__STA = and_58_out[2] ? 1'b1 : 1'bz;  // Driver driver_54
  assign CT_DEP__EB = and_58_out[1] ? 1'b1 : 1'bz;  // Driver driver_55
  assign {CT_DEP__URB, CT_DEP__UMB} = and_58_out[1] ? byte1 : 8'bz;  // Driver driver_56
  assign CT_DISP = multiplexer_11_out[0] ? 1'b1 : 1'bz;  // Driver driver_57
  Register #(.Bits(3)) register_23 (.D(multiplexer_11_out), .C(C_ct), .en(ex_e__bf), .Q(register_23_q));
  assign CT_BUS__DAM = register_23_q[0] ? 1'b1 : 1'bz;  // Driver driver_58
  assign CT_BUS__DAR = register_23_q[0] ? 1'b1 : 1'bz;  // Driver driver_59
  assign {CT_RF__RB, CT_RF__MB} = register_23_q[1] ? byte1_ex : 8'bz;  // Driver driver_60
  assign CT_BUS__DDR = register_23_q[1] ? 1'b1 : 1'bz;  // Driver driver_61
  assign CT_DEP__STB = register_23_q[2] ? 1'b1 : 1'bz;  // Driver driver_62
  assign {CT_DEP__ORB, CT_DEP__OMB} = register_23_q[2] ? byte1_ex : 8'bz;  // Driver driver_63
  assign CT_BUS__DASDN = register_23_q[2] ? {and_57_out, byte1_ex[1]} : 3'bz;  // Driver driver_64
  Register #(.Bits(3)) register_24 (.D(register_23_q), .C(C_ct), .en(st_e__bf), .Q(register_24_q));
  assign CT_BUS__DAG = register_24_q[0] ? 1'b1 : 1'bz;  // Driver driver_65
  assign CT_RF__SCSE = register_24_q[0] ? 1'b1 : 1'bz;  // Driver driver_66
  assign CT_RF__SCS = register_24_q[0] ? 1'b1 : 1'bz;  // Driver driver_67
  assign D_ST = register_24_q[1] ? 1'b1 : 1'bz;  // Driver driver_68
  assign CT_RF__SCN = register_24_q[1] ? register_18_q : 3'bz;  // Driver driver_69
  assign CT_BUS__DDG = register_24_q[1] ? 1'b1 : 1'bz;  // Driver driver_70
  assign D_LD = register_24_q[2] ? 1'b1 : 1'bz;  // Driver driver_71
  assign CT_RF__SCD = register_24_q[2] ? 1'b1 : 1'bz;  // Driver driver_72
  assign CT_RF__SCN = register_24_q[2] ? register_18_q : 3'bz;  // Driver driver_73
  assign CT_RF__DM = register_24_q[2] ? 1'b1 : 1'bz;  // Driver driver_74
  assign {CT_RF__WS, CT_RF__WM} = register_24_q[2] ? byte1_st : 8'bz;  // Driver driver_75
  assign CT_RF__E = register_24_q[2] ? 1'b1 : 1'bz;  // Driver driver_76
  Register register_25 (.D(register_24_q[0]), .C(C_ct), .en(cm_e__bf), .Q(register_25_q));
  assign com1 = register_25_q ? 1'b1 : 1'bz;  // Driver driver_77
  assign CT_DEP__EA = and_55_out[0] ? 1'b1 : 1'bz;  // Driver driver_78
  assign {CT_DEP__URA, CT_DEP__UMA} = and_55_out[0] ? {byte0[4:0], 3'b000} : 8'bz;  // Driver driver_79
  assign CT_DEP__EB = and_55_out[1] ? 1'b1 : 1'bz;  // Driver driver_80
  assign {CT_DEP__URB, CT_DEP__UMB} = and_55_out[1] ? byte1 : 8'bz;  // Driver driver_81
  assign CT_DEP__STA = and_55_out[2] ? 1'b1 : 1'bz;  // Driver driver_82
  assign CT_DEP__EOA = and_55_out[2] ? 1'b1 : 1'bz;  // Driver driver_83
  assign {CT_DEP__ORA, CT_DEP__OMA} = and_55_out[2] ? byte1 : 8'bz;  // Driver driver_84
  assign D_MD = register_32_q[0] ? {byte1_ex[1], and_59_out[0]} : 2'bz;  // Driver driver_85
  assign {CT_RF__RA, CT_RF__MA} = register_32_q[0] ? register_19_q : 8'bz;  // Driver driver_86
  assign CT_ALU__A = register_32_q[0] ? 9'h19 : 9'bz;  // Driver driver_87
  assign CT_ALU__M = register_32_q[0] ? 2'b11 : 2'bz;  // Driver driver_88
  assign CT_BUS__DAR = register_32_q[0] ? 1'b1 : 1'bz;  // Driver driver_89
  assign {CT_RF__RB, CT_RF__MB} = register_32_q[1] ? byte1_ex : 8'bz;  // Driver driver_90
  assign CT_BUS__DDR = register_32_q[1] ? 1'b1 : 1'bz;  // Driver driver_91
  assign CT_DEP__STB = register_32_q[2] ? 1'b1 : 1'bz;  // Driver driver_92
  assign {CT_DEP__ORB, CT_DEP__OMB} = register_32_q[2] ? byte1_ex : 8'bz;  // Driver driver_93
  Register #(.Bits(3)) register_26 (.D(register_32_q), .C(C_ct), .en(st_e__bf), .Q(register_26_q));
  assign CT_BUS__DAG = register_26_q[0] ? 1'b1 : 1'bz;  // Driver driver_94
  assign D_ST = register_26_q[1] ? 1'b1 : 1'bz;  // Driver driver_95
  assign CT_BUS__DDG = register_26_q[1] ? 1'b1 : 1'bz;  // Driver driver_96
  assign D_LD = register_26_q[2] ? 1'b1 : 1'bz;  // Driver driver_97
  assign CT_RF__DM = register_26_q[2] ? 1'b1 : 1'bz;  // Driver driver_98
  assign {CT_RF__WS, CT_RF__WM} = register_26_q[2] ? byte1_st : 8'bz;  // Driver driver_99
  assign CT_RF__E = register_26_q[2] ? 1'b1 : 1'bz;  // Driver driver_100
  Register register_27 (.D(register_26_q[0]), .C(C_ct), .en(cm_e__bf), .Q(register_27_q));
  assign com1 = register_27_q ? 1'b1 : 1'bz;  // Driver driver_101
  assign CT_DEP__EA = and_56_out ? 1'b1 : 1'bz;  // Driver driver_102
  assign {CT_DEP__URA, CT_DEP__UMA} = and_56_out ? byte1 : 8'bz;  // Driver driver_103
  assign CT_DEP__EB = and_56_out ? nand_3_out : 1'bz;  // Driver driver_104
  assign {CT_DEP__URB, CT_DEP__UMB} = and_56_out ? 8'hf8 : 8'bz;  // Driver driver_105
  assign CT_DISP = multiplexer_12_out ? 1'b1 : 1'bz;  // Driver driver_106
  Register register_28 (.D(multiplexer_12_out), .C(C_ct), .en(ex_e__bf), .Q(register_28_q));
  assign ex_nop = multiplexer_14_out ? 1'b1 : 1'bz;  // Driver driver_107
  assign CT_BUS__IDM = multiplexer_14_out ? 1'b1 : 1'bz;  // Driver driver_108
  assign CT_ALU__A = multiplexer_14_out ? 9'h19 : 9'bz;  // Driver driver_109
  assign CT_ALU__M = multiplexer_14_out ? 2'b11 : 2'bz;  // Driver driver_110
  assign {CT_RF__RA, CT_RF__MA} = multiplexer_14_out ? byte1_ex : 8'bz;  // Driver driver_111
  Register register_29 (.D(multiplexer_14_out), .C(C_ct), .en(st_e__bf), .Q(register_29_q));
  assign CT_RF__PCSE = register_29_q ? 1'b1 : 1'bz;  // Driver driver_112
  assign CT_RF__PCJ = register_29_q ? 1'b1 : 1'bz;  // Driver driver_113
  assign CT_BUS__IDM = register_29_q ? 1'b1 : 1'bz;  // Driver driver_114
  Register register_30 (.D(register_29_q), .C(C_ct), .en(cm_e__bf), .Q(register_30_q));
  assign CT_BUS__IDM = register_30_q ? 1'b1 : 1'bz;  // Driver driver_115
  Register register_31 (.D(register_30_q), .C(C_ct), .en(ecm_e__bf), .Q(register_31_q));
  assign com1 = register_31_q ? 1'b1 : 1'bz;  // Driver driver_116
  assign com1_M = register_31_q ? 1'b1 : 1'bz;  // Driver driver_117
  BitExtender #(.inputBits(16), .outputBits(32)) bitextender_5 (.in({byte2_ex, byte3_ex}), .out(bitextender_5_out));
  assign CT_DISP = multiplexer_13_out[0] ? 1'b1 : 1'bz;  // Driver driver_118
  Register #(.Bits(3)) register_32 (.D(multiplexer_13_out), .C(C_ct), .en(ex_e__bf), .Q(register_32_q));
  Multiplexer multiplexer_14 (.sel(multiplexer_10_out), .in_0(1'b0), .in_1(register_28_q), .out(multiplexer_14_out));
  Multiplexer #(.Selector_Bits(2), .Bits(32)) multiplexer_15 (
    .sel(CT_ALU__M), .in_0(R_B), .in_1({{24{1'b0}}, byte3_ex}), .in_2({{16{1'b0}}, byte2_ex, byte3_ex}),
    .in_3(bitextender_5_out), .out(multiplexer_15_out));
  Register #(.Bits(32)) register_33 (.D(ALU_R), .C(C), .en(alu_e), .Q(ALU_T__R));
  Register #(.Bits(8)) register_34 (.D(ALU_F), .C(C), .en(alu_e), .Q(ALU_T__F));
  // alu_32 alu_32_1: pin names not known; wires that end beside it: R_A, multiplexer_15_out, FL, CT_ALU__A, CT_RF__WM, alu_32_1_p6, alu_32_1_p6, alu_32_1_p8, alu_32_1_p8, alu_32_1_p10, alu_32_1_p10, ALU_R, ALU_F
  PullDown #(.Bits(32)) pulldown_9 (.out(alu_32_1_p10));
  addsub_4c32 addsub_4c32_1 (.a(SCS), .b({1'b0, CT_RF__SCN}), .sub(CT_RF__SCD), .s(scs_i), .c(fl_i[9]));
  and and_63 (and_63_out, byte0[0], byte0_iv[1], byte0_iv[2], byte0_iv[3], byte0[4], byte0[5], byte0[6], byte0_iv[7]);
  and and_64 (and_64_out, byte0_iv[0], byte0_iv[1], byte0_iv[2], byte0_iv[3], byte0[4], byte0[5], byte0[6], byte0_iv[7]);
  and and_65 (and_65_out, byte0[0], byte0[1], byte0_iv[2], byte0_iv[3], byte0[4], byte0[5], byte0[6], byte0_iv[7]);
  Multiplexer multiplexer_16 (.sel(ex_nop), .in_0(and_65_out), .in_1(1'b0), .out(multiplexer_16_out));
  PullDown pulldown_10 (.out(kernel_inst));
  PullDown pulldown_11 (.out(CT_RF__E));
  PullDown pulldown_12 (.out(CT_RF__DM));
  PullDown #(.Bits(5)) pulldown_13 (.out(CT_RF__WS));
  PullDown #(.Bits(3)) pulldown_14 (.out(CT_RF__WM));
  PullDown #(.Bits(5)) pulldown_15 (.out(CT_RF__RA));
  PullDown #(.Bits(3)) pulldown_16 (.out(CT_RF__MA));
  PullDown #(.Bits(5)) pulldown_17 (.out(CT_RF__RB));
  PullDown #(.Bits(3)) pulldown_18 (.out(CT_RF__MB));
  PullDown pulldown_19 (.out(CT_RF__PCSE));
  PullDown pulldown_20 (.out(CT_RF__PCJ));
  PullDown pulldown_21 (.out(CT_RF__PCR));
  PullDown #(.Bits(3)) pulldown_22 (.out(CT_RF__SCN));
  PullDown pulldown_23 (.out(CT_RF__SCD));
  PullDown pulldown_24 (.out(CT_RF__SCS));
  PullDown pulldown_25 (.out(CT_RF__SCSE));
  PullDown pulldown_26 (.out(CT_RF__FLS));
  PullDown #(.Bits(4)) pulldown_27 (.out(CT_RF__FLE));
  PullDown #(.Bits(9)) pulldown_28 (.out(CT_ALU__A));
  PullDown #(.Bits(2)) pulldown_29 (.out(CT_ALU__M));
  PullDown pulldown_30 (.out(CT_ALU__M2));
  PullDown pulldown_31 (.out(CT_BUS__IAR));
  PullDown pulldown_32 (.out(CT_BUS__IAG));
  PullDown pulldown_33 (.out(CT_BUS__IDR));
  PullDown pulldown_34 (.out(CT_BUS__IDM));
  PullDown pulldown_35 (.out(CT_BUS__DAR));
  PullDown pulldown_36 (.out(CT_BUS__DAM));
  PullDown pulldown_37 (.out(CT_BUS__DAG));
  PullDown pulldown_38 (.out(CT_BUS__DDR));
  PullDown pulldown_39 (.out(CT_BUS__DDG));
  PullDown pulldown_40 (.out(I_LD));
  PullDown pulldown_41 (.out(D_LD));
  PullDown pulldown_42 (.out(D_ST));
  PullDown #(.Bits(2)) pulldown_43 (.out(D_MD));
  PullDown pulldown_44 (.out(CT_MVR));
  Multiplexer multiplexer_17 (.sel(ex_nop), .in_0(and_64_out), .in_1(1'b0), .out(multiplexer_17_out));
  Multiplexer multiplexer_18 (.sel(ex_nop), .in_0(and_63_out), .in_1(1'b0), .out(multiplexer_18_out));
  assign CT_DEP__EA = and_64_out ? 1'b1 : 1'bz;  // Driver driver_119
  assign {CT_DEP__URA, CT_DEP__UMA} = and_64_out ? byte1 : 8'bz;  // Driver driver_120
  assign CT_DISP = multiplexer_17_out ? 1'b1 : 1'bz;  // Driver driver_121
  Register register_35 (.D(multiplexer_17_out), .C(C_ct), .en(ex_e__bf), .Q(register_35_q));
  assign ex_nop = register_35_q ? 1'b1 : 1'bz;  // Driver driver_122
  assign CT_BUS__IDM = register_35_q ? 1'b1 : 1'bz;  // Driver driver_123
  assign {CT_RF__RA, CT_RF__MA} = register_35_q ? byte1_ex : 8'bz;  // Driver driver_124
  assign CT_ALU__A = register_35_q ? 9'h19 : 9'bz;  // Driver driver_125
  assign CT_ALU__M = register_35_q ? 2'b11 : 2'bz;  // Driver driver_126
  assign {CT_RF__RB, CT_RF__MB} = register_35_q ? 8'he8 : 8'bz;  // Driver driver_127
  assign CT_BUS__DAM = register_35_q ? 1'b1 : 1'bz;  // Driver driver_128
  assign CT_BUS__DAR = register_35_q ? 1'b1 : 1'bz;  // Driver driver_129
  assign CT_BUS__DDR = register_35_q ? 1'b1 : 1'bz;  // Driver driver_130
  Register register_36 (.D(register_35_q), .C(C_ct), .en(st_e__bf), .Q(register_36_q));
  assign CT_BUS__IDM = register_36_q ? 1'b1 : 1'bz;  // Driver driver_131
  assign CT_RF__SCSE = register_36_q ? 1'b1 : 1'bz;  // Driver driver_132
  assign CT_RF__SCS = register_36_q ? 1'b1 : 1'bz;  // Driver driver_133
  assign CT_RF__SCN = register_36_q ? 3'b100 : 3'bz;  // Driver driver_134
  assign CT_RF__PCSE = register_36_q ? 1'b1 : 1'bz;  // Driver driver_135
  assign CT_RF__PCJ = register_36_q ? 1'b1 : 1'bz;  // Driver driver_136
  assign CT_BUS__DAG = register_36_q ? 1'b1 : 1'bz;  // Driver driver_137
  assign CT_BUS__DDG = register_36_q ? 1'b1 : 1'bz;  // Driver driver_138
  assign D_ST = register_36_q ? 1'b1 : 1'bz;  // Driver driver_139
  Register register_37 (.D(register_36_q), .C(C_ct), .en(cm_e__bf), .Q(register_37_q));
  assign CT_BUS__IDM = register_37_q ? 1'b1 : 1'bz;  // Driver driver_140
  Register register_38 (.D(register_37_q), .C(C_ct), .en(ecm_e__bf), .Q(register_38_q));
  assign com1 = register_38_q ? 1'b1 : 1'bz;  // Driver driver_141
  assign com1_M = register_38_q ? 1'b1 : 1'bz;  // Driver driver_142
  assign CT_DISP = multiplexer_18_out ? 1'b1 : 1'bz;  // Driver driver_143
  Register register_39 (.D(multiplexer_18_out), .C(C_ct), .en(ex_e__bf), .Q(register_39_q));
  assign ex_nop = register_39_q ? 1'b1 : 1'bz;  // Driver driver_144
  assign CT_BUS__IDM = register_39_q ? 1'b1 : 1'bz;  // Driver driver_145
  assign CT_BUS__DAM = register_39_q ? 1'b1 : 1'bz;  // Driver driver_146
  assign CT_BUS__DAR = register_39_q ? 1'b1 : 1'bz;  // Driver driver_147
  assign CT_BUS__DASDN = register_39_q ? 3'b100 : 3'bz;  // Driver driver_148
  Register register_40 (.D(register_39_q), .C(C_ct), .en(st_e__bf), .Q(register_40_q));
  assign CT_BUS__IDM = register_40_q ? 1'b1 : 1'bz;  // Driver driver_149
  assign D_LD = register_40_q ? 1'b1 : 1'bz;  // Driver driver_150
  assign CT_RF__SCSE = register_40_q ? 1'b1 : 1'bz;  // Driver driver_151
  assign CT_RF__SCD = register_40_q ? 1'b1 : 1'bz;  // Driver driver_152
  assign CT_RF__SCN = register_40_q ? 3'b100 : 3'bz;  // Driver driver_153
  assign CT_RF__SCS = register_40_q ? 1'b1 : 1'bz;  // Driver driver_154
  assign CT_RF__PCSE = register_40_q ? 1'b1 : 1'bz;  // Driver driver_155
  assign CT_RF__PCJ = register_40_q ? 1'b1 : 1'bz;  // Driver driver_156
  assign CT_RF__PCR = register_40_q ? 1'b1 : 1'bz;  // Driver driver_157
  assign CT_BUS__DAG = register_40_q ? 1'b1 : 1'bz;  // Driver driver_158
  Register register_41 (.D(register_40_q), .C(C_ct), .en(cm_e__bf), .Q(register_41_q));
  assign CT_BUS__IDM = register_41_q ? 1'b1 : 1'bz;  // Driver driver_159
  assign CT_BUS__IDM = register_41_q ? 1'b1 : 1'bz;  // Driver driver_160
  Register register_42 (.D(register_41_q), .C(C_ct), .en(ecm_e__bf), .Q(register_42_q));
  assign com1 = register_42_q ? 1'b1 : 1'bz;  // Driver driver_161
  assign com1_M = register_42_q ? 1'b1 : 1'bz;  // Driver driver_162
  assign CT_DISP = multiplexer_16_out ? 1'b1 : 1'bz;  // Driver driver_163
  Register register_43 (.D(multiplexer_16_out), .C(C_ct), .en(ex_e__bf), .Q(register_43_q));
  assign ex_nop = register_43_q ? 1'b1 : 1'bz;  // Driver driver_164
  assign hlt = register_43_q ? 1'b1 : 1'bz;  // Driver driver_165
  assign CT_BUS__IDM = register_43_q ? 1'b1 : 1'bz;  // Driver driver_166
  assign CT_BUS__IDM = register_43_q ? 1'b1 : 1'bz;  // Driver driver_167
  Register register_44 (.D(register_43_q), .C(C_ct), .en(st_e__bf), .Q(register_44_q));
  assign CT_RF__PCH = register_44_q ? 1'b1 : 1'bz;  // Driver driver_168
  assign CT_RF__PCSE = register_44_q ? 1'b1 : 1'bz;  // Driver driver_169
  assign CT_BUS__IDM = register_44_q ? 1'b1 : 1'bz;  // Driver driver_170
  Register register_45 (.D(register_44_q), .C(C_ct), .en(cm_e__bf), .Q(register_45_q));
  assign com1 = register_45_q ? 1'b1 : 1'bz;  // Driver driver_171
  PullDown pulldown_45 (.out(CT_DEP__STA));
  PullDown pulldown_46 (.out(CT_DEP__STB));
  PullDown pulldown_47 (.out(CT_DEP__EA));
  PullDown pulldown_48 (.out(CT_DEP__EB));
  PullDown pulldown_49 (.out(CT_DEP__EOA));
  PullDown #(.Bits(5)) pulldown_50 (.out(CT_DEP__URA));
  PullDown #(.Bits(3)) pulldown_51 (.out(CT_DEP__UMA));
  PullDown #(.Bits(5)) pulldown_52 (.out(CT_DEP__URB));
  PullDown #(.Bits(3)) pulldown_53 (.out(CT_DEP__UMB));
  PullDown #(.Bits(5)) pulldown_54 (.out(CT_DEP__ORA));
  PullDown #(.Bits(3)) pulldown_55 (.out(CT_DEP__OMA));
  PullDown #(.Bits(5)) pulldown_56 (.out(CT_DEP__ORB));
  PullDown #(.Bits(3)) pulldown_57 (.out(CT_DEP__OSC));
  PullDown pulldown_58 (.out(CT_DEP__OSCS));
  PullDown pulldown_59 (.out(CT_DEP__OSCE));
  PullDown #(.Bits(3)) pulldown_60 (.out(CT_DEP__OFL));
  PullDown pulldown_61 (.out(CT_DEP__OFLS));
  PullDown pulldown_62 (.out(CT_DEP__OFLE));
  PullDown #(.Bits(3)) pulldown_63 (.out(CT_DEP__USC));
  PullDown #(.Bits(3)) pulldown_64 (.out(CT_DEP__UFL));
  PullDown #(.Bits(3)) pulldown_65 (.out(CT_BUS__DASDN));
  PullDown pulldown_66 (.out(CT_BUS__DDM));
  PullDown pulldown_67 (.out(CT_RF__PCH));
  PullDown pulldown_68 (.out(hlt));
  PullDown pulldown_69 (.out(ex_nop));

  assign CLK_str = 1'b0;
  assign CSH_mode = 2'b00;
  assign CSH_run = 1'b0;
  assign DMA_sel = 3'b000;
  assign DMA_str = 1'b0;
  assign INT_out = 1'b0;
  assign INT_str = 1'b0;
  assign MMU_sel = 2'b00;
  assign MMU_str = 1'b0;

  // Other names for the same wires on the sheet: fl_i (some bits) = {FL[31:10], ALU_T__F};
  //   imm16_2_ex[15:0] = {byte2_ex, byte3_ex}; C_dt = C; C_i = C; ex_e = alu_e; ext_e = cm_e; ext_e__bf = cm_e__bf;
  //   int_proc = FL[14]; trap = FL[15]; GR_inst[4:0] = FL_inst; inst[31:0] = {byte0, byte1, byte2, byte3};
  //   inst_iv[31:24] = byte0_iv; pc_ov = fl_i[8]; PCS_d3[31:0] = pca_i; sc_ov = fl_i[9]; st_e = rf_e

  // Notes on the sheet:
  //   C: Hz: 16
  //   bus_e: default 1
  //   D_MD: 0:32
  //   1:16
  //   2:8
  //   3:u.u
  //   I_valid: default 1
  //   D_valid: default 1
  //   pipeline controller
  //   dependence circuit
  //   kernal mode system
  //   interrupt system
  //   inst id manager
  //   IO pins
  //   primeary signals
  //   decode circuit
  //   ALU
  //   register
  //   program counter controller
  //   bus system
  //   register system
  //   stack
  //   RAM
  //   jump
  //   ALU system
  //   flag circuit
  //   stack circuit
  //   call
  //   return
  //   halt
  //   control bus
endmodule
