// Digital circuit LCG-16.dig as structural Verilog
module LCG_16 (
  input  C_n,
  input  [15:0] P,
  input  [15:0] G,
  output G_o,
  output P_o,
  output C_o,
  output [15:0] C
);

  wire G0, G1, G2, G3, P0, P1, P2, P3;

  LCG_4C lcg_4c_1 (
    .G0(G0), .G1(G1), .G2(G2), .G3(G3), .P0(P0), .P1(P1), .P2(P2), .P3(P3), .C_n(C_n), .C_O(C_o), .G(G_o),
    .P(P_o), .C1(C[4]), .C2(C[8]), .C3(C[12]));
  LCG_4 lcg_4_1 (
    .G0(G[12]), .G1(G[13]), .G2(G[14]), .G3(G[15]), .P0(P[12]), .P1(P[13]), .P2(P[14]), .P3(P[15]),
    .C_n(C[12]), .G(G3), .P(P3), .C1(C[13]), .C2(C[14]), .C3(C[15]));
  LCG_4 lcg_4_2 (
    .G0(G[8]), .G1(G[9]), .G2(G[10]), .G3(G[11]), .P0(P[8]), .P1(P[9]), .P2(P[10]), .P3(P[11]), .C_n(C[8]),
    .G(G2), .P(P2), .C1(C[9]), .C2(C[10]), .C3(C[11]));
  LCG_4 lcg_4_3 (
    .G0(G[4]), .G1(G[5]), .G2(G[6]), .G3(G[7]), .P0(P[4]), .P1(P[5]), .P2(P[6]), .P3(P[7]), .C_n(C[4]),
    .G(G1), .P(P1), .C1(C[5]), .C2(C[6]), .C3(C[7]));
  LCG_4 lcg_4_4 (
    .G0(G[0]), .G1(G[1]), .G2(G[2]), .G3(G[3]), .P0(P[0]), .P1(P[1]), .P2(P[2]), .P3(P[3]), .C_n(C_n),
    .G(G0), .P(P0), .C1(C[1]), .C2(C[2]), .C3(C[3]));

  assign C[0] = C_n;
endmodule
