// Digital circuit LCG-4.dig as structural Verilog
module LCG_4 (
  input  G1,
  input  P1,
  input  G2,
  input  G3,
  input  G0,
  input  P2,
  input  P3,
  input  P0,
  input  C_n,
  output G,
  output P,
  output C2,
  output C3,
  output C1
);

  wire or_1_out, or_2_out, or_3_out, or_4_out, or_5_out, or_6_out, or_7_out, or_8_out, or_9_out, or_10_out,
       or_11_out, or_12_out, or_13_out;

  and and_1 (P, P0, P1, P2, P3);
  or or_1 (or_1_out, G0, G1, G2, G3);
  or or_2 (or_2_out, P1, G3, G2, G1);
  or or_3 (or_3_out, P2, G3, G2);
  or or_4 (or_4_out, P3, G3);
  or or_5 (or_5_out, G2, G1, G0, C_n);
  or or_6 (or_6_out, P0, G2, G1, G0);
  or or_7 (or_7_out, P1, G2, G1);
  or or_8 (or_8_out, P2, G2);
  or or_9 (or_9_out, G1, G0, C_n);
  or or_10 (or_10_out, P0, G1, G0);
  or or_11 (or_11_out, P1, G1);
  or or_12 (or_12_out, G0, C_n);
  or or_13 (or_13_out, P0, G0);
  and and_2 (G, or_1_out, or_2_out, or_3_out, or_4_out);
  and and_3 (C3, or_5_out, or_6_out, or_7_out, or_8_out);
  and and_4 (C2, or_9_out, or_10_out, or_11_out);
  and and_5 (C1, or_12_out, or_13_out);
endmodule
