// Digital circuit LCGP-32.dig as structural Verilog
module LCGP_32 (
  input  C_n,
  input  [31:0] P,
  output P_o,
  output C_o,
  output [31:0] C
);

  wire P0, P1, P2, P3, P4, P5, P6, P7;

  LCGP_8C lcgp_8c_1 (
    .P0(P0), .P1(P1), .P2(P2), .P3(P3), .P4(P4), .P5(P5), .P6(P6), .P7(P7), .C_n(C_n), .C_O(C_o), .P(P_o),
    .C1(C[4]), .C2(C[8]), .C3(C[12]), .C4(C[16]), .C5(C[20]), .C6(C[24]), .C7(C[28]));
  LCGP_4 lcgp_4_1 (
    .P0(P[28]), .P1(P[29]), .P2(P[30]), .P3(P[31]), .C_n(C[28]), .P(P7), .C1(C[29]), .C2(C[30]), .C3(C[31]));
  LCGP_4 lcgp_4_2 (
    .P0(P[24]), .P1(P[25]), .P2(P[26]), .P3(P[27]), .C_n(C[24]), .P(P6), .C1(C[25]), .C2(C[26]), .C3(C[27]));
  LCGP_4 lcgp_4_3 (
    .P0(P[20]), .P1(P[21]), .P2(P[22]), .P3(P[23]), .C_n(C[20]), .P(P5), .C1(C[21]), .C2(C[22]), .C3(C[23]));
  LCGP_4 lcgp_4_4 (
    .P0(P[16]), .P1(P[17]), .P2(P[18]), .P3(P[19]), .C_n(C[16]), .P(P4), .C1(C[17]), .C2(C[18]), .C3(C[19]));
  LCGP_4 lcgp_4_5 (
    .P0(P[12]), .P1(P[13]), .P2(P[14]), .P3(P[15]), .C_n(C[12]), .P(P3), .C1(C[13]), .C2(C[14]), .C3(C[15]));
  LCGP_4 lcgp_4_6 (.P0(P[8]), .P1(P[9]), .P2(P[10]), .P3(P[11]), .C_n(C[8]), .P(P2), .C1(C[9]), .C2(C[10]), .C3(C[11]));
  LCGP_4 lcgp_4_7 (.P0(P[4]), .P1(P[5]), .P2(P[6]), .P3(P[7]), .C_n(C[4]), .P(P1), .C1(C[5]), .C2(C[6]), .C3(C[7]));
  LCGP_4 lcgp_4_8 (.P0(P[0]), .P1(P[1]), .P2(P[2]), .P3(P[3]), .C_n(C_n), .P(P0), .C1(C[1]), .C2(C[2]), .C3(C[3]));

  assign C[0] = C_n;
endmodule
