// Digital circuit LCGP-8C.dig as structural Verilog
module LCGP_8C (
  input  P1,
  input  P2,
  input  P3,
  input  P0,
  input  C_n,
  input  P5,
  input  P6,
  input  P7,
  input  P4,
  output P,
  output C2,
  output C3,
  output C1,
  output C5,
  output C6,
  output C4,
  output C7,
  output C_O
);

  and and_1 (C_O, P0, P1, P2, P3, C_n, P4, P5, P6, P7);
  and and_2 (P, P0, P1, P2, P3, P4, P5, P6, P7);
  and and_3 (C7, C_n, P0, P1, P2, P3, P4, P5, P6);
  and and_4 (C6, C_n, P0, P1, P2, P3, P4, P5);
  and and_5 (C5, C_n, P0, P1, P2, P3, P4);
  and and_6 (C4, C_n, P0, P1, P2, P3);
  and and_7 (C3, C_n, P0, P1, P2);
  and and_8 (C2, C_n, P0, P1);
  and and_9 (C1, C_n, P0);
endmodule
