// Digital circuit MMU-BL.dig as structural Verilog
module MMU_BL (
  input  [31:0] addr_i,
  input  [31:0] base,
  input  [31:0] limit,
  input  [1:0] md,
  output [31:0] addr_o,
  output error,
  output carry
);

  wire and_1_out, and_2_out, and_3_out, comparator_1_eq, comparator_2_lt, not_1_out, or_1_out;
  wire [19:0] and_4_out, lcg_20_1_c, xor_1_out;

  and and_1 (and_1_out, ~md[1], ~md[0], addr_i[0], comparator_1_eq);  // And
  and and_2 (and_2_out, ~md[1], addr_i[0], addr_i[1], comparator_1_eq);  // And
  and and_3 (and_3_out, ~md[1], ~md[0], addr_i[1], comparator_1_eq);  // And
  Comparator #(.Bits(10)) comparator_1 (.a({10{1'b1}}), .b(addr_i[11:2]), .eq(comparator_1_eq));  // open: gt, lt
  assign xor_1_out = addr_i[31:12] ^ base[31:12];  // XOr xor_1, 20 bits wide
  assign and_4_out = addr_i[31:12] & base[31:12];  // And and_4, 20 bits wide
  Comparator #(.Bits(20)) comparator_2 (.a(addr_i[31:12]), .b(limit[31:12]), .lt(comparator_2_lt));  // open: gt, eq
  or or_1 (or_1_out, and_1_out, and_2_out, and_3_out);
  not not_1 (not_1_out, comparator_2_lt);
  LCG_20 lcg_20_1 (.C_n(1'b0), .P(xor_1_out), .G(and_4_out), .C_o(carry), .C(lcg_20_1_c));  // open: G_o, P_o
  assign addr_o[31:12] = xor_1_out ^ lcg_20_1_c;  // XOr xor_2, 20 bits wide
  or or_2 (error, carry, or_1_out, not_1_out);

  assign addr_o[11:0] = addr_i[11:0];
endmodule
