// Digital circuit MMU-D.dig as structural Verilog
module MMU_D (
  input  [31:0] addr_b,
  input  [1:0] md_b,
  input  [1:0] md_c,
  input  [31:0] virt_c,
  input  [31:0] addr_o,
  input  st,
  input  [31:0] limit,
  input  [31:0] base,
  input  req_c,
  input  ld,
  input  [5:0] mid_c,
  output [31:0] phys_c,
  output acp,
  output err_c,
  output err_o,
  output [5:0] mid_o
);

  wire mmu_bl_1_carry, mmu_bl_2_carry, or_1_out;
  wire [31:0] addr_ot, multiplexer_1_out;

  MMU_BL mmu_bl_1 (
    .addr_i(addr_b), .base(base), .limit(limit), .md(md_b), .addr_o(addr_ot), .error(err_o),
    .carry(mmu_bl_1_carry));
  MMU_BL mmu_bl_2 (
    .addr_i(virt_c), .base(base), .limit(limit), .md(md_c), .addr_o(phys_c), .error(err_c),
    .carry(mmu_bl_2_carry));
  or or_1 (or_1_out, ld, st);
  Multiplexer #(.Bits(32)) multiplexer_1 (.sel(ld), .in_0(addr_b), .in_1(addr_ot), .out(multiplexer_1_out));
  assign addr_o = or_1_out ? multiplexer_1_out : 32'bz;  // Driver driver_1

  assign acp = req_c;
  assign mid_o = mid_c;

  // Other names for the same wires on the sheet: mid[5:0] = mid_c
endmodule
