// Digital circuit ROB-PC.dig as structural Verilog
module ROB_PC (
  input  [31:0] D,
  input  [3:0] inst,
  input  [3:0] com_id,
  input  E,
  input  C,
  input  [3:0] read_id,
  input  [3:0] ret_id,
  output [31:0] D1,
  output [31:0] D2,
  output [31:0] D3
);

  wire R1_e, R2_e, R3_e, R4_e, R5_e, R6_e, R7_e, R8_e, R9_e, R10_e, R11_e, R12_e, R13_e, R14_e, R15_e, R16_e;
  wire [31:0] R1, R2, R3, R4, R5, R6, R7, R8, R9, R10, R11, R12, R13, R14, R15, R16;

  RegisterFile #(.AddrBits(4), .Bits(32)) registerfile_1 (
    .Din(D), .we(E), .Rw(inst), .C(C), .Ra(com_id), .Rb(read_id), .Da(D1), .Db(D2));
  Register #(.Bits(32)) register_1 (.D(D), .C(C), .en(R1_e), .Q(R1));
  Register #(.Bits(32)) register_2 (.D(D), .C(C), .en(R5_e), .Q(R5));
  Register #(.Bits(32)) register_3 (.D(D), .C(C), .en(R9_e), .Q(R9));
  Register #(.Bits(32)) register_4 (.D(D), .C(C), .en(R13_e), .Q(R13));
  Demultiplexer #(.Selector_Bits(4)) demultiplexer_1 (
    .sel(inst), .in(E), .out_0(R1_e), .out_1(R2_e), .out_2(R3_e), .out_3(R4_e), .out_4(R5_e), .out_5(R6_e),
    .out_6(R7_e), .out_7(R8_e), .out_8(R9_e), .out_9(R10_e), .out_10(R11_e), .out_11(R12_e), .out_12(R13_e),
    .out_13(R14_e), .out_14(R15_e), .out_15(R16_e));
  Register #(.Bits(32)) register_5 (.D(D), .C(C), .en(R2_e), .Q(R2));
  Register #(.Bits(32)) register_6 (.D(D), .C(C), .en(R6_e), .Q(R6));
  Register #(.Bits(32)) register_7 (.D(D), .C(C), .en(R10_e), .Q(R10));
  Register #(.Bits(32)) register_8 (.D(D), .C(C), .en(R14_e), .Q(R14));
  Multiplexer #(.Selector_Bits(4), .Bits(32)) multiplexer_1 (
    .sel(com_id), .in_0(R1), .in_1(R2), .in_2(R3), .in_3(R4), .in_4(R5), .in_5(R6), .in_6(R7), .in_7(R8),
    .in_8(R9), .in_9(R10), .in_10(R11), .in_11(R12), .in_12(R13), .in_13(R14), .in_14(R15), .in_15(R16),
    .out(D1));
  Register #(.Bits(32)) register_9 (.D(D), .C(C), .en(R3_e), .Q(R3));
  Register #(.Bits(32)) register_10 (.D(D), .C(C), .en(R7_e), .Q(R7));
  Register #(.Bits(32)) register_11 (.D(D), .C(C), .en(R11_e), .Q(R11));
  Register #(.Bits(32)) register_12 (.D(D), .C(C), .en(R15_e), .Q(R15));
  Multiplexer #(.Selector_Bits(4), .Bits(32)) multiplexer_2 (
    .sel(read_id), .in_0(R1), .in_1(R2), .in_2(R3), .in_3(R4), .in_4(R5), .in_5(R6), .in_6(R7), .in_7(R8),
    .in_8(R9), .in_9(R10), .in_10(R11), .in_11(R12), .in_12(R13), .in_13(R14), .in_14(R15), .in_15(R16),
    .out(D2));
  Register #(.Bits(32)) register_13 (.D(D), .C(C), .en(R4_e), .Q(R4));
  Register #(.Bits(32)) register_14 (.D(D), .C(C), .en(R8_e), .Q(R8));
  Register #(.Bits(32)) register_15 (.D(D), .C(C), .en(R12_e), .Q(R12));
  Register #(.Bits(32)) register_16 (.D(D), .C(C), .en(R16_e), .Q(R16));
  Multiplexer #(.Selector_Bits(4), .Bits(32)) multiplexer_3 (
    .sel(ret_id), .in_0(R1), .in_1(R2), .in_2(R3), .in_3(R4), .in_4(R5), .in_5(R6), .in_6(R7), .in_7(R8),
    .in_8(R9), .in_9(R10), .in_10(R11), .in_11(R12), .in_12(R13), .in_13(R14), .in_14(R15), .in_15(R16),
    .out(D3));
endmodule
