// Digital circuit ROB-gen 2.dig as structural Verilog
module ROB_gen_2 (
  input  [31:0] D1,
  input  [7:0] R1,
  input  [3:0] inst1,
  input  [3:0] com1_id,
  input  [3:0] com2_id,
  input  E1,
  input  C,
  input  W1,
  input  [3:0] inst2,
  input  [7:0] R2_2,
  input  [31:0] D2_2,
  input  W2_2,
  input  E2,
  output [31:0] D1_2,
  output [7:0] R1_2,
  output [31:0] D2,
  output [7:0] R2,
  output W1_2,
  output W2
);

  wire R1_e, R1_M, R2_e, R2_M, R3_e, R3_M, R4_e, R4_M, R5_e, R5_M, R6_e, R6_M, R7_e, R7_M, R8_e, R8_M, R9_e,
       R9_M, R10_e, R10_M, R11_e, R11_M, R12_e, R12_M, R13_e, R13_M, R14_e, R14_M, R15_e, R15_M, R16_e, R16_M;
  wire [15:0] demultiplexer_1_out_10;
  wire [40:0] multiplexer_1_out, multiplexer_2_out, multiplexer_3_out, multiplexer_4_out, multiplexer_5_out,
       multiplexer_6_out, multiplexer_7_out, multiplexer_8_out, multiplexer_9_out, multiplexer_10_out,
       multiplexer_11_out, multiplexer_12_out, multiplexer_13_out, multiplexer_14_out, multiplexer_15_out,
       multiplexer_16_out, R1_t, R2_t, R3, R4, R5, R6, R7, R8, R9, R10, R11, R12, R13, R14, R15, R16;

  Multiplexer #(.Bits(41)) multiplexer_1 (
    .sel(R1_M), .in_0({W1, R1, D1}), .in_1({W2_2, R2_2, D2_2}), .out(multiplexer_1_out));
  Multiplexer #(.Bits(41)) multiplexer_2 (
    .sel(R5_M), .in_0({W1, R1, D1}), .in_1({W2_2, R2_2, D2_2}), .out(multiplexer_2_out));
  Multiplexer #(.Bits(41)) multiplexer_3 (
    .sel(R9_M), .in_0({W1, R1, D1}), .in_1({W2_2, R2_2, D2_2}), .out(multiplexer_3_out));
  Multiplexer #(.Bits(41)) multiplexer_4 (
    .sel(R13_M), .in_0({W1, R1, D1}), .in_1({W2_2, R2_2, D2_2}), .out(multiplexer_4_out));
  Demultiplexer #(.Selector_Bits(4)) demultiplexer_1 (
    .sel(inst1), .in(E1), .out_0(demultiplexer_1_out_10[15]), .out_1(demultiplexer_1_out_10[14]),
    .out_2(demultiplexer_1_out_10[13]), .out_3(demultiplexer_1_out_10[12]),
    .out_4(demultiplexer_1_out_10[11]), .out_5(demultiplexer_1_out_10[10]),
    .out_6(demultiplexer_1_out_10[9]), .out_7(demultiplexer_1_out_10[8]), .out_8(demultiplexer_1_out_10[7]),
    .out_9(demultiplexer_1_out_10[6]), .out_10(demultiplexer_1_out_10[5]),
    .out_11(demultiplexer_1_out_10[4]), .out_12(demultiplexer_1_out_10[3]),
    .out_13(demultiplexer_1_out_10[2]), .out_14(demultiplexer_1_out_10[1]), .out_15(demultiplexer_1_out_10[0]));
  Register #(.Bits(41)) register_1 (.D(multiplexer_1_out), .C(C), .en(R1_e), .Q(R1_t));
  Register #(.Bits(41)) register_2 (.D(multiplexer_2_out), .C(C), .en(R5_e), .Q(R5));
  Register #(.Bits(41)) register_3 (.D(multiplexer_3_out), .C(C), .en(R9_e), .Q(R9));
  Register #(.Bits(41)) register_4 (.D(multiplexer_4_out), .C(C), .en(R13_e), .Q(R13));
  Demultiplexer #(.Selector_Bits(4)) demultiplexer_2 (
    .sel(inst2), .in(E2), .out_0(R1_M), .out_1(R2_M), .out_2(R3_M), .out_3(R4_M), .out_4(R5_M), .out_5(R6_M),
    .out_6(R7_M), .out_7(R8_M), .out_8(R9_M), .out_9(R10_M), .out_10(R11_M), .out_11(R12_M), .out_12(R13_M),
    .out_13(R14_M), .out_14(R15_M), .out_15(R16_M));
  Multiplexer #(.Bits(41)) multiplexer_5 (
    .sel(R2_M), .in_0({W1, R1, D1}), .in_1({W2_2, R2_2, D2_2}), .out(multiplexer_5_out));
  Register #(.Bits(41)) register_5 (.D(multiplexer_5_out), .C(C), .en(R2_e), .Q(R2_t));
  Multiplexer #(.Bits(41)) multiplexer_6 (
    .sel(R6_M), .in_0({W1, R1, D1}), .in_1({W2_2, R2_2, D2_2}), .out(multiplexer_6_out));
  Register #(.Bits(41)) register_6 (.D(multiplexer_6_out), .C(C), .en(R6_e), .Q(R6));
  Multiplexer #(.Bits(41)) multiplexer_7 (
    .sel(R10_M), .in_0({W1, R1, D1}), .in_1({W2_2, R2_2, D2_2}), .out(multiplexer_7_out));
  Register #(.Bits(41)) register_7 (.D(multiplexer_7_out), .C(C), .en(R10_e), .Q(R10));
  Multiplexer #(.Bits(41)) multiplexer_8 (
    .sel(R14_M), .in_0({W1, R1, D1}), .in_1({W2_2, R2_2, D2_2}), .out(multiplexer_8_out));
  Register #(.Bits(41)) register_8 (.D(multiplexer_8_out), .C(C), .en(R14_e), .Q(R14));
  assign {R1_e, R2_e, R3_e, R4_e, R5_e, R6_e, R7_e, R8_e, R9_e, R10_e, R11_e, R12_e, R13_e, R14_e, R15_e, R16_e} = {R1_M, R2_M, R3_M, R4_M, R5_M, R6_M, R7_M, R8_M, R9_M, R10_M, R11_M, R12_M, R13_M, R14_M, R15_M, R16_M} | demultiplexer_1_out_10;  // Or or_1, 16 bits wide
  Multiplexer #(.Bits(41)) multiplexer_9 (
    .sel(R3_M), .in_0({W1, R1, D1}), .in_1({W2_2, R2_2, D2_2}), .out(multiplexer_9_out));
  Multiplexer #(.Bits(41)) multiplexer_10 (
    .sel(R7_M), .in_0({W1, R1, D1}), .in_1({W2_2, R2_2, D2_2}), .out(multiplexer_10_out));
  Multiplexer #(.Bits(41)) multiplexer_11 (
    .sel(R11_M), .in_0({W1, R1, D1}), .in_1({W2_2, R2_2, D2_2}), .out(multiplexer_11_out));
  Multiplexer #(.Bits(41)) multiplexer_12 (
    .sel(R15_M), .in_0({W1, R1, D1}), .in_1({W2_2, R2_2, D2_2}), .out(multiplexer_12_out));
  Register #(.Bits(41)) register_9 (.D(multiplexer_9_out), .C(C), .en(R3_e), .Q(R3));
  Register #(.Bits(41)) register_10 (.D(multiplexer_10_out), .C(C), .en(R7_e), .Q(R7));
  Register #(.Bits(41)) register_11 (.D(multiplexer_11_out), .C(C), .en(R11_e), .Q(R11));
  Register #(.Bits(41)) register_12 (.D(multiplexer_12_out), .C(C), .en(R15_e), .Q(R15));
  Multiplexer #(.Bits(41)) multiplexer_13 (
    .sel(R4_M), .in_0({W1, R1, D1}), .in_1({W2_2, R2_2, D2_2}), .out(multiplexer_13_out));
  Register #(.Bits(41)) register_13 (.D(multiplexer_13_out), .C(C), .en(R4_e), .Q(R4));
  Multiplexer #(.Bits(41)) multiplexer_14 (
    .sel(R8_M), .in_0({W1, R1, D1}), .in_1({W2_2, R2_2, D2_2}), .out(multiplexer_14_out));
  Register #(.Bits(41)) register_14 (.D(multiplexer_14_out), .C(C), .en(R8_e), .Q(R8));
  Multiplexer #(.Bits(41)) multiplexer_15 (
    .sel(R12_M), .in_0({W1, R1, D1}), .in_1({W2_2, R2_2, D2_2}), .out(multiplexer_15_out));
  Register #(.Bits(41)) register_15 (.D(multiplexer_15_out), .C(C), .en(R12_e), .Q(R12));
  Multiplexer #(.Bits(41)) multiplexer_16 (
    .sel(R16_M), .in_0({W1, R1, D1}), .in_1({W2_2, R2_2, D2_2}), .out(multiplexer_16_out));
  Register #(.Bits(41)) register_16 (.D(multiplexer_16_out), .C(C), .en(R16_e), .Q(R16));
  Multiplexer #(.Selector_Bits(4), .Bits(41)) multiplexer_17 (
    .sel(com1_id), .in_0(R1_t), .in_1(R2_t), .in_2(R3), .in_3(R4), .in_4(R5), .in_5(R6), .in_6(R7),
    .in_7(R8), .in_8(R9), .in_9(R10), .in_10(R11), .in_11(R12), .in_12(R13), .in_13(R14), .in_14(R15),
    .in_15(R16), .out({W1_2, R1_2, D1_2}));
  Multiplexer #(.Selector_Bits(4), .Bits(41)) multiplexer_18 (
    .sel(com2_id), .in_0(R1_t), .in_1(R2_t), .in_2(R3), .in_3(R4), .in_4(R5), .in_5(R6), .in_6(R7),
    .in_7(R8), .in_8(R9), .in_9(R10), .in_10(R11), .in_11(R12), .in_12(R13), .in_13(R14), .in_14(R15),
    .in_15(R16), .out({W2, R2, D2}));

  // Other names for the same wires on the sheet: D1_O[31:0] = D1_2; R1_O[7:0] = R1_2; W1_O = W1_2; D2_O[31:0] = D2;
  //   R2_O[7:0] = R2; W2_O = W2; L1[40:0] = {W1, R1, D1}; D2_t[31:0] = D2_2; L2[40:0] = {W2_2, R2_2, D2_2};
  //   R1_I[7:0] = R1; R2_I[7:0] = R2_2; W2_t = W2_2
endmodule
