// Digital circuit ROB-gen.dig as structural Verilog
module ROB_gen (
  input  [3:0] inst1,
  input  [3:0] com1_id,
  input  E1,
  input  C,
  input  [3:0] com2_id,
  input  [31:0] D2,
  input  [3:0] inst2,
  input  [31:0] D1,
  input  E2,
  input  [7:0] R1,
  input  [7:0] R2,
  input  com1,
  input  com2,
  input  [3:0] ret_id,
  input  [15:0] clr_16,
  input  EX1,
  input  EX2,
  input  ep1,
  input  ep2,
  output [31:0] D1_O,
  output [7:0] R1_O,
  output [31:0] D2_O,
  output [7:0] R2_O,
  output W1_O,
  output W2_O,
  output [31:0] DR_O,
  output EX2_O,
  output EX1_O
);

  wire nor_1_out, nor_2_out, priorityencoder_1_any, priorityencoder_2_any, R1_e, R2_e, R3_e, R4_e, R5_e,
       R6_e, R7_e, R8_e, R9_e, R10_e, R11_e, R12_e, R13_e, R14_e, R15_e, R16_e, xor_1_out, xor_2_out;
  wire [1:0] R1_M, R2_M, R3_M, R4_M, R5_M, R6_M, R7_M, R8_M, R9_M, R10_M, R11_M, R12_M, R13_M, R14_M, R15_M,
       R16_M;
  wire [3:0] priorityencoder_1_num, priorityencoder_2_num;
  wire [15:0] and_1_out, and_2_out, B_RM, comparator_13_eq, comparator_29_eq, demultiplexer_1_out_0,
       demultiplexer_2_out_0, demultiplexer_3_out_0, demultiplexer_4_out_0, demultiplexer_5_out_0,
       demultiplexer_6_out_0, or_5_out;
  wire [31:0] B1, B2;
  wire [45:1] L1, L2;
  wire [46:0] multiplexer_9_out, multiplexer_10_out, multiplexer_11_out, multiplexer_12_out,
       multiplexer_13_out, multiplexer_14_out, multiplexer_15_out, multiplexer_16_out, multiplexer_17_out,
       multiplexer_18_out, multiplexer_19_out, multiplexer_20_out, multiplexer_21_out, multiplexer_22_out,
       multiplexer_23_out, multiplexer_24_out, multiplexer_27_out, R1_t, R2_t, R3, R4, R5, R6, R7, R8, R9,
       R10, R11, R12, R13, R14, R15, R16;
  wire [46:42] multiplexer_25_out, multiplexer_26_out;

  nor nor_1 (nor_1_out, R1[2], R1[1], R1[0]);
  xor xor_1 (xor_1_out, R1[0], R1[1]);
  nor nor_2 (nor_2_out, R2[2], R2[1], R2[0]);
  xor xor_2 (xor_2_out, R2[0], R2[1]);
  nor nor_3 (L1[45], R1[1], R1[0]);
  or or_1 (L1[43], nor_1_out, R1[0]);
  or or_2 (L1[42], xor_1_out, nor_1_out);
  nor nor_4 (L2[45], R2[1], R2[0]);
  or or_3 (L2[43], nor_2_out, R2[0]);
  or or_4 (L2[42], xor_2_out, nor_2_out);
  inst_comp inst_comp_1 (.A_id(inst1), .A_ep(ep1), .B_id(inst2), .B_ep(ep2));  // open: A_new
  Multiplexer #(.Bits(8)) multiplexer_1 (.sel(L1[45]), .in_0(B1[31:24]), .in_1(D1[31:24]), .out(L1[32:25]));
  Multiplexer #(.Bits(8)) multiplexer_2 (.sel(L1[45]), .in_0(B1[23:16]), .in_1(D1[23:16]), .out(L1[24:17]));
  Multiplexer #(.Bits(8)) multiplexer_3 (.sel(L1[43]), .in_0(B1[15:8]), .in_1(D1[15:8]), .out(L1[16:9]));
  Multiplexer #(.Bits(8)) multiplexer_4 (.sel(L1[42]), .in_0(B1[7:0]), .in_1(D1[7:0]), .out(L1[8:1]));
  Multiplexer #(.Bits(8)) multiplexer_5 (.sel(L2[45]), .in_0(B2[31:24]), .in_1(D2[31:24]), .out(L2[32:25]));
  Multiplexer #(.Bits(8)) multiplexer_6 (.sel(L2[45]), .in_0(B2[23:16]), .in_1(D2[23:16]), .out(L2[24:17]));
  Multiplexer #(.Bits(8)) multiplexer_7 (.sel(L2[43]), .in_0(B2[15:8]), .in_1(D2[15:8]), .out(L2[16:9]));
  Multiplexer #(.Bits(8)) multiplexer_8 (.sel(L2[42]), .in_0(B2[7:0]), .in_1(D2[7:0]), .out(L2[8:1]));
  Demultiplexer #(.Selector_Bits(4)) demultiplexer_1 (
    .sel(com1_id), .in(com1), .out_0(demultiplexer_1_out_0[15]), .out_1(demultiplexer_1_out_0[14]),
    .out_2(demultiplexer_1_out_0[13]), .out_3(demultiplexer_1_out_0[12]), .out_4(demultiplexer_1_out_0[11]),
    .out_5(demultiplexer_1_out_0[10]), .out_6(demultiplexer_1_out_0[9]), .out_7(demultiplexer_1_out_0[8]),
    .out_8(demultiplexer_1_out_0[7]), .out_9(demultiplexer_1_out_0[6]), .out_10(demultiplexer_1_out_0[5]),
    .out_11(demultiplexer_1_out_0[4]), .out_12(demultiplexer_1_out_0[3]), .out_13(demultiplexer_1_out_0[2]),
    .out_14(demultiplexer_1_out_0[1]), .out_15(demultiplexer_1_out_0[0]));
  Demultiplexer #(.Selector_Bits(4)) demultiplexer_2 (
    .sel(inst1), .in(E1), .out_0(demultiplexer_2_out_0[15]), .out_1(demultiplexer_2_out_0[14]),
    .out_2(demultiplexer_2_out_0[13]), .out_3(demultiplexer_2_out_0[12]), .out_4(demultiplexer_2_out_0[11]),
    .out_5(demultiplexer_2_out_0[10]), .out_6(demultiplexer_2_out_0[9]), .out_7(demultiplexer_2_out_0[8]),
    .out_8(demultiplexer_2_out_0[7]), .out_9(demultiplexer_2_out_0[6]), .out_10(demultiplexer_2_out_0[5]),
    .out_11(demultiplexer_2_out_0[4]), .out_12(demultiplexer_2_out_0[3]), .out_13(demultiplexer_2_out_0[2]),
    .out_14(demultiplexer_2_out_0[1]), .out_15(demultiplexer_2_out_0[0]));
  Multiplexer #(.Selector_Bits(2), .Bits(47)) multiplexer_9 (
    .sel(R1_M), .in_0({1'b1, {2{L1[45]}}, L1[43:42], EX1, R1, L1[32:1], 1'b1}),
    .in_1({1'b1, {2{L2[45]}}, L2[43:42], EX2, R2, L2[32:1], 1'b1}), .in_2({47{1'b0}}), .in_3({47{1'b0}}),
    .out(multiplexer_9_out));
  Multiplexer #(.Selector_Bits(2), .Bits(47)) multiplexer_10 (
    .sel(R5_M), .in_0({1'b1, {2{L1[45]}}, L1[43:42], EX1, R1, L1[32:1], 1'b1}),
    .in_1({1'b1, {2{L2[45]}}, L2[43:42], EX2, R2, L2[32:1], 1'b1}), .in_2({47{1'b0}}), .in_3({47{1'b0}}),
    .out(multiplexer_10_out));
  Multiplexer #(.Selector_Bits(2), .Bits(47)) multiplexer_11 (
    .sel(R9_M), .in_0({1'b1, {2{L1[45]}}, L1[43:42], EX1, R1, L1[32:1], 1'b1}),
    .in_1({1'b1, {2{L2[45]}}, L2[43:42], EX2, R2, L2[32:1], 1'b1}), .in_2({47{1'b0}}), .in_3({47{1'b0}}),
    .out(multiplexer_11_out));
  Multiplexer #(.Selector_Bits(2), .Bits(47)) multiplexer_12 (
    .sel(R13_M), .in_0({1'b1, {2{L1[45]}}, L1[43:42], EX1, R1, L1[32:1], 1'b1}),
    .in_1({1'b1, {2{L2[45]}}, L2[43:42], EX2, R2, L2[32:1], 1'b1}), .in_2({47{1'b0}}), .in_3({47{1'b0}}),
    .out(multiplexer_12_out));
  Register #(.Bits(47)) register_1 (.D(multiplexer_9_out), .C(C), .en(R1_e), .Q(R1_t));
  Register #(.Bits(47)) register_2 (.D(multiplexer_10_out), .C(C), .en(R5_e), .Q(R5));
  Register #(.Bits(47)) register_3 (.D(multiplexer_11_out), .C(C), .en(R9_e), .Q(R9));
  Register #(.Bits(47)) register_4 (.D(multiplexer_12_out), .C(C), .en(R13_e), .Q(R13));
  Demultiplexer #(.Selector_Bits(4)) demultiplexer_3 (
    .sel(com2_id), .in(com2), .out_0(demultiplexer_3_out_0[15]), .out_1(demultiplexer_3_out_0[14]),
    .out_2(demultiplexer_3_out_0[13]), .out_3(demultiplexer_3_out_0[12]), .out_4(demultiplexer_3_out_0[11]),
    .out_5(demultiplexer_3_out_0[10]), .out_6(demultiplexer_3_out_0[9]), .out_7(demultiplexer_3_out_0[8]),
    .out_8(demultiplexer_3_out_0[7]), .out_9(demultiplexer_3_out_0[6]), .out_10(demultiplexer_3_out_0[5]),
    .out_11(demultiplexer_3_out_0[4]), .out_12(demultiplexer_3_out_0[3]), .out_13(demultiplexer_3_out_0[2]),
    .out_14(demultiplexer_3_out_0[1]), .out_15(demultiplexer_3_out_0[0]));
  Demultiplexer #(.Selector_Bits(4)) demultiplexer_4 (
    .sel(inst2), .in(E2), .out_0(demultiplexer_4_out_0[15]), .out_1(demultiplexer_4_out_0[14]),
    .out_2(demultiplexer_4_out_0[13]), .out_3(demultiplexer_4_out_0[12]), .out_4(demultiplexer_4_out_0[11]),
    .out_5(demultiplexer_4_out_0[10]), .out_6(demultiplexer_4_out_0[9]), .out_7(demultiplexer_4_out_0[8]),
    .out_8(demultiplexer_4_out_0[7]), .out_9(demultiplexer_4_out_0[6]), .out_10(demultiplexer_4_out_0[5]),
    .out_11(demultiplexer_4_out_0[4]), .out_12(demultiplexer_4_out_0[3]), .out_13(demultiplexer_4_out_0[2]),
    .out_14(demultiplexer_4_out_0[1]), .out_15(demultiplexer_4_out_0[0]));
  Multiplexer #(.Selector_Bits(2), .Bits(47)) multiplexer_13 (
    .sel(R2_M), .in_0({1'b1, {2{L1[45]}}, L1[43:42], EX1, R1, L1[32:1], 1'b1}),
    .in_1({1'b1, {2{L2[45]}}, L2[43:42], EX2, R2, L2[32:1], 1'b1}), .in_2({47{1'b0}}), .in_3({47{1'b0}}),
    .out(multiplexer_13_out));
  Register #(.Bits(47)) register_5 (.D(multiplexer_13_out), .C(C), .en(R2_e), .Q(R2_t));
  Multiplexer #(.Selector_Bits(2), .Bits(47)) multiplexer_14 (
    .sel(R6_M), .in_0({1'b1, {2{L1[45]}}, L1[43:42], EX1, R1, L1[32:1], 1'b1}),
    .in_1({1'b1, {2{L2[45]}}, L2[43:42], EX2, R2, L2[32:1], 1'b1}), .in_2({47{1'b0}}), .in_3({47{1'b0}}),
    .out(multiplexer_14_out));
  Register #(.Bits(47)) register_6 (.D(multiplexer_14_out), .C(C), .en(R6_e), .Q(R6));
  Multiplexer #(.Selector_Bits(2), .Bits(47)) multiplexer_15 (
    .sel(R10_M), .in_0({1'b1, {2{L1[45]}}, L1[43:42], EX1, R1, L1[32:1], 1'b1}),
    .in_1({1'b1, {2{L2[45]}}, L2[43:42], EX2, R2, L2[32:1], 1'b1}), .in_2({47{1'b0}}), .in_3({47{1'b0}}),
    .out(multiplexer_15_out));
  Register #(.Bits(47)) register_7 (.D(multiplexer_15_out), .C(C), .en(R10_e), .Q(R10));
  Multiplexer #(.Selector_Bits(2), .Bits(47)) multiplexer_16 (
    .sel(R14_M), .in_0({1'b1, {2{L1[45]}}, L1[43:42], EX1, R1, L1[32:1], 1'b1}),
    .in_1({1'b1, {2{L2[45]}}, L2[43:42], EX2, R2, L2[32:1], 1'b1}), .in_2({47{1'b0}}), .in_3({47{1'b0}}),
    .out(multiplexer_16_out));
  Register #(.Bits(47)) register_8 (.D(multiplexer_16_out), .C(C), .en(R14_e), .Q(R14));
  assign or_5_out = demultiplexer_3_out_0 | {clr_16[0], clr_16[1], clr_16[2], clr_16[3], clr_16[4], clr_16[5], clr_16[6], clr_16[7], clr_16[8], clr_16[9], clr_16[10], clr_16[11], clr_16[12], clr_16[13], clr_16[14], clr_16[15]} | demultiplexer_1_out_0;  // Or or_5, 16 bits wide
  assign {R1_e, R2_e, R3_e, R4_e, R5_e, R6_e, R7_e, R8_e, R9_e, R10_e, R11_e, R12_e, R13_e, R14_e, R15_e, R16_e} = demultiplexer_3_out_0 | demultiplexer_1_out_0 | {clr_16[0], clr_16[1], clr_16[2], clr_16[3], clr_16[4], clr_16[5], clr_16[6], clr_16[7], clr_16[8], clr_16[9], clr_16[10], clr_16[11], clr_16[12], clr_16[13], clr_16[14], clr_16[15]} | demultiplexer_4_out_0 | demultiplexer_2_out_0 | B_RM;  // Or or_6, 16 bits wide
  Multiplexer #(.Selector_Bits(2), .Bits(47)) multiplexer_17 (
    .sel(R3_M), .in_0({1'b1, {2{L1[45]}}, L1[43:42], EX1, R1, L1[32:1], 1'b1}),
    .in_1({1'b1, {2{L2[45]}}, L2[43:42], EX2, R2, L2[32:1], 1'b1}), .in_2({47{1'b0}}), .in_3({47{1'b0}}),
    .out(multiplexer_17_out));
  Multiplexer #(.Selector_Bits(2), .Bits(47)) multiplexer_18 (
    .sel(R7_M), .in_0({1'b1, {2{L1[45]}}, L1[43:42], EX1, R1, L1[32:1], 1'b1}),
    .in_1({1'b1, {2{L2[45]}}, L2[43:42], EX2, R2, L2[32:1], 1'b1}), .in_2({47{1'b0}}), .in_3({47{1'b0}}),
    .out(multiplexer_18_out));
  Multiplexer #(.Selector_Bits(2), .Bits(47)) multiplexer_19 (
    .sel(R11_M), .in_0({1'b1, {2{L1[45]}}, L1[43:42], EX1, R1, L1[32:1], 1'b1}),
    .in_1({1'b1, {2{L2[45]}}, L2[43:42], EX2, R2, L2[32:1], 1'b1}), .in_2({47{1'b0}}), .in_3({47{1'b0}}),
    .out(multiplexer_19_out));
  Multiplexer #(.Selector_Bits(2), .Bits(47)) multiplexer_20 (
    .sel(R15_M), .in_0({1'b1, {2{L1[45]}}, L1[43:42], EX1, R1, L1[32:1], 1'b1}),
    .in_1({1'b1, {2{L2[45]}}, L2[43:42], EX2, R2, L2[32:1], 1'b1}), .in_2({47{1'b0}}), .in_3({47{1'b0}}),
    .out(multiplexer_20_out));
  Register #(.Bits(47)) register_9 (.D(multiplexer_17_out), .C(C), .en(R3_e), .Q(R3));
  Register #(.Bits(47)) register_10 (.D(multiplexer_18_out), .C(C), .en(R7_e), .Q(R7));
  Register #(.Bits(47)) register_11 (.D(multiplexer_19_out), .C(C), .en(R11_e), .Q(R11));
  Register #(.Bits(47)) register_12 (.D(multiplexer_20_out), .C(C), .en(R15_e), .Q(R15));
  assign {R1_M[1], R2_M[1], R3_M[1], R4_M[1], R5_M[1], R6_M[1], R7_M[1], R8_M[1], R9_M[1], R10_M[1], R11_M[1], R12_M[1], R13_M[1], R14_M[1], R15_M[1], R16_M[1]} = or_5_out | B_RM;  // Or or_7, 16 bits wide
  assign {R1_M[0], R2_M[0], R3_M[0], R4_M[0], R5_M[0], R6_M[0], R7_M[0], R8_M[0], R9_M[0], R10_M[0], R11_M[0], R12_M[0], R13_M[0], R14_M[0], R15_M[0], R16_M[0]} = or_5_out | demultiplexer_4_out_0;  // Or or_8, 16 bits wide
  Multiplexer #(.Selector_Bits(2), .Bits(47)) multiplexer_21 (
    .sel(R4_M), .in_0({1'b1, {2{L1[45]}}, L1[43:42], EX1, R1, L1[32:1], 1'b1}),
    .in_1({1'b1, {2{L2[45]}}, L2[43:42], EX2, R2, L2[32:1], 1'b1}), .in_2({47{1'b0}}), .in_3({47{1'b0}}),
    .out(multiplexer_21_out));
  Register #(.Bits(47)) register_13 (.D(multiplexer_21_out), .C(C), .en(R4_e), .Q(R4));
  Multiplexer #(.Selector_Bits(2), .Bits(47)) multiplexer_22 (
    .sel(R8_M), .in_0({1'b1, {2{L1[45]}}, L1[43:42], EX1, R1, L1[32:1], 1'b1}),
    .in_1({1'b1, {2{L2[45]}}, L2[43:42], EX2, R2, L2[32:1], 1'b1}), .in_2({47{1'b0}}), .in_3({47{1'b0}}),
    .out(multiplexer_22_out));
  Register #(.Bits(47)) register_14 (.D(multiplexer_22_out), .C(C), .en(R8_e), .Q(R8));
  Multiplexer #(.Selector_Bits(2), .Bits(47)) multiplexer_23 (
    .sel(R12_M), .in_0({1'b1, {2{L1[45]}}, L1[43:42], EX1, R1, L1[32:1], 1'b1}),
    .in_1({1'b1, {2{L2[45]}}, L2[43:42], EX2, R2, L2[32:1], 1'b1}), .in_2({47{1'b0}}), .in_3({47{1'b0}}),
    .out(multiplexer_23_out));
  Register #(.Bits(47)) register_15 (.D(multiplexer_23_out), .C(C), .en(R12_e), .Q(R12));
  Multiplexer #(.Selector_Bits(2), .Bits(47)) multiplexer_24 (
    .sel(R16_M), .in_0({1'b1, {2{L1[45]}}, L1[43:42], EX1, R1, L1[32:1], 1'b1}),
    .in_1({1'b1, {2{L2[45]}}, L2[43:42], EX2, R2, L2[32:1], 1'b1}), .in_2({47{1'b0}}), .in_3({47{1'b0}}),
    .out(multiplexer_24_out));
  Register #(.Bits(47)) register_16 (.D(multiplexer_24_out), .C(C), .en(R16_e), .Q(R16));
  Multiplexer #(.Selector_Bits(4), .Bits(47)) multiplexer_25 (
    .sel(com1_id), .in_0(R1_t), .in_1(R2_t), .in_2(R3), .in_3(R4), .in_4(R5), .in_5(R6), .in_6(R7),
    .in_7(R8), .in_8(R9), .in_9(R10), .in_10(R11), .in_11(R12), .in_12(R13), .in_13(R14), .in_14(R15),
    .in_15(R16), .out({multiplexer_25_out, EX1_O, R1_O, D1_O, W1_O}));
  Multiplexer #(.Selector_Bits(4), .Bits(47)) multiplexer_26 (
    .sel(com2_id), .in_0(R1_t), .in_1(R2_t), .in_2(R3), .in_3(R4), .in_4(R5), .in_5(R6), .in_6(R7),
    .in_7(R8), .in_8(R9), .in_9(R10), .in_10(R11), .in_11(R12), .in_12(R13), .in_13(R14), .in_14(R15),
    .in_15(R16), .out({multiplexer_26_out, EX2_O, R2_O, D2_O, W2_O}));
  Comparator #(.Bits(5)) comparator_1 (.a(R1_t[40:36]), .b(R1[7:3]), .eq(comparator_13_eq[15]));  // open: gt, lt
  Comparator #(.Bits(5)) comparator_2 (.a(R2_t[40:36]), .b(R1[7:3]), .eq(comparator_13_eq[14]));  // open: gt, lt
  Comparator #(.Bits(5)) comparator_3 (.a(R3[40:36]), .b(R1[7:3]), .eq(comparator_13_eq[13]));  // open: gt, lt
  Comparator #(.Bits(5)) comparator_4 (.a(R4[40:36]), .b(R1[7:3]), .eq(comparator_13_eq[12]));  // open: gt, lt
  Comparator #(.Bits(5)) comparator_5 (.a(R5[40:36]), .b(R1[7:3]), .eq(comparator_13_eq[11]));  // open: gt, lt
  Comparator #(.Bits(5)) comparator_6 (.a(R6[40:36]), .b(R1[7:3]), .eq(comparator_13_eq[10]));  // open: gt, lt
  Comparator #(.Bits(5)) comparator_7 (.a(R7[40:36]), .b(R1[7:3]), .eq(comparator_13_eq[9]));  // open: gt, lt
  Comparator #(.Bits(5)) comparator_8 (.a(R8[40:36]), .b(R1[7:3]), .eq(comparator_13_eq[8]));  // open: gt, lt
  Comparator #(.Bits(5)) comparator_9 (.a(R9[40:36]), .b(R1[7:3]), .eq(comparator_13_eq[7]));  // open: gt, lt
  Comparator #(.Bits(5)) comparator_10 (.a(R10[40:36]), .b(R1[7:3]), .eq(comparator_13_eq[6]));  // open: gt, lt
  Comparator #(.Bits(5)) comparator_11 (.a(R11[40:36]), .b(R1[7:3]), .eq(comparator_13_eq[5]));  // open: gt, lt
  Comparator #(.Bits(5)) comparator_12 (.a(R12[40:36]), .b(R1[7:3]), .eq(comparator_13_eq[4]));  // open: gt, lt
  Comparator #(.Bits(5)) comparator_13 (.a(R13[40:36]), .b(R1[7:3]), .eq(comparator_13_eq[3]));  // open: gt, lt
  Comparator #(.Bits(5)) comparator_14 (.a(R14[40:36]), .b(R1[7:3]), .eq(comparator_13_eq[2]));  // open: gt, lt
  Comparator #(.Bits(5)) comparator_15 (.a(R15[40:36]), .b(R1[7:3]), .eq(comparator_13_eq[1]));  // open: gt, lt
  Comparator #(.Bits(5)) comparator_16 (.a(R16[40:36]), .b(R1[7:3]), .eq(comparator_13_eq[0]));  // open: gt, lt
  Multiplexer #(.Selector_Bits(4), .Bits(47)) multiplexer_27 (
    .sel(ret_id), .in_0(R1_t), .in_1(R2_t), .in_2(R3), .in_3(R4), .in_4(R5), .in_5(R6), .in_6(R7), .in_7(R8),
    .in_8(R9), .in_9(R10), .in_10(R11), .in_11(R12), .in_12(R13), .in_13(R14), .in_14(R15), .in_15(R16),
    .out({multiplexer_27_out[46:33], DR_O, multiplexer_27_out[0]}));
  assign and_1_out = comparator_13_eq & {R1_t[46], R2_t[46], R3[46], R4[46], R5[46], R6[46], R7[46], R8[46], R9[46], R10[46], R11[46], R12[46], R13[46], R14[46], R15[46], R16[46]};  // And and_1, 16 bits wide
  PriorityEncoder #(.Selector_Bits(4)) priorityencoder_1 (
    .in0(and_1_out[15]), .in1(and_1_out[14]), .in2(and_1_out[13]), .in3(and_1_out[12]), .in4(and_1_out[11]),
    .in5(and_1_out[10]), .in6(and_1_out[9]), .in7(and_1_out[8]), .in8(and_1_out[7]), .in9(and_1_out[6]),
    .in10(and_1_out[5]), .in11(and_1_out[4]), .in12(and_1_out[3]), .in13(and_1_out[2]), .in14(and_1_out[1]),
    .in15(and_1_out[0]), .num(priorityencoder_1_num), .any(priorityencoder_1_any));
  Comparator #(.Bits(5)) comparator_17 (.a(R1_t[40:36]), .b(R2[7:3]), .eq(comparator_29_eq[15]));  // open: gt, lt
  Comparator #(.Bits(5)) comparator_18 (.a(R2_t[40:36]), .b(R2[7:3]), .eq(comparator_29_eq[14]));  // open: gt, lt
  Comparator #(.Bits(5)) comparator_19 (.a(R3[40:36]), .b(R2[7:3]), .eq(comparator_29_eq[13]));  // open: gt, lt
  Comparator #(.Bits(5)) comparator_20 (.a(R4[40:36]), .b(R2[7:3]), .eq(comparator_29_eq[12]));  // open: gt, lt
  Comparator #(.Bits(5)) comparator_21 (.a(R5[40:36]), .b(R2[7:3]), .eq(comparator_29_eq[11]));  // open: gt, lt
  Comparator #(.Bits(5)) comparator_22 (.a(R6[40:36]), .b(R2[7:3]), .eq(comparator_29_eq[10]));  // open: gt, lt
  Comparator #(.Bits(5)) comparator_23 (.a(R7[40:36]), .b(R2[7:3]), .eq(comparator_29_eq[9]));  // open: gt, lt
  Comparator #(.Bits(5)) comparator_24 (.a(R8[40:36]), .b(R2[7:3]), .eq(comparator_29_eq[8]));  // open: gt, lt
  Comparator #(.Bits(5)) comparator_25 (.a(R9[40:36]), .b(R2[7:3]), .eq(comparator_29_eq[7]));  // open: gt, lt
  Comparator #(.Bits(5)) comparator_26 (.a(R10[40:36]), .b(R2[7:3]), .eq(comparator_29_eq[6]));  // open: gt, lt
  Comparator #(.Bits(5)) comparator_27 (.a(R11[40:36]), .b(R2[7:3]), .eq(comparator_29_eq[5]));  // open: gt, lt
  Comparator #(.Bits(5)) comparator_28 (.a(R12[40:36]), .b(R2[7:3]), .eq(comparator_29_eq[4]));  // open: gt, lt
  Comparator #(.Bits(5)) comparator_29 (.a(R13[40:36]), .b(R2[7:3]), .eq(comparator_29_eq[3]));  // open: gt, lt
  Comparator #(.Bits(5)) comparator_30 (.a(R14[40:36]), .b(R2[7:3]), .eq(comparator_29_eq[2]));  // open: gt, lt
  Comparator #(.Bits(5)) comparator_31 (.a(R15[40:36]), .b(R2[7:3]), .eq(comparator_29_eq[1]));  // open: gt, lt
  Comparator #(.Bits(5)) comparator_32 (.a(R16[40:36]), .b(R2[7:3]), .eq(comparator_29_eq[0]));  // open: gt, lt
  assign and_2_out = comparator_29_eq & {R1_t[46], R2_t[46], R3[46], R4[46], R5[46], R6[46], R7[46], R8[46], R9[46], R10[46], R11[46], R12[46], R13[46], R14[46], R15[46], R16[46]};  // And and_2, 16 bits wide
  Multiplexer #(.Selector_Bits(4), .Bits(32)) multiplexer_28 (
    .sel(priorityencoder_1_num), .in_0(R1_t[32:1]), .in_1(R2_t[32:1]), .in_2(R3[32:1]), .in_3(R4[32:1]),
    .in_4(R5[32:1]), .in_5(R6[32:1]), .in_6(R7[32:1]), .in_7(R8[32:1]), .in_8(R9[32:1]), .in_9(R10[32:1]),
    .in_10(R11[32:1]), .in_11(R12[32:1]), .in_12(R13[32:1]), .in_13(R14[32:1]), .in_14(R15[32:1]),
    .in_15(R16[32:1]), .out(B1));
  Demultiplexer #(.Selector_Bits(4)) demultiplexer_5 (
    .sel(priorityencoder_1_num), .in(priorityencoder_1_any), .out_0(demultiplexer_5_out_0[15]),
    .out_1(demultiplexer_5_out_0[14]), .out_2(demultiplexer_5_out_0[13]), .out_3(demultiplexer_5_out_0[12]),
    .out_4(demultiplexer_5_out_0[11]), .out_5(demultiplexer_5_out_0[10]), .out_6(demultiplexer_5_out_0[9]),
    .out_7(demultiplexer_5_out_0[8]), .out_8(demultiplexer_5_out_0[7]), .out_9(demultiplexer_5_out_0[6]),
    .out_10(demultiplexer_5_out_0[5]), .out_11(demultiplexer_5_out_0[4]), .out_12(demultiplexer_5_out_0[3]),
    .out_13(demultiplexer_5_out_0[2]), .out_14(demultiplexer_5_out_0[1]), .out_15(demultiplexer_5_out_0[0]));
  PriorityEncoder #(.Selector_Bits(4)) priorityencoder_2 (
    .in0(and_2_out[15]), .in1(and_2_out[14]), .in2(and_2_out[13]), .in3(and_2_out[12]), .in4(and_2_out[11]),
    .in5(and_2_out[10]), .in6(and_2_out[9]), .in7(and_2_out[8]), .in8(and_2_out[7]), .in9(and_2_out[6]),
    .in10(and_2_out[5]), .in11(and_2_out[4]), .in12(and_2_out[3]), .in13(and_2_out[2]), .in14(and_2_out[1]),
    .in15(and_2_out[0]), .num(priorityencoder_2_num), .any(priorityencoder_2_any));
  Multiplexer #(.Selector_Bits(4), .Bits(32)) multiplexer_29 (
    .sel(priorityencoder_2_num), .in_0(R1_t[32:1]), .in_1(R2_t[32:1]), .in_2(R3[32:1]), .in_3(R4[32:1]),
    .in_4(R5[32:1]), .in_5(R6[32:1]), .in_6(R7[32:1]), .in_7(R8[32:1]), .in_8(R9[32:1]), .in_9(R10[32:1]),
    .in_10(R11[32:1]), .in_11(R12[32:1]), .in_12(R13[32:1]), .in_13(R14[32:1]), .in_14(R15[32:1]),
    .in_15(R16[32:1]), .out(B2));
  Demultiplexer #(.Selector_Bits(4)) demultiplexer_6 (
    .sel(priorityencoder_2_num), .in(priorityencoder_2_any), .out_0(demultiplexer_6_out_0[15]),
    .out_1(demultiplexer_6_out_0[14]), .out_2(demultiplexer_6_out_0[13]), .out_3(demultiplexer_6_out_0[12]),
    .out_4(demultiplexer_6_out_0[11]), .out_5(demultiplexer_6_out_0[10]), .out_6(demultiplexer_6_out_0[9]),
    .out_7(demultiplexer_6_out_0[8]), .out_8(demultiplexer_6_out_0[7]), .out_9(demultiplexer_6_out_0[6]),
    .out_10(demultiplexer_6_out_0[5]), .out_11(demultiplexer_6_out_0[4]), .out_12(demultiplexer_6_out_0[3]),
    .out_13(demultiplexer_6_out_0[2]), .out_14(demultiplexer_6_out_0[1]), .out_15(demultiplexer_6_out_0[0]));
  assign B_RM = demultiplexer_6_out_0 | demultiplexer_5_out_0;  // Or or_9, 16 bits wide

  // Other names for the same wires on the sheet: L2 (some bits) = {L2[45], EX2, R2};
  //   L1 (some bits) = {L1[45], EX1, R1}; D3_O[31:0] = DR_O;
  //   clr_16_t[15:0] = {clr_16[0], clr_16[1], clr_16[2], clr_16[3], clr_16[4], clr_16[5], clr_16[6], clr_16[7], clr_16[8], clr_16[9], clr_16[10], clr_16[11], clr_16[12], clr_16[13], clr_16[14], clr_16[15]};
  //   clri[15:0] = clr_16; EX1_I = EX1; EX2_I = EX2; R1_I[7:0] = R1; R2_I[7:0] = R2
endmodule
