// Digital circuit addsub-4c32.dig as structural Verilog
module addsub_4c32 (
  input  [3:0] b,
  input  [31:0] a,
  input  sub,
  output [31:0] s,
  output c
);

  wire add_1_c_o, xor_3_out;
  wire [3:0] bitextender_1_out, xor_1_out;
  wire [27:0] bitextender_2_out, lcgp_28_1_c, xor_2_out;

  BitExtender #(.inputBits(1), .outputBits(4)) bitextender_1 (.in(sub), .out(bitextender_1_out));
  assign xor_1_out = b ^ bitextender_1_out;  // XOr xor_1, 4 bits wide
  BitExtender #(.inputBits(1), .outputBits(28)) bitextender_2 (.in(sub), .out(bitextender_2_out));
  assign xor_2_out = bitextender_2_out ^ a[31:4];  // XOr xor_2, 28 bits wide
  Add #(.Bits(4)) add_1 (.a(a[3:0]), .b(xor_1_out), .c_i(sub), .s(s[3:0]), .c_o(add_1_c_o));
  xor xor_3 (xor_3_out, sub, add_1_c_o);
  LCGP_28 lcgp_28_1 (.P(xor_2_out), .C_n(xor_3_out), .C_o(c), .C(lcgp_28_1_c));  // open: P_o
  assign s[31:4] = lcgp_28_1_c ^ a[31:4];  // XOr xor_4, 28 bits wide

  // Notes on the sheet:
  //   b: second input to add
  //   a: first input to add
  //   s: the result of the addition
  //   sub: subtract
  //   c: carry output. If set there was an overflow.
endmodule
