// Digital circuit alu-32.dig as structural Verilog
module alu_32 (
  input  [31:0] A,
  input  [31:0] B,
  input  [8:0] CT,
  input  [7:0] F_I,
  input  [31:0] E,
  input  [2:0] RM,
  output [31:0] E_B,
  output [31:0] E_A,
  output [31:0] R_O,
  output [7:0] F_O
);

  wire and_2_out, and_3_out, and_9_out, c8, c16, c32, c_i, multiplexer_10_out, multiplexer_15_out,
       multiplexer_19_out, multiplexer_21_out, multiplexer_22_out, not_1_out, not_2_out, not_3_out,
       not_4_out, not_5_out, not_6_out, or_1_out, or_2_out, or_3_out, or_5_out, or_7_out, xnor_1_out,
       xor_1_out, xor_2_out, xor_5_out;
  wire [0:0] m_bit, multiplexer_2_out;
  wire [1:0] and_12_out, multiplexer_4_out;
  wire [3:0] multiplexer_8_out;
  wire [7:0] multiplexer_13_out;
  wire [15:0] multiplexer_18_out;
  wire [30:0] bitextender_1_out, multiplexer_5_out;
  wire [31:0] and_4_out, and_5_out, and_6_out, and_7_out, expand_32_1_o, expand_32_2_o, expand_32_3_o,
       expand_32_4_o, invert_32_1_o, invert_32_2_o, lcg_32_1_c, multiplexer_1_out, multiplexer_3_out,
       multiplexer_6_out, multiplexer_11_out, multiplexer_16_out, multiplexer_20_out, multiplexer_23_out,
       or_6_out, xor_3_out, xor_4_out, xor_6_out;

  invert_32 invert_32_1 (.I(A), .O(invert_32_1_o));
  or or_1 (or_1_out, A[0], A[1], A[2], A[3], A[4], A[5], A[6], A[7], A[8], A[9], A[10], A[11], A[12], A[13], A[14], A[15], A[16], A[17], A[18], A[19], A[20], A[21], A[22], A[23], A[24], A[25], A[26], A[27], A[28], A[29], A[30], A[31]);
  Multiplexer #(.Bits(32)) multiplexer_1 (.sel(CT[6]), .in_0(A), .in_1(invert_32_1_o), .out(multiplexer_1_out));
  BitExtender #(.inputBits(1), .outputBits(31)) bitextender_1 (.in(c_i), .out(bitextender_1_out));
  or or_2 (or_2_out, RM[0], RM[2]);
  not not_1 (not_1_out, RM[1]);
  Multiplexer multiplexer_2 (
    .sel(CT[7]), .in_0(bitextender_1_out[0]), .in_1(multiplexer_1_out[31]), .out(multiplexer_2_out[0]));
  or or_3 (or_3_out, B[5], B[6], B[7], B[8], B[9], B[10], B[11], B[12], B[13], B[14], B[15], B[16], B[17], B[18], B[19], B[20], B[21], B[22], B[23], B[24], B[25], B[26], B[27], B[28], B[29], B[30], B[31]);
  and and_1 (m_bit[0], or_2_out, not_1_out);
  Multiplexer #(.Bits(32)) multiplexer_3 (
    .sel(B[0]), .in_0(multiplexer_1_out), .in_1({multiplexer_1_out[30:0], multiplexer_2_out[0]}),
    .out(multiplexer_3_out));
  Multiplexer #(.Bits(2)) multiplexer_4 (
    .sel(CT[7]), .in_0(bitextender_1_out[2:1]), .in_1(multiplexer_3_out[31:30]), .out(multiplexer_4_out));
  Multiplexer multiplexer_5 (.sel(B[0]), .in_0(1'b0), .in_1(multiplexer_1_out[31]), .out(multiplexer_5_out[0]));
  Multiplexer #(.Bits(32)) multiplexer_6 (
    .sel(B[1]), .in_0(multiplexer_3_out), .in_1({multiplexer_3_out[29:0], multiplexer_4_out}),
    .out(multiplexer_6_out));
  Multiplexer #(.Bits(2)) multiplexer_7 (
    .sel(B[1]), .in_0(2'b00), .in_1(multiplexer_3_out[31:30]), .out(multiplexer_5_out[2:1]));
  Multiplexer #(.Bits(4)) multiplexer_8 (
    .sel(CT[7]), .in_0(bitextender_1_out[6:3]), .in_1(multiplexer_6_out[31:28]), .out(multiplexer_8_out));
  Multiplexer #(.Bits(4)) multiplexer_9 (
    .sel(B[2]), .in_0(4'b0000), .in_1(multiplexer_6_out[31:28]), .out(multiplexer_5_out[6:3]));
  and and_2 (and_2_out, not_3_out, xor_1_out);
  Multiplexer #(.Selector_Bits(2)) multiplexer_10 (
    .sel({RM[1], m_bit[0]}), .in_0(c32), .in_1(c16), .in_2(c8), .in_3(1'b0), .out(multiplexer_10_out));
  Multiplexer #(.Bits(32)) multiplexer_11 (
    .sel(B[2]), .in_0(multiplexer_6_out), .in_1({multiplexer_6_out[27:0], multiplexer_8_out}),
    .out(multiplexer_11_out));
  Multiplexer #(.Bits(8)) multiplexer_12 (
    .sel(B[3]), .in_0({8{1'b0}}), .in_1(multiplexer_11_out[31:24]), .out(multiplexer_5_out[14:7]));
  and and_3 (and_3_out, or_3_out, not_2_out);
  not not_2 (not_2_out, CT[7]);
  or or_4 (F_O[3], and_9_out, and_2_out);
  xor xor_1 (xor_1_out, multiplexer_10_out, CT[1]);
  xor xor_2 (xor_2_out, F_I[3], CT[1]);
  assign xor_3_out = B ^ expand_32_1_o;  // XOr xor_3, 32 bits wide
  Multiplexer #(.Bits(8)) multiplexer_13 (
    .sel(CT[7]), .in_0(bitextender_1_out[14:7]), .in_1(multiplexer_11_out[31:24]), .out(multiplexer_13_out));
  Multiplexer #(.Bits(16)) multiplexer_14 (
    .sel(B[4]), .in_0({16{1'b0}}), .in_1(multiplexer_16_out[31:16]), .out(multiplexer_5_out[30:15]));
  Multiplexer multiplexer_15 (.sel(and_3_out), .in_0(or_5_out), .in_1(or_1_out), .out(multiplexer_15_out));
  assign and_4_out = A & xor_3_out;  // And and_4, 32 bits wide
  assign xor_4_out = A ^ xor_3_out;  // XOr xor_4, 32 bits wide
  Multiplexer #(.Bits(32)) multiplexer_16 (
    .sel(B[3]), .in_0(multiplexer_11_out), .in_1({multiplexer_11_out[23:0], multiplexer_13_out}),
    .out(multiplexer_16_out));
  Multiplexer multiplexer_17 (.sel(CT[0]), .in_0(xor_2_out), .in_1(CT[1]), .out(c_i));
  expand_32 expand_32_1 (.I(CT[1]), .O(expand_32_1_o));
  Multiplexer #(.Bits(16)) multiplexer_18 (
    .sel(CT[7]), .in_0(bitextender_1_out[30:15]), .in_1(multiplexer_16_out[31:16]), .out(multiplexer_18_out));
  Multiplexer #(.Selector_Bits(2)) multiplexer_19 (
    .sel({RM[1], m_bit[0]}), .in_0(A[31]), .in_1(A[15]), .in_2(A[7]), .in_3(1'b0), .out(multiplexer_19_out));
  LCG_32 lcg_32_1 (
    .C_n(c_i), .P(xor_4_out), .G(and_4_out), .C_o(c32),
    .C({lcg_32_1_c[31:17], c16, lcg_32_1_c[15:9], c8, lcg_32_1_c[7:5], F_O[4], lcg_32_1_c[3:0]}));  // open: G_o, P_o
  expand_32 expand_32_2 (.I(CT[2]), .O(expand_32_2_o));
  Multiplexer #(.Bits(32)) multiplexer_20 (
    .sel(B[4]), .in_0(multiplexer_16_out), .in_1({multiplexer_16_out[15:0], multiplexer_18_out}),
    .out(multiplexer_20_out));
  or or_5 (or_5_out, multiplexer_5_out[30], multiplexer_5_out[29], multiplexer_5_out[28], multiplexer_5_out[27], multiplexer_5_out[26], multiplexer_5_out[25], multiplexer_5_out[24], multiplexer_5_out[23], multiplexer_5_out[22], multiplexer_5_out[21], multiplexer_5_out[20], multiplexer_5_out[19], multiplexer_5_out[18], multiplexer_5_out[17], multiplexer_5_out[16], multiplexer_5_out[15], multiplexer_5_out[14], multiplexer_5_out[13], multiplexer_5_out[12], multiplexer_5_out[11], multiplexer_5_out[10], multiplexer_5_out[9], multiplexer_5_out[8], multiplexer_5_out[7], multiplexer_5_out[6], multiplexer_5_out[5], multiplexer_5_out[4], multiplexer_5_out[3], multiplexer_5_out[2], multiplexer_5_out[1], multiplexer_5_out[0]);
  Multiplexer #(.Selector_Bits(2)) multiplexer_21 (
    .sel({RM[1], m_bit[0]}), .in_0(xor_3_out[31]), .in_1(xor_3_out[15]), .in_2(xor_3_out[7]), .in_3(1'b0),
    .out(multiplexer_21_out));
  assign and_5_out = and_4_out & expand_32_2_o;  // And and_5, 32 bits wide
  assign and_6_out = xor_4_out & expand_32_3_o;  // And and_6, 32 bits wide
  expand_32 expand_32_3 (.I(CT[3]), .O(expand_32_3_o));
  invert_32 invert_32_2 (.I(multiplexer_20_out), .O(invert_32_2_o));
  Multiplexer #(.Selector_Bits(2)) multiplexer_22 (
    .sel({RM[1], m_bit[0]}), .in_0(R_O[31]), .in_1(R_O[15]), .in_2(R_O[7]), .in_3(1'b0),
    .out(multiplexer_22_out));
  assign or_6_out = and_5_out | and_6_out;  // Or or_6, 32 bits wide
  expand_32 expand_32_4 (.I(CT[4]), .O(expand_32_4_o));
  Multiplexer #(.Bits(32)) multiplexer_23 (
    .sel(CT[6]), .in_0(multiplexer_20_out), .in_1(invert_32_2_o), .out(multiplexer_23_out));
  xnor xnor_1 (xnor_1_out, multiplexer_19_out, multiplexer_21_out);
  xor xor_5 (xor_5_out, multiplexer_21_out, multiplexer_22_out);
  assign and_7_out = {lcg_32_1_c[31:17], c16, lcg_32_1_c[15:9], c8, lcg_32_1_c[7:5], F_O[4], lcg_32_1_c[3:0]} & expand_32_4_o;  // And and_7, 32 bits wide
  and and_8 (F_O[5], xnor_1_out, xor_5_out);
  assign xor_6_out = and_7_out ^ or_6_out;  // XOr xor_6, 32 bits wide
  not not_3 (not_3_out, CT[5]);
  and and_9 (and_9_out, multiplexer_15_out, CT[5]);
  not not_4 (not_4_out, and_3_out);
  not not_5 (not_5_out, CT[8]);
  not not_6 (not_6_out, CT[5]);
  not not_7 (F_O[0], or_7_out);
  and and_10 (F_O[2], ~multiplexer_22_out, or_7_out);  // And
  and and_11 (F_O[1], multiplexer_22_out, or_7_out);
  and and_12 (and_12_out[0], CT[5], not_4_out, not_5_out);
  and and_13 (and_12_out[1], not_6_out, CT[8]);
  Multiplexer #(.Selector_Bits(2), .Bits(32)) multiplexer_24 (
    .sel(and_12_out), .in_0(xor_6_out), .in_1(multiplexer_23_out), .in_2(E), .in_3(E), .out(R_O));
  or or_7 (or_7_out, R_O[0], R_O[1], R_O[2], R_O[3], R_O[4], R_O[5], R_O[6], R_O[7], R_O[8], R_O[9], R_O[10], R_O[11], R_O[12], R_O[13], R_O[14], R_O[15], R_O[16], R_O[17], R_O[18], R_O[19], R_O[20], R_O[21], R_O[22], R_O[23], R_O[24], R_O[25], R_O[26], R_O[27], R_O[28], R_O[29], R_O[30], R_O[31]);

  assign E_A = A;
  assign E_B = B;
  assign F_O[7:6] = {F_I[7], 1'b1};

  // Other names for the same wires on the sheet: c4 = F_O[4]; ans[31:0] = R_O; c_o = F_O[3]; E_I[31:0] = E;
  //   F[7:0] = F_I; n_o = F_O[1]; o_o = F_O[5]; p_o = F_O[2]; m_bit[1] = RM[1]; z_o = F_O[0]

  // Notes on the sheet:
  //   CT: control:
  //   0: disableCarry
  //   1: subMode
  //   2: andSel
  //   3: xorSel
  //   4: carryCalc
  //   5: shift
  //   6: invShift
  //   7: roll
  //   8: exp
  //   E: expand in
  //   RM: register mode:
  //   0: 32
  //   1: 16L
  //   2: 8L
  //   3: 8H
  //   4: 16H
  //   5: S16L
  //   6: S8L
  //   7: S8H
endmodule
