// Digital circuit bus16-demux.dig as structural Verilog
module bus16_demux (
  input  [15:0] bus,
  input  [3:0] id,
  input  E
);

  wire [15:0] demultiplexer_1_out_15;

  Demultiplexer #(.Selector_Bits(4)) demultiplexer_1 (
    .sel(id), .in(E), .out_0(demultiplexer_1_out_15[0]), .out_1(demultiplexer_1_out_15[1]),
    .out_2(demultiplexer_1_out_15[2]), .out_3(demultiplexer_1_out_15[3]), .out_4(demultiplexer_1_out_15[4]),
    .out_5(demultiplexer_1_out_15[5]), .out_6(demultiplexer_1_out_15[6]), .out_7(demultiplexer_1_out_15[7]),
    .out_8(demultiplexer_1_out_15[8]), .out_9(demultiplexer_1_out_15[9]),
    .out_10(demultiplexer_1_out_15[10]), .out_11(demultiplexer_1_out_15[11]),
    .out_12(demultiplexer_1_out_15[12]), .out_13(demultiplexer_1_out_15[13]),
    .out_14(demultiplexer_1_out_15[14]), .out_15(demultiplexer_1_out_15[15]));
  assign bus[0] = demultiplexer_1_out_15[0] ? 1'b1 : 1'bz;  // Driver driver_1
  assign bus[1] = demultiplexer_1_out_15[1] ? 1'b1 : 1'bz;  // Driver driver_2
  assign bus[2] = demultiplexer_1_out_15[2] ? 1'b1 : 1'bz;  // Driver driver_3
  assign bus[3] = demultiplexer_1_out_15[3] ? 1'b1 : 1'bz;  // Driver driver_4
  assign bus[4] = demultiplexer_1_out_15[4] ? 1'b1 : 1'bz;  // Driver driver_5
  assign bus[5] = demultiplexer_1_out_15[5] ? 1'b1 : 1'bz;  // Driver driver_6
  assign bus[6] = demultiplexer_1_out_15[6] ? 1'b1 : 1'bz;  // Driver driver_7
  assign bus[7] = demultiplexer_1_out_15[7] ? 1'b1 : 1'bz;  // Driver driver_8
  assign bus[8] = demultiplexer_1_out_15[8] ? 1'b1 : 1'bz;  // Driver driver_9
  assign bus[9] = demultiplexer_1_out_15[9] ? 1'b1 : 1'bz;  // Driver driver_10
  assign bus[10] = demultiplexer_1_out_15[10] ? 1'b1 : 1'bz;  // Driver driver_11
  assign bus[11] = demultiplexer_1_out_15[11] ? 1'b1 : 1'bz;  // Driver driver_12
  assign bus[12] = demultiplexer_1_out_15[12] ? 1'b1 : 1'bz;  // Driver driver_13
  assign bus[13] = demultiplexer_1_out_15[13] ? 1'b1 : 1'bz;  // Driver driver_14
  assign bus[14] = demultiplexer_1_out_15[14] ? 1'b1 : 1'bz;  // Driver driver_15
  assign bus[15] = demultiplexer_1_out_15[15] ? 1'b1 : 1'bz;  // Driver driver_16
endmodule
