// Digital circuit bus16x2-demux.dig as structural Verilog
module bus16x2_demux (
  input  [15:0] bus_1,
  input  [3:0] id,
  input  E,
  input  [15:0] bus_2
);

  wire [15:0] demultiplexer_1_out_15;

  Demultiplexer #(.Selector_Bits(4)) demultiplexer_1 (
    .sel(id), .in(E), .out_0(demultiplexer_1_out_15[0]), .out_1(demultiplexer_1_out_15[1]),
    .out_2(demultiplexer_1_out_15[2]), .out_3(demultiplexer_1_out_15[3]), .out_4(demultiplexer_1_out_15[4]),
    .out_5(demultiplexer_1_out_15[5]), .out_6(demultiplexer_1_out_15[6]), .out_7(demultiplexer_1_out_15[7]),
    .out_8(demultiplexer_1_out_15[8]), .out_9(demultiplexer_1_out_15[9]),
    .out_10(demultiplexer_1_out_15[10]), .out_11(demultiplexer_1_out_15[11]),
    .out_12(demultiplexer_1_out_15[12]), .out_13(demultiplexer_1_out_15[13]),
    .out_14(demultiplexer_1_out_15[14]), .out_15(demultiplexer_1_out_15[15]));
  assign bus_1[0] = demultiplexer_1_out_15[0] ? 1'b1 : 1'bz;  // Driver driver_1
  assign bus_1[1] = demultiplexer_1_out_15[1] ? 1'b1 : 1'bz;  // Driver driver_2
  assign bus_1[2] = demultiplexer_1_out_15[2] ? 1'b1 : 1'bz;  // Driver driver_3
  assign bus_1[3] = demultiplexer_1_out_15[3] ? 1'b1 : 1'bz;  // Driver driver_4
  assign bus_1[4] = demultiplexer_1_out_15[4] ? 1'b1 : 1'bz;  // Driver driver_5
  assign bus_1[5] = demultiplexer_1_out_15[5] ? 1'b1 : 1'bz;  // Driver driver_6
  assign bus_1[6] = demultiplexer_1_out_15[6] ? 1'b1 : 1'bz;  // Driver driver_7
  assign bus_1[7] = demultiplexer_1_out_15[7] ? 1'b1 : 1'bz;  // Driver driver_8
  assign bus_1[8] = demultiplexer_1_out_15[8] ? 1'b1 : 1'bz;  // Driver driver_9
  assign bus_1[9] = demultiplexer_1_out_15[9] ? 1'b1 : 1'bz;  // Driver driver_10
  assign bus_1[10] = demultiplexer_1_out_15[10] ? 1'b1 : 1'bz;  // Driver driver_11
  assign bus_1[11] = demultiplexer_1_out_15[11] ? 1'b1 : 1'bz;  // Driver driver_12
  assign bus_1[12] = demultiplexer_1_out_15[12] ? 1'b1 : 1'bz;  // Driver driver_13
  assign bus_1[13] = demultiplexer_1_out_15[13] ? 1'b1 : 1'bz;  // Driver driver_14
  assign bus_1[14] = demultiplexer_1_out_15[14] ? 1'b1 : 1'bz;  // Driver driver_15
  assign bus_1[15] = demultiplexer_1_out_15[15] ? 1'b1 : 1'bz;  // Driver driver_16
  assign bus_2[0] = demultiplexer_1_out_15[0] ? 1'b1 : 1'bz;  // Driver driver_17
  assign bus_2[1] = demultiplexer_1_out_15[1] ? 1'b1 : 1'bz;  // Driver driver_18
  assign bus_2[2] = demultiplexer_1_out_15[2] ? 1'b1 : 1'bz;  // Driver driver_19
  assign bus_2[3] = demultiplexer_1_out_15[3] ? 1'b1 : 1'bz;  // Driver driver_20
  assign bus_2[4] = demultiplexer_1_out_15[4] ? 1'b1 : 1'bz;  // Driver driver_21
  assign bus_2[5] = demultiplexer_1_out_15[5] ? 1'b1 : 1'bz;  // Driver driver_22
  assign bus_2[6] = demultiplexer_1_out_15[6] ? 1'b1 : 1'bz;  // Driver driver_23
  assign bus_2[7] = demultiplexer_1_out_15[7] ? 1'b1 : 1'bz;  // Driver driver_24
  assign bus_2[8] = demultiplexer_1_out_15[8] ? 1'b1 : 1'bz;  // Driver driver_25
  assign bus_2[9] = demultiplexer_1_out_15[9] ? 1'b1 : 1'bz;  // Driver driver_26
  assign bus_2[10] = demultiplexer_1_out_15[10] ? 1'b1 : 1'bz;  // Driver driver_27
  assign bus_2[11] = demultiplexer_1_out_15[11] ? 1'b1 : 1'bz;  // Driver driver_28
  assign bus_2[12] = demultiplexer_1_out_15[12] ? 1'b1 : 1'bz;  // Driver driver_29
  assign bus_2[13] = demultiplexer_1_out_15[13] ? 1'b1 : 1'bz;  // Driver driver_30
  assign bus_2[14] = demultiplexer_1_out_15[14] ? 1'b1 : 1'bz;  // Driver driver_31
  assign bus_2[15] = demultiplexer_1_out_15[15] ? 1'b1 : 1'bz;  // Driver driver_32
endmodule
