// Digital circuit computer-32-test.dig as structural Verilog
module computer_32_test (
  input  C
);

  wire and_1_out, and_2_out, and_3_out, and_4_out, and_5_out, and_6_out, and_7_out, and_8_out, and_9_out,
       comparator_1_eq, comparator_2_eq, comparator_3_eq, comparator_4_eq, comparator_5_eq, comparator_6_eq,
       comparator_7_eq, cpu_32_1_clk_str, cpu_32_1_csh_run, cpu_32_1_d_ld, cpu_32_1_d_st, cpu_32_1_dma_str,
       cpu_32_1_i_ld, cpu_32_1_int_out, cpu_32_1_int_str, cpu_32_1_mmu_str, cpu_test_1_p2, cpu_test_1_p3,
       cpu_test_1_p4, cpu_test_1_p5, cpu_test_1_p11, cpu_test_1_p13, cpu_test_1_p15, cpu_test_1_p18,
       cpu_test_1_p20, dipswitch_5_out, dipswitch_6_out, dipswitch_7_out, dipswitch_8_out, dipswitch_9_out,
       dipswitch_10_out, ipu_test_1_p1, ipu_test_1_p2, ipu_test_1_p3, ipu_test_1_p4, ipu_test_1_p5,
       ipu_test_1_p6, ipu_test_1_p7, ipu_test_1_p8, ipu_test_1_p9, ipu_test_1_p10, ipu_test_1_p11,
       ipu_test_1_p12, mmu_d_1_p1, mmu_d_1_p2, mmu_d_1_p3, mmu_d_1_p4, mmu_d_1_p5, mmu_d_1_p14;
  wire [0:0] keyboard_1_av;
  wire [1:0] cpu_32_1_csh_mode, cpu_32_1_mmu_sel;
  wire [2:0] cpu_32_1_dma_sel;
  wire [15:0] keyboard_1_d;
  wire [31:0] driver_1_out, driver_2_out, pulldown_1_out, pulldown_2_out, ramdualaccess_1_d1,
       ramdualaccess_1_d2, register_1_q;

  // IPU_test ipu_test_1: pin names not known; wires that end beside it: ipu_test_1_p1, ipu_test_1_p2, ipu_test_1_p3, ipu_test_1_p4, ipu_test_1_p5, ipu_test_1_p6, ipu_test_1_p7, ipu_test_1_p8, ipu_test_1_p9, ipu_test_1_p10, ipu_test_1_p11, ipu_test_1_p12
  // cpu_test cpu_test_1: pin names not known; wires that end beside it: C, cpu_test_1_p2, cpu_test_1_p3, cpu_test_1_p4, cpu_test_1_p5, ipu_test_1_p1, ipu_test_1_p2, ipu_test_1_p3, ipu_test_1_p4, ipu_test_1_p5, cpu_test_1_p11, ipu_test_1_p6, cpu_test_1_p13, ipu_test_1_p7, cpu_test_1_p15, ipu_test_1_p8, ipu_test_1_p9, cpu_test_1_p18, ipu_test_1_p10, cpu_test_1_p20, ipu_test_1_p11, ipu_test_1_p12
  DipSwitch dipswitch_1 (.out(cpu_test_1_p2));
  DipSwitch dipswitch_2 (.out(cpu_test_1_p3));
  DipSwitch dipswitch_3 (.out(cpu_test_1_p4));
  DipSwitch dipswitch_4 (.out(cpu_test_1_p5));
  // MMU_D mmu_d_1: pin names not known; wires that end beside it: mmu_d_1_p1, mmu_d_1_p2, mmu_d_1_p3, mmu_d_1_p4, mmu_d_1_p5, mmu_d_1_p2, mmu_d_1_p5, mmu_d_1_p3, cpu_test_1_p20, cpu_test_1_p18, cpu_test_1_p13, cpu_test_1_p15, cpu_test_1_p11, mmu_d_1_p14, mmu_d_1_p1, mmu_d_1_p14, mmu_d_1_p4
  computer_32 computer_32_1 ();  // open: C
  cpu_32 cpu_32_1 (
    .C(C), .E(dipswitch_5_out), .bus_e(dipswitch_6_out), .run(dipswitch_7_out), .I_valid(1'b1),
    .I_D__bus(driver_2_out), .I_A__bus(pulldown_1_out), .I_LD(cpu_32_1_i_ld), .D_valid(1'b1),
    .D_D__bus(driver_1_out), .D_A__bus(pulldown_2_out), .D_LD(cpu_32_1_d_ld), .D_ST(cpu_32_1_d_st),
    .INT_nor(dipswitch_8_out), .INT_nmk(dipswitch_9_out), .INT_out(cpu_32_1_int_out),
    .INT_str(cpu_32_1_int_str), .CLK_str(cpu_32_1_clk_str), .CSH_run(cpu_32_1_csh_run),
    .CSH_mode(cpu_32_1_csh_mode), .DMA_str(cpu_32_1_dma_str), .DMA_sel(cpu_32_1_dma_sel),
    .MMU_str(cpu_32_1_mmu_str), .MMU_sel(cpu_32_1_mmu_sel));  // open: D_MD
  DipSwitch dipswitch_5 (.out(dipswitch_5_out));
  DipSwitch #(.dipDefault("true")) dipswitch_6 (.out(dipswitch_6_out));
  DipSwitch dipswitch_7 (.out(dipswitch_7_out));
  PullDown #(.Bits(32)) pulldown_1 (.out(pulldown_1_out));
  PullDown #(.Bits(32)) pulldown_2 (.out(pulldown_2_out));
  DipSwitch dipswitch_8 (.out(dipswitch_8_out));
  DipSwitch dipswitch_9 (.out(dipswitch_9_out));
  and and_1 (and_1_out, comparator_1_eq, cpu_32_1_d_ld);
  and and_2 (and_2_out, cpu_32_1_d_st, comparator_1_eq);
  Comparator #(.Bits(6)) comparator_1 (.a(pulldown_2_out[31:26]), .b({6{1'b0}}), .eq(comparator_1_eq));  // open: gt, lt
  Comparator #(.Bits(6)) comparator_2 (.a(pulldown_1_out[31:26]), .b({6{1'b0}}), .eq(comparator_2_eq));  // open: gt, lt
  Comparator #(.Bits(6)) comparator_3 (.a(pulldown_2_out[31:26]), .b(6'b000010), .eq(comparator_3_eq));  // open: gt, lt
  Comparator #(.Bits(30)) comparator_4 (
    .a(pulldown_2_out[31:2]), .b(30'h1000000), .eq(comparator_4_eq));  // open: gt, lt
  Comparator #(.Bits(30)) comparator_5 (
    .a(pulldown_2_out[31:2]), .b(30'h1000001), .eq(comparator_5_eq));  // open: gt, lt
  Comparator #(.Bits(30)) comparator_6 (
    .a(pulldown_2_out[31:2]), .b(30'h1000002), .eq(comparator_6_eq));  // open: gt, lt
  Comparator #(.Bits(30)) comparator_7 (
    .a(pulldown_2_out[31:2]), .b(30'h1000003), .eq(comparator_7_eq));  // open: gt, lt
  and and_3 (and_3_out, comparator_2_eq, cpu_32_1_i_ld);
  and and_4 (and_4_out, comparator_3_eq, cpu_32_1_d_ld);
  and and_5 (and_5_out, cpu_32_1_d_st, comparator_3_eq);
  RAMDualAccess #(.AddrBits(24), .isProgramMemory("true"), .Bits(32)) ramdualaccess_1 (
    .str(and_2_out), .C(C), .ld(1'b1), .A1(pulldown_2_out[25:2]), .Din1(driver_1_out),
    .A2(pulldown_1_out[25:2]), .D1(ramdualaccess_1_d1), .D2(ramdualaccess_1_d2));
  and and_6 (and_6_out, cpu_32_1_d_ld, comparator_4_eq);
  and and_7 (and_7_out, cpu_32_1_d_ld, comparator_5_eq);
  and and_8 (and_8_out, cpu_32_1_d_st, C, comparator_6_eq);
  and and_9 (and_9_out, cpu_32_1_d_st, comparator_7_eq);
  assign driver_1_out = and_1_out ? ramdualaccess_1_d1 : 32'bz;  // Driver driver_1
  assign driver_2_out = and_3_out ? ramdualaccess_1_d2 : 32'bz;  // Driver driver_2
  GraphicCard #(.graphicHeight(90), .Bits(32)) graphiccard_1 (
    .A(pulldown_2_out[16:2]), .str(and_5_out), .C(C), .ld(and_4_out), .B(dipswitch_10_out), .D(driver_1_out));
  DipSwitch dipswitch_10 (.out(dipswitch_10_out));
  Keyboard keyboard_1 (.C(and_8_out), .en(1'b1), .D(keyboard_1_d), .av(keyboard_1_av[0]));
  Register #(.Bits(32)) register_1 (.D(driver_1_out), .C(C), .en(and_5_out), .Q(register_1_q));
  Terminal terminal_1 (.D(driver_1_out), .C(C), .en(and_9_out));
  // Probe on register_1_q
  assign driver_1_out = and_6_out ? {{16{1'b0}}, keyboard_1_d} : 32'bz;  // Driver driver_3
  assign driver_1_out = and_7_out ? {{31{1'b0}}, keyboard_1_av[0]} : 32'bz;  // Driver driver_4

  // Notes on the sheet:
  //   C: Hz: 2147483647
endmodule
