// Digital circuit cpu-32 test.dig as structural Verilog
module cpu_32_test (
  input  E,
  input  [31:0] I_D__bus,
  input  [31:0] D_D__bus,
  input  [31:0] I_A__bus,
  input  [31:0] D_A__bus,
  input  INT_nor,
  input  [5:0] INT_lev,
  input  run,
  input  I_valid,
  input  D_accept,
  input  C,
  input  [31:0] INT_vec,
  input  B_used,
  input  [31:0] MMU_abs,
  input  INT_racp,
  input  boot,
  input  [31:0] reset_vec,
  output I_LD,
  output D_LD,
  output D_ST,
  output MMU_dis,
  output MMU_en,
  output INT_str,
  output [1:0] CSH_mode,
  output CSH_run,
  output [5:0] INT_rid,
  output [1:0] D_MD,
  output [31:0] MMU_base,
  output INT_acp,
  output INT_req
);

  wire alu_32_1_p6, alu_32_1_p9, ALU_A_CLR, ALU_A_CMP, ALU_A_DRD, ALU_A_DRE, ALU_A_EP, ALU_A_FRD, ALU_A_FRE,
       ALU_A_LD, ALU_A_LRD, ALU_A_STD, ALU_A_STF, ALU_A_UUD, ALU_A_UUF, ALU_A_V, ALU_A_VD, ALU_A_VF,
       ALU_B_CLR, ALU_B_CMP, ALU_B_DRD, ALU_B_DRE, ALU_B_EP, ALU_B_FRD, ALU_B_FRE, ALU_B_LD, ALU_B_LRD,
       ALU_B_STD, ALU_B_STF, ALU_B_UUD, ALU_B_UUF, ALU_B_V, ALU_B_VD, ALU_B_VF, ALU_busy, ALU_free,
       and_1_out, and_2_out, and_3_out, and_4_out, and_5_out, and_6_out, and_7_out, and_8_out, and_9_out,
       and_10_out, and_11_out, and_12_out, and_13_out, and_15_out, and_16_out, and_17_out, and_18_out,
       and_19_out, and_20_out, and_21_out, and_23_out, and_24_out, and_26_out, and_28_out, and_32_out,
       and_33_out, and_37_out, and_38_out, and_39_out, and_40_out, and_41_out, and_43_out, and_44_out,
       and_45_out, and_46_out, and_47_out, and_48_out, and_49_out, and_50_out, and_51_out, and_52_out,
       and_53_out, and_54_out, and_55_out, and_56_out, and_57_out, and_60_out, and_63_out, and_64_out,
       and_65_out, and_66_out, and_67_out, and_68_out, and_69_out, and_70_out, and_71_out, and_72_out,
       and_73_out, and_74_out, and_76_out, and_77_out, and_78_out, and_79_out, and_82_out, and_83_out,
       and_87_out, and_88_out, and_89_out, and_90_out, and_91_out, and_92_out, and_93_out, and_94_out,
       and_95_out, and_96_out, and_97_out, and_98_out, and_100_out, and_101_out, and_104_out, and_105_out,
       and_110_out, and_116_out, and_117_out, and_118_out, and_119_out, and_120_out, and_121_out,
       and_122_out, and_123_out, and_124_out, and_125_out, and_126_out, and_127_out, and_128_out,
       and_131_out, and_133_out, and_134_out, and_139_out, and_140_out, and_141_out, and_142_out,
       and_143_out, and_144_out, and_147_out, and_148_out, and_149_out, and_150_out, and_152_out,
       and_153_out, and_154_out, and_155_out, and_157_out, and_158_out, and_159_out, and_160_out,
       and_161_out, and_162_out, and_163_out, and_169_out, and_170_out, and_173_out, and_174_out,
       and_175_out, and_176_out, and_177_out, and_178_out, and_179_out, and_180_out, and_184_out,
       and_189_out, and_191_out, and_192_out, and_193_out, and_194_out, and_195_out, and_196_out,
       and_197_out, and_198_out, and_199_out, and_201_out, and_202_out, and_203_out, and_204_out,
       and_209_out, B, bitselector_1_out, boot_t, BTB_JP, BTB_override, C_ct, C_dt, clr, clr_ep, clr_self,
       clrs_ep, com1, com1_ep, com1_M, com2, com2_ep, comparator_1_eq, comparator_2_eq, comparator_3_eq,
       comparator_4_eq, comparator_5_eq, comparator_6_eq, comparator_7_eq, comparator_8_eq, comparator_9_eq,
       comparator_10_eq, comparator_11_eq, comparator_12_eq, comparator_13_eq, comparator_14_eq,
       comparator_15_eq, comparator_16_gt, comparator_17_gt, comparator_18_eq, comparator_19_eq,
       comparator_20_gt, comparator_20_lt, comparator_21_eq, comparator_22_eq, comparator_23_eq,
       comparator_24_eq, CT_ALU__LD, CT_ALU__M, CT_ALU__M2, CT_ALU__WD, CT_ALU__WF, CT_BLOCK, CT_BUS__DAG,
       CT_BUS__DAM, CT_BUS__DAR, CT_BUS__DDG, CT_BUS__DDM, CT_BUS__DDR, CT_BUS__IAG, CT_BUS__IAR,
       CT_BUS__IDM, CT_BUS__IDR, CT_CALL__LD, CT_CALLM, CT_DIR__EXM, CT_DIR__LD, CT_DIR__M, CT_DIR__MS,
       CT_DISP, CT_FL__W1, CT_FL__W2, CT_FU__EPOCH, CT_FU__EX, CT_FU__MF, CT_ILVE, CT_ILVSM, CT_INT,
       CT_int__mask, CT_int__unmask, CT_INT__W, CT_INTM, CT_ISCCM, CT_ISCE, CT_ISCSM, CT_ISS__HALT,
       CT_ISS__OFL, CT_ISS__OLDB, CT_ISS__ORC, CT_ISS__OSC, CT_ISS__OSTB, CT_ISS__UFL, CT_ISS__UMM,
       CT_ISS__URA, CT_ISS__URB, CT_JMP, CT_JPU__JP, CT_JPU__LD, CT_KILL, CT_LDB__LD, CT_MB__LD, CT_MB__OFFM,
       CT_MB__ST, CT_MVR, CT_PVECE, CT_RET__LD, CT_RF__DM, CT_RF__E, CT_RF__EX1, CT_RF__EX2, CT_RF__FLS,
       CT_RF__PCAE, CT_RF__PCH, CT_RF__PCJ, CT_RF__PCR, CT_RF__PCSE, CT_RF__SCAE, CT_RF__SCD, CT_RF__SCSE,
       CT_RF__SCSRE, CT_RF__SCSS, CT_RF__W1, CT_RF__W2, CT_ROB__EX__E, CT_ROB__FL__STA, CT_ROB__FL__STB,
       CT_ROB__GEN__STA, CT_ROB__GEN__STB, CT_ROB__INT__STA, CT_ROB__INT__STB, CT_ROB__ST__E, CT_rollback,
       CT_SC__W1, CT_SC__W2, CT_STB__LD, CT_TRAP__LD, CT_UBTB, CT_USCB, d_ff_1_q, d_ff_3_q, d_ff_7_q,
       d_ff_9_nq, d_ff_11_q, d_ff_12_q, d_ff_13_q, d_ff_32_q, d_ff_33_nq, d_ff_38_q, dc_e, DC_q,
       dipswitch_1_out, dipswitch_2_out, dipswitch_3_out, dipswitch_4_out, dipswitch_5_out, dipswitch_6_out,
       dipswitch_7_out, dipswitch_8_out, dipswitch_9_out, dipswitch_10_out, dipswitch_11_out,
       dipswitch_12_out, dipswitch_13_out, DIR_busy, DIR_CLR, DIR_EP, DIR_EX, DIR_free, DIR_LD, DIR_RD,
       DIR_ST, DIR_V, E_t, epoch_DP, epoch_IS, ex_nop, ext_en, Fl_ECLR, Fl_INT, Fl_JPU, Fl_JPU__EP, Fl_MEM,
       FL_MEM__EP, FOR_UA, FOR_UB, FOR_UF, ft_e, FT_q, halt_FT_DC_ISS, halted, hlt, id_full,
       id_manager_debug_1_eclr_ep, id_manager_debug_1_v, inst_comp_1_a_new, inst_comp_2_a_new,
       inst_comp_3_a_new, inst_comp_4_a_new, inst_comp_5_a_new, inst_comp_6_a_new, inst_comp_7_a_new,
       inst_comp_9_a_new, inst_comp_11_a_new, inst_comp_12_a_new, int_accept, int_enable, int_epoch,
       INT_HALT, int_mask, int_mask_iv, ISS_kernel, ISS_q, issue, issue_e, JPU_A__ST, JPU_BTB__J,
       JPU_BTB__ST, JPU_BTB__V, JPU_CALL, JPU_free, JPU_INT, JPU_JP, JPU_LD, JPU_MF, JPU_MFE, JPU_MISS,
       JPU_RET, kernel_inst, LDB_B__EP, LDB_B__MF, LDB_B__RD, LDB_B__ST, LDB_busy, LDB_forward, LDB_ldV,
       LDB_M__EP, LDB_M__V, load_buffer_debug_1_ep_o, load_buffer_debug_1_fl, load_buffer_debug_1_fl_ep,
       load_buffer_debug_1_full, load_buffer_debug_1_mf_o, load_buffer_debug_1_v, MB_busy, MB_ep, MB_free,
       MB_LD, MB_ld__e, MB_LDB__LD, MB_MF, MB_MFE, MB_st__e, MB_STB__LD, MB_type__st, MEM_AC, MEM_BF__free,
       MEM_CLR, MEM_EP, MEM_LD, MEM_LD__CLR, MEM_LD__EP, MEM_LD__RD, MEM_LD__REC, MEM_RD, MEM_TYPE__ST, mode,
       monoflop_1_q, monoflop_2_q, multiplexer_9_out, multiplexer_12_out, multiplexer_18_out,
       multiplexer_20_out, multiplexer_23_out, multiplexer_24_out, multiplexer_26_out, multiplexer_27_out,
       multiplexer_28_out, multiplexer_34_out, multiplexer_42_out, multiplexer_43_out, multiplexer_44_out,
       multiplexer_52_out, multiplexer_55_out, multiplexer_56_out, multiplexer_57_out, multiplexer_58_out,
       multiplexer_59_out, multiplexer_63_out, multiplexer_66_out, multiplexer_67_out, multiplexer_68_out,
       multiplexer_76_out, nand_11_out, nand_12_out, nor_1_out, nor_2_out, nor_3_out, nor_4_out, nor_7_out,
       nor_8_out, nor_10_out, nor_11_out, not_2_out, not_6_out, not_7_out, not_9_out, not_10_out, not_11_out,
       not_12_out, not_13_out, not_14_out, not_16_out, not_17_out, not_19_out, not_20_out, not_22_out,
       not_23_out, not_24_out, not_27_out, not_29_out, not_31_out, not_34_out, not_35_out, or_1_out,
       or_2_out, or_4_out, or_5_out, or_6_out, or_7_out, or_9_out, or_10_out, or_11_out, or_12_out,
       or_13_out, or_22_out, or_23_out, or_24_out, or_26_out, or_27_out, or_28_out, or_31_out, or_33_out,
       or_34_out, or_35_out, or_36_out, or_39_out, or_40_out, or_41_out, or_44_out, or_45_out, or_46_out,
       or_47_out, or_48_out, or_50_out, or_52_out, or_53_out, or_54_out, or_55_out, or_56_out, or_57_out,
       or_58_out, or_59_out, or_60_out, or_62_out, or_63_out, or_64_out, or_65_out, or_69_out, or_70_out,
       or_73_out, PCA, priorityencoder_3_any, register_24_q, register_25_q, register_26_q, register_33_q,
       register_34_q, register_35_q, register_42_q, register_45_q, register_48_q, register_67_q,
       register_70_q, RET_EPOCH, ROB_FL_EPA, ROB_FL_EPB, ROB_GEN_EPA, ROB_GEN_EPB, ROB_GEN_EX1, ROB_GEN_EX2,
       rs_ff_1_nq, rs_ff_3_q, rs_ff_6_nq, rs_ff_6_q, rs_ff_7_q, rs_ff_8_nq, rs_ff_8_q, rs_ff_9_nq,
       rs_ff_10_nq, rs_ff_11_nq, rs_ff_12_nq, rs_ff_13_nq, rs_ff_18_q, rs_ff_19_q, rs_ff_20_q, rs_ff_21_q,
       rs_ff_24_nq, rs_ff_as_1_q, RS_full, run_t, RX_ILVE, RX_ILVM, RX_ISCE, RX_ISCM, RX_PGBSE, RX_PGBSM,
       RX_PVECE, RX_PVECM, STB_busy, STB_M__EP, STB_M__V, store_buffer_debug_1_full, sub_1_c_o, TRAP_busy,
       TRAP_EP, TRAP_free, TRAP_IRD, TRAP_RD, TRAP_ST, V_q, \wait , waiting, xor_2_out;
  wire [0:0] and_99_out, JPU_BTBPK, keyboard_1_av;
  wire [1:0] and_112_out, and_114_out, and_129_out, and_130_out, bitextender_6_out, bitextender_7_out,
       d_ff_14_q, d_ff_18_q, d_ff_19_q, d_ff_20_q, d_ff_21_q, JPU_BTB__pred, JPU_pred, LDB_M__MD, MB_MD,
       multiplexer_14_out, priorityencoder_1_num, priorityencoder_2_num, register_16_q, STB_M__MD,
       store_controller_half_1_d1_sel, store_controller_half_1_d2_sel, store_controller_half_2_d1_sel,
       store_controller_half_2_d2_sel;
  wire [1:1] or_25_out, register_46_q, register_71_q;
  wire [2:0] ALU_A_RM, ALU_B_RM, and_102_out, and_106_out, CT_ISS__UFU, CT_RF__MA, CT_RF__MB, CT_RF__SCN,
       CT_RF__WM, CT_SP__MOF, multiplexer_17_out, multiplexer_21_out, multiplexer_50_out, nand_1_out,
       nand_2_out, nand_4_out, nand_8_out, not_18_out, not_21_out, register_22_q, register_47_q,
       store_controller_1_d1_sel, store_controller_1_d2_sel;
  wire [2:1] nor_5_out;
  wire [3:0] ALU_A_INST, ALU_B_INST, clr_id, clr_sel, clrs_id, com1_inst, com2_inst, CT_FU__INST, DIR_INST,
       Fl_JPU__INST, FL_MEM__ID, FOR_IA, FOR_IB, FOR_IF, FU_I__V, id_manager_debug_1_eclr_id, inst_DP,
       inst_IS, int_inst_t, LD_id, LDB_B__INST, LDB_M__ID, load_buffer_debug_1_fl_id,
       load_buffer_debug_1_id_o, MB_INST, MEM_INST, MEM_LD__INST, multiplexer_8_out, multiplexer_25_out,
       multiplexer_41_out, multiplexer_51_out, multiplexer_62_out, multiplexer_70_out, multiplexer_75_out,
       priorityencoder_3_num, register_23_q, register_32_q, register_41_q, register_66_q, RET_INST,
       ROB_FL_INSTA, ROB_FL_INSTB, ROB_GEN_INSTA, ROB_GEN_INSTB, ROB_INT_INSTA, ROB_INT_INSTB, STB_M__ID,
       TRAP_INST;
  wire [3:2] FU_F__V;
  wire [4:0] CT_ISS__RA, CT_ISS__RB, CT_ISS__RC, CT_RF__RA, CT_RF__RB, CT_RF__WS;
  wire [4:4] FU_CLR;
  wire [5:0] CT_INT__D, d_ff_2_q, ILV, ILV_i, multiplexer_3_out, ROB_INT_A, ROB_INT_B, TRAP_INT;
  wire [6:6] and_200_out;
  wire [7:0] ALU_A_F, ALU_A_FI, ALU_A_T__F, ALU_B_F, ALU_B_FI, ALU_B_T__F, bitextender_3_out, byte_D0,
       byte_D0_iv, byte_D1, byte_D2, byte_D3, byte_I0, byte_I0_iv, byte_I1, byte_I2, byte_I3, CT_DIR__EXID,
       CT_FL__D1, CT_FL__D2, CT_FU__WR, CT_INTID, CT_RF__R1, CT_RF__R2, demultiplexer_1_out_0,
       demultiplexer_2_out_0, DIR_WR, fl_i, FU_free, LDB_B__WR, load_buffer_debug_1_wr_o, MB_WR,
       multiplexer_11_out, multiplexer_31_out, multiplexer_33_out, multiplexer_47_out, multiplexer_49_out,
       multiplexer_54_out, multiplexer_65_out, or_3_out, register_29_q, register_31_q, register_38_q,
       register_40_q, register_44_q, register_69_q, ROB_FL_A, ROB_FL_B, ROB_GEN_WA, ROB_GEN_WB, xor_3_out;
  wire [7:3] ALU_A_WR, ALU_B_WR, FU_D__V;
  wire [7:6] register_10_q;
  wire [8:0] ALU_A_CT, ALU_B_CT, CT_ALU__CT, multiplexer_32_out, multiplexer_48_out, register_30_q,
       register_39_q;
  wire [9:0] and_42_out;
  wire [15:0] and_181_out, and_183_out, and_185_out, and_186_out, and_188_out, bitextender_4_out,
       bitextender_5_out, bitextender_8_out, bitextender_10_out, bitextender_11_out, clr_16, clrs_16,
       d_ff_35_q, demultiplexer_3_out_0, demultiplexer_4_out_0, icmk_16, icmks_16, id_manager_debug_1_c16,
       id_manager_debug_1_us, id_manager_debug_1_vv1, id_manager_debug_1_vv2, INT_inst, keyboard_1_d,
       multiplexer_39_out, multiplexer_79_out, not_32_out, not_33_out, or_66_out, or_67_out, or_68_out,
       register_54_q, register_92_q, register_96_q, register_97_q, V1_inst, V2_inst;
  wire [31:0] A_q, add_1_s, add_4c32_1_s, add_4c32_2_s, alu_32_1_p8, alu_32_1_p11, alu_32_1_p12,
       alu_32_1_p14, ALU_A_A, ALU_A_B, ALU_A_R, ALU_A_T__R, ALU_B_A, ALU_B_B, ALU_B_R, ALU_B_T__R,
       bitextender_1_out, bitextender_2_out, counter_1_out, counter_2_out, CT_RF__D1, CT_RF__D2, CT_RF__DR,
       CT_SC__D1, CT_SC__D2, CT_SC__FD, d_ff_34_q, D_q, DIR, FL, HALT_PC, I_A__R_q, I_D__R_q, int_pc,
       int_vec_t, ISC, ISC_i, ISC_sc, JPU_ADDR, JPU_BTB__tar, JPU_PC, LD_addr, LDB_B__D, LDB_ldD, LDB_M__A,
       load_buffer_debug_1_fl_pc, MB_addr, MB_data, MB_PC, MEM_FPC, MEM_LD__D, multiplexer_2_out,
       multiplexer_4_out, multiplexer_10_out, multiplexer_13_out, multiplexer_15_out, multiplexer_19_out,
       multiplexer_22_out, multiplexer_29_out, multiplexer_30_out, multiplexer_35_out, multiplexer_36_out,
       multiplexer_37_out, multiplexer_38_out, multiplexer_40_out, multiplexer_45_out, multiplexer_46_out,
       multiplexer_53_out, multiplexer_60_out, multiplexer_64_out, multiplexer_69_out, multiplexer_72_out,
       multiplexer_74_out, multiplexer_77_out, multiplexer_78_out, mVec, pc_read, pc_ret, pca_i, PCS, PCS_DC,
       PCS_FT, pcs_i, PVEC, PVEC_i, R_A, R_B, register_1_q, register_11_q, register_15_q, register_17_q,
       register_27_q, register_28_q, register_36_q, register_37_q, register_43_q, register_53_q,
       register_68_q, register_91_q, ROB_GEN_DA, ROB_GEN_DB, RX_SEL, SCA, sca_i, SCS, STB_M__A, STB_M__D;
  wire [31:24] res_station_debug_1_disp_32;
  wire [36:0] and_182_out, bitextender_9_out, BTB_D_q, BTB_DP, BTB_fetch, BTB_pack__iss, BTB_packet;

  PullDown #(.Bits(32)) pulldown_1 (.out(I_A__bus));
  PullUp pullup_1 (.out(I_valid));
  // Probe on CT_RF__WS
  // Probe on CT_RF__WM
  // Probe on CT_RF__RA
  // Probe on CT_RF__MA
  // Probe on CT_RF__RB
  // Probe on CT_RF__MB
  PullDown #(.Bits(32)) pulldown_2 (.out(D_A__bus));
  // Probe inst on {byte_I0, byte_I1, byte_I2, byte_I3}
  // Probe R_A on R_A
  // Probe R_B on R_B
  // Probe PC on PCS
  // Probe SCS on SCS
  // Probe SCA on SCA
  // Probe FL on FL
  // Probe CT_BUS-_IDM on CT_BUS__IDM
  // Probe C_i on C_dt
  Comparator #(.Bits(22)) comparator_1 (.a(I_A__bus[31:10]), .b({22{1'b1}}), .eq(comparator_1_eq));  // open: gt, lt
  Comparator #(.Bits(10)) comparator_2 (.a(D_A__bus[31:22]), .b(10'h3f0), .eq(comparator_2_eq));  // open: gt, lt
  Comparator #(.Bits(10)) comparator_3 (.a(I_A__bus[31:22]), .b(10'h3f0), .eq(comparator_3_eq));  // open: gt, lt
  Comparator #(.Bits(6)) comparator_4 (.a(D_A__bus[31:26]), .b({6{1'b0}}), .eq(comparator_4_eq));  // open: gt, lt
  Comparator #(.Bits(6)) comparator_5 (.a(I_A__bus[31:26]), .b({6{1'b0}}), .eq(comparator_5_eq));  // open: gt, lt
  Comparator #(.Bits(6)) comparator_6 (.a(D_A__bus[31:26]), .b(6'b000010), .eq(comparator_6_eq));  // open: gt, lt
  and and_1 (and_1_out, comparator_1_eq, I_LD);
  and and_2 (and_2_out, D_LD, comparator_2_eq);
  and and_3 (and_3_out, I_LD, comparator_3_eq);
  and and_4 (and_4_out, D_ST, comparator_4_eq);
  and and_5 (and_5_out, comparator_4_eq, D_LD);
  and and_6 (and_6_out, I_LD, comparator_5_eq);
  and and_7 (and_7_out, comparator_6_eq, D_LD);
  and and_8 (and_8_out, D_ST, comparator_6_eq);
  Comparator #(.Bits(30)) comparator_7 (.a(D_A__bus[31:2]), .b(30'h1000000), .eq(comparator_7_eq));  // open: gt, lt
  Comparator #(.Bits(30)) comparator_8 (.a(D_A__bus[31:2]), .b(30'h1000001), .eq(comparator_8_eq));  // open: gt, lt
  Comparator #(.Bits(30)) comparator_9 (.a(D_A__bus[31:2]), .b(30'h1000002), .eq(comparator_9_eq));  // open: gt, lt
  Comparator #(.Bits(30)) comparator_10 (.a(D_A__bus[31:2]), .b(30'h1000003), .eq(comparator_10_eq));  // open: gt, lt
  ROM #(.AddrBits(6), .Bits(32)) rom_1 (.A(I_A__bus[7:2]), .sel(and_1_out), .D(I_D__bus));
  and and_9 (and_9_out, D_LD, comparator_7_eq);
  and and_10 (and_10_out, D_LD, comparator_8_eq);
  and and_11 (and_11_out, D_ST, C_dt, comparator_9_eq);
  and and_12 (and_12_out, D_ST, comparator_10_eq);
  // Probe com1 on com1
  // Probe com2 on com2
  // Probe com1_inst on com1_inst
  // Probe com2_inst on com2_inst
  // Probe PC_inst on inst_IS
  rom_test rom_test_1 (
    .D1(D_D__bus), .D2(I_D__bus), .C(C_dt), .mode(D_MD), .ld1(and_2_out), .ld2(and_3_out), ._1A(D_A__bus),
    ._2A(I_A__bus));
  ram_test ram_test_1 (
    .D1(D_D__bus), .D2(I_D__bus), .D2_V(I_valid), .str(and_4_out), .C(C_dt), .mode(D_MD), .ld1(and_5_out),
    .ld2(and_6_out), .D_in(D_D__bus), ._1A(D_A__bus), ._2A(I_A__bus));
  GraphicCard #(.graphicHeight(90), .Bits(32)) graphiccard_1 (
    .A(D_A__bus[16:2]), .str(and_8_out), .C(C_dt), .ld(and_7_out), .B(dipswitch_1_out), .D(D_D__bus));
  DipSwitch dipswitch_1 (.out(dipswitch_1_out));
  Keyboard keyboard_1 (.C(and_11_out), .en(1'b1), .D(keyboard_1_d), .av(keyboard_1_av[0]));
  Terminal #(.termWidth(100), .termHeight(50)) terminal_1 (.D(D_D__bus), .C(C_dt), .en(and_12_out));
  Register #(.Bits(32)) register_1 (.D(D_D__bus), .C(C_dt), .en(and_8_out), .Q(register_1_q));
  // Probe on register_1_q
  assign D_D__bus = and_9_out ? {{16{1'b0}}, keyboard_1_d} : 32'bz;  // Driver driver_1
  assign D_D__bus = and_10_out ? {{31{1'b0}}, keyboard_1_av[0]} : 32'bz;  // Driver driver_2
  Comparator #(.Bits(32)) comparator_11 (.a(PCS), .b(32'h40), .eq(comparator_11_eq));  // open: gt, lt
  Comparator #(.Bits(32)) comparator_12 (.a(PCS), .b(32'h58), .eq(comparator_12_eq));  // open: gt, lt
  RS_FF_AS rs_ff_as_1 (.S(run_t), .R(dipswitch_2_out), .Q(rs_ff_as_1_q));  // open: nQ
  DipSwitch dipswitch_2 (.out(dipswitch_2_out));
  LED led_1 (.in(comparator_11_eq));
  LED led_2 (.in(comparator_12_eq));
  DipSwitch #(.dipDefault("true")) dipswitch_3 (.out(dipswitch_3_out));
  DipSwitch dipswitch_4 (.out(dipswitch_4_out));
  // Probe E on E_t
  // Probe R on run_t
  // Probe issue_e on issue_e
  // Probe CT_ISS-_OLDB on CT_ISS__OLDB
  // Probe clr on clr
  // Probe halt-FT-DC-ISS on halt_FT_DC_ISS
  // Probe issue_32 on {byte_I0, byte_I1, byte_I2, byte_I3}
  // Probe disp_32 on {byte_D0, byte_D1, byte_D2, byte_D3}
  // Probe FL_MEM on Fl_MEM
  // Probe FL_JPU on Fl_JPU
  // Probe FL_ECLR on Fl_ECLR
  // Probe FL_INT on Fl_INT
  // Probe on com1
  // Probe on com2
  // Probe on com1_inst
  // Probe on com2_inst
  // Probe on epoch_IS
  // Probe on inst_IS
  Comparator #(.Bits(32)) comparator_13 (.a(counter_1_out), .b(32'h4), .eq(comparator_13_eq));  // open: gt, lt
  Comparator #(.Bits(32)) comparator_14 (.a(counter_1_out), .b(32'h8), .eq(comparator_14_eq));  // open: gt, lt
  Comparator #(.Bits(32)) comparator_15 (.a(counter_1_out), .b(32'ha), .eq(comparator_15_eq));  // open: gt, lt
  Counter #(.Bits(32)) counter_1 (
    .en(dipswitch_3_out), .C(C_dt), .clr(dipswitch_4_out), .out(counter_1_out));  // open: ovf
  Counter #(.Bits(32)) counter_2 (
    .en(rs_ff_as_1_q), .C(C_dt), .clr(dipswitch_2_out), .out(counter_2_out));  // open: ovf
  // Probe cycle on counter_1_out
  // Probe Ecycle on counter_2_out
  RS_FF_AS rs_ff_as_2 (.S(comparator_13_eq), .R(dipswitch_5_out), .Q(E_t), .nQ(B));
  DipSwitch dipswitch_5 (.out(dipswitch_5_out));
  RS_FF_AS rs_ff_as_3 (.S(comparator_14_eq), .R(comparator_15_eq), .Q(run_t));  // open: nQ
  LED led_3 (.in(MB_ld__e));
  LED led_4 (.in(MB_st__e));
  DipSwitch dipswitch_6 (.out(dipswitch_6_out));
  Multiplexer multiplexer_1 (.sel(dipswitch_7_out), .in_0(dipswitch_6_out), .in_1(C), .out(C_dt));
  DipSwitch dipswitch_7 (.out(dipswitch_7_out));
  not not_1 (C_ct, C_dt);
  Break #(.Cycles(1000000)) break_1 (.brk(Fl_ECLR));
  not not_2 (not_2_out, I_valid);
  assign CT_BUS__IDM = not_2_out ? 1'b1 : 1'bz;  // Driver driver_3
  and and_13 (and_13_out, I_valid, ft_e);
  assign CT_RF__PCSE = and_13_out ? 1'b1 : 1'bz;  // Driver driver_4
  assign CT_BUS__IAR = and_13_out ? 1'b1 : 1'bz;  // Driver driver_5
  assign CT_BUS__IAG = ft_e ? 1'b1 : 1'bz;  // Driver driver_6
  assign I_LD = ft_e ? 1'b1 : 1'bz;  // Driver driver_7
  or or_1 (or_1_out, issue, INT_acp);
  Comparator #(.Bits(32)) comparator_16 (.a(PCS), .b(mVec), .gt(comparator_16_gt));  // open: eq, lt
  BitExtender #(.inputBits(16), .outputBits(32)) bitextender_1 (.in({byte_D2, byte_D3}), .out(bitextender_1_out));
  RS_FF rs_ff_1 (.S(Fl_INT), .C(C_ct), .R(CT_INTM), .nQ(rs_ff_1_nq));  // open: Q
  and and_14 (Fl_INT, rs_ff_1_nq, int_accept);
  PullDown pulldown_3 (.out(CT_ISCSM));
  PullDown pulldown_4 (.out(CT_ISCCM));
  PullDown pulldown_5 (.out(CT_ISCE));
  PullDown pulldown_6 (.out(CT_ILVE));
  PullDown pulldown_7 (.out(JPU_INT));
  or or_2 (or_2_out, halted, waiting);
  D_FF d_ff_1 (.D(INT_nor), .C(C_dt), .Q(d_ff_1_q));  // open: nQ
  D_FF #(.Bits(6)) d_ff_2 (.D(INT_lev), .C(C_dt), .Q(d_ff_2_q));  // open: nQ
  D_FF d_ff_3 (.D(INT_nor), .C(C_dt), .Q(d_ff_3_q));  // open: nQ
  Register #(.Bits(6)) level (.D(ILV_i), .C(C_dt), .en(CT_ILVE), .Q(ILV));
  Register #(.Bits(32)) u_ISC (.D(ISC_i), .C(C_dt), .en(CT_ISCE), .Q(ISC));
  Register #(.Bits(32)) register_2 (.D(INT_vec), .C(C_dt), .en(int_enable), .Q(int_vec_t));
  and and_15 (and_15_out, nor_1_out, CT_RF__W1, CT_RF__EX1);
  LED led_5 (.in(CT_JPU__LD));
  LED led_6 (.in(D_ST));
  LED led_7 (.in(JPU_BTB__ST));
  LED led_8 (.in(Fl_MEM));
  LED led_9 (.in(epoch_IS));
  // Probe ID on inst_DP
  id_manager_debug id_manager_debug_1 (
    .C(C_ct), .\use (or_1_out), .S1_inst(V1_inst), .S2_inst(V2_inst), .E_inst(INT_inst), .clr(clr),
    .clr_self(clr_self), .clr_ep(clr_ep), .clr_id(clr_id), .epoch(epoch_IS), .id(inst_IS),
    .V(id_manager_debug_1_v), .com1(com1), .com1_id(com1_inst), .com1_ep(com1_ep), .com2(com2),
    .com2_id(com2_inst), .com2_ep(com2_ep), .ext_en(ext_en), .cmk_16(icmk_16), .clr_16(clr_16),
    .cmks_16(icmks_16), .clrs_16(clrs_16), .VV1(id_manager_debug_1_vv1), .VV2(id_manager_debug_1_vv2),
    .US(id_manager_debug_1_us), .C16(id_manager_debug_1_c16), .eclr_v(Fl_ECLR),
    .eclr_id(id_manager_debug_1_eclr_id), .eclr_ep(id_manager_debug_1_eclr_ep));
  flush_mux flush_mux_1 (
    .M_v(Fl_MEM), .M_id(FL_MEM__ID), .M_ep(FL_MEM__EP), .J_v(Fl_JPU), .J_id(Fl_JPU__INST), .J_ep(Fl_JPU__EP),
    .I_v(Fl_INT), .I_id(com1_inst), .I_ep(com1_ep), .sel(clr_sel), .self(clr_self), .m_v_2(clr),
    .m_id_2(clr_id), .m_ep_2(clr_ep), .E_v(Fl_ECLR), .E_id(id_manager_debug_1_eclr_id),
    .E_ep(id_manager_debug_1_eclr_ep));  // open: E_acp
  Add #(.Bits(32)) add_1 (.a(R_A), .b(bitextender_1_out), .c_i(1'b0), .s(add_1_s));  // open: c_o
  and and_16 (and_16_out, or_2_out, INT_nor);
  D_FF d_ff_4 (.D(d_ff_3_q), .C(C_ct), .Q(int_enable));  // open: nQ
  D_FF d_ff_5 (.D(CT_INT__W), .C(C_dt), .Q(INT_req));  // open: nQ
  D_FF #(.Bits(6)) d_ff_6 (.D(CT_INT__D), .C(C_dt), .Q(INT_rid));  // open: nQ
  Demultiplexer #(.Selector_Bits(3)) demultiplexer_1 (
    .sel(CT_RF__R1[2:0]), .in(and_15_out), .out_0(demultiplexer_1_out_0[0]),
    .out_1(demultiplexer_1_out_0[1]), .out_2(demultiplexer_1_out_0[2]), .out_3(demultiplexer_1_out_0[3]),
    .out_4(demultiplexer_1_out_0[4]), .out_5(demultiplexer_1_out_0[5]), .out_6(demultiplexer_1_out_0[6]),
    .out_7(demultiplexer_1_out_0[7]));
  and and_17 (and_17_out, 1'b0, ~comparator_16_gt);  // And
  PullDown pulldown_8 (.out(CT_ILVSM));
  Comparator #(.Bits(6)) comparator_17 (.a(d_ff_2_q), .b(ILV), .gt(comparator_17_gt));  // open: eq, lt
  nor nor_1 (nor_1_out, CT_RF__R1[7], CT_RF__R1[6], CT_RF__R1[5], CT_RF__R1[4], CT_RF__R1[3]);
  DipSwitch dipswitch_8 (.out(dipswitch_8_out));
  DipSwitch dipswitch_9 (.out(dipswitch_9_out));
  LED led_10 (.in(halt_FT_DC_ISS));
  LED led_11 (.in(clr));
  LED led_12 (.in(LDB_B__RD));
  // Probe FU on FU_free
  // Probe INST on {byte_I0, byte_I1, byte_I2, byte_I3}
  // Probe INST on {byte_D0, byte_D1, byte_D2, byte_D3}
  not not_3 (id_full, id_manager_debug_1_v);
  RS_FF u_mode (.S(and_17_out), .C(C_dt), .R(comparator_16_gt), .Q(mode));  // open: nQ
  Register #(.Bits(32)) MVR (.D(add_1_s), .C(C_dt), .en(CT_MVR), .Q(mVec));
  RS_FF rs_ff_2 (.S(Fl_INT), .C(C_ct), .R(INT_acp), .Q(INT_HALT));  // open: nQ
  RS_FF rs_ff_3 (.S(Fl_INT), .C(C_ct), .R(INT_acp), .Q(rs_ff_3_q));  // open: nQ
  Comparator #(.Bits(4)) comparator_18 (.a(inst_IS), .b(com1_inst), .eq(comparator_18_eq));  // open: gt, lt
  assign CT_JPU__LD = INT_acp ? 1'b1 : 1'bz;  // Driver driver_8
  assign JPU_INT = INT_acp ? 1'b1 : 1'bz;  // Driver driver_9
  assign CT_ISS__OSTB = INT_acp ? 1'b1 : 1'bz;  // Driver driver_10
  and and_18 (and_18_out, d_ff_1_q, int_mask_iv, comparator_17_gt);
  RS_FF rs_ff_4 (.S(CT_int__mask), .C(C_dt), .R(CT_int__unmask), .Q(int_mask), .nQ(int_mask_iv));
  Register #(.Bits(32)) register_3 (.D(PCS_DC), .C(C_dt), .en(INT_acp), .Q(int_pc));
  Register #(.Bits(4)) register_4 (.D(inst_IS), .C(C_ct), .en(INT_acp), .Q(int_inst_t));
  Register register_5 (.D(epoch_IS), .C(C_ct), .en(INT_acp), .Q(int_epoch));
  assign {or_3_out[7:5], RX_PGBSE, RX_ILVE, RX_ISCE, RX_PVECE, or_3_out[0]} = {demultiplexer_2_out_0[7:5], RX_PGBSM, RX_ILVM, RX_ISCM, RX_PVECM, demultiplexer_2_out_0[0]} | demultiplexer_1_out_0;  // Or or_3, 8 bits wide
  LED led_13 (.in(LDB_B__ST));
  LED led_14 (.in(JPU_CALL));
  and and_19 (and_19_out, JPU_CALL, dipswitch_8_out);
  LED led_15 (.in(CT_RET__LD));
  and and_20 (and_20_out, CT_RET__LD, dipswitch_9_out);
  LED led_16 (.in(LDB_forward));
  assign byte_I0_iv = ~byte_I0;  // Not not_4, 8 bits wide
  assign byte_D0_iv = ~byte_D0;  // Not not_5, 8 bits wide
  or or_4 (or_4_out, clr, \wait );
  or or_5 (or_5_out, run_t, Fl_INT);
  D_FF d_ff_7 (.D(B), .C(C_dt), .Q(d_ff_7_q));  // open: nQ
  D_FF d_ff_8 (.D(and_18_out), .C(C_ct), .Q(int_accept));  // open: nQ
  and and_21 (and_21_out, nor_2_out, CT_RF__W2, CT_RF__EX2);
  Monoflop monoflop_1 (.C(and_19_out), .R(dipswitch_10_out), .Q(monoflop_1_q));  // open: nQ
  DipSwitch dipswitch_10 (.out(dipswitch_10_out));
  Monoflop monoflop_2 (.C(and_20_out), .R(dipswitch_11_out), .Q(monoflop_2_q));  // open: nQ
  DipSwitch dipswitch_11 (.out(dipswitch_11_out));
  Register #(.Bits(32)) D (.D(D_D__bus), .C(C_dt), .en(D_ST), .Q(D_q));
  Register #(.Bits(32)) A (.D(D_A__bus), .C(C_dt), .en(D_ST), .Q(A_q));
  RS_FF FT (.S(or_5_out), .C(C_ct), .R(\wait ), .Q(FT_q), .nQ(waiting));
  not not_6 (not_6_out, halt_FT_DC_ISS);
  D_FF d_ff_9 (.D(d_ff_7_q), .C(C_dt), .nQ(d_ff_9_nq));  // open: Q
  and and_22 (INT_acp, rs_ff_3_q, comparator_18_eq, ~STB_busy);  // And
  nor nor_2 (nor_2_out, CT_RF__R2[7], CT_RF__R2[6], CT_RF__R2[5], CT_RF__R2[4], CT_RF__R2[3]);
  Demultiplexer #(.Selector_Bits(3)) demultiplexer_2 (
    .sel(CT_RF__R2[2:0]), .in(and_21_out), .out_0(demultiplexer_2_out_0[0]), .out_1(RX_PVECM),
    .out_2(RX_ISCM), .out_3(RX_ILVM), .out_4(RX_PGBSM), .out_5(demultiplexer_2_out_0[5]),
    .out_6(demultiplexer_2_out_0[6]), .out_7(demultiplexer_2_out_0[7]));
  and and_23 (and_23_out, byte_D0_iv[0], byte_D0[1], byte_D0[2], byte_D0_iv[3], byte_D0[4], byte_D0[5], byte_D0[6], byte_D0_iv[7]);
  and and_24 (and_24_out, byte_D0[0], byte_D0[1], byte_D0[2], byte_D0_iv[3], byte_D0[4], byte_D0[5], byte_D0[6], byte_D0_iv[7]);
  Break #(.Cycles(1000000)) A_2 (.brk(monoflop_1_q));
  Break #(.Cycles(1000000)) A_3 (.brk(monoflop_2_q));
  // Probe on D_q
  // Probe on A_q
  not not_7 (not_7_out, or_4_out);
  and and_25 (boot_t, d_ff_7_q, d_ff_9_nq);
  // Probe V1_inst on V1_inst
  // Probe VG1_inst on id_manager_debug_1_vv1
  // Probe V2_inst on V2_inst
  // Probe VG2_inst on id_manager_debug_1_vv2
  // Probe U_inst on id_manager_debug_1_us
  // Probe CLR_inst on id_manager_debug_1_c16
  D_FF d_ff_10 (.D(INT_acp), .C(C_ct), .Q(CT_INTM));  // open: nQ
  and and_26 (and_26_out, not_7_out, FT_q);
  Register DC (.D(and_26_out), .C(C_ct), .en(or_6_out), .Q(DC_q));
  and and_27 (ft_e, FT_q, not_6_out);
  or or_6 (or_6_out, not_6_out, or_4_out);
  Register #(.Bits(32)) register_6 (.D(PCS), .C(C_dt), .en(CT_RF__PCSE), .Q(PCS_FT));
  assign CT_RF__PCSE = boot_t ? 1'b1 : 1'bz;  // Driver driver_11
  DipSwitch dipswitch_12 (.out(dipswitch_12_out));
  Sub #(.Bits(4)) sub_1 (.a(clr_id), .b(4'b0000), .c_i(clr_self), .s(clrs_id), .c_o(sub_1_c_o));
  assign MB_LD = CT_INTM ? 1'b1 : 1'bz;  // Driver driver_12
  assign CT_MB__ST = CT_INTM ? 1'b1 : 1'bz;  // Driver driver_13
  assign CT_FU__INST = CT_INTM ? int_inst_t : 4'bz;  // Driver driver_14
  assign CT_FU__EPOCH = CT_INTM ? int_epoch : 1'bz;  // Driver driver_15
  assign CT_ISCCM = CT_INTM ? 1'b1 : 1'bz;  // Driver driver_16
  assign CT_ISCE = CT_INTM ? 1'b1 : 1'bz;  // Driver driver_17
  assign CT_RF__SCD = CT_INTM ? 1'b1 : 1'bz;  // Driver driver_18
  assign CT_RF__SCN = CT_INTM ? 3'b100 : 3'bz;  // Driver driver_19
  assign CT_ISCSM = CT_INTM ? 1'b1 : 1'bz;  // Driver driver_20
  Multiplexer #(.Bits(32)) multiplexer_2 (.sel(RX_ISCM), .in_0(CT_RF__D1), .in_1(CT_RF__D2), .out(multiplexer_2_out));
  Multiplexer #(.Bits(6)) multiplexer_3 (
    .sel(RX_ILVM), .in_0(CT_RF__D1[5:0]), .in_1(CT_RF__D2[5:0]), .out(multiplexer_3_out));
  PullDown pulldown_9 (.out(CT_int__mask));
  PullDown pulldown_10 (.out(CT_int__unmask));
  PullDown pulldown_11 (.out(CT_PVECE));
  Register #(.Bits(32)) u_PVEC (.D(PVEC_i), .C(C_dt), .en(CT_PVECE), .Q(PVEC));
  assign CT_FU__EPOCH = and_23_out ? epoch_DP : 1'bz;  // Driver driver_21
  assign CT_FU__INST = and_23_out ? inst_DP : 4'bz;  // Driver driver_22
  assign CT_TRAP__LD = and_23_out ? 1'b1 : 1'bz;  // Driver driver_23
  assign CT_INT = and_23_out ? 1'b1 : 1'bz;  // Driver driver_24
  assign CT_INTID = and_23_out ? byte_D3 : 8'bz;  // Driver driver_25
  assign CT_FU__EPOCH = and_24_out ? epoch_DP : 1'bz;  // Driver driver_26
  assign CT_FU__INST = and_24_out ? inst_DP : 4'bz;  // Driver driver_27
  assign CT_TRAP__LD = and_24_out ? 1'b1 : 1'bz;  // Driver driver_28
  and and_28 (and_28_out, not_7_out, DC_q);
  Register ISS (.D(and_28_out), .C(C_ct), .en(or_7_out), .Q(ISS_q));
  and and_29 (dc_e, DC_q, not_6_out);
  or or_7 (or_7_out, not_6_out, or_4_out);
  Register #(.Bits(32)) register_7 (.D(PCS_FT), .C(C_dt), .en(CT_RF__PCSE), .Q(PCS_DC));
  D_FF d_ff_11 (.D(boot_t), .C(C_dt), .Q(d_ff_11_q));  // open: nQ
  or or_8 (halt_FT_DC_ISS, id_full, RS_full, INT_HALT, dipswitch_13_out, dipswitch_12_out, LDB_busy, STB_busy);
  DipSwitch dipswitch_13 (.out(dipswitch_13_out));
  xor xor_1 (clrs_ep, clr_ep, sub_1_c_o);
  nor nor_3 (nor_3_out, CT_DIR__EXID[7], CT_DIR__EXID[6], CT_DIR__EXID[5], CT_DIR__EXID[4], CT_DIR__EXID[3]);
  Multiplexer #(.Selector_Bits(3), .Bits(32)) multiplexer_4 (
    .sel(CT_DIR__EXID[2:0]), .in_0(32'h1), .in_1(PVEC), .in_2(ISC), .in_3({{26{1'b0}}, ILV}),
    .in_4({32{1'b0}}), .in_5({32{1'b0}}), .in_6({32{1'b0}}), .in_7({32{1'b0}}), .out(multiplexer_4_out));
  and and_30 (issue_e, ISS_q, not_6_out);
  PullDown pulldown_12 (.out(CT_DISP));
  PullDown pulldown_13 (.out(CT_rollback));
  PullDown pulldown_14 (.out(com2));
  PullDown #(.Bits(4)) pulldown_15 (.out(com2_inst));
  PullDown pulldown_16 (.out(com1_M));
  PullDown pulldown_17 (.out(com1));
  PullDown #(.Bits(4)) pulldown_18 (.out(com1_inst));
  Multiplexer #(.Bits(32)) multiplexer_5 (.sel(CT_ISCSM), .in_0(multiplexer_2_out), .in_1(ISC_sc), .out(ISC_i));
  assign CT_ISCE = RX_ISCE ? 1'b1 : 1'bz;  // Driver driver_29
  Multiplexer #(.Bits(6)) multiplexer_6 (.sel(int_accept), .in_0(multiplexer_3_out), .in_1(INT_lev), .out(ILV_i));
  assign CT_ILVE = RX_ILVE ? 1'b1 : 1'bz;  // Driver driver_30
  assign RX_SEL = bitextender_2_out & multiplexer_4_out;  // And and_31, 32 bits wide
  assign CT_BUS__IAR = d_ff_11_q ? 1'b1 : 1'bz;  // Driver driver_31
  Multiplexer #(.Bits(32)) multiplexer_7 (.sel(RX_PVECM), .in_0(CT_RF__D1), .in_1(CT_RF__D2), .out(PVEC_i));
  assign CT_PVECE = RX_PVECE ? 1'b1 : 1'bz;  // Driver driver_32
  BitExtender #(.inputBits(1), .outputBits(32)) bitextender_2 (.in(nor_3_out), .out(bitextender_2_out));
  Multiplexer #(.Bits(4)) multiplexer_8 (.sel(com2), .in_0(com1_inst), .in_1(com2_inst), .out(multiplexer_8_out));
  ROB_SC rob_sc_1 (
    .C(C_dt), .E(CT_RF__SCSRE), .D(ISC_sc), .inst(inst_DP), .com1(com1), .com2(com2), .com1_id(com1_inst),
    .com2_id(com2_inst), .clr_16(clr_16), .roll(clr_id), .SCA(SCA), .W1(CT_SC__W1), .D1(CT_SC__D1),
    .W2(CT_SC__W2), .D2(CT_SC__D2), .D3(CT_SC__FD));
  BTB btb_1 (
    .C(C_dt), .E(JPU_BTB__ST), .V_in(1'b1), .id(JPU_PC[5:2]), .tag(JPU_PC[17:6]), .pred(JPU_pred),
    .tar(JPU_ADDR), .R_id(PCS[5:2]), .R_tag(PCS[17:6]), .V(BTB_packet[1]), .J(BTB_JP),
    .pred_O(BTB_packet[4:3]), .tar_O(BTB_packet[36:5]));
  or or_9 (or_9_out, MEM_AC, MEM_CLR);
  not not_8 (MEM_LD__REC, LDB_forward);
  inst_comp inst_comp_1 (.A_id(MEM_INST), .A_ep(MEM_EP), .B_id(clrs_id), .B_ep(clrs_ep), .A_new(inst_comp_1_a_new));
  inst_comp inst_comp_2 (
    .A_id(MEM_LD__INST), .A_ep(MEM_LD__EP), .B_id(clrs_id), .B_ep(clrs_ep), .A_new(inst_comp_2_a_new));
  Comparator #(.Bits(4)) comparator_19 (.a(TRAP_INST), .b(com1_inst), .eq(comparator_19_eq));  // open: gt, lt
  Register #(.Bits(4)) register_8 (.D(CT_FU__INST), .C(C_ct), .en(CT_TRAP__LD), .Q(TRAP_INST));
  Register register_9 (.D(CT_FU__EPOCH), .C(C_ct), .en(CT_TRAP__LD), .Q(TRAP_EP));
  D_FF d_ff_12 (.D(CT_INT), .C(C_ct), .Q(d_ff_12_q));  // open: nQ
  D_FF d_ff_13 (.D(CT_TRAP__LD), .C(C_ct), .Q(d_ff_13_q));  // open: nQ
  Register #(.Bits(8)) register_10 (.D(CT_INTID), .C(C_ct), .en(CT_TRAP__LD), .Q({register_10_q, TRAP_INT}));
  RS_FF rs_ff_5 (.S(CT_TRAP__LD), .C(C_ct), .R(FU_CLR[4]), .Q(TRAP_RD));  // open: nQ
  D_FF #(.Bits(2)) d_ff_14 (.D({LDB_M__V, STB_M__V}), .C(C_ct), .Q(d_ff_14_q));  // open: nQ
  and and_32 (and_32_out, ~MEM_LD, or_9_out);  // And
  and and_33 (and_33_out, com1, comparator_19_eq);
  ROB_gen rob_gen_1 (
    .D1_O(CT_RF__D1), .R1_O(CT_RF__R1), .W1_O(CT_RF__W1), .EX1_O(CT_RF__EX1), .D2_O(CT_RF__D2),
    .R2_O(CT_RF__R2), .W2_O(CT_RF__W2), .EX2_O(CT_RF__EX2), .DR_O(CT_RF__DR), .C(C_dt),
    .E1(CT_ROB__GEN__STA), .E2(CT_ROB__GEN__STB), .D1(ROB_GEN_DA), .D2(ROB_GEN_DB), .R1(ROB_GEN_WA),
    .R2(ROB_GEN_WB), .EX1(ROB_GEN_EX1), .EX2(ROB_GEN_EX2), .inst1(ROB_GEN_INSTA), .inst2(ROB_GEN_INSTB),
    .ep1(ROB_GEN_EPA), .ep2(ROB_GEN_EPB), .com1(com1), .com2(com2), .com1_id(com1_inst), .com2_id(com2_inst),
    .clr_16(clr_16), .ret_id(RET_INST));
  ROB_PC rob_pc_1 (
    .C(C_dt), .E(issue), .D(PCS_DC), .inst(inst_IS), .com_id(multiplexer_8_out), .read_id(inst_DP),
    .ret_id(RET_INST), .D1(pca_i), .D2(pc_read), .D3(pc_ret));
  DipSwitch dipswitch_14 (.out(BTB_packet[0]));
  or or_10 (or_10_out, multiplexer_12_out, MEM_BF__free);
  or or_11 (or_11_out, d_ff_14_q[0], d_ff_14_q[1], MEM_CLR);
  RS_FF rs_ff_6 (.S(MEM_LD), .C(C_ct), .R(and_32_out), .Q(rs_ff_6_q), .nQ(rs_ff_6_nq));
  and and_34 (MEM_CLR, inst_comp_1_a_new, ~MEM_TYPE__ST, clr);  // And
  and and_35 (MEM_LD__CLR, inst_comp_2_a_new, clr);
  inst_comp inst_comp_3 (.A_id(TRAP_INST), .A_ep(TRAP_EP), .B_id(clr_id), .B_ep(clr_ep), .A_new(inst_comp_3_a_new));
  and and_36 (TRAP_IRD, ~FU_CLR[4], d_ff_12_q, d_ff_13_q);  // And
  and and_37 (and_37_out, byte_D0[3], byte_D0[0]);
  and and_38 (and_38_out, byte_D0[2], byte_D0[0]);
  and and_39 (and_39_out, byte_D0_iv[3], byte_D0_iv[2], byte_D0[1], byte_D0_iv[0]);
  and and_40 (and_40_out, byte_D0_iv[4], byte_D0[3], byte_D0[2], byte_D0[1]);
  and and_41 (and_41_out, byte_D0[4], byte_D0_iv[3], byte_D0_iv[2], byte_D0[1], byte_D0[0]);
  and and_42 (and_42_out[7], byte_D0_iv[4], byte_D0[3], byte_D0[2]);
  and and_43 (and_43_out, byte_D0[4], byte_D0[2], byte_D0_iv[1]);
  and and_44 (and_44_out, byte_D0[4], byte_D0_iv[3], byte_D0_iv[2]);
  and and_45 (and_45_out, byte_D0_iv[4], byte_D0_iv[3], byte_D0_iv[2]);
  and and_46 (and_46_out, byte_D0_iv[4], byte_D0_iv[3]);
  and and_47 (and_47_out, byte_D0_iv[4], byte_D0[3], byte_D0_iv[2], byte_D0_iv[1]);
  and and_48 (and_48_out, byte_D0_iv[4], byte_D0[3], byte_D0_iv[2]);
  and and_49 (and_49_out, byte_D0[4], byte_D0[3]);
  and and_50 (and_50_out, byte_D0_iv[4], byte_D0_iv[3], byte_D0[2], byte_D0_iv[1]);
  and and_51 (and_51_out, byte_D0[4], byte_D0[2], byte_D0[1]);
  and and_52 (and_52_out, byte_D0_iv[4], byte_D0_iv[3], byte_D0_iv[2], byte_D0[1], byte_D0[0]);
  and and_53 (and_53_out, byte_D0_iv[2], byte_D0_iv[0]);
  and and_54 (and_54_out, byte_D0[2], byte_D0[0]);
  and and_55 (and_55_out, byte_D0[1], byte_D0[2], byte_D0[4]);
  and and_56 (and_56_out, byte_D0[3], byte_D0[4]);
  not not_9 (not_9_out, MEM_CLR);
  not not_10 (not_10_out, B_used);
  not not_11 (not_11_out, MEM_CLR);
  not not_12 (not_12_out, B_used);
  and and_57 (and_57_out, ~FU_CLR[4], ~d_ff_12_q, d_ff_13_q);  // And
  and and_58 (MEM_AC, or_10_out, D_accept, not_9_out, not_10_out);
  and and_59 (MEM_RD, not_11_out, not_12_out, rs_ff_6_q);
  or or_12 (or_12_out, rs_ff_6_nq, MEM_AC, MEM_CLR);
  and and_60 (and_60_out, rs_ff_7_q, and_33_out);
  or or_13 (or_13_out, and_57_out, FU_I__V[0]);
  and and_61 (TRAP_busy, TRAP_RD, ~TRAP_ST);  // And
  or or_14 (and_42_out[9], and_37_out, and_38_out, and_39_out);
  or or_15 (and_42_out[6], and_43_out, and_40_out, and_41_out);
  or or_16 (and_42_out[5], and_42_out[7], and_43_out, and_44_out);
  or or_17 (and_42_out[4], and_50_out, and_51_out, and_45_out);
  or or_18 (and_42_out[3], and_46_out, and_51_out, and_47_out);
  or or_19 (and_42_out[2], and_48_out, and_49_out);
  or or_20 (and_42_out[1], and_50_out, and_51_out, and_52_out);
  or or_21 (and_42_out[0], byte_D0[3], byte_D0[1], and_53_out, and_54_out);
  nor nor_4 (nor_4_out, and_55_out, and_56_out);
  ROB_FL rob_fl_1 (
    .C(C_dt), .E1(CT_ROB__FL__STA), .E2(CT_ROB__FL__STB), .D1(ROB_FL_A), .D2(ROB_FL_B), .inst1(ROB_FL_INSTA),
    .inst2(ROB_FL_INSTB), .com1(com1), .com2(com2), .com1_id(com1_inst), .com2_id(com2_inst),
    .clr_16(clr_16), .W1_O(CT_FL__W1), .D1_O(CT_FL__D1), .W2_O(CT_FL__W2), .D2_O(CT_FL__D2));
  or or_22 (or_22_out, clr_sel[0], CT_JMP);
  xor xor_2 (xor_2_out, STB_M__EP, LDB_M__EP);
  Comparator #(.Bits(4)) comparator_20 (
    .a(LDB_M__ID), .b(STB_M__ID), .gt(comparator_20_gt), .lt(comparator_20_lt));  // open: eq
  and and_62 (MEM_LD, or_11_out, or_12_out);
  Register #(.Bits(32)) register_11 (.D(pc_read), .C(C_dt), .en(CT_TRAP__LD), .Q(register_11_q));
  and and_63 (and_63_out, inst_comp_3_a_new, clr, ~CT_TRAP__LD);  // And
  and and_64 (and_64_out, and_60_out, ~CT_TRAP__LD);  // And
  nor nor_5 (nor_5_out[1], byte_D1[1], nor_5_out[2]);
  nor nor_6 (nor_5_out[2], byte_D1[0], byte_D1[1], byte_D1[2]);
  and and_65 (and_65_out, byte_D0_iv[7], byte_D0_iv[6], byte_D0[5]);
  and and_66 (and_66_out, byte_D0_iv[7], byte_D0[6], byte_D0_iv[5]);
  PriorityEncoder #(.Selector_Bits(2)) priorityencoder_1 (
    .in0(1'b1), .in1(or_22_out), .in2(CT_RF__PCH), .in3(1'b0), .num(priorityencoder_1_num));  // open: any
  and and_67 (and_67_out, STB_M__V, LDB_M__V);
  Multiplexer multiplexer_9 (
    .sel(xor_2_out), .in_0(comparator_20_gt), .in_1(comparator_20_lt), .out(multiplexer_9_out));
  and and_68 (and_68_out, MEM_AC, MEM_RD, not_13_out, not_14_out);
  not not_13 (not_13_out, MEM_TYPE__ST);
  not not_14 (not_14_out, MEM_CLR);
  or or_23 (or_23_out, MEM_LD__REC, MEM_LD__CLR);
  assign \wait  = and_60_out ? 1'b1 : 1'bz;  // Driver driver_33
  assign CT_RF__PCH = and_60_out ? 1'b1 : 1'bz;  // Driver driver_34
  or or_24 (or_24_out, and_63_out, and_64_out);
  not not_15 (TRAP_free, TRAP_busy);
  and and_69 (and_69_out, byte_D0_iv[0], byte_D0_iv[1], byte_D0[2], byte_D0[3], byte_D0[4], byte_D0_iv[5], byte_D0_iv[6], byte_D0_iv[7]);
  and and_70 (and_70_out, byte_D0[1], byte_D0_iv[2], byte_D0[3], byte_D0[4], byte_D0_iv[5], byte_D0_iv[6], byte_D0_iv[7]);
  and and_71 (and_71_out, byte_D0[1], byte_D0[2], byte_D0[3], byte_D0[4], byte_D0_iv[5], byte_D0_iv[6], byte_D0_iv[7]);
  or or_25 (or_25_out[1], byte_D1[1], byte_D1[2], byte_D1[0]);
  or or_26 (or_26_out, and_66_out, and_65_out);
  and and_72 (and_72_out, com1, CT_RF__W1, ~CT_RF__EX1);  // And
  and and_73 (and_73_out, com2, CT_RF__W2, ~CT_RF__EX2);  // And
  PullDown #(.Bits(16)) pulldown_19 (.out(INT_inst));
  PullDown #(.Bits(16)) pulldown_20 (.out(V1_inst));
  PullDown #(.Bits(16)) pulldown_21 (.out(V2_inst));
  PullDown pulldown_22 (.out(CT_RF__SCSRE));
  Multiplexer #(.Selector_Bits(2), .Bits(32)) multiplexer_10 (
    .sel(priorityencoder_1_num), .in_0(MEM_FPC), .in_1(JPU_ADDR), .in_2(HALT_PC), .in_3({32{1'b0}}),
    .out(multiplexer_10_out));
  and and_74 (and_74_out, clr_self, clr);
  Multiplexer #(.Bits(8)) multiplexer_11 (
    .sel(CT_BUS__IDM), .in_0(I_D__bus[31:24]), .in_1(8'h72), .out(multiplexer_11_out));
  Multiplexer multiplexer_12 (.sel(and_67_out), .in_0(STB_M__V), .in_1(multiplexer_9_out), .out(multiplexer_12_out));
  D_FF #(.Bits(32)) d_ff_15 (.D(register_11_q), .C(C_ct), .Q(HALT_PC));  // open: nQ
  RS_FF rs_ff_7 (.S(CT_TRAP__LD), .C(C_ct), .R(or_24_out), .Q(rs_ff_7_q));  // open: nQ
  and and_75 (FU_CLR[4], inst_comp_3_a_new, clr);
  bus16x2_demux bus16x2_demux_1 (.bus_1(V1_inst), .bus_2(V2_inst), .E(or_13_out), .id(TRAP_INST));
  bus16_demux bus16_demux_1 (.bus(INT_inst), .E(FU_I__V[0]), .id(TRAP_INST));
  and and_76 (and_76_out, byte_D0[4], byte_D0[3], byte_D0_iv[1], byte_D0_iv[2], byte_D0_iv[5], byte_D0_iv[6], byte_D0_iv[7]);
  or or_27 (or_27_out, and_69_out, and_70_out);
  not not_16 (not_16_out, multiplexer_12_out);
  Multiplexer #(.Bits(32)) multiplexer_13 (
    .sel(multiplexer_12_out), .in_0(LDB_M__A), .in_1(STB_M__A), .out(multiplexer_13_out));
  Multiplexer #(.Bits(2)) multiplexer_14 (
    .sel(multiplexer_12_out), .in_0(LDB_M__MD), .in_1(STB_M__MD), .out(multiplexer_14_out));
  and and_77 (and_77_out, or_23_out, ~and_68_out);  // And
  assign CT_RF__PCSE = and_60_out ? 1'b1 : 1'bz;  // Driver driver_35
  assign CT_RF__PCJ = and_60_out ? 1'b1 : 1'bz;  // Driver driver_36
  and and_78 (and_78_out, and_71_out, byte_D0[0]);
  and and_79 (and_79_out, byte_D0_iv[0], and_71_out);
  // regFile4 regfile4_1: pin names not known; wires that end beside it: C_dt, and_72_out, and_73_out, CT_RF__D1, CT_RF__D2, CT_RF__R1[7:3], CT_RF__R1[2:0], CT_RF__R2[7:3], CT_RF__R2[2:0], CT_RF__RA, CT_RF__MA, CT_RF__RB, CT_RF__MB, pcs_i, CT_RF__PCSE, pca_i, CT_RF__PCAE, ISC_sc, CT_RF__SCSS, CT_RF__SCSE, sca_i, CT_RF__SCAE, CT_RF__SCAE, {{23{1'b0}}, FL[14], fl_i}, CT_RF__FLS, 4'b0001, pc_read, R_A, R_B, PCS, PCA, SCS, SCA, FL
  PriorityEncoder #(.Selector_Bits(2)) priorityencoder_2 (
    .in0(1'b1), .in1(BTB_JP), .in2(CT_RF__PCJ), .in3(boot_t), .num(priorityencoder_2_num));  // open: any
  or or_28 (or_28_out, boot_t, and_74_out, or_22_out, BTB_JP);
  Register #(.Bits(37)) BTB_F (
    .D({BTB_packet[36:3], BTB_JP, BTB_packet[1:0]}), .C(C_dt), .en(CT_BUS__IAR), .Q(BTB_fetch));
  Register #(.Bits(32)) I_A__R (.D(PCS), .C(C_dt), .en(CT_BUS__IAR), .Q(I_A__R_q));
  Register #(.Bits(32)) I_D__R (.D({multiplexer_11_out, I_D__bus[23:0]}), .C(C_dt), .en(dc_e), .Q(I_D__R_q));
  Register #(.Bits(37)) BTB_D (.D(BTB_fetch), .C(C_dt), .en(dc_e), .Q(BTB_D_q));
  and and_80 (MB_LDB__LD, LDB_M__V, MEM_LD, not_16_out);
  and and_81 (MB_STB__LD, multiplexer_12_out, MEM_LD);
  Register register_12 (.D(multiplexer_12_out), .C(C_dt), .en(MEM_LD), .Q(MEM_TYPE__ST));
  Register register_13 (.D(LDB_M__EP), .C(C_dt), .en(MEM_LD), .Q(MEM_EP));
  Register #(.Bits(4)) register_14 (.D(LDB_M__ID), .C(C_dt), .en(MEM_LD), .Q(MEM_INST));
  Register #(.Bits(32)) register_15 (.D(multiplexer_13_out), .C(C_dt), .en(MEM_LD), .Q(register_15_q));
  Register #(.Bits(2)) register_16 (.D(multiplexer_14_out), .C(C_dt), .en(MEM_LD), .Q(register_16_q));
  Register #(.Bits(32)) register_17 (.D(STB_M__D), .C(C_dt), .en(MEM_LD), .Q(register_17_q));
  not not_17 (not_17_out, MEM_LD__CLR);
  RS_FF rs_ff_8 (.S(and_68_out), .C(C_dt), .R(and_77_out), .Q(rs_ff_8_q), .nQ(rs_ff_8_nq));
  Register #(.Bits(32)) register_18 (.D(D_D__bus), .C(C_dt), .en(MEM_AC), .Q(MEM_LD__D));
  Register #(.Bits(4)) register_19 (.D(MEM_INST), .C(C_dt), .en(MEM_AC), .Q(MEM_LD__INST));
  Register register_20 (.D(MEM_EP), .C(C_dt), .en(MEM_AC), .Q(MEM_LD__EP));
  and and_82 (and_82_out, byte_D0_iv[7], byte_D0_iv[6], byte_D0_iv[5], byte_D0_iv[4]);
  and and_83 (and_83_out, byte_D0_iv[7], byte_D0_iv[6], byte_D0_iv[5], byte_D0[4], byte_D0_iv[3]);
  assign {CT_RF__RA, CT_RF__MA} = or_31_out ? byte_D1 : 8'bz;  // Driver driver_37
  assign {CT_RF__RB, CT_RF__MB} = or_31_out ? byte_D2 : 8'bz;  // Driver driver_38
  assign CT_ALU__LD = or_31_out ? CT_DISP : 1'bz;  // Driver driver_39
  assign CT_ALU__CT = or_31_out ? {1'b0, and_42_out[7:0]} : 9'bz;  // Driver driver_40
  assign CT_ALU__M = or_31_out ? and_42_out[9] : 1'bz;  // Driver driver_41
  assign CT_FU__INST = or_31_out ? inst_DP : 4'bz;  // Driver driver_42
  assign CT_FU__EPOCH = or_31_out ? epoch_DP : 1'bz;  // Driver driver_43
  assign CT_FU__WR = or_31_out ? byte_D1 : 8'bz;  // Driver driver_44
  assign CT_ALU__WD = or_31_out ? nor_4_out : 1'bz;  // Driver driver_45
  assign CT_ALU__WF = or_31_out ? 1'b1 : 1'bz;  // Driver driver_46
  assign {CT_RF__RA, CT_RF__MA} = or_27_out ? byte_D2 : 8'bz;  // Driver driver_47
  assign CT_DIR__LD = or_27_out ? CT_DISP : 1'bz;  // Driver driver_48
  assign CT_DIR__M = or_27_out ? and_70_out : 1'bz;  // Driver driver_49
  assign CT_DIR__MS = or_27_out ? byte_D0[0] : 1'bz;  // Driver driver_50
  assign CT_FU__INST = or_27_out ? inst_DP : 4'bz;  // Driver driver_51
  assign CT_FU__EPOCH = or_27_out ? epoch_DP : 1'bz;  // Driver driver_52
  assign CT_FU__WR = or_27_out ? byte_D1 : 8'bz;  // Driver driver_53
  assign CT_RF__SCSS = and_71_out ? 1'b1 : 1'bz;  // Driver driver_54
  assign {CT_RF__RB, CT_RF__MB} = and_71_out ? 8'hf0 : 8'bz;  // Driver driver_55
  assign {CT_RF__RA, CT_RF__MA} = and_78_out ? byte_D1 : 8'bz;  // Driver driver_56
  assign CT_FU__WR = and_79_out ? byte_D1 : 8'bz;  // Driver driver_57
  assign CT_MB__LD = and_71_out ? CT_DISP : 1'bz;  // Driver driver_58
  assign CT_MB__ST = and_78_out ? 1'b1 : 1'bz;  // Driver driver_59
  assign CT_SP__MOF = and_78_out ? {1'b1, or_25_out[1], byte_D1[1]} : 3'bz;  // Driver driver_60
  assign CT_MB__OFFM = and_71_out ? 1'b1 : 1'bz;  // Driver driver_61
  assign CT_RF__SCSE = and_71_out ? 1'b1 : 1'bz;  // Driver driver_62
  assign CT_RF__SCN = and_71_out ? {nor_5_out, byte_D1[1]} : 3'bz;  // Driver driver_63
  assign CT_RF__SCD = and_78_out ? 1'b1 : 1'bz;  // Driver driver_64
  assign CT_FU__INST = and_71_out ? inst_DP : 4'bz;  // Driver driver_65
  assign CT_FU__EPOCH = and_71_out ? epoch_DP : 1'bz;  // Driver driver_66
  assign CT_RF__SCSRE = and_71_out ? 1'b1 : 1'bz;  // Driver driver_67
  assign CT_FU__EPOCH = or_26_out ? epoch_DP : 1'bz;  // Driver driver_68
  assign CT_FU__INST = or_26_out ? inst_DP : 4'bz;  // Driver driver_69
  assign {CT_RF__RB, CT_RF__MB} = or_26_out ? {byte_D0[4:0], 3'b000} : 8'bz;  // Driver driver_70
  assign {CT_RF__RA, CT_RF__MA} = and_66_out ? byte_D1 : 8'bz;  // Driver driver_71
  assign CT_FU__WR = and_65_out ? byte_D1 : 8'bz;  // Driver driver_72
  assign CT_MB__LD = or_26_out ? CT_DISP : 1'bz;  // Driver driver_73
  assign CT_MB__ST = and_66_out ? 1'b1 : 1'bz;  // Driver driver_74
  or or_29 (CT_RF__PCAE, com1, com2);
  ROB_INT rob_int_1 (
    .C(C_dt), .E1(CT_ROB__INT__STA), .E2(CT_ROB__INT__STB), .D1(ROB_INT_A), .D2(ROB_INT_B),
    .inst1(ROB_INT_INSTA), .inst2(ROB_INT_INSTB), .com1(com1), .com2(com2), .com1_id(com1_inst),
    .com2_id(com2_inst), .clr_16(clr_16), .W_O(CT_INT__W), .D_O(CT_INT__D));
  Multiplexer #(.Selector_Bits(2), .Bits(32)) multiplexer_15 (
    .sel(priorityencoder_2_num), .in_0(PCS), .in_1(BTB_packet[36:5]), .in_2(multiplexer_10_out),
    .in_3(32'hffffff00), .out(multiplexer_15_out));
  assign I_A__bus = CT_BUS__IAG ? I_A__R_q : 32'bz;  // Driver driver_75
  D_FF #(.Bits(32)) d_ff_16 (.D(I_D__R_q), .C(C_ct), .Q({byte_I0, byte_I1, byte_I2, byte_I3}));  // open: nQ
  D_FF #(.Bits(37)) d_ff_17 (.D(BTB_D_q), .C(C_ct), .Q(BTB_pack__iss));  // open: nQ
  assign D_A__bus = MEM_RD ? register_15_q : 32'bz;  // Driver driver_76
  assign D_MD = MEM_RD ? register_16_q : 2'bz;  // Driver driver_77
  assign D_D__bus = D_ST ? register_17_q : 32'bz;  // Driver driver_78
  and and_84 (MEM_LD__RD, not_17_out, rs_ff_8_q);
  or or_30 (MEM_BF__free, rs_ff_8_nq, MEM_LD__RD, MEM_LD__CLR);
  Multiplexer #(.Bits(32)) multiplexer_16 (
    .sel(or_28_out), .in_0(add_4c32_1_s), .in_1(multiplexer_15_out), .out(pcs_i));
  add_4c32 add_4c32_1 (.a(multiplexer_15_out), .b(4'b0100), .s(add_4c32_1_s));  // open: c
  and and_85 (D_LD, ~MEM_TYPE__ST, MEM_RD);  // And
  and and_86 (D_ST, MEM_RD, MEM_TYPE__ST);
  RS_FF u_HLT (.S(run_t), .C(C_ct), .R(hlt), .nQ(halted));  // open: Q
  Register register_21 (.D(CT_KILL), .C(C_ct), .en(CT_TRAP__LD), .Q(hlt));
  PullDown pulldown_23 (.out(CT_INT));
  PullDown #(.Bits(8)) pulldown_24 (.out(CT_INTID));
  or or_31 (or_31_out, and_82_out, and_76_out, and_83_out);
  BitExtender #(.inputBits(1), .outputBits(8)) bitextender_3 (.in(byte_D0[3]), .out(bitextender_3_out));
  assign xor_3_out = FL[7:0] ^ bitextender_3_out;  // XOr xor_3, 8 bits wide
  and and_87 (and_87_out, com1, CT_SC__W1);
  and and_88 (and_88_out, com2, CT_SC__W2);
  and and_89 (and_89_out, byte_D2[7], CT_DIR__MS);
  BitExtender #(.inputBits(1)) bitextender_4 (.in(and_89_out), .out(bitextender_4_out));
  Multiplexer #(.Bits(3)) multiplexer_17 (
    .sel(CT_MB__ST), .in_0(CT_FU__WR[2:0]), .in_1(CT_RF__MA), .out(multiplexer_17_out));
  and and_90 (and_90_out, byte_D0[1], byte_D0_iv[2], byte_D0[3], byte_D0[4], byte_D0[5], byte_D0[6], byte_D0_iv[7]);
  assign CT_RF__SCSE = clr ? 1'b1 : 1'bz;  // Driver driver_79
  assign CT_RF__SCSS = clr ? 1'b1 : 1'bz;  // Driver driver_80
  Multiplexer multiplexer_18 (.sel(and_102_out[2]), .in_0(nand_1_out[2]), .in_1(1'b1), .out(multiplexer_18_out));
  not not_18 (not_18_out[0], register_22_q[0]);
  xor xor_4 (not_18_out[1], register_22_q[0], register_22_q[1]);
  xor xor_5 (not_18_out[2], register_22_q[1], register_22_q[2]);
  Multiplexer #(.Bits(32)) multiplexer_19 (
    .sel(CT_ALU__M), .in_0(R_B), .in_1({{16{1'b0}}, byte_D2, byte_D3}), .out(multiplexer_19_out));
  PullDown #(.Bits(8)) pulldown_25 (.out(CT_DIR__EXID));
  PullDown pulldown_26 (.out(CT_DIR__EXM));
  PullDown pulldown_27 (.out(CT_FU__EX));
  and and_91 (and_91_out, byte_D0_iv[4], byte_D0[5], byte_D0[6], byte_D0_iv[7]);
  Multiplexer #(.Selector_Bits(3)) multiplexer_20 (
    .sel(byte_D0[2:0]), .in_0(xor_3_out[0]), .in_1(xor_3_out[1]), .in_2(xor_3_out[2]), .in_3(xor_3_out[3]),
    .in_4(xor_3_out[4]), .in_5(xor_3_out[5]), .in_6(xor_3_out[6]), .in_7(xor_3_out[7]),
    .out(multiplexer_20_out));
  or or_32 (CT_RF__SCAE, and_87_out, and_88_out);
  and and_92 (and_92_out, multiplexer_18_out, CT_ALU__LD);
  Register register_22 (.D(and_92_out), .C(C_ct), .en(or_33_out), .Q(register_22_q[2]));
  not not_19 (not_19_out, multiplexer_18_out);
  or or_33 (or_33_out, not_19_out, multiplexer_21_out[2]);
  Multiplexer #(.Bits(3)) multiplexer_21 (
    .sel(or_34_out), .in_0(not_18_out), .in_1(and_102_out), .out(multiplexer_21_out));
  or or_34 (or_34_out, and_102_out[0], and_102_out[1], and_102_out[2]);
  Register #(.Bits(4)) register_23 (.D(CT_FU__INST), .C(C_ct), .en(multiplexer_21_out[2]), .Q(register_23_q));
  Register register_24 (.D(CT_FU__EPOCH), .C(C_ct), .en(multiplexer_21_out[2]), .Q(register_24_q));
  Register register_25 (.D(CT_ALU__WD), .C(C_ct), .en(multiplexer_21_out[2]), .Q(register_25_q));
  Register register_26 (.D(CT_ALU__WF), .C(C_ct), .en(multiplexer_21_out[2]), .Q(register_26_q));
  Register #(.Bits(32)) register_27 (.D(R_A), .C(C_dt), .en(multiplexer_21_out[2]), .Q(register_27_q));
  Register #(.Bits(32)) register_28 (.D(multiplexer_19_out), .C(C_dt), .en(multiplexer_21_out[2]), .Q(register_28_q));
  Register #(.Bits(8)) register_29 (.D(FL[7:0]), .C(C_dt), .en(multiplexer_21_out[2]), .Q(register_29_q));
  Register #(.Bits(9)) register_30 (.D(CT_ALU__CT), .C(C_ct), .en(multiplexer_21_out[2]), .Q(register_30_q));
  Register #(.Bits(8)) register_31 (.D(CT_FU__WR), .C(C_ct), .en(multiplexer_21_out[2]), .Q(register_31_q));
  Multiplexer #(.Bits(32)) multiplexer_22 (
    .sel(CT_DIR__M), .in_0(R_A), .in_1({bitextender_4_out, byte_D2, byte_D3}), .out(multiplexer_22_out));
  or or_35 (or_35_out, multiplexer_17_out[0], multiplexer_17_out[2]);
  not not_20 (not_20_out, multiplexer_17_out[1]);
  and and_93 (and_93_out, byte_D0_iv[0], byte_D0_iv[1], byte_D0_iv[2], byte_D0_iv[3], byte_D0[4], byte_D0[5], byte_D0[6], byte_D0_iv[7]);
  and and_94 (and_94_out, byte_D0[0], byte_D0_iv[1], byte_D0_iv[2], byte_D0_iv[3], byte_D0[4], byte_D0[5], byte_D0[6], byte_D0_iv[7]);
  and and_95 (and_95_out, byte_D0_iv[1], byte_D0[2], byte_D0_iv[3], byte_D0[4], byte_D0[5], byte_D0[6], byte_D0_iv[7]);
  and and_96 (and_96_out, byte_D0[0], byte_D0_iv[1], byte_D0[2], byte_D0[3], byte_D0[4], byte_D0_iv[5], byte_D0_iv[6], byte_D0_iv[7]);
  and and_97 (and_97_out, byte_D0[0], and_90_out);
  and and_98 (and_98_out, and_90_out, byte_D0_iv[0]);
  Multiplexer multiplexer_23 (
    .sel(and_102_out[1]), .in_0(nand_1_out[1]), .in_1(nand_1_out[2]), .out(multiplexer_23_out));
  Multiplexer multiplexer_24 (
    .sel(register_22_q[2]), .in_0(CT_ALU__LD), .in_1(register_22_q[2]), .out(multiplexer_24_out));
  Multiplexer #(.Bits(4)) multiplexer_25 (
    .sel(register_22_q[2]), .in_0(CT_FU__INST), .in_1(register_23_q), .out(multiplexer_25_out));
  inst_comp inst_comp_4 (
    .A_id(register_23_q), .A_ep(register_24_q), .B_id(clr_id), .B_ep(clr_ep), .A_new(inst_comp_4_a_new));
  Multiplexer multiplexer_26 (
    .sel(register_22_q[2]), .in_0(CT_FU__EPOCH), .in_1(register_24_q), .out(multiplexer_26_out));
  Multiplexer multiplexer_27 (
    .sel(register_22_q[2]), .in_0(CT_ALU__WD), .in_1(register_25_q), .out(multiplexer_27_out));
  Multiplexer multiplexer_28 (
    .sel(register_22_q[2]), .in_0(CT_ALU__WF), .in_1(register_26_q), .out(multiplexer_28_out));
  Multiplexer #(.Bits(32)) multiplexer_29 (
    .sel(register_22_q[2]), .in_0(R_A), .in_1(register_27_q), .out(multiplexer_29_out));
  Multiplexer #(.Bits(32)) multiplexer_30 (
    .sel(register_22_q[2]), .in_0(multiplexer_19_out), .in_1(register_28_q), .out(multiplexer_30_out));
  Multiplexer #(.Bits(8)) multiplexer_31 (
    .sel(register_22_q[2]), .in_0(FL[7:0]), .in_1(register_29_q), .out(multiplexer_31_out));
  Multiplexer #(.Bits(9)) multiplexer_32 (
    .sel(register_22_q[2]), .in_0(CT_ALU__CT), .in_1(register_30_q), .out(multiplexer_32_out));
  Multiplexer #(.Bits(8)) multiplexer_33 (
    .sel(register_22_q[2]), .in_0(CT_FU__WR), .in_1(register_31_q), .out(multiplexer_33_out));
  Multiplexer multiplexer_34 (.sel(and_106_out[2]), .in_0(nand_4_out[2]), .in_1(1'b1), .out(multiplexer_34_out));
  not not_21 (not_21_out[0], register_47_q[0]);
  xor xor_6 (not_21_out[1], register_47_q[0], register_47_q[1]);
  xor xor_7 (not_21_out[2], register_47_q[1], register_47_q[2]);
  Multiplexer #(.Bits(32)) multiplexer_35 (
    .sel(CT_DIR__EXM), .in_0(multiplexer_22_out), .in_1(RX_SEL), .out(multiplexer_35_out));
  Multiplexer #(.Bits(32)) multiplexer_36 (.sel(CT_INTM), .in_0(R_A), .in_1(int_pc), .out(multiplexer_36_out));
  add_4c32 add_4c32_2 (.a(pc_read), .b(4'b0100), .s(add_4c32_2_s));  // open: c
  BitExtender #(.inputBits(3)) bitextender_5 (.in(CT_SP__MOF), .out(bitextender_5_out));
  and and_99 (and_99_out[0], or_35_out, not_20_out);
  and and_100 (and_100_out, multiplexer_23_out, multiplexer_24_out);
  not not_22 (not_22_out, multiplexer_23_out);
  or or_36 (or_36_out, not_22_out, multiplexer_21_out[1]);
  or or_37 (register_22_q[1], register_46_q[1], register_22_q[2]);
  nand nand_1 (nand_1_out[2], inst_comp_4_a_new, register_22_q[2], clr);
  Register #(.Bits(4)) register_32 (.D(multiplexer_25_out), .C(C_ct), .en(multiplexer_21_out[1]), .Q(register_32_q));
  Register register_33 (.D(multiplexer_26_out), .C(C_ct), .en(multiplexer_21_out[1]), .Q(register_33_q));
  Register register_34 (.D(multiplexer_27_out), .C(C_ct), .en(multiplexer_21_out[1]), .Q(register_34_q));
  Register register_35 (.D(multiplexer_28_out), .C(C_ct), .en(multiplexer_21_out[1]), .Q(register_35_q));
  Register #(.Bits(32)) register_36 (.D(multiplexer_29_out), .C(C_dt), .en(multiplexer_21_out[1]), .Q(register_36_q));
  Register #(.Bits(32)) register_37 (.D(multiplexer_30_out), .C(C_dt), .en(multiplexer_21_out[1]), .Q(register_37_q));
  Register #(.Bits(8)) register_38 (.D(multiplexer_31_out), .C(C_dt), .en(multiplexer_21_out[1]), .Q(register_38_q));
  Register #(.Bits(9)) register_39 (.D(multiplexer_32_out), .C(C_ct), .en(multiplexer_21_out[1]), .Q(register_39_q));
  Register #(.Bits(8)) register_40 (.D(multiplexer_33_out), .C(C_ct), .en(multiplexer_21_out[1]), .Q(register_40_q));
  and and_101 (and_101_out, multiplexer_34_out, CT_DIR__LD);
  not not_23 (not_23_out, multiplexer_34_out);
  Register #(.Bits(4)) register_41 (.D(CT_FU__INST), .C(C_ct), .en(multiplexer_50_out[2]), .Q(register_41_q));
  Register register_42 (.D(CT_FU__EPOCH), .C(C_ct), .en(multiplexer_50_out[2]), .Q(register_42_q));
  Register #(.Bits(32)) register_43 (.D(multiplexer_35_out), .C(C_dt), .en(multiplexer_50_out[2]), .Q(register_43_q));
  Register #(.Bits(8)) register_44 (.D(CT_FU__WR), .C(C_ct), .en(multiplexer_50_out[2]), .Q(register_44_q));
  Register register_45 (.D(CT_FU__EX), .C(C_ct), .en(multiplexer_50_out[2]), .Q(register_45_q));
  Multiplexer #(.Bits(32)) multiplexer_37 (
    .sel(CT_CALLM), .in_0(multiplexer_36_out), .in_1(add_4c32_2_s), .out(multiplexer_37_out));
  Multiplexer #(.Bits(32)) multiplexer_38 (.sel(CT_INTM), .in_0(R_B), .in_1(ISC), .out(multiplexer_38_out));
  Multiplexer #(.Bits(16)) multiplexer_39 (
    .sel(CT_MB__OFFM), .in_0({byte_D2, byte_D3}), .in_1(bitextender_5_out), .out(multiplexer_39_out));
  assign CT_FU__EPOCH = and_91_out ? epoch_DP : 1'bz;  // Driver driver_81
  assign CT_FU__INST = and_91_out ? inst_DP : 4'bz;  // Driver driver_82
  assign {CT_RF__RA, CT_RF__MA} = and_91_out ? byte_D1 : 8'bz;  // Driver driver_83
  assign CT_JPU__LD = and_91_out ? CT_DISP : 1'bz;  // Driver driver_84
  assign CT_JPU__JP = and_91_out ? multiplexer_20_out : 1'bz;  // Driver driver_85
  assign JPU_A__ST = and_91_out ? 1'b1 : 1'bz;  // Driver driver_86
  assign CT_FU__EPOCH = and_93_out ? epoch_DP : 1'bz;  // Driver driver_87
  assign CT_FU__INST = and_93_out ? inst_DP : 4'bz;  // Driver driver_88
  assign {CT_RF__RA, CT_RF__MA} = and_93_out ? byte_D1 : 8'bz;  // Driver driver_89
  assign {CT_RF__RB, CT_RF__MB} = and_93_out ? 8'hf0 : 8'bz;  // Driver driver_90
  assign CT_JPU__LD = and_93_out ? 1'b1 : 1'bz;  // Driver driver_91
  assign CT_JPU__JP = and_93_out ? CT_DISP : 1'bz;  // Driver driver_92
  assign JPU_A__ST = and_93_out ? 1'b1 : 1'bz;  // Driver driver_93
  assign CT_MB__LD = and_93_out ? 1'b1 : 1'bz;  // Driver driver_94
  assign CT_MB__ST = and_93_out ? 1'b1 : 1'bz;  // Driver driver_95
  assign CT_CALLM = and_93_out ? 1'b1 : 1'bz;  // Driver driver_96
  assign CT_SP__MOF = and_93_out ? 3'b100 : 3'bz;  // Driver driver_97
  assign CT_MB__OFFM = and_93_out ? 1'b1 : 1'bz;  // Driver driver_98
  assign CT_RF__SCSE = and_93_out ? 1'b1 : 1'bz;  // Driver driver_99
  assign CT_RF__SCSS = and_93_out ? 1'b1 : 1'bz;  // Driver driver_100
  assign CT_RF__SCD = and_93_out ? 1'b1 : 1'bz;  // Driver driver_101
  assign CT_RF__SCN = and_93_out ? 3'b100 : 3'bz;  // Driver driver_102
  assign CT_FU__MF = and_93_out ? 1'b1 : 1'bz;  // Driver driver_103
  assign JPU_CALL = and_93_out ? 1'b1 : 1'bz;  // Driver driver_104
  assign CT_RF__SCSRE = and_93_out ? 1'b1 : 1'bz;  // Driver driver_105
  assign CT_FU__EPOCH = and_94_out ? epoch_DP : 1'bz;  // Driver driver_106
  assign CT_FU__INST = and_94_out ? inst_DP : 4'bz;  // Driver driver_107
  assign {CT_RF__RB, CT_RF__MB} = and_94_out ? 8'hf0 : 8'bz;  // Driver driver_108
  assign CT_FU__WR = and_94_out ? 8'he8 : 8'bz;  // Driver driver_109
  assign CT_MB__LD = and_94_out ? 1'b1 : 1'bz;  // Driver driver_110
  assign CT_MB__OFFM = and_94_out ? 1'b1 : 1'bz;  // Driver driver_111
  assign CT_RF__SCSE = and_94_out ? 1'b1 : 1'bz;  // Driver driver_112
  assign CT_RF__SCSS = and_94_out ? 1'b1 : 1'bz;  // Driver driver_113
  assign CT_RF__SCN = and_94_out ? 3'b100 : 3'bz;  // Driver driver_114
  assign CT_FU__MF = and_94_out ? 1'b1 : 1'bz;  // Driver driver_115
  assign CT_RET__LD = and_94_out ? 1'b1 : 1'bz;  // Driver driver_116
  assign CT_RF__SCSRE = and_94_out ? 1'b1 : 1'bz;  // Driver driver_117
  assign CT_KILL = and_95_out ? byte_D0[0] : 1'bz;  // Driver driver_118
  assign CT_FU__EPOCH = and_95_out ? epoch_DP : 1'bz;  // Driver driver_119
  assign CT_FU__INST = and_95_out ? inst_DP : 4'bz;  // Driver driver_120
  assign CT_TRAP__LD = and_95_out ? 1'b1 : 1'bz;  // Driver driver_121
  bus16x2_demux bus16x2_demux_2 (.bus_1(V1_inst), .bus_2(V2_inst), .E(and_96_out), .id(inst_DP));
  assign CT_FU__WR = and_97_out ? byte_D3 : 8'bz;  // Driver driver_122
  assign {CT_RF__RA, CT_RF__MA} = and_97_out ? byte_D1 : 8'bz;  // Driver driver_123
  assign CT_DIR__LD = and_90_out ? CT_DISP : 1'bz;  // Driver driver_124
  assign CT_FU__INST = and_90_out ? inst_DP : 4'bz;  // Driver driver_125
  assign CT_FU__EPOCH = and_90_out ? epoch_DP : 1'bz;  // Driver driver_126
  assign CT_FU__WR = and_98_out ? byte_D1 : 8'bz;  // Driver driver_127
  assign CT_DIR__EXID = and_98_out ? byte_D3 : 8'bz;  // Driver driver_128
  assign CT_DIR__EXM = and_90_out ? 1'b1 : 1'bz;  // Driver driver_129
  assign CT_FU__EX = and_90_out ? 1'b1 : 1'bz;  // Driver driver_130
  Multiplexer #(.Bits(32)) multiplexer_40 (.sel(CT_ISCCM), .in_0(SCS), .in_1(ISC), .out(multiplexer_40_out));
  Register register_46 (.D(and_100_out), .C(C_ct), .en(or_36_out), .Q(register_46_q[1]));
  or or_38 (register_22_q[0], ALU_busy, register_46_q[1], register_22_q[2]);
  assign and_102_out = nand_2_out & register_22_q;  // And and_102, 3 bits wide
  Multiplexer #(.Bits(4)) multiplexer_41 (
    .sel(register_22_q[1]), .in_0(CT_FU__INST), .in_1(register_32_q), .out(multiplexer_41_out));
  inst_comp inst_comp_5 (
    .A_id(register_32_q), .A_ep(register_33_q), .B_id(clr_id), .B_ep(clr_ep), .A_new(inst_comp_5_a_new));
  Multiplexer multiplexer_42 (
    .sel(register_22_q[1]), .in_0(CT_FU__EPOCH), .in_1(register_33_q), .out(multiplexer_42_out));
  Multiplexer multiplexer_43 (
    .sel(register_22_q[1]), .in_0(CT_ALU__WD), .in_1(register_34_q), .out(multiplexer_43_out));
  Multiplexer multiplexer_44 (
    .sel(register_22_q[1]), .in_0(CT_ALU__WF), .in_1(register_35_q), .out(multiplexer_44_out));
  Multiplexer #(.Bits(32)) multiplexer_45 (
    .sel(register_22_q[1]), .in_0(R_A), .in_1(register_36_q), .out(multiplexer_45_out));
  Multiplexer #(.Bits(32)) multiplexer_46 (
    .sel(register_22_q[1]), .in_0(multiplexer_19_out), .in_1(register_37_q), .out(multiplexer_46_out));
  Multiplexer #(.Bits(8)) multiplexer_47 (
    .sel(register_22_q[1]), .in_0(FL[7:0]), .in_1(register_38_q), .out(multiplexer_47_out));
  Multiplexer #(.Bits(9)) multiplexer_48 (
    .sel(register_22_q[1]), .in_0(CT_ALU__CT), .in_1(register_39_q), .out(multiplexer_48_out));
  Multiplexer #(.Bits(8)) multiplexer_49 (
    .sel(register_22_q[1]), .in_0(CT_FU__WR), .in_1(register_40_q), .out(multiplexer_49_out));
  Register register_47 (.D(and_101_out), .C(C_ct), .en(or_39_out), .Q(register_47_q[2]));
  or or_39 (or_39_out, not_23_out, multiplexer_50_out[2]);
  Multiplexer #(.Bits(3)) multiplexer_50 (
    .sel(or_40_out), .in_0(not_21_out), .in_1(and_106_out), .out(multiplexer_50_out));
  or or_40 (or_40_out, and_106_out[0], and_106_out[1], and_106_out[2]);
  Multiplexer #(.Bits(4)) multiplexer_51 (
    .sel(register_47_q[2]), .in_0(CT_FU__INST), .in_1(register_41_q), .out(multiplexer_51_out));
  inst_comp inst_comp_6 (
    .A_id(register_41_q), .A_ep(register_42_q), .B_id(clr_id), .B_ep(clr_ep), .A_new(inst_comp_6_a_new));
  Multiplexer multiplexer_52 (
    .sel(register_47_q[2]), .in_0(CT_FU__EPOCH), .in_1(register_42_q), .out(multiplexer_52_out));
  Multiplexer #(.Bits(32)) multiplexer_53 (
    .sel(register_47_q[2]), .in_0(multiplexer_35_out), .in_1(register_43_q), .out(multiplexer_53_out));
  Multiplexer #(.Bits(8)) multiplexer_54 (
    .sel(register_47_q[2]), .in_0(CT_FU__WR), .in_1(register_44_q), .out(multiplexer_54_out));
  Multiplexer multiplexer_55 (.sel(register_47_q[2]), .in_0(CT_FU__EX), .in_1(register_45_q), .out(multiplexer_55_out));
  and and_103 (MB_LD, MB_free, CT_MB__LD);
  Register register_48 (.D(CT_MB__LD), .C(C_ct), .en(1'b1), .Q(register_48_q));
  Register #(.Bits(4)) register_49 (.D(CT_FU__INST), .C(C_ct), .en(MB_LD), .Q(MB_INST));
  Register register_50 (.D(CT_FU__EPOCH), .C(C_ct), .en(MB_LD), .Q(MB_ep));
  Register register_51 (.D(CT_MB__ST), .C(C_ct), .en(MB_LD), .Q(MB_type__st));
  Register #(.Bits(32)) register_52 (.D(multiplexer_37_out), .C(C_dt), .en(MB_LD), .Q(MB_data));
  Register #(.Bits(32)) register_53 (.D(multiplexer_38_out), .C(C_dt), .en(MB_LD), .Q(register_53_q));
  Register #(.Bits(16)) register_54 (.D(multiplexer_39_out), .C(C_dt), .en(MB_LD), .Q(register_54_q));
  Register #(.Bits(2)) register_55 (.D({multiplexer_17_out[1], and_99_out[0]}), .C(C_ct), .en(MB_LD), .Q(MB_MD));
  Register #(.Bits(8)) register_56 (.D(CT_FU__WR), .C(C_ct), .en(MB_LD), .Q(MB_WR));
  Register register_57 (.D(CT_FU__MF), .C(C_ct), .en(MB_LD), .Q(MB_MF));
  Register #(.Bits(32)) register_58 (.D(pc_read), .C(C_dt), .en(MB_LD), .Q(MB_PC));
  Multiplexer multiplexer_56 (
    .sel(and_102_out[0]), .in_0(nand_1_out[0]), .in_1(nand_1_out[1]), .out(multiplexer_56_out));
  Multiplexer multiplexer_57 (
    .sel(register_22_q[1]), .in_0(CT_ALU__LD), .in_1(register_46_q[1]), .out(multiplexer_57_out));
  and and_104 (and_104_out, multiplexer_56_out, multiplexer_57_out);
  nand nand_2 (nand_2_out[2], ALU_busy, register_46_q[1], register_22_q[2]);
  nand nand_3 (nand_1_out[1], inst_comp_5_a_new, register_46_q[1], clr);
  Register #(.Bits(4)) register_59 (.D(multiplexer_41_out), .C(C_ct), .en(ALU_A_LD), .Q(ALU_A_INST));
  Register register_60 (.D(multiplexer_42_out), .C(C_ct), .en(ALU_A_LD), .Q(ALU_A_EP));
  Register #(.Bits(32)) register_61 (.D(multiplexer_45_out), .C(C_dt), .en(ALU_A_LD), .Q(ALU_A_A));
  Register #(.Bits(32)) register_62 (.D(multiplexer_46_out), .C(C_dt), .en(ALU_A_LD), .Q(ALU_A_B));
  Register #(.Bits(8)) register_63 (.D(multiplexer_47_out), .C(C_dt), .en(ALU_A_LD), .Q(ALU_A_FI));
  Register #(.Bits(9)) register_64 (.D(multiplexer_48_out), .C(C_ct), .en(ALU_A_LD), .Q(ALU_A_CT));
  Register #(.Bits(8)) register_65 (.D(multiplexer_49_out), .C(C_ct), .en(ALU_A_LD), .Q({ALU_A_WR, ALU_A_RM}));
  Multiplexer multiplexer_58 (
    .sel(and_106_out[1]), .in_0(nand_4_out[1]), .in_1(nand_4_out[2]), .out(multiplexer_58_out));
  Multiplexer multiplexer_59 (
    .sel(register_47_q[2]), .in_0(CT_DIR__LD), .in_1(register_47_q[2]), .out(multiplexer_59_out));
  and and_105 (and_105_out, multiplexer_58_out, multiplexer_59_out);
  not not_24 (not_24_out, multiplexer_58_out);
  nand nand_4 (nand_4_out[2], inst_comp_6_a_new, register_47_q[2], clr);
  Register #(.Bits(4)) register_66 (.D(multiplexer_51_out), .C(C_ct), .en(multiplexer_50_out[1]), .Q(register_66_q));
  Register register_67 (.D(multiplexer_52_out), .C(C_ct), .en(multiplexer_50_out[1]), .Q(register_67_q));
  Register #(.Bits(32)) register_68 (.D(multiplexer_53_out), .C(C_dt), .en(multiplexer_50_out[1]), .Q(register_68_q));
  Register #(.Bits(8)) register_69 (.D(multiplexer_54_out), .C(C_ct), .en(multiplexer_50_out[1]), .Q(register_69_q));
  Register register_70 (.D(multiplexer_55_out), .C(C_ct), .en(multiplexer_50_out[1]), .Q(register_70_q));
  Multiplexer #(.Bits(32)) multiplexer_60 (
    .sel(clr), .in_0(multiplexer_40_out), .in_1(CT_SC__FD), .out(multiplexer_60_out));
  Multiplexer #(.Bits(32)) multiplexer_61 (.sel(and_88_out), .in_0(CT_SC__D1), .in_1(CT_SC__D2), .out(sca_i));
  nand nand_5 (nand_2_out[1], ALU_busy, register_46_q[1]);
  Register register_71 (.D(and_105_out), .C(C_ct), .en(or_41_out), .Q(register_71_q[1]));
  or or_41 (or_41_out, not_24_out, multiplexer_50_out[1]);
  or or_42 (register_47_q[1], register_71_q[1], register_47_q[2]);
  assign and_106_out = nand_8_out & register_47_q;  // And and_106, 3 bits wide
  Multiplexer #(.Bits(4)) multiplexer_62 (
    .sel(register_47_q[1]), .in_0(CT_FU__INST), .in_1(register_66_q), .out(multiplexer_62_out));
  inst_comp inst_comp_7 (
    .A_id(register_66_q), .A_ep(register_67_q), .B_id(clr_id), .B_ep(clr_ep), .A_new(inst_comp_7_a_new));
  Multiplexer multiplexer_63 (
    .sel(register_47_q[1]), .in_0(CT_FU__EPOCH), .in_1(register_67_q), .out(multiplexer_63_out));
  Multiplexer #(.Bits(32)) multiplexer_64 (
    .sel(register_47_q[1]), .in_0(multiplexer_35_out), .in_1(register_68_q), .out(multiplexer_64_out));
  Multiplexer #(.Bits(8)) multiplexer_65 (
    .sel(register_47_q[1]), .in_0(CT_FU__WR), .in_1(register_69_q), .out(multiplexer_65_out));
  Multiplexer multiplexer_66 (.sel(register_47_q[1]), .in_0(CT_FU__EX), .in_1(register_70_q), .out(multiplexer_66_out));
  and and_107 (MB_MFE, MB_MF, register_48_q);
  and and_108 (MB_st__e, register_48_q, MB_type__st);
  and and_109 (MB_ld__e, register_48_q, ~MB_type__st);  // And
  add_s16c32 add_s16c32_1 (.a(register_53_q), .b(register_54_q), .s(MB_addr));  // open: c
  addsub_4c32 addsub_4c32_1 (.a(multiplexer_60_out), .b({1'b0, CT_RF__SCN}), .sub(CT_RF__SCD), .s(ISC_sc));  // open: c
  not not_25 (nand_2_out[0], ALU_busy);
  nand nand_6 (nand_1_out[0], or_45_out, ALU_busy, clr);
  inst_comp inst_comp_8 (.A_id(ALU_A_INST), .A_ep(ALU_A_EP), .B_id(clr_id), .B_ep(clr_ep), .A_new(ALU_A_CMP));
  Multiplexer multiplexer_67 (
    .sel(and_106_out[0]), .in_0(nand_4_out[0]), .in_1(nand_4_out[1]), .out(multiplexer_67_out));
  Multiplexer multiplexer_68 (
    .sel(register_47_q[1]), .in_0(CT_DIR__LD), .in_1(register_71_q[1]), .out(multiplexer_68_out));
  and and_110 (and_110_out, multiplexer_67_out, multiplexer_68_out);
  or or_43 (register_47_q[0], DIR_busy, register_71_q[1], register_47_q[2]);
  nand nand_7 (nand_4_out[1], inst_comp_7_a_new, register_71_q[1], clr);
  Register #(.Bits(4)) register_72 (.D(multiplexer_62_out), .C(C_ct), .en(DIR_LD), .Q(DIR_INST));
  Register register_73 (.D(multiplexer_63_out), .C(C_ct), .en(DIR_LD), .Q(DIR_EP));
  Register #(.Bits(32)) register_74 (.D(multiplexer_64_out), .C(C_dt), .en(DIR_LD), .Q(DIR));
  Register #(.Bits(8)) register_75 (.D(multiplexer_65_out), .C(C_ct), .en(DIR_LD), .Q(DIR_WR));
  Register register_76 (.D(multiplexer_66_out), .C(C_ct), .en(DIR_LD), .Q(DIR_EX));
  Register #(.Bits(4)) register_77 (.D(multiplexer_41_out), .C(C_ct), .en(ALU_B_LD), .Q(ALU_B_INST));
  Register register_78 (.D(multiplexer_42_out), .C(C_ct), .en(ALU_B_LD), .Q(ALU_B_EP));
  Register #(.Bits(32)) register_79 (.D(multiplexer_45_out), .C(C_dt), .en(ALU_B_LD), .Q(ALU_B_A));
  Register #(.Bits(32)) register_80 (.D(multiplexer_46_out), .C(C_dt), .en(ALU_B_LD), .Q(ALU_B_B));
  Register #(.Bits(8)) register_81 (.D(multiplexer_47_out), .C(C_dt), .en(ALU_B_LD), .Q(ALU_B_FI));
  Register #(.Bits(9)) register_82 (.D(multiplexer_48_out), .C(C_ct), .en(ALU_B_LD), .Q(ALU_B_CT));
  Register #(.Bits(8)) register_83 (.D(multiplexer_49_out), .C(C_ct), .en(ALU_B_LD), .Q({ALU_B_WR, ALU_B_RM}));
  nand nand_8 (nand_8_out[2], DIR_busy, register_71_q[1], register_47_q[2]);
  and and_111 (LDB_forward, MB_ld__e, LDB_ldV);
  or or_44 (or_44_out, MEM_LD__RD, LDB_forward);
  and and_112 (and_112_out[0], ALU_A_LD, multiplexer_43_out);
  BitExtender #(.inputBits(1), .outputBits(2)) bitextender_6 (.in(ALU_A_CLR), .out(bitextender_6_out));
  and and_113 (and_112_out[1], ALU_A_LD, multiplexer_44_out);
  and and_114 (and_114_out[0], ALU_B_LD, multiplexer_43_out);
  BitExtender #(.inputBits(1), .outputBits(2)) bitextender_7 (.in(ALU_B_CLR), .out(bitextender_7_out));
  and and_115 (and_114_out[1], ALU_B_LD, multiplexer_44_out);
  or or_45 (or_45_out, ALU_A_CMP, ALU_B_CMP);
  nand nand_9 (nand_8_out[1], DIR_busy, register_71_q[1]);
  not not_26 (nand_8_out[0], DIR_busy);
  inst_comp inst_comp_9 (.A_id(DIR_INST), .A_ep(DIR_EP), .B_id(clr_id), .B_ep(clr_ep), .A_new(inst_comp_9_a_new));
  and and_116 (and_116_out, CT_ISS__OSTB, ~clr);  // And
  Multiplexer #(.Bits(32)) multiplexer_69 (
    .sel(LDB_forward), .in_0(MEM_LD__D), .in_1(LDB_ldD), .out(multiplexer_69_out));
  Multiplexer #(.Bits(4)) multiplexer_70 (
    .sel(LDB_forward), .in_0(MEM_LD__INST), .in_1(MB_INST), .out(multiplexer_70_out));
  and and_117 (and_117_out, CT_ISS__OLDB, ~clr);  // And
  and and_118 (and_118_out, ~and_112_out[0], ALU_A_STD);  // And
  and and_119 (and_119_out, ~and_112_out[1], ALU_A_STF);  // And
  and and_120 (and_120_out, ~and_114_out[0], ALU_B_STD);  // And
  and and_121 (and_121_out, ~and_114_out[1], ALU_B_STF);  // And
  inst_comp inst_comp_10 (.A_id(ALU_B_INST), .A_ep(ALU_B_EP), .B_id(clr_id), .B_ep(clr_ep), .A_new(ALU_B_CMP));
  nand nand_10 (nand_4_out[0], inst_comp_9_a_new, DIR_busy, clr);
  and and_122 (and_122_out, byte_I0[3], byte_I0[0]);
  and and_123 (and_123_out, byte_I0[2], byte_I0[0]);
  and and_124 (and_124_out, byte_I0_iv[3], byte_I0_iv[2], byte_I0[1], byte_I0_iv[0]);
  and and_125 (and_125_out, byte_I0_iv[2], byte_I0_iv[0]);
  and and_126 (and_126_out, byte_I0[2], byte_I0[0]);
  and and_127 (and_127_out, byte_I0[1], byte_I0[2], byte_I0[4]);
  and and_128 (and_128_out, byte_I0[3], byte_I0[4]);
  D_FF #(.Bits(2)) d_ff_18 (.D(and_112_out), .C(C_ct), .Q(d_ff_18_q));  // open: nQ
  assign and_129_out = d_ff_18_q & ~bitextender_6_out;  // And and_129, 2 bits wide
  RS_FF rs_ff_9 (.S(and_112_out[0]), .C(C_ct), .R(and_118_out), .nQ(rs_ff_9_nq));  // open: Q
  RS_FF rs_ff_10 (.S(and_112_out[1]), .C(C_ct), .R(and_119_out), .nQ(rs_ff_10_nq));  // open: Q
  D_FF #(.Bits(2)) d_ff_19 (.D(and_114_out), .C(C_ct), .Q(d_ff_19_q));  // open: nQ
  assign and_130_out = d_ff_19_q & ~bitextender_7_out;  // And and_130, 2 bits wide
  RS_FF rs_ff_11 (.S(and_114_out[0]), .C(C_ct), .R(and_120_out), .nQ(rs_ff_11_nq));  // open: Q
  RS_FF rs_ff_12 (.S(and_114_out[1]), .C(C_ct), .R(and_121_out), .nQ(rs_ff_12_nq));  // open: Q
  and and_131 (and_131_out, ~and_110_out, DIR_ST);  // And
  and and_132 (DIR_CLR, clr, inst_comp_9_a_new);
  store_buffer_debug store_buffer_debug_1 (
    .C(C_dt), .LD(MB_STB__LD), .W_d(MB_st__e), .inst_W(MB_INST), .D(MB_data), .A(MB_addr), .MD(MB_MD),
    .W_id(and_116_out), .epoch(epoch_IS), .inst(inst_IS), .com1(com1), .com2(com2), .com1_id(com1_inst),
    .com2_id(com2_inst), .ld_ep(MB_ep), .ld_id(MB_INST), .ld_addr(MB_addr), .clr(clr), .clr_ep(clr_ep),
    .clr_id(clr_id), .full(store_buffer_debug_1_full), .V(STB_M__V), .D_O(STB_M__D), .A_O(STB_M__A),
    .MD_O(STB_M__MD), .id_O(STB_M__ID), .ep_O(STB_M__EP), .ld_V(LDB_ldV), .ld_D(LDB_ldD));
  load_buffer_debug load_buffer_debug_1 (
    .C(C_dt), .LD(MB_LDB__LD), .LDB(FU_D__V[3]), .W_d(or_44_out), .inst_WD(multiplexer_70_out),
    .D(multiplexer_69_out), .W_a(MB_ld__e), .WC_a(LDB_forward), .inst_WA(MB_INST), .A(MB_addr), .MD(MB_MD),
    .MF(MB_MF), .WR(MB_WR), .PC(MB_PC), .W_id(and_117_out), .epoch(epoch_IS), .inst(inst_IS), .com1(com1),
    .com2(com2), .com1_id(com1_inst), .com2_id(com2_inst), .st(MB_st__e), .st_ep(MB_ep), .st_id(MB_INST),
    .st_addr(MB_addr), .st_data(MB_data), .clr(clr), .clr_ep(clr_ep), .clr_id(clr_id),
    .full(load_buffer_debug_1_full), .V(load_buffer_debug_1_v), .D_O(LDB_B__D),
    .id_O(load_buffer_debug_1_id_o), .ep_O(load_buffer_debug_1_ep_o), .WR_O(load_buffer_debug_1_wr_o),
    .MF_O(load_buffer_debug_1_mf_o), .M_V(LDB_M__V), .M_A(LDB_M__A), .M_MD(LDB_M__MD), .M_id(LDB_M__ID),
    .M_ep(LDB_M__EP), .fl(load_buffer_debug_1_fl), .fl_ep(load_buffer_debug_1_fl_ep),
    .fl_id(load_buffer_debug_1_fl_id), .fl_PC(load_buffer_debug_1_fl_pc));
  and and_133 (and_133_out, byte_I0_iv[7], byte_I0_iv[6], byte_I0[5]);
  and and_134 (and_134_out, byte_I0_iv[7], byte_I0[6], byte_I0_iv[5]);
  D_FF #(.Bits(2)) d_ff_20 (.D(and_129_out), .C(C_ct), .Q(d_ff_20_q));  // open: nQ
  and and_135 (ALU_A_UUD, rs_ff_9_nq, ALU_A_V);
  and and_136 (ALU_A_UUF, rs_ff_10_nq, ALU_A_V);
  D_FF #(.Bits(2)) d_ff_21 (.D(and_130_out), .C(C_ct), .Q(d_ff_21_q));  // open: nQ
  and and_137 (ALU_B_UUD, rs_ff_11_nq, ALU_B_V);
  and and_138 (ALU_B_UUF, rs_ff_12_nq, ALU_B_V);
  or or_46 (or_46_out, ALU_A_CLR, and_160_out);
  or or_47 (or_47_out, ALU_B_CLR, and_161_out);
  // alu_32 alu_32_1: pin names not known; wires that end beside it: ALU_A_A, ALU_A_B, ALU_A_FI, ALU_A_CT, ALU_A_RM, alu_32_1_p6, alu_32_1_p6, alu_32_1_p8, alu_32_1_p9, alu_32_1_p9, alu_32_1_p11, alu_32_1_p12, alu_32_1_p12, alu_32_1_p14, ALU_A_R, ALU_A_F
  alu_32 alu_32_2 (
    .A(ALU_B_A), .B(ALU_B_B), .F_I(ALU_B_FI), .CT(ALU_B_CT), .RM(ALU_B_RM), .E_A(alu_32_1_p8),
    .E_B(alu_32_1_p11), .E(alu_32_1_p14), .R_O(ALU_B_R), .F_O(ALU_B_F));
  RS_FF rs_ff_13 (.S(and_110_out), .C(C_ct), .R(and_131_out), .nQ(rs_ff_13_nq));  // open: Q
  D_FF V (.D(DIR_LD), .C(C_ct), .Q(V_q));  // open: nQ
  bus16x2_demux bus16x2_demux_3 (.bus_1(V1_inst), .bus_2(V2_inst), .E(DIR_V), .id(DIR_INST));
  and and_139 (and_139_out, byte_I0[4], byte_I0[3], byte_I0_iv[1], byte_I0_iv[2], byte_I0_iv[5], byte_I0_iv[6], byte_I0_iv[7]);
  or or_48 (or_48_out, and_122_out, and_123_out, and_124_out);
  nor nor_7 (nor_7_out, byte_I0[3], byte_I0[1], and_125_out, and_126_out);
  nor nor_8 (nor_8_out, and_127_out, and_128_out);
  and and_140 (and_140_out, byte_I0_iv[0], byte_I0_iv[1], byte_I0[2], byte_I0[3], byte_I0[4], byte_I0_iv[5], byte_I0_iv[6], byte_I0_iv[7]);
  and and_141 (and_141_out, byte_I0[1], byte_I0_iv[2], byte_I0[3], byte_I0[4], byte_I0_iv[5], byte_I0_iv[6], byte_I0_iv[7]);
  and and_142 (and_142_out, byte_I0_iv[4], byte_I0[5], byte_I0[6], byte_I0_iv[7]);
  and and_143 (and_143_out, com1, CT_FL__W1);
  and and_144 (and_144_out, com2, CT_FL__W2);
  assign {ALU_A_FRE, ALU_A_DRE} = d_ff_20_q & ~bitextender_6_out;  // And and_145, 2 bits wide
  assign {ALU_B_FRE, ALU_B_DRE} = d_ff_21_q & ~bitextender_7_out;  // And and_146, 2 bits wide
  and and_147 (and_147_out, ALU_A_VD, ~or_46_out);  // And
  and and_148 (and_148_out, ALU_A_VF, ~or_46_out);  // And
  and and_149 (and_149_out, ALU_B_VD, ~or_47_out);  // And
  and and_150 (and_150_out, ALU_B_VF, ~or_47_out);  // And
  PullDown #(.Bits(32)) pulldown_28 (.out(alu_32_1_p12));
  PullDown #(.Bits(32)) pulldown_29 (.out(alu_32_1_p14));
  or or_49 (DIR_free, DIR_ST, rs_ff_13_nq);
  and and_151 (DIR_RD, V_q, ~DIR_CLR);  // And
  D_FF d_ff_22 (.D(store_buffer_debug_1_full), .C(C_ct), .Q(STB_busy));  // open: nQ
  D_FF d_ff_23 (.D(load_buffer_debug_1_full), .C(C_ct), .Q(LDB_busy));  // open: nQ
  D_FF #(.Bits(4)) d_ff_24 (.D(load_buffer_debug_1_id_o), .C(C_ct), .Q(LDB_B__INST));  // open: nQ
  D_FF #(.Bits(8)) d_ff_25 (.D(load_buffer_debug_1_wr_o), .C(C_ct), .Q(LDB_B__WR));  // open: nQ
  D_FF d_ff_26 (.D(load_buffer_debug_1_fl), .C(C_ct), .Q(Fl_MEM));  // open: nQ
  D_FF #(.Bits(4)) d_ff_27 (.D(load_buffer_debug_1_fl_id), .C(C_ct), .Q(FL_MEM__ID));  // open: nQ
  and and_152 (and_152_out, byte_I0[1], byte_I0[2], byte_I0[3], byte_I0[4], byte_I0_iv[5], byte_I0_iv[6], byte_I0_iv[7]);
  or or_50 (or_50_out, and_133_out, and_134_out);
  Comparator #(.Bits(3)) comparator_21 (.a(byte_I0[2:0]), .b(3'b110), .eq(comparator_21_eq));  // open: gt, lt
  or or_51 (CT_RF__FLS, and_143_out, and_144_out);
  RS_FF rs_ff_14 (.S(ALU_A_DRE), .C(C_ct), .R(ALU_A_DRD), .Q(ALU_A_DRD));  // open: nQ
  RS_FF rs_ff_15 (.S(ALU_A_FRE), .C(C_ct), .R(ALU_A_FRD), .Q(ALU_A_FRD));  // open: nQ
  RS_FF rs_ff_16 (.S(ALU_B_DRE), .C(C_ct), .R(ALU_B_DRD), .Q(ALU_B_DRD));  // open: nQ
  RS_FF rs_ff_17 (.S(ALU_B_FRE), .C(C_ct), .R(ALU_B_FRD), .Q(ALU_B_FRD));  // open: nQ
  RS_FF rs_ff_18 (.S(and_147_out), .C(C_ct), .R(or_46_out), .Q(rs_ff_18_q));  // open: nQ
  RS_FF rs_ff_19 (.S(and_148_out), .C(C_ct), .R(or_46_out), .Q(rs_ff_19_q));  // open: nQ
  RS_FF rs_ff_20 (.S(and_149_out), .C(C_ct), .R(or_47_out), .Q(rs_ff_20_q));  // open: nQ
  RS_FF rs_ff_21 (.S(and_150_out), .C(C_ct), .R(or_47_out), .Q(rs_ff_21_q));  // open: nQ
  D_FF d_ff_28 (.D(load_buffer_debug_1_ep_o), .C(C_ct), .Q(LDB_B__EP));  // open: nQ
  D_FF d_ff_29 (.D(load_buffer_debug_1_mf_o), .C(C_ct), .Q(LDB_B__MF));  // open: nQ
  D_FF d_ff_30 (.D(load_buffer_debug_1_fl_ep), .C(C_ct), .Q(FL_MEM__EP));  // open: nQ
  D_FF #(.Bits(32)) d_ff_31 (.D(load_buffer_debug_1_fl_pc), .C(C_ct), .Q(MEM_FPC));  // open: nQ
  and and_153 (and_153_out, byte_I0_iv[7], byte_I0_iv[6], byte_I0_iv[5], byte_I0_iv[4]);
  and and_154 (and_154_out, byte_I0_iv[7], byte_I0_iv[6], byte_I0_iv[5], byte_I0[4], byte_I0_iv[3]);
  or or_52 (or_52_out, and_140_out, and_141_out);
  and and_155 (and_155_out, byte_I0[0], byte_I0_iv[1], byte_I0[2], byte_I0[3], byte_I0[4], byte_I0_iv[5], byte_I0_iv[6], byte_I0_iv[7]);
  not not_27 (not_27_out, comparator_21_eq);
  or or_53 (or_53_out, ALU_A_VD, ALU_A_UUD, rs_ff_18_q);
  or or_54 (or_54_out, ALU_A_VF, ALU_A_UUF, rs_ff_19_q);
  or or_55 (or_55_out, ALU_B_VD, ALU_B_UUD, rs_ff_20_q);
  or or_56 (or_56_out, ALU_B_VF, ALU_B_UUF, rs_ff_21_q);
  and and_156 (DIR_LD, and_110_out, DIR_free);
  not not_28 (DIR_busy, DIR_free);
  and and_157 (and_157_out, d_ff_32_q, ~FU_D__V[3]);  // And
  not not_29 (not_29_out, or_48_out);
  and and_158 (and_158_out, and_152_out, byte_I0[0]);
  and and_159 (and_159_out, byte_I0_iv[0], and_152_out);
  or or_57 (or_57_out, ALU_A_STD, rs_ff_9_nq);
  or or_58 (or_58_out, ALU_A_STF, rs_ff_10_nq);
  or or_59 (or_59_out, ALU_B_STD, rs_ff_11_nq);
  or or_60 (or_60_out, ALU_B_STF, rs_ff_12_nq);
  and and_160 (and_160_out, or_53_out, ~ALU_A_CLR, or_54_out);  // And
  bus16x2_demux bus16x2_demux_4 (.bus_1(V1_inst), .bus_2(V2_inst), .E(and_160_out), .id(ALU_A_INST));
  and and_161 (and_161_out, or_55_out, ~ALU_B_CLR, or_56_out);  // And
  bus16x2_demux bus16x2_demux_5 (.bus_1(V1_inst), .bus_2(V2_inst), .E(and_161_out), .id(ALU_B_INST));
  nor nor_9 (ALU_busy, ALU_A_LRD, ALU_B_LRD);
  or or_61 (ALU_free, ALU_A_LRD, ALU_B_LRD);
  Register #(.Bits(32)) register_84 (.D(ALU_A_R), .C(C_dt), .en(ALU_A_DRE), .Q(ALU_A_T__R));
  Register #(.Bits(8)) register_85 (.D(ALU_A_F), .C(C_dt), .en(ALU_A_FRE), .Q(ALU_A_T__F));
  Register #(.Bits(32)) register_86 (.D(ALU_B_R), .C(C_dt), .en(ALU_B_DRE), .Q(ALU_B_T__R));
  Register #(.Bits(8)) register_87 (.D(ALU_B_F), .C(C_dt), .en(ALU_B_FRE), .Q(ALU_B_T__F));
  and and_162 (and_162_out, ~MB_MF, MB_st__e);  // And
  and and_163 (and_163_out, ~LDB_B__MF, FU_D__V[3]);  // And
  D_FF d_ff_32 (.D(load_buffer_debug_1_v), .C(C_ct), .Q(d_ff_32_q));  // open: nQ
  D_FF d_ff_33 (.D(and_157_out), .C(C_ct), .nQ(d_ff_33_nq));  // open: Q
  and and_164 (LDB_B__RD, d_ff_32_q, d_ff_33_nq);
  or or_62 (or_62_out, and_153_out, and_139_out, and_154_out);
  assign issue = or_62_out ? issue_e : 1'bz;  // Driver driver_131
  assign CT_ISS__URA = or_62_out ? 1'b1 : 1'bz;  // Driver driver_132
  assign CT_ISS__URB = or_62_out ? not_29_out : 1'bz;  // Driver driver_133
  assign CT_ISS__RA = or_62_out ? byte_I1[7:3] : 5'bz;  // Driver driver_134
  assign CT_ISS__RB = or_62_out ? byte_I2[7:3] : 5'bz;  // Driver driver_135
  assign CT_ISS__UFL = or_62_out ? nor_7_out : 1'bz;  // Driver driver_136
  assign CT_ISS__ORC = or_62_out ? nor_8_out : 1'bz;  // Driver driver_137
  assign CT_ISS__RC = or_62_out ? byte_I1[7:3] : 5'bz;  // Driver driver_138
  assign CT_ISS__OFL = or_62_out ? 1'b1 : 1'bz;  // Driver driver_139
  assign CT_ISS__UFU = or_62_out ? 3'b001 : 3'bz;  // Driver driver_140
  assign CT_ISS__URA = and_140_out ? 1'b1 : 1'bz;  // Driver driver_141
  assign CT_ISS__RA = and_140_out ? byte_I2[7:3] : 5'bz;  // Driver driver_142
  assign issue = or_52_out ? issue_e : 1'bz;  // Driver driver_143
  assign CT_ISS__ORC = or_52_out ? 1'b1 : 1'bz;  // Driver driver_144
  assign CT_ISS__RC = or_52_out ? byte_I1[7:3] : 5'bz;  // Driver driver_145
  assign CT_ISS__UFU = or_52_out ? 3'b010 : 3'bz;  // Driver driver_146
  assign issue = and_152_out ? issue_e : 1'bz;  // Driver driver_147
  assign CT_ISS__URB = and_152_out ? 1'b1 : 1'bz;  // Driver driver_148
  assign CT_ISS__RB = and_152_out ? 5'b11110 : 5'bz;  // Driver driver_149
  assign CT_ISS__OSC = and_152_out ? 1'b1 : 1'bz;  // Driver driver_150
  assign CT_ISS__UMM = and_152_out ? 1'b1 : 1'bz;  // Driver driver_151
  assign CT_ISS__UFU = and_152_out ? 3'b011 : 3'bz;  // Driver driver_152
  assign CT_ISS__URA = and_158_out ? 1'b1 : 1'bz;  // Driver driver_153
  assign CT_ISS__RA = and_158_out ? byte_I1[7:3] : 5'bz;  // Driver driver_154
  assign CT_ISS__OSTB = and_158_out ? issue_e : 1'bz;  // Driver driver_155
  assign CT_ISS__ORC = and_159_out ? 1'b1 : 1'bz;  // Driver driver_156
  assign CT_ISS__RC = and_159_out ? byte_I1[7:3] : 5'bz;  // Driver driver_157
  assign CT_ISS__OLDB = and_159_out ? issue_e : 1'bz;  // Driver driver_158
  assign issue = or_50_out ? issue_e : 1'bz;  // Driver driver_159
  assign CT_ISS__URA = or_50_out ? 1'b1 : 1'bz;  // Driver driver_160
  assign CT_ISS__RA = or_50_out ? byte_I0[4:0] : 5'bz;  // Driver driver_161
  assign CT_ISS__UMM = or_50_out ? 1'b1 : 1'bz;  // Driver driver_162
  assign CT_ISS__UFU = or_50_out ? 3'b011 : 3'bz;  // Driver driver_163
  assign CT_ISS__URB = and_134_out ? 1'b1 : 1'bz;  // Driver driver_164
  assign CT_ISS__RB = and_134_out ? byte_I1[7:3] : 5'bz;  // Driver driver_165
  assign CT_ISS__ORC = and_133_out ? 1'b1 : 1'bz;  // Driver driver_166
  assign CT_ISS__RC = and_133_out ? byte_I1[7:3] : 5'bz;  // Driver driver_167
  assign CT_ISS__OLDB = and_133_out ? issue_e : 1'bz;  // Driver driver_168
  assign CT_ISS__OSTB = and_134_out ? issue_e : 1'bz;  // Driver driver_169
  assign issue = and_155_out ? issue_e : 1'bz;  // Driver driver_170
  assign CT_BLOCK = and_155_out ? 1'b1 : 1'bz;  // Driver driver_171
  assign CT_UBTB = and_142_out ? issue_e : 1'bz;  // Driver driver_172
  assign issue = and_142_out ? issue_e : 1'bz;  // Driver driver_173
  assign CT_ISS__URA = and_142_out ? 1'b1 : 1'bz;  // Driver driver_174
  assign CT_ISS__RA = and_142_out ? byte_I1[7:3] : 5'bz;  // Driver driver_175
  assign CT_ISS__UFL = and_142_out ? not_27_out : 1'bz;  // Driver driver_176
  assign CT_ISS__UFU = and_142_out ? 3'b111 : 3'bz;  // Driver driver_177
  DipSwitch dipswitch_15 (.out(MB_busy));
  assign CT_RF__PCSE = Fl_MEM ? 1'b1 : 1'bz;  // Driver driver_178
  assign CT_RF__PCJ = Fl_MEM ? 1'b1 : 1'bz;  // Driver driver_179
  Multiplexer #(.Bits(8)) multiplexer_71 (.sel(and_144_out), .in_0(CT_FL__D1), .in_1(CT_FL__D2), .out(fl_i));
  and and_165 (ALU_A_LD, and_104_out, or_58_out, or_57_out);
  and and_166 (ALU_A_LRD, or_57_out, or_58_out);
  nand nand_11 (nand_11_out, or_57_out, or_58_out);
  and and_167 (ALU_B_LD, nand_11_out, and_104_out, or_60_out, or_59_out);
  and and_168 (ALU_B_LRD, or_59_out, or_60_out);
  and and_169 (and_169_out, ~ALU_A_LD, or_46_out);  // And
  and and_170 (and_170_out, ~ALU_B_LD, or_47_out);  // And
  bus16_demux bus16_demux_2 (.bus(V1_inst), .E(MB_st__e), .id(MB_INST));
  bus16_demux bus16_demux_3 (.bus(V2_inst), .E(and_162_out), .id(MB_INST));
  bus16_demux bus16_demux_4 (.bus(V1_inst), .E(FU_D__V[3]), .id(LDB_B__INST));
  bus16_demux bus16_demux_5 (.bus(V2_inst), .E(and_163_out), .id(LDB_B__INST));
  not not_30 (MB_free, MB_busy);
  and and_171 (ALU_A_CLR, clr, ALU_A_CMP);
  and and_172 (ALU_B_CLR, clr, ALU_B_CMP);
  RS_FF rs_ff_22 (.S(ALU_A_LD), .C(C_ct), .R(and_169_out), .Q(ALU_A_V));  // open: nQ
  RS_FF rs_ff_23 (.S(ALU_B_LD), .C(C_ct), .R(and_170_out), .Q(ALU_B_V));  // open: nQ
  and and_173 (and_173_out, byte_I0[1], byte_I0_iv[2], byte_I0[3], byte_I0[4], byte_I0[5], byte_I0[6], byte_I0_iv[7]);
  not not_31 (not_31_out, E_t);
  and and_174 (and_174_out, byte_I0_iv[0], byte_I0_iv[1], byte_I0_iv[2], byte_I0_iv[3], byte_I0[4], byte_I0[5], byte_I0[6], byte_I0_iv[7]);
  and and_175 (and_175_out, byte_I0[0], byte_I0_iv[1], byte_I0_iv[2], byte_I0_iv[3], byte_I0[4], byte_I0[5], byte_I0[6], byte_I0_iv[7]);
  and and_176 (and_176_out, byte_I0_iv[1], byte_I0[2], byte_I0_iv[3], byte_I0[4], byte_I0[5], byte_I0[6], byte_I0_iv[7]);
  and and_177 (and_177_out, byte_I0[0], and_173_out);
  and and_178 (and_178_out, and_173_out, byte_I0_iv[0]);
  and and_179 (and_179_out, byte_I0_iv[0], byte_I0[1], byte_I0[2], byte_I0_iv[3], byte_I0[4], byte_I0[5], byte_I0[6], byte_I0_iv[7]);
  and and_180 (and_180_out, byte_I0[0], byte_I0[1], byte_I0[2], byte_I0_iv[3], byte_I0[4], byte_I0[5], byte_I0[6], byte_I0_iv[7]);
  res_station_debug res_station_debug_1 (
    .C(C_ct), .res(not_31_out), .E(issue), .D({byte_I0, byte_I1, byte_I2, byte_I3}), .BTB_PK(BTB_pack__iss),
    .ep_I(epoch_IS), .inst(inst_IS), .URA(CT_ISS__URA), .URB(CT_ISS__URB), .RA(CT_ISS__RA), .RB(CT_ISS__RB),
    .UMM(CT_ISS__UMM), .UFL(CT_ISS__UFL), .UFU(CT_ISS__UFU), .ORC(CT_ISS__ORC), .RC(CT_ISS__RC),
    .OSC(CT_ISS__OSC), .OFL(CT_ISS__OFL), .BLOCK(CT_BLOCK), .com1(com1), .com2(com2), .com1_inst(com1_inst),
    .com2_inst(com2_inst), .pcm1(CT_ROB__GEN__STA), .pcm2(CT_ROB__GEN__STB), .pcm1_inst(ROB_GEN_INSTA),
    .pcm2_inst(ROB_GEN_INSTB), .pcmf1(CT_ROB__FL__STA), .pcmf2(CT_ROB__FL__STB), .pcmf1_inst(ROB_FL_INSTA),
    .pcmf2_inst(ROB_FL_INSTB), .clr(clr), .clr_ep(clr_ep), .clr_id(clr_id), .FU_free(FU_free), .V(CT_DISP),
    .disp_32({res_station_debug_1_disp_32, byte_D1, byte_D2, byte_D3}), .BTB_DP(BTB_DP), .ep_O(epoch_DP),
    .disp(inst_DP), .full(RS_full), .U1(FOR_UA), .U2(FOR_UB), .U3(FOR_UF), .I1(FOR_IA), .I2(FOR_IB),
    .I3(FOR_IF));
  store_controller store_controller_1 (
    .C(C_ct), .in1(ALU_A_DRD), .in2(ALU_B_DRD), .in3(DIR_RD), .in4(LDB_B__RD), .in5(1'b0), .in6(1'b0),
    .in7(1'b0), .in8(1'b0), .clr({3'b000, FU_CLR[4], 1'b0, DIR_CLR, ALU_B_CLR, ALU_A_CLR}),
    .D1_sel(store_controller_1_d1_sel), .D2_sel(store_controller_1_d2_sel), .ST1(CT_ROB__GEN__STA),
    .ST2(CT_ROB__GEN__STB), .out1(ALU_A_STD), .out2(ALU_B_STD), .out3(DIR_ST), .out4(LDB_B__ST),
    .V({FU_D__V, DIR_V, ALU_B_VD, ALU_A_VD}));  // open: out5, out6, out7, out8
  store_controller_half store_controller_half_1 (
    .C(C_ct), .in1(ALU_A_FRD), .in2(ALU_B_FRD), .in3(1'b0), .in4(1'b0),
    .clr({1'b0, DIR_CLR, ALU_B_CLR, ALU_A_CLR}), .D1_sel(store_controller_half_1_d1_sel),
    .D2_sel(store_controller_half_1_d2_sel), .ST1(CT_ROB__FL__STA), .ST2(CT_ROB__FL__STB), .out1(ALU_A_STF),
    .out2(ALU_B_STF), .V({FU_F__V, ALU_B_VF, ALU_A_VF}));  // open: out3, out4
  store_controller_half store_controller_half_2 (
    .C(C_ct), .in1(TRAP_IRD), .in2(1'b0), .in3(1'b0), .in4(1'b0), .clr({3'b000, FU_CLR[4]}),
    .D1_sel(store_controller_half_2_d1_sel), .D2_sel(store_controller_half_2_d2_sel), .ST1(CT_ROB__INT__STA),
    .ST2(CT_ROB__INT__STB), .out1(TRAP_ST), .V(FU_I__V));  // open: out2, out3, out4
  Demultiplexer #(.Selector_Bits(4)) demultiplexer_3 (
    .sel(priorityencoder_3_num), .in(and_191_out), .out_0(demultiplexer_3_out_0[0]),
    .out_1(demultiplexer_3_out_0[1]), .out_2(demultiplexer_3_out_0[2]), .out_3(demultiplexer_3_out_0[3]),
    .out_4(demultiplexer_3_out_0[4]), .out_5(demultiplexer_3_out_0[5]), .out_6(demultiplexer_3_out_0[6]),
    .out_7(demultiplexer_3_out_0[7]), .out_8(demultiplexer_3_out_0[8]), .out_9(demultiplexer_3_out_0[9]),
    .out_10(demultiplexer_3_out_0[10]), .out_11(demultiplexer_3_out_0[11]),
    .out_12(demultiplexer_3_out_0[12]), .out_13(demultiplexer_3_out_0[13]),
    .out_14(demultiplexer_3_out_0[14]), .out_15(demultiplexer_3_out_0[15]));
  Demultiplexer #(.Selector_Bits(4)) demultiplexer_4 (
    .sel(CT_FU__INST), .in(CT_RET__LD), .out_0(demultiplexer_4_out_0[0]), .out_1(demultiplexer_4_out_0[1]),
    .out_2(demultiplexer_4_out_0[2]), .out_3(demultiplexer_4_out_0[3]), .out_4(demultiplexer_4_out_0[4]),
    .out_5(demultiplexer_4_out_0[5]), .out_6(demultiplexer_4_out_0[6]), .out_7(demultiplexer_4_out_0[7]),
    .out_8(demultiplexer_4_out_0[8]), .out_9(demultiplexer_4_out_0[9]), .out_10(demultiplexer_4_out_0[10]),
    .out_11(demultiplexer_4_out_0[11]), .out_12(demultiplexer_4_out_0[12]),
    .out_13(demultiplexer_4_out_0[13]), .out_14(demultiplexer_4_out_0[14]), .out_15(demultiplexer_4_out_0[15]));
  or or_63 (or_63_out, JPU_INT, JPU_RET);
  nor nor_10 (nor_10_out, JPU_INT, JPU_RET);
  nor nor_11 (nor_11_out, JPU_INT, JPU_RET);
  assign ISS_kernel = and_176_out ? byte_I0[0] : 1'bz;  // Driver driver_180
  assign CT_BLOCK = and_176_out ? 1'b1 : 1'bz;  // Driver driver_181
  assign issue = and_176_out ? issue_e : 1'bz;  // Driver driver_182
  assign CT_ISS__HALT = and_176_out ? 1'b1 : 1'bz;  // Driver driver_183
  assign CT_ISS__UMM = and_176_out ? 1'b1 : 1'bz;  // Driver driver_184
  assign CT_ISS__UFU = and_176_out ? 3'b100 : 3'bz;  // Driver driver_185
  assign CT_ISS__URA = and_177_out ? 1'b1 : 1'bz;  // Driver driver_186
  assign CT_ISS__RA = and_177_out ? byte_I1[7:3] : 5'bz;  // Driver driver_187
  assign ISS_kernel = and_173_out ? 1'b1 : 1'bz;  // Driver driver_188
  assign issue = and_173_out ? issue_e : 1'bz;  // Driver driver_189
  assign CT_ISS__UFU = and_173_out ? 3'b010 : 3'bz;  // Driver driver_190
  assign CT_BLOCK = and_173_out ? 1'b1 : 1'bz;  // Driver driver_191
  assign CT_ISS__UMM = and_173_out ? 1'b1 : 1'bz;  // Driver driver_192
  assign CT_ISS__ORC = and_178_out ? 1'b1 : 1'bz;  // Driver driver_193
  assign CT_ISS__RC = and_178_out ? byte_I1[7:3] : 5'bz;  // Driver driver_194
  assign CT_BLOCK = and_179_out ? 1'b1 : 1'bz;  // Driver driver_195
  assign issue = and_179_out ? issue_e : 1'bz;  // Driver driver_196
  assign CT_ISS__HALT = and_179_out ? 1'b1 : 1'bz;  // Driver driver_197
  assign CT_ISS__UMM = and_179_out ? 1'b1 : 1'bz;  // Driver driver_198
  assign CT_ISS__UFU = and_179_out ? 3'b100 : 3'bz;  // Driver driver_199
  assign ISS_kernel = and_180_out ? 1'b1 : 1'bz;  // Driver driver_200
  assign CT_BLOCK = and_180_out ? 1'b1 : 1'bz;  // Driver driver_201
  assign issue = and_180_out ? issue_e : 1'bz;  // Driver driver_202
  assign CT_ISS__HALT = and_180_out ? 1'b1 : 1'bz;  // Driver driver_203
  assign CT_ISS__UMM = and_180_out ? 1'b1 : 1'bz;  // Driver driver_204
  assign CT_ISS__UFU = and_180_out ? 3'b100 : 3'bz;  // Driver driver_205
  PullDown #(.Bits(3)) pulldown_30 (.out(CT_ISS__UFU));
  PullDown pulldown_31 (.out(CT_ISS__OSTB));
  PullDown pulldown_32 (.out(clr));
  PullDown pulldown_33 (.out(clr_ep));
  PullDown #(.Bits(4)) pulldown_34 (.out(clr_id));
  Multiplexer #(.Bits(32)) multiplexer_72 (.sel(JPU_INT), .in_0(CT_RF__DR), .in_1(int_vec_t), .out(multiplexer_72_out));
  BitExtender #(.inputBits(1)) bitextender_8 (.in(nor_10_out), .out(bitextender_8_out));
  BitExtender #(.inputBits(1), .outputBits(37)) bitextender_9 (.in(nor_11_out), .out(bitextender_9_out));
  BitExtender #(.inputBits(1)) bitextender_10 (.in(CT_FU__EPOCH), .out(bitextender_10_out));
  assign not_32_out = ~demultiplexer_4_out_0;  // Not not_32, 16 bits wide
  BitExtender #(.inputBits(1)) bitextender_11 (.in(CT_FU__EPOCH), .out(bitextender_11_out));
  assign issue = and_174_out ? issue_e : 1'bz;  // Driver driver_206
  assign CT_ISS__URA = and_174_out ? 1'b1 : 1'bz;  // Driver driver_207
  assign CT_ISS__RA = and_174_out ? byte_I1[7:3] : 5'bz;  // Driver driver_208
  assign CT_ISS__URB = and_174_out ? 1'b1 : 1'bz;  // Driver driver_209
  assign CT_ISS__RB = and_174_out ? 5'b11110 : 5'bz;  // Driver driver_210
  assign CT_ISS__OSC = and_174_out ? 1'b1 : 1'bz;  // Driver driver_211
  assign CT_ISS__UMM = and_174_out ? 1'b1 : 1'bz;  // Driver driver_212
  assign CT_ISS__UFU = and_174_out ? 3'b110 : 3'bz;  // Driver driver_213
  assign CT_ISS__OSTB = and_174_out ? issue_e : 1'bz;  // Driver driver_214
  assign CT_UBTB = and_174_out ? issue_e : 1'bz;  // Driver driver_215
  assign issue = and_175_out ? issue_e : 1'bz;  // Driver driver_216
  assign CT_ISS__URB = and_175_out ? 1'b1 : 1'bz;  // Driver driver_217
  assign CT_ISS__RB = and_175_out ? 5'b11110 : 5'bz;  // Driver driver_218
  assign CT_ISS__OSC = and_175_out ? 1'b1 : 1'bz;  // Driver driver_219
  assign CT_ISS__UMM = and_175_out ? 1'b1 : 1'bz;  // Driver driver_220
  assign CT_ISS__UFU = and_175_out ? 3'b110 : 3'bz;  // Driver driver_221
  assign CT_ISS__OLDB = and_175_out ? issue_e : 1'bz;  // Driver driver_222
  assign CT_UBTB = and_175_out ? issue_e : 1'bz;  // Driver driver_223
  Multiplexer #(.Bits(8)) multiplexer_73 (
    .sel(CT_DISP), .in_0(8'h72), .in_1(res_station_debug_1_disp_32), .out(byte_D0));
  Multiplexer #(.Bits(32)) multiplexer_74 (.sel(JPU_RET), .in_0(pc_read), .in_1(pc_ret), .out(multiplexer_74_out));
  Multiplexer #(.Bits(4)) multiplexer_75 (.sel(JPU_RET), .in_0(CT_FU__INST), .in_1(RET_INST), .out(multiplexer_75_out));
  Multiplexer multiplexer_76 (.sel(JPU_RET), .in_0(CT_FU__EPOCH), .in_1(RET_EPOCH), .out(multiplexer_76_out));
  Multiplexer #(.Bits(32)) multiplexer_77 (
    .sel(or_63_out), .in_0(R_A), .in_1(multiplexer_72_out), .out(multiplexer_77_out));
  assign and_181_out = {byte_D2, byte_D3} & bitextender_8_out;  // And and_181, 16 bits wide
  assign and_182_out = BTB_DP & bitextender_9_out;  // And and_182, 37 bits wide
  or or_64 (or_64_out, CT_JPU__JP, JPU_INT, JPU_RET);
  or or_65 (or_65_out, CT_FU__MF, JPU_RET);
  assign not_33_out = ~demultiplexer_3_out_0;  // Not not_33, 16 bits wide
  assign or_66_out = bitextender_10_out | not_32_out;  // Or or_66, 16 bits wide
  assign and_183_out = bitextender_11_out & demultiplexer_4_out_0;  // And and_183, 16 bits wide
  and and_184 (and_184_out, ~CT_JPU__LD, JPU_BTB__ST);  // And
  assign or_67_out = register_96_q | demultiplexer_4_out_0;  // Or or_67, 16 bits wide
  assign or_68_out = register_97_q | and_183_out;  // Or or_68, 16 bits wide
  // data_select_32 data_select_32_1: pin names not known; wires that end beside it: store_controller_1_d1_sel, store_controller_1_d2_sel, ALU_A_T__R, ALU_B_T__R, DIR, LDB_B__D, {32{1'b0}}, {32{1'b0}}, {32{1'b0}}, {32{1'b0}}, ROB_GEN_DA, ROB_GEN_DB
  data_select_8H data_select_8h_1 (
    .D1_sel(store_controller_half_1_d1_sel), .D2_sel(store_controller_half_1_d2_sel), .in1(ALU_A_T__F),
    .in2(ALU_B_T__F), .in3({8{1'b0}}), .in4({8{1'b0}}), .out1(ROB_FL_A), .out2(ROB_FL_B));
  data_select_6H data_select_6h_1 (
    .D1_sel(store_controller_half_2_d1_sel), .D2_sel(store_controller_half_2_d2_sel), .in1(TRAP_INT),
    .in2({6{1'b0}}), .in3({6{1'b0}}), .in4({6{1'b0}}), .out1(ROB_INT_A), .out2(ROB_INT_B));
  data_select_1 data_select_1_1 (
    .D1_sel(store_controller_1_d1_sel), .D2_sel(store_controller_1_d2_sel), .in1(ALU_A_EP), .in2(ALU_B_EP),
    .in3(DIR_EP), .in4(LDB_B__EP), .in5(1'b0), .in6(1'b0), .in7(1'b0), .in8(1'b0), .out1(ROB_GEN_EPA),
    .out2(ROB_GEN_EPB));
  RS_FF rs_ff_24 (.S(CT_JPU__LD), .C(C_ct), .R(and_184_out), .Q(JPU_BTB__ST), .nQ(rs_ff_24_nq));
  Register #(.Bits(32)) register_88 (.D(multiplexer_74_out), .C(C_dt), .en(JPU_LD), .Q(JPU_PC));
  Register #(.Bits(4)) register_89 (.D(multiplexer_75_out), .C(C_ct), .en(JPU_LD), .Q(Fl_JPU__INST));
  Register register_90 (.D(multiplexer_76_out), .C(C_ct), .en(JPU_LD), .Q(Fl_JPU__EP));
  Register #(.Bits(32)) register_91 (.D(multiplexer_77_out), .C(C_dt), .en(JPU_LD), .Q(register_91_q));
  Register #(.Bits(16)) register_92 (.D(and_181_out), .C(C_dt), .en(JPU_LD), .Q(register_92_q));
  Register #(.Bits(37)) register_93 (
    .D(and_182_out), .C(C_ct), .en(JPU_LD),
    .Q({JPU_BTB__tar, JPU_BTB__pred, JPU_BTB__J, JPU_BTB__V, JPU_BTBPK[0]}));
  Register register_94 (.D(or_64_out), .C(C_ct), .en(JPU_LD), .Q(JPU_JP));
  Register register_95 (.D(or_65_out), .C(C_ct), .en(JPU_LD), .Q(JPU_MF));
  assign and_185_out = icmks_16 & not_33_out & or_67_out;  // And and_185, 16 bits wide
  or or_69 (or_69_out, CT_RET__LD, and_191_out, ext_en);
  assign and_186_out = or_66_out & or_68_out;  // And and_186, 16 bits wide
  or or_70 (or_70_out, rs_ff_24_nq, JPU_BTB__ST);
  D_FF #(.Bits(32)) d_ff_34 (.D(register_91_q), .C(C_ct), .Q(d_ff_34_q));  // open: nQ
  D_FF #(.Bits(16)) d_ff_35 (.D(register_92_q), .C(C_ct), .Q(d_ff_35_q));  // open: nQ
  and and_187 (JPU_LD, CT_JPU__LD, or_70_out);
  Register #(.Bits(16)) register_96 (.D(and_185_out), .C(C_ct), .en(or_69_out), .Q(register_96_q));
  Register #(.Bits(16)) register_97 (.D(and_186_out), .C(C_ct), .en(or_69_out), .Q(register_97_q));
  add_s16c32 add_s16c32_2 (.a(multiplexer_78_out), .b(multiplexer_79_out), .s(JPU_ADDR));  // open: c
  Multiplexer #(.Bits(32)) multiplexer_78 (.sel(JPU_JP), .in_0(JPU_PC), .in_1(d_ff_34_q), .out(multiplexer_78_out));
  Multiplexer #(.Bits(16)) multiplexer_79 (.sel(JPU_JP), .in_0(16'h4), .in_1(d_ff_35_q), .out(multiplexer_79_out));
  assign and_188_out = V1_inst & register_96_q;  // And and_188, 16 bits wide
  BitSelector #(.Selector_Bits(4)) bitselector_1 (
    .in(register_97_q), .sel(priorityencoder_3_num), .out(bitselector_1_out));
  PullDown pulldown_35 (.out(CT_ALU__M));
  PullDown pulldown_36 (.out(CT_ALU__LD));
  PullDown pulldown_37 (.out(CT_ALU__WD));
  PullDown pulldown_38 (.out(CT_ALU__WF));
  PullDown pulldown_39 (.out(CT_FU__EPOCH));
  PullDown #(.Bits(4)) pulldown_40 (.out(CT_FU__INST));
  PullDown #(.Bits(8)) pulldown_41 (.out(CT_FU__WR));
  PullDown pulldown_42 (.out(CT_DIR__LD));
  PullDown pulldown_43 (.out(CT_DIR__M));
  PullDown pulldown_44 (.out(CT_DIR__MS));
  PullDown pulldown_45 (.out(MB_ep));
  PullDown #(.Bits(4)) pulldown_46 (.out(LD_id));
  PullDown #(.Bits(32)) pulldown_47 (.out(LD_addr));
  PullDown pulldown_48 (.out(CT_STB__LD));
  PullDown pulldown_49 (.out(CT_LDB__LD));
  PullDown pulldown_50 (.out(CT_MB__LD));
  PullDown pulldown_51 (.out(CT_MB__ST));
  PullDown pulldown_52 (.out(CT_ISS__OLDB));
  PullDown pulldown_53 (.out(CT_UBTB));
  PullDown pulldown_54 (.out(CT_USCB));
  and and_189 (and_189_out, ~JPU_MF, JPU_BTB__ST);  // And
  data_select_8 data_select_8_1 (
    .D1_sel(store_controller_1_d1_sel), .D2_sel(store_controller_1_d2_sel), .in1({ALU_A_WR, ALU_A_RM}),
    .in2({ALU_B_WR, ALU_B_RM}), .in3(DIR_WR), .in4(LDB_B__WR), .in5({8{1'b0}}), .in6({8{1'b0}}),
    .in7({8{1'b0}}), .in8({8{1'b0}}), .out1(ROB_GEN_WA), .out2(ROB_GEN_WB));
  data_select_4H data_select_4h_1 (
    .D1_sel(store_controller_half_1_d1_sel), .D2_sel(store_controller_half_1_d2_sel), .in1(ALU_A_INST),
    .in2(ALU_B_INST), .in3(4'b0000), .in4(4'b0000), .out1(ROB_FL_INSTA), .out2(ROB_FL_INSTB));
  data_select_4H data_select_4h_2 (
    .D1_sel(store_controller_half_2_d1_sel), .D2_sel(store_controller_half_2_d2_sel), .in1(TRAP_INST),
    .in2(4'b0000), .in3(4'b0000), .in4(4'b0000), .out1(ROB_INT_INSTA), .out2(ROB_INT_INSTB));
  data_select_1H data_select_1h_1 (
    .D1_sel(store_controller_half_1_d1_sel), .D2_sel(store_controller_half_1_d2_sel), .in1(ALU_A_EP),
    .in2(ALU_B_EP), .in3(1'b0), .in4(1'b0), .out1(ROB_FL_EPA), .out2(ROB_FL_EPB));
  PriorityEncoder #(.Selector_Bits(4)) priorityencoder_3 (
    .in0(and_188_out[0]), .in1(and_188_out[1]), .in2(and_188_out[2]), .in3(and_188_out[3]),
    .in4(and_188_out[4]), .in5(and_188_out[5]), .in6(and_188_out[6]), .in7(and_188_out[7]),
    .in8(and_188_out[8]), .in9(and_188_out[9]), .in10(and_188_out[10]), .in11(and_188_out[11]),
    .in12(and_188_out[12]), .in13(and_188_out[13]), .in14(and_188_out[14]), .in15(and_188_out[15]),
    .num(priorityencoder_3_num), .any(priorityencoder_3_any));
  PullDown pulldown_55 (.out(CT_BLOCK));
  and and_190 (JPU_MFE, JPU_MF, JPU_BTB__ST);
  bus16_demux bus16_demux_6 (.bus(V1_inst), .E(and_189_out), .id(Fl_JPU__INST));
  bus16_demux bus16_demux_7 (.bus(V2_inst), .E(JPU_BTB__ST), .id(Fl_JPU__INST));
  not not_34 (not_34_out, BTB_override);
  and and_191 (and_191_out, FU_D__V[3], priorityencoder_3_any);
  xor xor_8 (JPU_MISS, JPU_BTB__J, JPU_JP);
  not not_35 (not_35_out, JPU_BTB__pred[0]);
  PullDown pulldown_56 (.out(kernel_inst));
  PullDown pulldown_57 (.out(CT_RF__E));
  PullDown pulldown_58 (.out(CT_RF__DM));
  PullDown #(.Bits(5)) pulldown_59 (.out(CT_RF__WS));
  PullDown #(.Bits(3)) pulldown_60 (.out(CT_RF__WM));
  PullDown #(.Bits(5)) pulldown_61 (.out(CT_RF__RA));
  PullDown #(.Bits(3)) pulldown_62 (.out(CT_RF__MA));
  PullDown #(.Bits(5)) pulldown_63 (.out(CT_RF__RB));
  PullDown #(.Bits(3)) pulldown_64 (.out(CT_RF__MB));
  PullDown pulldown_65 (.out(CT_RF__PCSE));
  PullDown pulldown_66 (.out(CT_RF__PCJ));
  PullDown pulldown_67 (.out(CT_RF__PCR));
  PullDown #(.Bits(3)) pulldown_68 (.out(CT_RF__SCN));
  PullDown pulldown_69 (.out(CT_RF__SCD));
  PullDown #(.Bits(9)) pulldown_70 (.out(CT_ALU__CT));
  PullDown pulldown_71 (.out(CT_ALU__M));
  PullDown pulldown_72 (.out(CT_ALU__M2));
  PullDown pulldown_73 (.out(CT_BUS__IAR));
  PullDown pulldown_74 (.out(CT_BUS__IAG));
  PullDown pulldown_75 (.out(CT_BUS__IDR));
  PullDown pulldown_76 (.out(CT_BUS__IDM));
  PullDown pulldown_77 (.out(CT_BUS__DAR));
  PullDown pulldown_78 (.out(CT_BUS__DAM));
  PullDown pulldown_79 (.out(CT_BUS__DAG));
  PullDown pulldown_80 (.out(CT_BUS__DDR));
  PullDown pulldown_81 (.out(CT_BUS__DDG));
  PullDown pulldown_82 (.out(I_LD));
  PullDown pulldown_83 (.out(D_LD));
  PullDown pulldown_84 (.out(D_ST));
  PullDown #(.Bits(2)) pulldown_85 (.out(D_MD));
  PullDown pulldown_86 (.out(CT_MVR));
  and and_192 (and_192_out, JPU_BTB__pred[0], JPU_BTB__pred[1]);
  and and_193 (and_193_out, JPU_BTB__pred[0], JPU_JP);
  and and_194 (and_194_out, JPU_BTB__pred[1], JPU_JP);
  and and_195 (and_195_out, not_35_out, not_34_out, JPU_BTB__pred[1]);
  and and_196 (and_196_out, not_35_out, not_34_out, JPU_JP);
  and and_197 (and_197_out, JPU_BTB__pred[1], not_34_out, JPU_JP);
  D_FF #(.Bits(4)) d_ff_36 (.D(priorityencoder_3_num), .C(C_ct), .Q(RET_INST));  // open: nQ
  D_FF d_ff_37 (.D(bitselector_1_out), .C(C_ct), .Q(RET_EPOCH));  // open: nQ
  and and_198 (and_198_out, ~and_202_out, and_191_out);  // And
  inst_comp inst_comp_11 (.A_id(RET_INST), .A_ep(RET_EPOCH), .B_id(clr_id), .B_ep(clr_ep), .A_new(inst_comp_11_a_new));
  and and_199 (and_199_out, ~and_202_out, and_191_out);  // And
  inst_comp inst_comp_12 (
    .A_id(priorityencoder_3_num), .A_ep(bitselector_1_out), .B_id(clr_id), .B_ep(clr_ep),
    .A_new(inst_comp_12_a_new));
  PullDown pulldown_87 (.out(CT_TRAP__LD));
  PullDown pulldown_88 (.out(CT_KILL));
  PullDown pulldown_89 (.out(ISS_kernel));
  data_select_4 data_select_4_1 (
    .D1_sel(store_controller_1_d1_sel), .D2_sel(store_controller_1_d2_sel), .in1(ALU_A_INST),
    .in2(ALU_B_INST), .in3(DIR_INST), .in4(LDB_B__INST), .in5(4'b0000), .in6(4'b0000), .in7(4'b0000),
    .in8(4'b0000), .out1(ROB_GEN_INSTA), .out2(ROB_GEN_INSTB));
  and and_200 (and_200_out[6], MB_free, JPU_free);
  or or_71 (JPU_pred[1], and_192_out, and_193_out, and_194_out, BTB_override);
  or or_72 (JPU_pred[0], and_195_out, and_196_out, and_197_out);
  not not_36 (JPU_free, and_198_out);
  and and_201 (and_201_out, inst_comp_11_a_new, clr);
  D_FF d_ff_38 (.D(and_199_out), .C(C_ct), .Q(d_ff_38_q));  // open: nQ
  and and_202 (and_202_out, inst_comp_12_a_new, clr);
  PullDown pulldown_90 (.out(ex_nop));
  PullDown pulldown_91 (.out(CT_ISS__HALT));
  Comparator #(.Bits(32)) comparator_22 (.a(JPU_ADDR), .b(JPU_BTB__tar), .eq(comparator_22_eq));  // open: gt, lt
  and and_203 (and_203_out, ~and_201_out, d_ff_38_q);  // And
  PullDown pulldown_92 (.out(issue));
  PullDown pulldown_93 (.out(CT_ISS__URA));
  PullDown pulldown_94 (.out(CT_ISS__URB));
  PullDown #(.Bits(5)) pulldown_95 (.out(CT_ISS__RA));
  PullDown #(.Bits(5)) pulldown_96 (.out(CT_ISS__RB));
  PullDown pulldown_97 (.out(CT_ISS__UMM));
  PullDown pulldown_98 (.out(CT_ISS__UFL));
  PullDown pulldown_99 (.out(CT_ISS__ORC));
  PullDown #(.Bits(5)) pulldown_100 (.out(CT_ISS__RC));
  PullDown pulldown_101 (.out(CT_ISS__OSC));
  PullDown pulldown_102 (.out(CT_ISS__OFL));
  PullDown pulldown_103 (.out(CT_ROB__EX__E));
  PullDown pulldown_104 (.out(CT_ROB__ST__E));
  PullDown #(.Bits(3)) pulldown_105 (.out(CT_SP__MOF));
  PullDown pulldown_106 (.out(CT_BUS__DDM));
  PullDown pulldown_107 (.out(CT_RF__PCH));
  PullDown pulldown_108 (.out(\wait ));
  nand nand_12 (nand_12_out, JPU_BTB__V, comparator_22_eq);
  and and_204 (and_204_out, JPU_MISS, JPU_BTB__V, comparator_22_eq);
  and and_205 (Fl_JPU, or_73_out, JPU_BTB__ST);
  Comparator #(.Bits(3)) comparator_23 (
    .a(store_controller_1_d1_sel), .b(3'b010), .eq(comparator_23_eq));  // open: gt, lt
  Comparator #(.Bits(3)) comparator_24 (
    .a(store_controller_1_d2_sel), .b(3'b010), .eq(comparator_24_eq));  // open: gt, lt
  D_FF #(.Bits(8)) d_ff_39 (
    .D({JPU_free, and_200_out[6], 1'b0, TRAP_free, MB_free, DIR_free, ALU_free, 1'b1}), .C(C_ct), .Q(FU_free));  // open: nQ
  assign CT_JPU__LD = and_203_out ? 1'b1 : 1'bz;  // Driver driver_224
  assign JPU_RET = and_203_out ? 1'b1 : 1'bz;  // Driver driver_225
  and and_206 (ROB_GEN_EX1, comparator_23_eq, DIR_EX);
  and and_207 (ROB_GEN_EX2, comparator_24_eq, DIR_EX);
  and and_208 (BTB_override, JPU_JP, nand_12_out);
  and and_209 (and_209_out, nand_12_out, JPU_BTB__J);
  or or_73 (or_73_out, and_204_out, and_209_out, BTB_override);
  assign CT_RF__PCSE = Fl_JPU ? 1'b1 : 1'bz;  // Driver driver_226
  assign CT_RF__PCJ = Fl_JPU ? 1'b1 : 1'bz;  // Driver driver_227
  assign CT_JMP = Fl_JPU ? 1'b1 : 1'bz;  // Driver driver_228
  PullDown pulldown_109 (.out(CT_RF__SCSRE));
  PullDown pulldown_110 (.out(CT_RF__SCSE));
  PullDown pulldown_111 (.out(CT_RF__SCSS));
  PullDown pulldown_112 (.out(CT_JPU__JP));
  PullDown pulldown_113 (.out(JPU_A__ST));
  PullDown pulldown_114 (.out(CT_MB__OFFM));
  PullDown pulldown_115 (.out(JPU_BTB__ST));
  PullDown pulldown_116 (.out(CT_JPU__LD));
  PullDown pulldown_117 (.out(CT_JMP));
  PullDown pulldown_118 (.out(CT_FU__MF));
  PullDown pulldown_119 (.out(CT_CALL__LD));
  PullDown pulldown_120 (.out(CT_RET__LD));
  PullDown pulldown_121 (.out(JPU_RET));
  PullDown pulldown_122 (.out(JPU_free));
  PullDown pulldown_123 (.out(JPU_CALL));
  PullDown pulldown_124 (.out(CT_CALLM));

  assign CSH_mode = 2'b00;
  assign CSH_run = 1'b0;
  assign INT_str = 1'b0;
  assign MMU_base = {32{1'b0}};
  assign MMU_dis = 1'b0;
  assign MMU_en = 1'b0;

  // Other names for the same wires on the sheet: disp_32[31:0] = {byte_D0, byte_D1, byte_D2, byte_D3};
  //   imm16_2[15:0] = {byte_D2, byte_D3}; FU_CLR[2:0] = {DIR_CLR, ALU_B_CLR, ALU_A_CLR}; ALU_A_WR[2:0] = ALU_A_RM;
  //   ALU_B_WR[2:0] = ALU_B_RM; BTB_packet[2] = BTB_JP; BTB_pred[1:0] = BTB_packet[4:3];
  //   BTB_tar[31:0] = BTB_packet[36:5]; BTB_V = BTB_packet[1]; C_i = C_dt; C_t = C_dt; Fl_INT__EP = com1_ep;
  //   Fl_INT__INST[3:0] = com1_inst; CT_RF__SCAS = CT_RF__SCAE; fl_i[8] = FL[14]; int_proc = FL[14]; trap = FL[15];
  //   FU_D__V[2:0] = {DIR_V, ALU_B_VD, ALU_A_VD}; LDB_B__V = FU_D__V[3]; FU_F__V[1:0] = {ALU_B_VF, ALU_A_VF};
  //   TRAP_VI = FU_I__V[0]; INT_ISS = INT_acp; issue_32[31:0] = {byte_I0, byte_I1, byte_I2, byte_I3};
  //   JPU_BTBPK[36:1] = {JPU_BTB__tar, JPU_BTB__pred, JPU_BTB__J, JPU_BTB__V}; JPU_EN = JPU_BTB__ST;
  //   JPU_ST = JPU_BTB__ST; run_int = Fl_INT; scs_i[31:0] = ISC_sc; TRAP_CLR = FU_CLR[4]

  // Notes on the sheet:
  //   D_MD: 0:32
  //   1:16
  //   2:8
  //   3:u.u
  //   D_accept: default 1
  //   C: Hz: 50000
  //   tests
  //   contents of rom_1 (hex, n*v repeats v):
  //   39,38,38,37,a,38,37,35,36,a
  //   decode circuit
  //   IO pins
  //   primeary signals
  //   pipeline controller
  //   kernal mode system
  //   interrupt system
  //   ext system
  //   syscall
  //   iret
  //   inst id manager
  //   interrupt commit
  //   ALU
  //   register
  //   stack
  //   RAM
  //   register system
  //   ROB
  //   program counter controller
  //   bus system
  //   data bus ctrl
  //   trap
  //   jump
  //   call
  //   return
  //   wait/halt
  //   block
  //   exld/st
  //   stack circuit
  //   ALU system
  //   dir circuit
  //   load/store circuit
  //   issue circuit
  //   flag circuit
  //   FU aribiter
  //   jmp circuit
  //   return unit
  //   control bus
endmodule
