// Digital circuit cpu-32.dig as structural Verilog
module cpu_32 (
  input  E,
  input  [31:0] I_D__bus,
  input  [31:0] D_D__bus,
  input  [31:0] I_A__bus,
  input  [31:0] D_A__bus,
  input  run,
  input  I_valid,
  input  D_accept,
  input  C,
  input  B_used,
  input  boot,
  input  [31:0] reset_vec,
  input  INT_in,
  input  [3:0] INT_lev,
  input  [31:0] INT_vec,
  input  INT_rqac,
  input  [31:0] MMU_abs,
  input  [5:0] INT_id__bus,
  input  [31:0] INT_d__bus,
  input  INT_ker,
  output I_LD,
  output D_LD,
  output D_ST,
  output [1:0] D_MD,
  output INT_acp,
  output INT_req,
  output MMU_dis,
  output MMU_en,
  output [1:0] CSH_mode,
  output CSH_run,
  output [31:0] MMU_base,
  output [31:0] MMU_limit,
  output INT_pstr,
  output INT_vstr,
  output INT_ret
);

  wire ALU_A_CLR, ALU_A_CMP, ALU_A_DRD, ALU_A_DRE, ALU_A_FRD, ALU_A_FRE, ALU_A_LD, ALU_A_LRD, ALU_A_STD,
       ALU_A_STF, ALU_A_UUD, ALU_A_UUF, ALU_A_V, ALU_A_VD, ALU_A_VF, ALU_B_CLR, ALU_B_CMP, ALU_B_DRD,
       ALU_B_DRE, ALU_B_FRD, ALU_B_FRE, ALU_B_LD, ALU_B_LRD, ALU_B_STD, ALU_B_STF, ALU_B_UUD, ALU_B_UUF,
       ALU_B_V, ALU_B_VD, ALU_B_VF, ALU_busy, ALU_free, and_1_out, and_3_out, and_5_out, and_6_out,
       and_7_out, and_9_out, and_10_out, and_11_out, and_13_out, and_15_out, and_19_out, and_20_out,
       and_21_out, and_25_out, and_26_out, and_27_out, and_28_out, and_29_out, and_31_out, and_32_out,
       and_33_out, and_34_out, and_35_out, and_36_out, and_37_out, and_38_out, and_39_out, and_40_out,
       and_41_out, and_42_out, and_43_out, and_44_out, and_45_out, and_48_out, and_49_out, and_52_out,
       and_53_out, and_54_out, and_55_out, and_56_out, and_57_out, and_58_out, and_59_out, and_60_out,
       and_61_out, and_62_out, and_63_out, and_65_out, and_66_out, and_67_out, and_68_out, and_72_out,
       and_73_out, and_76_out, and_77_out, and_78_out, and_79_out, and_80_out, and_81_out, and_82_out,
       and_83_out, and_84_out, and_85_out, and_86_out, and_87_out, and_89_out, and_90_out, and_93_out,
       and_94_out, and_99_out, and_105_out, and_106_out, and_107_out, and_108_out, and_109_out, and_110_out,
       and_111_out, and_112_out, and_113_out, and_114_out, and_115_out, and_116_out, and_117_out,
       and_120_out, and_122_out, and_123_out, and_128_out, and_129_out, and_130_out, and_131_out,
       and_134_out, and_135_out, and_136_out, and_137_out, and_139_out, and_140_out, and_141_out,
       and_142_out, and_144_out, and_145_out, and_146_out, and_147_out, and_148_out, and_149_out,
       and_150_out, and_152_out, and_153_out, and_158_out, and_159_out, and_162_out, and_163_out,
       and_164_out, and_165_out, and_166_out, and_167_out, and_168_out, and_169_out, and_170_out,
       and_174_out, and_179_out, and_181_out, and_182_out, and_183_out, and_184_out, and_185_out,
       and_186_out, and_187_out, and_188_out, and_189_out, and_191_out, and_192_out, and_193_out,
       and_194_out, and_199_out, bitselector_1_out, boot_t, BTB_JP, BTB_override, BUS_INSTV, C_ct, clr,
       clr_ep, clr_self, com1, com1_ep, com2, com2_ep, comparator_1_gt, comparator_2_gt, comparator_3_eq,
       comparator_4_eq, comparator_5_eq, comparator_6_gt, comparator_6_lt, comparator_7_eq, comparator_8_eq,
       comparator_9_eq, comparator_10_eq, CT_ALU__LD, CT_ALU__M, CT_ALU__M2, CT_ALU__WD, CT_ALU__WF,
       CT_BLOCK, CT_BUS__DAG, CT_BUS__DAM, CT_BUS__DAR, CT_BUS__DDG, CT_BUS__DDM, CT_BUS__DDR, CT_BUS__IAG,
       CT_BUS__IAR, CT_BUS__IDM, CT_BUS__IDR, CT_CALL__LD, CT_CALLM, CT_DIR__EXM, CT_DIR__LD, CT_DIR__M,
       CT_DIR__MS, CT_DISP, CT_FL__W1, CT_FL__W2, CT_FU__EPOCH, CT_FU__EX, CT_FU__MF, CT_ILVE, CT_ILVSM,
       CT_INT, CT_INT__W, CT_INTM, CT_ISCE, CT_ISCM, CT_ISCS, CT_ISS__HALT, CT_ISS__OFL, CT_ISS__OLDB,
       CT_ISS__ORC, CT_ISS__OSC, CT_ISS__OSTB, CT_ISS__UFL, CT_ISS__UMM, CT_ISS__URA, CT_ISS__URB, CT_JMP,
       CT_JPU__JP, CT_JPU__LD, CT_KILL, CT_LDB__LD, CT_MB__LD, CT_MB__OFFM, CT_MB__ST, CT_MVR, CT_PVECE,
       CT_RET__LD, CT_RF__DM, CT_RF__E, CT_RF__EX1, CT_RF__EX2, CT_RF__FLS, CT_RF__PCAE, CT_RF__PCH,
       CT_RF__PCJ, CT_RF__PCR, CT_RF__PCSE, CT_RF__SCAE, CT_RF__SCD, CT_RF__SCSE, CT_RF__SCSRE, CT_RF__SCSS,
       CT_RF__W1, CT_RF__W2, CT_ROB__EX__E, CT_ROB__FL__STA, CT_ROB__FL__STB, CT_ROB__GEN__STA,
       CT_ROB__GEN__STB, CT_ROB__INT__STA, CT_ROB__INT__STB, CT_ROB__ST__E, CT_SC__W1, CT_SC__W2, CT_STB__LD,
       CT_TRAP__LD, CT_UBTB, CT_USCB, d_ff_1_q, d_ff_3_q, d_ff_7_q, d_ff_9_nq, d_ff_11_q, d_ff_12_q,
       d_ff_13_q, d_ff_32_q, d_ff_33_nq, d_ff_38_q, dc_e, DC_q, dipswitch_1_out, dipswitch_2_out, DIR_busy,
       DIR_CLR, DIR_EX, DIR_free, DIR_LD, DIR_RD, DIR_ST, DIR_V, epoch_DP, epoch_IS, ex_nop, ext_en, Fl_ECLR,
       Fl_INT, Fl_JPU, Fl_JPU__EP, Fl_MEM, FL_MEM__EP, ft_e, FT_q, halt_FT_DC_ISS, halted, hlt, id_full,
       id_manager_1_eclr_ep, id_manager_1_v, inst_comp_1_a_new, inst_comp_2_a_new, inst_comp_3_a_new,
       inst_comp_4_a_new, inst_comp_5_a_new, inst_comp_7_a_new, inst_comp_9_a_new, inst_comp_10_a_new,
       inst_sfcomp_1_a_new, inst_sfcomp_2_a_new, int_accept, int_enable, int_epoch, INT_HALT, ISS_kernel,
       ISS_q, issue, issue_e, JPU_A__ST, JPU_BTB__J, JPU_BTB__ST, JPU_BTB__V, JPU_CALL, JPU_free, JPU_INT,
       JPU_JP, JPU_LD, JPU_MF, JPU_MFE, JPU_MISS, JPU_RET, kernel_inst, LDB_B__MF, LDB_B__RD, LDB_B__ST,
       LDB_busy, LDB_forward, LDB_ldV, LDB_M__EP, LDB_M__V, load_buffer_1_fl, load_buffer_1_fl_ep,
       load_buffer_1_full, load_buffer_1_mf_o, load_buffer_1_v, MB_busy, MB_ep, MB_free, MB_LD, MB_ld__e,
       MB_LDB__LD, MB_MF, MB_MFE, MB_st__e, MB_STB__LD, MB_type__st, MEM_AC, MEM_BF__free, MEM_CLR, MEM_EP,
       MEM_LD, MEM_LD__CLR, MEM_LD__EP, MEM_LD__RD, MEM_LD__REC, MEM_RD, MEM_TYPE__ST, mode,
       multiplexer_7_out, multiplexer_9_out, multiplexer_16_out, multiplexer_18_out, multiplexer_22_out,
       multiplexer_23_out, multiplexer_25_out, multiplexer_26_out, multiplexer_27_out, multiplexer_33_out,
       multiplexer_39_out, multiplexer_40_out, multiplexer_41_out, multiplexer_49_out, multiplexer_52_out,
       multiplexer_54_out, multiplexer_55_out, multiplexer_56_out, multiplexer_57_out, multiplexer_60_out,
       multiplexer_63_out, multiplexer_64_out, multiplexer_65_out, multiplexer_72_out, nand_11_out,
       nand_12_out, nor_1_out, nor_2_out, nor_3_out, nor_4_out, nor_7_out, nor_8_out, nor_10_out, nor_11_out,
       not_2_out, not_6_out, not_7_out, not_9_out, not_10_out, not_11_out, not_12_out, not_13_out,
       not_14_out, not_16_out, not_17_out, not_19_out, not_20_out, not_22_out, not_23_out, not_24_out,
       not_27_out, not_29_out, not_33_out, not_34_out, not_35_out, or_1_out, or_2_out, or_4_out, or_5_out,
       or_6_out, or_7_out, or_9_out, or_10_out, or_11_out, or_12_out, or_13_out, or_14_out, or_23_out,
       or_24_out, or_25_out, or_27_out, or_28_out, or_29_out, or_32_out, or_34_out, or_35_out, or_36_out,
       or_37_out, or_38_out, or_41_out, or_42_out, or_43_out, or_46_out, or_47_out, or_48_out, or_49_out,
       or_50_out, or_52_out, or_53_out, or_54_out, or_55_out, or_56_out, or_57_out, or_58_out, or_59_out,
       or_60_out, or_61_out, or_63_out, or_65_out, or_66_out, or_67_out, or_71_out, or_72_out, or_75_out,
       PCA, priorityencoder_3_any, register_12_q, register_25_q, register_26_q, register_27_q, register_34_q,
       register_35_q, register_36_q, register_43_q, register_46_q, register_49_q, register_61_q,
       register_68_q, register_71_q, register_74_q, register_79_q, RET_EPOCH, ROB_GEN_DA, ROB_GEN_DB,
       ROB_GEN_EX1, ROB_GEN_EX2, rs_ff_1_nq, rs_ff_3_q, rs_ff_5_nq, rs_ff_5_q, rs_ff_6_q, rs_ff_7_nq,
       rs_ff_7_q, rs_ff_8_nq, rs_ff_9_nq, rs_ff_10_nq, rs_ff_11_nq, rs_ff_12_nq, rs_ff_17_q, rs_ff_18_q,
       rs_ff_19_q, rs_ff_20_q, rs_ff_23_nq, RS_full, RX_ILVE, RX_ILVM, RX_ISCE, RX_ISCM, RX_PGBSE, RX_PGLME,
       RX_PGLMM, RX_PVECE, RX_PVECM, STB_busy, STB_M__EP, STB_M__V, store_buffer_1_full, TRAP_busy, TRAP_EP,
       TRAP_free, TRAP_IRD, TRAP_RD, TRAP_ST, undriven, V_q, \wait , waiting, xor_1_out;
  wire [0:0] and_88_out, JPU_BTBPK;
  wire [1:0] and_101_out, and_103_out, and_118_out, and_119_out, bitextender_6_out, bitextender_7_out,
       d_ff_14_q, d_ff_19_q, d_ff_20_q, d_ff_21_q, d_ff_22_q, JPU_BTB__pred, JPU_pred, LDB_M__MD, MB_MD,
       multiplexer_11_out, priorityencoder_1_num, priorityencoder_2_num, register_17_q, STB_M__MD,
       store_controller_half_1_d1_sel, store_controller_half_1_d2_sel, store_controller_half_2_d1_sel,
       store_controller_half_2_d2_sel;
  wire [1:1] or_26_out, register_47_q, register_72_q;
  wire [2:0] ALU_A_RM, ALU_B_RM, and_91_out, and_95_out, CT_ISS__UFU, CT_RF__MA, CT_RF__MB, CT_RF__SCN,
       CT_RF__WM, CT_SP__MOF, multiplexer_15_out, multiplexer_19_out, multiplexer_47_out, nand_1_out,
       nand_2_out, nand_4_out, nand_8_out, not_18_out, not_21_out, register_23_q, register_48_q,
       store_controller_1_d1_sel, store_controller_1_d2_sel;
  wire [2:1] nor_5_out;
  wire [3:0] ALU_A_INST, ALU_B_INST, clr_id, clr_sel, com1_inst, com2_inst, CT_FU__INST, d_ff_2_q, DIR_INST,
       Fl_JPU__INST, FL_MEM__ID, FU_I__V, id_manager_1_eclr_id, inst_DP, inst_IS, int_inst_t, LD_id,
       LDB_B__INST, LDB_M__ID, load_buffer_1_fl_id, load_buffer_1_id_o, MB_INST, MEM_INST, MEM_LD__INST,
       multiplexer_24_out, multiplexer_38_out, multiplexer_48_out, multiplexer_59_out, multiplexer_67_out,
       multiplexer_71_out, priorityencoder_3_num, register_24_q, register_33_q, register_42_q, register_67_q,
       RET_INST, ROB_FL_INSTA, ROB_FL_INSTB, ROB_GEN_INSTA, ROB_GEN_INSTB, ROB_INT_INSTA, ROB_INT_INSTB,
       STB_M__ID, TRAP_INST;
  wire [3:2] FU_F__V;
  wire [4:0] CT_ISS__RA, CT_ISS__RB, CT_ISS__RC, CT_RF__RA, CT_RF__RB, CT_RF__WS, ILV, ILV_i,
       multiplexer_2_out;
  wire [4:4] FU_CLR;
  wire [5:0] CT_INT__D, INT_rid__bus, ROB_INT_A, ROB_INT_B, TRAP_INT;
  wire [6:6] and_190_out;
  wire [7:0] ALU_A_F, ALU_A_FI, ALU_A_T__F, ALU_B_F, ALU_B_FI, ALU_B_T__F, bitextender_3_out, byte_D0,
       byte_D0_iv, byte_D1, byte_D2, byte_D3, byte_I0, byte_I0_iv, byte_I1, byte_I2, byte_I3, CT_DIR__EXID,
       CT_FL__D1, CT_FL__D2, CT_FU__WR, CT_INTID, CT_RF__R1, CT_RF__R2, demultiplexer_1_out_0,
       demultiplexer_2_out_0, DIR_WR, fl_i, FU_free, LDB_B__WR, load_buffer_1_wr_o, MB_WR,
       multiplexer_30_out, multiplexer_32_out, multiplexer_44_out, multiplexer_46_out, multiplexer_51_out,
       multiplexer_62_out, or_3_out, register_30_q, register_32_q, register_39_q, register_41_q,
       register_45_q, register_70_q, ROB_FL_A, ROB_FL_B, ROB_GEN_WA, ROB_GEN_WB, xor_2_out;
  wire [7:3] ALU_A_WR, ALU_B_WR, FU_D__V;
  wire [7:6] register_10_q;
  wire [8:0] ALU_A_CT, ALU_B_CT, CT_ALU__CT, multiplexer_31_out, multiplexer_45_out, register_31_q,
       register_40_q;
  wire [9:0] and_30_out;
  wire [15:0] and_171_out, and_173_out, and_175_out, and_176_out, and_178_out, bitextender_4_out,
       bitextender_5_out, bitextender_8_out, bitextender_10_out, bitextender_11_out, clr_16, clrs_16,
       d_ff_35_q, demultiplexer_3_out_0, demultiplexer_4_out_0, icmk_16, icmks_16, INT_inst,
       multiplexer_37_out, multiplexer_75_out, not_31_out, not_32_out, or_68_out, or_69_out, or_70_out,
       register_55_q, register_93_q, register_97_q, register_98_q, V1_inst, V2_inst;
  wire [31:0] add_1_s, add_4c32_1_s, add_4c32_2_s, ALU_A_A, ALU_A_B, ALU_A_R, ALU_A_T__R, ALU_B_A, ALU_B_B,
       ALU_B_R, ALU_B_T__R, bitextender_1_out, bitextender_2_out, CT_RF__D1, CT_RF__D2, CT_RF__DR, CT_SC__D1,
       CT_SC__D2, CT_SC__FD, d_ff_34_q, DIR, FL, HALT_PC, I_A__R_q, I_D__R_q, int_pc, int_vec_t, ISC, ISC_i,
       ISC_sc, JPU_ADDR, JPU_BTB__tar, JPU_PC, LD_addr, LDB_B__D, LDB_ldD, LDB_M__A, load_buffer_1_fl_pc,
       MB_addr, MB_data, MB_PC, MEM_FPC, MEM_LD__D, multiplexer_1_out, multiplexer_3_out, multiplexer_8_out,
       multiplexer_10_out, multiplexer_12_out, multiplexer_17_out, multiplexer_20_out, multiplexer_21_out,
       multiplexer_28_out, multiplexer_29_out, multiplexer_34_out, multiplexer_35_out, multiplexer_36_out,
       multiplexer_42_out, multiplexer_43_out, multiplexer_50_out, multiplexer_53_out, multiplexer_58_out,
       multiplexer_61_out, multiplexer_66_out, multiplexer_69_out, multiplexer_70_out, multiplexer_73_out,
       multiplexer_74_out, mVec, pc_read, pc_ret, pca_i, PCS, PCS_DC, PCS_FT, pcs_i, pulldown_18_out,
       pulldown_19_out, PVEC, PVEC_i, R_A, R_B, register_11_q, register_16_q, register_18_q, register_28_q,
       register_29_q, register_37_q, register_38_q, register_44_q, register_54_q, register_69_q,
       register_92_q, RX_SEL, SCA, sca_i, SCS, STB_M__A, STB_M__D;
  wire [36:0] and_172_out, bitextender_9_out, BTB_D_q, BTB_DP, BTB_fetch, BTB_pack__iss, BTB_packet;

  not not_1 (C_ct, C);
  not not_2 (not_2_out, I_valid);
  assign CT_BUS__IDM = not_2_out ? 1'b1 : 1'bz;  // Driver driver_1
  and and_1 (and_1_out, I_valid, ft_e);
  assign CT_RF__PCSE = and_1_out ? 1'b1 : 1'bz;  // Driver driver_2
  assign CT_BUS__IAR = and_1_out ? 1'b1 : 1'bz;  // Driver driver_3
  assign CT_BUS__IAG = ft_e ? 1'b1 : 1'bz;  // Driver driver_4
  assign I_LD = ft_e ? 1'b1 : 1'bz;  // Driver driver_5
  or or_1 (or_1_out, issue, INT_acp);
  Comparator #(.Bits(32)) comparator_1 (.a(PCS), .b(mVec), .gt(comparator_1_gt));  // open: eq, lt
  BitExtender #(.inputBits(16), .outputBits(32)) bitextender_1 (.in({byte_D2, byte_D3}), .out(bitextender_1_out));
  RS_FF rs_ff_1 (.S(Fl_INT), .C(C_ct), .R(CT_INTM), .nQ(rs_ff_1_nq));  // open: Q
  and and_2 (Fl_INT, rs_ff_1_nq, int_accept);
  PullDown pulldown_1 (.out(CT_ISCS));
  PullDown pulldown_2 (.out(CT_ISCM));
  PullDown pulldown_3 (.out(CT_ISCE));
  PullDown pulldown_4 (.out(CT_ILVE));
  or or_2 (or_2_out, halted, waiting);
  D_FF d_ff_1 (.D(INT_in), .C(C), .Q(d_ff_1_q));  // open: nQ
  D_FF #(.Bits(4)) d_ff_2 (.D(INT_lev), .C(C), .Q(d_ff_2_q));  // open: nQ
  D_FF d_ff_3 (.D(INT_in), .C(C), .Q(d_ff_3_q));  // open: nQ
  Register #(.Bits(5)) level (.D(ILV_i), .C(C), .en(CT_ILVE), .Q(ILV));
  Register #(.Bits(32)) register_1 (.D(ISC_i), .C(C), .en(CT_ISCE), .Q(ISC));
  Register #(.Bits(32)) register_2 (.D(INT_vec), .C(C), .en(int_enable), .Q(int_vec_t));
  and and_3 (and_3_out, nor_1_out, CT_RF__W1, CT_RF__EX1);
  id_manager id_manager_1 (
    .C(C_ct), .\use (or_1_out), .S1_inst(V1_inst), .S2_inst(V2_inst), .E_inst(INT_inst), .clr(clr),
    .clr_self(clr_self), .clr_ep(clr_ep), .clr_id(clr_id), .epoch(epoch_IS), .id(inst_IS),
    .V(id_manager_1_v), .com1(com1), .com1_id(com1_inst), .com1_ep(com1_ep), .com2(com2),
    .com2_id(com2_inst), .com2_ep(com2_ep), .ext_en(ext_en), .cmk_16(icmk_16), .clr_16(clr_16),
    .cmks_16(icmks_16), .clrs_16(clrs_16), .eclr_v(Fl_ECLR), .eclr_id(id_manager_1_eclr_id),
    .eclr_ep(id_manager_1_eclr_ep), .eclr(undriven));
  flush_mux flush_mux_1 (
    .M_v(Fl_MEM), .M_id(FL_MEM__ID), .M_ep(FL_MEM__EP), .J_v(Fl_JPU), .J_id(Fl_JPU__INST), .J_ep(Fl_JPU__EP),
    .I_v(Fl_INT), .I_id(com2_inst), .I_ep(com2_ep), .sel(clr_sel), .self(clr_self), .m_v_2(clr),
    .m_id_2(clr_id), .m_ep_2(clr_ep), .E_v(Fl_ECLR), .E_id(id_manager_1_eclr_id), .E_ep(id_manager_1_eclr_ep));
  Add #(.Bits(32)) add_1 (.a(R_A), .b(bitextender_1_out), .c_i(1'b0), .s(add_1_s));  // open: c_o
  // And and_4 has open pins: In_1=or_2_out, In_2=INT_in, out=open
  D_FF d_ff_4 (.D(d_ff_3_q), .C(C_ct), .Q(int_enable));  // open: nQ
  D_FF d_ff_5 (.D(CT_INT__W), .C(C), .Q(INT_req));  // open: nQ
  D_FF #(.Bits(6)) d_ff_6 (.D(CT_INT__D), .C(C), .Q(INT_rid__bus));  // open: nQ
  Demultiplexer #(.Selector_Bits(3)) demultiplexer_1 (
    .sel(CT_RF__R1[2:0]), .in(and_3_out), .out_0(demultiplexer_1_out_0[0]), .out_1(demultiplexer_1_out_0[1]),
    .out_2(demultiplexer_1_out_0[2]), .out_3(demultiplexer_1_out_0[3]), .out_4(demultiplexer_1_out_0[4]),
    .out_5(demultiplexer_1_out_0[5]), .out_6(demultiplexer_1_out_0[6]), .out_7(demultiplexer_1_out_0[7]));
  and and_5 (and_5_out, 1'b0, ~comparator_1_gt);  // And
  Comparator #(.Bits(5)) comparator_2 (.a({1'b0, d_ff_2_q}), .b(ILV), .gt(comparator_2_gt));  // open: eq, lt
  nor nor_1 (nor_1_out, CT_RF__R1[7], CT_RF__R1[6], CT_RF__R1[5], CT_RF__R1[4], CT_RF__R1[3]);
  not not_3 (id_full, id_manager_1_v);
  RS_FF u_mode (.S(and_5_out), .C(C), .R(comparator_1_gt), .Q(mode));  // open: nQ
  Register #(.Bits(32)) MVR (.D(add_1_s), .C(C), .en(CT_MVR), .Q(mVec));
  RS_FF rs_ff_2 (.S(Fl_INT), .C(C_ct), .R(INT_acp), .Q(INT_HALT));  // open: nQ
  RS_FF rs_ff_3 (.S(Fl_INT), .C(C_ct), .R(INT_acp), .Q(rs_ff_3_q));  // open: nQ
  Comparator #(.Bits(4)) comparator_3 (.a(inst_IS), .b(com1_inst), .eq(comparator_3_eq));  // open: gt, lt
  assign CT_JPU__LD = INT_acp ? 1'b1 : 1'bz;  // Driver driver_6
  assign JPU_INT = INT_acp ? 1'b1 : 1'bz;  // Driver driver_7
  assign CT_ISS__OSTB = INT_acp ? 1'b1 : 1'bz;  // Driver driver_8
  and and_6 (and_6_out, d_ff_1_q, comparator_2_gt);
  Register #(.Bits(32)) register_3 (.D(pca_i), .C(C), .en(INT_acp), .Q(int_pc));
  Register #(.Bits(4)) register_4 (.D(inst_IS), .C(C_ct), .en(INT_acp), .Q(int_inst_t));
  Register register_5 (.D(epoch_IS), .C(C_ct), .en(INT_acp), .Q(int_epoch));
  assign {or_3_out[7:6], RX_PGLME, RX_PGBSE, RX_ILVE, RX_ISCE, RX_PVECE, or_3_out[0]} = {demultiplexer_2_out_0[7:5], RX_PGLMM, RX_ILVM, RX_ISCM, RX_PVECM, demultiplexer_2_out_0[0]} | demultiplexer_1_out_0;  // Or or_3, 8 bits wide
  assign byte_I0_iv = ~byte_I0;  // Not not_4, 8 bits wide
  assign byte_D0_iv = ~byte_D0;  // Not not_5, 8 bits wide
  or or_4 (or_4_out, clr, \wait );
  or or_5 (or_5_out, run, Fl_INT);
  D_FF d_ff_7 (.D(boot), .C(C), .Q(d_ff_7_q));  // open: nQ
  PullDown pulldown_5 (.out(JPU_INT));
  PullDown pulldown_6 (.out(CT_ILVSM));
  D_FF d_ff_8 (.D(and_6_out), .C(C_ct), .Q(int_accept));  // open: nQ
  and and_7 (and_7_out, nor_2_out, CT_RF__W2, CT_RF__EX2);
  RS_FF FT (.S(or_5_out), .C(C_ct), .R(\wait ), .Q(FT_q), .nQ(waiting));
  not not_6 (not_6_out, halt_FT_DC_ISS);
  D_FF d_ff_9 (.D(d_ff_7_q), .C(C), .nQ(d_ff_9_nq));  // open: Q
  and and_8 (INT_acp, rs_ff_3_q, comparator_3_eq, ~STB_busy);  // And
  nor nor_2 (nor_2_out, CT_RF__R2[7], CT_RF__R2[6], CT_RF__R2[5], CT_RF__R2[4], CT_RF__R2[3]);
  Demultiplexer #(.Selector_Bits(3)) demultiplexer_2 (
    .sel(CT_RF__R2[2:0]), .in(and_7_out), .out_0(demultiplexer_2_out_0[0]), .out_1(RX_PVECM),
    .out_2(RX_ISCM), .out_3(RX_ILVM), .out_4(RX_PGLMM), .out_5(demultiplexer_2_out_0[5]),
    .out_6(demultiplexer_2_out_0[6]), .out_7(demultiplexer_2_out_0[7]));
  and and_9 (and_9_out, byte_D0_iv[0], byte_D0[1], byte_D0[2], byte_D0_iv[3], byte_D0[4], byte_D0[5], byte_D0[6], byte_D0_iv[7], CT_DISP);
  and and_10 (and_10_out, byte_D0[0], byte_D0[1], byte_D0[2], byte_D0_iv[3], byte_D0[4], byte_D0[5], byte_D0[6], byte_D0_iv[7], CT_DISP);
  and and_11 (and_11_out, byte_D0_iv[1], byte_D0_iv[2], byte_D0[3], byte_D0[4], byte_D0[5], byte_D0[6], byte_D0_iv[7], CT_DISP);
  not not_7 (not_7_out, or_4_out);
  and and_12 (boot_t, d_ff_7_q, d_ff_9_nq);
  D_FF d_ff_10 (.D(INT_acp), .C(C_ct), .Q(CT_INTM));  // open: nQ
  and and_13 (and_13_out, not_7_out, FT_q);
  Register DC (.D(and_13_out), .C(C_ct), .en(or_6_out), .Q(DC_q));
  and and_14 (ft_e, FT_q, not_6_out);
  or or_6 (or_6_out, not_6_out, or_4_out);
  Register #(.Bits(32)) register_6 (.D(PCS), .C(C), .en(CT_RF__PCSE), .Q(PCS_FT));
  assign CT_RF__PCSE = boot_t ? 1'b1 : 1'bz;  // Driver driver_9
  DipSwitch dipswitch_1 (.out(dipswitch_1_out));
  assign CT_MB__LD = CT_INTM ? 1'b1 : 1'bz;  // Driver driver_10
  assign CT_MB__OFFM = CT_INTM ? 1'b1 : 1'bz;  // Driver driver_11
  assign CT_MB__ST = CT_INTM ? 1'b1 : 1'bz;  // Driver driver_12
  assign CT_FU__INST = CT_INTM ? int_inst_t : 4'bz;  // Driver driver_13
  assign CT_FU__EPOCH = CT_INTM ? int_epoch : 1'bz;  // Driver driver_14
  Multiplexer #(.Bits(32)) multiplexer_1 (.sel(RX_ISCM), .in_0(CT_RF__D1), .in_1(CT_RF__D2), .out(multiplexer_1_out));
  Multiplexer #(.Bits(5)) multiplexer_2 (
    .sel(RX_ILVM), .in_0(CT_RF__D1[4:0]), .in_1(CT_RF__D2[4:0]), .out(multiplexer_2_out));
  PullDown pulldown_7 (.out(CT_PVECE));
  Register #(.Bits(32)) u_PVEC (.D(PVEC_i), .C(C), .en(CT_PVECE), .Q(PVEC));
  assign CT_FU__EPOCH = and_9_out ? epoch_DP : 1'bz;  // Driver driver_15
  assign CT_FU__INST = and_9_out ? inst_DP : 4'bz;  // Driver driver_16
  assign CT_TRAP__LD = and_9_out ? 1'b1 : 1'bz;  // Driver driver_17
  assign CT_INT = and_9_out ? 1'b1 : 1'bz;  // Driver driver_18
  assign CT_INTID = and_9_out ? byte_D3 : 8'bz;  // Driver driver_19
  assign CT_FU__EPOCH = and_10_out ? epoch_DP : 1'bz;  // Driver driver_20
  assign CT_FU__INST = and_10_out ? inst_DP : 4'bz;  // Driver driver_21
  assign CT_TRAP__LD = and_10_out ? 1'b1 : 1'bz;  // Driver driver_22
  assign CT_BLOCK = and_11_out ? 1'b1 : 1'bz;  // Driver driver_23
  assign issue = and_11_out ? 1'b1 : 1'bz;  // Driver driver_24
  assign CT_ISS__HALT = and_11_out ? 1'b1 : 1'bz;  // Driver driver_25
  assign CT_ISS__UMM = and_11_out ? 1'b1 : 1'bz;  // Driver driver_26
  assign CT_ISS__UFU = and_11_out ? 3'b100 : 3'bz;  // Driver driver_27
  and and_15 (and_15_out, not_7_out, DC_q);
  Register ISS (.D(and_15_out), .C(C_ct), .en(or_7_out), .Q(ISS_q));
  and and_16 (dc_e, DC_q, not_6_out);
  or or_7 (or_7_out, not_6_out, or_4_out);
  Register #(.Bits(32)) register_7 (.D(PCS_FT), .C(C), .en(CT_RF__PCSE), .Q(PCS_DC));
  D_FF d_ff_11 (.D(boot_t), .C(C), .Q(d_ff_11_q));  // open: nQ
  or or_8 (halt_FT_DC_ISS, id_full, RS_full, INT_HALT, dipswitch_2_out, dipswitch_1_out, LDB_busy, STB_busy);
  DipSwitch dipswitch_2 (.out(dipswitch_2_out));
  assign \wait  = Fl_ECLR ? 1'b1 : 1'bz;  // Driver driver_28
  assign CT_RF__PCH = Fl_ECLR ? 1'b1 : 1'bz;  // Driver driver_29
  assign CT_RF__PCSE = Fl_ECLR ? 1'b1 : 1'bz;  // Driver driver_30
  assign CT_RF__PCJ = Fl_ECLR ? 1'b1 : 1'bz;  // Driver driver_31
  nor nor_3 (nor_3_out, CT_DIR__EXID[7], CT_DIR__EXID[6], CT_DIR__EXID[5], CT_DIR__EXID[4], CT_DIR__EXID[3]);
  Multiplexer #(.Selector_Bits(3), .Bits(32)) multiplexer_3 (
    .sel(CT_DIR__EXID[2:0]), .in_0(32'h1), .in_1(PVEC), .in_2(ISC), .in_3({{27{1'b0}}, ILV}),
    .in_4({32{1'b0}}), .in_5({32{1'b0}}), .in_6({32{1'b0}}), .in_7({32{1'b0}}), .out(multiplexer_3_out));
  and and_17 (issue_e, ISS_q, BUS_INSTV, not_6_out);
  PullDown pulldown_8 (.out(CT_DISP));
  Multiplexer #(.Bits(32)) multiplexer_4 (.sel(CT_ISCS), .in_0(multiplexer_1_out), .in_1(ISC_sc), .out(ISC_i));
  assign CT_ISCE = RX_ISCE ? 1'b1 : 1'bz;  // Driver driver_32
  Multiplexer #(.Bits(5)) multiplexer_5 (
    .sel(int_accept), .in_0(multiplexer_2_out), .in_1({1'b1, INT_lev}), .out(ILV_i));
  assign CT_ILVE = RX_ILVE ? 1'b1 : 1'bz;  // Driver driver_33
  assign RX_SEL = bitextender_2_out & multiplexer_3_out;  // And and_18, 32 bits wide
  assign CT_BUS__IAR = d_ff_11_q ? 1'b1 : 1'bz;  // Driver driver_34
  assign CT_RF__PCSE = d_ff_11_q ? 1'b1 : 1'bz;  // Driver driver_35
  assign CT_ISCM = CT_INTM ? 1'b1 : 1'bz;  // Driver driver_36
  assign CT_ISCE = CT_INTM ? 1'b1 : 1'bz;  // Driver driver_37
  assign CT_RF__SCD = CT_INTM ? 1'b1 : 1'bz;  // Driver driver_38
  assign CT_RF__SCN = CT_INTM ? 3'b100 : 3'bz;  // Driver driver_39
  assign CT_ISCS = CT_INTM ? 1'b1 : 1'bz;  // Driver driver_40
  Multiplexer #(.Bits(32)) multiplexer_6 (.sel(RX_PVECM), .in_0(CT_RF__D1), .in_1(CT_RF__D2), .out(PVEC_i));
  assign CT_PVECE = RX_PVECE ? 1'b1 : 1'bz;  // Driver driver_41
  BitExtender #(.inputBits(1), .outputBits(32)) bitextender_2 (.in(nor_3_out), .out(bitextender_2_out));
  DipSwitch dipswitch_3 (.out(BTB_packet[0]));
  BTB btb_1 (
    .C(C), .E(JPU_BTB__ST), .V_in(1'b1), .id(JPU_PC[5:2]), .tag(JPU_PC[17:6]), .pred(JPU_pred),
    .tar(JPU_ADDR), .R_id(PCS[5:2]), .R_tag(PCS[17:6]), .V(BTB_packet[1]), .J(BTB_JP),
    .pred_O(BTB_packet[4:3]), .tar_O(BTB_packet[36:5]));
  or or_9 (or_9_out, MEM_AC, MEM_CLR);
  not not_8 (MEM_LD__REC, LDB_forward);
  inst_sfcomp inst_sfcomp_1 (
    .A_id(MEM_INST), .A_ep(MEM_EP), .B_id(clr_id), .B_ep(clr_ep), .B_eq(clr_self), .A_new(inst_sfcomp_1_a_new));
  inst_sfcomp inst_sfcomp_2 (
    .A_id(MEM_LD__INST), .A_ep(MEM_LD__EP), .B_id(clr_id), .B_ep(clr_ep), .B_eq(clr_self),
    .A_new(inst_sfcomp_2_a_new));
  Comparator #(.Bits(4)) comparator_4 (.a(TRAP_INST), .b(com1_inst), .eq(comparator_4_eq));  // open: gt, lt
  Comparator #(.Bits(4)) comparator_5 (.a(TRAP_INST), .b(com2_inst), .eq(comparator_5_eq));  // open: gt, lt
  Register #(.Bits(4)) register_8 (.D(CT_FU__INST), .C(C_ct), .en(CT_TRAP__LD), .Q(TRAP_INST));
  Register register_9 (.D(CT_FU__EPOCH), .C(C_ct), .en(CT_TRAP__LD), .Q(TRAP_EP));
  D_FF d_ff_12 (.D(CT_INT), .C(C_ct), .Q(d_ff_12_q));  // open: nQ
  D_FF d_ff_13 (.D(CT_TRAP__LD), .C(C_ct), .Q(d_ff_13_q));  // open: nQ
  Register #(.Bits(8)) register_10 (.D(CT_INTID), .C(C_ct), .en(CT_TRAP__LD), .Q({register_10_q, TRAP_INT}));
  RS_FF rs_ff_4 (.S(CT_TRAP__LD), .C(C_ct), .R(FU_CLR[4]), .Q(TRAP_RD));  // open: nQ
  ROB_SC rob_sc_1 (
    .C(C), .E(CT_RF__SCSRE), .D(ISC_sc), .inst(inst_DP), .com1(com1), .com2(com2), .com1_id(com1_inst),
    .com2_id(com2_inst), .clr_16(clr_16), .roll(clr_id), .SCA(SCA), .W1(CT_SC__W1), .D1(CT_SC__D1),
    .W2(CT_SC__W2), .D2(CT_SC__D2), .D3(CT_SC__FD));
  D_FF #(.Bits(2)) d_ff_14 (.D({LDB_M__V, STB_M__V}), .C(C_ct), .Q(d_ff_14_q));  // open: nQ
  and and_19 (and_19_out, ~MEM_LD, or_9_out);  // And
  and and_20 (and_20_out, com1, comparator_4_eq);
  and and_21 (and_21_out, com2, comparator_5_eq);
  // ROB_gen rob_gen_1: pin names not known; wires that end beside it: C, CT_ROB__GEN__STA, CT_ROB__GEN__STB, ROB_GEN_DA, ROB_GEN_DB, ROB_GEN_WA, ROB_GEN_WB, ROB_GEN_EX1, ROB_GEN_EX2, ROB_GEN_INSTA, ROB_GEN_INSTB, com1, com2, com1_inst, com2_inst, clr_16, RET_INST, CT_RF__D1, CT_RF__R1, CT_RF__W1, CT_RF__EX1, CT_RF__D2, CT_RF__R2, CT_RF__W2, CT_RF__EX2, CT_RF__DR
  ROB_PC rob_pc_1 (
    .C(C), .E(issue), .D(PCS_DC), .inst(inst_IS), .com_id(com1_inst), .read_id(inst_DP), .ret_id(RET_INST),
    .D1(pca_i), .D2(pc_read), .D3(pc_ret));
  or or_10 (or_10_out, multiplexer_9_out, MEM_BF__free);
  or or_11 (or_11_out, d_ff_14_q[0], d_ff_14_q[1], MEM_CLR);
  RS_FF rs_ff_5 (.S(MEM_LD), .C(C_ct), .R(and_19_out), .Q(rs_ff_5_q), .nQ(rs_ff_5_nq));
  and and_22 (MEM_CLR, inst_sfcomp_1_a_new, ~MEM_TYPE__ST, clr);  // And
  and and_23 (MEM_LD__CLR, inst_sfcomp_2_a_new, clr);
  or or_12 (or_12_out, and_20_out, and_21_out);
  inst_comp inst_comp_1 (.A_id(TRAP_INST), .A_ep(TRAP_EP), .B_id(clr_id), .B_ep(clr_ep), .A_new(inst_comp_1_a_new));
  and and_24 (TRAP_IRD, ~FU_CLR[4], d_ff_12_q, d_ff_13_q);  // And
  and and_25 (and_25_out, byte_D0[3], byte_D0[0]);
  and and_26 (and_26_out, byte_D0[2], byte_D0[0]);
  and and_27 (and_27_out, byte_D0_iv[3], byte_D0_iv[2], byte_D0[1], byte_D0_iv[0]);
  and and_28 (and_28_out, byte_D0_iv[4], byte_D0[3], byte_D0[2], byte_D0[1]);
  and and_29 (and_29_out, byte_D0[4], byte_D0_iv[3], byte_D0_iv[2], byte_D0[1], byte_D0[0]);
  and and_30 (and_30_out[7], byte_D0_iv[4], byte_D0[3], byte_D0[2]);
  and and_31 (and_31_out, byte_D0[4], byte_D0[2], byte_D0_iv[1]);
  and and_32 (and_32_out, byte_D0[4], byte_D0_iv[3], byte_D0_iv[2]);
  and and_33 (and_33_out, byte_D0_iv[4], byte_D0_iv[3], byte_D0_iv[2]);
  and and_34 (and_34_out, byte_D0_iv[4], byte_D0_iv[3]);
  and and_35 (and_35_out, byte_D0_iv[4], byte_D0[3], byte_D0_iv[2], byte_D0_iv[1]);
  and and_36 (and_36_out, byte_D0_iv[4], byte_D0[3], byte_D0_iv[2]);
  and and_37 (and_37_out, byte_D0[4], byte_D0[3]);
  and and_38 (and_38_out, byte_D0_iv[4], byte_D0_iv[3], byte_D0[2], byte_D0_iv[1]);
  and and_39 (and_39_out, byte_D0[4], byte_D0[2], byte_D0[1]);
  and and_40 (and_40_out, byte_D0_iv[4], byte_D0_iv[3], byte_D0_iv[2], byte_D0[1], byte_D0[0]);
  and and_41 (and_41_out, byte_D0_iv[2], byte_D0_iv[0]);
  and and_42 (and_42_out, byte_D0[2], byte_D0[0]);
  and and_43 (and_43_out, byte_D0[1], byte_D0[2], byte_D0[4]);
  and and_44 (and_44_out, byte_D0[3], byte_D0[4]);
  not not_9 (not_9_out, MEM_CLR);
  not not_10 (not_10_out, B_used);
  not not_11 (not_11_out, MEM_CLR);
  not not_12 (not_12_out, B_used);
  and and_45 (and_45_out, ~FU_CLR[4], ~d_ff_12_q, d_ff_13_q);  // And
  and and_46 (MEM_AC, or_10_out, D_accept, not_9_out, not_10_out);
  and and_47 (MEM_RD, not_11_out, not_12_out, rs_ff_5_q);
  or or_13 (or_13_out, rs_ff_5_nq, MEM_AC, MEM_CLR);
  and and_48 (and_48_out, or_12_out, hlt, rs_ff_6_q);
  and and_49 (and_49_out, or_12_out, rs_ff_6_q);
  or or_14 (or_14_out, and_45_out, FU_I__V[0]);
  and and_50 (TRAP_busy, TRAP_RD, ~TRAP_ST);  // And
  or or_15 (and_30_out[9], and_25_out, and_26_out, and_27_out);
  or or_16 (and_30_out[6], and_31_out, and_28_out, and_29_out);
  or or_17 (and_30_out[5], and_30_out[7], and_31_out, and_32_out);
  or or_18 (and_30_out[4], and_38_out, and_39_out, and_33_out);
  or or_19 (and_30_out[3], and_34_out, and_39_out, and_35_out);
  or or_20 (and_30_out[2], and_36_out, and_37_out);
  or or_21 (and_30_out[1], and_38_out, and_39_out, and_40_out);
  or or_22 (and_30_out[0], byte_D0[3], byte_D0[1], and_41_out, and_42_out);
  nor nor_4 (nor_4_out, and_43_out, and_44_out);
  ROB_FL rob_fl_1 (
    .C(C), .E1(CT_ROB__FL__STA), .E2(CT_ROB__FL__STB), .D1(ROB_FL_A), .D2(ROB_FL_B), .inst1(ROB_FL_INSTA),
    .inst2(ROB_FL_INSTB), .com1(com1), .com2(com2), .com1_id(com1_inst), .com2_id(com2_inst),
    .clr_16(clr_16), .W1_O(CT_FL__W1), .D1_O(CT_FL__D1), .W2_O(CT_FL__W2), .D2_O(CT_FL__D2));
  or or_23 (or_23_out, clr_sel[0], CT_JMP);
  Register #(.Bits(37)) BTB_F (.D({BTB_packet[36:3], BTB_JP, BTB_packet[1:0]}), .C(C), .en(CT_BUS__IAR), .Q(BTB_fetch));
  Register #(.Bits(32)) I_A__R (.D(PCS), .C(C), .en(CT_BUS__IAR), .Q(I_A__R_q));
  xor xor_1 (xor_1_out, STB_M__EP, LDB_M__EP);
  Comparator #(.Bits(4)) comparator_6 (
    .a(LDB_M__ID), .b(STB_M__ID), .gt(comparator_6_gt), .lt(comparator_6_lt));  // open: eq
  and and_51 (MEM_LD, or_11_out, or_13_out);
  Register #(.Bits(32)) register_11 (.D(pc_read), .C(C), .en(CT_TRAP__LD), .Q(register_11_q));
  and and_52 (and_52_out, inst_comp_1_a_new, clr, ~CT_TRAP__LD);  // And
  and and_53 (and_53_out, and_49_out, ~CT_TRAP__LD);  // And
  nor nor_5 (nor_5_out[1], byte_D1[1], nor_5_out[2]);
  nor nor_6 (nor_5_out[2], byte_D1[0], byte_D1[1], byte_D1[2]);
  and and_54 (and_54_out, byte_D0_iv[7], byte_D0_iv[6], byte_D0[5], CT_DISP);
  and and_55 (and_55_out, byte_D0_iv[7], byte_D0[6], byte_D0_iv[5], CT_DISP);
  PriorityEncoder #(.Selector_Bits(2)) priorityencoder_1 (
    .in0(1'b1), .in1(or_23_out), .in2(CT_RF__PCH), .in3(1'b0), .num(priorityencoder_1_num));  // open: any
  assign I_A__bus = CT_BUS__IAG ? I_A__R_q : 32'bz;  // Driver driver_42
  and and_56 (and_56_out, STB_M__V, LDB_M__V);
  Multiplexer multiplexer_7 (.sel(xor_1_out), .in_0(comparator_6_gt), .in_1(comparator_6_lt), .out(multiplexer_7_out));
  and and_57 (and_57_out, MEM_AC, MEM_RD, not_13_out, not_14_out);
  not not_13 (not_13_out, MEM_TYPE__ST);
  not not_14 (not_14_out, MEM_CLR);
  or or_24 (or_24_out, MEM_LD__REC, MEM_LD__CLR);
  RS_FF u_HLT (.S(run), .C(C_ct), .R(and_48_out), .nQ(halted));  // open: Q
  or or_25 (or_25_out, and_52_out, and_53_out);
  not not_15 (TRAP_free, TRAP_busy);
  and and_58 (and_58_out, byte_D0_iv[0], byte_D0_iv[1], byte_D0[2], byte_D0[3], byte_D0[4], byte_D0_iv[5], byte_D0_iv[6], byte_D0_iv[7], CT_DISP);
  and and_59 (and_59_out, byte_D0[1], byte_D0_iv[2], byte_D0[3], byte_D0[4], byte_D0_iv[5], byte_D0_iv[6], byte_D0_iv[7], CT_DISP);
  and and_60 (and_60_out, byte_D0[1], byte_D0[2], byte_D0[3], byte_D0[4], byte_D0_iv[5], byte_D0_iv[6], byte_D0_iv[7], CT_DISP);
  or or_26 (or_26_out[1], byte_D1[1], byte_D1[2], byte_D1[0]);
  or or_27 (or_27_out, and_55_out, and_54_out);
  and and_61 (and_61_out, com1, CT_RF__W1, ~CT_RF__EX1);  // And
  and and_62 (and_62_out, com2, CT_RF__W2, ~CT_RF__EX2);  // And
  PullDown #(.Bits(16)) pulldown_9 (.out(INT_inst));
  PullDown #(.Bits(16)) pulldown_10 (.out(V1_inst));
  PullDown #(.Bits(16)) pulldown_11 (.out(V2_inst));
  PullDown pulldown_12 (.out(CT_RF__SCSRE));
  Multiplexer #(.Selector_Bits(2), .Bits(32)) multiplexer_8 (
    .sel(priorityencoder_1_num), .in_0(MEM_FPC), .in_1(JPU_ADDR), .in_2(HALT_PC), .in_3({32{1'b0}}),
    .out(multiplexer_8_out));
  and and_63 (and_63_out, clr_self, clr);
  Multiplexer multiplexer_9 (.sel(and_56_out), .in_0(STB_M__V), .in_1(multiplexer_7_out), .out(multiplexer_9_out));
  D_FF #(.Bits(32)) d_ff_15 (.D(register_11_q), .C(C_ct), .Q(HALT_PC));  // open: nQ
  RS_FF rs_ff_6 (.S(CT_TRAP__LD), .C(C_ct), .R(or_25_out), .Q(rs_ff_6_q));  // open: nQ
  and and_64 (FU_CLR[4], inst_comp_1_a_new, clr);
  bus16x2_demux bus16x2_demux_1 (.bus_1(V1_inst), .bus_2(V2_inst), .E(or_14_out), .id(TRAP_INST));
  bus16_demux bus16_demux_1 (.bus(INT_inst), .E(or_14_out), .id(TRAP_INST));
  and and_65 (and_65_out, CT_DISP, byte_D0[4], byte_D0[3], byte_D0_iv[1], byte_D0_iv[2], byte_D0_iv[5], byte_D0_iv[6], byte_D0_iv[7]);
  or or_28 (or_28_out, and_58_out, and_59_out);
  not not_16 (not_16_out, multiplexer_9_out);
  Multiplexer #(.Bits(32)) multiplexer_10 (
    .sel(multiplexer_9_out), .in_0(LDB_M__A), .in_1(STB_M__A), .out(multiplexer_10_out));
  Multiplexer #(.Bits(2)) multiplexer_11 (
    .sel(multiplexer_9_out), .in_0(LDB_M__MD), .in_1(STB_M__MD), .out(multiplexer_11_out));
  and and_66 (and_66_out, or_24_out, ~and_57_out);  // And
  and and_67 (and_67_out, and_60_out, byte_D0[0]);
  and and_68 (and_68_out, byte_D0_iv[0], and_60_out);
  // regFile4 regfile4_1: pin names not known; wires that end beside it: C, and_61_out, and_62_out, CT_RF__D1, CT_RF__D2, CT_RF__R1[7:3], CT_RF__R1[2:0], CT_RF__R2[7:3], CT_RF__R2[2:0], CT_RF__RA, CT_RF__MA, CT_RF__RB, CT_RF__MB, pcs_i, CT_RF__PCSE, pca_i, CT_RF__PCAE, ISC_sc, CT_RF__SCSS, CT_RF__SCSE, sca_i, CT_RF__SCAE, CT_RF__SCAE, {{23{1'b0}}, FL[14], fl_i}, CT_RF__FLS, 4'b0001, pc_read, R_A, R_B, PCS, PCA, SCS, SCA, FL
  PriorityEncoder #(.Selector_Bits(2)) priorityencoder_2 (
    .in0(1'b1), .in1(BTB_JP), .in2(CT_RF__PCJ), .in3(boot_t), .num(priorityencoder_2_num));  // open: any
  or or_29 (or_29_out, boot_t, and_63_out, or_23_out, BTB_JP);
  Register #(.Bits(37)) BTB_D (.D(BTB_fetch), .C(C), .en(dc_e), .Q(BTB_D_q));
  Register #(.Bits(32)) I_D__R (.D(I_D__bus), .C(C), .en(dc_e), .Q(I_D__R_q));
  Register register_12 (.D(CT_BUS__IDM), .C(C), .en(dc_e), .Q(register_12_q));
  and and_69 (MB_LDB__LD, LDB_M__V, MEM_LD, not_16_out);
  and and_70 (MB_STB__LD, multiplexer_9_out, MEM_LD);
  Register register_13 (.D(multiplexer_9_out), .C(C), .en(MEM_LD), .Q(MEM_TYPE__ST));
  Register register_14 (.D(LDB_M__EP), .C(C), .en(MEM_LD), .Q(MEM_EP));
  Register #(.Bits(4)) register_15 (.D(LDB_M__ID), .C(C), .en(MEM_LD), .Q(MEM_INST));
  Register #(.Bits(32)) register_16 (.D(multiplexer_10_out), .C(C), .en(MEM_LD), .Q(register_16_q));
  Register #(.Bits(2)) register_17 (.D(multiplexer_11_out), .C(C), .en(MEM_LD), .Q(register_17_q));
  Register #(.Bits(32)) register_18 (.D(STB_M__D), .C(C), .en(MEM_LD), .Q(register_18_q));
  not not_17 (not_17_out, MEM_LD__CLR);
  RS_FF rs_ff_7 (.S(and_57_out), .C(C), .R(and_66_out), .Q(rs_ff_7_q), .nQ(rs_ff_7_nq));
  Register #(.Bits(32)) register_19 (.D(D_D__bus), .C(C), .en(MEM_AC), .Q(MEM_LD__D));
  Register #(.Bits(4)) register_20 (.D(MEM_INST), .C(C), .en(MEM_AC), .Q(MEM_LD__INST));
  Register register_21 (.D(MEM_EP), .C(C), .en(MEM_AC), .Q(MEM_LD__EP));
  assign {CT_RF__RA, CT_RF__MA} = or_32_out ? byte_D1 : 8'bz;  // Driver driver_43
  assign {CT_RF__RB, CT_RF__MB} = or_32_out ? byte_D2 : 8'bz;  // Driver driver_44
  assign CT_ALU__LD = or_32_out ? 1'b1 : 1'bz;  // Driver driver_45
  assign CT_ALU__CT = or_32_out ? {1'b0, and_30_out[7:0]} : 9'bz;  // Driver driver_46
  assign CT_ALU__M = or_32_out ? and_30_out[9] : 1'bz;  // Driver driver_47
  assign CT_FU__INST = or_32_out ? inst_DP : 4'bz;  // Driver driver_48
  assign CT_FU__EPOCH = or_32_out ? epoch_DP : 1'bz;  // Driver driver_49
  assign CT_FU__WR = or_32_out ? byte_D1 : 8'bz;  // Driver driver_50
  assign CT_ALU__WD = or_32_out ? nor_4_out : 1'bz;  // Driver driver_51
  assign CT_ALU__WF = or_32_out ? 1'b1 : 1'bz;  // Driver driver_52
  assign {CT_RF__RA, CT_RF__MA} = or_28_out ? byte_D2 : 8'bz;  // Driver driver_53
  assign CT_DIR__LD = or_28_out ? 1'b1 : 1'bz;  // Driver driver_54
  assign CT_DIR__M = or_28_out ? and_59_out : 1'bz;  // Driver driver_55
  assign CT_DIR__MS = or_28_out ? byte_D0[0] : 1'bz;  // Driver driver_56
  assign CT_FU__INST = or_28_out ? inst_DP : 4'bz;  // Driver driver_57
  assign CT_FU__EPOCH = or_28_out ? epoch_DP : 1'bz;  // Driver driver_58
  assign CT_FU__WR = or_28_out ? byte_D1 : 8'bz;  // Driver driver_59
  assign CT_RF__SCSS = and_60_out ? 1'b1 : 1'bz;  // Driver driver_60
  assign {CT_RF__RB, CT_RF__MB} = and_60_out ? 8'hf0 : 8'bz;  // Driver driver_61
  assign {CT_RF__RA, CT_RF__MA} = and_67_out ? byte_D1 : 8'bz;  // Driver driver_62
  assign CT_FU__WR = and_68_out ? byte_D1 : 8'bz;  // Driver driver_63
  assign CT_MB__LD = and_60_out ? 1'b1 : 1'bz;  // Driver driver_64
  assign CT_MB__ST = and_67_out ? 1'b1 : 1'bz;  // Driver driver_65
  assign CT_SP__MOF = and_67_out ? {1'b1, or_26_out[1], byte_D1[1]} : 3'bz;  // Driver driver_66
  assign CT_MB__OFFM = and_60_out ? 1'b1 : 1'bz;  // Driver driver_67
  assign CT_RF__SCSE = and_60_out ? 1'b1 : 1'bz;  // Driver driver_68
  assign CT_RF__SCN = and_60_out ? {nor_5_out, byte_D1[1]} : 3'bz;  // Driver driver_69
  assign CT_RF__SCD = and_67_out ? 1'b1 : 1'bz;  // Driver driver_70
  assign CT_FU__INST = and_60_out ? inst_DP : 4'bz;  // Driver driver_71
  assign CT_FU__EPOCH = and_60_out ? epoch_DP : 1'bz;  // Driver driver_72
  assign CT_RF__SCSRE = and_60_out ? 1'b1 : 1'bz;  // Driver driver_73
  assign CT_FU__EPOCH = or_27_out ? epoch_DP : 1'bz;  // Driver driver_74
  assign CT_FU__INST = or_27_out ? inst_DP : 4'bz;  // Driver driver_75
  assign {CT_RF__RB, CT_RF__MB} = or_27_out ? {byte_D0[4:0], 3'b000} : 8'bz;  // Driver driver_76
  assign {CT_RF__RA, CT_RF__MA} = and_55_out ? byte_D1 : 8'bz;  // Driver driver_77
  assign CT_FU__WR = and_54_out ? byte_D1 : 8'bz;  // Driver driver_78
  assign CT_MB__LD = or_27_out ? 1'b1 : 1'bz;  // Driver driver_79
  assign CT_MB__ST = and_55_out ? 1'b1 : 1'bz;  // Driver driver_80
  or or_30 (CT_RF__PCAE, com1, com2);
  ROB_INT rob_int_1 (
    .C(C), .E1(CT_ROB__INT__STA), .E2(CT_ROB__INT__STB), .D1(ROB_INT_A), .D2(ROB_INT_B),
    .inst1(ROB_INT_INSTA), .inst2(ROB_INT_INSTB), .com1(com1), .com2(com2), .com1_id(com1_inst),
    .com2_id(com2_inst), .clr_16(clr_16), .W_O(CT_INT__W), .D_O(CT_INT__D));
  Multiplexer #(.Selector_Bits(2), .Bits(32)) multiplexer_12 (
    .sel(priorityencoder_2_num), .in_0(PCS), .in_1(BTB_packet[36:5]), .in_2(multiplexer_8_out),
    .in_3(reset_vec), .out(multiplexer_12_out));
  assign D_A__bus = MEM_RD ? register_16_q : 32'bz;  // Driver driver_81
  assign D_MD = MEM_RD ? register_17_q : 2'bz;  // Driver driver_82
  assign D_D__bus = D_ST ? register_18_q : 32'bz;  // Driver driver_83
  and and_71 (MEM_LD__RD, not_17_out, rs_ff_7_q);
  or or_31 (MEM_BF__free, rs_ff_7_nq, MEM_LD__RD, MEM_LD__CLR);
  Register register_22 (.D(CT_KILL), .C(C_ct), .en(CT_TRAP__LD), .Q(hlt));
  and and_72 (and_72_out, byte_D0_iv[7], byte_D0_iv[6], CT_DISP, byte_D0_iv[5], byte_D0_iv[4]);
  and and_73 (and_73_out, byte_D0_iv[7], byte_D0_iv[6], byte_D0_iv[5], byte_D0[4], byte_D0_iv[3], CT_DISP);
  Multiplexer #(.Bits(32)) multiplexer_13 (
    .sel(or_29_out), .in_0(add_4c32_1_s), .in_1(multiplexer_12_out), .out(pcs_i));
  add_4c32 add_4c32_1 (.a(multiplexer_12_out), .b(4'b0100), .s(add_4c32_1_s));  // open: c
  D_FF #(.Bits(37)) d_ff_16 (.D(BTB_D_q), .C(C_ct), .Q(BTB_pack__iss));  // open: nQ
  D_FF #(.Bits(32)) d_ff_17 (.D(I_D__R_q), .C(C_ct), .Q({byte_I0, byte_I1, byte_I2, byte_I3}));  // open: nQ
  D_FF d_ff_18 (.D(register_12_q), .C(C_ct), .nQ(BUS_INSTV));  // open: Q
  and and_74 (D_LD, ~MEM_TYPE__ST, MEM_RD);  // And
  and and_75 (D_ST, MEM_RD, MEM_TYPE__ST);
  PullDown pulldown_13 (.out(CT_INT));
  PullDown #(.Bits(8)) pulldown_14 (.out(CT_INTID));
  or or_32 (or_32_out, and_72_out, and_65_out, and_73_out);
  BitExtender #(.inputBits(1), .outputBits(8)) bitextender_3 (.in(byte_D0[3]), .out(bitextender_3_out));
  assign xor_2_out = FL[7:0] ^ bitextender_3_out;  // XOr xor_2, 8 bits wide
  and and_76 (and_76_out, com1, CT_SC__W1);
  and and_77 (and_77_out, com2, CT_SC__W2);
  Multiplexer #(.Bits(32)) multiplexer_14 (.sel(and_77_out), .in_0(CT_SC__D1), .in_1(CT_SC__D2), .out(sca_i));
  and and_78 (and_78_out, byte_D2[7], CT_DIR__MS);
  BitExtender #(.inputBits(1)) bitextender_4 (.in(and_78_out), .out(bitextender_4_out));
  Multiplexer #(.Bits(3)) multiplexer_15 (
    .sel(CT_MB__ST), .in_0(CT_FU__WR[2:0]), .in_1(CT_RF__MA), .out(multiplexer_15_out));
  and and_79 (and_79_out, byte_D0[1], byte_D0_iv[2], byte_D0[3], byte_D0[4], byte_D0[5], byte_D0[6], byte_D0_iv[7], CT_DISP);
  or or_33 (CT_RF__SCAE, and_76_out, and_77_out);
  Multiplexer multiplexer_16 (.sel(and_91_out[2]), .in_0(nand_1_out[2]), .in_1(1'b1), .out(multiplexer_16_out));
  not not_18 (not_18_out[0], register_23_q[0]);
  xor xor_3 (not_18_out[1], register_23_q[0], register_23_q[1]);
  xor xor_4 (not_18_out[2], register_23_q[1], register_23_q[2]);
  Multiplexer #(.Bits(32)) multiplexer_17 (
    .sel(CT_ALU__M), .in_0(R_B), .in_1({{16{1'b0}}, byte_D2, byte_D3}), .out(multiplexer_17_out));
  PullDown #(.Bits(8)) pulldown_15 (.out(CT_DIR__EXID));
  PullDown pulldown_16 (.out(CT_DIR__EXM));
  PullDown pulldown_17 (.out(CT_FU__EX));
  and and_80 (and_80_out, byte_D0_iv[4], byte_D0[5], byte_D0[6], byte_D0_iv[7], CT_DISP);
  Multiplexer #(.Selector_Bits(3)) multiplexer_18 (
    .sel(byte_D0[2:0]), .in_0(xor_2_out[0]), .in_1(xor_2_out[1]), .in_2(xor_2_out[2]), .in_3(xor_2_out[3]),
    .in_4(xor_2_out[4]), .in_5(xor_2_out[5]), .in_6(xor_2_out[6]), .in_7(xor_2_out[7]),
    .out(multiplexer_18_out));
  and and_81 (and_81_out, multiplexer_16_out, CT_ALU__LD);
  Register register_23 (.D(and_81_out), .C(C_ct), .en(or_34_out), .Q(register_23_q[2]));
  not not_19 (not_19_out, multiplexer_16_out);
  or or_34 (or_34_out, not_19_out, multiplexer_19_out[2]);
  Multiplexer #(.Bits(3)) multiplexer_19 (
    .sel(or_35_out), .in_0(not_18_out), .in_1(and_91_out), .out(multiplexer_19_out));
  or or_35 (or_35_out, and_91_out[0], and_91_out[1], and_91_out[2]);
  Register #(.Bits(4)) register_24 (.D(CT_FU__INST), .C(C_ct), .en(multiplexer_19_out[2]), .Q(register_24_q));
  Register register_25 (.D(CT_FU__EPOCH), .C(C_ct), .en(multiplexer_19_out[2]), .Q(register_25_q));
  Register register_26 (.D(CT_ALU__WD), .C(C_ct), .en(multiplexer_19_out[2]), .Q(register_26_q));
  Register register_27 (.D(CT_ALU__WF), .C(C_ct), .en(multiplexer_19_out[2]), .Q(register_27_q));
  Register #(.Bits(32)) register_28 (.D(R_A), .C(C), .en(multiplexer_19_out[2]), .Q(register_28_q));
  Register #(.Bits(32)) register_29 (.D(multiplexer_17_out), .C(C), .en(multiplexer_19_out[2]), .Q(register_29_q));
  Register #(.Bits(8)) register_30 (.D(FL[7:0]), .C(C), .en(multiplexer_19_out[2]), .Q(register_30_q));
  Register #(.Bits(9)) register_31 (.D(CT_ALU__CT), .C(C_ct), .en(multiplexer_19_out[2]), .Q(register_31_q));
  Register #(.Bits(8)) register_32 (.D(CT_FU__WR), .C(C_ct), .en(multiplexer_19_out[2]), .Q(register_32_q));
  Multiplexer #(.Bits(32)) multiplexer_20 (
    .sel(CT_DIR__M), .in_0(R_A), .in_1({bitextender_4_out, byte_D2, byte_D3}), .out(multiplexer_20_out));
  Multiplexer #(.Bits(32)) multiplexer_21 (.sel(CT_INTM), .in_0(pc_read), .in_1(int_pc), .out(multiplexer_21_out));
  or or_36 (or_36_out, CT_INTM, CT_CALLM);
  or or_37 (or_37_out, multiplexer_15_out[0], multiplexer_15_out[2]);
  not not_20 (not_20_out, multiplexer_15_out[1]);
  and and_82 (and_82_out, byte_D0_iv[0], byte_D0_iv[1], byte_D0_iv[2], byte_D0_iv[3], byte_D0[4], byte_D0[5], byte_D0[6], byte_D0_iv[7], CT_DISP);
  and and_83 (and_83_out, byte_D0[0], byte_D0_iv[1], byte_D0_iv[2], byte_D0_iv[3], byte_D0[4], byte_D0[5], byte_D0[6], byte_D0_iv[7], CT_DISP);
  and and_84 (and_84_out, byte_D0_iv[1], byte_D0[2], byte_D0_iv[3], byte_D0[4], byte_D0[5], byte_D0[6], byte_D0_iv[7], CT_DISP);
  and and_85 (and_85_out, byte_D0[0], byte_D0_iv[1], byte_D0[2], byte_D0[3], byte_D0[4], byte_D0_iv[5], byte_D0_iv[6], byte_D0_iv[7], CT_DISP);
  and and_86 (and_86_out, byte_D0[0], and_79_out);
  and and_87 (and_87_out, and_79_out, byte_D0_iv[0]);
  Multiplexer multiplexer_22 (
    .sel(and_91_out[1]), .in_0(nand_1_out[1]), .in_1(nand_1_out[2]), .out(multiplexer_22_out));
  Multiplexer multiplexer_23 (
    .sel(register_23_q[2]), .in_0(CT_ALU__LD), .in_1(register_23_q[2]), .out(multiplexer_23_out));
  Multiplexer #(.Bits(4)) multiplexer_24 (
    .sel(register_23_q[2]), .in_0(CT_FU__INST), .in_1(register_24_q), .out(multiplexer_24_out));
  inst_comp inst_comp_2 (
    .A_id(register_24_q), .A_ep(register_25_q), .B_id(clr_id), .B_ep(clr_ep), .A_new(inst_comp_2_a_new));
  Multiplexer multiplexer_25 (
    .sel(register_23_q[2]), .in_0(CT_FU__EPOCH), .in_1(register_25_q), .out(multiplexer_25_out));
  Multiplexer multiplexer_26 (
    .sel(register_23_q[2]), .in_0(CT_ALU__WD), .in_1(register_26_q), .out(multiplexer_26_out));
  Multiplexer multiplexer_27 (
    .sel(register_23_q[2]), .in_0(CT_ALU__WF), .in_1(register_27_q), .out(multiplexer_27_out));
  Multiplexer #(.Bits(32)) multiplexer_28 (
    .sel(register_23_q[2]), .in_0(R_A), .in_1(register_28_q), .out(multiplexer_28_out));
  Multiplexer #(.Bits(32)) multiplexer_29 (
    .sel(register_23_q[2]), .in_0(multiplexer_17_out), .in_1(register_29_q), .out(multiplexer_29_out));
  Multiplexer #(.Bits(8)) multiplexer_30 (
    .sel(register_23_q[2]), .in_0(FL[7:0]), .in_1(register_30_q), .out(multiplexer_30_out));
  Multiplexer #(.Bits(9)) multiplexer_31 (
    .sel(register_23_q[2]), .in_0(CT_ALU__CT), .in_1(register_31_q), .out(multiplexer_31_out));
  Multiplexer #(.Bits(8)) multiplexer_32 (
    .sel(register_23_q[2]), .in_0(CT_FU__WR), .in_1(register_32_q), .out(multiplexer_32_out));
  Multiplexer multiplexer_33 (.sel(and_95_out[2]), .in_0(nand_4_out[2]), .in_1(1'b1), .out(multiplexer_33_out));
  not not_21 (not_21_out[0], register_48_q[0]);
  xor xor_5 (not_21_out[1], register_48_q[0], register_48_q[1]);
  xor xor_6 (not_21_out[2], register_48_q[1], register_48_q[2]);
  Multiplexer #(.Bits(32)) multiplexer_34 (
    .sel(CT_DIR__EXM), .in_0(multiplexer_20_out), .in_1(RX_SEL), .out(multiplexer_34_out));
  add_4c32 add_4c32_2 (.a(multiplexer_21_out), .b(4'b0100), .s(add_4c32_2_s));  // open: c
  BitExtender #(.inputBits(3)) bitextender_5 (.in(CT_SP__MOF), .out(bitextender_5_out));
  and and_88 (and_88_out[0], or_37_out, not_20_out);
  and and_89 (and_89_out, multiplexer_22_out, multiplexer_23_out);
  not not_22 (not_22_out, multiplexer_22_out);
  or or_38 (or_38_out, not_22_out, multiplexer_19_out[1]);
  or or_39 (register_23_q[1], register_47_q[1], register_23_q[2]);
  nand nand_1 (nand_1_out[2], inst_comp_2_a_new, register_23_q[2], clr);
  Register #(.Bits(4)) register_33 (.D(multiplexer_24_out), .C(C_ct), .en(multiplexer_19_out[1]), .Q(register_33_q));
  Register register_34 (.D(multiplexer_25_out), .C(C_ct), .en(multiplexer_19_out[1]), .Q(register_34_q));
  Register register_35 (.D(multiplexer_26_out), .C(C_ct), .en(multiplexer_19_out[1]), .Q(register_35_q));
  Register register_36 (.D(multiplexer_27_out), .C(C_ct), .en(multiplexer_19_out[1]), .Q(register_36_q));
  Register #(.Bits(32)) register_37 (.D(multiplexer_28_out), .C(C), .en(multiplexer_19_out[1]), .Q(register_37_q));
  Register #(.Bits(32)) register_38 (.D(multiplexer_29_out), .C(C), .en(multiplexer_19_out[1]), .Q(register_38_q));
  Register #(.Bits(8)) register_39 (.D(multiplexer_30_out), .C(C), .en(multiplexer_19_out[1]), .Q(register_39_q));
  Register #(.Bits(9)) register_40 (.D(multiplexer_31_out), .C(C_ct), .en(multiplexer_19_out[1]), .Q(register_40_q));
  Register #(.Bits(8)) register_41 (.D(multiplexer_32_out), .C(C_ct), .en(multiplexer_19_out[1]), .Q(register_41_q));
  and and_90 (and_90_out, multiplexer_33_out, CT_DIR__LD);
  not not_23 (not_23_out, multiplexer_33_out);
  Register #(.Bits(4)) register_42 (.D(CT_FU__INST), .C(C_ct), .en(multiplexer_47_out[2]), .Q(register_42_q));
  Register register_43 (.D(CT_FU__EPOCH), .C(C_ct), .en(multiplexer_47_out[2]), .Q(register_43_q));
  Register #(.Bits(32)) register_44 (.D(multiplexer_34_out), .C(C), .en(multiplexer_47_out[2]), .Q(register_44_q));
  Register #(.Bits(8)) register_45 (.D(CT_FU__WR), .C(C_ct), .en(multiplexer_47_out[2]), .Q(register_45_q));
  Register register_46 (.D(CT_FU__EX), .C(C_ct), .en(multiplexer_47_out[2]), .Q(register_46_q));
  Multiplexer #(.Bits(32)) multiplexer_35 (.sel(or_36_out), .in_0(R_A), .in_1(add_4c32_2_s), .out(multiplexer_35_out));
  Multiplexer #(.Bits(32)) multiplexer_36 (.sel(CT_INTM), .in_0(R_B), .in_1(ISC), .out(multiplexer_36_out));
  Multiplexer #(.Bits(16)) multiplexer_37 (
    .sel(CT_MB__OFFM), .in_0({byte_D2, byte_D3}), .in_1(bitextender_5_out), .out(multiplexer_37_out));
  assign CT_FU__EPOCH = and_80_out ? epoch_DP : 1'bz;  // Driver driver_84
  assign CT_FU__INST = and_80_out ? inst_DP : 4'bz;  // Driver driver_85
  assign {CT_RF__RA, CT_RF__MA} = and_80_out ? byte_D1 : 8'bz;  // Driver driver_86
  assign CT_JPU__LD = and_80_out ? 1'b1 : 1'bz;  // Driver driver_87
  assign CT_JPU__JP = and_80_out ? multiplexer_18_out : 1'bz;  // Driver driver_88
  assign JPU_A__ST = and_80_out ? 1'b1 : 1'bz;  // Driver driver_89
  assign CT_FU__EPOCH = and_82_out ? epoch_DP : 1'bz;  // Driver driver_90
  assign CT_FU__INST = and_82_out ? inst_DP : 4'bz;  // Driver driver_91
  assign {CT_RF__RA, CT_RF__MA} = and_82_out ? byte_D1 : 8'bz;  // Driver driver_92
  assign {CT_RF__RB, CT_RF__MB} = and_82_out ? 8'hf0 : 8'bz;  // Driver driver_93
  assign CT_JPU__LD = and_82_out ? 1'b1 : 1'bz;  // Driver driver_94
  assign CT_JPU__JP = and_82_out ? 1'b1 : 1'bz;  // Driver driver_95
  assign JPU_A__ST = and_82_out ? 1'b1 : 1'bz;  // Driver driver_96
  assign CT_MB__LD = and_82_out ? 1'b1 : 1'bz;  // Driver driver_97
  assign CT_MB__ST = and_82_out ? 1'b1 : 1'bz;  // Driver driver_98
  assign CT_CALLM = and_82_out ? 1'b1 : 1'bz;  // Driver driver_99
  assign CT_SP__MOF = and_82_out ? 3'b100 : 3'bz;  // Driver driver_100
  assign CT_MB__OFFM = and_82_out ? 1'b1 : 1'bz;  // Driver driver_101
  assign CT_RF__SCSE = and_82_out ? 1'b1 : 1'bz;  // Driver driver_102
  assign CT_RF__SCSS = and_82_out ? 1'b1 : 1'bz;  // Driver driver_103
  assign CT_RF__SCD = and_82_out ? 1'b1 : 1'bz;  // Driver driver_104
  assign CT_RF__SCN = and_82_out ? 3'b100 : 3'bz;  // Driver driver_105
  assign CT_FU__MF = and_82_out ? 1'b1 : 1'bz;  // Driver driver_106
  assign JPU_CALL = and_82_out ? 1'b1 : 1'bz;  // Driver driver_107
  assign CT_RF__SCSRE = and_82_out ? 1'b1 : 1'bz;  // Driver driver_108
  assign CT_FU__EPOCH = and_83_out ? epoch_DP : 1'bz;  // Driver driver_109
  assign CT_FU__INST = and_83_out ? inst_DP : 4'bz;  // Driver driver_110
  assign {CT_RF__RB, CT_RF__MB} = and_83_out ? 8'hf0 : 8'bz;  // Driver driver_111
  assign CT_FU__WR = and_83_out ? 8'he8 : 8'bz;  // Driver driver_112
  assign CT_MB__LD = and_83_out ? 1'b1 : 1'bz;  // Driver driver_113
  assign CT_MB__OFFM = and_83_out ? 1'b1 : 1'bz;  // Driver driver_114
  assign CT_RF__SCSE = and_83_out ? 1'b1 : 1'bz;  // Driver driver_115
  assign CT_RF__SCSS = and_83_out ? 1'b1 : 1'bz;  // Driver driver_116
  assign CT_RF__SCN = and_83_out ? 3'b100 : 3'bz;  // Driver driver_117
  assign CT_FU__MF = and_83_out ? 1'b1 : 1'bz;  // Driver driver_118
  assign CT_RET__LD = and_83_out ? 1'b1 : 1'bz;  // Driver driver_119
  assign CT_RF__SCSRE = and_83_out ? 1'b1 : 1'bz;  // Driver driver_120
  assign CT_KILL = and_84_out ? byte_D0[0] : 1'bz;  // Driver driver_121
  assign CT_FU__EPOCH = and_84_out ? epoch_DP : 1'bz;  // Driver driver_122
  assign CT_FU__INST = and_84_out ? inst_DP : 4'bz;  // Driver driver_123
  assign CT_TRAP__LD = and_84_out ? 1'b1 : 1'bz;  // Driver driver_124
  bus16x2_demux bus16x2_demux_2 (.bus_1(V1_inst), .bus_2(V2_inst), .E(and_85_out), .id(inst_DP));
  assign CT_FU__WR = and_86_out ? byte_D3 : 8'bz;  // Driver driver_125
  assign {CT_RF__RA, CT_RF__MA} = and_86_out ? byte_D1 : 8'bz;  // Driver driver_126
  assign CT_DIR__LD = and_79_out ? 1'b1 : 1'bz;  // Driver driver_127
  assign CT_FU__INST = and_79_out ? inst_DP : 4'bz;  // Driver driver_128
  assign CT_FU__EPOCH = and_79_out ? epoch_DP : 1'bz;  // Driver driver_129
  assign CT_FU__WR = and_87_out ? byte_D1 : 8'bz;  // Driver driver_130
  assign CT_DIR__EXID = and_87_out ? byte_D3 : 8'bz;  // Driver driver_131
  assign CT_DIR__EXM = and_79_out ? 1'b1 : 1'bz;  // Driver driver_132
  assign CT_FU__EX = and_79_out ? 1'b1 : 1'bz;  // Driver driver_133
  Register register_47 (.D(and_89_out), .C(C_ct), .en(or_38_out), .Q(register_47_q[1]));
  or or_40 (register_23_q[0], ALU_busy, register_47_q[1], register_23_q[2]);
  assign and_91_out = nand_2_out & register_23_q;  // And and_91, 3 bits wide
  Multiplexer #(.Bits(4)) multiplexer_38 (
    .sel(register_23_q[1]), .in_0(CT_FU__INST), .in_1(register_33_q), .out(multiplexer_38_out));
  inst_comp inst_comp_3 (
    .A_id(register_33_q), .A_ep(register_34_q), .B_id(clr_id), .B_ep(clr_ep), .A_new(inst_comp_3_a_new));
  Multiplexer multiplexer_39 (
    .sel(register_23_q[1]), .in_0(CT_FU__EPOCH), .in_1(register_34_q), .out(multiplexer_39_out));
  Multiplexer multiplexer_40 (
    .sel(register_23_q[1]), .in_0(CT_ALU__WD), .in_1(register_35_q), .out(multiplexer_40_out));
  Multiplexer multiplexer_41 (
    .sel(register_23_q[1]), .in_0(CT_ALU__WF), .in_1(register_36_q), .out(multiplexer_41_out));
  Multiplexer #(.Bits(32)) multiplexer_42 (
    .sel(register_23_q[1]), .in_0(R_A), .in_1(register_37_q), .out(multiplexer_42_out));
  Multiplexer #(.Bits(32)) multiplexer_43 (
    .sel(register_23_q[1]), .in_0(multiplexer_17_out), .in_1(register_38_q), .out(multiplexer_43_out));
  Multiplexer #(.Bits(8)) multiplexer_44 (
    .sel(register_23_q[1]), .in_0(FL[7:0]), .in_1(register_39_q), .out(multiplexer_44_out));
  Multiplexer #(.Bits(9)) multiplexer_45 (
    .sel(register_23_q[1]), .in_0(CT_ALU__CT), .in_1(register_40_q), .out(multiplexer_45_out));
  Multiplexer #(.Bits(8)) multiplexer_46 (
    .sel(register_23_q[1]), .in_0(CT_FU__WR), .in_1(register_41_q), .out(multiplexer_46_out));
  Register register_48 (.D(and_90_out), .C(C_ct), .en(or_41_out), .Q(register_48_q[2]));
  or or_41 (or_41_out, not_23_out, multiplexer_47_out[2]);
  Multiplexer #(.Bits(3)) multiplexer_47 (
    .sel(or_42_out), .in_0(not_21_out), .in_1(and_95_out), .out(multiplexer_47_out));
  or or_42 (or_42_out, and_95_out[0], and_95_out[1], and_95_out[2]);
  Multiplexer #(.Bits(4)) multiplexer_48 (
    .sel(register_48_q[2]), .in_0(CT_FU__INST), .in_1(register_42_q), .out(multiplexer_48_out));
  inst_comp inst_comp_4 (
    .A_id(register_42_q), .A_ep(register_43_q), .B_id(clr_id), .B_ep(clr_ep), .A_new(inst_comp_4_a_new));
  Multiplexer multiplexer_49 (
    .sel(register_48_q[2]), .in_0(CT_FU__EPOCH), .in_1(register_43_q), .out(multiplexer_49_out));
  Multiplexer #(.Bits(32)) multiplexer_50 (
    .sel(register_48_q[2]), .in_0(multiplexer_34_out), .in_1(register_44_q), .out(multiplexer_50_out));
  Multiplexer #(.Bits(8)) multiplexer_51 (
    .sel(register_48_q[2]), .in_0(CT_FU__WR), .in_1(register_45_q), .out(multiplexer_51_out));
  Multiplexer multiplexer_52 (.sel(register_48_q[2]), .in_0(CT_FU__EX), .in_1(register_46_q), .out(multiplexer_52_out));
  and and_92 (MB_LD, MB_free, CT_MB__LD);
  Register register_49 (.D(CT_MB__LD), .C(C_ct), .en(1'b1), .Q(register_49_q));
  Register #(.Bits(4)) register_50 (.D(CT_FU__INST), .C(C_ct), .en(MB_LD), .Q(MB_INST));
  Register register_51 (.D(CT_FU__EPOCH), .C(C_ct), .en(MB_LD), .Q(MB_ep));
  Register register_52 (.D(CT_MB__ST), .C(C_ct), .en(MB_LD), .Q(MB_type__st));
  Register #(.Bits(32)) register_53 (.D(multiplexer_35_out), .C(C), .en(MB_LD), .Q(MB_data));
  Register #(.Bits(32)) register_54 (.D(multiplexer_36_out), .C(C), .en(MB_LD), .Q(register_54_q));
  Register #(.Bits(16)) register_55 (.D(multiplexer_37_out), .C(C), .en(MB_LD), .Q(register_55_q));
  Register #(.Bits(2)) register_56 (.D({multiplexer_15_out[1], and_88_out[0]}), .C(C_ct), .en(MB_LD), .Q(MB_MD));
  Register #(.Bits(8)) register_57 (.D(CT_FU__WR), .C(C_ct), .en(MB_LD), .Q(MB_WR));
  Register register_58 (.D(CT_FU__MF), .C(C_ct), .en(MB_LD), .Q(MB_MF));
  Register #(.Bits(32)) register_59 (.D(pc_read), .C(C), .en(MB_LD), .Q(MB_PC));
  Multiplexer #(.Bits(32)) multiplexer_53 (.sel(CT_ISCM), .in_0(SCS), .in_1(ISC), .out(multiplexer_53_out));
  Multiplexer multiplexer_54 (
    .sel(and_91_out[0]), .in_0(nand_1_out[0]), .in_1(nand_1_out[1]), .out(multiplexer_54_out));
  Multiplexer multiplexer_55 (
    .sel(register_23_q[1]), .in_0(CT_ALU__LD), .in_1(register_47_q[1]), .out(multiplexer_55_out));
  and and_93 (and_93_out, multiplexer_54_out, multiplexer_55_out);
  nand nand_2 (nand_2_out[2], ALU_busy, register_47_q[1], register_23_q[2]);
  nand nand_3 (nand_1_out[1], inst_comp_3_a_new, register_47_q[1], clr);
  Register #(.Bits(4)) register_60 (.D(multiplexer_38_out), .C(C_ct), .en(ALU_A_LD), .Q(ALU_A_INST));
  Register register_61 (.D(multiplexer_39_out), .C(C_ct), .en(ALU_A_LD), .Q(register_61_q));
  Register #(.Bits(32)) register_62 (.D(multiplexer_42_out), .C(C), .en(ALU_A_LD), .Q(ALU_A_A));
  Register #(.Bits(32)) register_63 (.D(multiplexer_43_out), .C(C), .en(ALU_A_LD), .Q(ALU_A_B));
  Register #(.Bits(8)) register_64 (.D(multiplexer_44_out), .C(C), .en(ALU_A_LD), .Q(ALU_A_FI));
  Register #(.Bits(9)) register_65 (.D(multiplexer_45_out), .C(C_ct), .en(ALU_A_LD), .Q(ALU_A_CT));
  Register #(.Bits(8)) register_66 (.D(multiplexer_46_out), .C(C_ct), .en(ALU_A_LD), .Q({ALU_A_WR, ALU_A_RM}));
  Multiplexer multiplexer_56 (
    .sel(and_95_out[1]), .in_0(nand_4_out[1]), .in_1(nand_4_out[2]), .out(multiplexer_56_out));
  Multiplexer multiplexer_57 (
    .sel(register_48_q[2]), .in_0(CT_DIR__LD), .in_1(register_48_q[2]), .out(multiplexer_57_out));
  and and_94 (and_94_out, multiplexer_56_out, multiplexer_57_out);
  not not_24 (not_24_out, multiplexer_56_out);
  nand nand_4 (nand_4_out[2], inst_comp_4_a_new, register_48_q[2], clr);
  Register #(.Bits(4)) register_67 (.D(multiplexer_48_out), .C(C_ct), .en(multiplexer_47_out[1]), .Q(register_67_q));
  Register register_68 (.D(multiplexer_49_out), .C(C_ct), .en(multiplexer_47_out[1]), .Q(register_68_q));
  Register #(.Bits(32)) register_69 (.D(multiplexer_50_out), .C(C), .en(multiplexer_47_out[1]), .Q(register_69_q));
  Register #(.Bits(8)) register_70 (.D(multiplexer_51_out), .C(C_ct), .en(multiplexer_47_out[1]), .Q(register_70_q));
  Register register_71 (.D(multiplexer_52_out), .C(C_ct), .en(multiplexer_47_out[1]), .Q(register_71_q));
  Multiplexer #(.Bits(32)) multiplexer_58 (
    .sel(clr), .in_0(multiplexer_53_out), .in_1(CT_SC__FD), .out(multiplexer_58_out));
  nand nand_5 (nand_2_out[1], ALU_busy, register_47_q[1]);
  Register register_72 (.D(and_94_out), .C(C_ct), .en(or_43_out), .Q(register_72_q[1]));
  or or_43 (or_43_out, not_24_out, multiplexer_47_out[1]);
  or or_44 (register_48_q[1], register_72_q[1], register_48_q[2]);
  assign and_95_out = nand_8_out & register_48_q;  // And and_95, 3 bits wide
  Multiplexer #(.Bits(4)) multiplexer_59 (
    .sel(register_48_q[1]), .in_0(CT_FU__INST), .in_1(register_67_q), .out(multiplexer_59_out));
  inst_comp inst_comp_5 (
    .A_id(register_67_q), .A_ep(register_68_q), .B_id(clr_id), .B_ep(clr_ep), .A_new(inst_comp_5_a_new));
  Multiplexer multiplexer_60 (
    .sel(register_48_q[1]), .in_0(CT_FU__EPOCH), .in_1(register_68_q), .out(multiplexer_60_out));
  Multiplexer #(.Bits(32)) multiplexer_61 (
    .sel(register_48_q[1]), .in_0(multiplexer_34_out), .in_1(register_69_q), .out(multiplexer_61_out));
  Multiplexer #(.Bits(8)) multiplexer_62 (
    .sel(register_48_q[1]), .in_0(CT_FU__WR), .in_1(register_70_q), .out(multiplexer_62_out));
  Multiplexer multiplexer_63 (.sel(register_48_q[1]), .in_0(CT_FU__EX), .in_1(register_71_q), .out(multiplexer_63_out));
  and and_96 (MB_MFE, MB_MF, register_49_q);
  and and_97 (MB_st__e, register_49_q, MB_type__st);
  and and_98 (MB_ld__e, register_49_q, ~MB_type__st);  // And
  add_s16c32 add_s16c32_1 (.a(register_54_q), .b(register_55_q), .s(MB_addr));  // open: c
  addsub_4c32 addsub_4c32_1 (.a(multiplexer_58_out), .b({1'b0, CT_RF__SCN}), .sub(CT_RF__SCD), .s(ISC_sc));  // open: c
  assign CT_RF__SCSE = clr ? 1'b1 : 1'bz;  // Driver driver_134
  assign CT_RF__SCSS = clr ? 1'b1 : 1'bz;  // Driver driver_135
  not not_25 (nand_2_out[0], ALU_busy);
  nand nand_6 (nand_1_out[0], or_47_out, ALU_busy, clr);
  inst_comp inst_comp_6 (.A_id(ALU_A_INST), .A_ep(register_61_q), .B_id(clr_id), .B_ep(clr_ep), .A_new(ALU_A_CMP));
  Multiplexer multiplexer_64 (
    .sel(and_95_out[0]), .in_0(nand_4_out[0]), .in_1(nand_4_out[1]), .out(multiplexer_64_out));
  Multiplexer multiplexer_65 (
    .sel(register_48_q[1]), .in_0(CT_DIR__LD), .in_1(register_72_q[1]), .out(multiplexer_65_out));
  and and_99 (and_99_out, multiplexer_64_out, multiplexer_65_out);
  or or_45 (register_48_q[0], DIR_busy, register_72_q[1], register_48_q[2]);
  nand nand_7 (nand_4_out[1], inst_comp_5_a_new, register_72_q[1], clr);
  Register #(.Bits(4)) register_73 (.D(multiplexer_59_out), .C(C_ct), .en(DIR_LD), .Q(DIR_INST));
  Register register_74 (.D(multiplexer_60_out), .C(C_ct), .en(DIR_LD), .Q(register_74_q));
  Register #(.Bits(32)) register_75 (.D(multiplexer_61_out), .C(C), .en(DIR_LD), .Q(DIR));
  Register #(.Bits(8)) register_76 (.D(multiplexer_62_out), .C(C_ct), .en(DIR_LD), .Q(DIR_WR));
  Register register_77 (.D(multiplexer_63_out), .C(C_ct), .en(DIR_LD), .Q(DIR_EX));
  Register #(.Bits(4)) register_78 (.D(multiplexer_38_out), .C(C_ct), .en(ALU_B_LD), .Q(ALU_B_INST));
  Register register_79 (.D(multiplexer_39_out), .C(C_ct), .en(ALU_B_LD), .Q(register_79_q));
  Register #(.Bits(32)) register_80 (.D(multiplexer_42_out), .C(C), .en(ALU_B_LD), .Q(ALU_B_A));
  Register #(.Bits(32)) register_81 (.D(multiplexer_43_out), .C(C), .en(ALU_B_LD), .Q(ALU_B_B));
  Register #(.Bits(8)) register_82 (.D(multiplexer_44_out), .C(C), .en(ALU_B_LD), .Q(ALU_B_FI));
  Register #(.Bits(9)) register_83 (.D(multiplexer_45_out), .C(C_ct), .en(ALU_B_LD), .Q(ALU_B_CT));
  Register #(.Bits(8)) register_84 (.D(multiplexer_46_out), .C(C_ct), .en(ALU_B_LD), .Q({ALU_B_WR, ALU_B_RM}));
  nand nand_8 (nand_8_out[2], DIR_busy, register_72_q[1], register_48_q[2]);
  and and_100 (LDB_forward, MB_ld__e, LDB_ldV);
  or or_46 (or_46_out, MEM_LD__RD, LDB_forward);
  and and_101 (and_101_out[0], ALU_A_LD, multiplexer_40_out);
  BitExtender #(.inputBits(1), .outputBits(2)) bitextender_6 (.in(ALU_A_CLR), .out(bitextender_6_out));
  and and_102 (and_101_out[1], ALU_A_LD, multiplexer_41_out);
  and and_103 (and_103_out[0], ALU_B_LD, multiplexer_40_out);
  BitExtender #(.inputBits(1), .outputBits(2)) bitextender_7 (.in(ALU_B_CLR), .out(bitextender_7_out));
  and and_104 (and_103_out[1], ALU_B_LD, multiplexer_41_out);
  or or_47 (or_47_out, ALU_A_CMP, ALU_B_CMP);
  nand nand_9 (nand_8_out[1], DIR_busy, register_72_q[1]);
  not not_26 (nand_8_out[0], DIR_busy);
  inst_comp inst_comp_7 (
    .A_id(DIR_INST), .A_ep(register_74_q), .B_id(clr_id), .B_ep(clr_ep), .A_new(inst_comp_7_a_new));
  and and_105 (and_105_out, CT_ISS__OSTB, ~clr);  // And
  Multiplexer #(.Bits(32)) multiplexer_66 (
    .sel(LDB_forward), .in_0(MEM_LD__D), .in_1(LDB_ldD), .out(multiplexer_66_out));
  Multiplexer #(.Bits(4)) multiplexer_67 (
    .sel(LDB_forward), .in_0(MEM_LD__INST), .in_1(MB_INST), .out(multiplexer_67_out));
  and and_106 (and_106_out, CT_ISS__OLDB, ~clr);  // And
  and and_107 (and_107_out, ~and_101_out[0], ALU_A_STD);  // And
  and and_108 (and_108_out, ~and_101_out[1], ALU_A_STF);  // And
  and and_109 (and_109_out, ~and_103_out[0], ALU_B_STD);  // And
  and and_110 (and_110_out, ~and_103_out[1], ALU_B_STF);  // And
  inst_comp inst_comp_8 (.A_id(ALU_B_INST), .A_ep(register_79_q), .B_id(clr_id), .B_ep(clr_ep), .A_new(ALU_B_CMP));
  nand nand_10 (nand_4_out[0], inst_comp_7_a_new, DIR_busy, clr);
  and and_111 (and_111_out, byte_I0[3], byte_I0[0]);
  and and_112 (and_112_out, byte_I0[2], byte_I0[0]);
  and and_113 (and_113_out, byte_I0_iv[3], byte_I0_iv[2], byte_I0[1], byte_I0_iv[0]);
  and and_114 (and_114_out, byte_I0_iv[2], byte_I0_iv[0]);
  and and_115 (and_115_out, byte_I0[2], byte_I0[0]);
  and and_116 (and_116_out, byte_I0[1], byte_I0[2], byte_I0[4]);
  and and_117 (and_117_out, byte_I0[3], byte_I0[4]);
  D_FF #(.Bits(2)) d_ff_19 (.D(and_101_out), .C(C_ct), .Q(d_ff_19_q));  // open: nQ
  assign and_118_out = d_ff_19_q & ~bitextender_6_out;  // And and_118, 2 bits wide
  RS_FF rs_ff_8 (.S(and_101_out[0]), .C(C_ct), .R(and_107_out), .nQ(rs_ff_8_nq));  // open: Q
  RS_FF rs_ff_9 (.S(and_101_out[1]), .C(C_ct), .R(and_108_out), .nQ(rs_ff_9_nq));  // open: Q
  D_FF #(.Bits(2)) d_ff_20 (.D(and_103_out), .C(C_ct), .Q(d_ff_20_q));  // open: nQ
  assign and_119_out = d_ff_20_q & ~bitextender_7_out;  // And and_119, 2 bits wide
  RS_FF rs_ff_10 (.S(and_103_out[0]), .C(C_ct), .R(and_109_out), .nQ(rs_ff_10_nq));  // open: Q
  RS_FF rs_ff_11 (.S(and_103_out[1]), .C(C_ct), .R(and_110_out), .nQ(rs_ff_11_nq));  // open: Q
  and and_120 (and_120_out, ~and_99_out, DIR_ST);  // And
  and and_121 (DIR_CLR, clr, inst_comp_7_a_new);
  store_buffer store_buffer_1 (
    .C(C), .LD(MB_STB__LD), .W_d(MB_st__e), .inst_W(MB_INST), .D(MB_data), .A(MB_addr), .MD(MB_MD),
    .W_id(and_105_out), .epoch(epoch_IS), .inst(inst_IS), .com1(com1), .com2(com2), .com1_id(com1_inst),
    .com2_id(com2_inst), .ld_ep(MB_ep), .ld_id(MB_INST), .ld_addr(MB_addr), .clr(clr), .clr_ep(clr_ep),
    .clr_id(clr_id), .full(store_buffer_1_full), .V(STB_M__V), .D_O(STB_M__D), .A_O(STB_M__A),
    .MD_O(STB_M__MD), .id_O(STB_M__ID), .ep_O(STB_M__EP), .ld_V(LDB_ldV), .ld_D(LDB_ldD));
  load_buffer load_buffer_1 (
    .C(C), .LD(MB_LDB__LD), .LDB(FU_D__V[3]), .W_d(or_46_out), .inst_WD(multiplexer_67_out),
    .D(multiplexer_66_out), .W_a(MB_ld__e), .WC_a(LDB_forward), .inst_WA(MB_INST), .A(MB_addr), .MD(MB_MD),
    .MF(MB_MF), .WR(MB_WR), .PC(MB_PC), .W_id(and_106_out), .epoch(epoch_IS), .inst(inst_IS), .com1(com1),
    .com2(com2), .com1_id(com1_inst), .com2_id(com2_inst), .st(MB_st__e), .st_ep(MB_ep), .st_id(MB_INST),
    .st_addr(MB_addr), .st_data(MB_data), .clr(clr), .clr_ep(clr_ep), .clr_id(clr_id),
    .full(load_buffer_1_full), .V(load_buffer_1_v), .D_O(LDB_B__D), .id_O(load_buffer_1_id_o),
    .WR_O(load_buffer_1_wr_o), .MF_O(load_buffer_1_mf_o), .M_V(LDB_M__V), .M_A(LDB_M__A), .M_MD(LDB_M__MD),
    .M_id(LDB_M__ID), .M_ep(LDB_M__EP), .fl(load_buffer_1_fl), .fl_ep(load_buffer_1_fl_ep),
    .fl_id(load_buffer_1_fl_id), .fl_PC(load_buffer_1_fl_pc));
  and and_122 (and_122_out, byte_I0_iv[7], byte_I0_iv[6], byte_I0[5], issue_e);
  and and_123 (and_123_out, byte_I0_iv[7], byte_I0[6], byte_I0_iv[5], issue_e);
  D_FF #(.Bits(2)) d_ff_21 (.D(and_118_out), .C(C_ct), .Q(d_ff_21_q));  // open: nQ
  and and_124 (ALU_A_UUD, rs_ff_8_nq, ALU_A_V);
  and and_125 (ALU_A_UUF, rs_ff_9_nq, ALU_A_V);
  D_FF #(.Bits(2)) d_ff_22 (.D(and_119_out), .C(C_ct), .Q(d_ff_22_q));  // open: nQ
  and and_126 (ALU_B_UUD, rs_ff_10_nq, ALU_B_V);
  and and_127 (ALU_B_UUF, rs_ff_11_nq, ALU_B_V);
  or or_48 (or_48_out, ALU_A_CLR, and_147_out);
  or or_49 (or_49_out, ALU_B_CLR, and_148_out);
  alu_32 alu_32_1 (
    .A(ALU_A_A), .B(ALU_A_B), .F_I(ALU_A_FI), .CT(ALU_A_CT), .RM(ALU_A_RM), .E(pulldown_18_out),
    .R_O(ALU_A_R), .F_O(ALU_A_F));  // open: E_A, E_B
  alu_32 alu_32_2 (
    .A(ALU_B_A), .B(ALU_B_B), .F_I(ALU_B_FI), .CT(ALU_B_CT), .RM(ALU_B_RM), .E(pulldown_19_out),
    .R_O(ALU_B_R), .F_O(ALU_B_F));  // open: E_A, E_B
  RS_FF rs_ff_12 (.S(and_99_out), .C(C_ct), .R(and_120_out), .nQ(rs_ff_12_nq));  // open: Q
  D_FF V (.D(DIR_LD), .C(C_ct), .Q(V_q));  // open: nQ
  bus16x2_demux bus16x2_demux_3 (.bus_1(V1_inst), .bus_2(V2_inst), .E(DIR_V), .id(DIR_INST));
  and and_128 (and_128_out, issue_e, byte_I0[4], byte_I0[3], byte_I0_iv[1], byte_I0_iv[2], byte_I0_iv[5], byte_I0_iv[6], byte_I0_iv[7]);
  or or_50 (or_50_out, and_111_out, and_112_out, and_113_out);
  nor nor_7 (nor_7_out, byte_I0[3], byte_I0[1], and_114_out, and_115_out);
  nor nor_8 (nor_8_out, and_116_out, and_117_out);
  and and_129 (and_129_out, byte_I0_iv[0], byte_I0_iv[1], byte_I0[2], byte_I0[3], byte_I0[4], byte_I0_iv[5], byte_I0_iv[6], byte_I0_iv[7], issue_e);
  and and_130 (and_130_out, byte_I0[1], byte_I0_iv[2], byte_I0[3], byte_I0[4], byte_I0_iv[5], byte_I0_iv[6], byte_I0_iv[7], issue_e);
  and and_131 (and_131_out, byte_I0_iv[4], byte_I0[5], byte_I0[6], byte_I0_iv[7], issue_e);
  assign {ALU_A_FRE, ALU_A_DRE} = d_ff_21_q & ~bitextender_6_out;  // And and_132, 2 bits wide
  assign {ALU_B_FRE, ALU_B_DRE} = d_ff_22_q & ~bitextender_7_out;  // And and_133, 2 bits wide
  and and_134 (and_134_out, ALU_A_VD, ~or_48_out);  // And
  and and_135 (and_135_out, ALU_A_VF, ~or_48_out);  // And
  and and_136 (and_136_out, ALU_B_VD, ~or_49_out);  // And
  and and_137 (and_137_out, ALU_B_VF, ~or_49_out);  // And
  PullDown #(.Bits(32)) pulldown_18 (.out(pulldown_18_out));
  PullDown #(.Bits(32)) pulldown_19 (.out(pulldown_19_out));
  or or_51 (DIR_free, DIR_ST, rs_ff_12_nq);
  and and_138 (DIR_RD, V_q, ~DIR_CLR);  // And
  D_FF d_ff_23 (.D(store_buffer_1_full), .C(C_ct), .Q(STB_busy));  // open: nQ
  D_FF d_ff_24 (.D(load_buffer_1_full), .C(C_ct), .Q(LDB_busy));  // open: nQ
  D_FF #(.Bits(4)) d_ff_25 (.D(load_buffer_1_id_o), .C(C_ct), .Q(LDB_B__INST));  // open: nQ
  D_FF d_ff_26 (.D(load_buffer_1_mf_o), .C(C_ct), .Q(LDB_B__MF));  // open: nQ
  D_FF d_ff_27 (.D(load_buffer_1_fl), .C(C_ct), .Q(Fl_MEM));  // open: nQ
  D_FF #(.Bits(4)) d_ff_28 (.D(load_buffer_1_fl_id), .C(C_ct), .Q(FL_MEM__ID));  // open: nQ
  and and_139 (and_139_out, byte_I0[1], byte_I0[2], byte_I0[3], byte_I0[4], byte_I0_iv[5], byte_I0_iv[6], byte_I0_iv[7], issue_e);
  or or_52 (or_52_out, and_122_out, and_123_out);
  Comparator #(.Bits(3)) comparator_7 (.a(byte_I0[2:0]), .b(3'b110), .eq(comparator_7_eq));  // open: gt, lt
  RS_FF rs_ff_13 (.S(ALU_A_DRE), .C(C_ct), .R(ALU_A_DRD), .Q(ALU_A_DRD));  // open: nQ
  RS_FF rs_ff_14 (.S(ALU_A_FRE), .C(C_ct), .R(ALU_A_FRD), .Q(ALU_A_FRD));  // open: nQ
  RS_FF rs_ff_15 (.S(ALU_B_DRE), .C(C_ct), .R(ALU_B_DRD), .Q(ALU_B_DRD));  // open: nQ
  RS_FF rs_ff_16 (.S(ALU_B_FRE), .C(C_ct), .R(ALU_B_FRD), .Q(ALU_B_FRD));  // open: nQ
  RS_FF rs_ff_17 (.S(and_134_out), .C(C_ct), .R(or_48_out), .Q(rs_ff_17_q));  // open: nQ
  RS_FF rs_ff_18 (.S(and_135_out), .C(C_ct), .R(or_48_out), .Q(rs_ff_18_q));  // open: nQ
  RS_FF rs_ff_19 (.S(and_136_out), .C(C_ct), .R(or_49_out), .Q(rs_ff_19_q));  // open: nQ
  RS_FF rs_ff_20 (.S(and_137_out), .C(C_ct), .R(or_49_out), .Q(rs_ff_20_q));  // open: nQ
  D_FF #(.Bits(8)) d_ff_29 (.D(load_buffer_1_wr_o), .C(C_ct), .Q(LDB_B__WR));  // open: nQ
  D_FF d_ff_30 (.D(load_buffer_1_fl_ep), .C(C_ct), .Q(FL_MEM__EP));  // open: nQ
  D_FF #(.Bits(32)) d_ff_31 (.D(load_buffer_1_fl_pc), .C(C_ct), .Q(MEM_FPC));  // open: nQ
  and and_140 (and_140_out, byte_I0_iv[7], byte_I0_iv[6], issue_e, byte_I0_iv[5], byte_I0_iv[4]);
  and and_141 (and_141_out, byte_I0_iv[7], byte_I0_iv[6], byte_I0_iv[5], byte_I0[4], byte_I0_iv[3], issue_e);
  or or_53 (or_53_out, and_129_out, and_130_out);
  and and_142 (and_142_out, byte_I0[0], byte_I0_iv[1], byte_I0[2], byte_I0[3], byte_I0[4], byte_I0_iv[5], byte_I0_iv[6], byte_I0_iv[7], issue_e);
  not not_27 (not_27_out, comparator_7_eq);
  or or_54 (or_54_out, ALU_A_VD, ALU_A_UUD, rs_ff_17_q);
  or or_55 (or_55_out, ALU_A_VF, ALU_A_UUF, rs_ff_18_q);
  or or_56 (or_56_out, ALU_B_VD, ALU_B_UUD, rs_ff_19_q);
  or or_57 (or_57_out, ALU_B_VF, ALU_B_UUF, rs_ff_20_q);
  and and_143 (DIR_LD, and_99_out, DIR_free);
  not not_28 (DIR_busy, DIR_free);
  and and_144 (and_144_out, d_ff_32_q, ~FU_D__V[3]);  // And
  not not_29 (not_29_out, or_50_out);
  and and_145 (and_145_out, and_139_out, byte_I0[0]);
  and and_146 (and_146_out, byte_I0_iv[0], and_139_out);
  or or_58 (or_58_out, ALU_A_STD, rs_ff_8_nq);
  or or_59 (or_59_out, ALU_A_STF, rs_ff_9_nq);
  or or_60 (or_60_out, ALU_B_STD, rs_ff_10_nq);
  or or_61 (or_61_out, ALU_B_STF, rs_ff_11_nq);
  and and_147 (and_147_out, or_54_out, ~ALU_A_CLR, or_55_out);  // And
  bus16x2_demux bus16x2_demux_4 (.bus_1(V1_inst), .bus_2(V2_inst), .E(and_147_out), .id(ALU_A_INST));
  and and_148 (and_148_out, or_56_out, ~ALU_B_CLR, or_57_out);  // And
  bus16x2_demux bus16x2_demux_5 (.bus_1(V1_inst), .bus_2(V2_inst), .E(and_148_out), .id(ALU_B_INST));
  nor nor_9 (ALU_busy, ALU_A_LRD, ALU_B_LRD);
  or or_62 (ALU_free, ALU_A_LRD, ALU_B_LRD);
  Register #(.Bits(32)) register_85 (.D(ALU_A_R), .C(C), .en(ALU_A_DRE), .Q(ALU_A_T__R));
  Register #(.Bits(8)) register_86 (.D(ALU_A_F), .C(C), .en(ALU_A_FRE), .Q(ALU_A_T__F));
  Register #(.Bits(32)) register_87 (.D(ALU_B_R), .C(C), .en(ALU_B_DRE), .Q(ALU_B_T__R));
  Register #(.Bits(8)) register_88 (.D(ALU_B_F), .C(C), .en(ALU_B_FRE), .Q(ALU_B_T__F));
  and and_149 (and_149_out, ~MB_MF, MB_st__e);  // And
  and and_150 (and_150_out, ~LDB_B__MF, FU_D__V[3]);  // And
  D_FF d_ff_32 (.D(load_buffer_1_v), .C(C_ct), .Q(d_ff_32_q));  // open: nQ
  D_FF d_ff_33 (.D(and_144_out), .C(C_ct), .nQ(d_ff_33_nq));  // open: Q
  and and_151 (LDB_B__RD, d_ff_32_q, d_ff_33_nq);
  or or_63 (or_63_out, and_140_out, and_128_out, and_141_out);
  assign issue = or_63_out ? 1'b1 : 1'bz;  // Driver driver_136
  assign CT_ISS__URA = or_63_out ? 1'b1 : 1'bz;  // Driver driver_137
  assign CT_ISS__URB = or_63_out ? not_29_out : 1'bz;  // Driver driver_138
  assign CT_ISS__RA = or_63_out ? byte_I1[7:3] : 5'bz;  // Driver driver_139
  assign CT_ISS__RB = or_63_out ? byte_I2[7:3] : 5'bz;  // Driver driver_140
  assign CT_ISS__UFL = or_63_out ? nor_7_out : 1'bz;  // Driver driver_141
  assign CT_ISS__ORC = or_63_out ? nor_8_out : 1'bz;  // Driver driver_142
  assign CT_ISS__RC = or_63_out ? byte_I1[7:3] : 5'bz;  // Driver driver_143
  assign CT_ISS__OFL = or_63_out ? 1'b1 : 1'bz;  // Driver driver_144
  assign CT_ISS__UFU = or_63_out ? 3'b001 : 3'bz;  // Driver driver_145
  assign CT_ISS__URA = and_129_out ? 1'b1 : 1'bz;  // Driver driver_146
  assign CT_ISS__RA = and_129_out ? byte_I2[7:3] : 5'bz;  // Driver driver_147
  assign issue = or_53_out ? 1'b1 : 1'bz;  // Driver driver_148
  assign CT_ISS__ORC = or_53_out ? 1'b1 : 1'bz;  // Driver driver_149
  assign CT_ISS__RC = or_53_out ? byte_I1[7:3] : 5'bz;  // Driver driver_150
  assign CT_ISS__UFU = or_53_out ? 3'b010 : 3'bz;  // Driver driver_151
  assign issue = and_139_out ? 1'b1 : 1'bz;  // Driver driver_152
  assign CT_ISS__URB = and_139_out ? 1'b1 : 1'bz;  // Driver driver_153
  assign CT_ISS__RB = and_139_out ? 5'b11110 : 5'bz;  // Driver driver_154
  assign CT_ISS__OSC = and_139_out ? 1'b1 : 1'bz;  // Driver driver_155
  assign CT_ISS__UMM = and_139_out ? 1'b1 : 1'bz;  // Driver driver_156
  assign CT_ISS__UFU = and_139_out ? 3'b011 : 3'bz;  // Driver driver_157
  assign CT_ISS__URA = and_145_out ? 1'b1 : 1'bz;  // Driver driver_158
  assign CT_ISS__RA = and_145_out ? byte_I1[7:3] : 5'bz;  // Driver driver_159
  assign CT_ISS__OSTB = and_145_out ? 1'b1 : 1'bz;  // Driver driver_160
  assign CT_ISS__ORC = and_146_out ? 1'b1 : 1'bz;  // Driver driver_161
  assign CT_ISS__RC = and_146_out ? byte_I1[7:3] : 5'bz;  // Driver driver_162
  assign CT_ISS__OLDB = and_146_out ? 1'b1 : 1'bz;  // Driver driver_163
  assign issue = or_52_out ? 1'b1 : 1'bz;  // Driver driver_164
  assign CT_ISS__URA = or_52_out ? 1'b1 : 1'bz;  // Driver driver_165
  assign CT_ISS__RA = or_52_out ? byte_I0[4:0] : 5'bz;  // Driver driver_166
  assign CT_ISS__UMM = or_52_out ? 1'b1 : 1'bz;  // Driver driver_167
  assign CT_ISS__UFU = or_52_out ? 3'b011 : 3'bz;  // Driver driver_168
  assign CT_ISS__URB = and_123_out ? 1'b1 : 1'bz;  // Driver driver_169
  assign CT_ISS__RB = and_123_out ? byte_I1[7:3] : 5'bz;  // Driver driver_170
  assign CT_ISS__ORC = and_122_out ? 1'b1 : 1'bz;  // Driver driver_171
  assign CT_ISS__RC = and_122_out ? byte_I1[7:3] : 5'bz;  // Driver driver_172
  assign CT_ISS__OLDB = and_122_out ? 1'b1 : 1'bz;  // Driver driver_173
  assign CT_ISS__OSTB = and_123_out ? 1'b1 : 1'bz;  // Driver driver_174
  assign issue = and_142_out ? 1'b1 : 1'bz;  // Driver driver_175
  assign CT_BLOCK = and_142_out ? 1'b1 : 1'bz;  // Driver driver_176
  assign CT_UBTB = and_131_out ? 1'b1 : 1'bz;  // Driver driver_177
  assign issue = and_131_out ? 1'b1 : 1'bz;  // Driver driver_178
  assign CT_ISS__URA = and_131_out ? 1'b1 : 1'bz;  // Driver driver_179
  assign CT_ISS__RA = and_131_out ? byte_I1[7:3] : 5'bz;  // Driver driver_180
  assign CT_ISS__UFL = and_131_out ? not_27_out : 1'bz;  // Driver driver_181
  assign CT_ISS__UFU = and_131_out ? 3'b111 : 3'bz;  // Driver driver_182
  and and_152 (and_152_out, com1, CT_FL__W1);
  and and_153 (and_153_out, com2, CT_FL__W2);
  DipSwitch dipswitch_4 (.out(MB_busy));
  assign CT_RF__PCSE = Fl_MEM ? 1'b1 : 1'bz;  // Driver driver_183
  assign CT_RF__PCJ = Fl_MEM ? 1'b1 : 1'bz;  // Driver driver_184
  Multiplexer #(.Bits(8)) multiplexer_68 (.sel(and_153_out), .in_0(CT_FL__D1), .in_1(CT_FL__D2), .out(fl_i));
  and and_154 (ALU_A_LD, and_93_out, or_59_out, or_58_out);
  and and_155 (ALU_A_LRD, or_58_out, or_59_out);
  nand nand_11 (nand_11_out, or_58_out, or_59_out);
  and and_156 (ALU_B_LD, nand_11_out, and_93_out, or_61_out, or_60_out);
  and and_157 (ALU_B_LRD, or_60_out, or_61_out);
  and and_158 (and_158_out, ~ALU_A_LD, or_48_out);  // And
  and and_159 (and_159_out, ~ALU_B_LD, or_49_out);  // And
  bus16_demux bus16_demux_2 (.bus(V1_inst), .E(MB_st__e), .id(MB_INST));
  bus16_demux bus16_demux_3 (.bus(V2_inst), .E(and_149_out), .id(MB_INST));
  bus16_demux bus16_demux_4 (.bus(V1_inst), .E(FU_D__V[3]), .id(LDB_B__INST));
  bus16_demux bus16_demux_5 (.bus(V2_inst), .E(and_150_out), .id(LDB_B__INST));
  not not_30 (MB_free, MB_busy);
  or or_64 (CT_RF__FLS, and_152_out, and_153_out);
  and and_160 (ALU_A_CLR, clr, ALU_A_CMP);
  and and_161 (ALU_B_CLR, clr, ALU_B_CMP);
  RS_FF rs_ff_21 (.S(ALU_A_LD), .C(C_ct), .R(and_158_out), .Q(ALU_A_V));  // open: nQ
  RS_FF rs_ff_22 (.S(ALU_B_LD), .C(C_ct), .R(and_159_out), .Q(ALU_B_V));  // open: nQ
  and and_162 (and_162_out, byte_I0[1], byte_I0_iv[2], byte_I0[3], byte_I0[4], byte_I0[5], byte_I0[6], byte_I0_iv[7], issue_e);
  and and_163 (and_163_out, byte_I0_iv[0], byte_I0_iv[1], byte_I0_iv[2], byte_I0_iv[3], byte_I0[4], byte_I0[5], byte_I0[6], byte_I0_iv[7], issue_e);
  and and_164 (and_164_out, byte_I0[0], byte_I0_iv[1], byte_I0_iv[2], byte_I0_iv[3], byte_I0[4], byte_I0[5], byte_I0[6], byte_I0_iv[7], issue_e);
  and and_165 (and_165_out, byte_I0_iv[1], byte_I0[2], byte_I0_iv[3], byte_I0[4], byte_I0[5], byte_I0[6], byte_I0_iv[7], issue_e);
  and and_166 (and_166_out, byte_I0[0], and_162_out);
  and and_167 (and_167_out, and_162_out, byte_I0_iv[0]);
  and and_168 (and_168_out, byte_I0_iv[0], byte_I0[1], byte_I0[2], byte_I0_iv[3], byte_I0[4], byte_I0[5], byte_I0[6], byte_I0_iv[7], issue_e);
  and and_169 (and_169_out, byte_I0[0], byte_I0[1], byte_I0[2], byte_I0_iv[3], byte_I0[4], byte_I0[5], byte_I0[6], byte_I0_iv[7], issue_e);
  and and_170 (and_170_out, byte_I0_iv[1], byte_I0_iv[2], byte_I0[3], byte_I0[4], byte_I0[5], byte_I0[6], byte_I0_iv[7], issue_e);
  store_controller store_controller_1 (
    .C(C_ct), .in1(ALU_A_DRD), .in2(ALU_B_DRD), .in3(DIR_RD), .in4(LDB_B__RD), .in5(1'b0), .in6(1'b0),
    .in7(1'b0), .in8(1'b0), .clr({3'b000, FU_CLR[4], 1'b0, DIR_CLR, ALU_B_CLR, ALU_A_CLR}),
    .D1_sel(store_controller_1_d1_sel), .D2_sel(store_controller_1_d2_sel), .ST1(CT_ROB__GEN__STA),
    .ST2(CT_ROB__GEN__STB), .out1(ALU_A_STD), .out2(ALU_B_STD), .out3(DIR_ST), .out4(LDB_B__ST),
    .V({FU_D__V, DIR_V, ALU_B_VD, ALU_A_VD}));  // open: out5, out6, out7, out8
  store_controller_half store_controller_half_1 (
    .C(C_ct), .in1(ALU_A_FRD), .in2(ALU_B_FRD), .in3(1'b0), .in4(1'b0),
    .clr({1'b0, DIR_CLR, ALU_B_CLR, ALU_A_CLR}), .D1_sel(store_controller_half_1_d1_sel),
    .D2_sel(store_controller_half_1_d2_sel), .ST1(CT_ROB__FL__STA), .ST2(CT_ROB__FL__STB), .out1(ALU_A_STF),
    .out2(ALU_B_STF), .V({FU_F__V, ALU_B_VF, ALU_A_VF}));  // open: out3, out4
  store_controller_half store_controller_half_2 (
    .C(C_ct), .in1(TRAP_IRD), .in2(1'b0), .in3(1'b0), .in4(1'b0), .clr({3'b000, FU_CLR[4]}),
    .D1_sel(store_controller_half_2_d1_sel), .D2_sel(store_controller_half_2_d2_sel), .ST1(CT_ROB__INT__STA),
    .ST2(CT_ROB__INT__STB), .out1(TRAP_ST), .V(FU_I__V));  // open: out2, out3, out4
  Demultiplexer #(.Selector_Bits(4)) demultiplexer_3 (
    .sel(priorityencoder_3_num), .in(and_181_out), .out_0(demultiplexer_3_out_0[0]),
    .out_1(demultiplexer_3_out_0[1]), .out_2(demultiplexer_3_out_0[2]), .out_3(demultiplexer_3_out_0[3]),
    .out_4(demultiplexer_3_out_0[4]), .out_5(demultiplexer_3_out_0[5]), .out_6(demultiplexer_3_out_0[6]),
    .out_7(demultiplexer_3_out_0[7]), .out_8(demultiplexer_3_out_0[8]), .out_9(demultiplexer_3_out_0[9]),
    .out_10(demultiplexer_3_out_0[10]), .out_11(demultiplexer_3_out_0[11]),
    .out_12(demultiplexer_3_out_0[12]), .out_13(demultiplexer_3_out_0[13]),
    .out_14(demultiplexer_3_out_0[14]), .out_15(demultiplexer_3_out_0[15]));
  Demultiplexer #(.Selector_Bits(4)) demultiplexer_4 (
    .sel(CT_FU__INST), .in(CT_RET__LD), .out_0(demultiplexer_4_out_0[0]), .out_1(demultiplexer_4_out_0[1]),
    .out_2(demultiplexer_4_out_0[2]), .out_3(demultiplexer_4_out_0[3]), .out_4(demultiplexer_4_out_0[4]),
    .out_5(demultiplexer_4_out_0[5]), .out_6(demultiplexer_4_out_0[6]), .out_7(demultiplexer_4_out_0[7]),
    .out_8(demultiplexer_4_out_0[8]), .out_9(demultiplexer_4_out_0[9]), .out_10(demultiplexer_4_out_0[10]),
    .out_11(demultiplexer_4_out_0[11]), .out_12(demultiplexer_4_out_0[12]),
    .out_13(demultiplexer_4_out_0[13]), .out_14(demultiplexer_4_out_0[14]), .out_15(demultiplexer_4_out_0[15]));
  or or_65 (or_65_out, JPU_INT, JPU_RET);
  nor nor_10 (nor_10_out, JPU_INT, JPU_RET);
  nor nor_11 (nor_11_out, JPU_INT, JPU_RET);
  assign ISS_kernel = and_165_out ? byte_I0[0] : 1'bz;  // Driver driver_185
  assign CT_ISS__HALT = and_165_out ? 1'b1 : 1'bz;  // Driver driver_186
  assign CT_BLOCK = and_165_out ? 1'b1 : 1'bz;  // Driver driver_187
  assign issue = and_165_out ? 1'b1 : 1'bz;  // Driver driver_188
  assign CT_ISS__UMM = and_165_out ? 1'b1 : 1'bz;  // Driver driver_189
  assign CT_ISS__UFU = and_165_out ? 3'b100 : 3'bz;  // Driver driver_190
  assign CT_ISS__URA = and_166_out ? 1'b1 : 1'bz;  // Driver driver_191
  assign CT_ISS__RA = and_166_out ? byte_I1[7:3] : 5'bz;  // Driver driver_192
  assign ISS_kernel = and_162_out ? 1'b1 : 1'bz;  // Driver driver_193
  assign issue = and_162_out ? 1'b1 : 1'bz;  // Driver driver_194
  assign CT_ISS__UFU = and_162_out ? 3'b010 : 3'bz;  // Driver driver_195
  assign CT_BLOCK = and_162_out ? 1'b1 : 1'bz;  // Driver driver_196
  assign CT_ISS__UMM = and_162_out ? 1'b1 : 1'bz;  // Driver driver_197
  assign CT_ISS__ORC = and_167_out ? 1'b1 : 1'bz;  // Driver driver_198
  assign CT_ISS__RC = and_167_out ? byte_I1[7:3] : 5'bz;  // Driver driver_199
  assign CT_BLOCK = and_168_out ? 1'b1 : 1'bz;  // Driver driver_200
  assign issue = and_168_out ? 1'b1 : 1'bz;  // Driver driver_201
  assign CT_ISS__HALT = and_168_out ? 1'b1 : 1'bz;  // Driver driver_202
  assign CT_ISS__UMM = and_168_out ? 1'b1 : 1'bz;  // Driver driver_203
  assign CT_ISS__UFU = and_168_out ? 3'b100 : 3'bz;  // Driver driver_204
  assign ISS_kernel = and_169_out ? 1'b1 : 1'bz;  // Driver driver_205
  assign CT_BLOCK = and_169_out ? 1'b1 : 1'bz;  // Driver driver_206
  assign issue = and_169_out ? 1'b1 : 1'bz;  // Driver driver_207
  assign CT_ISS__HALT = and_169_out ? 1'b1 : 1'bz;  // Driver driver_208
  assign CT_ISS__UMM = and_169_out ? 1'b1 : 1'bz;  // Driver driver_209
  assign CT_ISS__UFU = and_169_out ? 3'b100 : 3'bz;  // Driver driver_210
  assign CT_BLOCK = and_170_out ? 1'b1 : 1'bz;  // Driver driver_211
  assign issue = and_170_out ? 1'b1 : 1'bz;  // Driver driver_212
  assign CT_ISS__HALT = and_170_out ? 1'b1 : 1'bz;  // Driver driver_213
  assign CT_ISS__UMM = and_170_out ? 1'b1 : 1'bz;  // Driver driver_214
  assign CT_ISS__UFU = and_170_out ? 3'b100 : 3'bz;  // Driver driver_215
  Multiplexer #(.Bits(32)) multiplexer_69 (.sel(JPU_INT), .in_0(CT_RF__DR), .in_1(int_vec_t), .out(multiplexer_69_out));
  BitExtender #(.inputBits(1)) bitextender_8 (.in(nor_10_out), .out(bitextender_8_out));
  BitExtender #(.inputBits(1), .outputBits(37)) bitextender_9 (.in(nor_11_out), .out(bitextender_9_out));
  BitExtender #(.inputBits(1)) bitextender_10 (.in(CT_FU__EPOCH), .out(bitextender_10_out));
  assign not_31_out = ~demultiplexer_4_out_0;  // Not not_31, 16 bits wide
  BitExtender #(.inputBits(1)) bitextender_11 (.in(CT_FU__EPOCH), .out(bitextender_11_out));
  assign issue = and_163_out ? 1'b1 : 1'bz;  // Driver driver_216
  assign CT_ISS__URA = and_163_out ? 1'b1 : 1'bz;  // Driver driver_217
  assign CT_ISS__RA = and_163_out ? byte_I1[7:3] : 5'bz;  // Driver driver_218
  assign CT_ISS__URB = and_163_out ? 1'b1 : 1'bz;  // Driver driver_219
  assign CT_ISS__RB = and_163_out ? 5'b11110 : 5'bz;  // Driver driver_220
  assign CT_ISS__OSC = and_163_out ? 1'b1 : 1'bz;  // Driver driver_221
  assign CT_ISS__UMM = and_163_out ? 1'b1 : 1'bz;  // Driver driver_222
  assign CT_ISS__UFU = and_163_out ? 3'b110 : 3'bz;  // Driver driver_223
  assign CT_ISS__OSTB = and_163_out ? 1'b1 : 1'bz;  // Driver driver_224
  assign CT_UBTB = and_163_out ? 1'b1 : 1'bz;  // Driver driver_225
  assign issue = and_164_out ? 1'b1 : 1'bz;  // Driver driver_226
  assign CT_ISS__URB = and_164_out ? 1'b1 : 1'bz;  // Driver driver_227
  assign CT_ISS__RB = and_164_out ? 5'b11110 : 5'bz;  // Driver driver_228
  assign CT_ISS__OSC = and_164_out ? 1'b1 : 1'bz;  // Driver driver_229
  assign CT_ISS__UMM = and_164_out ? 1'b1 : 1'bz;  // Driver driver_230
  assign CT_ISS__UFU = and_164_out ? 3'b110 : 3'bz;  // Driver driver_231
  assign CT_ISS__OLDB = and_164_out ? 1'b1 : 1'bz;  // Driver driver_232
  assign CT_UBTB = and_164_out ? 1'b1 : 1'bz;  // Driver driver_233
  Multiplexer #(.Bits(32)) multiplexer_70 (.sel(JPU_RET), .in_0(pc_read), .in_1(pc_ret), .out(multiplexer_70_out));
  Multiplexer #(.Bits(4)) multiplexer_71 (.sel(JPU_RET), .in_0(CT_FU__INST), .in_1(RET_INST), .out(multiplexer_71_out));
  Multiplexer multiplexer_72 (.sel(JPU_RET), .in_0(CT_FU__EPOCH), .in_1(RET_EPOCH), .out(multiplexer_72_out));
  Multiplexer #(.Bits(32)) multiplexer_73 (
    .sel(or_65_out), .in_0(R_A), .in_1(multiplexer_69_out), .out(multiplexer_73_out));
  assign and_171_out = {byte_D2, byte_D3} & bitextender_8_out;  // And and_171, 16 bits wide
  assign and_172_out = BTB_DP & bitextender_9_out;  // And and_172, 37 bits wide
  or or_66 (or_66_out, CT_JPU__JP, JPU_INT, JPU_RET);
  or or_67 (or_67_out, CT_FU__MF, JPU_RET);
  assign not_32_out = ~demultiplexer_3_out_0;  // Not not_32, 16 bits wide
  assign or_68_out = bitextender_10_out | not_31_out;  // Or or_68, 16 bits wide
  assign and_173_out = bitextender_11_out & demultiplexer_4_out_0;  // And and_173, 16 bits wide
  and and_174 (and_174_out, ~CT_JPU__LD, JPU_BTB__ST);  // And
  assign or_69_out = register_97_q | demultiplexer_4_out_0;  // Or or_69, 16 bits wide
  assign or_70_out = register_98_q | and_173_out;  // Or or_70, 16 bits wide
  // data_select_32 data_select_32_1: pin names not known; wires that end beside it: store_controller_1_d1_sel, store_controller_1_d2_sel, ALU_A_T__R, ALU_B_T__R, DIR, LDB_B__D, {32{1'b0}}, {32{1'b0}}, {32{1'b0}}, {32{1'b0}}, ROB_GEN_DA, ROB_GEN_DB
  data_select_8H data_select_8h_1 (
    .D1_sel(store_controller_half_1_d1_sel), .D2_sel(store_controller_half_1_d2_sel), .in1(ALU_A_T__F),
    .in2(ALU_B_T__F), .in3({8{1'b0}}), .in4({8{1'b0}}), .out1(ROB_FL_A), .out2(ROB_FL_B));
  data_select_6H data_select_6h_1 (
    .D1_sel(store_controller_half_2_d1_sel), .D2_sel(store_controller_half_2_d2_sel), .in1(TRAP_INT),
    .in2({6{1'b0}}), .in3({6{1'b0}}), .in4({6{1'b0}}), .out1(ROB_INT_A), .out2(ROB_INT_B));
  RS_FF rs_ff_23 (.S(CT_JPU__LD), .C(C_ct), .R(and_174_out), .Q(JPU_BTB__ST), .nQ(rs_ff_23_nq));
  Register #(.Bits(32)) register_89 (.D(multiplexer_70_out), .C(C), .en(JPU_LD), .Q(JPU_PC));
  Register #(.Bits(4)) register_90 (.D(multiplexer_71_out), .C(C_ct), .en(JPU_LD), .Q(Fl_JPU__INST));
  Register register_91 (.D(multiplexer_72_out), .C(C_ct), .en(JPU_LD), .Q(Fl_JPU__EP));
  Register #(.Bits(32)) register_92 (.D(multiplexer_73_out), .C(C), .en(JPU_LD), .Q(register_92_q));
  Register #(.Bits(16)) register_93 (.D(and_171_out), .C(C), .en(JPU_LD), .Q(register_93_q));
  Register #(.Bits(37)) register_94 (
    .D(and_172_out), .C(C_ct), .en(JPU_LD),
    .Q({JPU_BTB__tar, JPU_BTB__pred, JPU_BTB__J, JPU_BTB__V, JPU_BTBPK[0]}));
  Register register_95 (.D(or_66_out), .C(C_ct), .en(JPU_LD), .Q(JPU_JP));
  Register register_96 (.D(or_67_out), .C(C_ct), .en(JPU_LD), .Q(JPU_MF));
  assign and_175_out = icmks_16 & not_32_out & or_69_out;  // And and_175, 16 bits wide
  or or_71 (or_71_out, CT_RET__LD, and_181_out, ext_en);
  assign and_176_out = or_68_out & or_70_out;  // And and_176, 16 bits wide
  or or_72 (or_72_out, rs_ff_23_nq, JPU_BTB__ST);
  D_FF #(.Bits(32)) d_ff_34 (.D(register_92_q), .C(C_ct), .Q(d_ff_34_q));  // open: nQ
  D_FF #(.Bits(16)) d_ff_35 (.D(register_93_q), .C(C_ct), .Q(d_ff_35_q));  // open: nQ
  and and_177 (JPU_LD, CT_JPU__LD, or_72_out);
  Register #(.Bits(16)) register_97 (.D(and_175_out), .C(C_ct), .en(or_71_out), .Q(register_97_q));
  Register #(.Bits(16)) register_98 (.D(and_176_out), .C(C_ct), .en(or_71_out), .Q(register_98_q));
  add_s16c32 add_s16c32_2 (.a(multiplexer_74_out), .b(multiplexer_75_out), .s(JPU_ADDR));  // open: c
  Multiplexer #(.Bits(32)) multiplexer_74 (.sel(JPU_JP), .in_0(JPU_PC), .in_1(d_ff_34_q), .out(multiplexer_74_out));
  Multiplexer #(.Bits(16)) multiplexer_75 (.sel(JPU_JP), .in_0(16'h4), .in_1(d_ff_35_q), .out(multiplexer_75_out));
  assign and_178_out = V1_inst & register_97_q;  // And and_178, 16 bits wide
  BitSelector #(.Selector_Bits(4)) bitselector_1 (
    .in(register_98_q), .sel(priorityencoder_3_num), .out(bitselector_1_out));
  PullDown #(.Bits(3)) pulldown_20 (.out(CT_ISS__UFU));
  PullDown pulldown_21 (.out(CT_ISS__OSTB));
  PullDown pulldown_22 (.out(clr));
  PullDown pulldown_23 (.out(clr_ep));
  PullDown #(.Bits(4)) pulldown_24 (.out(clr_id));
  PullDown pulldown_25 (.out(CT_ALU__M));
  PullDown pulldown_26 (.out(CT_ALU__LD));
  PullDown pulldown_27 (.out(CT_ALU__WD));
  PullDown pulldown_28 (.out(CT_ALU__WF));
  PullDown pulldown_29 (.out(CT_FU__EPOCH));
  PullDown #(.Bits(4)) pulldown_30 (.out(CT_FU__INST));
  PullDown #(.Bits(8)) pulldown_31 (.out(CT_FU__WR));
  PullDown pulldown_32 (.out(CT_DIR__LD));
  PullDown pulldown_33 (.out(CT_DIR__M));
  PullDown pulldown_34 (.out(CT_DIR__MS));
  PullDown pulldown_35 (.out(MB_ep));
  PullDown #(.Bits(4)) pulldown_36 (.out(LD_id));
  PullDown #(.Bits(32)) pulldown_37 (.out(LD_addr));
  PullDown pulldown_38 (.out(CT_STB__LD));
  PullDown pulldown_39 (.out(CT_LDB__LD));
  PullDown pulldown_40 (.out(CT_MB__LD));
  PullDown pulldown_41 (.out(CT_MB__ST));
  PullDown pulldown_42 (.out(CT_ISS__OLDB));
  PullDown pulldown_43 (.out(CT_UBTB));
  PullDown pulldown_44 (.out(CT_USCB));
  and and_179 (and_179_out, ~JPU_MF, JPU_BTB__ST);  // And
  data_select_8 data_select_8_1 (
    .D1_sel(store_controller_1_d1_sel), .D2_sel(store_controller_1_d2_sel), .in1({ALU_A_WR, ALU_A_RM}),
    .in2({ALU_B_WR, ALU_B_RM}), .in3(DIR_WR), .in4(LDB_B__WR), .in5({8{1'b0}}), .in6({8{1'b0}}),
    .in7({8{1'b0}}), .in8({8{1'b0}}), .out1(ROB_GEN_WA), .out2(ROB_GEN_WB));
  data_select_4H data_select_4h_1 (
    .D1_sel(store_controller_half_1_d1_sel), .D2_sel(store_controller_half_1_d2_sel), .in1(ALU_A_INST),
    .in2(ALU_B_INST), .in3(4'b0000), .in4(4'b0000), .out1(ROB_FL_INSTA), .out2(ROB_FL_INSTB));
  data_select_4H data_select_4h_2 (
    .D1_sel(store_controller_half_2_d1_sel), .D2_sel(store_controller_half_2_d2_sel), .in1(TRAP_INST),
    .in2(4'b0000), .in3(4'b0000), .in4(4'b0000), .out1(ROB_INT_INSTA), .out2(ROB_INT_INSTB));
  PriorityEncoder #(.Selector_Bits(4)) priorityencoder_3 (
    .in0(and_178_out[0]), .in1(and_178_out[1]), .in2(and_178_out[2]), .in3(and_178_out[3]),
    .in4(and_178_out[4]), .in5(and_178_out[5]), .in6(and_178_out[6]), .in7(and_178_out[7]),
    .in8(and_178_out[8]), .in9(and_178_out[9]), .in10(and_178_out[10]), .in11(and_178_out[11]),
    .in12(and_178_out[12]), .in13(and_178_out[13]), .in14(and_178_out[14]), .in15(and_178_out[15]),
    .num(priorityencoder_3_num), .any(priorityencoder_3_any));
  PullDown pulldown_45 (.out(CT_BLOCK));
  and and_180 (JPU_MFE, JPU_MF, JPU_BTB__ST);
  bus16_demux bus16_demux_6 (.bus(V1_inst), .E(and_179_out), .id(Fl_JPU__INST));
  bus16_demux bus16_demux_7 (.bus(V2_inst), .E(JPU_BTB__ST), .id(Fl_JPU__INST));
  not not_33 (not_33_out, BTB_override);
  and and_181 (and_181_out, FU_D__V[3], priorityencoder_3_any);
  xor xor_7 (JPU_MISS, JPU_BTB__J, JPU_JP);
  not not_34 (not_34_out, JPU_BTB__pred[0]);
  PullDown pulldown_46 (.out(kernel_inst));
  PullDown pulldown_47 (.out(CT_RF__E));
  PullDown pulldown_48 (.out(CT_RF__DM));
  PullDown #(.Bits(5)) pulldown_49 (.out(CT_RF__WS));
  PullDown #(.Bits(3)) pulldown_50 (.out(CT_RF__WM));
  PullDown #(.Bits(5)) pulldown_51 (.out(CT_RF__RA));
  PullDown #(.Bits(3)) pulldown_52 (.out(CT_RF__MA));
  PullDown #(.Bits(5)) pulldown_53 (.out(CT_RF__RB));
  PullDown #(.Bits(3)) pulldown_54 (.out(CT_RF__MB));
  PullDown pulldown_55 (.out(CT_RF__PCSE));
  PullDown pulldown_56 (.out(CT_RF__PCJ));
  PullDown pulldown_57 (.out(CT_RF__PCR));
  PullDown #(.Bits(3)) pulldown_58 (.out(CT_RF__SCN));
  PullDown pulldown_59 (.out(CT_RF__SCD));
  PullDown #(.Bits(9)) pulldown_60 (.out(CT_ALU__CT));
  PullDown pulldown_61 (.out(CT_ALU__M));
  PullDown pulldown_62 (.out(CT_ALU__M2));
  PullDown pulldown_63 (.out(CT_BUS__IAR));
  PullDown pulldown_64 (.out(CT_BUS__IAG));
  PullDown pulldown_65 (.out(CT_BUS__IDR));
  PullDown pulldown_66 (.out(CT_BUS__IDM));
  PullDown pulldown_67 (.out(CT_BUS__DAR));
  PullDown pulldown_68 (.out(CT_BUS__DAM));
  PullDown pulldown_69 (.out(CT_BUS__DAG));
  PullDown pulldown_70 (.out(CT_BUS__DDR));
  PullDown pulldown_71 (.out(CT_BUS__DDG));
  PullDown pulldown_72 (.out(I_LD));
  PullDown pulldown_73 (.out(D_LD));
  PullDown pulldown_74 (.out(D_ST));
  PullDown #(.Bits(2)) pulldown_75 (.out(D_MD));
  PullDown pulldown_76 (.out(CT_MVR));
  and and_182 (and_182_out, JPU_BTB__pred[0], JPU_BTB__pred[1]);
  and and_183 (and_183_out, JPU_BTB__pred[0], JPU_JP);
  and and_184 (and_184_out, JPU_BTB__pred[1], JPU_JP);
  and and_185 (and_185_out, not_34_out, not_33_out, JPU_BTB__pred[1]);
  and and_186 (and_186_out, not_34_out, not_33_out, JPU_JP);
  and and_187 (and_187_out, JPU_BTB__pred[1], not_33_out, JPU_JP);
  D_FF #(.Bits(4)) d_ff_36 (.D(priorityencoder_3_num), .C(C_ct), .Q(RET_INST));  // open: nQ
  D_FF d_ff_37 (.D(bitselector_1_out), .C(C_ct), .Q(RET_EPOCH));  // open: nQ
  and and_188 (and_188_out, ~and_192_out, and_181_out);  // And
  inst_comp inst_comp_9 (.A_id(RET_INST), .A_ep(RET_EPOCH), .B_id(clr_id), .B_ep(clr_ep), .A_new(inst_comp_9_a_new));
  and and_189 (and_189_out, ~and_192_out, and_181_out);  // And
  inst_comp inst_comp_10 (
    .A_id(priorityencoder_3_num), .A_ep(bitselector_1_out), .B_id(clr_id), .B_ep(clr_ep),
    .A_new(inst_comp_10_a_new));
  PullDown pulldown_77 (.out(CT_TRAP__LD));
  PullDown pulldown_78 (.out(CT_KILL));
  PullDown pulldown_79 (.out(ISS_kernel));
  data_select_4 data_select_4_1 (
    .D1_sel(store_controller_1_d1_sel), .D2_sel(store_controller_1_d2_sel), .in1(ALU_A_INST),
    .in2(ALU_B_INST), .in3(DIR_INST), .in4(LDB_B__INST), .in5(4'b0000), .in6(4'b0000), .in7(4'b0000),
    .in8(4'b0000), .out1(ROB_GEN_INSTA), .out2(ROB_GEN_INSTB));
  and and_190 (and_190_out[6], MB_free, JPU_free);
  or or_73 (JPU_pred[1], and_182_out, and_183_out, and_184_out, BTB_override);
  or or_74 (JPU_pred[0], and_185_out, and_186_out, and_187_out);
  not not_35 (not_35_out, E);
  not not_36 (JPU_free, and_188_out);
  and and_191 (and_191_out, inst_comp_9_a_new, clr);
  D_FF d_ff_38 (.D(and_189_out), .C(C_ct), .Q(d_ff_38_q));  // open: nQ
  and and_192 (and_192_out, inst_comp_10_a_new, clr);
  res_station res_station_1 (
    .C(C_ct), .res(not_35_out), .E(issue), .D({byte_I0, byte_I1, byte_I2, byte_I3}), .BTB_PK(BTB_pack__iss),
    .ep_I(epoch_IS), .inst(inst_IS), .URA(CT_ISS__URA), .URB(CT_ISS__URB), .RA(CT_ISS__RA), .RB(CT_ISS__RB),
    .UMM(CT_ISS__UMM), .UFL(CT_ISS__UFL), .UFU(CT_ISS__UFU), .ORC(CT_ISS__ORC), .RC(CT_ISS__RC),
    .OSC(CT_ISS__OSC), .OFL(CT_ISS__OFL), .BLOCK(CT_BLOCK), .com1(com1), .com2(com2), .com1_inst(com1_inst),
    .com2_inst(com2_inst), .clr(clr), .clr_ep(clr_ep), .clr_id(clr_id), .FU_free(FU_free), .V(CT_DISP),
    .disp_32({byte_D0, byte_D1, byte_D2, byte_D3}), .BTB_DP(BTB_DP), .ep_O(epoch_DP), .disp(inst_DP),
    .full(RS_full));
  PullDown pulldown_80 (.out(ex_nop));
  PullDown pulldown_81 (.out(CT_ISS__HALT));
  Comparator #(.Bits(32)) comparator_8 (.a(JPU_ADDR), .b(JPU_BTB__tar), .eq(comparator_8_eq));  // open: gt, lt
  and and_193 (and_193_out, ~and_191_out, d_ff_38_q);  // And
  PullDown pulldown_82 (.out(issue));
  PullDown pulldown_83 (.out(CT_ISS__URA));
  PullDown pulldown_84 (.out(CT_ISS__URB));
  PullDown #(.Bits(5)) pulldown_85 (.out(CT_ISS__RA));
  PullDown #(.Bits(5)) pulldown_86 (.out(CT_ISS__RB));
  PullDown pulldown_87 (.out(CT_ISS__UMM));
  PullDown pulldown_88 (.out(CT_ISS__UFL));
  PullDown pulldown_89 (.out(CT_ISS__ORC));
  PullDown #(.Bits(5)) pulldown_90 (.out(CT_ISS__RC));
  PullDown pulldown_91 (.out(CT_ISS__OSC));
  PullDown pulldown_92 (.out(CT_ISS__OFL));
  PullDown pulldown_93 (.out(CT_ROB__EX__E));
  PullDown pulldown_94 (.out(CT_ROB__ST__E));
  PullDown #(.Bits(3)) pulldown_95 (.out(CT_SP__MOF));
  PullDown pulldown_96 (.out(CT_BUS__DDM));
  PullDown pulldown_97 (.out(CT_RF__PCH));
  PullDown pulldown_98 (.out(\wait ));
  nand nand_12 (nand_12_out, JPU_BTB__V, comparator_8_eq);
  and and_194 (and_194_out, JPU_MISS, JPU_BTB__V, comparator_8_eq);
  and and_195 (Fl_JPU, or_75_out, JPU_BTB__ST);
  Comparator #(.Bits(3)) comparator_9 (
    .a(store_controller_1_d1_sel), .b(3'b010), .eq(comparator_9_eq));  // open: gt, lt
  Comparator #(.Bits(3)) comparator_10 (
    .a(store_controller_1_d2_sel), .b(3'b010), .eq(comparator_10_eq));  // open: gt, lt
  D_FF #(.Bits(8)) d_ff_39 (
    .D({JPU_free, and_190_out[6], 1'b0, TRAP_free, MB_free, DIR_free, ALU_free, 1'b1}), .C(C_ct), .Q(FU_free));  // open: nQ
  assign CT_JPU__LD = and_193_out ? 1'b1 : 1'bz;  // Driver driver_234
  assign JPU_RET = and_193_out ? 1'b1 : 1'bz;  // Driver driver_235
  and and_196 (ROB_GEN_EX1, comparator_9_eq, DIR_EX);
  and and_197 (ROB_GEN_EX2, comparator_10_eq, DIR_EX);
  and and_198 (BTB_override, JPU_JP, nand_12_out);
  and and_199 (and_199_out, nand_12_out, JPU_BTB__J);
  or or_75 (or_75_out, and_194_out, and_199_out, BTB_override);
  assign CT_RF__PCSE = Fl_JPU ? 1'b1 : 1'bz;  // Driver driver_236
  assign CT_RF__PCJ = Fl_JPU ? 1'b1 : 1'bz;  // Driver driver_237
  assign CT_JMP = Fl_JPU ? 1'b1 : 1'bz;  // Driver driver_238
  PullDown pulldown_99 (.out(CT_RF__SCSRE));
  PullDown pulldown_100 (.out(CT_RF__SCSE));
  PullDown pulldown_101 (.out(CT_RF__SCSS));
  PullDown pulldown_102 (.out(CT_JPU__JP));
  PullDown pulldown_103 (.out(JPU_A__ST));
  PullDown pulldown_104 (.out(CT_MB__OFFM));
  PullDown pulldown_105 (.out(JPU_BTB__ST));
  PullDown pulldown_106 (.out(CT_JPU__LD));
  PullDown pulldown_107 (.out(CT_JMP));
  PullDown pulldown_108 (.out(CT_FU__MF));
  PullDown pulldown_109 (.out(CT_CALL__LD));
  PullDown pulldown_110 (.out(CT_RET__LD));
  PullDown pulldown_111 (.out(JPU_RET));
  PullDown pulldown_112 (.out(JPU_free));
  PullDown pulldown_113 (.out(JPU_CALL));
  PullDown pulldown_114 (.out(CT_CALLM));

  assign CSH_mode = 2'b00;
  assign CSH_run = 1'b0;
  assign INT_pstr = 1'b0;
  assign INT_ret = 1'b0;
  assign INT_vstr = 1'b0;
  assign MMU_base = {32{1'b0}};
  assign MMU_dis = 1'b0;
  assign MMU_en = 1'b0;
  assign MMU_limit = {32{1'b0}};

  // Other names for the same wires on the sheet: FU_CLR[2:0] = {DIR_CLR, ALU_B_CLR, ALU_A_CLR};
  //   ALU_A_WR[2:0] = ALU_A_RM; ALU_B_WR[2:0] = ALU_B_RM; B = boot; BTB_packet[2] = BTB_JP;
  //   BTB_pred[1:0] = BTB_packet[4:3]; BTB_tar[31:0] = BTB_packet[36:5]; BTB_V = BTB_packet[1]; C_dt = C; C_i = C;
  //   Fl_INT__EP = com2_ep; Fl_INT__INST[3:0] = com2_inst; CT_RF__SCAS = CT_RF__SCAE;
  //   disp_32[31:0] = {byte_D0, byte_D1, byte_D2, byte_D3}; imm16_2[15:0] = {byte_D2, byte_D3}; disp_e = CT_DISP;
  //   fl_i[8] = FL[14]; int_proc = FL[14]; trap = FL[15]; FU_D__V[2:0] = {DIR_V, ALU_B_VD, ALU_A_VD};
  //   LDB_B__V = FU_D__V[3]; FU_F__V[1:0] = {ALU_B_VF, ALU_A_VF}; TRAP_VI = FU_I__V[0]; INT_ISS = INT_acp;
  //   issue_32[31:0] = {byte_I0, byte_I1, byte_I2, byte_I3};
  //   JPU_BTBPK[36:1] = {JPU_BTB__tar, JPU_BTB__pred, JPU_BTB__J, JPU_BTB__V}; JPU_EN = JPU_BTB__ST;
  //   JPU_ST = JPU_BTB__ST; run_int = Fl_INT; scs_i[31:0] = ISC_sc; TRAP_CLR = FU_CLR[4]

  // Notes on the sheet:
  //   D_MD: 0:32
  //   1:16
  //   2:8
  //   3:u.u
  //   D_accept: default 1
  //   C: Hz: 16
  //   decode circuit
  //   IO pins
  //   primeary signals
  //   pipeline controller
  //   kernal mode system
  //   interrupt system
  //   ext system
  //   syscall
  //   iret
  //   intervec/pri
  //   inst id manager
  //   interrupt commit
  //   ALU
  //   register
  //   stack
  //   RAM
  //   register system
  //   ROB
  //   program counter controller
  //   bus system
  //   data bus ctrl
  //   trap
  //   jump
  //   call
  //   return
  //   wait/halt
  //   block
  //   exld/st
  //   stack circuit
  //   ALU system
  //   dir circuit
  //   load/store circuit
  //   issue circuit
  //   flag circuit
  //   FU aribiter
  //   jmp circuit
  //   return unit
  //   control bus
endmodule
