// Digital circuit data-select-1.dig as structural Verilog
module data_select_1 (
  input  in1,
  input  in2,
  input  in3,
  input  in4,
  input  in5,
  input  in6,
  input  in7,
  input  in8,
  input  [2:0] D1_sel,
  input  [2:0] D2_sel,
  output out1,
  output out2
);

  Multiplexer #(.Selector_Bits(3)) multiplexer_1 (
    .sel(D1_sel), .in_0(in1), .in_1(in2), .in_2(in3), .in_3(in4), .in_4(in5), .in_5(in6), .in_6(in7),
    .in_7(in8), .out(out1));
  Multiplexer #(.Selector_Bits(3)) multiplexer_2 (
    .sel(D2_sel), .in_0(in1), .in_1(in2), .in_2(in3), .in_3(in4), .in_4(in5), .in_5(in6), .in_6(in7),
    .in_7(in8), .out(out2));

  // Other names for the same wires on the sheet: I1 = in1; I2 = in2; I3 = in3; I4 = in4; I5 = in5; I6 = in6; I7 = in7;
  //   I8 = in8; O1 = out1; O2 = out2
endmodule
