// Digital circuit data-select-1H.dig as structural Verilog
module data_select_1H (
  input  in1,
  input  in2,
  input  in3,
  input  in4,
  input  [1:0] D1_sel,
  input  [1:0] D2_sel,
  output out1,
  output out2
);

  Multiplexer #(.Selector_Bits(2)) multiplexer_1 (
    .sel(D1_sel), .in_0(in1), .in_1(in2), .in_2(in3), .in_3(in4), .out(out1));
  Multiplexer #(.Selector_Bits(2)) multiplexer_2 (
    .sel(D2_sel), .in_0(in1), .in_1(in2), .in_2(in3), .in_3(in4), .out(out2));

  // Other names for the same wires on the sheet: I1 = in1; I2 = in2; I3 = in3; I4 = in4; O1 = out1; O2 = out2
endmodule
