// Digital circuit data-select-4H.dig as structural Verilog
module data_select_4H (
  input  [3:0] in1,
  input  [3:0] in2,
  input  [3:0] in3,
  input  [3:0] in4,
  input  [1:0] D1_sel,
  input  [1:0] D2_sel,
  output [3:0] out1,
  output [3:0] out2
);

  Multiplexer #(.Selector_Bits(2), .Bits(4)) multiplexer_1 (
    .sel(D1_sel), .in_0(in1), .in_1(in2), .in_2(in3), .in_3(in4), .out(out1));
  Multiplexer #(.Selector_Bits(2), .Bits(4)) multiplexer_2 (
    .sel(D2_sel), .in_0(in1), .in_1(in2), .in_2(in3), .in_3(in4), .out(out2));

  // Other names for the same wires on the sheet: I1[3:0] = in1; I2[3:0] = in2; I3[3:0] = in3; I4[3:0] = in4;
  //   O1[3:0] = out1; O2[3:0] = out2
endmodule
