// Digital circuit data-select-8H.dig as structural Verilog
module data_select_8H (
  input  [7:0] in1,
  input  [7:0] in2,
  input  [7:0] in3,
  input  [7:0] in4,
  input  [1:0] D1_sel,
  input  [1:0] D2_sel,
  output [7:0] out1,
  output [7:0] out2
);

  Multiplexer #(.Selector_Bits(2), .Bits(8)) multiplexer_1 (
    .sel(D1_sel), .in_0(in1), .in_1(in2), .in_2(in3), .in_3(in4), .out(out1));
  Multiplexer #(.Selector_Bits(2), .Bits(8)) multiplexer_2 (
    .sel(D2_sel), .in_0(in1), .in_1(in2), .in_2(in3), .in_3(in4), .out(out2));

  // Other names for the same wires on the sheet: I1[7:0] = in1; I2[7:0] = in2; I3[7:0] = in3; I4[7:0] = in4;
  //   O1[7:0] = out1; O2[7:0] = out2
endmodule
