// Digital circuit data-selector.dig as structural Verilog
module data_selector (
  input  [31:0] in1,
  input  [31:0] in2,
  input  [31:0] in3,
  input  [31:0] in4,
  input  [31:0] in5,
  input  [31:0] in6,
  input  [31:0] in7,
  input  [31:0] in8,
  input  [2:0] D1_sel,
  input  [2:0] D2_sel,
  output [31:0] out1,
  output [31:0] out2
);

  Multiplexer #(.Selector_Bits(3), .Bits(32)) multiplexer_1 (
    .sel(D1_sel), .in_0(in1), .in_1(in2), .in_2(in3), .in_3(in4), .in_4(in5), .in_5(in6), .in_6(in7),
    .in_7(in8), .out(out1));
  Multiplexer #(.Selector_Bits(3), .Bits(32)) multiplexer_2 (
    .sel(D2_sel), .in_0(in1), .in_1(in2), .in_2(in3), .in_3(in4), .in_4(in5), .in_5(in6), .in_6(in7),
    .in_7(in8), .out(out2));

  // Other names for the same wires on the sheet: I1[31:0] = in1; I2[31:0] = in2; I3[31:0] = in3; I4[31:0] = in4;
  //   I5[31:0] = in5; I6[31:0] = in6; I7[31:0] = in7; I8[31:0] = in8; O1[31:0] = out1; O2[31:0] = out2
endmodule
