// Digital circuit fill-4.dig as structural Verilog
module fill_4 (
  input  in1,
  input  in2,
  input  in3,
  input  in4,
  input  on,
  output v,
  output out1,
  output out2,
  output out3,
  output out4
);

  or or_1 (out4, in4, on);
  or or_2 (out3, in3, in4, on);
  or or_3 (out2, in2, in3, in4, on);
  or or_4 (out1, in1, in2, in3, in4, on);
  or or_5 (v, in1, in2, in3, in4);
endmodule
