// Digital circuit flush-mux.dig as structural Verilog
module flush_mux (
  input  [3:0] M_id,
  input  M_ep,
  input  [3:0] J_id,
  input  J_ep,
  input  M_v,
  input  J_v,
  input  [3:0] I_id,
  input  I_ep,
  input  I_v,
  input  [3:0] E_id,
  input  E_v,
  input  E_ep,
  input  M_self,
  output [3:0] m_id_2,
  output m_ep_2,
  output m_v_2,
  output self,
  output [3:0] sel,
  output E_acp
);

  wire comparator_1_gt, comparator_1_lt, decoder_1_out_1, multiplexer_1_out, multiplexer_3_out, nand_1_out,
       not_1_out, or_1_out, or_2_out, xor_1_out;
  wire [1:0] priorityencoder_1_num;
  wire [3:0] multiplexer_2_out;

  not not_1 (not_1_out, M_v);
  Comparator #(.Bits(4)) comparator_1 (.a(M_id), .b(J_id), .gt(comparator_1_gt), .lt(comparator_1_lt));  // open: eq
  or or_1 (or_1_out, multiplexer_1_out, not_1_out);
  Multiplexer multiplexer_1 (.sel(xor_1_out), .in_0(comparator_1_gt), .in_1(comparator_1_lt), .out(multiplexer_1_out));
  xor xor_1 (xor_1_out, M_ep, J_ep);
  nand nand_1 (nand_1_out, or_1_out, J_v);
  Multiplexer #(.Bits(4)) multiplexer_2 (.sel(nand_1_out), .in_0(J_id), .in_1(M_id), .out(multiplexer_2_out));
  Multiplexer multiplexer_3 (.sel(nand_1_out), .in_0(J_ep), .in_1(M_ep), .out(multiplexer_3_out));
  or or_2 (or_2_out, M_v, J_v);
  PriorityEncoder #(.Selector_Bits(2)) priorityencoder_1 (
    .in0(1'b0), .in1(or_2_out), .in2(I_v), .in3(E_v), .num(priorityencoder_1_num));  // open: any
  Decoder #(.Selector_Bits(2)) decoder_1 (
    .sel(priorityencoder_1_num), .out_1(decoder_1_out_1), .out_2(sel[2]), .out_3(E_acp));  // open: out_0
  or or_3 (m_v_2, M_v, J_v, I_v, E_v);
  Demultiplexer demultiplexer_1 (.sel(nand_1_out), .in(decoder_1_out_1), .out_0(sel[0]), .out_1(sel[1]));
  and and_1 (self, decoder_1_out_1, M_self, nand_1_out);
  Multiplexer #(.Selector_Bits(2), .Bits(4)) multiplexer_4 (
    .sel(priorityencoder_1_num), .in_0(4'b0000), .in_1(multiplexer_2_out), .in_2(I_id), .in_3(E_id),
    .out(m_id_2));
  Multiplexer #(.Selector_Bits(2)) multiplexer_5 (
    .sel(priorityencoder_1_num), .in_0(1'b0), .in_1(multiplexer_3_out), .in_2(I_ep), .in_3(E_ep), .out(m_ep_2));

  assign sel[3] = E_acp;
endmodule
