// Digital circuit id-manager.dig as structural Verilog
module id_manager (
  input  \use ,
  input  C,
  input  [15:0] S_inst,
  input  clr,
  input  [3:0] clr_id,
  input  clr_ep,
  output [3:0] id,
  output V,
  output com1,
  output com2,
  output [3:0] com2_id,
  output [3:0] com1_id,
  output epoch
);

  wire add_1_c_o, multiplexer_2_out, multiplexer_3_out, not_2_out, not_3_out, or_1_out, or_3_out, or_5_out,
       or_6_out, used, used1, used2, valid1, valid2, xor_1_out;
  wire [0:0] and_2_out;
  wire [3:0] add_1_s, add_2_s, multiplexer_1_out;
  wire [15:0] and_1_out, and_5_out, and_6_out, bitextender_1_out, bitextender_2_out, com1_16, com2_16,
       demultiplexer_1_out_0, fill_16_1_out1, nor_1_out, not_1_out, or_2_out, or_4_out, use_16, used_q,
       valid_q, xor_2_out;

  Demultiplexer #(.Selector_Bits(4)) demultiplexer_1 (
    .sel(clr_id), .in(clr), .out_0(demultiplexer_1_out_0[0]), .out_1(demultiplexer_1_out_0[1]),
    .out_2(demultiplexer_1_out_0[2]), .out_3(demultiplexer_1_out_0[3]), .out_4(demultiplexer_1_out_0[4]),
    .out_5(demultiplexer_1_out_0[5]), .out_6(demultiplexer_1_out_0[6]), .out_7(demultiplexer_1_out_0[7]),
    .out_8(demultiplexer_1_out_0[8]), .out_9(demultiplexer_1_out_0[9]), .out_10(demultiplexer_1_out_0[10]),
    .out_11(demultiplexer_1_out_0[11]), .out_12(demultiplexer_1_out_0[12]),
    .out_13(demultiplexer_1_out_0[13]), .out_14(demultiplexer_1_out_0[14]), .out_15(demultiplexer_1_out_0[15]));
  xor xor_1 (xor_1_out, epoch, clr_ep);
  assign not_1_out = ~demultiplexer_1_out_0;  // Not not_1, 16 bits wide
  fill_16 fill_16_1 (
    .in1(demultiplexer_1_out_0[15]), .in2(demultiplexer_1_out_0[14]), .in3(demultiplexer_1_out_0[13]),
    .in4(demultiplexer_1_out_0[12]), .in5(demultiplexer_1_out_0[11]), .in6(demultiplexer_1_out_0[10]),
    .in7(demultiplexer_1_out_0[9]), .in8(demultiplexer_1_out_0[8]), .in9(demultiplexer_1_out_0[7]),
    .in10(demultiplexer_1_out_0[6]), .in11(demultiplexer_1_out_0[5]), .in12(demultiplexer_1_out_0[4]),
    .in13(demultiplexer_1_out_0[3]), .in14(demultiplexer_1_out_0[2]), .in15(demultiplexer_1_out_0[1]),
    .in16(demultiplexer_1_out_0[0]), .out1(fill_16_1_out1[15]), .out2(fill_16_1_out1[14]),
    .out3(fill_16_1_out1[13]), .out4(fill_16_1_out1[12]), .out5(fill_16_1_out1[11]),
    .out6(fill_16_1_out1[10]), .out7(fill_16_1_out1[9]), .out8(fill_16_1_out1[8]), .out9(fill_16_1_out1[7]),
    .out10(fill_16_1_out1[6]), .out11(fill_16_1_out1[5]), .out12(fill_16_1_out1[4]),
    .out13(fill_16_1_out1[3]), .out14(fill_16_1_out1[2]), .out15(fill_16_1_out1[1]), .out16(fill_16_1_out1[0]));
  BitExtender #(.inputBits(1)) bitextender_1 (.in(xor_1_out), .out(bitextender_1_out));
  BitExtender #(.inputBits(1)) bitextender_2 (.in(clr), .out(bitextender_2_out));
  assign xor_2_out = bitextender_1_out ^ fill_16_1_out1;  // XOr xor_2, 16 bits wide
  assign nor_1_out = ~(com1_16 | com2_16 | and_1_out);  // NOr nor_1, 16 bits wide
  assign and_1_out = not_1_out & bitextender_2_out & xor_2_out;  // And and_1, 16 bits wide
  and and_2 (and_2_out[0], valid1, ~valid2);  // And
  not not_2 (not_2_out, used);
  and and_3 (com1, valid1, used1);
  and and_4 (com2, valid1, used1, valid2, used2);
  assign and_5_out = used_q & nor_1_out;  // And and_5, 16 bits wide
  Add #(.Bits(4)) add_1 (.a(id), .b(4'b0000), .c_i(not_2_out), .s(add_1_s), .c_o(add_1_c_o));
  or or_1 (or_1_out, com1, com2);
  assign and_6_out = valid_q & nor_1_out;  // And and_6, 16 bits wide
  Add #(.Bits(4)) add_2 (.a(com1_id), .b({2'b00, valid2, and_2_out[0]}), .c_i(1'b0), .s(add_2_s));  // open: c_o
  assign or_2_out = use_16 | and_5_out;  // Or or_2, 16 bits wide
  not not_3 (not_3_out, clr_ep);
  or or_3 (or_3_out, com1, com2, clr, S_inst[0], S_inst[1], S_inst[2], S_inst[3], S_inst[4], S_inst[5], S_inst[6], S_inst[7], S_inst[8], S_inst[9], S_inst[10], S_inst[11], S_inst[12], S_inst[13], S_inst[14], S_inst[15]);
  assign or_4_out = S_inst | and_6_out;  // Or or_4, 16 bits wide
  or or_5 (or_5_out, com1, com2, \use , clr);
  Multiplexer #(.Bits(4)) multiplexer_1 (.sel(clr), .in_0(add_1_s), .in_1(clr_id), .out(multiplexer_1_out));
  or or_6 (or_6_out, clr, \use );
  Multiplexer multiplexer_2 (.sel(clr), .in_0(add_1_c_o), .in_1(not_3_out), .out(multiplexer_2_out));
  Register #(.Bits(4)) register_1 (.D(add_2_s), .C(C), .en(or_1_out), .Q(com1_id));
  Register #(.Bits(16)) u_used (.D(or_2_out), .C(C), .en(or_5_out), .Q(used_q));
  Register #(.Bits(4)) register_2 (.D(multiplexer_1_out), .C(C), .en(or_6_out), .Q(id));
  Multiplexer multiplexer_3 (.sel(clr), .in_0(add_1_c_o), .in_1(clr_ep), .out(multiplexer_3_out));
  Register #(.Bits(16)) valid (.D(or_4_out), .C(C), .en(or_3_out), .Q(valid_q));
  Add #(.Bits(4)) add_3 (.a(com1_id), .b(4'b0001), .c_i(1'b0), .s(com2_id));  // open: c_o
  BitSelector #(.Selector_Bits(4)) bitselector_1 (.in(used_q), .sel(com1_id), .out(used1));
  BitSelector #(.Selector_Bits(4)) bitselector_2 (.in(used_q), .sel(com2_id), .out(used2));
  BitSelector #(.Selector_Bits(4)) bitselector_3 (.in(used_q), .sel(id), .out(used));
  JK_FF jk_ff_1 (.J(multiplexer_3_out), .C(C), .K(multiplexer_2_out), .Q(epoch));  // open: nQ
  BitSelector #(.Selector_Bits(4)) bitselector_4 (.in(valid_q), .sel(com1_id), .out(valid1));
  BitSelector #(.Selector_Bits(4)) bitselector_5 (.in(valid_q), .sel(com2_id), .out(valid2));
  not not_4 (V, used);
  Demultiplexer #(.Selector_Bits(4)) demultiplexer_2 (
    .sel(com1_id), .in(com1), .out_0(com1_16[0]), .out_1(com1_16[1]), .out_2(com1_16[2]), .out_3(com1_16[3]),
    .out_4(com1_16[4]), .out_5(com1_16[5]), .out_6(com1_16[6]), .out_7(com1_16[7]), .out_8(com1_16[8]),
    .out_9(com1_16[9]), .out_10(com1_16[10]), .out_11(com1_16[11]), .out_12(com1_16[12]),
    .out_13(com1_16[13]), .out_14(com1_16[14]), .out_15(com1_16[15]));
  Demultiplexer #(.Selector_Bits(4)) demultiplexer_3 (
    .sel(com2_id), .in(com2), .out_0(com2_16[0]), .out_1(com2_16[1]), .out_2(com2_16[2]), .out_3(com2_16[3]),
    .out_4(com2_16[4]), .out_5(com2_16[5]), .out_6(com2_16[6]), .out_7(com2_16[7]), .out_8(com2_16[8]),
    .out_9(com2_16[9]), .out_10(com2_16[10]), .out_11(com2_16[11]), .out_12(com2_16[12]),
    .out_13(com2_16[13]), .out_14(com2_16[14]), .out_15(com2_16[15]));
  Demultiplexer #(.Selector_Bits(4)) demultiplexer_4 (
    .sel(id), .in(\use ), .out_0(use_16[0]), .out_1(use_16[1]), .out_2(use_16[2]), .out_3(use_16[3]),
    .out_4(use_16[4]), .out_5(use_16[5]), .out_6(use_16[6]), .out_7(use_16[7]), .out_8(use_16[8]),
    .out_9(use_16[9]), .out_10(use_16[10]), .out_11(use_16[11]), .out_12(use_16[12]), .out_13(use_16[13]),
    .out_14(use_16[14]), .out_15(use_16[15]));

  // Other names for the same wires on the sheet: clear = clr; store_16[15:0] = S_inst
endmodule
