// Digital circuit index-compressor-half.dig as structural Verilog
module index_compressor_half (
  input  in0,
  input  in1,
  input  in2,
  input  in3,
  output [1:0] out0,
  output [1:0] out1,
  output [1:0] out2,
  output [1:0] out3,
  output [3:0] V
);

  wire [1:0] add_1_c_o, add_h_1_c_o;
  wire [2:0] and_1_out, and_2_out, and_3_out, and_4_out, bitextender_1_out, bitextender_2_out,
       bitextender_3_out, bitextender_4_out, demultiplexer_1_out_0, demultiplexer_1_out_1,
       demultiplexer_2_out_0, demultiplexer_2_out_1, demultiplexer_2_out_2, demultiplexer_3_out_0,
       demultiplexer_3_out_1, demultiplexer_3_out_2;

  BitExtender #(.inputBits(1), .outputBits(3)) bitextender_1 (.in(in0), .out(bitextender_1_out));
  BitExtender #(.inputBits(1), .outputBits(3)) bitextender_2 (.in(in1), .out(bitextender_2_out));
  add_h add_h_1 (.a(in0), .b(in1), .s(add_h_1_c_o[0]), .c_o(add_h_1_c_o[1]));
  Add add_1 (.a(in0), .b(in1), .c_i(in2), .s(add_1_c_o[0]), .c_o(add_1_c_o[1]));
  assign and_1_out = 3'b100 & bitextender_1_out;  // And and_1, 3 bits wide
  assign and_2_out = 3'b101 & bitextender_2_out;  // And and_2, 3 bits wide
  Demultiplexer #(.Bits(3)) demultiplexer_1 (
    .sel(in0), .in(and_2_out), .out_0(demultiplexer_1_out_0), .out_1(demultiplexer_1_out_1));
  BitExtender #(.inputBits(1), .outputBits(3)) bitextender_3 (.in(in2), .out(bitextender_3_out));
  assign and_3_out = 3'b110 & bitextender_3_out;  // And and_3, 3 bits wide
  Demultiplexer #(.Selector_Bits(2), .Bits(3)) demultiplexer_2 (
    .sel(add_h_1_c_o), .in(and_3_out), .out_0(demultiplexer_2_out_0), .out_1(demultiplexer_2_out_1),
    .out_2(demultiplexer_2_out_2));  // open: out_3
  BitExtender #(.inputBits(1), .outputBits(3)) bitextender_4 (.in(in3), .out(bitextender_4_out));
  assign and_4_out = 3'b111 & bitextender_4_out;  // And and_4, 3 bits wide
  Demultiplexer #(.Selector_Bits(2), .Bits(3)) demultiplexer_3 (
    .sel(add_1_c_o), .in(and_4_out), .out_0(demultiplexer_3_out_0), .out_1(demultiplexer_3_out_1),
    .out_2(demultiplexer_3_out_2), .out_3({V[3], out3}));
  assign {V[0], out0} = and_1_out | demultiplexer_1_out_0 | demultiplexer_2_out_0 | demultiplexer_3_out_0;  // Or or_1, 3 bits wide
  assign {V[1], out1} = demultiplexer_1_out_1 | demultiplexer_2_out_1 | demultiplexer_3_out_1;  // Or or_2, 3 bits wide
  assign {V[2], out2} = demultiplexer_2_out_2 | demultiplexer_3_out_2;  // Or or_3, 3 bits wide

  // Other names for the same wires on the sheet: O3[1:0] = out3; O0[1:0] = out0; O1[1:0] = out1; O2[1:0] = out2;
  //   I0 = in0; I1 = in1; I2 = in2; I3 = in3
endmodule
