// Digital circuit inst-comp.dig as structural Verilog
module inst_comp (
  input  [3:0] A_id,
  input  A_ep,
  input  [3:0] B_id,
  input  B_ep,
  output A_old
);

  wire comparator_1_gt, comparator_1_lt, xor_1_out;

  Comparator #(.Bits(4)) comparator_1 (.a(A_id), .b(B_id), .gt(comparator_1_gt), .lt(comparator_1_lt));  // open: eq
  xor xor_1 (xor_1_out, A_ep, B_ep);
  Multiplexer multiplexer_1 (.sel(xor_1_out), .in_0(comparator_1_gt), .in_1(comparator_1_lt), .out(A_old));
endmodule
