// Digital circuit inst-sfcomp.dig as structural Verilog
module inst_sfcomp (
  input  [3:0] A_id,
  input  A_ep,
  input  [3:0] B_id,
  input  B_ep,
  input  B_eq,
  output A_new
);

  wire comparator_1_gt, comparator_1_lt, multiplexer_1_out, xor_1_out;

  Comparator #(.Bits(4)) comparator_1 (.a(A_id), .b(B_id), .gt(comparator_1_gt), .lt(comparator_1_lt));  // open: eq
  xor xor_1 (xor_1_out, A_ep, B_eq, B_ep);
  Multiplexer multiplexer_1 (.sel(xor_1_out), .in_0(comparator_1_gt), .in_1(comparator_1_lt), .out(multiplexer_1_out));
  xor xor_2 (A_new, multiplexer_1_out, B_eq);
endmodule
