// Digital circuit execution buffer-3.dig as structural Verilog
module execution_buffer_3 (
);

  wire and_1_out, and_2_out, C_ct, C_dt, clr, clr_ep, CT_DIR__LD, CT_DIR__M, CT_FU__EPOCH, DIR_busy, DIR_LD,
       inst_comp_1_a_old, inst_comp_2_a_old, inst_comp_3_a_old, multiplexer_2_out, multiplexer_6_out,
       multiplexer_7_out, multiplexer_9_out, multiplexer_10_out, multiplexer_11_out, multiplexer_13_out,
       not_1_out, not_3_out, not_4_out, or_1_out, or_2_out, or_3_out, register_2_q, register_8_q,
       register_12_q;
  wire [1:0] or_4_out;
  wire [2:0] and_3_out, multiplexer_3_out, nand_1_out, nand_2_out, not_2_out;
  wire [2:1] register_5_q;
  wire [3:0] clr_id, CT_FU__INST, DIR_INST, multiplexer_8_out, multiplexer_12_out, register_1_q, register_7_q;
  wire [7:0] CT_FU__WR, DIR_WR, multiplexer_5_out, multiplexer_15_out, register_4_q, register_10_q;
  wire [31:0] DIR, multiplexer_1_out, multiplexer_4_out, multiplexer_14_out, R_A, register_3_q, register_9_q,
       undriven;

  not not_1 (not_1_out, clr);
  not not_2 (not_2_out[0], or_4_out[0]);
  Multiplexer #(.Bits(32)) multiplexer_1 (.sel(CT_DIR__M), .in_0(R_A), .in_1(undriven), .out(multiplexer_1_out));
  Multiplexer multiplexer_2 (.sel(and_3_out[2]), .in_0(nand_1_out[2]), .in_1(not_1_out), .out(multiplexer_2_out));
  and and_1 (and_1_out, multiplexer_2_out, CT_DIR__LD);
  xor xor_1 (not_2_out[1], or_4_out[0], or_4_out[1]);
  xor xor_2 (not_2_out[2], or_4_out[1], register_5_q[2]);
  Register #(.Bits(4)) register_1 (.D(CT_FU__INST), .C(C_ct), .en(multiplexer_3_out[2]), .Q(register_1_q));
  Register register_2 (.D(CT_FU__EPOCH), .C(C_ct), .en(multiplexer_3_out[2]), .Q(register_2_q));
  Register #(.Bits(32)) register_3 (.D(multiplexer_1_out), .C(C_dt), .en(multiplexer_3_out[2]), .Q(register_3_q));
  Register #(.Bits(8)) register_4 (.D(CT_FU__WR), .C(C_ct), .en(multiplexer_3_out[2]), .Q(register_4_q));
  Register register_5 (.D(and_1_out), .C(C_ct), .en(or_1_out), .Q(register_5_q[2]));
  not not_3 (not_3_out, multiplexer_2_out);
  or or_1 (or_1_out, not_3_out, multiplexer_3_out[2]);
  Multiplexer #(.Bits(3)) multiplexer_3 (.sel(or_2_out), .in_0(not_2_out), .in_1(and_3_out), .out(multiplexer_3_out));
  or or_2 (or_2_out, and_3_out[0], and_3_out[1], and_3_out[2]);
  Multiplexer #(.Bits(32)) multiplexer_4 (
    .sel(register_5_q[2]), .in_0(multiplexer_1_out), .in_1(register_3_q), .out(multiplexer_4_out));
  Multiplexer #(.Bits(8)) multiplexer_5 (
    .sel(register_5_q[2]), .in_0(CT_FU__WR), .in_1(register_4_q), .out(multiplexer_5_out));
  Multiplexer multiplexer_6 (.sel(and_3_out[1]), .in_0(nand_1_out[1]), .in_1(nand_1_out[2]), .out(multiplexer_6_out));
  Multiplexer multiplexer_7 (.sel(register_5_q[2]), .in_0(CT_DIR__LD), .in_1(register_5_q[2]), .out(multiplexer_7_out));
  Multiplexer #(.Bits(4)) multiplexer_8 (
    .sel(register_5_q[2]), .in_0(CT_FU__INST), .in_1(register_1_q), .out(multiplexer_8_out));
  inst_comp inst_comp_1 (
    .A_id(register_1_q), .A_ep(register_2_q), .B_id(clr_id), .B_ep(clr_ep), .A_old(inst_comp_1_a_old));
  Multiplexer multiplexer_9 (.sel(register_5_q[2]), .in_0(CT_FU__EPOCH), .in_1(register_2_q), .out(multiplexer_9_out));
  and and_2 (and_2_out, multiplexer_6_out, multiplexer_7_out);
  Register register_6 (.D(and_2_out), .C(C_ct), .en(or_3_out), .Q(register_5_q[1]));
  not not_4 (not_4_out, multiplexer_6_out);
  or or_3 (or_3_out, not_4_out, multiplexer_3_out[1]);
  or or_4 (or_4_out[1], register_5_q[1], register_5_q[2]);
  nand nand_1 (nand_1_out[2], inst_comp_1_a_old, clr);
  Register #(.Bits(4)) register_7 (.D(multiplexer_8_out), .C(C_ct), .en(multiplexer_3_out[1]), .Q(register_7_q));
  Register register_8 (.D(multiplexer_9_out), .C(C_ct), .en(multiplexer_3_out[1]), .Q(register_8_q));
  Register #(.Bits(32)) register_9 (.D(multiplexer_4_out), .C(C_dt), .en(multiplexer_3_out[1]), .Q(register_9_q));
  Register #(.Bits(8)) register_10 (.D(multiplexer_5_out), .C(C_ct), .en(multiplexer_3_out[1]), .Q(register_10_q));
  Multiplexer multiplexer_10 (.sel(and_3_out[0]), .in_0(nand_1_out[0]), .in_1(nand_1_out[1]), .out(multiplexer_10_out));
  Multiplexer multiplexer_11 (.sel(or_4_out[1]), .in_0(CT_DIR__LD), .in_1(register_5_q[1]), .out(multiplexer_11_out));
  or or_5 (or_4_out[0], DIR_busy, register_5_q[1], register_5_q[2]);
  assign and_3_out = nand_2_out & {register_5_q[2], or_4_out};  // And and_3, 3 bits wide
  Multiplexer #(.Bits(4)) multiplexer_12 (
    .sel(or_4_out[1]), .in_0(CT_FU__INST), .in_1(register_7_q), .out(multiplexer_12_out));
  inst_comp inst_comp_2 (
    .A_id(register_7_q), .A_ep(register_8_q), .B_id(clr_id), .B_ep(clr_ep), .A_old(inst_comp_2_a_old));
  Multiplexer multiplexer_13 (.sel(or_4_out[1]), .in_0(CT_FU__EPOCH), .in_1(register_8_q), .out(multiplexer_13_out));
  Multiplexer #(.Bits(32)) multiplexer_14 (
    .sel(or_4_out[1]), .in_0(multiplexer_1_out), .in_1(register_9_q), .out(multiplexer_14_out));
  Multiplexer #(.Bits(8)) multiplexer_15 (
    .sel(or_4_out[1]), .in_0(CT_FU__WR), .in_1(register_10_q), .out(multiplexer_15_out));
  // And and_4 has open pins: In_1=multiplexer_10_out, In_2=multiplexer_11_out, out=open
  nand nand_2 (nand_2_out[2], DIR_busy, register_5_q[1], register_5_q[2]);
  nand nand_3 (nand_1_out[1], inst_comp_2_a_old, clr);
  Register #(.Bits(4)) register_11 (.D(multiplexer_12_out), .C(C_ct), .en(DIR_LD), .Q(DIR_INST));
  Register register_12 (.D(multiplexer_13_out), .C(C_ct), .en(DIR_LD), .Q(register_12_q));
  Register #(.Bits(32)) register_13 (.D(multiplexer_14_out), .C(C_dt), .en(DIR_LD), .Q(DIR));
  Register #(.Bits(8)) register_14 (.D(multiplexer_15_out), .C(C_ct), .en(DIR_LD), .Q(DIR_WR));
  nand nand_4 (nand_2_out[1], DIR_busy, register_5_q[1]);
  inst_comp inst_comp_3 (
    .A_id(DIR_INST), .A_ep(register_12_q), .B_id(clr_id), .B_ep(clr_ep), .A_old(inst_comp_3_a_old));
  not not_5 (nand_2_out[0], DIR_busy);
  nand nand_5 (nand_1_out[0], inst_comp_3_a_old, clr);
endmodule
