// Digital circuit execution buffer-4.dig as structural Verilog
module execution_buffer_4 (
);

  wire and_1_out, and_2_out, and_3_out, and_4_out, and_5_out, and_6_out, and_7_out, and_8_out, and_10_out,
       and_11_out, and_12_out, and_13_out, and_15_out, C_ct, clr, clr_ep, comparator_1_eq, comparator_2_eq,
       comparator_3_eq, comparator_4_eq, CT_FU__EPOCH, CT_RET__LD, d_ff_1_q, inst_comp_1_a_new,
       inst_comp_2_a_new, inst_comp_3_a_new, inst_comp_4_a_new, MB_MFE, multiplexer_1_out, multiplexer_2_out,
       multiplexer_3_out, multiplexer_4_out, multiplexer_7_out, multiplexer_8_out, multiplexer_10_out,
       multiplexer_11_out, multiplexer_12_out, multiplexer_13_out, multiplexer_15_out, multiplexer_16_out,
       multiplexer_17_out, multiplexer_18_out, not_1_out, not_3_out, not_4_out, not_5_out, not_6_out,
       or_1_out, or_2_out, or_3_out, or_4_out, or_6_out, or_8_out, or_10_out, or_11_out, register_3_q,
       register_5_q, register_8_q, register_11_q, RET_busy, RET_busy__I, RET_CLR, RET_free, RET_free__I,
       RET_LD, RET_RD, RET_ST, rs_ff_1_q, rs_ff_2_q, rs_ff_3_q, rs_ff_4_q, rs_ff_5_nq;
  wire [0:0] or_9_out;
  wire [2:1] register_6_q;
  wire [3:0] and_9_out, clr_id, CT_FU__INST, MB_INST, multiplexer_5_out, multiplexer_6_out,
       multiplexer_9_out, multiplexer_14_out, nand_1_out, nand_3_out, not_2_out, register_2_q, register_4_q,
       register_7_q, RET_INST;

  not not_1 (not_1_out, clr);
  Multiplexer multiplexer_1 (.sel(and_9_out[3]), .in_0(nand_1_out[3]), .in_1(not_1_out), .out(multiplexer_1_out));
  not not_2 (not_2_out[0], or_9_out[0]);
  xor xor_1 (not_2_out[1], or_9_out[0], clr);
  xor xor_2 (not_2_out[2], clr, clr);
  xor xor_3 (not_2_out[3], clr, clr);
  Multiplexer multiplexer_2 (.sel(multiplexer_5_out[3]), .in_0(and_3_out), .in_1(1'b0), .out(multiplexer_2_out));
  and and_1 (and_1_out, ~1'b0, multiplexer_5_out[3]);  // And
  RS_FF rs_ff_1 (.S(multiplexer_2_out), .C(C_ct), .R(and_1_out), .Q(rs_ff_1_q));  // open: nQ
  and and_2 (and_2_out, multiplexer_1_out, CT_RET__LD);
  Register register_1 (.D(and_2_out), .C(C_ct), .en(or_1_out), .Q(clr));
  not not_3 (not_3_out, multiplexer_1_out);
  or or_1 (or_1_out, not_3_out, multiplexer_5_out[3]);
  or or_2 (or_2_out, and_9_out[0], and_9_out[1], and_9_out[2], and_9_out[3]);
  Register #(.Bits(4)) register_2 (.D(CT_FU__INST), .C(C_ct), .en(multiplexer_5_out[3]), .Q(register_2_q));
  Register register_3 (.D(CT_FU__EPOCH), .C(C_ct), .en(multiplexer_5_out[3]), .Q(register_3_q));
  Comparator #(.Bits(4)) comparator_1 (.a(register_2_q), .b(MB_INST), .eq(comparator_1_eq));  // open: gt, lt
  or or_3 (or_3_out, rs_ff_1_q, and_3_out);
  Multiplexer multiplexer_3 (.sel(and_9_out[2]), .in_0(nand_1_out[2]), .in_1(nand_1_out[3]), .out(multiplexer_3_out));
  Multiplexer multiplexer_4 (.sel(clr), .in_0(CT_RET__LD), .in_1(clr), .out(multiplexer_4_out));
  Multiplexer #(.Bits(4)) multiplexer_5 (.sel(or_2_out), .in_0(not_2_out), .in_1(and_9_out), .out(multiplexer_5_out));
  Multiplexer #(.Bits(4)) multiplexer_6 (.sel(clr), .in_0(CT_FU__INST), .in_1(register_2_q), .out(multiplexer_6_out));
  inst_comp inst_comp_1 (
    .A_id(register_2_q), .A_ep(register_3_q), .B_id(clr_id), .B_ep(clr_ep), .A_new(inst_comp_1_a_new));
  Multiplexer multiplexer_7 (.sel(clr), .in_0(CT_FU__EPOCH), .in_1(register_3_q), .out(multiplexer_7_out));
  and and_3 (and_3_out, comparator_1_eq, MB_MFE);
  Multiplexer multiplexer_8 (.sel(multiplexer_5_out[2]), .in_0(and_6_out), .in_1(or_3_out), .out(multiplexer_8_out));
  and and_4 (and_4_out, ~or_3_out, multiplexer_5_out[2]);  // And
  and and_5 (and_5_out, multiplexer_3_out, multiplexer_4_out);
  not not_4 (not_4_out, multiplexer_3_out);
  nand nand_1 (nand_1_out[3], inst_comp_1_a_new, clr);
  Register #(.Bits(4)) register_4 (.D(multiplexer_6_out), .C(C_ct), .en(multiplexer_5_out[2]), .Q(register_4_q));
  Register register_5 (.D(multiplexer_7_out), .C(C_ct), .en(multiplexer_5_out[2]), .Q(register_5_q));
  Comparator #(.Bits(4)) comparator_2 (.a(register_4_q), .b(MB_INST), .eq(comparator_2_eq));  // open: gt, lt
  RS_FF rs_ff_2 (.S(multiplexer_8_out), .C(C_ct), .R(and_4_out), .Q(rs_ff_2_q));  // open: nQ
  Register register_6 (.D(and_5_out), .C(C_ct), .en(or_4_out), .Q(register_6_q[2]));
  or or_4 (or_4_out, not_4_out, multiplexer_5_out[2]);
  or or_5 (clr, register_6_q[2], clr);
  Multiplexer #(.Bits(4)) multiplexer_9 (.sel(clr), .in_0(CT_FU__INST), .in_1(register_4_q), .out(multiplexer_9_out));
  inst_comp inst_comp_2 (
    .A_id(register_4_q), .A_ep(register_5_q), .B_id(clr_id), .B_ep(clr_ep), .A_new(inst_comp_2_a_new));
  Multiplexer multiplexer_10 (.sel(clr), .in_0(CT_FU__EPOCH), .in_1(register_5_q), .out(multiplexer_10_out));
  and and_6 (and_6_out, comparator_2_eq, MB_MFE);
  or or_6 (or_6_out, rs_ff_2_q, and_6_out);
  Multiplexer multiplexer_11 (.sel(and_9_out[1]), .in_0(nand_1_out[1]), .in_1(nand_1_out[2]), .out(multiplexer_11_out));
  Multiplexer multiplexer_12 (.sel(clr), .in_0(CT_RET__LD), .in_1(register_6_q[2]), .out(multiplexer_12_out));
  and and_7 (and_7_out, multiplexer_11_out, multiplexer_12_out);
  not not_5 (not_5_out, multiplexer_11_out);
  or or_7 (clr, register_6_q[1], register_6_q[2], clr);
  nand nand_2 (nand_1_out[2], inst_comp_2_a_new, clr);
  Register #(.Bits(4)) register_7 (.D(multiplexer_9_out), .C(C_ct), .en(multiplexer_5_out[1]), .Q(register_7_q));
  Register register_8 (.D(multiplexer_10_out), .C(C_ct), .en(multiplexer_5_out[1]), .Q(register_8_q));
  Comparator #(.Bits(4)) comparator_3 (.a(register_7_q), .b(MB_INST), .eq(comparator_3_eq));  // open: gt, lt
  Multiplexer multiplexer_13 (.sel(multiplexer_5_out[1]), .in_0(and_10_out), .in_1(or_6_out), .out(multiplexer_13_out));
  and and_8 (and_8_out, ~or_6_out, multiplexer_5_out[1]);  // And
  RS_FF rs_ff_3 (.S(multiplexer_13_out), .C(C_ct), .R(and_8_out), .Q(rs_ff_3_q));  // open: nQ
  Register register_9 (.D(and_7_out), .C(C_ct), .en(or_8_out), .Q(register_6_q[1]));
  or or_8 (or_8_out, not_5_out, multiplexer_5_out[1]);
  or or_9 (or_9_out[0], RET_busy__I, register_6_q[1], register_6_q[2], clr);
  assign and_9_out = nand_3_out & {{3{clr}}, or_9_out[0]};  // And and_9, 4 bits wide
  Multiplexer #(.Bits(4)) multiplexer_14 (.sel(clr), .in_0(CT_FU__INST), .in_1(register_7_q), .out(multiplexer_14_out));
  inst_comp inst_comp_3 (
    .A_id(register_7_q), .A_ep(register_8_q), .B_id(clr_id), .B_ep(clr_ep), .A_new(inst_comp_3_a_new));
  Multiplexer multiplexer_15 (.sel(clr), .in_0(CT_FU__EPOCH), .in_1(register_8_q), .out(multiplexer_15_out));
  and and_10 (and_10_out, comparator_3_eq, MB_MFE);
  or or_10 (or_10_out, rs_ff_3_q, and_10_out);
  Multiplexer multiplexer_16 (.sel(and_9_out[0]), .in_0(nand_1_out[0]), .in_1(nand_1_out[1]), .out(multiplexer_16_out));
  Multiplexer multiplexer_17 (.sel(clr), .in_0(CT_RET__LD), .in_1(register_6_q[1]), .out(multiplexer_17_out));
  and and_11 (and_11_out, multiplexer_16_out, multiplexer_17_out);
  nand nand_3 (nand_3_out[3], RET_busy__I, register_6_q[1], register_6_q[2], clr);
  nand nand_4 (nand_1_out[1], inst_comp_3_a_new, clr);
  Register #(.Bits(4)) register_10 (.D(multiplexer_14_out), .C(C_ct), .en(RET_LD), .Q(RET_INST));
  Register register_11 (.D(multiplexer_15_out), .C(C_ct), .en(RET_LD), .Q(register_11_q));
  Comparator #(.Bits(4)) comparator_4 (.a(RET_INST), .b(MB_INST), .eq(comparator_4_eq));  // open: gt, lt
  Multiplexer multiplexer_18 (.sel(RET_LD), .in_0(and_13_out), .in_1(or_10_out), .out(multiplexer_18_out));
  and and_12 (and_12_out, ~or_10_out, RET_LD);  // And
  RS_FF rs_ff_4 (.S(multiplexer_18_out), .C(C_ct), .R(and_12_out), .Q(rs_ff_4_q));  // open: nQ
  not not_6 (not_6_out, and_7_out);
  nand nand_5 (nand_3_out[2], RET_busy__I, register_6_q[1], register_6_q[2]);
  and and_13 (and_13_out, comparator_4_eq, MB_MFE);
  or or_11 (or_11_out, rs_ff_4_q, and_13_out);
  or or_12 (RET_free, not_6_out, RET_ST);
  nand nand_6 (nand_3_out[1], RET_busy__I, register_6_q[1]);
  not not_7 (nand_3_out[0], RET_busy__I);
  inst_comp inst_comp_4 (
    .A_id(RET_INST), .A_ep(register_11_q), .B_id(clr_id), .B_ep(clr_ep), .A_new(inst_comp_4_a_new));
  not not_8 (RET_busy, RET_free);
  nand nand_7 (nand_1_out[0], inst_comp_4_a_new, clr);
  and and_14 (RET_CLR, clr, inst_comp_4_a_new);
  D_FF d_ff_1 (.D(or_11_out), .C(C_ct), .Q(d_ff_1_q));  // open: nQ
  and and_15 (and_15_out, ~and_11_out, RET_ST);  // And
  D_FF d_ff_2 (.D(d_ff_1_q), .C(C_ct), .Q(RET_ST));  // open: nQ
  RS_FF rs_ff_5 (.S(and_11_out), .C(C_ct), .R(and_15_out), .Q(RET_RD), .nQ(rs_ff_5_nq));
  or or_13 (RET_free__I, RET_ST, rs_ff_5_nq);
  and and_16 (RET_LD, and_11_out, RET_free__I);
  not not_9 (RET_busy__I, RET_free__I);
endmodule
