// Digital circuit history3.dig as structural Verilog
module history3 (
  input  [4:0] R,
  input  [31:0] D,
  input  push,
  input  C,
  input  pop,
  input  ex_push,
  input  [4:0] RBP,
  output [7:0] out,
  output empty,
  output full,
  output [31:0] out1,
  output [31:0] out2,
  output [31:0] out3,
  output [31:0] out4,
  output [31:0] out5,
  output [31:0] out6,
  output [31:0] out7,
  output [31:0] out8
);

  wire addr_0, counterpreset_1_ovf, d_ff_1_q, halt, HFH1, HFH2, HFH3, HFH4, HFH5, HFH6, HFH7, HFH8, HFM1,
       HFM2, HFM3, HFM4, HFM5, HFM6, HFM7, HFM8, HFS1, HFS2, HFS3, HFS4, HFS5, HFS6, HFS7, HFS8, HFV1, HFV2,
       HFV3, HFV4, HFV5, HFV6, HFV7, HFV8, LM1, LM2, LM3, LM4, not_2_out, PM1, PM2, PM3, PM4,
       priorityencoder_1_any, priorityencoder_2_any, priorityencoder_3_any, priorityencoder_4_any,
       priorityencoder_5_any, priorityencoder_6_any, priorityencoder_7_any, priorityencoder_8_any, sub_3_c_o,
       W1, W2, W3, W4, xor_2_out;
  wire [0:0] not_1_out, undriven;
  wire [1:1] addr_01;
  wire [2:0] add_2_s, priorityencoder_1_num, priorityencoder_2_num, priorityencoder_3_num,
       priorityencoder_4_num, priorityencoder_5_num, priorityencoder_6_num, priorityencoder_7_num,
       priorityencoder_8_num, sub_1_s, sub_2_s;
  wire [3:0] bitextender_2_out, decoder_1_out_0;
  wire [4:0] add_1_s, addr_234, bitextender_1_out, counterpreset_1_out, multiplexer_3_out, multiplexer_4_out,
       multiplexer_5_out, multiplexer_6_out, multiplexer_7_out, multiplexer_9_out, multiplexer_11_out,
       multiplexer_13_out, multiplexer_15_out, sub_3_s, top, top_plus_1, xor_1_out;
  wire [7:0] bitextender_3_out, D_t, demultiplexer_2_out_0, demultiplexer_2_out_1, demultiplexer_2_out_2,
       demultiplexer_2_out_3, demultiplexer_2_out_4, demultiplexer_2_out_5, demultiplexer_2_out_6,
       demultiplexer_2_out_7, demultiplexer_10_out_6, demultiplexer_10_out_7, demultiplexer_11_out_0,
       demultiplexer_11_out_1, demultiplexer_11_out_2, demultiplexer_11_out_3, demultiplexer_11_out_4,
       demultiplexer_11_out_5, fill_8_1_out8;
  wire [41:0] HF1, HF1_da, HF1_db, HF2, HF2_da, HF2_db, HF3, HF3_da, HF3_db, HF4, HF4_da, HF4_db, HF5, HF6,
       HF7, HF8, log1, log2, multiplexer_8_out, multiplexer_10_out, multiplexer_12_out, multiplexer_14_out,
       register_2_q, register_3_q, register_4_q, register_5_q, register_6_q, register_7_q, register_8_q,
       register_9_q;

  not not_1 (not_1_out[0], ex_push);
  BitExtender #(.inputBits(1), .outputBits(5)) bitextender_1 (.in(pop), .out(bitextender_1_out));
  assign xor_1_out = bitextender_1_out ^ {1'b0, pop, 1'b0, ex_push, not_1_out[0]};  // XOr xor_1, 5 bits wide
  Decoder #(.Selector_Bits(2)) decoder_1 (
    .sel({addr_01[1], addr_0}), .out_0(decoder_1_out_0[0]), .out_1(decoder_1_out_0[1]),
    .out_2(decoder_1_out_0[2]), .out_3(decoder_1_out_0[3]));
  Add #(.Bits(5)) add_1 (.a({addr_234[2:0], addr_01[1], addr_0}), .b(xor_1_out), .c_i(pop), .s(add_1_s));  // open: c_o
  Add #(.Bits(3)) add_2 (.a(addr_234[2:0]), .b(3'b001), .c_i(1'b0), .s(add_2_s));  // open: c_o
  Sub #(.Bits(3)) sub_1 (.a(addr_234[2:0]), .b(3'b001), .c_i(1'b0), .s(sub_1_s));  // open: c_o
  Sub #(.Bits(3)) sub_2 (.a(addr_234[2:0]), .b(3'b010), .c_i(1'b0), .s(sub_2_s));  // open: c_o
  BitExtender #(.inputBits(1), .outputBits(4)) bitextender_2 (.in(ex_push), .out(bitextender_2_out));
  Register #(.Bits(5)) register_1 (.D(add_1_s), .C(C), .Q({addr_234[2:0], addr_01[1], addr_0}));  // open: en
  assign {LM4, LM3, LM2, LM1} = {decoder_1_out_0[2:0], undriven[0]} & bitextender_2_out;  // And and_1, 4 bits wide
  xor xor_2 (xor_2_out, pop, push);
  Multiplexer #(.Bits(3)) multiplexer_1 (.sel(pop), .in_0(add_2_s), .in_1(sub_1_s), .out(top_plus_1[2:0]));
  Multiplexer #(.Bits(3)) multiplexer_2 (.sel(pop), .in_0(addr_234[2:0]), .in_1(sub_2_s), .out(top[2:0]));
  assign {W4, W3, W2, W1} = decoder_1_out_0 | {LM4, LM3, LM2, LM1};  // Or or_1, 4 bits wide
  CounterPreset #(.Bits(5)) counterpreset_1 (
    .en(xor_2_out), .C(C), .dir(pop), .in({5{1'b0}}), .ld(1'b0), .clr(1'b0), .out(counterpreset_1_out),
    .ovf(counterpreset_1_ovf));
  D_FF d_ff_1 (.D(counterpreset_1_ovf), .C(C), .Q(d_ff_1_q));  // open: nQ
  Sub #(.Bits(5)) sub_3 (.a(counterpreset_1_out), .b(5'b00001), .c_i(1'b0), .s(sub_3_s), .c_o(sub_3_c_o));
  Multiplexer #(.Bits(5)) multiplexer_3 (
    .sel(xor_2_out), .in_0(sub_3_s), .in_1(counterpreset_1_out), .out(multiplexer_3_out));
  and and_2 (empty, sub_3_c_o, ~d_ff_1_q);  // And
  and and_3 (full, d_ff_1_q, sub_3_c_o);
  RegisterFile #(.AddrBits(5), .Bits(8)) registerfile_1 (
    .Din(D_t), .we(push), .Rw(multiplexer_3_out), .C(C), .Ra(sub_3_s), .Rb({5{1'b0}}), .Da(out));  // open: Db
  Multiplexer #(.Bits(5)) multiplexer_4 (.sel(PM1), .in_0(top_plus_1), .in_1(addr_234), .out(multiplexer_4_out));
  Multiplexer #(.Bits(5)) multiplexer_5 (.sel(PM2), .in_0(top_plus_1), .in_1(addr_234), .out(multiplexer_5_out));
  Multiplexer #(.Bits(5)) multiplexer_6 (.sel(PM3), .in_0(top_plus_1), .in_1(addr_234), .out(multiplexer_6_out));
  Multiplexer #(.Bits(5)) multiplexer_7 (.sel(PM4), .in_0(top_plus_1), .in_1(addr_234), .out(multiplexer_7_out));
  Multiplexer #(.Bits(42)) multiplexer_8 (.sel(LM1), .in_0(log1), .in_1(log2), .out(multiplexer_8_out));
  Multiplexer #(.Bits(5)) multiplexer_9 (.sel(PM1), .in_0(top), .in_1(top_plus_1), .out(multiplexer_9_out));
  Multiplexer #(.Bits(42)) multiplexer_10 (.sel(LM2), .in_0(log1), .in_1(log2), .out(multiplexer_10_out));
  Multiplexer #(.Bits(5)) multiplexer_11 (.sel(PM2), .in_0(top), .in_1(top_plus_1), .out(multiplexer_11_out));
  Multiplexer #(.Bits(42)) multiplexer_12 (.sel(LM3), .in_0(log1), .in_1(log2), .out(multiplexer_12_out));
  Multiplexer #(.Bits(5)) multiplexer_13 (.sel(PM3), .in_0(top), .in_1(top_plus_1), .out(multiplexer_13_out));
  Multiplexer #(.Bits(42)) multiplexer_14 (.sel(LM4), .in_0(log1), .in_1(log2), .out(multiplexer_14_out));
  Multiplexer #(.Bits(5)) multiplexer_15 (.sel(PM4), .in_0(top), .in_1(top_plus_1), .out(multiplexer_15_out));
  RegisterFile #(.AddrBits(3), .Bits(42)) u_HF1 (
    .Din(multiplexer_8_out), .we(W1), .Rw(multiplexer_9_out[2:0]), .C(C), .Ra(multiplexer_9_out[2:0]),
    .Rb(multiplexer_4_out[2:0]), .Da(HF1_da), .Db(HF1_db));
  RegisterFile #(.AddrBits(3), .Bits(42)) u_HF2 (
    .Din(multiplexer_10_out), .we(W2), .Rw(multiplexer_11_out[2:0]), .C(C), .Ra(multiplexer_11_out[2:0]),
    .Rb(multiplexer_5_out[2:0]), .Da(HF2_da), .Db(HF2_db));
  RegisterFile #(.AddrBits(3), .Bits(42)) u_HF3 (
    .Din(multiplexer_12_out), .we(W3), .Rw(multiplexer_13_out[2:0]), .C(C), .Ra(multiplexer_13_out[2:0]),
    .Rb(multiplexer_6_out[2:0]), .Da(HF3_da), .Db(HF3_db));
  RegisterFile #(.AddrBits(3), .Bits(42)) u_HF4 (
    .Din(multiplexer_14_out), .we(W4), .Rw(multiplexer_15_out[2:0]), .C(C), .Ra(multiplexer_15_out[2:0]),
    .Rb(multiplexer_7_out[2:0]), .Da(HF4_da), .Db(HF4_db));
  Register #(.Bits(42)) register_2 (.D(HF1_da), .C(C), .en(HFS1), .Q(register_2_q));
  Register #(.Bits(42)) register_3 (.D(HF1_db), .C(C), .en(HFS5), .Q(register_3_q));
  Register #(.Bits(42)) register_4 (.D(HF2_da), .C(C), .en(HFS2), .Q(register_4_q));
  Register #(.Bits(42)) register_5 (.D(HF2_db), .C(C), .en(HFS6), .Q(register_5_q));
  Register #(.Bits(42)) register_6 (.D(HF3_da), .C(C), .en(HFS3), .Q(register_6_q));
  Register #(.Bits(42)) register_7 (.D(HF3_db), .C(C), .en(HFS7), .Q(register_7_q));
  Register #(.Bits(42)) register_8 (.D(HF4_da), .C(C), .en(HFS4), .Q(register_8_q));
  Register #(.Bits(42)) register_9 (.D(HF4_db), .C(C), .en(HFS8), .Q(register_9_q));
  Multiplexer #(.Bits(42)) multiplexer_16 (.sel(HFM1), .in_0(HF1_da), .in_1(register_2_q), .out(HF1));
  Multiplexer #(.Bits(42)) multiplexer_17 (.sel(HFM5), .in_0(HF1_db), .in_1(register_3_q), .out(HF5));
  Multiplexer #(.Bits(42)) multiplexer_18 (.sel(HFM2), .in_0(HF2_da), .in_1(register_4_q), .out(HF2));
  Multiplexer #(.Bits(42)) multiplexer_19 (.sel(HFM6), .in_0(HF2_db), .in_1(register_5_q), .out(HF6));
  Multiplexer #(.Bits(42)) multiplexer_20 (.sel(HFM3), .in_0(HF3_da), .in_1(register_6_q), .out(HF3));
  Multiplexer #(.Bits(42)) multiplexer_21 (.sel(HFM7), .in_0(HF3_db), .in_1(register_7_q), .out(HF7));
  Multiplexer #(.Bits(42)) multiplexer_22 (.sel(HFM4), .in_0(HF4_da), .in_1(register_8_q), .out(HF4));
  Multiplexer #(.Bits(42)) multiplexer_23 (.sel(HFM8), .in_0(HF4_db), .in_1(register_9_q), .out(HF8));
  fill_8 fill_8_1 (
    .on(1'b0), .in1(HFH1), .in2(HFH2), .in3(HFH3), .in4(HFH4), .in5(HFH5), .in6(HFH6), .in7(HFH7),
    .in8(HFH8), .out1(fill_8_1_out8[0]), .out2(fill_8_1_out8[1]), .out3(fill_8_1_out8[2]),
    .out4(fill_8_1_out8[3]), .out5(fill_8_1_out8[4]), .out6(fill_8_1_out8[5]), .out7(fill_8_1_out8[6]),
    .out8(fill_8_1_out8[7]), .v(halt));
  BitExtender #(.inputBits(1), .outputBits(8)) bitextender_3 (.in(not_2_out), .out(bitextender_3_out));
  not not_2 (not_2_out, halt);
  or or_2 (HFV1, fill_8_1_out8[0], bitextender_3_out[0]);
  Comparator comparator_1 (.a(HF1[37]), .b(RBP[0]), .eq(HFH1));  // open: gt, lt
  Comparator comparator_2 (.a(HF2[37]), .b(RBP[0]), .eq(HFH2));  // open: gt, lt
  Comparator comparator_3 (.a(HF3[37]), .b(RBP[0]), .eq(HFH3));  // open: gt, lt
  Comparator comparator_4 (.a(HF4[37]), .b(RBP[0]), .eq(HFH4));  // open: gt, lt
  Comparator comparator_5 (.a(HF5[37]), .b(RBP[0]), .eq(HFH5));  // open: gt, lt
  Comparator comparator_6 (.a(HF6[37]), .b(RBP[0]), .eq(HFH6));  // open: gt, lt
  Comparator comparator_7 (.a(HF7[37]), .b(RBP[0]), .eq(HFH7));  // open: gt, lt
  Comparator comparator_8 (.a(HF8[37]), .b(RBP[0]), .eq(HFH8));  // open: gt, lt
  Demultiplexer #(.Selector_Bits(3)) demultiplexer_1 (
    .sel(HF1[34:32]), .in(HFV1), .out_0(demultiplexer_2_out_0[0]), .out_1(demultiplexer_2_out_1[0]),
    .out_2(demultiplexer_2_out_2[0]), .out_3(demultiplexer_2_out_3[0]), .out_4(demultiplexer_2_out_4[0]),
    .out_5(demultiplexer_2_out_5[0]), .out_6(demultiplexer_2_out_6[0]), .out_7(demultiplexer_2_out_7[0]));
  Demultiplexer #(.Selector_Bits(3)) demultiplexer_2 (
    .sel(HF2[34:32]), .in(HFV2), .out_0(demultiplexer_2_out_0[1]), .out_1(demultiplexer_2_out_1[1]),
    .out_2(demultiplexer_2_out_2[1]), .out_3(demultiplexer_2_out_3[1]), .out_4(demultiplexer_2_out_4[1]),
    .out_5(demultiplexer_2_out_5[1]), .out_6(demultiplexer_2_out_6[1]), .out_7(demultiplexer_2_out_7[1]));
  Demultiplexer #(.Selector_Bits(3)) demultiplexer_3 (
    .sel(HF3[34:32]), .in(HFV3), .out_0(demultiplexer_2_out_0[2]), .out_1(demultiplexer_2_out_1[2]),
    .out_2(demultiplexer_2_out_2[2]), .out_3(demultiplexer_2_out_3[2]), .out_4(demultiplexer_2_out_4[2]),
    .out_5(demultiplexer_2_out_5[2]), .out_6(demultiplexer_2_out_6[2]), .out_7(demultiplexer_2_out_7[2]));
  Demultiplexer #(.Selector_Bits(3)) demultiplexer_4 (
    .sel(HF4[34:32]), .in(HFV4), .out_0(demultiplexer_2_out_0[3]), .out_1(demultiplexer_2_out_1[3]),
    .out_2(demultiplexer_2_out_2[3]), .out_3(demultiplexer_2_out_3[3]), .out_4(demultiplexer_2_out_4[3]),
    .out_5(demultiplexer_2_out_5[3]), .out_6(demultiplexer_2_out_6[3]), .out_7(demultiplexer_2_out_7[3]));
  Demultiplexer #(.Selector_Bits(3)) demultiplexer_5 (
    .sel(HF5[34:32]), .in(HFV5), .out_0(demultiplexer_2_out_0[4]), .out_1(demultiplexer_2_out_1[4]),
    .out_2(demultiplexer_2_out_2[4]), .out_3(demultiplexer_2_out_3[4]), .out_4(demultiplexer_2_out_4[4]),
    .out_5(demultiplexer_2_out_5[4]), .out_6(demultiplexer_2_out_6[4]), .out_7(demultiplexer_2_out_7[4]));
  Demultiplexer #(.Selector_Bits(3)) demultiplexer_6 (
    .sel(HF6[34:32]), .in(HFV6), .out_0(demultiplexer_2_out_0[5]), .out_1(demultiplexer_2_out_1[5]),
    .out_2(demultiplexer_2_out_2[5]), .out_3(demultiplexer_2_out_3[5]), .out_4(demultiplexer_2_out_4[5]),
    .out_5(demultiplexer_2_out_5[5]), .out_6(demultiplexer_2_out_6[5]), .out_7(demultiplexer_2_out_7[5]));
  Demultiplexer #(.Selector_Bits(3)) demultiplexer_7 (
    .sel(HF7[34:32]), .in(HFV7), .out_0(demultiplexer_2_out_0[6]), .out_1(demultiplexer_2_out_1[6]),
    .out_2(demultiplexer_2_out_2[6]), .out_3(demultiplexer_2_out_3[6]), .out_4(demultiplexer_2_out_4[6]),
    .out_5(demultiplexer_2_out_5[6]), .out_6(demultiplexer_2_out_6[6]), .out_7(demultiplexer_2_out_7[6]));
  Demultiplexer #(.Selector_Bits(3)) demultiplexer_8 (
    .sel(HF8[34:32]), .in(HFV8), .out_0(demultiplexer_2_out_0[7]), .out_1(demultiplexer_2_out_1[7]),
    .out_2(demultiplexer_2_out_2[7]), .out_3(demultiplexer_2_out_3[7]), .out_4(demultiplexer_2_out_4[7]),
    .out_5(demultiplexer_2_out_5[7]), .out_6(demultiplexer_2_out_6[7]), .out_7(demultiplexer_2_out_7[7]));
  PriorityEncoder #(.Selector_Bits(3)) priorityencoder_1 (
    .in0(demultiplexer_2_out_0[7]), .in1(demultiplexer_2_out_0[6]), .in2(demultiplexer_2_out_0[5]),
    .in3(demultiplexer_2_out_0[4]), .in4(demultiplexer_2_out_0[3]), .in5(demultiplexer_2_out_0[2]),
    .in6(demultiplexer_2_out_0[1]), .in7(demultiplexer_2_out_0[0]), .num(priorityencoder_1_num),
    .any(priorityencoder_1_any));
  PriorityEncoder #(.Selector_Bits(3)) priorityencoder_2 (
    .in0(demultiplexer_2_out_1[7]), .in1(demultiplexer_2_out_1[6]), .in2(demultiplexer_2_out_1[5]),
    .in3(demultiplexer_2_out_1[4]), .in4(demultiplexer_2_out_1[3]), .in5(demultiplexer_2_out_1[2]),
    .in6(demultiplexer_2_out_1[1]), .in7(demultiplexer_2_out_1[0]), .num(priorityencoder_2_num),
    .any(priorityencoder_2_any));
  PriorityEncoder #(.Selector_Bits(3)) priorityencoder_3 (
    .in0(demultiplexer_2_out_2[7]), .in1(demultiplexer_2_out_2[6]), .in2(demultiplexer_2_out_2[5]),
    .in3(demultiplexer_2_out_2[4]), .in4(demultiplexer_2_out_2[3]), .in5(demultiplexer_2_out_2[2]),
    .in6(demultiplexer_2_out_2[1]), .in7(demultiplexer_2_out_2[0]), .num(priorityencoder_3_num),
    .any(priorityencoder_3_any));
  PriorityEncoder #(.Selector_Bits(3)) priorityencoder_4 (
    .in0(demultiplexer_2_out_3[7]), .in1(demultiplexer_2_out_3[6]), .in2(demultiplexer_2_out_3[5]),
    .in3(demultiplexer_2_out_3[4]), .in4(demultiplexer_2_out_3[3]), .in5(demultiplexer_2_out_3[2]),
    .in6(demultiplexer_2_out_3[1]), .in7(demultiplexer_2_out_3[0]), .num(priorityencoder_4_num),
    .any(priorityencoder_4_any));
  PriorityEncoder #(.Selector_Bits(3)) priorityencoder_5 (
    .in0(demultiplexer_2_out_4[7]), .in1(demultiplexer_2_out_4[6]), .in2(demultiplexer_2_out_4[5]),
    .in3(demultiplexer_2_out_4[4]), .in4(demultiplexer_2_out_4[3]), .in5(demultiplexer_2_out_4[2]),
    .in6(demultiplexer_2_out_4[1]), .in7(demultiplexer_2_out_4[0]), .num(priorityencoder_5_num),
    .any(priorityencoder_5_any));
  PriorityEncoder #(.Selector_Bits(3)) priorityencoder_6 (
    .in0(demultiplexer_2_out_5[7]), .in1(demultiplexer_2_out_5[6]), .in2(demultiplexer_2_out_5[5]),
    .in3(demultiplexer_2_out_5[4]), .in4(demultiplexer_2_out_5[3]), .in5(demultiplexer_2_out_5[2]),
    .in6(demultiplexer_2_out_5[1]), .in7(demultiplexer_2_out_5[0]), .num(priorityencoder_6_num),
    .any(priorityencoder_6_any));
  PriorityEncoder #(.Selector_Bits(3)) priorityencoder_7 (
    .in0(demultiplexer_2_out_6[7]), .in1(demultiplexer_2_out_6[6]), .in2(demultiplexer_2_out_6[5]),
    .in3(demultiplexer_2_out_6[4]), .in4(demultiplexer_2_out_6[3]), .in5(demultiplexer_2_out_6[2]),
    .in6(demultiplexer_2_out_6[1]), .in7(demultiplexer_2_out_6[0]), .num(priorityencoder_7_num),
    .any(priorityencoder_7_any));
  PriorityEncoder #(.Selector_Bits(3)) priorityencoder_8 (
    .in0(demultiplexer_2_out_7[7]), .in1(demultiplexer_2_out_7[6]), .in2(demultiplexer_2_out_7[5]),
    .in3(demultiplexer_2_out_7[4]), .in4(demultiplexer_2_out_7[3]), .in5(demultiplexer_2_out_7[2]),
    .in6(demultiplexer_2_out_7[1]), .in7(demultiplexer_2_out_7[0]), .num(priorityencoder_8_num),
    .any(priorityencoder_8_any));
  Multiplexer #(.Selector_Bits(3), .Bits(32)) multiplexer_24 (
    .sel(priorityencoder_1_num), .in_0(HF8[31:0]), .in_1(HF7[31:0]), .in_2(HF6[31:0]), .in_3(HF5[31:0]),
    .in_4(HF4[31:0]), .in_5(HF3[31:0]), .in_6(HF2[31:0]), .in_7(HF1[31:0]), .out(out1));
  Multiplexer #(.Selector_Bits(3), .Bits(32)) multiplexer_25 (
    .sel(priorityencoder_2_num), .in_0(HF8[31:0]), .in_1(HF7[31:0]), .in_2(HF6[31:0]), .in_3(HF5[31:0]),
    .in_4(HF4[31:0]), .in_5(HF3[31:0]), .in_6(HF2[31:0]), .in_7(HF1[31:0]), .out(out2));
  Multiplexer #(.Selector_Bits(3), .Bits(32)) multiplexer_26 (
    .sel(priorityencoder_3_num), .in_0(HF8[31:0]), .in_1(HF7[31:0]), .in_2(HF6[31:0]), .in_3(HF5[31:0]),
    .in_4(HF4[31:0]), .in_5(HF3[31:0]), .in_6(HF2[31:0]), .in_7(HF1[31:0]), .out(out3));
  Multiplexer #(.Selector_Bits(3), .Bits(32)) multiplexer_27 (
    .sel(priorityencoder_4_num), .in_0(HF8[31:0]), .in_1(HF7[31:0]), .in_2(HF6[31:0]), .in_3(HF5[31:0]),
    .in_4(HF4[31:0]), .in_5(HF3[31:0]), .in_6(HF2[31:0]), .in_7(HF1[31:0]), .out(out4));
  Multiplexer #(.Selector_Bits(3), .Bits(32)) multiplexer_28 (
    .sel(priorityencoder_5_num), .in_0(HF8[31:0]), .in_1(HF7[31:0]), .in_2(HF6[31:0]), .in_3(HF5[31:0]),
    .in_4(HF4[31:0]), .in_5(HF3[31:0]), .in_6(HF2[31:0]), .in_7(HF1[31:0]), .out(out5));
  Multiplexer #(.Selector_Bits(3), .Bits(32)) multiplexer_29 (
    .sel(priorityencoder_6_num), .in_0(HF8[31:0]), .in_1(HF7[31:0]), .in_2(HF6[31:0]), .in_3(HF5[31:0]),
    .in_4(HF4[31:0]), .in_5(HF3[31:0]), .in_6(HF2[31:0]), .in_7(HF1[31:0]), .out(out6));
  Multiplexer #(.Selector_Bits(3), .Bits(32)) multiplexer_30 (
    .sel(priorityencoder_7_num), .in_0(HF8[31:0]), .in_1(HF7[31:0]), .in_2(HF6[31:0]), .in_3(HF5[31:0]),
    .in_4(HF4[31:0]), .in_5(HF3[31:0]), .in_6(HF2[31:0]), .in_7(HF1[31:0]), .out(out7));
  Multiplexer #(.Selector_Bits(3), .Bits(32)) multiplexer_31 (
    .sel(priorityencoder_8_num), .in_0(HF8[31:0]), .in_1(HF7[31:0]), .in_2(HF6[31:0]), .in_3(HF5[31:0]),
    .in_4(HF4[31:0]), .in_5(HF3[31:0]), .in_6(HF2[31:0]), .in_7(HF1[31:0]), .out(out8));
  Demultiplexer #(.Selector_Bits(3)) demultiplexer_9 (
    .sel(priorityencoder_1_num), .in(priorityencoder_1_any), .out_0(demultiplexer_11_out_0[0]),
    .out_1(demultiplexer_11_out_1[0]), .out_2(demultiplexer_11_out_2[0]), .out_3(demultiplexer_11_out_3[0]),
    .out_4(demultiplexer_11_out_4[0]), .out_5(demultiplexer_11_out_5[0]), .out_6(demultiplexer_10_out_6[0]),
    .out_7(demultiplexer_10_out_7[0]));
  Demultiplexer #(.Selector_Bits(3)) demultiplexer_10 (
    .sel(priorityencoder_2_num), .in(priorityencoder_2_any), .out_0(demultiplexer_11_out_0[1]),
    .out_1(demultiplexer_11_out_1[1]), .out_2(demultiplexer_11_out_2[1]), .out_3(demultiplexer_11_out_3[1]),
    .out_4(demultiplexer_11_out_4[1]), .out_5(demultiplexer_11_out_5[1]), .out_6(demultiplexer_10_out_6[1]),
    .out_7(demultiplexer_10_out_7[1]));
  Demultiplexer #(.Selector_Bits(3)) demultiplexer_11 (
    .sel(priorityencoder_3_num), .in(priorityencoder_3_any), .out_0(demultiplexer_11_out_0[2]),
    .out_1(demultiplexer_11_out_1[2]), .out_2(demultiplexer_11_out_2[2]), .out_3(demultiplexer_11_out_3[2]),
    .out_4(demultiplexer_11_out_4[2]), .out_5(demultiplexer_11_out_5[2]), .out_6(demultiplexer_10_out_6[2]),
    .out_7(demultiplexer_10_out_7[2]));
  Demultiplexer #(.Selector_Bits(3)) demultiplexer_12 (
    .sel(priorityencoder_4_num), .in(priorityencoder_4_any), .out_0(demultiplexer_11_out_0[3]),
    .out_1(demultiplexer_11_out_1[3]), .out_2(demultiplexer_11_out_2[3]), .out_3(demultiplexer_11_out_3[3]),
    .out_4(demultiplexer_11_out_4[3]), .out_5(demultiplexer_11_out_5[3]), .out_6(demultiplexer_10_out_6[3]),
    .out_7(demultiplexer_10_out_7[3]));
  Demultiplexer #(.Selector_Bits(3)) demultiplexer_13 (
    .sel(priorityencoder_5_num), .in(priorityencoder_5_any), .out_0(demultiplexer_11_out_0[4]),
    .out_1(demultiplexer_11_out_1[4]), .out_2(demultiplexer_11_out_2[4]), .out_3(demultiplexer_11_out_3[4]),
    .out_4(demultiplexer_11_out_4[4]), .out_5(demultiplexer_11_out_5[4]), .out_6(demultiplexer_10_out_6[4]),
    .out_7(demultiplexer_10_out_7[4]));
  Demultiplexer #(.Selector_Bits(3)) demultiplexer_14 (
    .sel(priorityencoder_6_num), .in(priorityencoder_6_any), .out_0(demultiplexer_11_out_0[5]),
    .out_1(demultiplexer_11_out_1[5]), .out_2(demultiplexer_11_out_2[5]), .out_3(demultiplexer_11_out_3[5]),
    .out_4(demultiplexer_11_out_4[5]), .out_5(demultiplexer_11_out_5[5]), .out_6(demultiplexer_10_out_6[5]),
    .out_7(demultiplexer_10_out_7[5]));
  Demultiplexer #(.Selector_Bits(3)) demultiplexer_15 (
    .sel(priorityencoder_7_num), .in(priorityencoder_7_any), .out_0(demultiplexer_11_out_0[6]),
    .out_1(demultiplexer_11_out_1[6]), .out_2(demultiplexer_11_out_2[6]), .out_3(demultiplexer_11_out_3[6]),
    .out_4(demultiplexer_11_out_4[6]), .out_5(demultiplexer_11_out_5[6]), .out_6(demultiplexer_10_out_6[6]),
    .out_7(demultiplexer_10_out_7[6]));
  Demultiplexer #(.Selector_Bits(3)) demultiplexer_16 (
    .sel(priorityencoder_8_num), .in(priorityencoder_8_any), .out_0(demultiplexer_11_out_0[7]),
    .out_1(demultiplexer_11_out_1[7]), .out_2(demultiplexer_11_out_2[7]), .out_3(demultiplexer_11_out_3[7]),
    .out_4(demultiplexer_11_out_4[7]), .out_5(demultiplexer_11_out_5[7]), .out_6(demultiplexer_10_out_6[7]),
    .out_7(demultiplexer_10_out_7[7]));
  nor nor_1 (HFS1, demultiplexer_11_out_0[7], demultiplexer_11_out_0[6], demultiplexer_11_out_0[5], demultiplexer_11_out_0[4], demultiplexer_11_out_0[3], demultiplexer_11_out_0[2], demultiplexer_11_out_0[1], demultiplexer_11_out_0[0]);
  nor nor_2 (HFS2, demultiplexer_11_out_1[7], demultiplexer_11_out_1[6], demultiplexer_11_out_1[5], demultiplexer_11_out_1[4], demultiplexer_11_out_1[3], demultiplexer_11_out_1[2], demultiplexer_11_out_1[1], demultiplexer_11_out_1[0]);
  nor nor_3 (HFS3, demultiplexer_11_out_2[7], demultiplexer_11_out_2[6], demultiplexer_11_out_2[5], demultiplexer_11_out_2[4], demultiplexer_11_out_2[3], demultiplexer_11_out_2[2], demultiplexer_11_out_2[1], demultiplexer_11_out_2[0]);
  nor nor_4 (HFS4, demultiplexer_11_out_3[7], demultiplexer_11_out_3[6], demultiplexer_11_out_3[5], demultiplexer_11_out_3[4], demultiplexer_11_out_3[3], demultiplexer_11_out_3[2], demultiplexer_11_out_3[1], demultiplexer_11_out_3[0]);
  nor nor_5 (HFS5, demultiplexer_11_out_4[7], demultiplexer_11_out_4[6], demultiplexer_11_out_4[5], demultiplexer_11_out_4[4], demultiplexer_11_out_4[3], demultiplexer_11_out_4[2], demultiplexer_11_out_4[1], demultiplexer_11_out_4[0]);
  nor nor_6 (HFS6, demultiplexer_11_out_5[7], demultiplexer_11_out_5[6], demultiplexer_11_out_5[5], demultiplexer_11_out_5[4], demultiplexer_11_out_5[3], demultiplexer_11_out_5[2], demultiplexer_11_out_5[1], demultiplexer_11_out_5[0]);
  nor nor_7 (HFS7, demultiplexer_10_out_6[7], demultiplexer_10_out_6[6], demultiplexer_10_out_6[5], demultiplexer_10_out_6[4], demultiplexer_10_out_6[3], demultiplexer_10_out_6[2], demultiplexer_10_out_6[1], demultiplexer_10_out_6[0]);
  nor nor_8 (HFS8, demultiplexer_10_out_7[7], demultiplexer_10_out_7[6], demultiplexer_10_out_7[5], demultiplexer_10_out_7[4], demultiplexer_10_out_7[3], demultiplexer_10_out_7[2], demultiplexer_10_out_7[1], demultiplexer_10_out_7[0]);
  D_FF d_ff_2 (.D(HFS1), .C(C), .Q(HFM1));  // open: nQ
  D_FF d_ff_3 (.D(HFS2), .C(C), .Q(HFM2));  // open: nQ
  D_FF d_ff_4 (.D(HFS3), .C(C), .Q(HFM3));  // open: nQ
  D_FF d_ff_5 (.D(HFS4), .C(C), .Q(HFM4));  // open: nQ
  D_FF d_ff_6 (.D(HFS5), .C(C), .Q(HFM5));  // open: nQ
  D_FF d_ff_7 (.D(HFS6), .C(C), .Q(HFM6));  // open: nQ
  D_FF d_ff_8 (.D(HFS7), .C(C), .Q(HFM7));  // open: nQ
  D_FF d_ff_9 (.D(HFS8), .C(C), .Q(HFM8));  // open: nQ
  // Pins of 3 and 5 bits meet at multiplexer_9_out
  // Pins of 3 and 5 bits meet at multiplexer_4_out
  // Pins of 3 and 5 bits meet at multiplexer_11_out
  // Pins of 3 and 5 bits meet at multiplexer_5_out
  // Pins of 3 and 5 bits meet at multiplexer_13_out
  // Pins of 3 and 5 bits meet at multiplexer_6_out
  // Pins of 3 and 5 bits meet at multiplexer_15_out
  // Pins of 3 and 5 bits meet at multiplexer_7_out
  // Pins of 3 and 5 bits meet at top_plus_1
  // Pins of 3 and 5 bits meet at addr_234
  // Pins of 3 and 5 bits meet at top
  // Pins of 1 and 5 bits meet at HF1[41:37]

  // Other names for the same wires on the sheet: addr_01[0] = addr_0; addr_1 = addr_01[1]; top_plus_2[4:0] = addr_234;
  //   D_in[31:0] = D; H_in[36:0] = {R, D}; HFD1[31:0] = HF1[31:0]; HFR1[4:0] = HF1[36:32]; HFI1[4:0] = HF1[41:37];
  //   HFD2[31:0] = HF2[31:0]; HFR2[4:0] = HF2[36:32]; HFI2[4:0] = HF2[41:37]; HFD3[31:0] = HF3[31:0];
  //   HFR3[4:0] = HF3[36:32]; HFI3[4:0] = HF3[41:37]; HFD4[31:0] = HF4[31:0]; HFR4[4:0] = HF4[36:32];
  //   HFI4[4:0] = HF4[41:37]; HFD5[31:0] = HF5[31:0]; HFR5[4:0] = HF5[36:32]; HFI5[4:0] = HF5[41:37];
  //   HFD6[31:0] = HF6[31:0]; HFR6[4:0] = HF6[36:32]; HFI6[4:0] = HF6[41:37]; HFD7[31:0] = HF7[31:0];
  //   HFR7[4:0] = HF7[36:32]; HFI7[4:0] = HF7[41:37]; HFD8[31:0] = HF8[31:0]; HFR8[4:0] = HF8[36:32];
  //   HFI8[4:0] = HF8[41:37]; marker[4:0] = RBP; push_ex = ex_push; R_in[4:0] = R
endmodule
