// Digital circuit history4.dig as structural Verilog
module history4 (
  input  [4:0] R,
  input  [31:0] D,
  input  push,
  input  C,
  input  pop,
  input  [4:0] RBP,
  input  [4:0] inst,
  output [31:0] out1,
  output [31:0] out2,
  output [31:0] out3,
  output [31:0] out4,
  output [31:0] out5,
  output [31:0] out6,
  output [31:0] out7,
  output [31:0] out8,
  output [31:0] out9,
  output [31:0] out10,
  output [31:0] out11,
  output [31:0] out12,
  output [31:0] out13,
  output [31:0] out14,
  output [31:0] out15,
  output [31:0] out16,
  output [31:0] out17,
  output [31:0] out18,
  output [31:0] out19,
  output [31:0] out20,
  output [31:0] out21,
  output [31:0] out22,
  output [31:0] out23,
  output [31:0] out24,
  output [31:0] out25,
  output [31:0] out26,
  output [31:0] out27,
  output [31:0] out28,
  output [31:0] out29,
  output [31:0] out30,
  output [31:0] out31,
  output [31:0] out32,
  output halt,
  output [31:0] valid
);

  wire add_1_c_o, addr_0, HFH1, HFH2, HFH3, HFH4, HFV1, HFV2, HFV3, HFV4, not_2_out, or_1_out, W1, W2;
  wire [1:0] priorityencoder_1_num, priorityencoder_2_num, priorityencoder_3_num, priorityencoder_4_num,
       priorityencoder_5_num, priorityencoder_6_num, priorityencoder_7_num, priorityencoder_8_num,
       priorityencoder_9_num, priorityencoder_10_num, priorityencoder_11_num, priorityencoder_12_num,
       priorityencoder_13_num, priorityencoder_14_num, priorityencoder_15_num, priorityencoder_16_num,
       priorityencoder_17_num, priorityencoder_18_num, priorityencoder_19_num, priorityencoder_20_num,
       priorityencoder_21_num, priorityencoder_22_num, priorityencoder_23_num, priorityencoder_24_num,
       priorityencoder_25_num, priorityencoder_26_num, priorityencoder_27_num, priorityencoder_28_num,
       priorityencoder_29_num, priorityencoder_30_num, priorityencoder_31_num, priorityencoder_32_num,
       priorityencoder_33_num;
  wire [2:0] not_1_out;
  wire [3:0] add_2_s, addr_1234, bitextender_1_out, demultiplexer_2_out_0, demultiplexer_2_out_1,
       demultiplexer_2_out_2, demultiplexer_2_out_3, demultiplexer_2_out_4, demultiplexer_2_out_5,
       demultiplexer_2_out_6, demultiplexer_2_out_7, demultiplexer_2_out_8, demultiplexer_2_out_9,
       demultiplexer_2_out_10, demultiplexer_2_out_11, demultiplexer_2_out_12, demultiplexer_2_out_13,
       demultiplexer_2_out_14, demultiplexer_2_out_15, demultiplexer_2_out_16, demultiplexer_2_out_17,
       demultiplexer_2_out_18, demultiplexer_2_out_19, demultiplexer_2_out_20, demultiplexer_2_out_21,
       demultiplexer_2_out_22, demultiplexer_2_out_23, demultiplexer_2_out_24, demultiplexer_2_out_25,
       demultiplexer_2_out_26, demultiplexer_2_out_27, demultiplexer_2_out_28, demultiplexer_2_out_29,
       demultiplexer_2_out_30, demultiplexer_2_out_31, fill_4_1_out4, multiplexer_1_out, multiplexer_3_out,
       sub_1_s, sub_2_s, top, top_plus_1;
  wire [4:0] add_1_s, multiplexer_2_out;
  wire [41:0] HF1, HF2, HF3, HF4;

  Demultiplexer #(.Selector_Bits(5)) demultiplexer_1 (
    .sel(HF1[36:32]), .in(HFV1), .out_0(demultiplexer_2_out_0[3]), .out_1(demultiplexer_2_out_1[3]),
    .out_2(demultiplexer_2_out_2[3]), .out_3(demultiplexer_2_out_3[3]), .out_4(demultiplexer_2_out_4[3]),
    .out_5(demultiplexer_2_out_5[3]), .out_6(demultiplexer_2_out_6[3]), .out_7(demultiplexer_2_out_7[3]),
    .out_8(demultiplexer_2_out_8[3]), .out_9(demultiplexer_2_out_9[3]), .out_10(demultiplexer_2_out_10[3]),
    .out_11(demultiplexer_2_out_11[3]), .out_12(demultiplexer_2_out_12[3]),
    .out_13(demultiplexer_2_out_13[3]), .out_14(demultiplexer_2_out_14[3]),
    .out_15(demultiplexer_2_out_15[3]), .out_16(demultiplexer_2_out_16[3]),
    .out_17(demultiplexer_2_out_17[3]), .out_18(demultiplexer_2_out_18[3]),
    .out_19(demultiplexer_2_out_19[3]), .out_20(demultiplexer_2_out_20[3]),
    .out_21(demultiplexer_2_out_21[3]), .out_22(demultiplexer_2_out_22[3]),
    .out_23(demultiplexer_2_out_23[3]), .out_24(demultiplexer_2_out_24[3]),
    .out_25(demultiplexer_2_out_25[3]), .out_26(demultiplexer_2_out_26[3]),
    .out_27(demultiplexer_2_out_27[3]), .out_28(demultiplexer_2_out_28[3]),
    .out_29(demultiplexer_2_out_29[3]), .out_30(demultiplexer_2_out_30[3]), .out_31(demultiplexer_2_out_31[3]));
  PriorityEncoder #(.Selector_Bits(2)) priorityencoder_1 (
    .in0(HFH1), .in1(HFH2), .in2(HFH3), .in3(HFH4), .num(priorityencoder_1_num), .any(not_1_out[2]));
  Multiplexer #(.Bits(4)) multiplexer_1 (.sel(addr_0), .in_0(top_plus_1), .in_1(addr_1234), .out(multiplexer_1_out));
  assign not_1_out[1:0] = ~priorityencoder_1_num;  // Not not_1, 2 bits wide
  Multiplexer #(.Bits(5)) multiplexer_2 (
    .sel(pop), .in_0(5'b00001), .in_1({2'b11, not_1_out}), .out(multiplexer_2_out));
  Multiplexer #(.Bits(4)) multiplexer_3 (.sel(addr_0), .in_0(top), .in_1(top_plus_1), .out(multiplexer_3_out));
  Add #(.Bits(5)) add_1 (.a({addr_1234, addr_0}), .b(multiplexer_2_out), .c_i(pop), .s(add_1_s), .c_o(add_1_c_o));
  or or_1 (or_1_out, push, pop);
  Demultiplexer #(.Selector_Bits(5)) demultiplexer_2 (
    .sel(HF2[36:32]), .in(HFV2), .out_0(demultiplexer_2_out_0[2]), .out_1(demultiplexer_2_out_1[2]),
    .out_2(demultiplexer_2_out_2[2]), .out_3(demultiplexer_2_out_3[2]), .out_4(demultiplexer_2_out_4[2]),
    .out_5(demultiplexer_2_out_5[2]), .out_6(demultiplexer_2_out_6[2]), .out_7(demultiplexer_2_out_7[2]),
    .out_8(demultiplexer_2_out_8[2]), .out_9(demultiplexer_2_out_9[2]), .out_10(demultiplexer_2_out_10[2]),
    .out_11(demultiplexer_2_out_11[2]), .out_12(demultiplexer_2_out_12[2]),
    .out_13(demultiplexer_2_out_13[2]), .out_14(demultiplexer_2_out_14[2]),
    .out_15(demultiplexer_2_out_15[2]), .out_16(demultiplexer_2_out_16[2]),
    .out_17(demultiplexer_2_out_17[2]), .out_18(demultiplexer_2_out_18[2]),
    .out_19(demultiplexer_2_out_19[2]), .out_20(demultiplexer_2_out_20[2]),
    .out_21(demultiplexer_2_out_21[2]), .out_22(demultiplexer_2_out_22[2]),
    .out_23(demultiplexer_2_out_23[2]), .out_24(demultiplexer_2_out_24[2]),
    .out_25(demultiplexer_2_out_25[2]), .out_26(demultiplexer_2_out_26[2]),
    .out_27(demultiplexer_2_out_27[2]), .out_28(demultiplexer_2_out_28[2]),
    .out_29(demultiplexer_2_out_29[2]), .out_30(demultiplexer_2_out_30[2]), .out_31(demultiplexer_2_out_31[2]));
  RegisterFile #(.AddrBits(4), .Bits(42)) u_HF1 (
    .Din({inst, R, D}), .we(W1), .Rw(multiplexer_3_out), .C(C), .Ra(multiplexer_3_out),
    .Rb(multiplexer_1_out), .Da(HF1), .Db(HF3));
  RegisterFile #(.AddrBits(4), .Bits(42)) u_HF2 (
    .Din({inst, R, D}), .we(W2), .Rw(top), .C(C), .Ra(top), .Rb(top_plus_1), .Da(HF2), .Db(HF4));
  Register #(.Bits(5)) register_1 (.D(add_1_s), .C(C), .en(or_1_out), .Q({addr_1234, addr_0}));
  fill_4 fill_4_1 (
    .on(1'b0), .in1(HFH4), .in2(HFH3), .in3(HFH2), .in4(HFH1), .out1(fill_4_1_out4[0]),
    .out2(fill_4_1_out4[1]), .out3(fill_4_1_out4[2]), .out4(fill_4_1_out4[3]), .v(halt));
  Demultiplexer #(.Selector_Bits(5)) demultiplexer_3 (
    .sel(HF3[36:32]), .in(HFV3), .out_0(demultiplexer_2_out_0[1]), .out_1(demultiplexer_2_out_1[1]),
    .out_2(demultiplexer_2_out_2[1]), .out_3(demultiplexer_2_out_3[1]), .out_4(demultiplexer_2_out_4[1]),
    .out_5(demultiplexer_2_out_5[1]), .out_6(demultiplexer_2_out_6[1]), .out_7(demultiplexer_2_out_7[1]),
    .out_8(demultiplexer_2_out_8[1]), .out_9(demultiplexer_2_out_9[1]), .out_10(demultiplexer_2_out_10[1]),
    .out_11(demultiplexer_2_out_11[1]), .out_12(demultiplexer_2_out_12[1]),
    .out_13(demultiplexer_2_out_13[1]), .out_14(demultiplexer_2_out_14[1]),
    .out_15(demultiplexer_2_out_15[1]), .out_16(demultiplexer_2_out_16[1]),
    .out_17(demultiplexer_2_out_17[1]), .out_18(demultiplexer_2_out_18[1]),
    .out_19(demultiplexer_2_out_19[1]), .out_20(demultiplexer_2_out_20[1]),
    .out_21(demultiplexer_2_out_21[1]), .out_22(demultiplexer_2_out_22[1]),
    .out_23(demultiplexer_2_out_23[1]), .out_24(demultiplexer_2_out_24[1]),
    .out_25(demultiplexer_2_out_25[1]), .out_26(demultiplexer_2_out_26[1]),
    .out_27(demultiplexer_2_out_27[1]), .out_28(demultiplexer_2_out_28[1]),
    .out_29(demultiplexer_2_out_29[1]), .out_30(demultiplexer_2_out_30[1]), .out_31(demultiplexer_2_out_31[1]));
  not not_2 (not_2_out, halt);
  assign {HFV1, HFV2, HFV3, HFV4} = fill_4_1_out4 | bitextender_1_out;  // Or or_2, 4 bits wide
  BitExtender #(.inputBits(1), .outputBits(4)) bitextender_1 (.in(not_2_out), .out(bitextender_1_out));
  Add #(.Bits(4)) add_2 (.a(addr_1234), .b(4'b0001), .c_i(1'b0), .s(add_2_s));  // open: c_o
  Sub #(.Bits(4)) sub_1 (.a(addr_1234), .b(4'b0001), .c_i(1'b0), .s(sub_1_s));  // open: c_o
  Sub #(.Bits(4)) sub_2 (.a(addr_1234), .b(4'b0010), .c_i(1'b0), .s(sub_2_s));  // open: c_o
  Demultiplexer demultiplexer_4 (.sel(addr_0), .in(push), .out_0(W1), .out_1(W2));
  Comparator #(.Bits(5)) comparator_1 (.a(HF1[41:37]), .b(RBP), .eq(HFH1));  // open: gt, lt
  Comparator #(.Bits(5)) comparator_2 (.a(HF2[41:37]), .b(RBP), .eq(HFH2));  // open: gt, lt
  Comparator #(.Bits(5)) comparator_3 (.a(HF3[41:37]), .b(RBP), .eq(HFH3));  // open: gt, lt
  Comparator #(.Bits(5)) comparator_4 (.a(HF4[41:37]), .b(RBP), .eq(HFH4));  // open: gt, lt
  Multiplexer #(.Bits(4)) multiplexer_4 (.sel(pop), .in_0(add_2_s), .in_1(sub_1_s), .out(top_plus_1));
  Multiplexer #(.Bits(4)) multiplexer_5 (.sel(pop), .in_0(addr_1234), .in_1(sub_2_s), .out(top));
  Demultiplexer #(.Selector_Bits(5)) demultiplexer_5 (
    .sel(HF4[36:32]), .in(HFV4), .out_0(demultiplexer_2_out_0[0]), .out_1(demultiplexer_2_out_1[0]),
    .out_2(demultiplexer_2_out_2[0]), .out_3(demultiplexer_2_out_3[0]), .out_4(demultiplexer_2_out_4[0]),
    .out_5(demultiplexer_2_out_5[0]), .out_6(demultiplexer_2_out_6[0]), .out_7(demultiplexer_2_out_7[0]),
    .out_8(demultiplexer_2_out_8[0]), .out_9(demultiplexer_2_out_9[0]), .out_10(demultiplexer_2_out_10[0]),
    .out_11(demultiplexer_2_out_11[0]), .out_12(demultiplexer_2_out_12[0]),
    .out_13(demultiplexer_2_out_13[0]), .out_14(demultiplexer_2_out_14[0]),
    .out_15(demultiplexer_2_out_15[0]), .out_16(demultiplexer_2_out_16[0]),
    .out_17(demultiplexer_2_out_17[0]), .out_18(demultiplexer_2_out_18[0]),
    .out_19(demultiplexer_2_out_19[0]), .out_20(demultiplexer_2_out_20[0]),
    .out_21(demultiplexer_2_out_21[0]), .out_22(demultiplexer_2_out_22[0]),
    .out_23(demultiplexer_2_out_23[0]), .out_24(demultiplexer_2_out_24[0]),
    .out_25(demultiplexer_2_out_25[0]), .out_26(demultiplexer_2_out_26[0]),
    .out_27(demultiplexer_2_out_27[0]), .out_28(demultiplexer_2_out_28[0]),
    .out_29(demultiplexer_2_out_29[0]), .out_30(demultiplexer_2_out_30[0]), .out_31(demultiplexer_2_out_31[0]));
  PriorityEncoder #(.Selector_Bits(2)) priorityencoder_2 (
    .in0(demultiplexer_2_out_0[3]), .in1(demultiplexer_2_out_0[2]), .in2(demultiplexer_2_out_0[1]),
    .in3(demultiplexer_2_out_0[0]), .num(priorityencoder_2_num), .any(valid[0]));
  PriorityEncoder #(.Selector_Bits(2)) priorityencoder_3 (
    .in0(demultiplexer_2_out_1[3]), .in1(demultiplexer_2_out_1[2]), .in2(demultiplexer_2_out_1[1]),
    .in3(demultiplexer_2_out_1[0]), .num(priorityencoder_3_num), .any(valid[1]));
  PriorityEncoder #(.Selector_Bits(2)) priorityencoder_4 (
    .in0(demultiplexer_2_out_2[3]), .in1(demultiplexer_2_out_2[2]), .in2(demultiplexer_2_out_2[1]),
    .in3(demultiplexer_2_out_2[0]), .num(priorityencoder_4_num), .any(valid[2]));
  PriorityEncoder #(.Selector_Bits(2)) priorityencoder_5 (
    .in0(demultiplexer_2_out_3[3]), .in1(demultiplexer_2_out_3[2]), .in2(demultiplexer_2_out_3[1]),
    .in3(demultiplexer_2_out_3[0]), .num(priorityencoder_5_num), .any(valid[3]));
  PriorityEncoder #(.Selector_Bits(2)) priorityencoder_6 (
    .in0(demultiplexer_2_out_4[3]), .in1(demultiplexer_2_out_4[2]), .in2(demultiplexer_2_out_4[1]),
    .in3(demultiplexer_2_out_4[0]), .num(priorityencoder_6_num), .any(valid[4]));
  PriorityEncoder #(.Selector_Bits(2)) priorityencoder_7 (
    .in0(demultiplexer_2_out_5[3]), .in1(demultiplexer_2_out_5[2]), .in2(demultiplexer_2_out_5[1]),
    .in3(demultiplexer_2_out_5[0]), .num(priorityencoder_7_num), .any(valid[5]));
  PriorityEncoder #(.Selector_Bits(2)) priorityencoder_8 (
    .in0(demultiplexer_2_out_6[3]), .in1(demultiplexer_2_out_6[2]), .in2(demultiplexer_2_out_6[1]),
    .in3(demultiplexer_2_out_6[0]), .num(priorityencoder_8_num), .any(valid[6]));
  PriorityEncoder #(.Selector_Bits(2)) priorityencoder_9 (
    .in0(demultiplexer_2_out_7[3]), .in1(demultiplexer_2_out_7[2]), .in2(demultiplexer_2_out_7[1]),
    .in3(demultiplexer_2_out_7[0]), .num(priorityencoder_9_num), .any(valid[7]));
  PriorityEncoder #(.Selector_Bits(2)) priorityencoder_10 (
    .in0(demultiplexer_2_out_8[3]), .in1(demultiplexer_2_out_8[2]), .in2(demultiplexer_2_out_8[1]),
    .in3(demultiplexer_2_out_8[0]), .num(priorityencoder_10_num), .any(valid[8]));
  PriorityEncoder #(.Selector_Bits(2)) priorityencoder_11 (
    .in0(demultiplexer_2_out_9[3]), .in1(demultiplexer_2_out_9[2]), .in2(demultiplexer_2_out_9[1]),
    .in3(demultiplexer_2_out_9[0]), .num(priorityencoder_11_num), .any(valid[9]));
  PriorityEncoder #(.Selector_Bits(2)) priorityencoder_12 (
    .in0(demultiplexer_2_out_10[3]), .in1(demultiplexer_2_out_10[2]), .in2(demultiplexer_2_out_10[1]),
    .in3(demultiplexer_2_out_10[0]), .num(priorityencoder_12_num), .any(valid[10]));
  PriorityEncoder #(.Selector_Bits(2)) priorityencoder_13 (
    .in0(demultiplexer_2_out_11[3]), .in1(demultiplexer_2_out_11[2]), .in2(demultiplexer_2_out_11[1]),
    .in3(demultiplexer_2_out_11[0]), .num(priorityencoder_13_num), .any(valid[11]));
  PriorityEncoder #(.Selector_Bits(2)) priorityencoder_14 (
    .in0(demultiplexer_2_out_12[3]), .in1(demultiplexer_2_out_12[2]), .in2(demultiplexer_2_out_12[1]),
    .in3(demultiplexer_2_out_12[0]), .num(priorityencoder_14_num), .any(valid[12]));
  PriorityEncoder #(.Selector_Bits(2)) priorityencoder_15 (
    .in0(demultiplexer_2_out_13[3]), .in1(demultiplexer_2_out_13[2]), .in2(demultiplexer_2_out_13[1]),
    .in3(demultiplexer_2_out_13[0]), .num(priorityencoder_15_num), .any(valid[13]));
  PriorityEncoder #(.Selector_Bits(2)) priorityencoder_16 (
    .in0(demultiplexer_2_out_14[3]), .in1(demultiplexer_2_out_14[2]), .in2(demultiplexer_2_out_14[1]),
    .in3(demultiplexer_2_out_14[0]), .num(priorityencoder_16_num), .any(valid[14]));
  PriorityEncoder #(.Selector_Bits(2)) priorityencoder_17 (
    .in0(demultiplexer_2_out_15[3]), .in1(demultiplexer_2_out_15[2]), .in2(demultiplexer_2_out_15[1]),
    .in3(demultiplexer_2_out_15[0]), .num(priorityencoder_17_num), .any(valid[15]));
  PriorityEncoder #(.Selector_Bits(2)) priorityencoder_18 (
    .in0(demultiplexer_2_out_16[3]), .in1(demultiplexer_2_out_16[2]), .in2(demultiplexer_2_out_16[1]),
    .in3(demultiplexer_2_out_16[0]), .num(priorityencoder_18_num), .any(valid[16]));
  PriorityEncoder #(.Selector_Bits(2)) priorityencoder_19 (
    .in0(demultiplexer_2_out_17[3]), .in1(demultiplexer_2_out_17[2]), .in2(demultiplexer_2_out_17[1]),
    .in3(demultiplexer_2_out_17[0]), .num(priorityencoder_19_num), .any(valid[17]));
  PriorityEncoder #(.Selector_Bits(2)) priorityencoder_20 (
    .in0(demultiplexer_2_out_18[3]), .in1(demultiplexer_2_out_18[2]), .in2(demultiplexer_2_out_18[1]),
    .in3(demultiplexer_2_out_18[0]), .num(priorityencoder_20_num), .any(valid[18]));
  PriorityEncoder #(.Selector_Bits(2)) priorityencoder_21 (
    .in0(demultiplexer_2_out_19[3]), .in1(demultiplexer_2_out_19[2]), .in2(demultiplexer_2_out_19[1]),
    .in3(demultiplexer_2_out_19[0]), .num(priorityencoder_21_num), .any(valid[19]));
  PriorityEncoder #(.Selector_Bits(2)) priorityencoder_22 (
    .in0(demultiplexer_2_out_20[3]), .in1(demultiplexer_2_out_20[2]), .in2(demultiplexer_2_out_20[1]),
    .in3(demultiplexer_2_out_20[0]), .num(priorityencoder_22_num), .any(valid[20]));
  PriorityEncoder #(.Selector_Bits(2)) priorityencoder_23 (
    .in0(demultiplexer_2_out_21[3]), .in1(demultiplexer_2_out_21[2]), .in2(demultiplexer_2_out_21[1]),
    .in3(demultiplexer_2_out_21[0]), .num(priorityencoder_23_num), .any(valid[21]));
  PriorityEncoder #(.Selector_Bits(2)) priorityencoder_24 (
    .in0(demultiplexer_2_out_22[3]), .in1(demultiplexer_2_out_22[2]), .in2(demultiplexer_2_out_22[1]),
    .in3(demultiplexer_2_out_22[0]), .num(priorityencoder_24_num), .any(valid[22]));
  PriorityEncoder #(.Selector_Bits(2)) priorityencoder_25 (
    .in0(demultiplexer_2_out_23[3]), .in1(demultiplexer_2_out_23[2]), .in2(demultiplexer_2_out_23[1]),
    .in3(demultiplexer_2_out_23[0]), .num(priorityencoder_25_num), .any(valid[23]));
  PriorityEncoder #(.Selector_Bits(2)) priorityencoder_26 (
    .in0(demultiplexer_2_out_24[3]), .in1(demultiplexer_2_out_24[2]), .in2(demultiplexer_2_out_24[1]),
    .in3(demultiplexer_2_out_24[0]), .num(priorityencoder_26_num), .any(valid[24]));
  PriorityEncoder #(.Selector_Bits(2)) priorityencoder_27 (
    .in0(demultiplexer_2_out_25[3]), .in1(demultiplexer_2_out_25[2]), .in2(demultiplexer_2_out_25[1]),
    .in3(demultiplexer_2_out_25[0]), .num(priorityencoder_27_num), .any(valid[25]));
  PriorityEncoder #(.Selector_Bits(2)) priorityencoder_28 (
    .in0(demultiplexer_2_out_26[3]), .in1(demultiplexer_2_out_26[2]), .in2(demultiplexer_2_out_26[1]),
    .in3(demultiplexer_2_out_26[0]), .num(priorityencoder_28_num), .any(valid[26]));
  PriorityEncoder #(.Selector_Bits(2)) priorityencoder_29 (
    .in0(demultiplexer_2_out_27[3]), .in1(demultiplexer_2_out_27[2]), .in2(demultiplexer_2_out_27[1]),
    .in3(demultiplexer_2_out_27[0]), .num(priorityencoder_29_num), .any(valid[27]));
  PriorityEncoder #(.Selector_Bits(2)) priorityencoder_30 (
    .in0(demultiplexer_2_out_28[3]), .in1(demultiplexer_2_out_28[2]), .in2(demultiplexer_2_out_28[1]),
    .in3(demultiplexer_2_out_28[0]), .num(priorityencoder_30_num), .any(valid[28]));
  PriorityEncoder #(.Selector_Bits(2)) priorityencoder_31 (
    .in0(demultiplexer_2_out_29[3]), .in1(demultiplexer_2_out_29[2]), .in2(demultiplexer_2_out_29[1]),
    .in3(demultiplexer_2_out_29[0]), .num(priorityencoder_31_num), .any(valid[29]));
  PriorityEncoder #(.Selector_Bits(2)) priorityencoder_32 (
    .in0(demultiplexer_2_out_30[3]), .in1(demultiplexer_2_out_30[2]), .in2(demultiplexer_2_out_30[1]),
    .in3(demultiplexer_2_out_30[0]), .num(priorityencoder_32_num), .any(valid[30]));
  PriorityEncoder #(.Selector_Bits(2)) priorityencoder_33 (
    .in0(demultiplexer_2_out_31[3]), .in1(demultiplexer_2_out_31[2]), .in2(demultiplexer_2_out_31[1]),
    .in3(demultiplexer_2_out_31[0]), .num(priorityencoder_33_num), .any(valid[31]));
  Multiplexer #(.Selector_Bits(2), .Bits(32)) multiplexer_6 (
    .sel(priorityencoder_2_num), .in_0(HF1[31:0]), .in_1(HF2[31:0]), .in_2(HF3[31:0]), .in_3(HF4[31:0]),
    .out(out1));
  Multiplexer #(.Selector_Bits(2), .Bits(32)) multiplexer_7 (
    .sel(priorityencoder_3_num), .in_0(HF1[31:0]), .in_1(HF2[31:0]), .in_2(HF3[31:0]), .in_3(HF4[31:0]),
    .out(out2));
  Multiplexer #(.Selector_Bits(2), .Bits(32)) multiplexer_8 (
    .sel(priorityencoder_4_num), .in_0(HF1[31:0]), .in_1(HF2[31:0]), .in_2(HF3[31:0]), .in_3(HF4[31:0]),
    .out(out3));
  Multiplexer #(.Selector_Bits(2), .Bits(32)) multiplexer_9 (
    .sel(priorityencoder_5_num), .in_0(HF1[31:0]), .in_1(HF2[31:0]), .in_2(HF3[31:0]), .in_3(HF4[31:0]),
    .out(out4));
  Multiplexer #(.Selector_Bits(2), .Bits(32)) multiplexer_10 (
    .sel(priorityencoder_6_num), .in_0(HF1[31:0]), .in_1(HF2[31:0]), .in_2(HF3[31:0]), .in_3(HF4[31:0]),
    .out(out5));
  Multiplexer #(.Selector_Bits(2), .Bits(32)) multiplexer_11 (
    .sel(priorityencoder_7_num), .in_0(HF1[31:0]), .in_1(HF2[31:0]), .in_2(HF3[31:0]), .in_3(HF4[31:0]),
    .out(out6));
  Multiplexer #(.Selector_Bits(2), .Bits(32)) multiplexer_12 (
    .sel(priorityencoder_8_num), .in_0(HF1[31:0]), .in_1(HF2[31:0]), .in_2(HF3[31:0]), .in_3(HF4[31:0]),
    .out(out7));
  Multiplexer #(.Selector_Bits(2), .Bits(32)) multiplexer_13 (
    .sel(priorityencoder_9_num), .in_0(HF1[31:0]), .in_1(HF2[31:0]), .in_2(HF3[31:0]), .in_3(HF4[31:0]),
    .out(out8));
  Multiplexer #(.Selector_Bits(2), .Bits(32)) multiplexer_14 (
    .sel(priorityencoder_10_num), .in_0(HF1[31:0]), .in_1(HF2[31:0]), .in_2(HF3[31:0]), .in_3(HF4[31:0]),
    .out(out9));
  Multiplexer #(.Selector_Bits(2), .Bits(32)) multiplexer_15 (
    .sel(priorityencoder_11_num), .in_0(HF1[31:0]), .in_1(HF2[31:0]), .in_2(HF3[31:0]), .in_3(HF4[31:0]),
    .out(out10));
  Multiplexer #(.Selector_Bits(2), .Bits(32)) multiplexer_16 (
    .sel(priorityencoder_12_num), .in_0(HF1[31:0]), .in_1(HF2[31:0]), .in_2(HF3[31:0]), .in_3(HF4[31:0]),
    .out(out11));
  Multiplexer #(.Selector_Bits(2), .Bits(32)) multiplexer_17 (
    .sel(priorityencoder_13_num), .in_0(HF1[31:0]), .in_1(HF2[31:0]), .in_2(HF3[31:0]), .in_3(HF4[31:0]),
    .out(out12));
  Multiplexer #(.Selector_Bits(2), .Bits(32)) multiplexer_18 (
    .sel(priorityencoder_14_num), .in_0(HF1[31:0]), .in_1(HF2[31:0]), .in_2(HF3[31:0]), .in_3(HF4[31:0]),
    .out(out13));
  Multiplexer #(.Selector_Bits(2), .Bits(32)) multiplexer_19 (
    .sel(priorityencoder_15_num), .in_0(HF1[31:0]), .in_1(HF2[31:0]), .in_2(HF3[31:0]), .in_3(HF4[31:0]),
    .out(out14));
  Multiplexer #(.Selector_Bits(2), .Bits(32)) multiplexer_20 (
    .sel(priorityencoder_16_num), .in_0(HF1[31:0]), .in_1(HF2[31:0]), .in_2(HF3[31:0]), .in_3(HF4[31:0]),
    .out(out15));
  Multiplexer #(.Selector_Bits(2), .Bits(32)) multiplexer_21 (
    .sel(priorityencoder_17_num), .in_0(HF1[31:0]), .in_1(HF2[31:0]), .in_2(HF3[31:0]), .in_3(HF4[31:0]),
    .out(out16));
  Multiplexer #(.Selector_Bits(2), .Bits(32)) multiplexer_22 (
    .sel(priorityencoder_18_num), .in_0(HF1[31:0]), .in_1(HF2[31:0]), .in_2(HF3[31:0]), .in_3(HF4[31:0]),
    .out(out17));
  Multiplexer #(.Selector_Bits(2), .Bits(32)) multiplexer_23 (
    .sel(priorityencoder_19_num), .in_0(HF1[31:0]), .in_1(HF2[31:0]), .in_2(HF3[31:0]), .in_3(HF4[31:0]),
    .out(out18));
  Multiplexer #(.Selector_Bits(2), .Bits(32)) multiplexer_24 (
    .sel(priorityencoder_20_num), .in_0(HF1[31:0]), .in_1(HF2[31:0]), .in_2(HF3[31:0]), .in_3(HF4[31:0]),
    .out(out19));
  Multiplexer #(.Selector_Bits(2), .Bits(32)) multiplexer_25 (
    .sel(priorityencoder_21_num), .in_0(HF1[31:0]), .in_1(HF2[31:0]), .in_2(HF3[31:0]), .in_3(HF4[31:0]),
    .out(out20));
  Multiplexer #(.Selector_Bits(2), .Bits(32)) multiplexer_26 (
    .sel(priorityencoder_22_num), .in_0(HF1[31:0]), .in_1(HF2[31:0]), .in_2(HF3[31:0]), .in_3(HF4[31:0]),
    .out(out21));
  Multiplexer #(.Selector_Bits(2), .Bits(32)) multiplexer_27 (
    .sel(priorityencoder_23_num), .in_0(HF1[31:0]), .in_1(HF2[31:0]), .in_2(HF3[31:0]), .in_3(HF4[31:0]),
    .out(out22));
  Multiplexer #(.Selector_Bits(2), .Bits(32)) multiplexer_28 (
    .sel(priorityencoder_24_num), .in_0(HF1[31:0]), .in_1(HF2[31:0]), .in_2(HF3[31:0]), .in_3(HF4[31:0]),
    .out(out23));
  Multiplexer #(.Selector_Bits(2), .Bits(32)) multiplexer_29 (
    .sel(priorityencoder_25_num), .in_0(HF1[31:0]), .in_1(HF2[31:0]), .in_2(HF3[31:0]), .in_3(HF4[31:0]),
    .out(out24));
  Multiplexer #(.Selector_Bits(2), .Bits(32)) multiplexer_30 (
    .sel(priorityencoder_26_num), .in_0(HF1[31:0]), .in_1(HF2[31:0]), .in_2(HF3[31:0]), .in_3(HF4[31:0]),
    .out(out25));
  Multiplexer #(.Selector_Bits(2), .Bits(32)) multiplexer_31 (
    .sel(priorityencoder_27_num), .in_0(HF1[31:0]), .in_1(HF2[31:0]), .in_2(HF3[31:0]), .in_3(HF4[31:0]),
    .out(out26));
  Multiplexer #(.Selector_Bits(2), .Bits(32)) multiplexer_32 (
    .sel(priorityencoder_28_num), .in_0(HF1[31:0]), .in_1(HF2[31:0]), .in_2(HF3[31:0]), .in_3(HF4[31:0]),
    .out(out27));
  Multiplexer #(.Selector_Bits(2), .Bits(32)) multiplexer_33 (
    .sel(priorityencoder_29_num), .in_0(HF1[31:0]), .in_1(HF2[31:0]), .in_2(HF3[31:0]), .in_3(HF4[31:0]),
    .out(out28));
  Multiplexer #(.Selector_Bits(2), .Bits(32)) multiplexer_34 (
    .sel(priorityencoder_30_num), .in_0(HF1[31:0]), .in_1(HF2[31:0]), .in_2(HF3[31:0]), .in_3(HF4[31:0]),
    .out(out29));
  Multiplexer #(.Selector_Bits(2), .Bits(32)) multiplexer_35 (
    .sel(priorityencoder_31_num), .in_0(HF1[31:0]), .in_1(HF2[31:0]), .in_2(HF3[31:0]), .in_3(HF4[31:0]),
    .out(out30));
  Multiplexer #(.Selector_Bits(2), .Bits(32)) multiplexer_36 (
    .sel(priorityencoder_32_num), .in_0(HF1[31:0]), .in_1(HF2[31:0]), .in_2(HF3[31:0]), .in_3(HF4[31:0]),
    .out(out31));
  Multiplexer #(.Selector_Bits(2), .Bits(32)) multiplexer_37 (
    .sel(priorityencoder_33_num), .in_0(HF1[31:0]), .in_1(HF2[31:0]), .in_2(HF3[31:0]), .in_3(HF4[31:0]),
    .out(out32));

  // Other names for the same wires on the sheet: valid_32[31:0] = valid; PM = addr_0; top_plus_2[3:0] = addr_1234;
  //   D_in[31:0] = D; log[41:0] = {inst, R, D}; HFD1[31:0] = HF1[31:0]; HFR1[4:0] = HF1[36:32];
  //   HFI1[4:0] = HF1[41:37]; HFD2[31:0] = HF2[31:0]; HFR2[4:0] = HF2[36:32]; HFI2[4:0] = HF2[41:37];
  //   HFD3[31:0] = HF3[31:0]; HFR3[4:0] = HF3[36:32]; HFI3[4:0] = HF3[41:37]; HFD4[31:0] = HF4[31:0];
  //   HFR4[4:0] = HF4[36:32]; HFI4[4:0] = HF4[41:37]; inst_in[4:0] = inst; marker[4:0] = RBP; R_in[4:0] = R
endmodule
