// Digital circuit id-gen.dig as structural Verilog
module id_gen (
  input  \use ,
  input  com1,
  input  C,
  input  com2,
  input  [4:0] com1_id,
  input  [4:0] com2_id,
  output [4:0] id,
  output V
);

  wire [31:0] and_1_out, demultiplexer_1_out_0, demultiplexer_2_out_0, demultiplexer_3_out_0, nor_1_out,
       not_1_out, or_1_out, register_1_q;

  Demultiplexer #(.Selector_Bits(5)) demultiplexer_1 (
    .sel(com2_id), .in(com2), .out_0(demultiplexer_1_out_0[0]), .out_1(demultiplexer_1_out_0[1]),
    .out_2(demultiplexer_1_out_0[2]), .out_3(demultiplexer_1_out_0[3]), .out_4(demultiplexer_1_out_0[4]),
    .out_5(demultiplexer_1_out_0[5]), .out_6(demultiplexer_1_out_0[6]), .out_7(demultiplexer_1_out_0[7]),
    .out_8(demultiplexer_1_out_0[8]), .out_9(demultiplexer_1_out_0[9]), .out_10(demultiplexer_1_out_0[10]),
    .out_11(demultiplexer_1_out_0[11]), .out_12(demultiplexer_1_out_0[12]),
    .out_13(demultiplexer_1_out_0[13]), .out_14(demultiplexer_1_out_0[14]),
    .out_15(demultiplexer_1_out_0[15]), .out_16(demultiplexer_1_out_0[16]),
    .out_17(demultiplexer_1_out_0[17]), .out_18(demultiplexer_1_out_0[18]),
    .out_19(demultiplexer_1_out_0[19]), .out_20(demultiplexer_1_out_0[20]),
    .out_21(demultiplexer_1_out_0[21]), .out_22(demultiplexer_1_out_0[22]),
    .out_23(demultiplexer_1_out_0[23]), .out_24(demultiplexer_1_out_0[24]),
    .out_25(demultiplexer_1_out_0[25]), .out_26(demultiplexer_1_out_0[26]),
    .out_27(demultiplexer_1_out_0[27]), .out_28(demultiplexer_1_out_0[28]),
    .out_29(demultiplexer_1_out_0[29]), .out_30(demultiplexer_1_out_0[30]), .out_31(demultiplexer_1_out_0[31]));
  Demultiplexer #(.Selector_Bits(5)) demultiplexer_2 (
    .sel(com1_id), .in(com1), .out_0(demultiplexer_2_out_0[0]), .out_1(demultiplexer_2_out_0[1]),
    .out_2(demultiplexer_2_out_0[2]), .out_3(demultiplexer_2_out_0[3]), .out_4(demultiplexer_2_out_0[4]),
    .out_5(demultiplexer_2_out_0[5]), .out_6(demultiplexer_2_out_0[6]), .out_7(demultiplexer_2_out_0[7]),
    .out_8(demultiplexer_2_out_0[8]), .out_9(demultiplexer_2_out_0[9]), .out_10(demultiplexer_2_out_0[10]),
    .out_11(demultiplexer_2_out_0[11]), .out_12(demultiplexer_2_out_0[12]),
    .out_13(demultiplexer_2_out_0[13]), .out_14(demultiplexer_2_out_0[14]),
    .out_15(demultiplexer_2_out_0[15]), .out_16(demultiplexer_2_out_0[16]),
    .out_17(demultiplexer_2_out_0[17]), .out_18(demultiplexer_2_out_0[18]),
    .out_19(demultiplexer_2_out_0[19]), .out_20(demultiplexer_2_out_0[20]),
    .out_21(demultiplexer_2_out_0[21]), .out_22(demultiplexer_2_out_0[22]),
    .out_23(demultiplexer_2_out_0[23]), .out_24(demultiplexer_2_out_0[24]),
    .out_25(demultiplexer_2_out_0[25]), .out_26(demultiplexer_2_out_0[26]),
    .out_27(demultiplexer_2_out_0[27]), .out_28(demultiplexer_2_out_0[28]),
    .out_29(demultiplexer_2_out_0[29]), .out_30(demultiplexer_2_out_0[30]), .out_31(demultiplexer_2_out_0[31]));
  assign nor_1_out = ~(demultiplexer_1_out_0 | demultiplexer_2_out_0);  // NOr nor_1, 32 bits wide
  assign and_1_out = register_1_q & nor_1_out;  // And and_1, 32 bits wide
  Demultiplexer #(.Selector_Bits(5)) demultiplexer_3 (
    .sel(id), .in(\use ), .out_0(demultiplexer_3_out_0[0]), .out_1(demultiplexer_3_out_0[1]),
    .out_2(demultiplexer_3_out_0[2]), .out_3(demultiplexer_3_out_0[3]), .out_4(demultiplexer_3_out_0[4]),
    .out_5(demultiplexer_3_out_0[5]), .out_6(demultiplexer_3_out_0[6]), .out_7(demultiplexer_3_out_0[7]),
    .out_8(demultiplexer_3_out_0[8]), .out_9(demultiplexer_3_out_0[9]), .out_10(demultiplexer_3_out_0[10]),
    .out_11(demultiplexer_3_out_0[11]), .out_12(demultiplexer_3_out_0[12]),
    .out_13(demultiplexer_3_out_0[13]), .out_14(demultiplexer_3_out_0[14]),
    .out_15(demultiplexer_3_out_0[15]), .out_16(demultiplexer_3_out_0[16]),
    .out_17(demultiplexer_3_out_0[17]), .out_18(demultiplexer_3_out_0[18]),
    .out_19(demultiplexer_3_out_0[19]), .out_20(demultiplexer_3_out_0[20]),
    .out_21(demultiplexer_3_out_0[21]), .out_22(demultiplexer_3_out_0[22]),
    .out_23(demultiplexer_3_out_0[23]), .out_24(demultiplexer_3_out_0[24]),
    .out_25(demultiplexer_3_out_0[25]), .out_26(demultiplexer_3_out_0[26]),
    .out_27(demultiplexer_3_out_0[27]), .out_28(demultiplexer_3_out_0[28]),
    .out_29(demultiplexer_3_out_0[29]), .out_30(demultiplexer_3_out_0[30]), .out_31(demultiplexer_3_out_0[31]));
  assign or_1_out = and_1_out | demultiplexer_3_out_0;  // Or or_1, 32 bits wide
  Register #(.Bits(32)) register_1 (.D(or_1_out), .C(C), .en(1'b1), .Q(register_1_q));
  assign not_1_out = ~register_1_q;  // Not not_1, 32 bits wide
  PriorityEncoder #(.Selector_Bits(5)) priorityencoder_1 (
    .in0(not_1_out[0]), .in1(not_1_out[1]), .in2(not_1_out[2]), .in3(not_1_out[3]), .in4(not_1_out[4]),
    .in5(not_1_out[5]), .in6(not_1_out[6]), .in7(not_1_out[7]), .in8(not_1_out[8]), .in9(not_1_out[9]),
    .in10(not_1_out[10]), .in11(not_1_out[11]), .in12(not_1_out[12]), .in13(not_1_out[13]),
    .in14(not_1_out[14]), .in15(not_1_out[15]), .in16(not_1_out[16]), .in17(not_1_out[17]),
    .in18(not_1_out[18]), .in19(not_1_out[19]), .in20(not_1_out[20]), .in21(not_1_out[21]),
    .in22(not_1_out[22]), .in23(not_1_out[23]), .in24(not_1_out[24]), .in25(not_1_out[25]),
    .in26(not_1_out[26]), .in27(not_1_out[27]), .in28(not_1_out[28]), .in29(not_1_out[29]),
    .in30(not_1_out[30]), .in31(not_1_out[31]), .num(id), .any(V));
endmodule
