// Digital circuit BTB-buff.dig as structural Verilog
module BTB_buff (
  input  C,
  input  [1:0] rd_id,
  input  [35:0] BTB_I,
  input  E,
  input  [3:0] clr,
  output [35:0] BTB_O,
  output full,
  output [1:0] BTB_ISS,
  output [3:0] V
);

  wire and_1_out, and_2_out, and_3_out, and_4_out, and_5_out, E_M1, E_M2, E_M3, E_M4, priorityencoder_1_any;
  wire [3:0] not_1_out;
  wire [35:0] D_M1, D_M2, D_M3, D_M4;

  and and_1 (and_1_out, ~E_M1, E_M2);  // And
  RS_FF rs_ff_1 (.S(E_M1), .C(C), .R(and_1_out), .Q(V[0]));  // open: nQ
  Register #(.Bits(36)) register_1 (.D(BTB_I), .C(C), .en(E_M1), .Q(D_M1));
  assign not_1_out = ~V;  // Not not_1, 4 bits wide
  and and_2 (and_2_out, ~E_M2, E_M3);  // And
  PriorityEncoder #(.Selector_Bits(2)) priorityencoder_1 (
    .in0(not_1_out[0]), .in1(not_1_out[1]), .in2(not_1_out[2]), .in3(not_1_out[3]), .num(BTB_ISS),
    .any(priorityencoder_1_any));
  RS_FF rs_ff_2 (.S(E_M2), .C(C), .R(and_2_out), .Q(V[1]));  // open: nQ
  Register #(.Bits(36)) register_2 (.D(BTB_I), .C(C), .en(E_M2), .Q(D_M2));
  not not_2 (full, priorityencoder_1_any);
  and and_3 (and_3_out, priorityencoder_1_any, E);
  Multiplexer #(.Selector_Bits(2), .Bits(36)) multiplexer_1 (
    .sel(rd_id), .in_0(D_M1), .in_1(D_M2), .in_2(D_M3), .in_3(D_M4), .out(BTB_O));
  and and_4 (and_4_out, ~E_M3, E_M4);  // And
  RS_FF rs_ff_3 (.S(E_M3), .C(C), .R(and_4_out), .Q(V[2]));  // open: nQ
  Register #(.Bits(36)) register_3 (.D(BTB_I), .C(C), .en(E_M3), .Q(D_M3));
  Demultiplexer #(.Selector_Bits(2)) demultiplexer_1 (
    .sel(BTB_ISS), .in(and_3_out), .out_0(E_M1), .out_1(E_M2), .out_2(E_M3), .out_3(E_M4));
  and and_5 (and_5_out, ~E_M4, E_M1);  // And
  RS_FF rs_ff_4 (.S(E_M4), .C(C), .R(and_5_out), .Q(V[3]));  // open: nQ
  Register #(.Bits(36)) register_4 (.D(BTB_I), .C(C), .en(E_M4), .Q(D_M4));

  // Other names for the same wires on the sheet: BTB_IS[1:0] = BTB_ISS; R_M1 = E_M2; R_M2 = E_M3; R_M3 = E_M4;
  //   R_M4 = E_M1; SEL[1:0] = rd_id; V_M1 = V[0]; V_M2 = V[1]; V_M3 = V[2]; V_M4 = V[3]

  // Notes on the sheet:
  //   BTB_I: inst data
  //   E: inst data
endmodule
