// Digital circuit busMF16-demux.dig as structural Verilog
module busMF16_demux (
  input  [15:0] B_A,
  input  [3:0] id,
  input  E,
  input  M,
  input  [15:0] B_M
);

  wire [15:0] demultiplexer_1_out_14, demultiplexer_2_out_0, demultiplexer_2_out_1;

  Demultiplexer #(.Selector_Bits(4)) demultiplexer_1 (
    .sel(id), .in(E), .out_0(demultiplexer_1_out_14[0]), .out_1(demultiplexer_1_out_14[1]),
    .out_2(demultiplexer_1_out_14[2]), .out_3(demultiplexer_1_out_14[3]), .out_4(demultiplexer_1_out_14[4]),
    .out_5(demultiplexer_1_out_14[5]), .out_6(demultiplexer_1_out_14[6]), .out_7(demultiplexer_1_out_14[7]),
    .out_8(demultiplexer_1_out_14[8]), .out_9(demultiplexer_1_out_14[9]),
    .out_10(demultiplexer_1_out_14[10]), .out_11(demultiplexer_1_out_14[11]),
    .out_12(demultiplexer_1_out_14[12]), .out_13(demultiplexer_1_out_14[13]),
    .out_14(demultiplexer_1_out_14[14]), .out_15(demultiplexer_1_out_14[15]));
  Demultiplexer #(.Bits(16)) demultiplexer_2 (
    .sel(M), .in(demultiplexer_1_out_14), .out_0(demultiplexer_2_out_0), .out_1(demultiplexer_2_out_1));
  assign B_A[0] = demultiplexer_2_out_0[0] ? 1'b1 : 1'bz;  // Driver driver_1
  assign B_A[1] = demultiplexer_2_out_0[1] ? 1'b1 : 1'bz;  // Driver driver_2
  assign B_A[2] = demultiplexer_2_out_0[2] ? 1'b1 : 1'bz;  // Driver driver_3
  assign B_A[3] = demultiplexer_2_out_0[3] ? 1'b1 : 1'bz;  // Driver driver_4
  assign B_A[4] = demultiplexer_2_out_0[4] ? 1'b1 : 1'bz;  // Driver driver_5
  assign B_A[5] = demultiplexer_2_out_0[5] ? 1'b1 : 1'bz;  // Driver driver_6
  assign B_A[6] = demultiplexer_2_out_0[6] ? 1'b1 : 1'bz;  // Driver driver_7
  assign B_A[7] = demultiplexer_2_out_0[7] ? 1'b1 : 1'bz;  // Driver driver_8
  assign B_A[8] = demultiplexer_2_out_0[8] ? 1'b1 : 1'bz;  // Driver driver_9
  assign B_A[9] = demultiplexer_2_out_0[9] ? 1'b1 : 1'bz;  // Driver driver_10
  assign B_A[10] = demultiplexer_2_out_0[10] ? 1'b1 : 1'bz;  // Driver driver_11
  assign B_A[11] = demultiplexer_2_out_0[11] ? 1'b1 : 1'bz;  // Driver driver_12
  assign B_A[12] = demultiplexer_2_out_0[12] ? 1'b1 : 1'bz;  // Driver driver_13
  assign B_A[13] = demultiplexer_2_out_0[13] ? 1'b1 : 1'bz;  // Driver driver_14
  assign B_A[14] = demultiplexer_2_out_0[14] ? 1'b1 : 1'bz;  // Driver driver_15
  assign B_A[15] = demultiplexer_2_out_0[15] ? 1'b1 : 1'bz;  // Driver driver_16
  assign B_M[0] = demultiplexer_2_out_1[0] ? 1'b1 : 1'bz;  // Driver driver_17
  assign B_M[1] = demultiplexer_2_out_1[1] ? 1'b1 : 1'bz;  // Driver driver_18
  assign B_M[2] = demultiplexer_2_out_1[2] ? 1'b1 : 1'bz;  // Driver driver_19
  assign B_M[3] = demultiplexer_2_out_1[3] ? 1'b1 : 1'bz;  // Driver driver_20
  assign B_M[4] = demultiplexer_2_out_1[4] ? 1'b1 : 1'bz;  // Driver driver_21
  assign B_M[5] = demultiplexer_2_out_1[5] ? 1'b1 : 1'bz;  // Driver driver_22
  assign B_M[6] = demultiplexer_2_out_1[6] ? 1'b1 : 1'bz;  // Driver driver_23
  assign B_M[7] = demultiplexer_2_out_1[7] ? 1'b1 : 1'bz;  // Driver driver_24
  assign B_M[8] = demultiplexer_2_out_1[8] ? 1'b1 : 1'bz;  // Driver driver_25
  assign B_M[9] = demultiplexer_2_out_1[9] ? 1'b1 : 1'bz;  // Driver driver_26
  assign B_M[10] = demultiplexer_2_out_1[10] ? 1'b1 : 1'bz;  // Driver driver_27
  assign B_M[11] = demultiplexer_2_out_1[11] ? 1'b1 : 1'bz;  // Driver driver_28
  assign B_M[12] = demultiplexer_2_out_1[12] ? 1'b1 : 1'bz;  // Driver driver_29
  assign B_M[13] = demultiplexer_2_out_1[13] ? 1'b1 : 1'bz;  // Driver driver_30
  assign B_M[14] = demultiplexer_2_out_1[14] ? 1'b1 : 1'bz;  // Driver driver_31
  assign B_M[15] = demultiplexer_2_out_1[15] ? 1'b1 : 1'bz;  // Driver driver_32
endmodule
