// Digital circuit call unit.dig as structural Verilog
module call_unit (
);

  wire and_1_out, and_5_out, and_10_out, and_15_out, and_19_out, and_20_out, C_ct, CALL_busy, CALL_busy__I,
       CALL_CLR, CALL_free, CALL_free__I, CALL_LD, CALL_RD, CALL_ST, clr, clr_ep, comparator_1_eq,
       comparator_2_eq, comparator_3_eq, comparator_4_eq, comparator_5_eq, comparator_6_eq, comparator_7_eq,
       comparator_8_eq, CT_CALL__LD, CT_FU__EPOCH, inst_comp_1_a_new, inst_comp_2_a_new, inst_comp_3_a_new,
       inst_comp_4_a_new, JPU_MFE, MB_MFE, multiplexer_1_out, multiplexer_5_out, multiplexer_6_out,
       multiplexer_7_out, multiplexer_9_out, multiplexer_10_out, multiplexer_12_out, multiplexer_14_out,
       multiplexer_15_out, multiplexer_17_out, not_1_out, not_3_out, not_4_out, not_5_out, not_6_out,
       or_1_out, or_2_out, or_4_out, or_8_out, register_2_q, register_5_q, register_9_q, register_11_q,
       rs_ff_9_nq;
  wire [0:0] or_9_out;
  wire [1:0] and_2_out, and_3_out, and_6_out, and_7_out, and_9_out, and_12_out, and_14_out, and_16_out,
       bitextender_1_out, bitextender_2_out, bitextender_3_out, bitextender_4_out, multiplexer_2_out,
       multiplexer_8_out, multiplexer_13_out, multiplexer_18_out, or_3_out, or_6_out, or_10_out, or_12_out,
       rs_ff_1_q, rs_ff_3_q, rs_ff_5_q, rs_ff_7_q;
  wire [2:1] register_6_q;
  wire [3:0] and_11_out, CALL_INST, clr_id, CT_FU__INST, Fl_JPU__INST, MB_INST, multiplexer_3_out,
       multiplexer_4_out, multiplexer_11_out, multiplexer_16_out, nand_1_out, nand_3_out, not_2_out,
       register_1_q, register_4_q, register_8_q;
  wire [15:0] V1_inst;

  not not_1 (not_1_out, clr);
  not not_2 (not_2_out[0], or_9_out[0]);
  xor xor_1 (not_2_out[1], or_9_out[0], clr);
  xor xor_2 (not_2_out[2], clr, clr);
  xor xor_3 (not_2_out[3], clr, clr);
  Multiplexer multiplexer_1 (.sel(and_11_out[3]), .in_0(nand_1_out[3]), .in_1(not_1_out), .out(multiplexer_1_out));
  and and_1 (and_1_out, multiplexer_1_out, CT_CALL__LD);
  not not_3 (not_3_out, multiplexer_1_out);
  Register #(.Bits(4)) register_1 (.D(CT_FU__INST), .C(C_ct), .en(multiplexer_3_out[3]), .Q(register_1_q));
  Register register_2 (.D(CT_FU__EPOCH), .C(C_ct), .en(multiplexer_3_out[3]), .Q(register_2_q));
  Comparator #(.Bits(4)) comparator_1 (.a(register_1_q), .b(MB_INST), .eq(comparator_1_eq));  // open: gt, lt
  Comparator #(.Bits(4)) comparator_2 (.a(register_1_q), .b(Fl_JPU__INST), .eq(comparator_2_eq));  // open: gt, lt
  Multiplexer #(.Bits(2)) multiplexer_2 (
    .sel(multiplexer_3_out[3]), .in_0(and_3_out), .in_1(2'b00), .out(multiplexer_2_out));
  assign and_2_out = ~2'b00 & bitextender_1_out;  // And and_2, 2 bits wide
  RS_FF rs_ff_1 (.S(multiplexer_2_out[0]), .C(C_ct), .R(and_2_out[0]), .Q(rs_ff_1_q[0]));  // open: nQ
  RS_FF rs_ff_2 (.S(multiplexer_2_out[1]), .C(C_ct), .R(and_2_out[1]), .Q(rs_ff_1_q[1]));  // open: nQ
  Register register_3 (.D(and_1_out), .C(C_ct), .en(or_1_out), .Q(clr));
  or or_1 (or_1_out, not_3_out, multiplexer_3_out[3]);
  Multiplexer #(.Bits(4)) multiplexer_3 (.sel(or_2_out), .in_0(not_2_out), .in_1(and_11_out), .out(multiplexer_3_out));
  or or_2 (or_2_out, and_11_out[0], and_11_out[1], and_11_out[2], and_11_out[3]);
  Multiplexer #(.Bits(4)) multiplexer_4 (.sel(clr), .in_0(CT_FU__INST), .in_1(register_1_q), .out(multiplexer_4_out));
  inst_comp inst_comp_1 (
    .A_id(register_1_q), .A_ep(register_2_q), .B_id(clr_id), .B_ep(clr_ep), .A_new(inst_comp_1_a_new));
  Multiplexer multiplexer_5 (.sel(clr), .in_0(CT_FU__EPOCH), .in_1(register_2_q), .out(multiplexer_5_out));
  and and_3 (and_3_out[0], comparator_1_eq, MB_MFE);
  and and_4 (and_3_out[1], comparator_2_eq, JPU_MFE);
  BitExtender #(.inputBits(1), .outputBits(2)) bitextender_1 (.in(multiplexer_3_out[3]), .out(bitextender_1_out));
  assign or_3_out = rs_ff_1_q | and_3_out;  // Or or_3, 2 bits wide
  Multiplexer multiplexer_6 (.sel(and_11_out[2]), .in_0(nand_1_out[2]), .in_1(nand_1_out[3]), .out(multiplexer_6_out));
  and and_5 (and_5_out, multiplexer_6_out, multiplexer_7_out);
  Multiplexer multiplexer_7 (.sel(clr), .in_0(CT_CALL__LD), .in_1(clr), .out(multiplexer_7_out));
  nand nand_1 (nand_1_out[3], inst_comp_1_a_new, clr);
  Register #(.Bits(4)) register_4 (.D(multiplexer_4_out), .C(C_ct), .en(multiplexer_3_out[2]), .Q(register_4_q));
  Register register_5 (.D(multiplexer_5_out), .C(C_ct), .en(multiplexer_3_out[2]), .Q(register_5_q));
  Comparator #(.Bits(4)) comparator_3 (.a(register_4_q), .b(MB_INST), .eq(comparator_3_eq));  // open: gt, lt
  Comparator #(.Bits(4)) comparator_4 (.a(register_4_q), .b(Fl_JPU__INST), .eq(comparator_4_eq));  // open: gt, lt
  Multiplexer #(.Bits(2)) multiplexer_8 (
    .sel(multiplexer_3_out[2]), .in_0(and_7_out), .in_1(or_3_out), .out(multiplexer_8_out));
  assign and_6_out = ~or_3_out & bitextender_2_out;  // And and_6, 2 bits wide
  RS_FF rs_ff_3 (.S(multiplexer_8_out[0]), .C(C_ct), .R(and_6_out[0]), .Q(rs_ff_3_q[0]));  // open: nQ
  RS_FF rs_ff_4 (.S(multiplexer_8_out[1]), .C(C_ct), .R(and_6_out[1]), .Q(rs_ff_3_q[1]));  // open: nQ
  Register register_6 (.D(and_5_out), .C(C_ct), .en(or_4_out), .Q(register_6_q[2]));
  not not_4 (not_4_out, multiplexer_6_out);
  or or_4 (or_4_out, not_4_out, multiplexer_3_out[2]);
  or or_5 (clr, register_6_q[2], clr);
  and and_7 (and_7_out[0], comparator_3_eq, MB_MFE);
  and and_8 (and_7_out[1], comparator_4_eq, JPU_MFE);
  BitExtender #(.inputBits(1), .outputBits(2)) bitextender_2 (.in(multiplexer_3_out[2]), .out(bitextender_2_out));
  assign or_6_out = rs_ff_3_q | and_7_out;  // Or or_6, 2 bits wide
  Multiplexer multiplexer_9 (.sel(and_11_out[1]), .in_0(nand_1_out[1]), .in_1(nand_1_out[2]), .out(multiplexer_9_out));
  Multiplexer multiplexer_10 (.sel(clr), .in_0(CT_CALL__LD), .in_1(register_6_q[2]), .out(multiplexer_10_out));
  or or_7 (clr, register_6_q[1], register_6_q[2], clr);
  Multiplexer #(.Bits(4)) multiplexer_11 (.sel(clr), .in_0(CT_FU__INST), .in_1(register_4_q), .out(multiplexer_11_out));
  inst_comp inst_comp_2 (
    .A_id(register_4_q), .A_ep(register_5_q), .B_id(clr_id), .B_ep(clr_ep), .A_new(inst_comp_2_a_new));
  Multiplexer multiplexer_12 (.sel(clr), .in_0(CT_FU__EPOCH), .in_1(register_5_q), .out(multiplexer_12_out));
  Multiplexer #(.Bits(2)) multiplexer_13 (
    .sel(multiplexer_3_out[1]), .in_0(and_12_out), .in_1(or_6_out), .out(multiplexer_13_out));
  assign and_9_out = ~or_6_out & bitextender_3_out;  // And and_9, 2 bits wide
  and and_10 (and_10_out, multiplexer_9_out, multiplexer_10_out);
  Register register_7 (.D(and_10_out), .C(C_ct), .en(or_8_out), .Q(register_6_q[1]));
  not not_5 (not_5_out, multiplexer_9_out);
  or or_8 (or_8_out, not_5_out, multiplexer_3_out[1]);
  or or_9 (or_9_out[0], CALL_busy__I, register_6_q[1], register_6_q[2], clr);
  nand nand_2 (nand_1_out[2], inst_comp_2_a_new, clr);
  Register #(.Bits(4)) register_8 (.D(multiplexer_11_out), .C(C_ct), .en(multiplexer_3_out[1]), .Q(register_8_q));
  Register register_9 (.D(multiplexer_12_out), .C(C_ct), .en(multiplexer_3_out[1]), .Q(register_9_q));
  Comparator #(.Bits(4)) comparator_5 (.a(register_8_q), .b(MB_INST), .eq(comparator_5_eq));  // open: gt, lt
  Comparator #(.Bits(4)) comparator_6 (.a(register_8_q), .b(Fl_JPU__INST), .eq(comparator_6_eq));  // open: gt, lt
  BitExtender #(.inputBits(1), .outputBits(2)) bitextender_3 (.in(multiplexer_3_out[1]), .out(bitextender_3_out));
  assign or_10_out = rs_ff_5_q | and_12_out;  // Or or_10, 2 bits wide
  RS_FF rs_ff_5 (.S(multiplexer_13_out[0]), .C(C_ct), .R(and_9_out[0]), .Q(rs_ff_5_q[0]));  // open: nQ
  RS_FF rs_ff_6 (.S(multiplexer_13_out[1]), .C(C_ct), .R(and_9_out[1]), .Q(rs_ff_5_q[1]));  // open: nQ
  Multiplexer multiplexer_14 (
    .sel(and_11_out[0]), .in_0(nand_1_out[0]), .in_1(nand_1_out[1]), .out(multiplexer_14_out));
  Multiplexer multiplexer_15 (.sel(clr), .in_0(CT_CALL__LD), .in_1(register_6_q[1]), .out(multiplexer_15_out));
  nand nand_3 (nand_3_out[3], CALL_busy__I, register_6_q[1], register_6_q[2], clr);
  assign and_11_out = nand_3_out & {{3{clr}}, or_9_out[0]};  // And and_11, 4 bits wide
  Multiplexer #(.Bits(4)) multiplexer_16 (.sel(clr), .in_0(CT_FU__INST), .in_1(register_8_q), .out(multiplexer_16_out));
  inst_comp inst_comp_3 (
    .A_id(register_8_q), .A_ep(register_9_q), .B_id(clr_id), .B_ep(clr_ep), .A_new(inst_comp_3_a_new));
  Multiplexer multiplexer_17 (.sel(clr), .in_0(CT_FU__EPOCH), .in_1(register_9_q), .out(multiplexer_17_out));
  and and_12 (and_12_out[0], comparator_5_eq, MB_MFE);
  and and_13 (and_12_out[1], comparator_6_eq, JPU_MFE);
  Multiplexer #(.Bits(2)) multiplexer_18 (.sel(CALL_LD), .in_0(and_16_out), .in_1(or_10_out), .out(multiplexer_18_out));
  assign and_14_out = ~or_10_out & bitextender_4_out;  // And and_14, 2 bits wide
  and and_15 (and_15_out, multiplexer_14_out, multiplexer_15_out);
  nand nand_4 (nand_3_out[2], CALL_busy__I, register_6_q[1], register_6_q[2]);
  nand nand_5 (nand_1_out[1], inst_comp_3_a_new, clr);
  Register #(.Bits(4)) register_10 (.D(multiplexer_16_out), .C(C_ct), .en(CALL_LD), .Q(CALL_INST));
  Register register_11 (.D(multiplexer_17_out), .C(C_ct), .en(CALL_LD), .Q(register_11_q));
  Comparator #(.Bits(4)) comparator_7 (.a(CALL_INST), .b(MB_INST), .eq(comparator_7_eq));  // open: gt, lt
  Comparator #(.Bits(4)) comparator_8 (.a(CALL_INST), .b(Fl_JPU__INST), .eq(comparator_8_eq));  // open: gt, lt
  BitExtender #(.inputBits(1), .outputBits(2)) bitextender_4 (.in(CALL_LD), .out(bitextender_4_out));
  RS_FF rs_ff_7 (.S(multiplexer_18_out[0]), .C(C_ct), .R(and_14_out[0]), .Q(rs_ff_7_q[0]));  // open: nQ
  RS_FF rs_ff_8 (.S(multiplexer_18_out[1]), .C(C_ct), .R(and_14_out[1]), .Q(rs_ff_7_q[1]));  // open: nQ
  or or_11 (CALL_free, not_6_out, CALL_ST);
  not not_6 (not_6_out, and_10_out);
  nand nand_6 (nand_3_out[1], CALL_busy__I, register_6_q[1]);
  inst_comp inst_comp_4 (
    .A_id(CALL_INST), .A_ep(register_11_q), .B_id(clr_id), .B_ep(clr_ep), .A_new(inst_comp_4_a_new));
  and and_16 (and_16_out[0], comparator_7_eq, MB_MFE);
  and and_17 (and_16_out[1], comparator_8_eq, JPU_MFE);
  assign or_12_out = rs_ff_7_q | and_16_out;  // Or or_12, 2 bits wide
  not not_7 (nand_3_out[0], CALL_busy__I);
  nand nand_7 (nand_1_out[0], inst_comp_4_a_new, clr);
  and and_18 (CALL_ST, or_12_out[0], or_12_out[1]);
  not not_8 (CALL_busy, CALL_free);
  and and_19 (and_19_out, ~and_15_out, CALL_ST);  // And
  and and_20 (and_20_out, CALL_ST, CALL_RD);
  and and_21 (CALL_CLR, clr, inst_comp_4_a_new);
  RS_FF rs_ff_9 (.S(and_15_out), .C(C_ct), .R(and_19_out), .Q(CALL_RD), .nQ(rs_ff_9_nq));
  or or_13 (CALL_free__I, CALL_ST, rs_ff_9_nq);
  bus16_demux bus16_demux_1 (.bus(V1_inst), .E(and_20_out), .id(CALL_INST));
  and and_22 (CALL_LD, and_15_out, CALL_free__I);
  not not_9 (CALL_busy__I, CALL_free__I);
endmodule
