// Digital circuit free-list.dig as structural Verilog
module free_list (
  input  C,
  input  [7:0] D,
  input  push,
  input  pop,
  output [7:0] out,
  output empty,
  output full
);

  wire counterpreset_1_ovf, d_ff_1_q, sub_1_c_o, xor_1_out;
  wire [4:0] counterpreset_1_out, multiplexer_1_out, sub_1_s;

  xor xor_1 (xor_1_out, pop, push);
  CounterPreset #(.Bits(5)) counterpreset_1 (
    .en(xor_1_out), .C(C), .dir(pop), .in({5{1'b0}}), .ld(1'b0), .clr(1'b0), .out(counterpreset_1_out),
    .ovf(counterpreset_1_ovf));
  Sub #(.Bits(5)) sub_1 (.a(counterpreset_1_out), .b(5'b00001), .c_i(1'b0), .s(sub_1_s), .c_o(sub_1_c_o));
  D_FF d_ff_1 (.D(counterpreset_1_ovf), .C(C), .Q(d_ff_1_q));  // open: nQ
  Multiplexer #(.Bits(5)) multiplexer_1 (
    .sel(xor_1_out), .in_0(sub_1_s), .in_1(counterpreset_1_out), .out(multiplexer_1_out));
  and and_1 (empty, sub_1_c_o, ~d_ff_1_q);  // And
  and and_2 (full, d_ff_1_q, sub_1_c_o);
  RegisterFile #(.AddrBits(5), .Bits(8)) registerfile_1 (
    .Din(D), .we(push), .Rw(multiplexer_1_out), .C(C), .Ra(sub_1_s), .Rb({5{1'b0}}), .Da(out));  // open: Db
endmodule
