// Digital circuit history-queue.dig as structural Verilog
module history_queue (
  input  C,
  input  [4:0] S1,
  input  [4:0] S2,
  input  res,
  input  [4:0] R,
  input  [31:0] D,
  input  E,
  input  P1,
  input  P2,
  input  [4:0] id,
  input  [4:0] com1_id,
  input  com1,
  input  [4:0] com2_id,
  input  com2,
  output [31:0] D1,
  output [31:0] D2,
  output [4:0] I1,
  output [4:0] I2,
  output V1,
  output V2,
  output full
);

  wire and_8_out, and_9_out, and_11_out, and_13_out, and_14_out, and_15_out, and_16_out, and_17_out,
       and_18_out, and_19_out, and_20_out, and_21_out, and_22_out, and_23_out, and_24_out, and_25_out,
       and_26_out, and_27_out, not_2_out, or_11_out, S1_valid, S2_valid;
  wire [1:0] S1_next, S2_next;
  wire [2:0] R_2_q, R_3_q, R_4_q, R_5_q, R_6_q, R_7_q, R_8_q, R_9_q, R_10_q, R_11_q, R_12_q, R_13_q, R_14_q,
       R_15_q, R_16_q, R_q;
  wire [3:0] or_1_out, or_5_out, priorityencoder_3_num, priorityencoder_4_num, rotatel_4_1_out,
       rotatel_4_2_out;
  wire [4:0] id_2_q, id_3_q, id_4_q, id_5_q, id_6_q, id_7_q, id_8_q, id_9_q, id_10_q, id_11_q, id_12_q,
       id_13_q, id_14_q, id_15_q, id_16_q, id_q;
  wire [15:0] and_1_out, and_2_out, and_3_out, and_4_out, and_5_out, and_6_out, and_7_out, and_12_out,
       bitextender_1_out, bitextender_2_out, bitextender_3_out, bitextender_4_out, bitextender_5_out,
       bitextender_6_out, comparator_1_eq, comparator_2_eq, comparator_3_eq, comparator_4_eq,
       demultiplexer_16_out_0, demultiplexer_16_out_1, demultiplexer_16_out_2, demultiplexer_16_out_3,
       demultiplexer_32_out_0, demultiplexer_32_out_1, demultiplexer_32_out_2, demultiplexer_32_out_3,
       fill_16_1_out1, not_1_out, not_3_out, or_6_out, or_7_out, priority_16_1_out1, priority_16_2_out1,
       undriven, valid_q;
  wire [31:0] data_2_q, data_3_q, data_4_q, data_5_q, data_6_q, data_7_q, data_8_q, data_9_q, data_10_q,
       data_11_q, data_12_q, data_13_q, data_14_q, data_15_q, data_16_q, data_q, R_q_2, undriven_2;

  Demultiplexer #(.Selector_Bits(2)) demultiplexer_1 (
    .sel(undriven_2[31:30]), .in(undriven[15]), .out_0(demultiplexer_16_out_0[15]),
    .out_1(demultiplexer_16_out_1[15]), .out_2(demultiplexer_16_out_2[15]), .out_3(demultiplexer_16_out_3[15]));
  Demultiplexer #(.Selector_Bits(2)) demultiplexer_2 (
    .sel(undriven_2[29:28]), .in(undriven[14]), .out_0(demultiplexer_16_out_0[14]),
    .out_1(demultiplexer_16_out_1[14]), .out_2(demultiplexer_16_out_2[14]), .out_3(demultiplexer_16_out_3[14]));
  Demultiplexer #(.Selector_Bits(2)) demultiplexer_3 (
    .sel(undriven_2[27:26]), .in(undriven[13]), .out_0(demultiplexer_16_out_0[13]),
    .out_1(demultiplexer_16_out_1[13]), .out_2(demultiplexer_16_out_2[13]), .out_3(demultiplexer_16_out_3[13]));
  Demultiplexer #(.Selector_Bits(2)) demultiplexer_4 (
    .sel(undriven_2[25:24]), .in(undriven[12]), .out_0(demultiplexer_16_out_0[12]),
    .out_1(demultiplexer_16_out_1[12]), .out_2(demultiplexer_16_out_2[12]), .out_3(demultiplexer_16_out_3[12]));
  Demultiplexer #(.Selector_Bits(2)) demultiplexer_5 (
    .sel(undriven_2[23:22]), .in(undriven[11]), .out_0(demultiplexer_16_out_0[11]),
    .out_1(demultiplexer_16_out_1[11]), .out_2(demultiplexer_16_out_2[11]), .out_3(demultiplexer_16_out_3[11]));
  Demultiplexer #(.Selector_Bits(2)) demultiplexer_6 (
    .sel(undriven_2[21:20]), .in(undriven[10]), .out_0(demultiplexer_16_out_0[10]),
    .out_1(demultiplexer_16_out_1[10]), .out_2(demultiplexer_16_out_2[10]), .out_3(demultiplexer_16_out_3[10]));
  Demultiplexer #(.Selector_Bits(2)) demultiplexer_7 (
    .sel(undriven_2[19:18]), .in(undriven[9]), .out_0(demultiplexer_16_out_0[9]),
    .out_1(demultiplexer_16_out_1[9]), .out_2(demultiplexer_16_out_2[9]), .out_3(demultiplexer_16_out_3[9]));
  Demultiplexer #(.Selector_Bits(2)) demultiplexer_8 (
    .sel(undriven_2[17:16]), .in(undriven[8]), .out_0(demultiplexer_16_out_0[8]),
    .out_1(demultiplexer_16_out_1[8]), .out_2(demultiplexer_16_out_2[8]), .out_3(demultiplexer_16_out_3[8]));
  Demultiplexer #(.Selector_Bits(2)) demultiplexer_9 (
    .sel(undriven_2[15:14]), .in(undriven[7]), .out_0(demultiplexer_16_out_0[7]),
    .out_1(demultiplexer_16_out_1[7]), .out_2(demultiplexer_16_out_2[7]), .out_3(demultiplexer_16_out_3[7]));
  Demultiplexer #(.Selector_Bits(2)) demultiplexer_10 (
    .sel(undriven_2[13:12]), .in(undriven[6]), .out_0(demultiplexer_16_out_0[6]),
    .out_1(demultiplexer_16_out_1[6]), .out_2(demultiplexer_16_out_2[6]), .out_3(demultiplexer_16_out_3[6]));
  Demultiplexer #(.Selector_Bits(2)) demultiplexer_11 (
    .sel(undriven_2[11:10]), .in(undriven[5]), .out_0(demultiplexer_16_out_0[5]),
    .out_1(demultiplexer_16_out_1[5]), .out_2(demultiplexer_16_out_2[5]), .out_3(demultiplexer_16_out_3[5]));
  Demultiplexer #(.Selector_Bits(2)) demultiplexer_12 (
    .sel(undriven_2[9:8]), .in(undriven[4]), .out_0(demultiplexer_16_out_0[4]),
    .out_1(demultiplexer_16_out_1[4]), .out_2(demultiplexer_16_out_2[4]), .out_3(demultiplexer_16_out_3[4]));
  Demultiplexer #(.Selector_Bits(2)) demultiplexer_13 (
    .sel(undriven_2[7:6]), .in(undriven[3]), .out_0(demultiplexer_16_out_0[3]),
    .out_1(demultiplexer_16_out_1[3]), .out_2(demultiplexer_16_out_2[3]), .out_3(demultiplexer_16_out_3[3]));
  Demultiplexer #(.Selector_Bits(2)) demultiplexer_14 (
    .sel(undriven_2[5:4]), .in(undriven[2]), .out_0(demultiplexer_16_out_0[2]),
    .out_1(demultiplexer_16_out_1[2]), .out_2(demultiplexer_16_out_2[2]), .out_3(demultiplexer_16_out_3[2]));
  Demultiplexer #(.Selector_Bits(2)) demultiplexer_15 (
    .sel(undriven_2[3:2]), .in(undriven[1]), .out_0(demultiplexer_16_out_0[1]),
    .out_1(demultiplexer_16_out_1[1]), .out_2(demultiplexer_16_out_2[1]), .out_3(demultiplexer_16_out_3[1]));
  Demultiplexer #(.Selector_Bits(2)) demultiplexer_16 (
    .sel(undriven_2[1:0]), .in(undriven[0]), .out_0(demultiplexer_16_out_0[0]),
    .out_1(demultiplexer_16_out_1[0]), .out_2(demultiplexer_16_out_2[0]), .out_3(demultiplexer_16_out_3[0]));
  or or_1 (or_1_out[0], demultiplexer_16_out_0[15], demultiplexer_16_out_0[14], demultiplexer_16_out_0[13], demultiplexer_16_out_0[12], demultiplexer_16_out_0[11], demultiplexer_16_out_0[10], demultiplexer_16_out_0[9], demultiplexer_16_out_0[8], demultiplexer_16_out_0[7], demultiplexer_16_out_0[6], demultiplexer_16_out_0[5], demultiplexer_16_out_0[4], demultiplexer_16_out_0[3], demultiplexer_16_out_0[2], demultiplexer_16_out_0[1], demultiplexer_16_out_0[0]);
  rotateL_4 rotatel_4_1 (.in(or_1_out), .rot(S2[4:3]), .out(rotatel_4_1_out));
  or or_2 (or_1_out[1], demultiplexer_16_out_1[15], demultiplexer_16_out_1[14], demultiplexer_16_out_1[13], demultiplexer_16_out_1[12], demultiplexer_16_out_1[11], demultiplexer_16_out_1[10], demultiplexer_16_out_1[9], demultiplexer_16_out_1[8], demultiplexer_16_out_1[7], demultiplexer_16_out_1[6], demultiplexer_16_out_1[5], demultiplexer_16_out_1[4], demultiplexer_16_out_1[3], demultiplexer_16_out_1[2], demultiplexer_16_out_1[1], demultiplexer_16_out_1[0]);
  PriorityEncoder #(.Selector_Bits(2)) priorityencoder_1 (
    .in0(rotatel_4_1_out[1]), .in1(rotatel_4_1_out[2]), .in2(rotatel_4_1_out[3]), .in3(rotatel_4_1_out[0]),
    .num(S2_next), .any(S2_valid));
  or or_3 (or_1_out[2], demultiplexer_16_out_2[15], demultiplexer_16_out_2[14], demultiplexer_16_out_2[13], demultiplexer_16_out_2[12], demultiplexer_16_out_2[11], demultiplexer_16_out_2[10], demultiplexer_16_out_2[9], demultiplexer_16_out_2[8], demultiplexer_16_out_2[7], demultiplexer_16_out_2[6], demultiplexer_16_out_2[5], demultiplexer_16_out_2[4], demultiplexer_16_out_2[3], demultiplexer_16_out_2[2], demultiplexer_16_out_2[1], demultiplexer_16_out_2[0]);
  or or_4 (or_1_out[3], demultiplexer_16_out_3[15], demultiplexer_16_out_3[14], demultiplexer_16_out_3[13], demultiplexer_16_out_3[12], demultiplexer_16_out_3[11], demultiplexer_16_out_3[10], demultiplexer_16_out_3[9], demultiplexer_16_out_3[8], demultiplexer_16_out_3[7], demultiplexer_16_out_3[6], demultiplexer_16_out_3[5], demultiplexer_16_out_3[4], demultiplexer_16_out_3[3], demultiplexer_16_out_3[2], demultiplexer_16_out_3[1], demultiplexer_16_out_3[0]);
  assign not_1_out = ~valid_q;  // Not not_1, 16 bits wide
  priority_16 priority_16_1 (
    .in1(and_3_out[0]), .in2(and_3_out[1]), .in3(and_3_out[2]), .in4(and_3_out[3]), .in5(and_3_out[4]),
    .in6(and_3_out[5]), .in7(and_3_out[6]), .in8(and_3_out[7]), .in9(and_3_out[8]), .in10(and_3_out[9]),
    .in11(and_3_out[10]), .in12(and_3_out[11]), .in13(and_3_out[12]), .in14(and_3_out[13]),
    .in15(and_3_out[14]), .in16(and_3_out[15]), .out1(priority_16_1_out1[0]), .out2(priority_16_1_out1[1]),
    .out3(priority_16_1_out1[2]), .out4(priority_16_1_out1[3]), .out5(priority_16_1_out1[4]),
    .out6(priority_16_1_out1[5]), .out7(priority_16_1_out1[6]), .out8(priority_16_1_out1[7]),
    .out9(priority_16_1_out1[8]), .out10(priority_16_1_out1[9]), .out11(priority_16_1_out1[10]),
    .out12(priority_16_1_out1[11]), .out13(priority_16_1_out1[12]), .out14(priority_16_1_out1[13]),
    .out15(priority_16_1_out1[14]), .out16(priority_16_1_out1[15]));  // open: v
  Demultiplexer #(.Selector_Bits(2)) demultiplexer_17 (
    .sel(R_q_2[31:30]), .in(valid_q[15]), .out_0(demultiplexer_32_out_0[15]),
    .out_1(demultiplexer_32_out_1[15]), .out_2(demultiplexer_32_out_2[15]), .out_3(demultiplexer_32_out_3[15]));
  Demultiplexer #(.Selector_Bits(2)) demultiplexer_18 (
    .sel(R_q_2[29:28]), .in(valid_q[14]), .out_0(demultiplexer_32_out_0[14]),
    .out_1(demultiplexer_32_out_1[14]), .out_2(demultiplexer_32_out_2[14]), .out_3(demultiplexer_32_out_3[14]));
  Demultiplexer #(.Selector_Bits(2)) demultiplexer_19 (
    .sel(R_q_2[27:26]), .in(valid_q[13]), .out_0(demultiplexer_32_out_0[13]),
    .out_1(demultiplexer_32_out_1[13]), .out_2(demultiplexer_32_out_2[13]), .out_3(demultiplexer_32_out_3[13]));
  Demultiplexer #(.Selector_Bits(2)) demultiplexer_20 (
    .sel(R_q_2[25:24]), .in(valid_q[12]), .out_0(demultiplexer_32_out_0[12]),
    .out_1(demultiplexer_32_out_1[12]), .out_2(demultiplexer_32_out_2[12]), .out_3(demultiplexer_32_out_3[12]));
  Demultiplexer #(.Selector_Bits(2)) demultiplexer_21 (
    .sel(R_q_2[23:22]), .in(valid_q[11]), .out_0(demultiplexer_32_out_0[11]),
    .out_1(demultiplexer_32_out_1[11]), .out_2(demultiplexer_32_out_2[11]), .out_3(demultiplexer_32_out_3[11]));
  Demultiplexer #(.Selector_Bits(2)) demultiplexer_22 (
    .sel(R_q_2[21:20]), .in(valid_q[10]), .out_0(demultiplexer_32_out_0[10]),
    .out_1(demultiplexer_32_out_1[10]), .out_2(demultiplexer_32_out_2[10]), .out_3(demultiplexer_32_out_3[10]));
  Demultiplexer #(.Selector_Bits(2)) demultiplexer_23 (
    .sel(R_q_2[19:18]), .in(valid_q[9]), .out_0(demultiplexer_32_out_0[9]),
    .out_1(demultiplexer_32_out_1[9]), .out_2(demultiplexer_32_out_2[9]), .out_3(demultiplexer_32_out_3[9]));
  Demultiplexer #(.Selector_Bits(2)) demultiplexer_24 (
    .sel(R_q_2[17:16]), .in(valid_q[8]), .out_0(demultiplexer_32_out_0[8]),
    .out_1(demultiplexer_32_out_1[8]), .out_2(demultiplexer_32_out_2[8]), .out_3(demultiplexer_32_out_3[8]));
  Demultiplexer #(.Selector_Bits(2)) demultiplexer_25 (
    .sel(R_q_2[15:14]), .in(valid_q[7]), .out_0(demultiplexer_32_out_0[7]),
    .out_1(demultiplexer_32_out_1[7]), .out_2(demultiplexer_32_out_2[7]), .out_3(demultiplexer_32_out_3[7]));
  Demultiplexer #(.Selector_Bits(2)) demultiplexer_26 (
    .sel(R_q_2[13:12]), .in(valid_q[6]), .out_0(demultiplexer_32_out_0[6]),
    .out_1(demultiplexer_32_out_1[6]), .out_2(demultiplexer_32_out_2[6]), .out_3(demultiplexer_32_out_3[6]));
  Demultiplexer #(.Selector_Bits(2)) demultiplexer_27 (
    .sel(R_q_2[11:10]), .in(valid_q[5]), .out_0(demultiplexer_32_out_0[5]),
    .out_1(demultiplexer_32_out_1[5]), .out_2(demultiplexer_32_out_2[5]), .out_3(demultiplexer_32_out_3[5]));
  Demultiplexer #(.Selector_Bits(2)) demultiplexer_28 (
    .sel(R_q_2[9:8]), .in(valid_q[4]), .out_0(demultiplexer_32_out_0[4]), .out_1(demultiplexer_32_out_1[4]),
    .out_2(demultiplexer_32_out_2[4]), .out_3(demultiplexer_32_out_3[4]));
  Demultiplexer #(.Selector_Bits(2)) demultiplexer_29 (
    .sel(R_q_2[7:6]), .in(valid_q[3]), .out_0(demultiplexer_32_out_0[3]), .out_1(demultiplexer_32_out_1[3]),
    .out_2(demultiplexer_32_out_2[3]), .out_3(demultiplexer_32_out_3[3]));
  Demultiplexer #(.Selector_Bits(2)) demultiplexer_30 (
    .sel(R_q_2[5:4]), .in(valid_q[2]), .out_0(demultiplexer_32_out_0[2]), .out_1(demultiplexer_32_out_1[2]),
    .out_2(demultiplexer_32_out_2[2]), .out_3(demultiplexer_32_out_3[2]));
  Demultiplexer #(.Selector_Bits(2)) demultiplexer_31 (
    .sel(R_q_2[3:2]), .in(valid_q[1]), .out_0(demultiplexer_32_out_0[1]), .out_1(demultiplexer_32_out_1[1]),
    .out_2(demultiplexer_32_out_2[1]), .out_3(demultiplexer_32_out_3[1]));
  Demultiplexer #(.Selector_Bits(2)) demultiplexer_32 (
    .sel(R_q_2[1:0]), .in(valid_q[0]), .out_0(demultiplexer_32_out_0[0]), .out_1(demultiplexer_32_out_1[0]),
    .out_2(demultiplexer_32_out_2[0]), .out_3(demultiplexer_32_out_3[0]));
  BitExtender #(.inputBits(1)) bitextender_1 (.in(com2), .out(bitextender_1_out));
  assign and_1_out = comparator_1_eq & bitextender_1_out;  // And and_1, 16 bits wide
  BitExtender #(.inputBits(1)) bitextender_2 (.in(com1), .out(bitextender_2_out));
  assign and_2_out = comparator_2_eq & bitextender_2_out;  // And and_2, 16 bits wide
  priority_16 priority_16_2 (
    .in1(and_4_out[0]), .in2(and_4_out[1]), .in3(and_4_out[2]), .in4(and_4_out[3]), .in5(and_4_out[4]),
    .in6(and_4_out[5]), .in7(and_4_out[6]), .in8(and_4_out[7]), .in9(and_4_out[8]), .in10(and_4_out[9]),
    .in11(and_4_out[10]), .in12(and_4_out[11]), .in13(and_4_out[12]), .in14(and_4_out[13]),
    .in15(and_4_out[14]), .in16(and_4_out[15]), .out1(priority_16_2_out1[0]), .out2(priority_16_2_out1[1]),
    .out3(priority_16_2_out1[2]), .out4(priority_16_2_out1[3]), .out5(priority_16_2_out1[4]),
    .out6(priority_16_2_out1[5]), .out7(priority_16_2_out1[6]), .out8(priority_16_2_out1[7]),
    .out9(priority_16_2_out1[8]), .out10(priority_16_2_out1[9]), .out11(priority_16_2_out1[10]),
    .out12(priority_16_2_out1[11]), .out13(priority_16_2_out1[12]), .out14(priority_16_2_out1[13]),
    .out15(priority_16_2_out1[14]), .out16(priority_16_2_out1[15]));  // open: v
  BitExtender #(.inputBits(1)) bitextender_3 (.in(P2), .out(bitextender_3_out));
  assign and_3_out = comparator_3_eq & bitextender_3_out;  // And and_3, 16 bits wide
  or or_5 (or_5_out[0], demultiplexer_32_out_0[15], demultiplexer_32_out_0[14], demultiplexer_32_out_0[13], demultiplexer_32_out_0[12], demultiplexer_32_out_0[11], demultiplexer_32_out_0[10], demultiplexer_32_out_0[9], demultiplexer_32_out_0[8], demultiplexer_32_out_0[7], demultiplexer_32_out_0[6], demultiplexer_32_out_0[5], demultiplexer_32_out_0[4], demultiplexer_32_out_0[3], demultiplexer_32_out_0[2], demultiplexer_32_out_0[1], demultiplexer_32_out_0[0]);
  BitExtender #(.inputBits(1)) bitextender_4 (.in(P1), .out(bitextender_4_out));
  assign and_4_out = comparator_4_eq & bitextender_4_out;  // And and_4, 16 bits wide
  assign or_6_out = and_2_out | and_1_out | priority_16_1_out1 | priority_16_2_out1;  // Or or_6, 16 bits wide
  assign or_7_out = and_2_out | and_1_out | not_1_out | and_3_out | and_4_out;  // Or or_7, 16 bits wide
  rotateL_4 rotatel_4_2 (.in(or_5_out), .rot(S1[4:3]), .out(rotatel_4_2_out));
  not not_2 (not_2_out, res);
  or or_8 (or_5_out[1], demultiplexer_32_out_1[15], demultiplexer_32_out_1[14], demultiplexer_32_out_1[13], demultiplexer_32_out_1[12], demultiplexer_32_out_1[11], demultiplexer_32_out_1[10], demultiplexer_32_out_1[9], demultiplexer_32_out_1[8], demultiplexer_32_out_1[7], demultiplexer_32_out_1[6], demultiplexer_32_out_1[5], demultiplexer_32_out_1[4], demultiplexer_32_out_1[3], demultiplexer_32_out_1[2], demultiplexer_32_out_1[1], demultiplexer_32_out_1[0]);
  assign and_5_out = valid_q & comparator_3_eq;  // And and_5, 16 bits wide
  BitExtender #(.inputBits(1)) bitextender_5 (.in(not_2_out), .out(bitextender_5_out));
  assign not_3_out = ~or_6_out;  // Not not_3, 16 bits wide
  PriorityEncoder #(.Selector_Bits(2)) priorityencoder_2 (
    .in0(rotatel_4_2_out[1]), .in1(rotatel_4_2_out[2]), .in2(rotatel_4_2_out[3]), .in3(rotatel_4_2_out[0]),
    .num(S1_next), .any(S1_valid));
  or or_9 (or_5_out[2], demultiplexer_32_out_2[15], demultiplexer_32_out_2[14], demultiplexer_32_out_2[13], demultiplexer_32_out_2[12], demultiplexer_32_out_2[11], demultiplexer_32_out_2[10], demultiplexer_32_out_2[9], demultiplexer_32_out_2[8], demultiplexer_32_out_2[7], demultiplexer_32_out_2[6], demultiplexer_32_out_2[5], demultiplexer_32_out_2[4], demultiplexer_32_out_2[3], demultiplexer_32_out_2[2], demultiplexer_32_out_2[1], demultiplexer_32_out_2[0]);
  assign and_6_out = valid_q & comparator_4_eq;  // And and_6, 16 bits wide
  assign and_7_out = bitextender_5_out & not_3_out;  // And and_7, 16 bits wide
  fill_16 fill_16_1 (
    .in1(or_7_out[0]), .in2(or_7_out[1]), .in3(or_7_out[2]), .in4(or_7_out[3]), .in5(or_7_out[4]),
    .in6(or_7_out[5]), .in7(or_7_out[6]), .in8(or_7_out[7]), .in9(or_7_out[8]), .in10(or_7_out[9]),
    .in11(or_7_out[10]), .in12(or_7_out[11]), .in13(or_7_out[12]), .in14(or_7_out[13]), .in15(or_7_out[14]),
    .in16(or_7_out[15]), .out1(fill_16_1_out1[0]), .out2(fill_16_1_out1[1]), .out3(fill_16_1_out1[2]),
    .out4(fill_16_1_out1[3]), .out5(fill_16_1_out1[4]), .out6(fill_16_1_out1[5]), .out7(fill_16_1_out1[6]),
    .out8(fill_16_1_out1[7]), .out9(fill_16_1_out1[8]), .out10(fill_16_1_out1[9]),
    .out11(fill_16_1_out1[10]), .out12(fill_16_1_out1[11]), .out13(fill_16_1_out1[12]),
    .out14(fill_16_1_out1[13]), .out15(fill_16_1_out1[14]), .out16(fill_16_1_out1[15]));
  or or_10 (or_5_out[3], demultiplexer_32_out_3[15], demultiplexer_32_out_3[14], demultiplexer_32_out_3[13], demultiplexer_32_out_3[12], demultiplexer_32_out_3[11], demultiplexer_32_out_3[10], demultiplexer_32_out_3[9], demultiplexer_32_out_3[8], demultiplexer_32_out_3[7], demultiplexer_32_out_3[6], demultiplexer_32_out_3[5], demultiplexer_32_out_3[4], demultiplexer_32_out_3[3], demultiplexer_32_out_3[2], demultiplexer_32_out_3[1], demultiplexer_32_out_3[0]);
  and and_8 (and_8_out, V1, P1);
  and and_9 (and_9_out, V2, P2);
  and and_10 (full, valid_q[0], valid_q[1], valid_q[2], valid_q[3], valid_q[4], valid_q[5], valid_q[6], valid_q[7], valid_q[8], valid_q[9], valid_q[10], valid_q[11], valid_q[12], valid_q[13], valid_q[14], valid_q[15]);
  or or_11 (or_11_out, E, and_8_out, and_9_out, com1, com2);
  PriorityEncoder #(.Selector_Bits(4)) priorityencoder_3 (
    .in0(and_6_out[0]), .in1(and_6_out[1]), .in2(and_6_out[2]), .in3(and_6_out[3]), .in4(and_6_out[4]),
    .in5(and_6_out[5]), .in6(and_6_out[6]), .in7(and_6_out[7]), .in8(and_6_out[8]), .in9(and_6_out[9]),
    .in10(and_6_out[10]), .in11(and_6_out[11]), .in12(and_6_out[12]), .in13(and_6_out[13]),
    .in14(and_6_out[14]), .in15(and_6_out[15]), .num(priorityencoder_3_num), .any(V1));
  PriorityEncoder #(.Selector_Bits(4)) priorityencoder_4 (
    .in0(and_5_out[0]), .in1(and_5_out[1]), .in2(and_5_out[2]), .in3(and_5_out[3]), .in4(and_5_out[4]),
    .in5(and_5_out[5]), .in6(and_5_out[6]), .in7(and_5_out[7]), .in8(and_5_out[8]), .in9(and_5_out[9]),
    .in10(and_5_out[10]), .in11(and_5_out[11]), .in12(and_5_out[12]), .in13(and_5_out[13]),
    .in14(and_5_out[14]), .in15(and_5_out[15]), .num(priorityencoder_4_num), .any(V2));
  Comparator #(.Bits(5)) comparator_1 (.a(com2_id), .b(id_q), .eq(comparator_1_eq[0]));  // open: gt, lt
  Comparator #(.Bits(5)) comparator_2 (.a(com1_id), .b(id_q), .eq(comparator_2_eq[0]));  // open: gt, lt
  Register #(.Bits(5)) u_id (.D(id), .C(C), .en(and_12_out[0]), .Q(id_q));
  Comparator #(.Bits(5)) comparator_3 (.a(S2), .b({R_q_2[1:0], R_q}), .eq(comparator_3_eq[0]));  // open: gt, lt
  Comparator #(.Bits(5)) comparator_4 (.a(S1), .b({R_q_2[1:0], R_q}), .eq(comparator_4_eq[0]));  // open: gt, lt
  and and_11 (and_11_out, E, and_7_out[0]);
  Register valid (.D(and_11_out), .C(C), .en(and_12_out[0]), .Q(valid_q[0]));
  Register #(.Bits(5)) u_R (.D(R), .C(C), .en(and_12_out[0]), .Q({R_q_2[1:0], R_q}));
  Register #(.Bits(32)) data (.D(D), .C(C), .en(and_12_out[0]), .Q(data_q));
  assign and_12_out = fill_16_1_out1 & bitextender_6_out;  // And and_12, 16 bits wide
  BitExtender #(.inputBits(1)) bitextender_6 (.in(or_11_out), .out(bitextender_6_out));
  Comparator #(.Bits(5)) comparator_5 (.a(com2_id), .b(id_2_q), .eq(comparator_1_eq[1]));  // open: gt, lt
  Comparator #(.Bits(5)) comparator_6 (.a(com1_id), .b(id_2_q), .eq(comparator_2_eq[1]));  // open: gt, lt
  Register #(.Bits(5)) id_2 (.D(id_q), .C(C), .en(and_12_out[1]), .Q(id_2_q));
  Comparator #(.Bits(5)) comparator_7 (.a(S2), .b({R_q_2[3:2], R_2_q}), .eq(comparator_3_eq[1]));  // open: gt, lt
  Comparator #(.Bits(5)) comparator_8 (.a(S1), .b({R_q_2[3:2], R_2_q}), .eq(comparator_4_eq[1]));  // open: gt, lt
  and and_13 (and_13_out, valid_q[0], and_7_out[1]);
  Register valid_2 (.D(and_13_out), .C(C), .en(and_12_out[1]), .Q(valid_q[1]));
  Register #(.Bits(5)) R_2 (.D({R_q_2[1:0], R_q}), .C(C), .en(and_12_out[1]), .Q({R_q_2[3:2], R_2_q}));
  Register #(.Bits(32)) data_2 (.D(data_q), .C(C), .en(and_12_out[1]), .Q(data_2_q));
  Comparator #(.Bits(5)) comparator_9 (.a(com2_id), .b(id_3_q), .eq(comparator_1_eq[2]));  // open: gt, lt
  Comparator #(.Bits(5)) comparator_10 (.a(com1_id), .b(id_3_q), .eq(comparator_2_eq[2]));  // open: gt, lt
  Register #(.Bits(5)) id_3 (.D(id_2_q), .C(C), .en(and_12_out[2]), .Q(id_3_q));
  Comparator #(.Bits(5)) comparator_11 (.a(S2), .b({R_q_2[5:4], R_3_q}), .eq(comparator_3_eq[2]));  // open: gt, lt
  Comparator #(.Bits(5)) comparator_12 (.a(S1), .b({R_q_2[5:4], R_3_q}), .eq(comparator_4_eq[2]));  // open: gt, lt
  and and_14 (and_14_out, valid_q[1], and_7_out[2]);
  Register valid_3 (.D(and_14_out), .C(C), .en(and_12_out[2]), .Q(valid_q[2]));
  Register #(.Bits(5)) R_3 (.D({R_q_2[3:2], R_2_q}), .C(C), .en(and_12_out[2]), .Q({R_q_2[5:4], R_3_q}));
  Register #(.Bits(32)) data_3 (.D(data_2_q), .C(C), .en(and_12_out[2]), .Q(data_3_q));
  Comparator #(.Bits(5)) comparator_13 (.a(com2_id), .b(id_4_q), .eq(comparator_1_eq[3]));  // open: gt, lt
  Comparator #(.Bits(5)) comparator_14 (.a(com1_id), .b(id_4_q), .eq(comparator_2_eq[3]));  // open: gt, lt
  Register #(.Bits(5)) id_4 (.D(id_3_q), .C(C), .en(and_12_out[3]), .Q(id_4_q));
  Comparator #(.Bits(5)) comparator_15 (.a(S2), .b({R_q_2[7:6], R_4_q}), .eq(comparator_3_eq[3]));  // open: gt, lt
  Comparator #(.Bits(5)) comparator_16 (.a(S1), .b({R_q_2[7:6], R_4_q}), .eq(comparator_4_eq[3]));  // open: gt, lt
  and and_15 (and_15_out, valid_q[2], and_7_out[3]);
  Register valid_4 (.D(and_15_out), .C(C), .en(and_12_out[3]), .Q(valid_q[3]));
  Register #(.Bits(5)) R_4 (.D({R_q_2[5:4], R_3_q}), .C(C), .en(and_12_out[3]), .Q({R_q_2[7:6], R_4_q}));
  Register #(.Bits(32)) data_4 (.D(data_3_q), .C(C), .en(and_12_out[3]), .Q(data_4_q));
  Comparator #(.Bits(5)) comparator_17 (.a(com2_id), .b(id_5_q), .eq(comparator_1_eq[4]));  // open: gt, lt
  Comparator #(.Bits(5)) comparator_18 (.a(com1_id), .b(id_5_q), .eq(comparator_2_eq[4]));  // open: gt, lt
  Register #(.Bits(5)) id_5 (.D(id_4_q), .C(C), .en(and_12_out[4]), .Q(id_5_q));
  Comparator #(.Bits(5)) comparator_19 (.a(S2), .b({R_q_2[9:8], R_5_q}), .eq(comparator_3_eq[4]));  // open: gt, lt
  Comparator #(.Bits(5)) comparator_20 (.a(S1), .b({R_q_2[9:8], R_5_q}), .eq(comparator_4_eq[4]));  // open: gt, lt
  and and_16 (and_16_out, valid_q[3], and_7_out[4]);
  Register valid_5 (.D(and_16_out), .C(C), .en(and_12_out[4]), .Q(valid_q[4]));
  Register #(.Bits(5)) R_5 (.D({R_q_2[7:6], R_4_q}), .C(C), .en(and_12_out[4]), .Q({R_q_2[9:8], R_5_q}));
  Register #(.Bits(32)) data_5 (.D(data_4_q), .C(C), .en(and_12_out[4]), .Q(data_5_q));
  Comparator #(.Bits(5)) comparator_21 (.a(com2_id), .b(id_6_q), .eq(comparator_1_eq[5]));  // open: gt, lt
  Comparator #(.Bits(5)) comparator_22 (.a(com1_id), .b(id_6_q), .eq(comparator_2_eq[5]));  // open: gt, lt
  Register #(.Bits(5)) id_6 (.D(id_5_q), .C(C), .en(and_12_out[5]), .Q(id_6_q));
  Comparator #(.Bits(5)) comparator_23 (.a(S2), .b({R_q_2[11:10], R_6_q}), .eq(comparator_3_eq[5]));  // open: gt, lt
  Comparator #(.Bits(5)) comparator_24 (.a(S1), .b({R_q_2[11:10], R_6_q}), .eq(comparator_4_eq[5]));  // open: gt, lt
  and and_17 (and_17_out, valid_q[4], and_7_out[5]);
  Register valid_6 (.D(and_17_out), .C(C), .en(and_12_out[5]), .Q(valid_q[5]));
  Register #(.Bits(5)) R_6 (.D({R_q_2[9:8], R_5_q}), .C(C), .en(and_12_out[5]), .Q({R_q_2[11:10], R_6_q}));
  Register #(.Bits(32)) data_6 (.D(data_5_q), .C(C), .en(and_12_out[5]), .Q(data_6_q));
  Comparator #(.Bits(5)) comparator_25 (.a(com2_id), .b(id_7_q), .eq(comparator_1_eq[6]));  // open: gt, lt
  Comparator #(.Bits(5)) comparator_26 (.a(com1_id), .b(id_7_q), .eq(comparator_2_eq[6]));  // open: gt, lt
  Register #(.Bits(5)) id_7 (.D(id_6_q), .C(C), .en(and_12_out[6]), .Q(id_7_q));
  Comparator #(.Bits(5)) comparator_27 (.a(S2), .b({R_q_2[13:12], R_7_q}), .eq(comparator_3_eq[6]));  // open: gt, lt
  Comparator #(.Bits(5)) comparator_28 (.a(S1), .b({R_q_2[13:12], R_7_q}), .eq(comparator_4_eq[6]));  // open: gt, lt
  and and_18 (and_18_out, valid_q[5], and_7_out[6]);
  Register valid_7 (.D(and_18_out), .C(C), .en(and_12_out[6]), .Q(valid_q[6]));
  Register #(.Bits(5)) R_7 (.D({R_q_2[11:10], R_6_q}), .C(C), .en(and_12_out[6]), .Q({R_q_2[13:12], R_7_q}));
  Register #(.Bits(32)) data_7 (.D(data_6_q), .C(C), .en(and_12_out[6]), .Q(data_7_q));
  Comparator #(.Bits(5)) comparator_29 (.a(com2_id), .b(id_8_q), .eq(comparator_1_eq[7]));  // open: gt, lt
  Comparator #(.Bits(5)) comparator_30 (.a(com1_id), .b(id_8_q), .eq(comparator_2_eq[7]));  // open: gt, lt
  Register #(.Bits(5)) id_8 (.D(id_7_q), .C(C), .en(and_12_out[7]), .Q(id_8_q));
  Comparator #(.Bits(5)) comparator_31 (.a(S2), .b({R_q_2[15:14], R_8_q}), .eq(comparator_3_eq[7]));  // open: gt, lt
  Comparator #(.Bits(5)) comparator_32 (.a(S1), .b({R_q_2[15:14], R_8_q}), .eq(comparator_4_eq[7]));  // open: gt, lt
  and and_19 (and_19_out, valid_q[6], and_7_out[7]);
  Register valid_8 (.D(and_19_out), .C(C), .en(and_12_out[7]), .Q(valid_q[7]));
  Register #(.Bits(5)) R_8 (.D({R_q_2[13:12], R_7_q}), .C(C), .en(and_12_out[7]), .Q({R_q_2[15:14], R_8_q}));
  Register #(.Bits(32)) data_8 (.D(data_7_q), .C(C), .en(and_12_out[7]), .Q(data_8_q));
  Comparator #(.Bits(5)) comparator_33 (.a(com2_id), .b(id_9_q), .eq(comparator_1_eq[8]));  // open: gt, lt
  Comparator #(.Bits(5)) comparator_34 (.a(com1_id), .b(id_9_q), .eq(comparator_2_eq[8]));  // open: gt, lt
  Register #(.Bits(5)) id_9 (.D(id_8_q), .C(C), .en(and_12_out[8]), .Q(id_9_q));
  Comparator #(.Bits(5)) comparator_35 (.a(S2), .b({R_q_2[17:16], R_9_q}), .eq(comparator_3_eq[8]));  // open: gt, lt
  Comparator #(.Bits(5)) comparator_36 (.a(S1), .b({R_q_2[17:16], R_9_q}), .eq(comparator_4_eq[8]));  // open: gt, lt
  and and_20 (and_20_out, valid_q[7], and_7_out[8]);
  Register valid_9 (.D(and_20_out), .C(C), .en(and_12_out[8]), .Q(valid_q[8]));
  Register #(.Bits(5)) R_9 (.D({R_q_2[15:14], R_8_q}), .C(C), .en(and_12_out[8]), .Q({R_q_2[17:16], R_9_q}));
  Register #(.Bits(32)) data_9 (.D(data_8_q), .C(C), .en(and_12_out[8]), .Q(data_9_q));
  Comparator #(.Bits(5)) comparator_37 (.a(com2_id), .b(id_10_q), .eq(comparator_1_eq[9]));  // open: gt, lt
  Comparator #(.Bits(5)) comparator_38 (.a(com1_id), .b(id_10_q), .eq(comparator_2_eq[9]));  // open: gt, lt
  Register #(.Bits(5)) id_10 (.D(id_9_q), .C(C), .en(and_12_out[9]), .Q(id_10_q));
  Comparator #(.Bits(5)) comparator_39 (.a(S2), .b({R_q_2[19:18], R_10_q}), .eq(comparator_3_eq[9]));  // open: gt, lt
  Comparator #(.Bits(5)) comparator_40 (.a(S1), .b({R_q_2[19:18], R_10_q}), .eq(comparator_4_eq[9]));  // open: gt, lt
  and and_21 (and_21_out, valid_q[8], and_7_out[9]);
  Register valid_10 (.D(and_21_out), .C(C), .en(and_12_out[9]), .Q(valid_q[9]));
  Register #(.Bits(5)) R_10 (.D({R_q_2[17:16], R_9_q}), .C(C), .en(and_12_out[9]), .Q({R_q_2[19:18], R_10_q}));
  Register #(.Bits(32)) data_10 (.D(data_9_q), .C(C), .en(and_12_out[9]), .Q(data_10_q));
  Comparator #(.Bits(5)) comparator_41 (.a(com2_id), .b(id_11_q), .eq(comparator_1_eq[10]));  // open: gt, lt
  Comparator #(.Bits(5)) comparator_42 (.a(com1_id), .b(id_11_q), .eq(comparator_2_eq[10]));  // open: gt, lt
  Register #(.Bits(5)) id_11 (.D(id_10_q), .C(C), .en(and_12_out[10]), .Q(id_11_q));
  Comparator #(.Bits(5)) comparator_43 (.a(S2), .b({R_q_2[21:20], R_11_q}), .eq(comparator_3_eq[10]));  // open: gt, lt
  Comparator #(.Bits(5)) comparator_44 (.a(S1), .b({R_q_2[21:20], R_11_q}), .eq(comparator_4_eq[10]));  // open: gt, lt
  and and_22 (and_22_out, valid_q[9], and_7_out[10]);
  Register valid_11 (.D(and_22_out), .C(C), .en(and_12_out[10]), .Q(valid_q[10]));
  Register #(.Bits(5)) R_11 (.D({R_q_2[19:18], R_10_q}), .C(C), .en(and_12_out[10]), .Q({R_q_2[21:20], R_11_q}));
  Register #(.Bits(32)) data_11 (.D(data_10_q), .C(C), .en(and_12_out[10]), .Q(data_11_q));
  Comparator #(.Bits(5)) comparator_45 (.a(com2_id), .b(id_12_q), .eq(comparator_1_eq[11]));  // open: gt, lt
  Comparator #(.Bits(5)) comparator_46 (.a(com1_id), .b(id_12_q), .eq(comparator_2_eq[11]));  // open: gt, lt
  Register #(.Bits(5)) id_12 (.D(id_11_q), .C(C), .en(and_12_out[11]), .Q(id_12_q));
  Comparator #(.Bits(5)) comparator_47 (.a(S2), .b({R_q_2[23:22], R_12_q}), .eq(comparator_3_eq[11]));  // open: gt, lt
  Comparator #(.Bits(5)) comparator_48 (.a(S1), .b({R_q_2[23:22], R_12_q}), .eq(comparator_4_eq[11]));  // open: gt, lt
  and and_23 (and_23_out, valid_q[10], and_7_out[11]);
  Register valid_12 (.D(and_23_out), .C(C), .en(and_12_out[11]), .Q(valid_q[11]));
  Register #(.Bits(5)) R_12 (.D({R_q_2[21:20], R_11_q}), .C(C), .en(and_12_out[11]), .Q({R_q_2[23:22], R_12_q}));
  Register #(.Bits(32)) data_12 (.D(data_11_q), .C(C), .en(and_12_out[11]), .Q(data_12_q));
  Comparator #(.Bits(5)) comparator_49 (.a(com2_id), .b(id_13_q), .eq(comparator_1_eq[12]));  // open: gt, lt
  Comparator #(.Bits(5)) comparator_50 (.a(com1_id), .b(id_13_q), .eq(comparator_2_eq[12]));  // open: gt, lt
  Register #(.Bits(5)) id_13 (.D(id_12_q), .C(C), .en(and_12_out[12]), .Q(id_13_q));
  Comparator #(.Bits(5)) comparator_51 (.a(S2), .b({R_q_2[25:24], R_13_q}), .eq(comparator_3_eq[12]));  // open: gt, lt
  Comparator #(.Bits(5)) comparator_52 (.a(S1), .b({R_q_2[25:24], R_13_q}), .eq(comparator_4_eq[12]));  // open: gt, lt
  and and_24 (and_24_out, valid_q[11], and_7_out[12]);
  Register valid_13 (.D(and_24_out), .C(C), .en(and_12_out[12]), .Q(valid_q[12]));
  Register #(.Bits(5)) R_13 (.D({R_q_2[23:22], R_12_q}), .C(C), .en(and_12_out[12]), .Q({R_q_2[25:24], R_13_q}));
  Register #(.Bits(32)) data_13 (.D(data_12_q), .C(C), .en(and_12_out[12]), .Q(data_13_q));
  Comparator #(.Bits(5)) comparator_53 (.a(com2_id), .b(id_14_q), .eq(comparator_1_eq[13]));  // open: gt, lt
  Comparator #(.Bits(5)) comparator_54 (.a(com1_id), .b(id_14_q), .eq(comparator_2_eq[13]));  // open: gt, lt
  Register #(.Bits(5)) id_14 (.D(id_13_q), .C(C), .en(and_12_out[13]), .Q(id_14_q));
  Comparator #(.Bits(5)) comparator_55 (.a(S2), .b({R_q_2[27:26], R_14_q}), .eq(comparator_3_eq[13]));  // open: gt, lt
  Comparator #(.Bits(5)) comparator_56 (.a(S1), .b({R_q_2[27:26], R_14_q}), .eq(comparator_4_eq[13]));  // open: gt, lt
  and and_25 (and_25_out, valid_q[12], and_7_out[13]);
  Register valid_14 (.D(and_25_out), .C(C), .en(and_12_out[13]), .Q(valid_q[13]));
  Register #(.Bits(5)) R_14 (.D({R_q_2[25:24], R_13_q}), .C(C), .en(and_12_out[13]), .Q({R_q_2[27:26], R_14_q}));
  Register #(.Bits(32)) data_14 (.D(data_13_q), .C(C), .en(and_12_out[13]), .Q(data_14_q));
  Comparator #(.Bits(5)) comparator_57 (.a(com2_id), .b(id_15_q), .eq(comparator_1_eq[14]));  // open: gt, lt
  Comparator #(.Bits(5)) comparator_58 (.a(com1_id), .b(id_15_q), .eq(comparator_2_eq[14]));  // open: gt, lt
  Register #(.Bits(5)) id_15 (.D(id_14_q), .C(C), .en(and_12_out[14]), .Q(id_15_q));
  Comparator #(.Bits(5)) comparator_59 (.a(S2), .b({R_q_2[29:28], R_15_q}), .eq(comparator_3_eq[14]));  // open: gt, lt
  Comparator #(.Bits(5)) comparator_60 (.a(S1), .b({R_q_2[29:28], R_15_q}), .eq(comparator_4_eq[14]));  // open: gt, lt
  and and_26 (and_26_out, valid_q[13], and_7_out[14]);
  Register valid_15 (.D(and_26_out), .C(C), .en(and_12_out[14]), .Q(valid_q[14]));
  Register #(.Bits(5)) R_15 (.D({R_q_2[27:26], R_14_q}), .C(C), .en(and_12_out[14]), .Q({R_q_2[29:28], R_15_q}));
  Register #(.Bits(32)) data_15 (.D(data_14_q), .C(C), .en(and_12_out[14]), .Q(data_15_q));
  Comparator #(.Bits(5)) comparator_61 (.a(com2_id), .b(id_16_q), .eq(comparator_1_eq[15]));  // open: gt, lt
  Comparator #(.Bits(5)) comparator_62 (.a(com1_id), .b(id_16_q), .eq(comparator_2_eq[15]));  // open: gt, lt
  Register #(.Bits(5)) id_16 (.D(id_15_q), .C(C), .en(and_12_out[15]), .Q(id_16_q));
  Comparator #(.Bits(5)) comparator_63 (.a(S2), .b({R_q_2[31:30], R_16_q}), .eq(comparator_3_eq[15]));  // open: gt, lt
  Comparator #(.Bits(5)) comparator_64 (.a(S1), .b({R_q_2[31:30], R_16_q}), .eq(comparator_4_eq[15]));  // open: gt, lt
  and and_27 (and_27_out, valid_q[14], and_7_out[15]);
  Register valid_16 (.D(and_27_out), .C(C), .en(and_12_out[15]), .Q(valid_q[15]));
  Register #(.Bits(5)) R_16 (.D({R_q_2[29:28], R_15_q}), .C(C), .en(and_12_out[15]), .Q({R_q_2[31:30], R_16_q}));
  Register #(.Bits(32)) data_16 (.D(data_15_q), .C(C), .en(and_12_out[15]), .Q(data_16_q));
  Multiplexer #(.Selector_Bits(4), .Bits(5)) multiplexer_1 (
    .sel(priorityencoder_4_num), .in_0(id_q), .in_1(id_2_q), .in_2(id_3_q), .in_3(id_4_q), .in_4(id_5_q),
    .in_5(id_6_q), .in_6(id_7_q), .in_7(id_8_q), .in_8(id_9_q), .in_9(id_10_q), .in_10(id_11_q),
    .in_11(id_12_q), .in_12(id_13_q), .in_13(id_14_q), .in_14(id_15_q), .in_15(id_16_q), .out(I2));
  Multiplexer #(.Selector_Bits(4), .Bits(5)) multiplexer_2 (
    .sel(priorityencoder_3_num), .in_0(id_q), .in_1(id_2_q), .in_2(id_3_q), .in_3(id_4_q), .in_4(id_5_q),
    .in_5(id_6_q), .in_6(id_7_q), .in_7(id_8_q), .in_8(id_9_q), .in_9(id_10_q), .in_10(id_11_q),
    .in_11(id_12_q), .in_12(id_13_q), .in_13(id_14_q), .in_14(id_15_q), .in_15(id_16_q), .out(I1));
  Multiplexer #(.Selector_Bits(4), .Bits(32)) multiplexer_3 (
    .sel(priorityencoder_3_num), .in_0(data_q), .in_1(data_2_q), .in_2(data_3_q), .in_3(data_4_q),
    .in_4(data_5_q), .in_5(data_6_q), .in_6(data_7_q), .in_7(data_8_q), .in_8(data_9_q), .in_9(data_10_q),
    .in_10(data_11_q), .in_11(data_12_q), .in_12(data_13_q), .in_13(data_14_q), .in_14(data_15_q),
    .in_15(data_16_q), .out(D1));
  Multiplexer #(.Selector_Bits(4), .Bits(32)) multiplexer_4 (
    .sel(priorityencoder_4_num), .in_0(data_q), .in_1(data_2_q), .in_2(data_3_q), .in_3(data_4_q),
    .in_4(data_5_q), .in_5(data_6_q), .in_6(data_7_q), .in_7(data_8_q), .in_8(data_9_q), .in_9(data_10_q),
    .in_10(data_11_q), .in_11(data_12_q), .in_12(data_13_q), .in_13(data_14_q), .in_14(data_15_q),
    .in_15(data_16_q), .out(D2));

  // Other names for the same wires on the sheet: cm1 = com1; cm1_id[4:0] = com1_id; cm2 = com2; cm2_id[4:0] = com2_id;
  //   OD1[31:0] = D1; OD2[31:0] = D2; OI1[4:0] = I1; OI2[4:0] = I2
endmodule
