// Digital circuit inst-wfile-debug.dig as structural Verilog
module inst_wfile_debug (
  input  C,
  input  [5:0] SC_inst,
  input  [5:0] FL_inst,
  input  SC_sel,
  input  FL_sel,
  input  SC_e,
  input  FL_e,
  input  [4:0] Inst,
  input  [4:0] W,
  input  [4:0] RA,
  input  [4:0] RB,
  input  E1,
  input  com1,
  input  com2,
  input  [3:0] I_com1,
  input  [3:0] I_com2,
  input  res,
  input  clr,
  input  [3:0] clr_id,
  input  clr_ep,
  input  OBLK,
  output [4:0] R_A,
  output [4:0] R_B,
  output [4:0] SC_O,
  output [4:0] FL_O,
  output [4:0] BLK_O
);

  wire and_1_out, and_2_out, and_3_out, and_6_out, and_7_out, and_9_out, BLK_cmp, BLK_com1, BLK_com2, BLK_e,
       BLK_FM, BLK_M, comparator_31_eq, FL_cmp, FL_com1, FL_com2, FL_e_t, FL_FM, FL_M, multiplexer_42_out,
       multiplexer_50_out, not_2_out, not_3_out, or_1_out, R1_cmp, R1_com1, R1_com2, R1_e, R1_FM, R1_M,
       R2_cmp, R2_com1, R2_com2, R2_e, R2_FM, R2_M, R3_cmp, R3_com1, R3_com2, R3_e, R3_FM, R3_M, R4_cmp,
       R4_com1, R4_com2, R4_e, R4_FM, R4_M, R5_cmp, R5_com1, R5_com2, R5_e, R5_FM, R5_M, R6_cmp, R6_com1,
       R6_com2, R6_e, R6_FM, R6_M, R7_cmp, R7_com1, R7_com2, R7_e, R7_FM, R7_M, R8_cmp, R8_com1, R8_com2,
       R8_e, R8_FM, R8_M, R9_cmp, R9_com1, R9_com2, R9_e, R9_FM, R9_M, R10_cmp, R10_com1, R10_com2, R10_e,
       R10_FM, R10_M, R11_cmp, R11_com1, R11_com2, R11_e, R11_FM, R11_M, R12_cmp, R12_com1, R12_com2, R12_e,
       R12_FM, R12_M, R13_cmp, R13_com1, R13_com2, R13_e, R13_FM, R13_M, R14_cmp, R14_com1, R14_com2, R14_e,
       R14_FM, R14_M, R15_cmp, R15_com1, R15_com2, R15_e, R15_FM, R15_M, R16_cmp, R16_com1, R16_com2, R16_e,
       R16_FM, R16_M, R17_cmp, R17_com1, R17_com2, R17_e, R17_FM, R17_M, R18_cmp, R18_com1, R18_com2, R18_e,
       R18_FM, R18_M, R19_cmp, R19_com1, R19_com2, R19_e, R19_FM, R19_M, R20_cmp, R20_com1, R20_com2, R20_e,
       R20_FM, R20_M, R21_cmp, R21_com1, R21_com2, R21_e, R21_FM, R21_M, R22_cmp, R22_com1, R22_com2, R22_e,
       R22_FM, R22_M, R23_cmp, R23_com1, R23_com2, R23_e, R23_FM, R23_M, R24_cmp, R24_com1, R24_com2, R24_e,
       R24_FM, R24_M, R25_cmp, R25_com1, R25_com2, R25_e, R25_FM, R25_M, SBP_cmp, SBP_com1, SBP_com2, SBP_e,
       SBP_FM, SBP_M, SC_cmp, SC_com1, SC_com2, SC_e_t, SC_FM, SC_M;
  wire [4:4] BLK, FL, R_A_t, R_B_t, SC;
  wire [5:0] multiplexer_1_out, multiplexer_2_out, multiplexer_3_out, multiplexer_4_out, multiplexer_5_out,
       multiplexer_6_out, multiplexer_7_out, multiplexer_8_out, multiplexer_9_out, multiplexer_10_out,
       multiplexer_11_out, multiplexer_12_out, multiplexer_13_out, multiplexer_14_out, multiplexer_15_out,
       multiplexer_16_out, multiplexer_17_out, multiplexer_18_out, multiplexer_19_out, multiplexer_20_out,
       multiplexer_21_out, multiplexer_22_out, multiplexer_23_out, multiplexer_24_out, multiplexer_25_out,
       multiplexer_26_out, multiplexer_27_out, multiplexer_28_out, multiplexer_29_out, multiplexer_30_out,
       multiplexer_31_out, multiplexer_32_out, multiplexer_33_out, multiplexer_34_out, multiplexer_35_out,
       multiplexer_36_out, multiplexer_37_out, multiplexer_38_out, multiplexer_39_out, multiplexer_40_out,
       multiplexer_41_out, multiplexer_43_out, multiplexer_44_out, multiplexer_45_out, multiplexer_46_out,
       multiplexer_47_out, multiplexer_48_out, multiplexer_49_out, multiplexer_51_out, multiplexer_52_out,
       multiplexer_53_out, multiplexer_54_out, multiplexer_55_out, multiplexer_56_out, multiplexer_57_out,
       multiplexer_58_out, multiplexer_59_out, multiplexer_60_out, multiplexer_61_out, multiplexer_62_out,
       R1, R2, R3, R4, R5, R6, R7, R8, R9, R10, R11, R12, R13, R14, R15, R16, R17, R18, R19, R20, R21, R22,
       R23, R24, R25, SBP;
  wire [5:2] and_8_out, or_3_out, or_6_out;
  wire [31:0] and_4_out, and_5_out, and_11_out, bitextender_1_out, bitextender_2_out, bitextender_3_out,
       bitextender_4_out, demultiplexer_1_out_0, not_1_out, not_4_out, or_2_out;

  Multiplexer #(.Bits(6)) multiplexer_1 (
    .sel(BLK_FM), .in_0(6'b100000), .in_1({1'b0, clr_ep, clr_id}), .out(multiplexer_1_out));
  Multiplexer #(.Bits(6)) multiplexer_2 (
    .sel(R1_FM), .in_0(6'b100000), .in_1({1'b0, clr_ep, clr_id}), .out(multiplexer_2_out));
  Multiplexer #(.Bits(6)) multiplexer_3 (
    .sel(R5_FM), .in_0(6'b100000), .in_1({1'b0, clr_ep, clr_id}), .out(multiplexer_3_out));
  Multiplexer #(.Bits(6)) multiplexer_4 (
    .sel(R9_FM), .in_0(6'b100000), .in_1({1'b0, clr_ep, clr_id}), .out(multiplexer_4_out));
  Multiplexer #(.Bits(6)) multiplexer_5 (
    .sel(R13_FM), .in_0(6'b100000), .in_1({1'b0, clr_ep, clr_id}), .out(multiplexer_5_out));
  Multiplexer #(.Bits(6)) multiplexer_6 (
    .sel(R17_FM), .in_0(6'b100000), .in_1({1'b0, clr_ep, clr_id}), .out(multiplexer_6_out));
  Multiplexer #(.Bits(6)) multiplexer_7 (
    .sel(R21_FM), .in_0(6'b100000), .in_1({1'b0, clr_ep, clr_id}), .out(multiplexer_7_out));
  Multiplexer #(.Bits(6)) multiplexer_8 (
    .sel(R25_FM), .in_0(6'b100000), .in_1({1'b0, clr_ep, clr_id}), .out(multiplexer_8_out));
  Multiplexer #(.Bits(6)) multiplexer_9 (
    .sel(SBP_FM), .in_0(6'b100000), .in_1({1'b0, clr_ep, clr_id}), .out(multiplexer_9_out));
  Demultiplexer #(.Selector_Bits(5)) demultiplexer_1 (
    .sel(W), .in(E1), .out_0(demultiplexer_1_out_0[31]), .out_1(demultiplexer_1_out_0[30]),
    .out_2(demultiplexer_1_out_0[29]), .out_3(demultiplexer_1_out_0[28]), .out_4(demultiplexer_1_out_0[27]),
    .out_5(demultiplexer_1_out_0[26]), .out_6(demultiplexer_1_out_0[25]), .out_7(demultiplexer_1_out_0[24]),
    .out_8(demultiplexer_1_out_0[23]), .out_9(demultiplexer_1_out_0[22]), .out_10(demultiplexer_1_out_0[21]),
    .out_11(demultiplexer_1_out_0[20]), .out_12(demultiplexer_1_out_0[19]),
    .out_13(demultiplexer_1_out_0[18]), .out_14(demultiplexer_1_out_0[17]),
    .out_15(demultiplexer_1_out_0[16]), .out_16(demultiplexer_1_out_0[15]),
    .out_17(demultiplexer_1_out_0[14]), .out_18(demultiplexer_1_out_0[13]),
    .out_19(demultiplexer_1_out_0[12]), .out_20(demultiplexer_1_out_0[11]),
    .out_21(demultiplexer_1_out_0[10]), .out_22(demultiplexer_1_out_0[9]), .out_23(demultiplexer_1_out_0[8]),
    .out_24(demultiplexer_1_out_0[7]), .out_25(demultiplexer_1_out_0[6]), .out_26(demultiplexer_1_out_0[5]),
    .out_27(demultiplexer_1_out_0[4]), .out_28(demultiplexer_1_out_0[3]), .out_29(demultiplexer_1_out_0[2]),
    .out_30(demultiplexer_1_out_0[1]), .out_31(demultiplexer_1_out_0[0]));
  Multiplexer #(.Bits(6)) multiplexer_10 (
    .sel(BLK_M), .in_0({1'b0, Inst}), .in_1(multiplexer_1_out), .out(multiplexer_10_out));
  Register #(.Bits(6)) u_BLK (.D(multiplexer_10_out), .C(C), .en(BLK_e), .Q({BLK_O[4], BLK[4], BLK_O[3:0]}));
  Multiplexer #(.Bits(6)) multiplexer_11 (
    .sel(R1_M), .in_0({1'b0, Inst}), .in_1(multiplexer_2_out), .out(multiplexer_11_out));
  Register #(.Bits(6)) u_R1 (.D(multiplexer_11_out), .C(C), .en(R1_e), .Q(R1));
  Multiplexer #(.Bits(6)) multiplexer_12 (
    .sel(R5_M), .in_0({1'b0, Inst}), .in_1(multiplexer_3_out), .out(multiplexer_12_out));
  Register #(.Bits(6)) u_R5 (.D(multiplexer_12_out), .C(C), .en(R5_e), .Q(R5));
  Multiplexer #(.Bits(6)) multiplexer_13 (
    .sel(R9_M), .in_0({1'b0, Inst}), .in_1(multiplexer_4_out), .out(multiplexer_13_out));
  Register #(.Bits(6)) u_R9 (.D(multiplexer_13_out), .C(C), .en(R9_e), .Q(R9));
  Multiplexer #(.Bits(6)) multiplexer_14 (
    .sel(R13_M), .in_0({1'b0, Inst}), .in_1(multiplexer_5_out), .out(multiplexer_14_out));
  Register #(.Bits(6)) u_R13 (.D(multiplexer_14_out), .C(C), .en(R13_e), .Q(R13));
  Multiplexer #(.Bits(6)) multiplexer_15 (
    .sel(R17_M), .in_0({1'b0, Inst}), .in_1(multiplexer_6_out), .out(multiplexer_15_out));
  Register #(.Bits(6)) u_R17 (.D(multiplexer_15_out), .C(C), .en(R17_e), .Q(R17));
  Multiplexer #(.Bits(6)) multiplexer_16 (
    .sel(R21_M), .in_0({1'b0, Inst}), .in_1(multiplexer_7_out), .out(multiplexer_16_out));
  Register #(.Bits(6)) u_R21 (.D(multiplexer_16_out), .C(C), .en(R21_e), .Q(R21));
  Multiplexer #(.Bits(6)) multiplexer_17 (
    .sel(R25_M), .in_0({1'b0, Inst}), .in_1(multiplexer_8_out), .out(multiplexer_17_out));
  Register #(.Bits(6)) u_R25 (.D(multiplexer_17_out), .C(C), .en(R25_e), .Q(R25));
  Multiplexer #(.Bits(6)) multiplexer_18 (
    .sel(SBP_M), .in_0({1'b0, Inst}), .in_1(multiplexer_9_out), .out(multiplexer_18_out));
  Register #(.Bits(6)) u_SBP (.D(multiplexer_18_out), .C(C), .en(SBP_e), .Q(SBP));
  Comparator #(.Bits(4)) comparator_1 (.a(BLK_O[3:0]), .b(I_com2), .eq(BLK_com2));  // open: gt, lt
  Comparator #(.Bits(4)) comparator_2 (.a(BLK_O[3:0]), .b(I_com1), .eq(BLK_com1));  // open: gt, lt
  inst_comp inst_comp_1 (.A_id(BLK_O[3:0]), .A_ep(BLK[4]), .B_id(clr_id), .B_ep(clr_ep), .A_new(BLK_cmp));
  Comparator #(.Bits(4)) comparator_3 (.a(R1[3:0]), .b(I_com2), .eq(R1_com2));  // open: gt, lt
  Comparator #(.Bits(4)) comparator_4 (.a(R1[3:0]), .b(I_com1), .eq(R1_com1));  // open: gt, lt
  inst_comp inst_comp_2 (.A_id(R1[3:0]), .A_ep(R1[4]), .B_id(clr_id), .B_ep(clr_ep), .A_new(R1_cmp));
  Comparator #(.Bits(4)) comparator_5 (.a(R5[3:0]), .b(I_com2), .eq(R5_com2));  // open: gt, lt
  Comparator #(.Bits(4)) comparator_6 (.a(R5[3:0]), .b(I_com1), .eq(R5_com1));  // open: gt, lt
  inst_comp inst_comp_3 (.A_id(R5[3:0]), .A_ep(R5[4]), .B_id(clr_id), .B_ep(clr_ep), .A_new(R5_cmp));
  Comparator #(.Bits(4)) comparator_7 (.a(R9[3:0]), .b(I_com2), .eq(R9_com2));  // open: gt, lt
  Comparator #(.Bits(4)) comparator_8 (.a(R9[3:0]), .b(I_com1), .eq(R9_com1));  // open: gt, lt
  inst_comp inst_comp_4 (.A_id(R9[3:0]), .A_ep(R9[4]), .B_id(clr_id), .B_ep(clr_ep), .A_new(R9_cmp));
  Comparator #(.Bits(4)) comparator_9 (.a(R13[3:0]), .b(I_com2), .eq(R13_com2));  // open: gt, lt
  Comparator #(.Bits(4)) comparator_10 (.a(R13[3:0]), .b(I_com1), .eq(R13_com1));  // open: gt, lt
  inst_comp inst_comp_5 (.A_id(R13[3:0]), .A_ep(R13[4]), .B_id(clr_id), .B_ep(clr_ep), .A_new(R13_cmp));
  Comparator #(.Bits(4)) comparator_11 (.a(R17[3:0]), .b(I_com2), .eq(R17_com2));  // open: gt, lt
  Comparator #(.Bits(4)) comparator_12 (.a(R17[3:0]), .b(I_com1), .eq(R17_com1));  // open: gt, lt
  inst_comp inst_comp_6 (.A_id(R17[3:0]), .A_ep(R17[4]), .B_id(clr_id), .B_ep(clr_ep), .A_new(R17_cmp));
  Comparator #(.Bits(4)) comparator_13 (.a(R21[3:0]), .b(I_com2), .eq(R21_com2));  // open: gt, lt
  Comparator #(.Bits(4)) comparator_14 (.a(R21[3:0]), .b(I_com1), .eq(R21_com1));  // open: gt, lt
  inst_comp inst_comp_7 (.A_id(R21[3:0]), .A_ep(R21[4]), .B_id(clr_id), .B_ep(clr_ep), .A_new(R21_cmp));
  Comparator #(.Bits(4)) comparator_15 (.a(R25[3:0]), .b(I_com2), .eq(R25_com2));  // open: gt, lt
  Comparator #(.Bits(4)) comparator_16 (.a(R25[3:0]), .b(I_com1), .eq(R25_com1));  // open: gt, lt
  inst_comp inst_comp_8 (.A_id(R25[3:0]), .A_ep(R25[4]), .B_id(clr_id), .B_ep(clr_ep), .A_new(R25_cmp));
  Comparator #(.Bits(4)) comparator_17 (.a(SBP[3:0]), .b(I_com2), .eq(SBP_com2));  // open: gt, lt
  Comparator #(.Bits(4)) comparator_18 (.a(SBP[3:0]), .b(I_com1), .eq(SBP_com1));  // open: gt, lt
  inst_comp inst_comp_9 (.A_id(SBP[3:0]), .A_ep(SBP[4]), .B_id(clr_id), .B_ep(clr_ep), .A_new(SBP_cmp));
  Multiplexer #(.Bits(6)) multiplexer_19 (
    .sel(R2_FM), .in_0(6'b100000), .in_1({1'b0, clr_ep, clr_id}), .out(multiplexer_19_out));
  Multiplexer #(.Bits(6)) multiplexer_20 (
    .sel(R6_FM), .in_0(6'b100000), .in_1({1'b0, clr_ep, clr_id}), .out(multiplexer_20_out));
  Multiplexer #(.Bits(6)) multiplexer_21 (
    .sel(R10_FM), .in_0(6'b100000), .in_1({1'b0, clr_ep, clr_id}), .out(multiplexer_21_out));
  Multiplexer #(.Bits(6)) multiplexer_22 (
    .sel(R14_FM), .in_0(6'b100000), .in_1({1'b0, clr_ep, clr_id}), .out(multiplexer_22_out));
  Multiplexer #(.Bits(6)) multiplexer_23 (
    .sel(R18_FM), .in_0(6'b100000), .in_1({1'b0, clr_ep, clr_id}), .out(multiplexer_23_out));
  Multiplexer #(.Bits(6)) multiplexer_24 (
    .sel(R22_FM), .in_0(6'b100000), .in_1({1'b0, clr_ep, clr_id}), .out(multiplexer_24_out));
  Multiplexer #(.Bits(6)) multiplexer_25 (
    .sel(R2_M), .in_0({1'b0, Inst}), .in_1(multiplexer_19_out), .out(multiplexer_25_out));
  Register #(.Bits(6)) u_R2 (.D(multiplexer_25_out), .C(C), .en(R2_e), .Q(R2));
  Multiplexer #(.Bits(6)) multiplexer_26 (
    .sel(R6_M), .in_0({1'b0, Inst}), .in_1(multiplexer_20_out), .out(multiplexer_26_out));
  Register #(.Bits(6)) u_R6 (.D(multiplexer_26_out), .C(C), .en(R6_e), .Q(R6));
  Multiplexer #(.Bits(6)) multiplexer_27 (
    .sel(R10_M), .in_0({1'b0, Inst}), .in_1(multiplexer_21_out), .out(multiplexer_27_out));
  Register #(.Bits(6)) u_R10 (.D(multiplexer_27_out), .C(C), .en(R10_e), .Q(R10));
  Multiplexer #(.Bits(6)) multiplexer_28 (
    .sel(R14_M), .in_0({1'b0, Inst}), .in_1(multiplexer_22_out), .out(multiplexer_28_out));
  Register #(.Bits(6)) u_R14 (.D(multiplexer_28_out), .C(C), .en(R14_e), .Q(R14));
  Multiplexer #(.Bits(6)) multiplexer_29 (
    .sel(R18_M), .in_0({1'b0, Inst}), .in_1(multiplexer_23_out), .out(multiplexer_29_out));
  Register #(.Bits(6)) u_R18 (.D(multiplexer_29_out), .C(C), .en(R18_e), .Q(R18));
  Multiplexer #(.Bits(6)) multiplexer_30 (
    .sel(R22_M), .in_0({1'b0, Inst}), .in_1(multiplexer_24_out), .out(multiplexer_30_out));
  Register #(.Bits(6)) u_R22 (.D(multiplexer_30_out), .C(C), .en(R22_e), .Q(R22));
  Multiplexer #(.Bits(6)) multiplexer_31 (
    .sel(SC_FM), .in_0(6'b100000), .in_1({1'b0, clr_ep, clr_id}), .out(multiplexer_31_out));
  Comparator #(.Bits(4)) comparator_19 (.a(R2[3:0]), .b(I_com2), .eq(R2_com2));  // open: gt, lt
  Comparator #(.Bits(4)) comparator_20 (.a(R2[3:0]), .b(I_com1), .eq(R2_com1));  // open: gt, lt
  inst_comp inst_comp_10 (.A_id(R2[3:0]), .A_ep(R2[4]), .B_id(clr_id), .B_ep(clr_ep), .A_new(R2_cmp));
  Comparator #(.Bits(4)) comparator_21 (.a(R6[3:0]), .b(I_com2), .eq(R6_com2));  // open: gt, lt
  Comparator #(.Bits(4)) comparator_22 (.a(R6[3:0]), .b(I_com1), .eq(R6_com1));  // open: gt, lt
  inst_comp inst_comp_11 (.A_id(R6[3:0]), .A_ep(R6[4]), .B_id(clr_id), .B_ep(clr_ep), .A_new(R6_cmp));
  Comparator #(.Bits(4)) comparator_23 (.a(R10[3:0]), .b(I_com2), .eq(R10_com2));  // open: gt, lt
  Comparator #(.Bits(4)) comparator_24 (.a(R10[3:0]), .b(I_com1), .eq(R10_com1));  // open: gt, lt
  inst_comp inst_comp_12 (.A_id(R10[3:0]), .A_ep(R10[4]), .B_id(clr_id), .B_ep(clr_ep), .A_new(R10_cmp));
  Comparator #(.Bits(4)) comparator_25 (.a(R14[3:0]), .b(I_com2), .eq(R14_com2));  // open: gt, lt
  Comparator #(.Bits(4)) comparator_26 (.a(R14[3:0]), .b(I_com1), .eq(R14_com1));  // open: gt, lt
  inst_comp inst_comp_13 (.A_id(R14[3:0]), .A_ep(R14[4]), .B_id(clr_id), .B_ep(clr_ep), .A_new(R14_cmp));
  Comparator #(.Bits(4)) comparator_27 (.a(R18[3:0]), .b(I_com2), .eq(R18_com2));  // open: gt, lt
  Comparator #(.Bits(4)) comparator_28 (.a(R18[3:0]), .b(I_com1), .eq(R18_com1));  // open: gt, lt
  inst_comp inst_comp_14 (.A_id(R18[3:0]), .A_ep(R18[4]), .B_id(clr_id), .B_ep(clr_ep), .A_new(R18_cmp));
  Comparator #(.Bits(4)) comparator_29 (.a(R22[3:0]), .b(I_com2), .eq(R22_com2));  // open: gt, lt
  Comparator #(.Bits(4)) comparator_30 (.a(R22[3:0]), .b(I_com1), .eq(R22_com1));  // open: gt, lt
  inst_comp inst_comp_15 (.A_id(R22[3:0]), .A_ep(R22[4]), .B_id(clr_id), .B_ep(clr_ep), .A_new(R22_cmp));
  Multiplexer #(.Bits(6)) multiplexer_32 (.sel(SC_sel), .in_0({1'b0, Inst}), .in_1(SC_inst), .out(multiplexer_32_out));
  and and_1 (and_1_out, ~SC_M, SC_sel);  // And
  Multiplexer #(.Bits(6)) multiplexer_33 (
    .sel(FL_FM), .in_0(6'b100000), .in_1({1'b0, clr_ep, clr_id}), .out(multiplexer_33_out));
  Comparator #(.Bits(5)) comparator_31 (.a({5{1'b1}}), .b(W), .eq(comparator_31_eq));  // open: gt, lt
  BitExtender #(.inputBits(1), .outputBits(32)) bitextender_1 (.in(com2), .out(bitextender_1_out));
  BitExtender #(.inputBits(1), .outputBits(32)) bitextender_2 (.in(com1), .out(bitextender_2_out));
  Multiplexer #(.Bits(6)) multiplexer_34 (
    .sel(SC_M), .in_0(multiplexer_32_out), .in_1(multiplexer_31_out), .out(multiplexer_34_out));
  Multiplexer #(.Bits(6)) multiplexer_35 (
    .sel(and_2_out), .in_0({1'b0, Inst}), .in_1(FL_inst), .out(multiplexer_35_out));
  assign not_1_out = ~{R1[5], R2[5], R3[5], R4[5], R5[5], R6[5], R7[5], R8[5], R9[5], R10[5], R11[5], R12[5], R13[5], R14[5], R15[5], R16[5], R17[5], R18[5], R19[5], R20[5], R21[5], R22[5], R23[5], R24[5], R25[5], SBP[5], 4'b1111, SC_O[4], FL_O[4]};  // Not not_1, 32 bits wide
  Multiplexer #(.Bits(6)) multiplexer_36 (
    .sel(R3_FM), .in_0(6'b100000), .in_1({1'b0, clr_ep, clr_id}), .out(multiplexer_36_out));
  Multiplexer #(.Bits(6)) multiplexer_37 (
    .sel(R7_FM), .in_0(6'b100000), .in_1({1'b0, clr_ep, clr_id}), .out(multiplexer_37_out));
  Multiplexer #(.Bits(6)) multiplexer_38 (
    .sel(R11_FM), .in_0(6'b100000), .in_1({1'b0, clr_ep, clr_id}), .out(multiplexer_38_out));
  Multiplexer #(.Bits(6)) multiplexer_39 (
    .sel(R15_FM), .in_0(6'b100000), .in_1({1'b0, clr_ep, clr_id}), .out(multiplexer_39_out));
  Multiplexer #(.Bits(6)) multiplexer_40 (
    .sel(R19_FM), .in_0(6'b100000), .in_1({1'b0, clr_ep, clr_id}), .out(multiplexer_40_out));
  Multiplexer #(.Bits(6)) multiplexer_41 (
    .sel(R23_FM), .in_0(6'b100000), .in_1({1'b0, clr_ep, clr_id}), .out(multiplexer_41_out));
  Multiplexer multiplexer_42 (.sel(and_1_out), .in_0(SC_e_t), .in_1(SC_e), .out(multiplexer_42_out));
  Multiplexer #(.Bits(6)) multiplexer_43 (
    .sel(FL_M), .in_0(multiplexer_35_out), .in_1(multiplexer_33_out), .out(multiplexer_43_out));
  and and_2 (and_2_out, ~comparator_31_eq, FL_sel);  // And
  and and_3 (and_3_out, ~comparator_31_eq, ~FL_M, FL_sel);  // And
  assign and_4_out = not_1_out & bitextender_1_out & {R1_com2, R2_com2, R3_com2, R4_com2, R5_com2, R6_com2, R7_com2, R8_com2, R9_com2, R10_com2, R11_com2, R12_com2, R13_com2, R14_com2, R15_com2, R16_com2, R17_com2, R18_com2, R19_com2, R20_com2, R21_com2, R22_com2, R23_com2, R24_com2, R25_com2, SBP_com2, 4'b0000, SC_com2, FL_com2};  // And and_4, 32 bits wide
  assign and_5_out = not_1_out & bitextender_2_out & {R1_com1, R2_com1, R3_com1, R4_com1, R5_com1, R6_com1, R7_com1, R8_com1, R9_com1, R10_com1, R11_com1, R12_com1, R13_com1, R14_com1, R15_com1, R16_com1, R17_com1, R18_com1, R19_com1, R20_com1, R21_com1, R22_com1, R23_com1, R24_com1, R25_com1, SBP_com1, 4'b0000, SC_com1, FL_com1};  // And and_5, 32 bits wide
  Multiplexer #(.Bits(6)) multiplexer_44 (
    .sel(R3_M), .in_0({1'b0, Inst}), .in_1(multiplexer_36_out), .out(multiplexer_44_out));
  Multiplexer #(.Bits(6)) multiplexer_45 (
    .sel(R7_M), .in_0({1'b0, Inst}), .in_1(multiplexer_37_out), .out(multiplexer_45_out));
  Multiplexer #(.Bits(6)) multiplexer_46 (
    .sel(R11_M), .in_0({1'b0, Inst}), .in_1(multiplexer_38_out), .out(multiplexer_46_out));
  Multiplexer #(.Bits(6)) multiplexer_47 (
    .sel(R15_M), .in_0({1'b0, Inst}), .in_1(multiplexer_39_out), .out(multiplexer_47_out));
  Multiplexer #(.Bits(6)) multiplexer_48 (
    .sel(R19_M), .in_0({1'b0, Inst}), .in_1(multiplexer_40_out), .out(multiplexer_48_out));
  Multiplexer #(.Bits(6)) multiplexer_49 (
    .sel(R23_M), .in_0({1'b0, Inst}), .in_1(multiplexer_41_out), .out(multiplexer_49_out));
  Multiplexer multiplexer_50 (.sel(and_3_out), .in_0(FL_e_t), .in_1(FL_e), .out(multiplexer_50_out));
  not not_2 (not_2_out, BLK_O[4]);
  Register #(.Bits(6)) u_R3 (.D(multiplexer_44_out), .C(C), .en(R3_e), .Q(R3));
  Register #(.Bits(6)) u_R7 (.D(multiplexer_45_out), .C(C), .en(R7_e), .Q(R7));
  Register #(.Bits(6)) u_R11 (.D(multiplexer_46_out), .C(C), .en(R11_e), .Q(R11));
  Register #(.Bits(6)) u_R15 (.D(multiplexer_47_out), .C(C), .en(R15_e), .Q(R15));
  Register #(.Bits(6)) u_R19 (.D(multiplexer_48_out), .C(C), .en(R19_e), .Q(R19));
  Register #(.Bits(6)) u_R23 (.D(multiplexer_49_out), .C(C), .en(R23_e), .Q(R23));
  Register #(.Bits(6)) u_SC (.D(multiplexer_34_out), .C(C), .en(multiplexer_42_out), .Q({SC_O[4], SC[4], SC_O[3:0]}));
  Register #(.Bits(6)) u_FL (.D(multiplexer_43_out), .C(C), .en(multiplexer_50_out), .Q({FL_O[4], FL[4], FL_O[3:0]}));
  and and_6 (and_6_out, not_2_out, com2, BLK_com2);
  and and_7 (and_7_out, not_2_out, com1, BLK_com1);
  BitExtender #(.inputBits(1), .outputBits(32)) bitextender_3 (.in(res), .out(bitextender_3_out));
  BitExtender #(.inputBits(1), .outputBits(32)) bitextender_4 (.in(clr), .out(bitextender_4_out));
  Comparator #(.Bits(4)) comparator_32 (.a(R3[3:0]), .b(I_com2), .eq(R3_com2));  // open: gt, lt
  Comparator #(.Bits(4)) comparator_33 (.a(R3[3:0]), .b(I_com1), .eq(R3_com1));  // open: gt, lt
  inst_comp inst_comp_16 (.A_id(R3[3:0]), .A_ep(R3[4]), .B_id(clr_id), .B_ep(clr_ep), .A_new(R3_cmp));
  Comparator #(.Bits(4)) comparator_34 (.a(R7[3:0]), .b(I_com2), .eq(R7_com2));  // open: gt, lt
  Comparator #(.Bits(4)) comparator_35 (.a(R7[3:0]), .b(I_com1), .eq(R7_com1));  // open: gt, lt
  inst_comp inst_comp_17 (.A_id(R7[3:0]), .A_ep(R7[4]), .B_id(clr_id), .B_ep(clr_ep), .A_new(R7_cmp));
  Comparator #(.Bits(4)) comparator_36 (.a(R11[3:0]), .b(I_com2), .eq(R11_com2));  // open: gt, lt
  Comparator #(.Bits(4)) comparator_37 (.a(R11[3:0]), .b(I_com1), .eq(R11_com1));  // open: gt, lt
  inst_comp inst_comp_18 (.A_id(R11[3:0]), .A_ep(R11[4]), .B_id(clr_id), .B_ep(clr_ep), .A_new(R11_cmp));
  Comparator #(.Bits(4)) comparator_38 (.a(R15[3:0]), .b(I_com2), .eq(R15_com2));  // open: gt, lt
  Comparator #(.Bits(4)) comparator_39 (.a(R15[3:0]), .b(I_com1), .eq(R15_com1));  // open: gt, lt
  inst_comp inst_comp_19 (.A_id(R15[3:0]), .A_ep(R15[4]), .B_id(clr_id), .B_ep(clr_ep), .A_new(R15_cmp));
  Comparator #(.Bits(4)) comparator_40 (.a(R19[3:0]), .b(I_com2), .eq(R19_com2));  // open: gt, lt
  Comparator #(.Bits(4)) comparator_41 (.a(R19[3:0]), .b(I_com1), .eq(R19_com1));  // open: gt, lt
  inst_comp inst_comp_20 (.A_id(R19[3:0]), .A_ep(R19[4]), .B_id(clr_id), .B_ep(clr_ep), .A_new(R19_cmp));
  Comparator #(.Bits(4)) comparator_42 (.a(R23[3:0]), .b(I_com2), .eq(R23_com2));  // open: gt, lt
  Comparator #(.Bits(4)) comparator_43 (.a(R23[3:0]), .b(I_com1), .eq(R23_com1));  // open: gt, lt
  inst_comp inst_comp_21 (.A_id(R23[3:0]), .A_ep(R23[4]), .B_id(clr_id), .B_ep(clr_ep), .A_new(R23_cmp));
  Comparator #(.Bits(4)) comparator_44 (.a(SC_O[3:0]), .b(I_com2), .eq(SC_com2));  // open: gt, lt
  Comparator #(.Bits(4)) comparator_45 (.a(SC_O[3:0]), .b(I_com1), .eq(SC_com1));  // open: gt, lt
  inst_comp inst_comp_22 (.A_id(SC_O[3:0]), .A_ep(SC[4]), .B_id(clr_id), .B_ep(clr_ep), .A_new(SC_cmp));
  Comparator #(.Bits(4)) comparator_46 (.a(FL_O[3:0]), .b(I_com2), .eq(FL_com2));  // open: gt, lt
  Comparator #(.Bits(4)) comparator_47 (.a(FL_O[3:0]), .b(I_com1), .eq(FL_com1));  // open: gt, lt
  inst_comp inst_comp_23 (.A_id(FL_O[3:0]), .A_ep(FL[4]), .B_id(clr_id), .B_ep(clr_ep), .A_new(FL_cmp));
  assign {R1_FM, R2_FM, R3_FM, R4_FM, R5_FM, R6_FM, R7_FM, R8_FM, R9_FM, R10_FM, R11_FM, R12_FM, R13_FM, R14_FM, R15_FM, R16_FM, R17_FM, R18_FM, R19_FM, R20_FM, R21_FM, R22_FM, R23_FM, R24_FM, R25_FM, SBP_FM, and_8_out, SC_FM, FL_FM} = bitextender_4_out & {R1_cmp, R2_cmp, R3_cmp, R4_cmp, R5_cmp, R6_cmp, R7_cmp, R8_cmp, R9_cmp, R10_cmp, R11_cmp, R12_cmp, R13_cmp, R14_cmp, R15_cmp, R16_cmp, R17_cmp, R18_cmp, R19_cmp, R20_cmp, R21_cmp, R22_cmp, R23_cmp, R24_cmp, R25_cmp, SBP_cmp, 4'b0000, SC_cmp, FL_cmp};  // And and_8, 32 bits wide
  or or_1 (or_1_out, and_6_out, and_7_out, res);
  not not_3 (not_3_out, OBLK);
  Multiplexer #(.Bits(6)) multiplexer_51 (
    .sel(R4_FM), .in_0(6'b100000), .in_1({1'b0, clr_ep, clr_id}), .out(multiplexer_51_out));
  Multiplexer #(.Bits(6)) multiplexer_52 (
    .sel(R8_FM), .in_0(6'b100000), .in_1({1'b0, clr_ep, clr_id}), .out(multiplexer_52_out));
  Multiplexer #(.Bits(6)) multiplexer_53 (
    .sel(R12_FM), .in_0(6'b100000), .in_1({1'b0, clr_ep, clr_id}), .out(multiplexer_53_out));
  Multiplexer #(.Bits(6)) multiplexer_54 (
    .sel(R16_FM), .in_0(6'b100000), .in_1({1'b0, clr_ep, clr_id}), .out(multiplexer_54_out));
  Multiplexer #(.Bits(6)) multiplexer_55 (
    .sel(R20_FM), .in_0(6'b100000), .in_1({1'b0, clr_ep, clr_id}), .out(multiplexer_55_out));
  Multiplexer #(.Bits(6)) multiplexer_56 (
    .sel(R24_FM), .in_0(6'b100000), .in_1({1'b0, clr_ep, clr_id}), .out(multiplexer_56_out));
  and and_9 (and_9_out, or_1_out, not_3_out);
  and and_10 (BLK_FM, clr, BLK_cmp);
  assign or_2_out = and_4_out | and_5_out | bitextender_3_out;  // Or or_2, 32 bits wide
  assign not_4_out = ~demultiplexer_1_out_0;  // Not not_4, 32 bits wide
  assign {R1_e, R2_e, R3_e, R4_e, R5_e, R6_e, R7_e, R8_e, R9_e, R10_e, R11_e, R12_e, R13_e, R14_e, R15_e, R16_e, R17_e, R18_e, R19_e, R20_e, R21_e, R22_e, R23_e, R24_e, R25_e, SBP_e, or_3_out, SC_e_t, FL_e_t} = and_4_out | and_5_out | demultiplexer_1_out_0 | bitextender_3_out | {R1_FM, R2_FM, R3_FM, R4_FM, R5_FM, R6_FM, R7_FM, R8_FM, R9_FM, R10_FM, R11_FM, R12_FM, R13_FM, R14_FM, R15_FM, R16_FM, R17_FM, R18_FM, R19_FM, R20_FM, R21_FM, R22_FM, R23_FM, R24_FM, R25_FM, SBP_FM, and_8_out, SC_FM, FL_FM};  // Or or_3, 32 bits wide
  Multiplexer #(.Bits(6)) multiplexer_57 (
    .sel(R4_M), .in_0({1'b0, Inst}), .in_1(multiplexer_51_out), .out(multiplexer_57_out));
  Multiplexer #(.Bits(6)) multiplexer_58 (
    .sel(R8_M), .in_0({1'b0, Inst}), .in_1(multiplexer_52_out), .out(multiplexer_58_out));
  Multiplexer #(.Bits(6)) multiplexer_59 (
    .sel(R12_M), .in_0({1'b0, Inst}), .in_1(multiplexer_53_out), .out(multiplexer_59_out));
  Multiplexer #(.Bits(6)) multiplexer_60 (
    .sel(R16_M), .in_0({1'b0, Inst}), .in_1(multiplexer_54_out), .out(multiplexer_60_out));
  Multiplexer #(.Bits(6)) multiplexer_61 (
    .sel(R20_M), .in_0({1'b0, Inst}), .in_1(multiplexer_55_out), .out(multiplexer_61_out));
  Multiplexer #(.Bits(6)) multiplexer_62 (
    .sel(R24_M), .in_0({1'b0, Inst}), .in_1(multiplexer_56_out), .out(multiplexer_62_out));
  assign and_11_out = or_2_out & not_4_out;  // And and_11, 32 bits wide
  Register #(.Bits(6)) u_R4 (.D(multiplexer_57_out), .C(C), .en(R4_e), .Q(R4));
  Register #(.Bits(6)) u_R8 (.D(multiplexer_58_out), .C(C), .en(R8_e), .Q(R8));
  Register #(.Bits(6)) u_R12 (.D(multiplexer_59_out), .C(C), .en(R12_e), .Q(R12));
  Register #(.Bits(6)) u_R16 (.D(multiplexer_60_out), .C(C), .en(R16_e), .Q(R16));
  Register #(.Bits(6)) u_R20 (.D(multiplexer_61_out), .C(C), .en(R20_e), .Q(R20));
  Register #(.Bits(6)) u_R24 (.D(multiplexer_62_out), .C(C), .en(R24_e), .Q(R24));
  or or_4 (BLK_M, and_9_out, BLK_FM);
  or or_5 (BLK_e, and_6_out, and_7_out, OBLK, res, BLK_FM);
  assign {R1_M, R2_M, R3_M, R4_M, R5_M, R6_M, R7_M, R8_M, R9_M, R10_M, R11_M, R12_M, R13_M, R14_M, R15_M, R16_M, R17_M, R18_M, R19_M, R20_M, R21_M, R22_M, R23_M, R24_M, R25_M, SBP_M, or_6_out, SC_M, FL_M} = {R1_FM, R2_FM, R3_FM, R4_FM, R5_FM, R6_FM, R7_FM, R8_FM, R9_FM, R10_FM, R11_FM, R12_FM, R13_FM, R14_FM, R15_FM, R16_FM, R17_FM, R18_FM, R19_FM, R20_FM, R21_FM, R22_FM, R23_FM, R24_FM, R25_FM, SBP_FM, and_8_out, SC_FM, FL_FM} | and_11_out;  // Or or_6, 32 bits wide
  Comparator #(.Bits(4)) comparator_48 (.a(R4[3:0]), .b(I_com2), .eq(R4_com2));  // open: gt, lt
  Comparator #(.Bits(4)) comparator_49 (.a(R4[3:0]), .b(I_com1), .eq(R4_com1));  // open: gt, lt
  inst_comp inst_comp_24 (.A_id(R4[3:0]), .A_ep(R4[4]), .B_id(clr_id), .B_ep(clr_ep), .A_new(R4_cmp));
  Comparator #(.Bits(4)) comparator_50 (.a(R8[3:0]), .b(I_com2), .eq(R8_com2));  // open: gt, lt
  Comparator #(.Bits(4)) comparator_51 (.a(R8[3:0]), .b(I_com1), .eq(R8_com1));  // open: gt, lt
  inst_comp inst_comp_25 (.A_id(R8[3:0]), .A_ep(R8[4]), .B_id(clr_id), .B_ep(clr_ep), .A_new(R8_cmp));
  Comparator #(.Bits(4)) comparator_52 (.a(R12[3:0]), .b(I_com2), .eq(R12_com2));  // open: gt, lt
  Comparator #(.Bits(4)) comparator_53 (.a(R12[3:0]), .b(I_com1), .eq(R12_com1));  // open: gt, lt
  inst_comp inst_comp_26 (.A_id(R12[3:0]), .A_ep(R12[4]), .B_id(clr_id), .B_ep(clr_ep), .A_new(R12_cmp));
  Comparator #(.Bits(4)) comparator_54 (.a(R16[3:0]), .b(I_com2), .eq(R16_com2));  // open: gt, lt
  Comparator #(.Bits(4)) comparator_55 (.a(R16[3:0]), .b(I_com1), .eq(R16_com1));  // open: gt, lt
  inst_comp inst_comp_27 (.A_id(R16[3:0]), .A_ep(R16[4]), .B_id(clr_id), .B_ep(clr_ep), .A_new(R16_cmp));
  Comparator #(.Bits(4)) comparator_56 (.a(R20[3:0]), .b(I_com2), .eq(R20_com2));  // open: gt, lt
  Comparator #(.Bits(4)) comparator_57 (.a(R20[3:0]), .b(I_com1), .eq(R20_com1));  // open: gt, lt
  inst_comp inst_comp_28 (.A_id(R20[3:0]), .A_ep(R20[4]), .B_id(clr_id), .B_ep(clr_ep), .A_new(R20_cmp));
  Comparator #(.Bits(4)) comparator_58 (.a(R24[3:0]), .b(I_com2), .eq(R24_com2));  // open: gt, lt
  Comparator #(.Bits(4)) comparator_59 (.a(R24[3:0]), .b(I_com1), .eq(R24_com1));  // open: gt, lt
  inst_comp inst_comp_29 (.A_id(R24[3:0]), .A_ep(R24[4]), .B_id(clr_id), .B_ep(clr_ep), .A_new(R24_cmp));
  Multiplexer #(.Selector_Bits(5), .Bits(6)) multiplexer_63 (
    .sel(RA), .in_0(R1), .in_1(R2), .in_2(R3), .in_3(R4), .in_4(R5), .in_5(R6), .in_6(R7), .in_7(R8),
    .in_8(R9), .in_9(R10), .in_10(R11), .in_11(R12), .in_12(R13), .in_13(R14), .in_14(R15), .in_15(R16),
    .in_16(R17), .in_17(R18), .in_18(R19), .in_19(R20), .in_20(R21), .in_21(R22), .in_22(R23), .in_23(R24),
    .in_24(R25), .in_25(SBP), .in_26(6'b100000), .in_27(6'b100000), .in_28(6'b100000), .in_29(6'b100000),
    .in_30({SC_O[4], SC[4], SC_O[3:0]}), .in_31({FL_O[4], FL[4], FL_O[3:0]}),
    .out({R_A[4], R_A_t[4], R_A[3:0]}));
  Multiplexer #(.Selector_Bits(5), .Bits(6)) multiplexer_64 (
    .sel(RB), .in_0(R1), .in_1(R2), .in_2(R3), .in_3(R4), .in_4(R5), .in_5(R6), .in_6(R7), .in_7(R8),
    .in_8(R9), .in_9(R10), .in_10(R11), .in_11(R12), .in_12(R13), .in_13(R14), .in_14(R15), .in_15(R16),
    .in_16(R17), .in_17(R18), .in_18(R19), .in_19(R20), .in_20(R21), .in_21(R22), .in_22(R23), .in_23(R24),
    .in_24(R25), .in_25(SBP), .in_26(6'b100000), .in_27(6'b100000), .in_28(6'b100000), .in_29(6'b100000),
    .in_30({SC_O[4], SC[4], SC_O[3:0]}), .in_31({FL_O[4], FL[4], FL_O[3:0]}),
    .out({R_B[4], R_B_t[4], R_B[3:0]}));
  // Probe R1 on R1
  // Probe R2 on R2
  // Probe R3 on R3
  // Probe R4 on R4
  // Probe R5 on R5
  // Probe R6 on R6
  // Probe R7 on R7
  // Probe R8 on R8
  // Probe R9 on R9
  // Probe R10 on R10
  // Probe R11 on R11
  // Probe R12 on R12
  // Probe R13 on R13
  // Probe R14 on R14
  // Probe R15 on R15
  // Probe R16 on R16
  // Probe R17 on R17
  // Probe R18 on R18
  // Probe R19 on R19
  // Probe R20 on R20
  // Probe R21 on R21
  // Probe R22 on R22
  // Probe R23 on R23
  // Probe R24 on R24
  // Probe R25 on R25
  // Probe R26 on SBP
  // Probe R27 on 6'b100000
  // Probe R28 on 6'b100000
  // Probe R29 on 6'b100000
  // Probe R30 on 6'b100000
  // Probe R31 on {SC_O[4], SC[4], SC_O[3:0]}
  // Probe R32 on {FL_O[4], FL[4], FL_O[3:0]}

  // Other names for the same wires on the sheet: BLK (some bits) = BLK_O; clear = clr;
  //   rcom_id[4:0] = {clr_ep, clr_id}; E = E1; FL (some bits) = FL_O; FL_e__EX = FL_e; FL_i[5:0] = FL_inst;
  //   D_in[4:0] = Inst; inst_com1[3:0] = I_com1; inst_com2[3:0] = I_com2; R_A_t (some bits) = R_A;
  //   R_B_t (some bits) = R_B; RA_sel[4:0] = RA; RB_sel[4:0] = RB; reset = res; RW_sel[4:0] = W;
  //   SC (some bits) = SC_O; SC_e__EX = SC_e; SC_i[5:0] = SC_inst

  // Notes on the sheet:
  //   SC_inst: data input for SC
  //   FL_inst: data input for FL
  //   SC_sel: enable SC extern mode
  //   FL_sel: enable FL extern mode
  //   SC_e: SC register enable
  //   FL_e: FL register enable
  //   Inst: data in
  //   W: register to write:
  //   0~25: general
  //   26: zero
  //   27: one
  //   28: full
  //   29: program counter
  //   30: stack counter
  //   31: flag
  //   RA: register to read:
  //   0~25: general
  //   26: zero
  //   27: one
  //   28: full
  //   29: program counter
  //   30: stack counter
  //   31: flag
  //   RB: register to read:
  //   0~25: general
  //   26: zero
  //   27: one
  //   28: full
  //   29: program counter
  //   30: stack counter
  //   31: flag
  //   R_A: register out a
  //   R_B: register out b
  //   SC_O: SC out
  //   FL_O: FL out
  //   E1: enable
  //   com1: enable
  //   com2: enable
  //   I_com1: enable
  //   I_com2: enable
  //   res: reset
  //   OBLK: BLK register enable
  //   BLK_O: BLK out
endmodule
