// Digital circuit mux1x4.dig as structural Verilog
module mux1x4 (
  input  [3:0] A,
  input  [3:0] S,
  input  [3:0] B,
  output [3:0] out
);

  Multiplexer multiplexer_1 (.sel(S[3]), .in_0(A[3]), .in_1(B[3]), .out(out[3]));
  Multiplexer multiplexer_2 (.sel(S[2]), .in_0(A[2]), .in_1(B[2]), .out(out[2]));
  Multiplexer multiplexer_3 (.sel(S[1]), .in_0(A[1]), .in_1(B[1]), .out(out[1]));
  Multiplexer multiplexer_4 (.sel(S[0]), .in_0(A[0]), .in_1(B[0]), .out(out[0]));
endmodule
