// Digital circuit reg8x4-ready.dig as structural Verilog
module reg8x4_ready (
  input  [31:0] D_i,
  input  C,
  input  [3:0] E,
  input  [3:0] D,
  output [31:0] D_o,
  output [3:0] R
);

  wire DE1, DE2, DE3, DE4;

  assign {DE4, DE3, DE2, DE1} = ~E & D;  // And and_1, 4 bits wide
  Register #(.Bits(8)) R1 (.D(D_i[7:0]), .C(C), .en(E[0]), .Q(D_o[7:0]));
  Register #(.Bits(8)) R2 (.D(D_i[15:8]), .C(C), .en(E[1]), .Q(D_o[15:8]));
  Register #(.Bits(8)) R3 (.D(D_i[23:16]), .C(C), .en(E[2]), .Q(D_o[23:16]));
  Register #(.Bits(8)) R4 (.D(D_i[31:24]), .C(C), .en(E[3]), .Q(D_o[31:24]));
  RS_FF RD1 (.S(E[0]), .C(C), .R(DE1), .Q(R[0]));  // open: nQ
  RS_FF RD2 (.S(E[1]), .C(C), .R(DE2), .Q(R[1]));  // open: nQ
  RS_FF RD3 (.S(E[2]), .C(C), .R(DE3), .Q(R[2]));  // open: nQ
  RS_FF RD4 (.S(E[3]), .C(C), .R(DE4), .Q(R[3]));  // open: nQ

  // Other names for the same wires on the sheet: D1_i[7:0] = D_i[7:0]; D2_i[7:0] = D_i[15:8]; D3_i[7:0] = D_i[23:16];
  //   D4_i[7:0] = D_i[31:24]; E1 = E[0]; E2 = E[1]; E3 = E[2]; E4 = E[3]; R1[7:0] = D_o[7:0]; R2[7:0] = D_o[15:8];
  //   R3[7:0] = D_o[23:16]; R4[7:0] = D_o[31:24]; RD1 = R[0]; RD2 = R[1]; RD3 = R[2]; RD4 = R[3]

  // Notes on the sheet:
  //   D_i: data in
  //   E: enable
  //   D_o: data out
  //   D: disable
  //   R: ready
endmodule
