// Digital circuit rename test.dig as structural Verilog
module rename_test (
  input  C,
  input  [7:0] R_commit,
  input  push,
  input  pop,
  input  [7:0] R_arch,
  input  st,
  input  comm,
  input  [7:0] RA,
  input  [7:0] RB
);

  wire free_list_1_empty, free_list_1_full;
  wire [7:0] free_list_1_out;

  free_list free_list_1 (
    .C(C), .D(R_commit), .push(comm), .pop(st), .out(free_list_1_out), .empty(free_list_1_empty),
    .full(free_list_1_full));
  RegisterFile #(.AddrBits(8), .Bits(8)) registerfile_1 (
    .Din(free_list_1_out), .we(st), .Rw(R_arch), .C(C), .Ra(RA), .Rb(RB));  // open: Da, Db

  // Other names for the same wires on the sheet: commit = comm
endmodule
