// Digital circuit trap-ref-old.dig as structural Verilog
module trap_ref_old (
);

  wire and_1_out, and_2_out, and_3_out, and_4_out, C_ct, C_dt, clr, clr_ep, com1, com2, comparator_1_eq,
       comparator_2_eq, CT_FU__EPOCH, CT_INT, CT_RF__PCH, CT_RF__PCJ, CT_RF__PCSE, CT_TRAP__LD, d_ff_2_nq,
       dipswitch_1_out, Fl_TRAP, Fl_TRAP__EP, or_1_out, rs_ff_1_q, TRAP_CLR, TRAP_IRD, TRAP_VI, \wait ;
  wire [3:0] clr_id, com1_inst, com2_inst, CT_FU__INST, Fl_TRAP__INST;
  wire [15:0] INT_inst, V1_inst, V2_inst;
  wire [31:0] HALT_PC, pc_read, register_4_q;

  Comparator #(.Bits(4)) comparator_1 (.a(Fl_TRAP__INST), .b(com1_inst), .eq(comparator_1_eq));  // open: gt, lt
  Comparator #(.Bits(4)) comparator_2 (.a(Fl_TRAP__INST), .b(com2_inst), .eq(comparator_2_eq));  // open: gt, lt
  Register #(.Bits(4)) register_1 (.D(CT_FU__INST), .C(C_ct), .en(CT_TRAP__LD), .Q(Fl_TRAP__INST));
  Register register_2 (.D(CT_FU__EPOCH), .C(C_ct), .en(CT_TRAP__LD), .Q(Fl_TRAP__EP));
  DipSwitch dipswitch_1 (.out(dipswitch_1_out));
  Register register_3 (.D(CT_INT), .C(C_ct), .en(CT_TRAP__LD), .Q(TRAP_IRD));
  and and_1 (and_1_out, com1, comparator_1_eq);
  and and_2 (and_2_out, com2, comparator_2_eq);
  or or_1 (or_1_out, and_1_out, and_2_out);
  inst_comp inst_comp_1 (.A_id(Fl_TRAP__INST), .A_ep(Fl_TRAP__EP), .B_id(clr_id), .B_ep(clr_ep), .A_new(TRAP_CLR));
  bus16x2_demux bus16x2_demux_1 (.bus_1(V1_inst), .bus_2(V2_inst), .E(TRAP_VI), .id(Fl_TRAP__INST));
  bus16_demux bus16_demux_1 (.bus(INT_inst), .E(dipswitch_1_out), .id(Fl_TRAP__INST));
  and and_3 (and_3_out, rs_ff_1_q, or_1_out);
  Register #(.Bits(32)) register_4 (.D(pc_read), .C(C_dt), .en(CT_TRAP__LD), .Q(register_4_q));
  and and_4 (and_4_out, TRAP_CLR, clr, ~CT_TRAP__LD);  // And
  assign \wait  = and_3_out ? 1'b1 : 1'bz;  // Driver driver_1
  assign CT_RF__PCH = and_3_out ? 1'b1 : 1'bz;  // Driver driver_2
  D_FF #(.Bits(32)) d_ff_1 (.D(register_4_q), .C(C_ct), .Q(HALT_PC));  // open: nQ
  RS_FF rs_ff_1 (.S(CT_TRAP__LD), .C(C_ct), .R(and_4_out), .Q(rs_ff_1_q));  // open: nQ
  D_FF d_ff_2 (.D(rs_ff_1_q), .C(C_ct), .nQ(d_ff_2_nq));  // open: Q
  assign CT_RF__PCSE = and_3_out ? 1'b1 : 1'bz;  // Driver driver_3
  assign CT_RF__PCJ = and_3_out ? 1'b1 : 1'bz;  // Driver driver_4
  and and_5 (Fl_TRAP, rs_ff_1_q, d_ff_2_nq);

  // Other names for the same wires on the sheet: TRAP_EP = Fl_TRAP__EP; TRAP_INST[3:0] = Fl_TRAP__INST;
  //   TRAP_RUNP = Fl_TRAP

  // Notes on the sheet:
  //   dev 508f47c TRAP logic (cpu-32 test.dig), kept for reference after the forward-test rework.
  //   Fl_TRAP / Fl_TRAP-_INST / Fl_TRAP-_EP fed flush-mux T_v / T_id / T_ep (see flush-mux-old.dig),
  //   so a decoded trap (halt included) flushed the younger instructions.
endmodule
