// Digital circuit load-buffer.dig as structural Verilog
module load_buffer (
  input  C,
  input  [3:0] inst,
  input  [3:0] com1_id,
  input  [3:0] com2_id,
  input  com1,
  input  com2,
  input  st_ep,
  input  [3:0] st_id,
  input  epoch,
  input  [31:0] st_addr,
  input  W_id,
  input  [31:0] st_data,
  input  [3:0] inst_WD,
  input  [31:0] D,
  input  W_a,
  input  [3:0] inst_WA,
  input  [31:0] A,
  input  W_d,
  input  LDB,
  input  [1:0] MD,
  input  st,
  input  [7:0] WR,
  input  clr,
  input  [3:0] clr_id,
  input  clr_ep,
  input  MF,
  input  LD,
  input  [31:0] PC,
  output [31:0] D_O,
  output V,
  output full,
  output M_V,
  output [31:0] M_A,
  output fl,
  output [3:0] M_id,
  output M_ep,
  output [3:0] id_O,
  output [1:0] M_MD,
  output fl_ep,
  output [3:0] fl_id,
  output [7:0] WR_O,
  output MF_O,
  output [31:0] fl_PC
);

  wire and_1_out, and_2_out, and_4_out, and_9_out, and_10_out, and_11_out, and_12_out, and_21_out,
       and_22_out, and_23_out, and_27_out, and_28_out, and_30_out, and_34_out, and_35_out, and_37_out,
       and_40_out, and_41_out, and_44_out, and_47_out, and_48_out, comparator_1_eq, comparator_2_eq,
       comparator_3_eq, comparator_4_eq, comparator_5_eq, comparator_6_eq, comparator_7_eq, comparator_8_eq,
       comparator_9_eq, comparator_10_eq, comparator_11_eq, comparator_12_eq, comparator_13_eq,
       comparator_14_eq, comparator_15_eq, comparator_16_eq, comparator_17_eq, comparator_18_eq,
       comparator_19_eq, comparator_20_eq, d_ff_1_q, inst_comp_1_a_old, inst_comp_2_a_old, inst_comp_3_a_old,
       inst_comp_4_a_old, inst_comp_5_a_old, inst_comp_6_a_old, inst_comp_7_a_old, inst_comp_8_a_old, M1_AE,
       M1_AV, M1_CLR, M1_CMP, M1_DE, M1_DM, M1_DV, M1_epoch, M1_IE, M1_MF, M1_SEL__A, M1_SEL__D, M1_VO,
       M2_AE, M2_AV, M2_CLR, M2_CMP, M2_DE, M2_DM, M2_DV, M2_epoch, M2_IE, M2_MF, M2_SEL__A, M2_SEL__D,
       M2_VO, M3_AE, M3_AV, M3_CLR, M3_CMP, M3_DE, M3_DM, M3_DV, M3_epoch, M3_IE, M3_MF, M3_SEL__A,
       M3_SEL__D, M3_VO, M4_AE, M4_AV, M4_CLR, M4_CMP, M4_DE, M4_DM, M4_DV, M4_epoch, M4_IE, M4_MF,
       M4_SEL__A, M4_SEL__D, M4_VO, or_1_out, or_2_out, or_3_out, or_4_out, or_11_out, or_12_out, or_13_out,
       or_14_out, priorityencoder_1_any, priorityencoder_4_any, recon;
  wire [1:0] d_ff_2_q, d_ff_3_q, empty_id, flush_sel, M1_MD, M2_MD, M3_MD, M4_MD, multiplexer_7_out,
       priorityencoder_3_num, priorityencoder_4_num, register_2_q, register_4_q, register_5_q, register_6_q,
       register_9_q, register_10_q, register_14_q, register_16_q, sel_A, sel_D;
  wire [3:0] and_3_out, and_5_out, and_8_out, and_13_out, and_14_out, and_15_out, and_16_out, and_17_out,
       and_18_out, and_19_out, and_20_out, bitextender_1_out, bitextender_2_out, bitextender_3_out,
       bitextender_4_out, bitextender_5_out, bitextender_6_out, bitextender_7_out, bitselector_1_out,
       bitselector_2_out, bitselector_3_out, bitselector_4_out, fill_4_1_out1, fill_4_2_out1, M1_inst,
       M2_inst, M3_inst, M4_inst, mux1x4_1_out, mux1x4_2_out, not_1_out, not_2_out, not_3_out, not_5_out,
       not_6_out, or_5_out, or_6_out, or_8_out, or_9_out, priority_4_1_out1, priority_4_2_out1, register_1_q,
       register_3_q;
  wire [7:0] M1_WR, M2_WR, M3_WR, M4_WR;
  wire [31:0] M1_A, M1_D, M1_PC, M2_A, M2_D, M2_PC, M3_A, M3_D, M3_PC, M4_A, M4_D, M4_PC, multiplexer_15_out,
       multiplexer_16_out, multiplexer_17_out, multiplexer_18_out;

  fill_4 fill_4_1 (
    .on(1'b0), .in1(not_1_out[0]), .in2(not_1_out[1]), .in3(not_1_out[2]), .in4(not_1_out[3]),
    .out1(fill_4_1_out1[3]), .out2(fill_4_1_out1[2]), .out3(fill_4_1_out1[1]), .out4(fill_4_1_out1[0]));  // open: v
  fill_4 fill_4_2 (
    .on(1'b0), .in1(not_2_out[0]), .in2(not_2_out[1]), .in3(not_2_out[2]), .in4(not_2_out[3]),
    .out1(fill_4_2_out1[3]), .out2(fill_4_2_out1[2]), .out3(fill_4_2_out1[1]), .out4(fill_4_2_out1[0]));  // open: v
  and and_1 (and_1_out, LDB, ~recon);  // And
  assign not_1_out = ~register_1_q;  // Not not_1, 4 bits wide
  or or_1 (or_1_out, M4_CLR, M3_CLR, M2_CLR, M1_CLR);
  assign not_2_out = ~register_3_q;  // Not not_2, 4 bits wide
  or or_2 (or_2_out, M4_CLR, M3_CLR, M2_CLR, M1_CLR);
  Multiplexer #(.Selector_Bits(2), .Bits(8)) multiplexer_1 (
    .sel(sel_D), .in_0(M1_WR), .in_1(M2_WR), .in_2(M3_WR), .in_3(M4_WR), .out(WR_O));
  Multiplexer #(.Selector_Bits(2), .Bits(32)) multiplexer_2 (
    .sel(sel_A), .in_0(M1_A), .in_1(M2_A), .in_2(M3_A), .in_3(M4_A), .out(M_A));
  or or_3 (or_3_out, LD, or_1_out);
  priority_4 priority_4_1 (
    .on(LD), .in1(and_16_out[0]), .in2(and_16_out[1]), .in3(and_16_out[2]), .in4(and_16_out[3]),
    .out1(priority_4_1_out1[3]), .out2(priority_4_1_out1[2]), .out3(priority_4_1_out1[1]),
    .out4(priority_4_1_out1[0]));  // open: v
  and and_2 (and_2_out, not_5_out[3], W_id);
  assign and_3_out = ~{M4_CLR, M3_CLR, M2_CLR, M1_CLR} & {M4_AV, M3_AV, M2_AV, M1_AV};  // And and_3, 4 bits wide
  or or_4 (or_4_out, and_1_out, or_2_out);
  priority_4 priority_4_2 (
    .on(and_1_out), .in1(and_20_out[0]), .in2(and_20_out[1]), .in3(and_20_out[2]), .in4(and_20_out[3]),
    .out1(priority_4_2_out1[3]), .out2(priority_4_2_out1[2]), .out3(priority_4_2_out1[1]),
    .out4(priority_4_2_out1[0]));  // open: v
  and and_4 (and_4_out, not_6_out[3], W_id);
  assign and_5_out = ~{M4_CLR, M3_CLR, M2_CLR, M1_CLR} & {M4_DV, M3_DV, M2_DV, M1_DV};  // And and_5, 4 bits wide
  // Probe MR-1 on M1_WR
  // Probe MR-2 on M2_WR
  // Probe MR-3 on M3_WR
  // Probe MR-4 on M4_WR
  // Probe MV-1 on M1_VO
  // Probe MV-2 on M2_VO
  // Probe MV-3 on M3_VO
  // Probe MV-4 on M4_VO
  // Probe MAV-1 on M1_AV
  // Probe MAV-2 on M2_AV
  // Probe MAV-3 on M3_AV
  // Probe MAV-4 on M4_AV
  // Probe MDV-1 on M1_DV
  // Probe MDV-2 on M2_DV
  // Probe MDV-3 on M3_DV
  // Probe MDV-4 on M4_DV
  // Probe MID-1 on M1_inst
  // Probe MID-2 on M2_inst
  // Probe MID-3 on M3_inst
  // Probe MID-4 on M4_inst
  BitExtender #(.inputBits(1), .outputBits(4)) bitextender_1 (.in(st), .out(bitextender_1_out));
  assign not_3_out = ~{M4_VO, M3_VO, M2_VO, M1_VO};  // Not not_3, 4 bits wide
  BitExtender #(.inputBits(1), .outputBits(4)) bitextender_2 (.in(W_a), .out(bitextender_2_out));
  BitExtender #(.inputBits(1), .outputBits(4)) bitextender_3 (.in(W_d), .out(bitextender_3_out));
  Register register_1 (.D(and_2_out), .C(C), .en(or_8_out[3]), .Q(register_1_q[0]));
  BitSelector #(.Selector_Bits(2)) bitselector_1 (.in(and_3_out), .sel(register_2_q), .out(bitselector_1_out[0]));
  Register #(.Bits(2)) register_2 (.D(empty_id), .C(C), .en(W_id), .Q(register_2_q));
  BitSelector #(.Selector_Bits(2)) bitselector_2 (
    .in({M4_CLR, M3_CLR, M2_CLR, M1_CLR}), .sel(register_2_q), .out(bitselector_2_out[3]));
  Register register_3 (.D(and_4_out), .C(C), .en(or_9_out[3]), .Q(register_3_q[0]));
  BitSelector #(.Selector_Bits(2)) bitselector_3 (.in(and_5_out), .sel(register_4_q), .out(bitselector_3_out[0]));
  Register #(.Bits(2)) register_4 (.D(empty_id), .C(C), .en(W_id), .Q(register_4_q));
  BitSelector #(.Selector_Bits(2)) bitselector_4 (
    .in({M4_CLR, M3_CLR, M2_CLR, M1_CLR}), .sel(register_4_q), .out(bitselector_4_out[3]));
  assign {M4_DM, M3_DM, M2_DM, M1_DM} = {M4_CMP, M3_CMP, M2_CMP, M1_CMP} & bitextender_1_out & bitextender_1_out;  // And and_6, 4 bits wide
  PriorityEncoder #(.Selector_Bits(2)) priorityencoder_1 (
    .in0(not_3_out[0]), .in1(not_3_out[1]), .in2(not_3_out[2]), .in3(not_3_out[3]), .num(empty_id),
    .any(priorityencoder_1_any));
  assign {M4_AE, M3_AE, M2_AE, M1_AE} = {M4_SEL__A, M3_SEL__A, M2_SEL__A, M1_SEL__A} & bitextender_2_out;  // And and_7, 4 bits wide
  assign and_8_out = {M4_SEL__D, M3_SEL__D, M2_SEL__D, M1_SEL__D} & ~{M4_DV, M3_DV, M2_DV, M1_DV} & bitextender_3_out;  // And and_8, 4 bits wide
  assign or_5_out = priority_4_1_out1 | bitselector_2_out;  // Or or_5, 4 bits wide
  and and_9 (and_9_out, not_5_out[2], register_1_q[0]);
  Register #(.Bits(2)) register_5 (.D(register_2_q), .C(C), .en(W_id), .Q(register_5_q));
  assign or_6_out = priority_4_2_out1 | bitselector_4_out;  // Or or_6, 4 bits wide
  and and_10 (and_10_out, not_6_out[2], register_3_q[0]);
  Register #(.Bits(2)) register_6 (.D(register_4_q), .C(C), .en(W_id), .Q(register_6_q));
  not not_4 (full, priorityencoder_1_any);
  Multiplexer #(.Selector_Bits(2), .Bits(32)) multiplexer_3 (
    .sel(sel_D), .in_0(M1_D), .in_1(M2_D), .in_2(M3_D), .in_3(M4_D), .out(D_O));
  assign {M4_DE, M3_DE, M2_DE, M1_DE} = and_8_out | {M4_DM, M3_DM, M2_DM, M1_DM};  // Or or_7, 4 bits wide
  Multiplexer #(.Selector_Bits(2), .Bits(4)) multiplexer_4 (
    .sel(sel_A), .in_0(M1_inst), .in_1(M2_inst), .in_2(M3_inst), .in_3(M4_inst), .out(M_id));
  Register register_7 (.D(and_9_out), .C(C), .en(or_8_out[2]), .Q(register_1_q[1]));
  BitSelector #(.Selector_Bits(2)) bitselector_5 (.in(and_3_out), .sel(register_5_q), .out(bitselector_1_out[1]));
  BitSelector #(.Selector_Bits(2)) bitselector_6 (
    .in({M4_CLR, M3_CLR, M2_CLR, M1_CLR}), .sel(register_5_q), .out(bitselector_2_out[2]));
  Register register_8 (.D(and_10_out), .C(C), .en(or_9_out[2]), .Q(register_3_q[1]));
  BitSelector #(.Selector_Bits(2)) bitselector_7 (.in(and_5_out), .sel(register_6_q), .out(bitselector_3_out[1]));
  BitSelector #(.Selector_Bits(2)) bitselector_8 (
    .in({M4_CLR, M3_CLR, M2_CLR, M1_CLR}), .sel(register_6_q), .out(bitselector_4_out[2]));
  D_FF d_ff_1 (.D(fl), .C(C), .Q(d_ff_1_q));  // open: nQ
  RS_FF rs_ff_1 (.S(d_ff_1_q), .C(C), .R(LDB), .Q(recon));  // open: nQ
  PriorityEncoder #(.Selector_Bits(2)) priorityencoder_2 (
    .in0(M1_DM), .in1(M2_DM), .in2(M3_DM), .in3(M4_DM), .num(flush_sel), .any(fl));
  mux1x4 mux1x4_1 (.A(or_5_out), .B({1'b0, or_5_out[3:1]}), .S(or_8_out), .out(mux1x4_1_out));
  BitExtender #(.inputBits(1), .outputBits(4)) bitextender_4 (.in(or_3_out), .out(bitextender_4_out));
  BitExtender #(.inputBits(1), .outputBits(4)) bitextender_5 (.in(W_id), .out(bitextender_5_out));
  and and_11 (and_11_out, not_5_out[1], register_1_q[1]);
  Register #(.Bits(2)) register_9 (.D(register_5_q), .C(C), .en(W_id), .Q(register_9_q));
  mux1x4 mux1x4_2 (.A(or_6_out), .B({1'b0, or_6_out[3:1]}), .S(or_9_out), .out(mux1x4_2_out));
  BitExtender #(.inputBits(1), .outputBits(4)) bitextender_6 (.in(or_4_out), .out(bitextender_6_out));
  BitExtender #(.inputBits(1), .outputBits(4)) bitextender_7 (.in(W_id), .out(bitextender_7_out));
  and and_12 (and_12_out, not_6_out[1], register_3_q[1]);
  Register #(.Bits(2)) register_10 (.D(register_6_q), .C(C), .en(W_id), .Q(register_10_q));
  assign and_13_out = mux1x4_1_out & bitextender_4_out;  // And and_13, 4 bits wide
  assign and_14_out = bitextender_4_out & or_5_out;  // And and_14, 4 bits wide
  assign and_15_out = bitextender_5_out & fill_4_1_out1;  // And and_15, 4 bits wide
  Register register_11 (.D(and_11_out), .C(C), .en(or_8_out[1]), .Q(register_1_q[2]));
  assign and_16_out = register_1_q & bitselector_1_out;  // And and_16, 4 bits wide
  BitSelector #(.Selector_Bits(2)) bitselector_9 (.in(and_3_out), .sel(register_9_q), .out(bitselector_1_out[2]));
  BitSelector #(.Selector_Bits(2)) bitselector_10 (
    .in({M4_CLR, M3_CLR, M2_CLR, M1_CLR}), .sel(register_9_q), .out(bitselector_2_out[1]));
  assign and_17_out = mux1x4_2_out & bitextender_6_out;  // And and_17, 4 bits wide
  assign and_18_out = bitextender_6_out & or_6_out;  // And and_18, 4 bits wide
  assign and_19_out = bitextender_7_out & fill_4_2_out1;  // And and_19, 4 bits wide
  Register register_12 (.D(and_12_out), .C(C), .en(or_9_out[1]), .Q(register_3_q[2]));
  assign and_20_out = register_3_q & bitselector_3_out;  // And and_20, 4 bits wide
  BitSelector #(.Selector_Bits(2)) bitselector_11 (.in(and_5_out), .sel(register_10_q), .out(bitselector_3_out[2]));
  BitSelector #(.Selector_Bits(2)) bitselector_12 (
    .in({M4_CLR, M3_CLR, M2_CLR, M1_CLR}), .sel(register_10_q), .out(bitselector_4_out[1]));
  Multiplexer #(.Selector_Bits(2), .Bits(4)) multiplexer_5 (
    .sel(sel_D), .in_0(M1_inst), .in_1(M2_inst), .in_2(M3_inst), .in_3(M4_inst), .out(id_O));
  assign not_5_out = ~and_13_out;  // Not not_5, 4 bits wide
  assign or_8_out = and_14_out | and_15_out;  // Or or_8, 4 bits wide
  and and_21 (and_21_out, not_5_out[0], register_1_q[2]);
  Register register_13 (.D(and_21_out), .C(C), .en(or_8_out[0]), .Q(register_1_q[3]));
  Register #(.Bits(2)) register_14 (.D(register_9_q), .C(C), .en(W_id), .Q(register_14_q));
  assign not_6_out = ~and_17_out;  // Not not_6, 4 bits wide
  assign or_9_out = and_18_out | and_19_out;  // Or or_9, 4 bits wide
  and and_22 (and_22_out, not_6_out[0], register_3_q[2]);
  Register register_15 (.D(and_22_out), .C(C), .en(or_9_out[0]), .Q(register_3_q[3]));
  Register #(.Bits(2)) register_16 (.D(register_10_q), .C(C), .en(W_id), .Q(register_16_q));
  PriorityEncoder #(.Selector_Bits(2)) priorityencoder_3 (
    .in0(and_16_out[0]), .in1(and_16_out[1]), .in2(and_16_out[2]), .in3(and_16_out[3]),
    .num(priorityencoder_3_num), .any(M_V));
  BitSelector #(.Selector_Bits(2)) bitselector_13 (.in(and_3_out), .sel(register_14_q), .out(bitselector_1_out[3]));
  Multiplexer #(.Selector_Bits(2), .Bits(2)) multiplexer_6 (
    .sel(priorityencoder_3_num), .in_0(register_2_q), .in_1(register_5_q), .in_2(register_9_q),
    .in_3(register_14_q), .out(sel_A));
  BitSelector #(.Selector_Bits(2)) bitselector_14 (
    .in({M4_CLR, M3_CLR, M2_CLR, M1_CLR}), .sel(register_14_q), .out(bitselector_2_out[0]));
  PriorityEncoder #(.Selector_Bits(2)) priorityencoder_4 (
    .in0(and_20_out[0]), .in1(and_20_out[1]), .in2(and_20_out[2]), .in3(and_20_out[3]),
    .num(priorityencoder_4_num), .any(priorityencoder_4_any));
  BitSelector #(.Selector_Bits(2)) bitselector_15 (.in(and_5_out), .sel(register_16_q), .out(bitselector_3_out[3]));
  Multiplexer #(.Selector_Bits(2), .Bits(2)) multiplexer_7 (
    .sel(priorityencoder_4_num), .in_0(register_4_q), .in_1(register_6_q), .in_2(register_10_q),
    .in_3(register_16_q), .out(multiplexer_7_out));
  BitSelector #(.Selector_Bits(2)) bitselector_16 (
    .in({M4_CLR, M3_CLR, M2_CLR, M1_CLR}), .sel(register_16_q), .out(bitselector_4_out[0]));
  Multiplexer #(.Selector_Bits(2), .Bits(32)) multiplexer_8 (
    .sel(flush_sel), .in_0(M1_PC), .in_1(M2_PC), .in_2(M3_PC), .in_3(M4_PC), .out(fl_PC));
  Multiplexer #(.Selector_Bits(2)) multiplexer_9 (
    .sel(flush_sel), .in_0(M1_epoch), .in_1(M2_epoch), .in_2(M3_epoch), .in_3(M4_epoch), .out(fl_ep));
  Multiplexer #(.Selector_Bits(2), .Bits(4)) multiplexer_10 (
    .sel(flush_sel), .in_0(M1_inst), .in_1(M2_inst), .in_2(M3_inst), .in_3(M4_inst), .out(fl_id));
  Demultiplexer #(.Selector_Bits(2)) demultiplexer_1 (
    .sel(empty_id), .in(W_id), .out_0(M1_IE), .out_1(M2_IE), .out_2(M3_IE), .out_3(M4_IE));
  Multiplexer #(.Selector_Bits(2)) multiplexer_11 (
    .sel(sel_D), .in_0(M1_MF), .in_1(M2_MF), .in_2(M3_MF), .in_3(M4_MF), .out(MF_O));
  Multiplexer #(.Selector_Bits(2), .Bits(2)) multiplexer_12 (
    .sel(sel_A), .in_0(M1_MD), .in_1(M2_MD), .in_2(M3_MD), .in_3(M4_MD), .out(M_MD));
  Multiplexer #(.Selector_Bits(2)) multiplexer_13 (
    .sel(sel_A), .in_0(M1_epoch), .in_1(M2_epoch), .in_2(M3_epoch), .in_3(M4_epoch), .out(M_ep));
  or or_10 (V, recon, priorityencoder_4_any);
  Multiplexer #(.Bits(2)) multiplexer_14 (.sel(recon), .in_0(multiplexer_7_out), .in_1(d_ff_2_q), .out(sel_D));
  D_FF #(.Bits(2)) d_ff_2 (.D(d_ff_3_q), .C(C), .Q(d_ff_2_q));  // open: nQ
  D_FF #(.Bits(2)) d_ff_3 (.D(flush_sel), .C(C), .Q(d_ff_3_q));  // open: nQ
  and and_23 (and_23_out, ~M1_IE, or_11_out);  // And
  RS_FF rs_ff_2 (.S(M1_IE), .C(C), .R(and_23_out), .Q(M1_VO));  // open: nQ
  Comparator #(.Bits(32)) comparator_1 (.a(st_addr), .b(M1_A), .eq(comparator_1_eq));  // open: gt, lt
  Register #(.Bits(32)) register_17 (.D(A), .C(C), .en(M1_AE), .Q(M1_A));
  RS_FF rs_ff_3 (.S(M1_AE), .C(C), .R(or_11_out), .Q(M1_AV));  // open: nQ
  Register #(.Bits(32)) register_18 (.D(PC), .C(C), .en(M1_AE), .Q(M1_PC));
  Register #(.Bits(8)) register_19 (.D(WR), .C(C), .en(M1_AE), .Q(M1_WR));
  Register #(.Bits(2)) register_20 (.D(MD), .C(C), .en(M1_AE), .Q(M1_MD));
  Register register_21 (.D(MF), .C(C), .en(M1_AE), .Q(M1_MF));
  Register #(.Bits(32)) register_22 (.D(multiplexer_15_out), .C(C), .en(M1_DE), .Q(M1_D));
  RS_FF rs_ff_4 (.S(M1_DE), .C(C), .R(or_11_out), .Q(M1_DV));  // open: nQ
  Comparator #(.Bits(4)) comparator_2 (.a(M1_inst), .b(inst_WA), .eq(comparator_2_eq));  // open: gt, lt
  Comparator #(.Bits(4)) comparator_3 (.a(M1_inst), .b(inst_WD), .eq(comparator_3_eq));  // open: gt, lt
  Comparator #(.Bits(4)) comparator_4 (.a(M1_inst), .b(com1_id), .eq(comparator_4_eq));  // open: gt, lt
  Comparator #(.Bits(4)) comparator_5 (.a(M1_inst), .b(com2_id), .eq(comparator_5_eq));  // open: gt, lt
  Register #(.Bits(4)) register_23 (.D(inst), .C(C), .en(M1_IE), .Q(M1_inst));
  Register register_24 (.D(epoch), .C(C), .en(M1_IE), .Q(M1_epoch));
  inst_comp inst_comp_1 (.A_id(M1_inst), .A_ep(M1_epoch), .B_id(st_id), .B_ep(st_ep), .A_old(inst_comp_1_a_old));
  inst_comp inst_comp_2 (.A_id(M1_inst), .A_ep(M1_epoch), .B_id(clr_id), .B_ep(clr_ep), .A_old(inst_comp_2_a_old));
  and and_24 (M1_CMP, M1_VO, comparator_1_eq, inst_comp_1_a_old);
  Multiplexer #(.Bits(32)) multiplexer_15 (.sel(M1_DM), .in_0(D), .in_1(st_data), .out(multiplexer_15_out));
  and and_25 (M1_SEL__A, M1_VO, comparator_2_eq);
  and and_26 (M1_SEL__D, M1_VO, comparator_3_eq);
  or or_11 (or_11_out, and_28_out, M1_CLR, and_27_out);
  and and_27 (and_27_out, comparator_4_eq, com1);
  and and_28 (and_28_out, comparator_5_eq, com2);
  and and_29 (M1_CLR, inst_comp_2_a_old, clr);
  and and_30 (and_30_out, ~M2_IE, or_12_out);  // And
  RS_FF rs_ff_5 (.S(M2_IE), .C(C), .R(and_30_out), .Q(M2_VO));  // open: nQ
  Comparator #(.Bits(32)) comparator_6 (.a(st_addr), .b(M2_A), .eq(comparator_6_eq));  // open: gt, lt
  Register #(.Bits(32)) register_25 (.D(A), .C(C), .en(M2_AE), .Q(M2_A));
  RS_FF rs_ff_6 (.S(M2_AE), .C(C), .R(or_12_out), .Q(M2_AV));  // open: nQ
  Register #(.Bits(32)) register_26 (.D(PC), .C(C), .en(M2_AE), .Q(M2_PC));
  Register #(.Bits(8)) register_27 (.D(WR), .C(C), .en(M2_AE), .Q(M2_WR));
  Register #(.Bits(2)) register_28 (.D(MD), .C(C), .en(M2_AE), .Q(M2_MD));
  Register register_29 (.D(MF), .C(C), .en(M2_AE), .Q(M2_MF));
  Register #(.Bits(32)) register_30 (.D(multiplexer_16_out), .C(C), .en(M2_DE), .Q(M2_D));
  RS_FF rs_ff_7 (.S(M2_DE), .C(C), .R(or_12_out), .Q(M2_DV));  // open: nQ
  Comparator #(.Bits(4)) comparator_7 (.a(M2_inst), .b(inst_WA), .eq(comparator_7_eq));  // open: gt, lt
  Comparator #(.Bits(4)) comparator_8 (.a(M2_inst), .b(inst_WD), .eq(comparator_8_eq));  // open: gt, lt
  Comparator #(.Bits(4)) comparator_9 (.a(M2_inst), .b(com1_id), .eq(comparator_9_eq));  // open: gt, lt
  Comparator #(.Bits(4)) comparator_10 (.a(M2_inst), .b(com2_id), .eq(comparator_10_eq));  // open: gt, lt
  Register #(.Bits(4)) register_31 (.D(inst), .C(C), .en(M2_IE), .Q(M2_inst));
  Register register_32 (.D(epoch), .C(C), .en(M2_IE), .Q(M2_epoch));
  inst_comp inst_comp_3 (.A_id(M2_inst), .A_ep(M2_epoch), .B_id(st_id), .B_ep(st_ep), .A_old(inst_comp_3_a_old));
  inst_comp inst_comp_4 (.A_id(M2_inst), .A_ep(M2_epoch), .B_id(clr_id), .B_ep(clr_ep), .A_old(inst_comp_4_a_old));
  and and_31 (M2_CMP, M2_VO, comparator_6_eq, inst_comp_3_a_old);
  Multiplexer #(.Bits(32)) multiplexer_16 (.sel(M2_DM), .in_0(D), .in_1(st_data), .out(multiplexer_16_out));
  and and_32 (M2_SEL__A, M2_VO, comparator_7_eq);
  and and_33 (M2_SEL__D, M2_VO, comparator_8_eq);
  or or_12 (or_12_out, and_35_out, M2_CLR, and_34_out);
  and and_34 (and_34_out, comparator_9_eq, com1);
  and and_35 (and_35_out, comparator_10_eq, com2);
  and and_36 (M2_CLR, inst_comp_4_a_old, clr);
  and and_37 (and_37_out, ~M3_IE, or_13_out);  // And
  RS_FF rs_ff_8 (.S(M3_IE), .C(C), .R(and_37_out), .Q(M3_VO));  // open: nQ
  Comparator #(.Bits(32)) comparator_11 (.a(st_addr), .b(M3_A), .eq(comparator_11_eq));  // open: gt, lt
  Register #(.Bits(32)) register_33 (.D(A), .C(C), .en(M3_AE), .Q(M3_A));
  RS_FF rs_ff_9 (.S(M3_AE), .C(C), .R(or_13_out), .Q(M3_AV));  // open: nQ
  Register #(.Bits(32)) register_34 (.D(PC), .C(C), .en(M3_AE), .Q(M3_PC));
  Register #(.Bits(8)) register_35 (.D(WR), .C(C), .en(M3_AE), .Q(M3_WR));
  Register #(.Bits(2)) register_36 (.D(MD), .C(C), .en(M3_AE), .Q(M3_MD));
  Register register_37 (.D(MF), .C(C), .en(M3_AE), .Q(M3_MF));
  Register #(.Bits(32)) register_38 (.D(multiplexer_17_out), .C(C), .en(M3_DE), .Q(M3_D));
  RS_FF rs_ff_10 (.S(M3_DE), .C(C), .R(or_13_out), .Q(M3_DV));  // open: nQ
  Comparator #(.Bits(4)) comparator_12 (.a(M3_inst), .b(inst_WA), .eq(comparator_12_eq));  // open: gt, lt
  and and_38 (M3_SEL__A, M3_VO, comparator_12_eq);
  Comparator #(.Bits(4)) comparator_13 (.a(M3_inst), .b(inst_WD), .eq(comparator_13_eq));  // open: gt, lt
  and and_39 (M3_SEL__D, M3_VO, comparator_13_eq);
  or or_13 (or_13_out, and_41_out, M3_CLR, and_40_out);
  and and_40 (and_40_out, comparator_14_eq, com1);
  Comparator #(.Bits(4)) comparator_14 (.a(M3_inst), .b(com1_id), .eq(comparator_14_eq));  // open: gt, lt
  and and_41 (and_41_out, comparator_15_eq, com2);
  Comparator #(.Bits(4)) comparator_15 (.a(M3_inst), .b(com2_id), .eq(comparator_15_eq));  // open: gt, lt
  Register #(.Bits(4)) register_39 (.D(inst), .C(C), .en(M3_IE), .Q(M3_inst));
  Register register_40 (.D(epoch), .C(C), .en(M3_IE), .Q(M3_epoch));
  inst_comp inst_comp_5 (.A_id(M3_inst), .A_ep(M3_epoch), .B_id(st_id), .B_ep(st_ep), .A_old(inst_comp_5_a_old));
  inst_comp inst_comp_6 (.A_id(M3_inst), .A_ep(M3_epoch), .B_id(clr_id), .B_ep(clr_ep), .A_old(inst_comp_6_a_old));
  and and_42 (M3_CMP, M3_VO, comparator_11_eq, inst_comp_5_a_old);
  Multiplexer #(.Bits(32)) multiplexer_17 (.sel(M3_DM), .in_0(D), .in_1(st_data), .out(multiplexer_17_out));
  and and_43 (M3_CLR, inst_comp_6_a_old, clr);
  and and_44 (and_44_out, ~M4_IE, or_14_out);  // And
  RS_FF rs_ff_11 (.S(M4_IE), .C(C), .R(and_44_out), .Q(M4_VO));  // open: nQ
  Comparator #(.Bits(32)) comparator_16 (.a(st_addr), .b(M4_A), .eq(comparator_16_eq));  // open: gt, lt
  Register #(.Bits(32)) register_41 (.D(A), .C(C), .en(M4_AE), .Q(M4_A));
  RS_FF rs_ff_12 (.S(M4_AE), .C(C), .R(or_14_out), .Q(M4_AV));  // open: nQ
  Register #(.Bits(32)) register_42 (.D(PC), .C(C), .en(M4_AE), .Q(M4_PC));
  Register #(.Bits(8)) register_43 (.D(WR), .C(C), .en(M4_AE), .Q(M4_WR));
  Register #(.Bits(2)) register_44 (.D(MD), .C(C), .en(M4_AE), .Q(M4_MD));
  Register register_45 (.D(MF), .C(C), .en(M4_AE), .Q(M4_MF));
  Multiplexer #(.Bits(32)) multiplexer_18 (.sel(M4_DM), .in_0(D), .in_1(st_data), .out(multiplexer_18_out));
  Register #(.Bits(32)) register_46 (.D(multiplexer_18_out), .C(C), .en(M4_DE), .Q(M4_D));
  RS_FF rs_ff_13 (.S(M4_DE), .C(C), .R(or_14_out), .Q(M4_DV));  // open: nQ
  Comparator #(.Bits(4)) comparator_17 (.a(M4_inst), .b(inst_WA), .eq(comparator_17_eq));  // open: gt, lt
  and and_45 (M4_SEL__A, M4_VO, comparator_17_eq);
  Comparator #(.Bits(4)) comparator_18 (.a(M4_inst), .b(inst_WD), .eq(comparator_18_eq));  // open: gt, lt
  and and_46 (M4_SEL__D, M4_VO, comparator_18_eq);
  or or_14 (or_14_out, and_48_out, M4_CLR, and_47_out);
  and and_47 (and_47_out, comparator_19_eq, com1);
  Comparator #(.Bits(4)) comparator_19 (.a(M4_inst), .b(com1_id), .eq(comparator_19_eq));  // open: gt, lt
  and and_48 (and_48_out, comparator_20_eq, com2);
  Comparator #(.Bits(4)) comparator_20 (.a(M4_inst), .b(com2_id), .eq(comparator_20_eq));  // open: gt, lt
  Register #(.Bits(4)) register_47 (.D(inst), .C(C), .en(M4_IE), .Q(M4_inst));
  Register register_48 (.D(epoch), .C(C), .en(M4_IE), .Q(M4_epoch));
  inst_comp inst_comp_7 (.A_id(M4_inst), .A_ep(M4_epoch), .B_id(st_id), .B_ep(st_ep), .A_old(inst_comp_7_a_old));
  inst_comp inst_comp_8 (.A_id(M4_inst), .A_ep(M4_epoch), .B_id(clr_id), .B_ep(clr_ep), .A_old(inst_comp_8_a_old));
  and and_49 (M4_CLR, inst_comp_8_a_old, clr);
  and and_50 (M4_CMP, M4_VO, comparator_16_eq, inst_comp_7_a_old);

  // Other names for the same wires on the sheet: clear = clr; comp_addr[31:0] = st_addr; comp_ep = st_ep;
  //   comp_id[3:0] = st_id; flush = fl; flush_ep = fl_ep; flush_id[3:0] = fl_id; flush_PC[31:0] = fl_PC;
  //   MD_O[1:0] = M_MD; V_out = V
endmodule
