// Digital circuit mux8x4.dig as structural Verilog
module mux8x4 (
  input  [31:0] D1,
  input  [31:0] D2,
  input  [3:0] S,
  output [31:0] D_o
);

  Multiplexer #(.Bits(8)) multiplexer_1 (.sel(S[0]), .in_0(D1[7:0]), .in_1(D2[7:0]), .out(D_o[7:0]));
  Multiplexer #(.Bits(8)) multiplexer_2 (.sel(S[1]), .in_0(D1[15:8]), .in_1(D2[15:8]), .out(D_o[15:8]));
  Multiplexer #(.Bits(8)) multiplexer_3 (.sel(S[2]), .in_0(D1[23:16]), .in_1(D2[23:16]), .out(D_o[23:16]));
  Multiplexer #(.Bits(8)) multiplexer_4 (.sel(S[3]), .in_0(D1[31:24]), .in_1(D2[31:24]), .out(D_o[31:24]));

  // Other names for the same wires on the sheet: D1_1_i[7:0] = D1[7:0]; D1_2_i[7:0] = D1[15:8];
  //   D1_3_i[7:0] = D1[23:16]; D1_4_i[7:0] = D1[31:24]; D2_1_i[7:0] = D2[7:0]; D2_2_i[7:0] = D2[15:8];
  //   D2_3_i[7:0] = D2[23:16]; D2_4_i[7:0] = D2[31:24]; R1[7:0] = D_o[7:0]; R2[7:0] = D_o[15:8]; R3[7:0] = D_o[23:16];
  //   R4[7:0] = D_o[31:24]; S1 = S[0]; S2 = S[1]; S3 = S[2]; S4 = S[3]

  // Notes on the sheet:
  //   D_o: data out
  //   D1: data in 1
  //   D2: data in 2
  //   S: select
endmodule
