// Digital circuit priority-4.dig as structural Verilog
module priority_4 (
  input  in1,
  input  in2,
  input  in3,
  input  in4,
  input  on,
  output out1,
  output out2,
  output out3,
  output out4,
  output v
);

  wire nor_1_out, nor_2_out, not_1_out;

  not not_1 (not_1_out, in4);
  nor nor_1 (nor_1_out, in3, in4);
  nor nor_2 (nor_2_out, in2, in3, in4);
  or or_1 (v, in1, in2, in3, in4);
  and and_1 (out4, in4, on);
  and and_2 (out3, in3, on, not_1_out);
  and and_3 (out2, in2, on, nor_1_out);
  and and_4 (out1, in1, on, nor_2_out);
endmodule
