// Digital circuit priority-test4V.dig as structural Verilog
module priority_test4V (
  input  in1,
  input  in2,
  input  in3,
  input  in4,
  input  on,
  input  [3:0] test,
  output out1,
  output out2,
  output out3,
  output out4,
  output v
);

  wire and_5_out, and_6_out, and_7_out, and_8_out, nor_1_out, nor_2_out, not_1_out;

  nor nor_1 (nor_1_out, in3, in4);
  nor nor_2 (nor_2_out, in2, in3, in4);
  not not_1 (not_1_out, in4);
  and and_1 (out4, in4, on);
  and and_2 (out3, in3, on, not_1_out);
  and and_3 (out2, in2, on, nor_1_out);
  and and_4 (out1, in1, on, nor_2_out);
  and and_5 (and_5_out, in4, test[0]);
  and and_6 (and_6_out, in3, test[1], not_1_out);
  and and_7 (and_7_out, in2, test[2], nor_1_out);
  and and_8 (and_8_out, in1, test[3], nor_2_out);
  or or_1 (v, and_5_out, and_6_out, and_7_out, and_8_out);
endmodule
