// Digital circuit priority-test8.dig as structural Verilog
module priority_test8 (
  input  in1,
  input  in2,
  input  in3,
  input  in4,
  input  in5,
  input  in6,
  input  in7,
  input  in8,
  input  [7:0] test,
  output out1,
  output out2,
  output out3,
  output out4,
  output v,
  output out5,
  output out6,
  output out7,
  output out8
);

  wire nor_1_out, nor_2_out, nor_3_out, nor_4_out, nor_5_out, nor_6_out, not_1_out;
  wire [7:0] and_9_out;

  nor nor_1 (nor_1_out, in7, in8);
  nor nor_2 (nor_2_out, in6, in7, in8);
  nor nor_3 (nor_3_out, in5, in6, in7, in8);
  nor nor_4 (nor_4_out, in4, in5, in6, in7, in8);
  nor nor_5 (nor_5_out, in3, in4, in5, in6, in7, in8);
  nor nor_6 (nor_6_out, in2, in3, in4, in5, in6, in7, in8);
  not not_1 (not_1_out, in8);
  and and_1 (out8, in8, test[0]);
  and and_2 (out7, in7, test[1], not_1_out);
  and and_3 (out6, in6, test[2], nor_1_out);
  and and_4 (out5, in5, test[3], nor_2_out);
  and and_5 (out4, in4, test[4], nor_3_out);
  and and_6 (out3, in3, test[5], nor_4_out);
  and and_7 (out2, in2, test[6], nor_5_out);
  and and_8 (out1, in1, test[7], nor_6_out);
  assign and_9_out = test & {in8, in7, in6, in5, in4, in3, in2, in1};  // And and_9, 8 bits wide
  or or_1 (v, and_9_out[0], and_9_out[1], and_9_out[2], and_9_out[3], and_9_out[4], and_9_out[5], and_9_out[6], and_9_out[7]);
endmodule
