// Digital circuit priority-test8V.dig as structural Verilog
module priority_test8V (
  input  in1,
  input  in2,
  input  in3,
  input  in4,
  input  in5,
  input  in6,
  input  in7,
  input  in8,
  input  on,
  input  [7:0] test,
  output out1,
  output out2,
  output out3,
  output out4,
  output out5,
  output out6,
  output out7,
  output out8,
  output v
);

  wire and_9_out, and_10_out, and_11_out, and_12_out, and_13_out, and_14_out, and_15_out, and_16_out,
       nor_1_out, nor_2_out, nor_3_out, nor_4_out, nor_5_out, nor_6_out, not_1_out;

  nor nor_1 (nor_1_out, in7, in8);
  nor nor_2 (nor_2_out, in6, in7, in8);
  nor nor_3 (nor_3_out, in5, in6, in7, in8);
  nor nor_4 (nor_4_out, in4, in5, in6, in7, in8);
  nor nor_5 (nor_5_out, in3, in4, in5, in6, in7, in8);
  nor nor_6 (nor_6_out, in2, in3, in4, in5, in6, in7, in8);
  not not_1 (not_1_out, in8);
  and and_1 (out8, in8, on);
  and and_2 (out7, in7, on, not_1_out);
  and and_3 (out6, in6, on, nor_1_out);
  and and_4 (out5, in5, on, nor_2_out);
  and and_5 (out4, in4, on, nor_3_out);
  and and_6 (out3, in3, on, nor_4_out);
  and and_7 (out2, in2, on, nor_5_out);
  and and_8 (out1, in1, on, nor_6_out);
  and and_9 (and_9_out, in8, test[0]);
  and and_10 (and_10_out, in7, test[1], not_1_out);
  and and_11 (and_11_out, in6, test[2], nor_1_out);
  and and_12 (and_12_out, in5, test[3], nor_2_out);
  and and_13 (and_13_out, in4, test[4], nor_3_out);
  and and_14 (and_14_out, in3, test[5], nor_4_out);
  and and_15 (and_15_out, in2, test[6], nor_5_out);
  and and_16 (and_16_out, in1, test[7], nor_6_out);
  or or_1 (v, and_9_out, and_10_out, and_11_out, and_12_out, and_13_out, and_14_out, and_15_out, and_16_out);
endmodule
