// Digital circuit priority-test8V8B.dig as structural Verilog
module priority_test8V8B (
  input  in1,
  input  in2,
  input  in3,
  input  in4,
  input  in5,
  input  in6,
  input  in7,
  input  in8,
  input  on,
  input  [7:0] test,
  output out1,
  output out2,
  output out3,
  output out4,
  output out5,
  output out6,
  output out7,
  output out8,
  output [7:0] v
);

  wire nor_1_out, nor_2_out, nor_3_out, nor_4_out, nor_5_out, nor_6_out, not_1_out;

  nor nor_1 (nor_1_out, in7, in8);
  nor nor_2 (nor_2_out, in6, in7, in8);
  nor nor_3 (nor_3_out, in5, in6, in7, in8);
  nor nor_4 (nor_4_out, in4, in5, in6, in7, in8);
  nor nor_5 (nor_5_out, in3, in4, in5, in6, in7, in8);
  nor nor_6 (nor_6_out, in2, in3, in4, in5, in6, in7, in8);
  not not_1 (not_1_out, in8);
  and and_1 (out8, in8, on);
  and and_2 (out7, in7, on, not_1_out);
  and and_3 (out6, in6, on, nor_1_out);
  and and_4 (out5, in5, on, nor_2_out);
  and and_5 (out4, in4, on, nor_3_out);
  and and_6 (out3, in3, on, nor_4_out);
  and and_7 (out2, in2, on, nor_5_out);
  and and_8 (out1, in1, on, nor_6_out);
  and and_9 (v[7], in8, test[0]);
  and and_10 (v[6], in7, test[1], not_1_out);
  and and_11 (v[5], in6, test[2], nor_1_out);
  and and_12 (v[4], in5, test[3], nor_2_out);
  and and_13 (v[3], in4, test[4], nor_3_out);
  and and_14 (v[2], in3, test[5], nor_4_out);
  and and_15 (v[1], in2, test[6], nor_5_out);
  and and_16 (v[0], in1, test[7], nor_6_out);
endmodule
