// Digital circuit queue.dig as structural Verilog
module queue (
  input  C,
  input  [7:0] D,
  input  push,
  input  pop,
  output [7:0] out,
  output empty,
  output full
);

  wire comparator_1_eq, comparator_2_eq;
  wire [3:0] counterpreset_1_out, counterpreset_2_out, sub_1_s;

  CounterPreset #(.Bits(4)) counterpreset_1 (
    .en(push), .C(C), .dir(1'b0), .in(4'b0000), .ld(1'b0), .clr(1'b0), .out(counterpreset_1_out));  // open: ovf
  CounterPreset #(.Bits(4)) counterpreset_2 (
    .en(pop), .C(C), .dir(1'b0), .in(4'b0000), .ld(1'b0), .clr(1'b0), .out(counterpreset_2_out));  // open: ovf
  Comparator #(.Bits(4)) comparator_1 (
    .a(counterpreset_1_out), .b(counterpreset_2_out), .eq(comparator_1_eq));  // open: gt, lt
  Sub #(.Bits(4)) sub_1 (.a(counterpreset_2_out), .b(4'b0001), .c_i(1'b0), .s(sub_1_s));  // open: c_o
  Comparator #(.Bits(4)) comparator_2 (.a(sub_1_s), .b(counterpreset_1_out), .eq(comparator_2_eq));  // open: gt, lt
  Register register_1 (.D(comparator_2_eq), .C(C), .en(push), .Q(full));
  and and_1 (empty, comparator_1_eq, ~full);  // And
  RegisterFile #(.AddrBits(4), .Bits(8)) registerfile_1 (
    .Din(D), .we(push), .Rw(counterpreset_1_out), .C(C), .Ra(counterpreset_2_out), .Rb(4'b0000), .Da(out));  // open: Db
endmodule
