// Digital circuit ram-test.dig as structural Verilog
module ram_test (
  input  [31:0] D2,
  input  [31:0] D1,
  input  str,
  input  ld1,
  input  C,
  input  [31:0] _2A,
  input  [31:0] _1A,
  input  [31:0] D_in,
  input  [1:0] mode,
  input  ld2,
  input  D2_V
);

  wire and_1_out, and_2_out, and_5_out, D2_V_t, or_1_out, or_2_out, R0_e, R1_e, R2_e, R3_e;
  wire [3:0] and_3_out, bitextender_1_out;
  wire [3:1] mask;
  wire [7:0] bitextender_2_out, bitextender_3_out, bitextender_4_out, bitextender_5_out, R0, R0_d, R1, R1_d,
       R2, R2_d, R3, R3_d, R4, R5, R6, R7;
  wire [23:0] _1addr_plus_1, _2addr_plus_1, multiplexer_1_out, multiplexer_2_out, multiplexer_3_out,
       multiplexer_4_out, multiplexer_5_out, multiplexer_6_out, multiplexer_7_out, multiplexer_8_out,
       multiplexer_9_out, multiplexer_10_out;
  wire [31:0] and_4_out, multiplexer_13_out, multiplexer_14_out;

  Add #(.Bits(24), .generic("this.Bits=int(args.addrBits-2);")) add_1 (
    .a({24{1'b0}}), .b(_1A[25:2]), .c_i(1'b1), .s(_1addr_plus_1));  // open: c_o
  Add #(.Bits(24), .generic("this.Bits=int(args.addrBits-2);")) add_2 (
    .a({24{1'b0}}), .b(_2A[25:2]), .c_i(1'b1), .s(_2addr_plus_1));  // open: c_o
  or or_1 (or_1_out, _1A[0], _1A[1]);
  or or_2 (or_2_out, _2A[0], _2A[1]);
  and and_1 (and_1_out, _1A[0], _1A[1]);
  and and_2 (and_2_out, _2A[0], _2A[1]);
  nor nor_1 (mask[3], mode[0], mode[1]);
  BitExtender #(.inputBits(1), .outputBits(4)) bitextender_1 (.in(str), .out(bitextender_1_out));
  not not_1 (mask[1], mode[1]);
  Multiplexer #(.Bits(24), .generic("this.Bits=int(args.addrBits-2);")) multiplexer_1 (
    .sel(or_1_out), .in_0(_1A[25:2]), .in_1(_1addr_plus_1), .out(multiplexer_1_out));
  Multiplexer #(.Bits(24), .generic("this.Bits=int(args.addrBits-2);")) multiplexer_2 (
    .sel(or_2_out), .in_0(_2A[25:2]), .in_1(_2addr_plus_1), .out(multiplexer_2_out));
  Multiplexer #(.Bits(24), .generic("this.Bits=int(args.addrBits-2);")) multiplexer_3 (
    .sel(_1A[1]), .in_0(_1A[25:2]), .in_1(_1addr_plus_1), .out(multiplexer_3_out));
  Multiplexer #(.Bits(24), .generic("this.Bits=int(args.addrBits-2);")) multiplexer_4 (
    .sel(_2A[1]), .in_0(_2A[25:2]), .in_1(_2addr_plus_1), .out(multiplexer_4_out));
  Multiplexer #(.Bits(24), .generic("this.Bits=int(args.addrBits-2);")) multiplexer_5 (
    .sel(and_1_out), .in_0(_1A[25:2]), .in_1(_1addr_plus_1), .out(multiplexer_5_out));
  Multiplexer #(.Bits(24), .generic("this.Bits=int(args.addrBits-2);")) multiplexer_6 (
    .sel(and_2_out), .in_0(_2A[25:2]), .in_1(_2addr_plus_1), .out(multiplexer_6_out));
  assign and_3_out = bitextender_1_out & {{2{mask[3]}}, mask[1], 1'b1};  // And and_3, 4 bits wide
  RAMDualPort #(.AddrBits(24), .Bits(8)) u_R4 (.A(multiplexer_1_out), .Din(R0_d), .str(R0_e), .C(C), .ld(1'b1), .D(R0));
  RAMDualPort #(.AddrBits(24), .Bits(8)) u_R5 (.A(multiplexer_3_out), .Din(R1_d), .str(R1_e), .C(C), .ld(1'b1), .D(R1));
  RAMDualPort #(.AddrBits(24), .Bits(8)) u_R6 (.A(multiplexer_5_out), .Din(R2_d), .str(R2_e), .C(C), .ld(1'b1), .D(R2));
  RAMDualPort #(.AddrBits(24), .Bits(8)) u_R7 (.A(_1A[25:2]), .Din(R3_d), .str(R3_e), .C(C), .ld(1'b1), .D(R3));
  Multiplexer #(.Bits(24), .generic("this.Bits=int(args.addrBits-2);")) multiplexer_7 (
    .sel(D2_V_t), .in_0(multiplexer_1_out), .in_1(multiplexer_2_out), .out(multiplexer_7_out));
  Multiplexer #(.Bits(24), .generic("this.Bits=int(args.addrBits-2);")) multiplexer_8 (
    .sel(D2_V_t), .in_0(multiplexer_3_out), .in_1(multiplexer_4_out), .out(multiplexer_8_out));
  Multiplexer #(.Bits(24), .generic("this.Bits=int(args.addrBits-2);")) multiplexer_9 (
    .sel(D2_V_t), .in_0(multiplexer_5_out), .in_1(multiplexer_6_out), .out(multiplexer_9_out));
  Multiplexer #(.Bits(24), .generic("this.Bits=int(args.addrBits-2);")) multiplexer_10 (
    .sel(D2_V_t), .in_0(_1A[25:2]), .in_1(_2A[25:2]), .out(multiplexer_10_out));
  Multiplexer #(.Selector_Bits(2), .Bits(32)) multiplexer_11 (
    .sel(_1A[1:0]), .in_0(D_in), .in_1({D_in[23:0], D_in[31:24]}), .in_2({D_in[15:0], D_in[31:16]}),
    .in_3({D_in[7:0], D_in[31:8]}), .out({R3_d, R2_d, R1_d, R0_d}));
  Multiplexer #(.Selector_Bits(2), .Bits(4)) multiplexer_12 (
    .sel(_1A[1:0]), .in_0(and_3_out), .in_1({and_3_out[2:0], and_3_out[3]}),
    .in_2({and_3_out[1:0], and_3_out[3:2]}), .in_3({and_3_out[0], and_3_out[3:1]}),
    .out({R3_e, R2_e, R1_e, R0_e}));
  RAMDualPort #(.AddrBits(24), .Bits(8)) R4_2 (.A(multiplexer_7_out), .Din(R0_d), .str(R0_e), .C(C), .ld(1'b1), .D(R4));
  RAMDualPort #(.AddrBits(24), .Bits(8)) R5_2 (.A(multiplexer_8_out), .Din(R1_d), .str(R1_e), .C(C), .ld(1'b1), .D(R5));
  RAMDualPort #(.AddrBits(24), .Bits(8)) R6_2 (.A(multiplexer_9_out), .Din(R2_d), .str(R2_e), .C(C), .ld(1'b1), .D(R6));
  RAMDualPort #(.AddrBits(24), .Bits(8)) R7_2 (
    .A(multiplexer_10_out), .Din(R3_d), .str(R3_e), .C(C), .ld(1'b1), .D(R7));
  not not_2 (D2_V_t, str);
  assign D2_V = ld2 ? D2_V_t : 1'bz;  // Driver driver_1
  BitExtender #(.inputBits(1), .outputBits(8)) bitextender_2 (.in(1'b1), .out(bitextender_2_out));
  BitExtender #(.inputBits(1), .outputBits(8)) bitextender_3 (.in(mask[1]), .out(bitextender_3_out));
  BitExtender #(.inputBits(1), .outputBits(8)) bitextender_4 (.in(mask[3]), .out(bitextender_4_out));
  BitExtender #(.inputBits(1), .outputBits(8)) bitextender_5 (.in(mask[3]), .out(bitextender_5_out));
  Multiplexer #(.Selector_Bits(2), .Bits(32)) multiplexer_13 (
    .sel(_1A[1:0]), .in_0({R3, R2, R1, R0}), .in_1({R0, R3, R2, R1}), .in_2({R1, R0, R3, R2}),
    .in_3({R2, R1, R0, R3}), .out(multiplexer_13_out));
  Multiplexer #(.Selector_Bits(2), .Bits(32)) multiplexer_14 (
    .sel(_2A[1:0]), .in_0({R7, R6, R5, R4}), .in_1({R4, R7, R6, R5}), .in_2({R5, R4, R7, R6}),
    .in_3({R6, R5, R4, R7}), .out(multiplexer_14_out));
  assign and_4_out = {bitextender_5_out, bitextender_4_out, bitextender_3_out, bitextender_2_out} & multiplexer_13_out;  // And and_4, 32 bits wide
  and and_5 (and_5_out, ld2, D2_V_t);
  assign D1 = ld1 ? and_4_out : 32'bz;  // Driver driver_2
  assign D2 = and_5_out ? multiplexer_14_out : 32'bz;  // Driver driver_3

  // Other names for the same wires on the sheet: mask[2] = mask[3]; _1A_0 = _1A[0]; _1A_01[1:0] = _1A[1:0];
  //   _1A_1 = _1A[1]; _1addr[23:0] = _1A[25:2]; _1D_in[31:0] = D_in; _2A_0 = _2A[0]; _2A_01[1:0] = _2A[1:0];
  //   _2A_1 = _2A[1]; _2addr[23:0] = _2A[25:2]; D2_VO = D2_V; E = str; md[1:0] = mode
endmodule
