// Digital circuit reg8x4M.dig as structural Verilog
module reg8x4M (
  input  C,
  input  [3:0] E,
  input  [31:0] D1,
  input  [31:0] D2,
  input  [3:0] S,
  output [31:0] D_o
);

  wire [7:0] multiplexer_1_out, multiplexer_2_out, multiplexer_3_out, multiplexer_4_out;

  Multiplexer #(.Bits(8)) multiplexer_1 (.sel(S[0]), .in_0(D1[7:0]), .in_1(D2[7:0]), .out(multiplexer_1_out));
  Multiplexer #(.Bits(8)) multiplexer_2 (.sel(S[1]), .in_0(D1[15:8]), .in_1(D2[15:8]), .out(multiplexer_2_out));
  Multiplexer #(.Bits(8)) multiplexer_3 (.sel(S[2]), .in_0(D1[23:16]), .in_1(D2[23:16]), .out(multiplexer_3_out));
  Multiplexer #(.Bits(8)) multiplexer_4 (.sel(S[3]), .in_0(D1[31:24]), .in_1(D2[31:24]), .out(multiplexer_4_out));
  Register #(.Bits(8)) R1 (.D(multiplexer_1_out), .C(C), .en(E[0]), .Q(D_o[7:0]));
  Register #(.Bits(8)) R2 (.D(multiplexer_2_out), .C(C), .en(E[1]), .Q(D_o[15:8]));
  Register #(.Bits(8)) R3 (.D(multiplexer_3_out), .C(C), .en(E[2]), .Q(D_o[23:16]));
  Register #(.Bits(8)) R4 (.D(multiplexer_4_out), .C(C), .en(E[3]), .Q(D_o[31:24]));

  // Other names for the same wires on the sheet: D1_1_i[7:0] = D1[7:0]; D1_2_i[7:0] = D1[15:8];
  //   D1_3_i[7:0] = D1[23:16]; D1_4_i[7:0] = D1[31:24]; D2_1_i[7:0] = D2[7:0]; D2_2_i[7:0] = D2[15:8];
  //   D2_3_i[7:0] = D2[23:16]; D2_4_i[7:0] = D2[31:24]; E1 = E[0]; E2 = E[1]; E3 = E[2]; E4 = E[3];
  //   R1[7:0] = D_o[7:0]; R2[7:0] = D_o[15:8]; R3[7:0] = D_o[23:16]; R4[7:0] = D_o[31:24]; S1 = S[0]; S2 = S[1];
  //   S3 = S[2]; S4 = S[3]

  // Notes on the sheet:
  //   E: enable
  //   D_o: data out
  //   D1: data in 1
  //   D2: data in 2
  //   S: select
endmodule
