// Digital circuit regFile4.dig as structural Verilog
module regFile4 (
  input  C,
  input  [31:0] FL_i,
  input  FL_sel,
  input  [3:0] FL_e,
  input  [2:0] MW1,
  input  [4:0] RW1,
  input  [4:0] RA,
  input  [4:0] RB,
  input  [2:0] MA,
  input  [2:0] MB,
  input  E1,
  input  [31:0] D1,
  input  [31:0] PCS_i,
  input  PCS_e,
  input  SCA_sel,
  input  SCS_e,
  input  [31:0] SCS_i,
  input  [31:0] D2,
  input  [2:0] MW2,
  input  [4:0] RW2,
  input  [31:0] PCA_i,
  input  PCA_e,
  input  SCA_e,
  input  [31:0] SCA_i,
  input  E2,
  input  [31:0] PC_read,
  input  SC_sel,
  output [31:0] R_A,
  output [31:0] R_B,
  output [31:0] PCS_O,
  output [31:0] FL_O,
  output [31:0] SCS_O,
  output [31:0] PCA_O,
  output [31:0] SCA_O
);

  wire a_mux_a1, a_mux_a2, a_mux_c2, a_mux_d1, a_mux_d2, and_1_out, and_2_out, and_3_out, and_12_out,
       and_13_out, and_14_out, and_15_out, b_mux_a1, b_mux_a2, b_mux_c2, b_mux_d1, b_mux_d2, comparator_1_eq,
       comparator_2_eq, comparator_3_eq, comparator_4_eq, FLM, multiplexer_42_out, multiplexer_43_out,
       nand_1_out, nand_2_out, nand_3_out, nand_4_out, nor_3_out, nor_4_out, RM1, RM2, RM3, RM4, RM5, RM6,
       RM7, RM8, RM9, RM10, RM11, RM12, RM13, RM14, RM15, RM16, RM17, RM18, RM19, RM20, RM21, RM22, RM23,
       RM24, RM25, SBPM, SCAM, xor_1_out, xor_2_out;
  wire [3:0] bitextender_1_out, bitextender_2_out, bitextender_3_out, bitextender_4_out, FL_e_t, GR1_e,
       GR2_e, multiplexer_21_out, multiplexer_22_out, multiplexer_23_out, or_1_out, or_3_out, R1_e, R2_e,
       R3_e, R4_e, R5_e, R6_e, R7_e, R8_e, R9_e, R10_e, R11_e, R12_e, R13_e, R14_e, R15_e, R16_e, R17_e,
       R18_e, R19_e, R20_e, R21_e, R22_e, R23_e, R24_e, R25_e, SBP_e, SCA_e_t;
  wire [6:6] FL_d_o;
  wire [7:0] and_16_out, and_17_out, and_18_out, and_19_out, and_20_out, and_21_out, bitextender_5_out,
       bitextender_6_out, bitextender_7_out, bitextender_8_out, bitextender_9_out, bitextender_10_out,
       bitextender_11_out, bitextender_12_out, multiplexer_36_out, multiplexer_37_out, multiplexer_38_out,
       multiplexer_39_out;
  wire [29:26] or_11_out, or_12_out, or_13_out, or_14_out;
  wire [31:0] demultiplexer_2_out_0, demultiplexer_3_out_0, demultiplexer_4_out_0, demultiplexer_5_out_0,
       demultiplexer_6_out_0, demultiplexer_7_out_0, demultiplexer_8_out_0, demultiplexer_9_out_0,
       multiplexer_1_out, multiplexer_2_out, multiplexer_3_out, multiplexer_4_out, multiplexer_5_out,
       multiplexer_6_out, multiplexer_7_out, multiplexer_8_out, multiplexer_9_out, multiplexer_10_out,
       multiplexer_11_out, multiplexer_12_out, multiplexer_13_out, multiplexer_14_out, multiplexer_15_out,
       multiplexer_16_out, multiplexer_17_out, multiplexer_18_out, multiplexer_19_out, multiplexer_20_out,
       multiplexer_24_out, multiplexer_25_out, multiplexer_26_out, multiplexer_27_out, multiplexer_28_out,
       multiplexer_29_out, multiplexer_30_out, multiplexer_31_out, multiplexer_32_out, multiplexer_33_out,
       multiplexer_34_out, multiplexer_35_out, R1, R2, R3, R4, R5, R6, R7, R8, R9, R10, R11, R12, R13, R14,
       R15, R16, R17, R18, R19, R20, R21, R22, R23, R24, R25, R_A_t, R_B_t, SBP;
  wire [31:8] R1_i, R2_i;

  Comparator #(.Bits(5)) comparator_1 (.a(5'b11110), .b(RW1), .eq(comparator_1_eq));  // open: gt, lt
  Comparator #(.Bits(5)) comparator_2 (.a(5'b11110), .b(RW2), .eq(comparator_2_eq));  // open: gt, lt
  Multiplexer #(.Bits(32)) multiplexer_1 (
    .sel(RM1), .in_0({R1_i, D1[7:0]}), .in_1({R2_i, D2[7:0]}), .out(multiplexer_1_out));
  Multiplexer #(.Bits(32)) multiplexer_2 (
    .sel(RM5), .in_0({R1_i, D1[7:0]}), .in_1({R2_i, D2[7:0]}), .out(multiplexer_2_out));
  Multiplexer #(.Bits(32)) multiplexer_3 (
    .sel(RM9), .in_0({R1_i, D1[7:0]}), .in_1({R2_i, D2[7:0]}), .out(multiplexer_3_out));
  Multiplexer #(.Bits(32)) multiplexer_4 (
    .sel(RM13), .in_0({R1_i, D1[7:0]}), .in_1({R2_i, D2[7:0]}), .out(multiplexer_4_out));
  Multiplexer #(.Bits(32)) multiplexer_5 (
    .sel(RM17), .in_0({R1_i, D1[7:0]}), .in_1({R2_i, D2[7:0]}), .out(multiplexer_5_out));
  Multiplexer #(.Bits(32)) multiplexer_6 (
    .sel(RM21), .in_0({R1_i, D1[7:0]}), .in_1({R2_i, D2[7:0]}), .out(multiplexer_6_out));
  Multiplexer #(.Bits(32)) multiplexer_7 (
    .sel(RM25), .in_0({R1_i, D1[7:0]}), .in_1({R2_i, D2[7:0]}), .out(multiplexer_7_out));
  Multiplexer #(.Bits(32)) multiplexer_8 (
    .sel(SBPM), .in_0({R1_i, D1[7:0]}), .in_1({R2_i, D2[7:0]}), .out(multiplexer_8_out));
  nand nand_1 (nand_1_out, E1, comparator_1_eq);
  nand nand_2 (nand_2_out, E2, comparator_2_eq);
  reg8x4 u_R1 (.C(C), .D(multiplexer_1_out), .E(R1_e), .D_o(R1));
  reg8x4 u_R5 (.C(C), .D(multiplexer_2_out), .E(R5_e), .D_o(R5));
  reg8x4 u_R9 (.C(C), .D(multiplexer_3_out), .E(R9_e), .D_o(R9));
  reg8x4 u_R13 (.C(C), .D(multiplexer_4_out), .E(R13_e), .D_o(R13));
  reg8x4 u_R17 (.C(C), .D(multiplexer_5_out), .E(R17_e), .D_o(R17));
  reg8x4 u_R21 (.C(C), .D(multiplexer_6_out), .E(R21_e), .D_o(R21));
  reg8x4 u_R25 (.C(C), .D(multiplexer_7_out), .E(R25_e), .D_o(R25));
  reg8x4 u_SBP (.C(C), .D(multiplexer_8_out), .E(SBP_e), .D_o(SBP));
  Comparator #(.Bits(5)) comparator_3 (.a({5{1'b1}}), .b(RW1), .eq(comparator_3_eq));  // open: gt, lt
  Comparator #(.Bits(5)) comparator_4 (.a({5{1'b1}}), .b(RW2), .eq(comparator_4_eq));  // open: gt, lt
  and and_1 (and_1_out, SCA_sel, nand_2_out, nand_1_out);
  Multiplexer #(.Bits(32)) multiplexer_9 (
    .sel(SCAM), .in_0({R1_i, D1[7:0]}), .in_1({R2_i, D2[7:0]}), .out(multiplexer_9_out));
  and and_2 (and_2_out, SC_sel, nand_2_out, nand_1_out);
  Multiplexer #(.Bits(32)) multiplexer_10 (
    .sel(SCAM), .in_0({R1_i, D1[7:0]}), .in_1({R2_i, D2[7:0]}), .out(multiplexer_10_out));
  Multiplexer #(.Bits(32)) multiplexer_11 (
    .sel(FLM), .in_0({R1_i, D1[7:0]}), .in_1({R2_i, D2[7:0]}), .out(multiplexer_11_out));
  nand nand_3 (nand_3_out, E1, comparator_3_eq);
  nand nand_4 (nand_4_out, E2, comparator_4_eq);
  Multiplexer #(.Bits(32)) multiplexer_12 (
    .sel(RM2), .in_0({R1_i, D1[7:0]}), .in_1({R2_i, D2[7:0]}), .out(multiplexer_12_out));
  Multiplexer #(.Bits(32)) multiplexer_13 (
    .sel(RM6), .in_0({R1_i, D1[7:0]}), .in_1({R2_i, D2[7:0]}), .out(multiplexer_13_out));
  Multiplexer #(.Bits(32)) multiplexer_14 (
    .sel(RM10), .in_0({R1_i, D1[7:0]}), .in_1({R2_i, D2[7:0]}), .out(multiplexer_14_out));
  Multiplexer #(.Bits(32)) multiplexer_15 (
    .sel(RM14), .in_0({R1_i, D1[7:0]}), .in_1({R2_i, D2[7:0]}), .out(multiplexer_15_out));
  Multiplexer #(.Bits(32)) multiplexer_16 (
    .sel(RM18), .in_0({R1_i, D1[7:0]}), .in_1({R2_i, D2[7:0]}), .out(multiplexer_16_out));
  Multiplexer #(.Bits(32)) multiplexer_17 (
    .sel(RM22), .in_0({R1_i, D1[7:0]}), .in_1({R2_i, D2[7:0]}), .out(multiplexer_17_out));
  Multiplexer #(.Bits(32)) multiplexer_18 (
    .sel(and_1_out), .in_0(multiplexer_9_out), .in_1(SCA_i), .out(multiplexer_18_out));
  BitExtender #(.inputBits(1), .outputBits(4)) bitextender_1 (.in(SCA_e), .out(bitextender_1_out));
  Multiplexer #(.Bits(32)) multiplexer_19 (
    .sel(and_2_out), .in_0(multiplexer_10_out), .in_1(SCS_i), .out(multiplexer_19_out));
  BitExtender #(.inputBits(1), .outputBits(4)) bitextender_2 (.in(SCS_e), .out(bitextender_2_out));
  Multiplexer #(.Bits(32)) multiplexer_20 (
    .sel(and_3_out), .in_0(multiplexer_11_out), .in_1(FL_i), .out(multiplexer_20_out));
  and and_3 (and_3_out, nand_3_out, nand_4_out, FL_sel);
  reg8x4 u_R2 (.C(C), .D(multiplexer_12_out), .E(R2_e), .D_o(R2));
  reg8x4 u_R6 (.C(C), .D(multiplexer_13_out), .E(R6_e), .D_o(R6));
  reg8x4 u_R10 (.C(C), .D(multiplexer_14_out), .E(R10_e), .D_o(R10));
  reg8x4 u_R14 (.C(C), .D(multiplexer_15_out), .E(R14_e), .D_o(R14));
  reg8x4 u_R18 (.C(C), .D(multiplexer_16_out), .E(R18_e), .D_o(R18));
  reg8x4 u_R22 (.C(C), .D(multiplexer_17_out), .E(R22_e), .D_o(R22));
  BitExtender #(.inputBits(1), .outputBits(4)) bitextender_3 (.in(PCS_e), .out(bitextender_3_out));
  BitExtender #(.inputBits(1), .outputBits(4)) bitextender_4 (.in(PCA_e), .out(bitextender_4_out));
  Multiplexer #(.Bits(4)) multiplexer_21 (
    .sel(SCA_sel), .in_0(SCA_e_t), .in_1(bitextender_1_out), .out(multiplexer_21_out));
  Multiplexer #(.Bits(4)) multiplexer_22 (
    .sel(SC_sel), .in_0(SCA_e_t), .in_1(bitextender_2_out), .out(multiplexer_22_out));
  Multiplexer #(.Bits(4)) multiplexer_23 (.sel(and_3_out), .in_0(FL_e_t), .in_1(FL_e), .out(multiplexer_23_out));
  reg8x4 PC (.C(C), .D(PCS_i), .E(bitextender_3_out), .D_o(PCS_O));
  reg8x4 PC_2 (.C(C), .D(PCA_i), .E(bitextender_4_out), .D_o(PCA_O));
  reg8x4 SC (.C(C), .D(multiplexer_18_out), .E(multiplexer_21_out), .D_o(SCA_O));
  reg8x4 SC_2 (.C(C), .D(multiplexer_19_out), .E(multiplexer_22_out), .D_o(SCS_O));
  reg8x4 FL (.C(C), .D(multiplexer_20_out), .E(multiplexer_23_out), .D_o({FL_O[31:7], FL_d_o[6], FL_O[5:0]}));
  Multiplexer #(.Bits(32)) multiplexer_24 (
    .sel(RM3), .in_0({R1_i, D1[7:0]}), .in_1({R2_i, D2[7:0]}), .out(multiplexer_24_out));
  Multiplexer #(.Bits(32)) multiplexer_25 (
    .sel(RM7), .in_0({R1_i, D1[7:0]}), .in_1({R2_i, D2[7:0]}), .out(multiplexer_25_out));
  Multiplexer #(.Bits(32)) multiplexer_26 (
    .sel(RM11), .in_0({R1_i, D1[7:0]}), .in_1({R2_i, D2[7:0]}), .out(multiplexer_26_out));
  Multiplexer #(.Bits(32)) multiplexer_27 (
    .sel(RM15), .in_0({R1_i, D1[7:0]}), .in_1({R2_i, D2[7:0]}), .out(multiplexer_27_out));
  Multiplexer #(.Bits(32)) multiplexer_28 (
    .sel(RM19), .in_0({R1_i, D1[7:0]}), .in_1({R2_i, D2[7:0]}), .out(multiplexer_28_out));
  Multiplexer #(.Bits(32)) multiplexer_29 (
    .sel(RM23), .in_0({R1_i, D1[7:0]}), .in_1({R2_i, D2[7:0]}), .out(multiplexer_29_out));
  reg8x4 u_R3 (.C(C), .D(multiplexer_24_out), .E(R3_e), .D_o(R3));
  reg8x4 u_R7 (.C(C), .D(multiplexer_25_out), .E(R7_e), .D_o(R7));
  reg8x4 u_R11 (.C(C), .D(multiplexer_26_out), .E(R11_e), .D_o(R11));
  reg8x4 u_R15 (.C(C), .D(multiplexer_27_out), .E(R15_e), .D_o(R15));
  reg8x4 u_R19 (.C(C), .D(multiplexer_28_out), .E(R19_e), .D_o(R19));
  reg8x4 u_R23 (.C(C), .D(multiplexer_29_out), .E(R23_e), .D_o(R23));
  Multiplexer #(.Bits(32)) multiplexer_30 (
    .sel(RM4), .in_0({R1_i, D1[7:0]}), .in_1({R2_i, D2[7:0]}), .out(multiplexer_30_out));
  Multiplexer #(.Bits(32)) multiplexer_31 (
    .sel(RM8), .in_0({R1_i, D1[7:0]}), .in_1({R2_i, D2[7:0]}), .out(multiplexer_31_out));
  Multiplexer #(.Bits(32)) multiplexer_32 (
    .sel(RM12), .in_0({R1_i, D1[7:0]}), .in_1({R2_i, D2[7:0]}), .out(multiplexer_32_out));
  Multiplexer #(.Bits(32)) multiplexer_33 (
    .sel(RM16), .in_0({R1_i, D1[7:0]}), .in_1({R2_i, D2[7:0]}), .out(multiplexer_33_out));
  Multiplexer #(.Bits(32)) multiplexer_34 (
    .sel(RM20), .in_0({R1_i, D1[7:0]}), .in_1({R2_i, D2[7:0]}), .out(multiplexer_34_out));
  Multiplexer #(.Bits(32)) multiplexer_35 (
    .sel(RM24), .in_0({R1_i, D1[7:0]}), .in_1({R2_i, D2[7:0]}), .out(multiplexer_35_out));
  reg8x4 u_R4 (.C(C), .D(multiplexer_30_out), .E(R4_e), .D_o(R4));
  reg8x4 u_R8 (.C(C), .D(multiplexer_31_out), .E(R8_e), .D_o(R8));
  reg8x4 u_R12 (.C(C), .D(multiplexer_32_out), .E(R12_e), .D_o(R12));
  reg8x4 u_R16 (.C(C), .D(multiplexer_33_out), .E(R16_e), .D_o(R16));
  reg8x4 u_R20 (.C(C), .D(multiplexer_34_out), .E(R20_e), .D_o(R20));
  reg8x4 u_R24 (.C(C), .D(multiplexer_35_out), .E(R24_e), .D_o(R24));
  and and_4 (a_mux_c2, MA[2], MA[1]);
  nor nor_1 (a_mux_d1, MA[2], MA[1], MA[0]);
  and and_5 (b_mux_c2, MB[2], MB[1]);
  nor nor_2 (b_mux_d1, MB[2], MB[1], MB[0]);
  nor nor_3 (nor_3_out, MW1[2], MW1[1], MW1[0]);
  nor nor_4 (nor_4_out, MW2[2], MW2[1], MW2[0]);
  and and_6 (a_mux_a1, MA[1], MA[0]);
  and and_7 (a_mux_a2, MA[2], ~MA[1], ~MA[0]);  // And
  not not_1 (a_mux_d2, MA[1]);
  and and_8 (b_mux_a1, MB[1], MB[0]);
  and and_9 (b_mux_a2, MB[2], ~MB[1], ~MB[0]);  // And
  not not_2 (b_mux_d2, MB[1]);
  xor xor_1 (xor_1_out, MW1[0], MW1[1]);
  xor xor_2 (xor_2_out, MW2[0], MW2[1]);
  nor nor_5 (or_1_out[3], MW1[1], MW1[0]);
  or or_1 (or_1_out[1], nor_3_out, MW1[0]);
  or or_2 (or_1_out[0], xor_1_out, nor_3_out);
  nor nor_6 (or_3_out[3], MW2[1], MW2[0]);
  or or_3 (or_3_out[1], nor_4_out, MW2[0]);
  or or_4 (or_3_out[0], xor_2_out, nor_4_out);
  // Probe R1 on R1
  // Probe R2 on R2
  // Probe R3 on R3
  // Probe R4 on R4
  // Probe R5 on R5
  // Probe R6 on R6
  // Probe R7 on R7
  // Probe R8 on R8
  // Probe R9 on R9
  // Probe R10 on R10
  // Probe R11 on R11
  // Probe R12 on R12
  // Probe R13 on R13
  // Probe R14 on R14
  // Probe R15 on R15
  // Probe R16 on R16
  // Probe R17 on R17
  // Probe R18 on R18
  // Probe R19 on R19
  // Probe R20 on R20
  // Probe R21 on R21
  // Probe R22 on R22
  // Probe R23 on R23
  // Probe R24 on R24
  // Probe R25 on R25
  // Probe R26 on SBP
  // Probe R27 on {32{1'b0}}
  // Probe R28 on 32'h1
  // Probe R29 on {32{1'b1}}
  // Probe R30 on PC_read
  // Probe R31 on SCS_O
  // Probe R32 on {FL_O[31:7], 1'b1, FL_O[5:0]}
  Multiplexer #(.Bits(8)) multiplexer_36 (
    .sel(a_mux_a2), .in_0(R_A_t[15:8]), .in_1(R_A_t[31:24]), .out(multiplexer_36_out));
  Multiplexer #(.Bits(8)) multiplexer_37 (
    .sel(a_mux_a1), .in_0(R_A_t[7:0]), .in_1(R_A_t[15:8]), .out(multiplexer_37_out));
  Multiplexer #(.Bits(8)) multiplexer_38 (
    .sel(b_mux_a2), .in_0(R_B_t[15:8]), .in_1(R_B_t[31:24]), .out(multiplexer_38_out));
  Multiplexer #(.Bits(8)) multiplexer_39 (
    .sel(b_mux_a1), .in_0(R_B_t[7:0]), .in_1(R_B_t[15:8]), .out(multiplexer_39_out));
  assign GR1_e = {{2{or_1_out[3]}}, or_1_out[1:0]} & {4{E1}};  // And and_10, 4 bits wide
  assign GR2_e = {{2{or_3_out[3]}}, or_3_out[1:0]} & {4{E2}};  // And and_11, 4 bits wide
  Multiplexer #(.Bits(8)) multiplexer_40 (
    .sel(a_mux_a2), .in_0(multiplexer_37_out), .in_1(R_A_t[23:16]), .out(R_A[7:0]));
  Multiplexer #(.Bits(8)) multiplexer_41 (
    .sel(b_mux_a2), .in_0(multiplexer_39_out), .in_1(R_B_t[23:16]), .out(R_B[7:0]));
  BitExtender #(.inputBits(1), .outputBits(8)) bitextender_5 (.in(a_mux_d1), .out(bitextender_5_out));
  and and_12 (and_12_out, MA[2], multiplexer_42_out);
  Multiplexer multiplexer_42 (.sel(MA[1]), .in_0(multiplexer_36_out[7]), .in_1(R_A[7]), .out(multiplexer_42_out));
  and and_13 (and_13_out, R_A[7], a_mux_c2);
  BitExtender #(.inputBits(1), .outputBits(8)) bitextender_6 (.in(b_mux_d1), .out(bitextender_6_out));
  and and_14 (and_14_out, MB[2], multiplexer_43_out);
  Multiplexer multiplexer_43 (.sel(MB[1]), .in_0(multiplexer_38_out[7]), .in_1(R_B[7]), .out(multiplexer_43_out));
  and and_15 (and_15_out, R_B[7], b_mux_c2);
  Multiplexer #(.Selector_Bits(5), .Bits(32)) multiplexer_44 (
    .sel(RA), .in_0(R1), .in_1(R2), .in_2(R3), .in_3(R4), .in_4(R5), .in_5(R6), .in_6(R7), .in_7(R8),
    .in_8(R9), .in_9(R10), .in_10(R11), .in_11(R12), .in_12(R13), .in_13(R14), .in_14(R15), .in_15(R16),
    .in_16(R17), .in_17(R18), .in_18(R19), .in_19(R20), .in_20(R21), .in_21(R22), .in_22(R23), .in_23(R24),
    .in_24(R25), .in_25(SBP), .in_26({32{1'b0}}), .in_27(32'h1), .in_28({32{1'b1}}), .in_29(PC_read),
    .in_30(SCS_O), .in_31({FL_O[31:7], 1'b1, FL_O[5:0]}), .out(R_A_t));
  assign and_16_out = bitextender_5_out & R_A_t[31:24];  // And and_16, 8 bits wide
  assign and_17_out = bitextender_5_out & R_A_t[23:16];  // And and_17, 8 bits wide
  BitExtender #(.inputBits(1), .outputBits(8)) bitextender_7 (.in(a_mux_d2), .out(bitextender_7_out));
  assign and_18_out = bitextender_6_out & R_B_t[31:24];  // And and_18, 8 bits wide
  assign and_19_out = bitextender_6_out & R_B_t[23:16];  // And and_19, 8 bits wide
  BitExtender #(.inputBits(1), .outputBits(8)) bitextender_8 (.in(b_mux_d2), .out(bitextender_8_out));
  Multiplexer #(.Bits(8)) multiplexer_45 (.sel(MW1[2]), .in_0(D1[31:24]), .in_1(D1[15:8]), .out(R1_i[31:24]));
  Multiplexer #(.Bits(8)) multiplexer_46 (.sel(MW1[2]), .in_0(D1[23:16]), .in_1(D1[7:0]), .out(R1_i[23:16]));
  Multiplexer #(.Bits(8)) multiplexer_47 (.sel(MW1[1]), .in_0(D1[15:8]), .in_1(D1[7:0]), .out(R1_i[15:8]));
  Multiplexer #(.Bits(8)) multiplexer_48 (.sel(MW2[2]), .in_0(D2[31:24]), .in_1(D2[15:8]), .out(R2_i[31:24]));
  Multiplexer #(.Bits(8)) multiplexer_49 (.sel(MW2[2]), .in_0(D2[23:16]), .in_1(D2[7:0]), .out(R2_i[23:16]));
  Multiplexer #(.Bits(8)) multiplexer_50 (.sel(MW2[1]), .in_0(D2[15:8]), .in_1(D2[7:0]), .out(R2_i[15:8]));
  BitExtender #(.inputBits(1), .outputBits(8)) bitextender_9 (.in(and_12_out), .out(bitextender_9_out));
  assign and_20_out = bitextender_7_out & multiplexer_36_out;  // And and_20, 8 bits wide
  BitExtender #(.inputBits(1), .outputBits(8)) bitextender_10 (.in(and_13_out), .out(bitextender_10_out));
  BitExtender #(.inputBits(1), .outputBits(8)) bitextender_11 (.in(and_14_out), .out(bitextender_11_out));
  assign and_21_out = bitextender_8_out & multiplexer_38_out;  // And and_21, 8 bits wide
  BitExtender #(.inputBits(1), .outputBits(8)) bitextender_12 (.in(and_15_out), .out(bitextender_12_out));
  Multiplexer #(.Selector_Bits(5), .Bits(32)) multiplexer_51 (
    .sel(RB), .in_0(R1), .in_1(R2), .in_2(R3), .in_3(R4), .in_4(R5), .in_5(R6), .in_6(R7), .in_7(R8),
    .in_8(R9), .in_9(R10), .in_10(R11), .in_11(R12), .in_12(R13), .in_13(R14), .in_14(R15), .in_15(R16),
    .in_16(R17), .in_17(R18), .in_18(R19), .in_19(R20), .in_20(R21), .in_21(R22), .in_22(R23), .in_23(R24),
    .in_24(R25), .in_25(SBP), .in_26({32{1'b0}}), .in_27(32'h1), .in_28({32{1'b1}}), .in_29(PC_read),
    .in_30(SCS_O), .in_31({FL_O[31:7], 1'b1, FL_O[5:0]}), .out(R_B_t));
  assign R_A[31:24] = and_16_out | bitextender_9_out;  // Or or_5, 8 bits wide
  assign R_A[23:16] = and_17_out | bitextender_9_out;  // Or or_6, 8 bits wide
  assign R_A[15:8] = and_20_out | bitextender_10_out;  // Or or_7, 8 bits wide
  assign R_B[31:24] = and_18_out | bitextender_11_out;  // Or or_8, 8 bits wide
  assign R_B[23:16] = and_19_out | bitextender_11_out;  // Or or_9, 8 bits wide
  assign R_B[15:8] = and_21_out | bitextender_12_out;  // Or or_10, 8 bits wide
  Demultiplexer #(.Selector_Bits(5)) demultiplexer_1 (
    .sel(RW2), .in(E2), .out_0(RM1), .out_1(RM2), .out_2(RM3), .out_3(RM4), .out_4(RM5), .out_5(RM6),
    .out_6(RM7), .out_7(RM8), .out_8(RM9), .out_9(RM10), .out_10(RM11), .out_11(RM12), .out_12(RM13),
    .out_13(RM14), .out_14(RM15), .out_15(RM16), .out_16(RM17), .out_17(RM18), .out_18(RM19), .out_19(RM20),
    .out_20(RM21), .out_21(RM22), .out_22(RM23), .out_23(RM24), .out_24(RM25), .out_25(SBPM), .out_30(SCAM),
    .out_31(FLM));  // open: out_26, out_27, out_28, out_29
  Demultiplexer #(.Selector_Bits(5)) demultiplexer_2 (
    .sel(RW1), .in(GR1_e[0]), .out_0(demultiplexer_2_out_0[0]), .out_1(demultiplexer_2_out_0[1]),
    .out_2(demultiplexer_2_out_0[2]), .out_3(demultiplexer_2_out_0[3]), .out_4(demultiplexer_2_out_0[4]),
    .out_5(demultiplexer_2_out_0[5]), .out_6(demultiplexer_2_out_0[6]), .out_7(demultiplexer_2_out_0[7]),
    .out_8(demultiplexer_2_out_0[8]), .out_9(demultiplexer_2_out_0[9]), .out_10(demultiplexer_2_out_0[10]),
    .out_11(demultiplexer_2_out_0[11]), .out_12(demultiplexer_2_out_0[12]),
    .out_13(demultiplexer_2_out_0[13]), .out_14(demultiplexer_2_out_0[14]),
    .out_15(demultiplexer_2_out_0[15]), .out_16(demultiplexer_2_out_0[16]),
    .out_17(demultiplexer_2_out_0[17]), .out_18(demultiplexer_2_out_0[18]),
    .out_19(demultiplexer_2_out_0[19]), .out_20(demultiplexer_2_out_0[20]),
    .out_21(demultiplexer_2_out_0[21]), .out_22(demultiplexer_2_out_0[22]),
    .out_23(demultiplexer_2_out_0[23]), .out_24(demultiplexer_2_out_0[24]),
    .out_25(demultiplexer_2_out_0[25]), .out_26(demultiplexer_2_out_0[26]),
    .out_27(demultiplexer_2_out_0[27]), .out_28(demultiplexer_2_out_0[28]),
    .out_29(demultiplexer_2_out_0[29]), .out_30(demultiplexer_2_out_0[30]), .out_31(demultiplexer_2_out_0[31]));
  Demultiplexer #(.Selector_Bits(5)) demultiplexer_3 (
    .sel(RW1), .in(GR1_e[1]), .out_0(demultiplexer_3_out_0[0]), .out_1(demultiplexer_3_out_0[1]),
    .out_2(demultiplexer_3_out_0[2]), .out_3(demultiplexer_3_out_0[3]), .out_4(demultiplexer_3_out_0[4]),
    .out_5(demultiplexer_3_out_0[5]), .out_6(demultiplexer_3_out_0[6]), .out_7(demultiplexer_3_out_0[7]),
    .out_8(demultiplexer_3_out_0[8]), .out_9(demultiplexer_3_out_0[9]), .out_10(demultiplexer_3_out_0[10]),
    .out_11(demultiplexer_3_out_0[11]), .out_12(demultiplexer_3_out_0[12]),
    .out_13(demultiplexer_3_out_0[13]), .out_14(demultiplexer_3_out_0[14]),
    .out_15(demultiplexer_3_out_0[15]), .out_16(demultiplexer_3_out_0[16]),
    .out_17(demultiplexer_3_out_0[17]), .out_18(demultiplexer_3_out_0[18]),
    .out_19(demultiplexer_3_out_0[19]), .out_20(demultiplexer_3_out_0[20]),
    .out_21(demultiplexer_3_out_0[21]), .out_22(demultiplexer_3_out_0[22]),
    .out_23(demultiplexer_3_out_0[23]), .out_24(demultiplexer_3_out_0[24]),
    .out_25(demultiplexer_3_out_0[25]), .out_26(demultiplexer_3_out_0[26]),
    .out_27(demultiplexer_3_out_0[27]), .out_28(demultiplexer_3_out_0[28]),
    .out_29(demultiplexer_3_out_0[29]), .out_30(demultiplexer_3_out_0[30]), .out_31(demultiplexer_3_out_0[31]));
  Demultiplexer #(.Selector_Bits(5)) demultiplexer_4 (
    .sel(RW1), .in(GR1_e[2]), .out_0(demultiplexer_4_out_0[0]), .out_1(demultiplexer_4_out_0[1]),
    .out_2(demultiplexer_4_out_0[2]), .out_3(demultiplexer_4_out_0[3]), .out_4(demultiplexer_4_out_0[4]),
    .out_5(demultiplexer_4_out_0[5]), .out_6(demultiplexer_4_out_0[6]), .out_7(demultiplexer_4_out_0[7]),
    .out_8(demultiplexer_4_out_0[8]), .out_9(demultiplexer_4_out_0[9]), .out_10(demultiplexer_4_out_0[10]),
    .out_11(demultiplexer_4_out_0[11]), .out_12(demultiplexer_4_out_0[12]),
    .out_13(demultiplexer_4_out_0[13]), .out_14(demultiplexer_4_out_0[14]),
    .out_15(demultiplexer_4_out_0[15]), .out_16(demultiplexer_4_out_0[16]),
    .out_17(demultiplexer_4_out_0[17]), .out_18(demultiplexer_4_out_0[18]),
    .out_19(demultiplexer_4_out_0[19]), .out_20(demultiplexer_4_out_0[20]),
    .out_21(demultiplexer_4_out_0[21]), .out_22(demultiplexer_4_out_0[22]),
    .out_23(demultiplexer_4_out_0[23]), .out_24(demultiplexer_4_out_0[24]),
    .out_25(demultiplexer_4_out_0[25]), .out_26(demultiplexer_4_out_0[26]),
    .out_27(demultiplexer_4_out_0[27]), .out_28(demultiplexer_4_out_0[28]),
    .out_29(demultiplexer_4_out_0[29]), .out_30(demultiplexer_4_out_0[30]), .out_31(demultiplexer_4_out_0[31]));
  Demultiplexer #(.Selector_Bits(5)) demultiplexer_5 (
    .sel(RW1), .in(GR1_e[3]), .out_0(demultiplexer_5_out_0[0]), .out_1(demultiplexer_5_out_0[1]),
    .out_2(demultiplexer_5_out_0[2]), .out_3(demultiplexer_5_out_0[3]), .out_4(demultiplexer_5_out_0[4]),
    .out_5(demultiplexer_5_out_0[5]), .out_6(demultiplexer_5_out_0[6]), .out_7(demultiplexer_5_out_0[7]),
    .out_8(demultiplexer_5_out_0[8]), .out_9(demultiplexer_5_out_0[9]), .out_10(demultiplexer_5_out_0[10]),
    .out_11(demultiplexer_5_out_0[11]), .out_12(demultiplexer_5_out_0[12]),
    .out_13(demultiplexer_5_out_0[13]), .out_14(demultiplexer_5_out_0[14]),
    .out_15(demultiplexer_5_out_0[15]), .out_16(demultiplexer_5_out_0[16]),
    .out_17(demultiplexer_5_out_0[17]), .out_18(demultiplexer_5_out_0[18]),
    .out_19(demultiplexer_5_out_0[19]), .out_20(demultiplexer_5_out_0[20]),
    .out_21(demultiplexer_5_out_0[21]), .out_22(demultiplexer_5_out_0[22]),
    .out_23(demultiplexer_5_out_0[23]), .out_24(demultiplexer_5_out_0[24]),
    .out_25(demultiplexer_5_out_0[25]), .out_26(demultiplexer_5_out_0[26]),
    .out_27(demultiplexer_5_out_0[27]), .out_28(demultiplexer_5_out_0[28]),
    .out_29(demultiplexer_5_out_0[29]), .out_30(demultiplexer_5_out_0[30]), .out_31(demultiplexer_5_out_0[31]));
  Demultiplexer #(.Selector_Bits(5)) demultiplexer_6 (
    .sel(RW2), .in(GR2_e[0]), .out_0(demultiplexer_6_out_0[0]), .out_1(demultiplexer_6_out_0[1]),
    .out_2(demultiplexer_6_out_0[2]), .out_3(demultiplexer_6_out_0[3]), .out_4(demultiplexer_6_out_0[4]),
    .out_5(demultiplexer_6_out_0[5]), .out_6(demultiplexer_6_out_0[6]), .out_7(demultiplexer_6_out_0[7]),
    .out_8(demultiplexer_6_out_0[8]), .out_9(demultiplexer_6_out_0[9]), .out_10(demultiplexer_6_out_0[10]),
    .out_11(demultiplexer_6_out_0[11]), .out_12(demultiplexer_6_out_0[12]),
    .out_13(demultiplexer_6_out_0[13]), .out_14(demultiplexer_6_out_0[14]),
    .out_15(demultiplexer_6_out_0[15]), .out_16(demultiplexer_6_out_0[16]),
    .out_17(demultiplexer_6_out_0[17]), .out_18(demultiplexer_6_out_0[18]),
    .out_19(demultiplexer_6_out_0[19]), .out_20(demultiplexer_6_out_0[20]),
    .out_21(demultiplexer_6_out_0[21]), .out_22(demultiplexer_6_out_0[22]),
    .out_23(demultiplexer_6_out_0[23]), .out_24(demultiplexer_6_out_0[24]),
    .out_25(demultiplexer_6_out_0[25]), .out_26(demultiplexer_6_out_0[26]),
    .out_27(demultiplexer_6_out_0[27]), .out_28(demultiplexer_6_out_0[28]),
    .out_29(demultiplexer_6_out_0[29]), .out_30(demultiplexer_6_out_0[30]), .out_31(demultiplexer_6_out_0[31]));
  Demultiplexer #(.Selector_Bits(5)) demultiplexer_7 (
    .sel(RW2), .in(GR2_e[1]), .out_0(demultiplexer_7_out_0[0]), .out_1(demultiplexer_7_out_0[1]),
    .out_2(demultiplexer_7_out_0[2]), .out_3(demultiplexer_7_out_0[3]), .out_4(demultiplexer_7_out_0[4]),
    .out_5(demultiplexer_7_out_0[5]), .out_6(demultiplexer_7_out_0[6]), .out_7(demultiplexer_7_out_0[7]),
    .out_8(demultiplexer_7_out_0[8]), .out_9(demultiplexer_7_out_0[9]), .out_10(demultiplexer_7_out_0[10]),
    .out_11(demultiplexer_7_out_0[11]), .out_12(demultiplexer_7_out_0[12]),
    .out_13(demultiplexer_7_out_0[13]), .out_14(demultiplexer_7_out_0[14]),
    .out_15(demultiplexer_7_out_0[15]), .out_16(demultiplexer_7_out_0[16]),
    .out_17(demultiplexer_7_out_0[17]), .out_18(demultiplexer_7_out_0[18]),
    .out_19(demultiplexer_7_out_0[19]), .out_20(demultiplexer_7_out_0[20]),
    .out_21(demultiplexer_7_out_0[21]), .out_22(demultiplexer_7_out_0[22]),
    .out_23(demultiplexer_7_out_0[23]), .out_24(demultiplexer_7_out_0[24]),
    .out_25(demultiplexer_7_out_0[25]), .out_26(demultiplexer_7_out_0[26]),
    .out_27(demultiplexer_7_out_0[27]), .out_28(demultiplexer_7_out_0[28]),
    .out_29(demultiplexer_7_out_0[29]), .out_30(demultiplexer_7_out_0[30]), .out_31(demultiplexer_7_out_0[31]));
  Demultiplexer #(.Selector_Bits(5)) demultiplexer_8 (
    .sel(RW2), .in(GR2_e[2]), .out_0(demultiplexer_8_out_0[0]), .out_1(demultiplexer_8_out_0[1]),
    .out_2(demultiplexer_8_out_0[2]), .out_3(demultiplexer_8_out_0[3]), .out_4(demultiplexer_8_out_0[4]),
    .out_5(demultiplexer_8_out_0[5]), .out_6(demultiplexer_8_out_0[6]), .out_7(demultiplexer_8_out_0[7]),
    .out_8(demultiplexer_8_out_0[8]), .out_9(demultiplexer_8_out_0[9]), .out_10(demultiplexer_8_out_0[10]),
    .out_11(demultiplexer_8_out_0[11]), .out_12(demultiplexer_8_out_0[12]),
    .out_13(demultiplexer_8_out_0[13]), .out_14(demultiplexer_8_out_0[14]),
    .out_15(demultiplexer_8_out_0[15]), .out_16(demultiplexer_8_out_0[16]),
    .out_17(demultiplexer_8_out_0[17]), .out_18(demultiplexer_8_out_0[18]),
    .out_19(demultiplexer_8_out_0[19]), .out_20(demultiplexer_8_out_0[20]),
    .out_21(demultiplexer_8_out_0[21]), .out_22(demultiplexer_8_out_0[22]),
    .out_23(demultiplexer_8_out_0[23]), .out_24(demultiplexer_8_out_0[24]),
    .out_25(demultiplexer_8_out_0[25]), .out_26(demultiplexer_8_out_0[26]),
    .out_27(demultiplexer_8_out_0[27]), .out_28(demultiplexer_8_out_0[28]),
    .out_29(demultiplexer_8_out_0[29]), .out_30(demultiplexer_8_out_0[30]), .out_31(demultiplexer_8_out_0[31]));
  Demultiplexer #(.Selector_Bits(5)) demultiplexer_9 (
    .sel(RW2), .in(GR2_e[3]), .out_0(demultiplexer_9_out_0[0]), .out_1(demultiplexer_9_out_0[1]),
    .out_2(demultiplexer_9_out_0[2]), .out_3(demultiplexer_9_out_0[3]), .out_4(demultiplexer_9_out_0[4]),
    .out_5(demultiplexer_9_out_0[5]), .out_6(demultiplexer_9_out_0[6]), .out_7(demultiplexer_9_out_0[7]),
    .out_8(demultiplexer_9_out_0[8]), .out_9(demultiplexer_9_out_0[9]), .out_10(demultiplexer_9_out_0[10]),
    .out_11(demultiplexer_9_out_0[11]), .out_12(demultiplexer_9_out_0[12]),
    .out_13(demultiplexer_9_out_0[13]), .out_14(demultiplexer_9_out_0[14]),
    .out_15(demultiplexer_9_out_0[15]), .out_16(demultiplexer_9_out_0[16]),
    .out_17(demultiplexer_9_out_0[17]), .out_18(demultiplexer_9_out_0[18]),
    .out_19(demultiplexer_9_out_0[19]), .out_20(demultiplexer_9_out_0[20]),
    .out_21(demultiplexer_9_out_0[21]), .out_22(demultiplexer_9_out_0[22]),
    .out_23(demultiplexer_9_out_0[23]), .out_24(demultiplexer_9_out_0[24]),
    .out_25(demultiplexer_9_out_0[25]), .out_26(demultiplexer_9_out_0[26]),
    .out_27(demultiplexer_9_out_0[27]), .out_28(demultiplexer_9_out_0[28]),
    .out_29(demultiplexer_9_out_0[29]), .out_30(demultiplexer_9_out_0[30]), .out_31(demultiplexer_9_out_0[31]));
  assign {FL_e_t[0], SCA_e_t[0], or_11_out, SBP_e[0], R25_e[0], R24_e[0], R23_e[0], R22_e[0], R21_e[0], R20_e[0], R19_e[0], R18_e[0], R17_e[0], R16_e[0], R15_e[0], R14_e[0], R13_e[0], R12_e[0], R11_e[0], R10_e[0], R9_e[0], R8_e[0], R7_e[0], R6_e[0], R5_e[0], R4_e[0], R3_e[0], R2_e[0], R1_e[0]} = demultiplexer_2_out_0 | demultiplexer_6_out_0;  // Or or_11, 32 bits wide
  assign {FL_e_t[1], SCA_e_t[1], or_12_out, SBP_e[1], R25_e[1], R24_e[1], R23_e[1], R22_e[1], R21_e[1], R20_e[1], R19_e[1], R18_e[1], R17_e[1], R16_e[1], R15_e[1], R14_e[1], R13_e[1], R12_e[1], R11_e[1], R10_e[1], R9_e[1], R8_e[1], R7_e[1], R6_e[1], R5_e[1], R4_e[1], R3_e[1], R2_e[1], R1_e[1]} = demultiplexer_3_out_0 | demultiplexer_7_out_0;  // Or or_12, 32 bits wide
  assign {FL_e_t[2], SCA_e_t[2], or_13_out, SBP_e[2], R25_e[2], R24_e[2], R23_e[2], R22_e[2], R21_e[2], R20_e[2], R19_e[2], R18_e[2], R17_e[2], R16_e[2], R15_e[2], R14_e[2], R13_e[2], R12_e[2], R11_e[2], R10_e[2], R9_e[2], R8_e[2], R7_e[2], R6_e[2], R5_e[2], R4_e[2], R3_e[2], R2_e[2], R1_e[2]} = demultiplexer_4_out_0 | demultiplexer_8_out_0;  // Or or_13, 32 bits wide
  assign {FL_e_t[3], SCA_e_t[3], or_14_out, SBP_e[3], R25_e[3], R24_e[3], R23_e[3], R22_e[3], R21_e[3], R20_e[3], R19_e[3], R18_e[3], R17_e[3], R16_e[3], R15_e[3], R14_e[3], R13_e[3], R12_e[3], R11_e[3], R10_e[3], R9_e[3], R8_e[3], R7_e[3], R6_e[3], R5_e[3], R4_e[3], R3_e[3], R2_e[3], R1_e[3]} = demultiplexer_5_out_0 | demultiplexer_9_out_0;  // Or or_14, 32 bits wide

  assign FL_O[6] = 1'b1;

  // Other names for the same wires on the sheet: FL (some bits) = {FL_O[31:7], FL_O[5:0]}; D_A[31:0] = R_A;
  //   D_B[31:0] = R_B; A_mode[2:0] = MA; a_mux_b1 = MA[1]; a_mux_c1 = MA[2]; B_mode[2:0] = MB; b_mux_b1 = MB[1];
  //   b_mux_c1 = MB[2]; D1_I[31:0] = D1; R1_i[7:0] = D1[7:0]; D2_I[31:0] = D2; R2_i[7:0] = D2[7:0];
  //   FL_e__EX[3:0] = FL_e; PCA[31:0] = PCA_O; PCA_e__EX = PCA_e; PCS[31:0] = PCS_O; PCS_e__EX = PCS_e;
  //   RA_sel[4:0] = RA; RB_sel[4:0] = RB; RW1_sel[4:0] = RW1; RW2_sel[4:0] = RW2; SCA[31:0] = SCA_O;
  //   SCA_e__EX = SCA_e; SCS[31:0] = SCS_O; SCS_e__EX = SCS_e; SCS_sel = SC_sel; W1_mode[2:0] = MW1;
  //   w1_mux_3 = MW1[1]; w1_mux_1 = MW1[2]; w1_mux_2 = MW1[2]; W2_mode[2:0] = MW2; w2_mux_3 = MW2[1];
  //   w2_mux_1 = MW2[2]; w2_mux_2 = MW2[2]

  // Notes on the sheet:
  //   FL_i: data input for FL
  //   FL_sel: enable FL extern mode
  //   FL_e: FL register enable
  //   MW1: write mode:
  //   0: 32
  //   1: 16L
  //   2: 8L
  //   3: 8H
  //   4: 16H
  //   5: S16L (=16L)
  //   6: S8L (=8L)
  //   7: S8H (=8H)
  //   RW1: register to write:
  //   0~25: general
  //   26: zero
  //   27: one
  //   28: full
  //   29: program counter
  //   30: stack counter
  //   31: flag
  //   RA: register to read:
  //   0~25: general
  //   26: zero
  //   27: one
  //   28: full
  //   29: program counter
  //   30: stack counter
  //   31: flag
  //   RB: register to read:
  //   0~25: general
  //   26: zero
  //   27: one
  //   28: full
  //   29: program counter
  //   30: stack counter
  //   31: flag
  //   MA: read mode:
  //   0: 32
  //   1: 16L
  //   2: 8L
  //   3: 8H
  //   4: 16H
  //   5: S16L
  //   6: S8L
  //   7: S8H
  //   MB: read mode:
  //   0: 32
  //   1: 16L
  //   2: 8L
  //   3: 8H
  //   4: 16H
  //   5: S16L
  //   6: S8L
  //   7: S8H
  //   R_A: register out a
  //   R_B: register out b
  //   PCS_O: speculative PC out
  //   FL_O: FL out
  //   E1: enable
  //   D1: data in
  //   PCS_i: data input for speculative PC
  //   PCS_e: speculative PC register enable
  //   SCS_O: speculative SC out
  //   SCA_sel: enable architectual SC extern mode
  //   SCS_e: speculative SC register enable
  //   SCS_i: data input for speculative SC
  //   D2: data in
  //   MW2: write mode:
  //   0: 32
  //   1: 16L
  //   2: 8L
  //   3: 8H
  //   4: 16H
  //   5: S16L (=16L)
  //   6: S8L (=8L)
  //   7: S8H (=8H)
  //   RW2: register to write:
  //   0~25: general
  //   26: zero
  //   27: one
  //   28: full
  //   29: program counter
  //   30: stack counter
  //   31: flag
  //   PCA_i: data input for architectual PC
  //   PCA_e: architectual PC register enable
  //   PCA_O: architectual PC out
  //   SCA_e: speculative SC register enable
  //   SCA_i: data input for speculative SC
  //   E2: enable
  //   PC_read: cur instruction's PC value
  //   SCA_O: architectual SC out
  //   SC_sel: speculative SC extern mode
endmodule
