// Digital circuit rom-test.dig as structural Verilog
module rom_test (
  input  [31:0] D2,
  input  [31:0] D1,
  input  ld1,
  input  C,
  input  [31:0] _2A,
  input  [31:0] _1A,
  input  [1:0] mode,
  input  ld2
);

  wire [3:1] mask;
  wire [7:0] bitextender_1_out, bitextender_2_out, bitextender_3_out, bitextender_4_out;
  wire [17:0] addr_plus_1;
  wire [31:0] and_1_out, multiplexer_1_out, multiplexer_2_out, R0, R1, R2, R3;

  ROM #(.AddrBits(18), .Bits(32)) u_R0 (.A(_1A[19:2]), .sel(1'b1), .D(R0));
  ROM #(.AddrBits(18), .Bits(32)) u_R1 (.A(addr_plus_1), .sel(1'b1), .D(R1));
  nor nor_1 (mask[3], mode[0], mode[1]);
  not not_1 (mask[1], mode[1]);
  Add #(.Bits(18), .generic("this.Bits=int(args.addrBits-2);")) add_1 (
    .a({18{1'b0}}), .b(_1A[19:2]), .c_i(1'b1), .s(addr_plus_1));  // open: c_o
  ROM #(.AddrBits(18), .Bits(32)) u_R2 (.A(_1A[19:2]), .sel(1'b1), .D(R2));
  ROM #(.AddrBits(18), .Bits(32)) u_R3 (.A(addr_plus_1), .sel(1'b1), .D(R3));
  BitExtender #(.inputBits(1), .outputBits(8)) bitextender_1 (.in(1'b1), .out(bitextender_1_out));
  BitExtender #(.inputBits(1), .outputBits(8)) bitextender_2 (.in(mask[1]), .out(bitextender_2_out));
  BitExtender #(.inputBits(1), .outputBits(8)) bitextender_3 (.in(mask[3]), .out(bitextender_3_out));
  BitExtender #(.inputBits(1), .outputBits(8)) bitextender_4 (.in(mask[3]), .out(bitextender_4_out));
  Multiplexer #(.Selector_Bits(2), .Bits(32)) multiplexer_1 (
    .sel(_1A[1:0]), .in_0(R0), .in_1({R1[7:0], R0[31:8]}), .in_2({R1[15:0], R0[31:16]}),
    .in_3({R1[23:0], R0[31:24]}), .out(multiplexer_1_out));
  Multiplexer #(.Selector_Bits(2), .Bits(32)) multiplexer_2 (
    .sel(_1A[1:0]), .in_0(R2), .in_1({R3[7:0], R2[31:8]}), .in_2({R3[15:0], R2[31:16]}),
    .in_3({R3[23:0], R2[31:24]}), .out(multiplexer_2_out));
  assign and_1_out = {bitextender_4_out, bitextender_3_out, bitextender_2_out, bitextender_1_out} & multiplexer_1_out;  // And and_1, 32 bits wide
  assign D1 = ld1 ? and_1_out : 32'bz;  // Driver driver_1
  assign D2 = ld2 ? multiplexer_2_out : 32'bz;  // Driver driver_2

  // Other names for the same wires on the sheet: mask[2] = mask[3]; A_0 = _1A[0]; A_01[1:0] = _1A[1:0]; A_1 = _1A[1];
  //   addr[17:0] = _1A[19:2]; md[1:0] = mode

  // Notes on the sheet:
  //   R0 loads rom.bin
  //   R1 loads rom.bin
  //   R2 loads rom.bin
  //   R3 loads rom.bin
endmodule
