// Digital circuit store-buffer-debug-old.dig as structural Verilog
module store_buffer_debug_old (
  input  W_d,
  input  C,
  input  [31:0] D,
  input  [31:0] A,
  input  [3:0] inst,
  input  [3:0] com1_id,
  input  [3:0] com2_id,
  input  com1,
  input  com2,
  input  ld_ep,
  input  [3:0] ld_id,
  input  epoch,
  input  [31:0] ld_addr,
  input  W_id,
  input  [3:0] inst_W,
  input  LD,
  input  [1:0] MD,
  input  clr,
  input  [3:0] clr_id,
  input  clr_ep,
  input  W_p,
  input  [31:0] PA,
  input  [3:0] inst_WP,
  output [31:0] D_O,
  output [31:0] PA_O,
  output V,
  output full,
  output ld_V,
  output [31:0] ld_D,
  output [3:0] id_O,
  output ep_O,
  output [1:0] MD_O
);

  wire and_5_out, and_6_out, and_7_out, and_8_out, and_13_out, and_16_out, and_17_out, and_18_out,
       and_19_out, and_22_out, and_27_out, and_28_out, and_29_out, and_30_out, and_34_out, and_38_out,
       and_39_out, and_40_out, and_41_out, and_46_out, comparator_1_eq, comparator_2_eq, comparator_3_eq,
       comparator_4_eq, comparator_5_eq, comparator_6_eq, comparator_7_eq, comparator_8_eq, comparator_9_eq,
       comparator_10_eq, comparator_11_eq, comparator_12_eq, comparator_13_eq, comparator_14_eq,
       comparator_15_eq, comparator_16_eq, comparator_17_eq, comparator_18_eq, comparator_19_eq,
       comparator_20_eq, inst_comp_1_a_new, inst_comp_2_a_new, inst_comp_3_a_new, inst_comp_4_a_new,
       inst_comp_5_a_new, inst_comp_6_a_new, inst_comp_7_a_new, inst_comp_8_a_new, M1_CLR, M1_CMP, M1_COM,
       M1_DE, M1_epoch, M1_IE, M1_OLD, M1_PE, M1_RS, M1_SEL, M1_SELP, M1_VO, M2_CLR, M2_CMP, M2_COM, M2_DE,
       M2_epoch, M2_IE, M2_OLD, M2_PE, M2_RS, M2_SEL, M2_SELP, M2_VO, M3_CLR, M3_CMP, M3_COM, M3_DE,
       M3_epoch, M3_IE, M3_OLD, M3_PE, M3_RS, M3_SEL, M3_SELP, M3_VO, M4_CLR, M4_CMP, M4_COM, M4_DE,
       M4_epoch, M4_IE, M4_OLD, M4_PE, M4_RS, M4_SEL, M4_SELP, M4_VO, or_2_out, or_4_out, or_5_out, or_6_out,
       or_8_out, or_10_out, or_11_out, or_13_out, priorityencoder_2_any, rs_ff_2_q, rs_ff_9_q, rs_ff_16_q,
       rs_ff_23_q, V_t;
  wire [1:0] empty_id, M1_MD, M2_MD, M3_MD, M4_MD, priorityencoder_1_num, sel_com;
  wire [3:0] and_1_out, and_9_out, and_23_out, and_31_out, and_42_out, bitextender_1_out, bitextender_2_out,
       bitextender_3_out, bitextender_4_out, bitextender_5_out, bitextender_6_out, bitextender_7_out,
       bitextender_8_out, bitextender_9_out, bitextender_10_out, demultiplexer_2_out_0, M1_inst, M2_inst,
       M3_inst, M4_inst, not_1_out, not_3_out, or_3_out, or_7_out, or_9_out, or_12_out, rs_ff_4_q,
       rs_ff_11_q, rs_ff_18_q, rs_ff_25_q;
  wire [31:0] M1_A, M1_D, M1_PA, M2_A, M2_D, M2_PA, M3_A, M3_D, M3_PA, M4_A, M4_D, M4_PA;

  Multiplexer #(.Selector_Bits(2), .Bits(4)) multiplexer_1 (
    .sel(sel_com), .in_0(M1_inst), .in_1(M2_inst), .in_2(M3_inst), .in_3(M4_inst), .out(id_O));
  PriorityEncoder #(.Selector_Bits(2)) priorityencoder_1 (
    .in0(M1_CMP), .in1(M2_CMP), .in2(M3_CMP), .in3(M4_CMP), .num(priorityencoder_1_num), .any(ld_V));
  Multiplexer #(.Selector_Bits(2), .Bits(32)) multiplexer_2 (
    .sel(sel_com), .in_0(M1_D), .in_1(M2_D), .in_2(M3_D), .in_3(M4_D), .out(D_O));
  // Probe SIM1 on M1_inst
  // Probe SIM2 on M2_inst
  // Probe SIM3 on M3_inst
  // Probe SIM4 on M4_inst
  // Probe SVM1 on M1_VO
  // Probe SVM2 on M2_VO
  // Probe SVM3 on M3_VO
  // Probe SVM4 on M4_VO
  assign not_1_out = ~{M4_VO, M3_VO, M2_VO, M1_VO};  // Not not_1, 4 bits wide
  BitExtender #(.inputBits(1), .outputBits(4)) bitextender_1 (.in(W_p), .out(bitextender_1_out));
  BitExtender #(.inputBits(1), .outputBits(4)) bitextender_2 (.in(W_d), .out(bitextender_2_out));
  assign and_1_out = ~{M4_CLR, M3_CLR, M2_CLR, M1_CLR} & {M4_OLD, M3_OLD, M2_OLD, M1_OLD} & {M4_COM, M3_COM, M2_COM, M1_COM};  // And and_1, 4 bits wide
  PriorityEncoder #(.Selector_Bits(2)) priorityencoder_2 (
    .in0(not_1_out[0]), .in1(not_1_out[1]), .in2(not_1_out[2]), .in3(not_1_out[3]), .num(empty_id),
    .any(priorityencoder_2_any));
  assign {M4_PE, M3_PE, M2_PE, M1_PE} = {M4_SELP, M3_SELP, M2_SELP, M1_SELP} & bitextender_1_out;  // And and_2, 4 bits wide
  assign {M4_DE, M3_DE, M2_DE, M1_DE} = {M4_SEL, M3_SEL, M2_SEL, M1_SEL} & bitextender_2_out;  // And and_3, 4 bits wide
  Multiplexer #(.Selector_Bits(2)) multiplexer_3 (
    .sel(sel_com), .in_0(M1_epoch), .in_1(M2_epoch), .in_2(M3_epoch), .in_3(M4_epoch), .out(ep_O));
  Multiplexer #(.Selector_Bits(2), .Bits(32)) multiplexer_4 (
    .sel(priorityencoder_1_num), .in_0(M1_D), .in_1(M2_D), .in_2(M3_D), .in_3(M4_D), .out(ld_D));
  not not_2 (full, priorityencoder_2_any);
  Multiplexer #(.Selector_Bits(2), .Bits(32)) multiplexer_5 (
    .sel(sel_com), .in_0(M1_PA), .in_1(M2_PA), .in_2(M3_PA), .in_3(M4_PA), .out(PA_O));
  PriorityEncoder #(.Selector_Bits(2)) priorityencoder_3 (
    .in0(and_1_out[0]), .in1(and_1_out[1]), .in2(and_1_out[2]), .in3(and_1_out[3]), .num(sel_com), .any(V));
  // Probe SCM1 on M1_COM
  // Probe SCM2 on M2_COM
  // Probe SCM3 on M3_COM
  // Probe SCM4 on M4_COM
  // Probe SAM1 on M1_A
  // Probe SAM2 on M2_A
  // Probe SAM3 on M3_A
  // Probe SAM4 on M4_A
  Demultiplexer #(.Selector_Bits(2)) demultiplexer_1 (
    .sel(empty_id), .in(W_id), .out_0(M1_IE), .out_1(M2_IE), .out_2(M3_IE), .out_3(M4_IE));
  Demultiplexer #(.Selector_Bits(2)) demultiplexer_2 (
    .sel(sel_com), .in(V_t), .out_0(demultiplexer_2_out_0[0]), .out_1(demultiplexer_2_out_0[1]),
    .out_2(demultiplexer_2_out_0[2]), .out_3(demultiplexer_2_out_0[3]));
  and and_4 (V_t, V, LD);
  Multiplexer #(.Selector_Bits(2), .Bits(2)) multiplexer_6 (
    .sel(sel_com), .in_0(M1_MD), .in_1(M2_MD), .in_2(M3_MD), .in_3(M4_MD), .out(MD_O));
  assign {M4_RS, M3_RS, M2_RS, M1_RS} = {M4_CLR, M3_CLR, M2_CLR, M1_CLR} | demultiplexer_2_out_0;  // Or or_1, 4 bits wide
  assign not_3_out = ~{M4_VO, M3_VO, M2_VO, M1_VO};  // Not not_3, 4 bits wide
  and and_5 (and_5_out, M1_RS, ~M1_IE);  // And
  and and_6 (and_6_out, ~M1_RS, M1_DE);  // And
  and and_7 (and_7_out, or_4_out, ~M1_RS);  // And
  BitExtender #(.inputBits(1), .outputBits(4)) bitextender_3 (.in(or_2_out), .out(bitextender_3_out));
  BitExtender #(.inputBits(1), .outputBits(4)) bitextender_4 (.in(M1_RS), .out(bitextender_4_out));
  RS_FF rs_ff_1 (.S(M1_IE), .C(C), .R(and_5_out), .Q(M1_VO));  // open: nQ
  or or_2 (or_2_out, M1_IE, M1_VO);
  Comparator #(.Bits(32)) comparator_1 (.a(ld_addr), .b(M1_A), .eq(comparator_1_eq));  // open: gt, lt
  Register #(.Bits(32)) register_1 (.D(PA), .C(C), .en(M1_PE), .Q(M1_PA));
  Register #(.Bits(32)) register_2 (.D(A), .C(C), .en(M1_DE), .Q(M1_A));
  RS_FF rs_ff_2 (.S(and_6_out), .C(C), .R(M1_RS), .Q(rs_ff_2_q));  // open: nQ
  Register #(.Bits(32)) register_3 (.D(D), .C(C), .en(M1_DE), .Q(M1_D));
  Register #(.Bits(2)) register_4 (.D(MD), .C(C), .en(M1_DE), .Q(M1_MD));
  Comparator #(.Bits(4)) comparator_2 (.a(inst_WP), .b(M1_inst), .eq(comparator_2_eq));  // open: gt, lt
  Comparator #(.Bits(4)) comparator_3 (.a(M1_inst), .b(inst_W), .eq(comparator_3_eq));  // open: gt, lt
  RS_FF rs_ff_3 (.S(and_7_out), .C(C), .R(M1_RS), .Q(M1_COM));  // open: nQ
  and and_8 (and_8_out, com2, M1_VO, comparator_5_eq);
  Comparator #(.Bits(4)) comparator_4 (.a(M1_inst), .b(com1_id), .eq(comparator_4_eq));  // open: gt, lt
  Comparator #(.Bits(4)) comparator_5 (.a(M1_inst), .b(com2_id), .eq(comparator_5_eq));  // open: gt, lt
  Register #(.Bits(4)) register_5 (.D(inst), .C(C), .en(M1_IE), .Q(M1_inst));
  Register register_6 (.D(epoch), .C(C), .en(M1_IE), .Q(M1_epoch));
  inst_comp inst_comp_1 (.A_id(ld_id), .A_ep(ld_ep), .B_id(M1_inst), .B_ep(M1_epoch), .A_new(inst_comp_1_a_new));
  inst_comp inst_comp_2 (.A_id(M1_inst), .A_ep(M1_epoch), .B_id(clr_id), .B_ep(clr_ep), .A_new(inst_comp_2_a_new));
  assign and_9_out = {M4_IE, M3_IE, M2_IE, M1_IE} & bitextender_3_out & ~bitextender_4_out;  // And and_9, 4 bits wide
  assign or_3_out = {not_3_out[3:1], 1'b0} | rs_ff_4_q;  // Or or_3, 4 bits wide
  RS_FF rs_ff_4 (.S(and_9_out[0]), .C(C), .R(bitextender_4_out[0]), .Q(rs_ff_4_q[0]));  // open: nQ
  RS_FF rs_ff_5 (.S(and_9_out[1]), .C(C), .R(bitextender_4_out[1]), .Q(rs_ff_4_q[1]));  // open: nQ
  RS_FF rs_ff_6 (.S(and_9_out[2]), .C(C), .R(bitextender_4_out[2]), .Q(rs_ff_4_q[2]));  // open: nQ
  RS_FF rs_ff_7 (.S(and_9_out[3]), .C(C), .R(bitextender_4_out[3]), .Q(rs_ff_4_q[3]));  // open: nQ
  and and_10 (M1_CMP, comparator_1_eq, rs_ff_2_q, inst_comp_1_a_new);
  and and_11 (M1_SELP, M1_VO, comparator_2_eq);
  and and_12 (M1_SEL, M1_VO, comparator_3_eq);
  or or_4 (or_4_out, and_8_out, and_13_out);
  and and_13 (and_13_out, comparator_4_eq, M1_VO, com1);
  and and_14 (M1_CLR, inst_comp_2_a_new, clr);
  and and_15 (M1_OLD, or_3_out[0], or_3_out[1], or_3_out[2], or_3_out[3]);
  and and_16 (and_16_out, M2_RS, ~M2_IE);  // And
  and and_17 (and_17_out, ~M2_RS, M2_DE);  // And
  and and_18 (and_18_out, or_6_out, ~M2_RS);  // And
  and and_19 (and_19_out, com2, M2_VO, comparator_10_eq);
  BitExtender #(.inputBits(1), .outputBits(4)) bitextender_5 (.in(or_5_out), .out(bitextender_5_out));
  BitExtender #(.inputBits(1), .outputBits(4)) bitextender_6 (.in(M2_RS), .out(bitextender_6_out));
  RS_FF rs_ff_8 (.S(M2_IE), .C(C), .R(and_16_out), .Q(M2_VO));  // open: nQ
  or or_5 (or_5_out, M2_IE, M2_VO);
  Comparator #(.Bits(32)) comparator_6 (.a(ld_addr), .b(M2_A), .eq(comparator_6_eq));  // open: gt, lt
  Register #(.Bits(32)) register_7 (.D(PA), .C(C), .en(M2_PE), .Q(M2_PA));
  Register #(.Bits(32)) register_8 (.D(A), .C(C), .en(M2_DE), .Q(M2_A));
  RS_FF rs_ff_9 (.S(and_17_out), .C(C), .R(M2_RS), .Q(rs_ff_9_q));  // open: nQ
  Register #(.Bits(32)) register_9 (.D(D), .C(C), .en(M2_DE), .Q(M2_D));
  Register #(.Bits(2)) register_10 (.D(MD), .C(C), .en(M2_DE), .Q(M2_MD));
  Comparator #(.Bits(4)) comparator_7 (.a(inst_WP), .b(M2_inst), .eq(comparator_7_eq));  // open: gt, lt
  and and_20 (M2_SELP, M2_VO, comparator_7_eq);
  Comparator #(.Bits(4)) comparator_8 (.a(M2_inst), .b(inst_W), .eq(comparator_8_eq));  // open: gt, lt
  and and_21 (M2_SEL, M2_VO, comparator_8_eq);
  RS_FF rs_ff_10 (.S(and_18_out), .C(C), .R(M2_RS), .Q(M2_COM));  // open: nQ
  or or_6 (or_6_out, and_19_out, and_22_out);
  and and_22 (and_22_out, comparator_9_eq, M2_VO, com1);
  Comparator #(.Bits(4)) comparator_9 (.a(M2_inst), .b(com1_id), .eq(comparator_9_eq));  // open: gt, lt
  Comparator #(.Bits(4)) comparator_10 (.a(M2_inst), .b(com2_id), .eq(comparator_10_eq));  // open: gt, lt
  Register #(.Bits(4)) register_11 (.D(inst), .C(C), .en(M2_IE), .Q(M2_inst));
  Register register_12 (.D(epoch), .C(C), .en(M2_IE), .Q(M2_epoch));
  inst_comp inst_comp_3 (.A_id(ld_id), .A_ep(ld_ep), .B_id(M2_inst), .B_ep(M2_epoch), .A_new(inst_comp_3_a_new));
  inst_comp inst_comp_4 (.A_id(M2_inst), .A_ep(M2_epoch), .B_id(clr_id), .B_ep(clr_ep), .A_new(inst_comp_4_a_new));
  assign and_23_out = {M4_IE, M3_IE, M2_IE, M1_IE} & bitextender_5_out & ~bitextender_6_out;  // And and_23, 4 bits wide
  assign or_7_out = {not_3_out[3:2], 1'b0, not_3_out[0]} | rs_ff_11_q;  // Or or_7, 4 bits wide
  RS_FF rs_ff_11 (.S(and_23_out[0]), .C(C), .R(bitextender_6_out[0]), .Q(rs_ff_11_q[0]));  // open: nQ
  RS_FF rs_ff_12 (.S(and_23_out[1]), .C(C), .R(bitextender_6_out[1]), .Q(rs_ff_11_q[1]));  // open: nQ
  RS_FF rs_ff_13 (.S(and_23_out[2]), .C(C), .R(bitextender_6_out[2]), .Q(rs_ff_11_q[2]));  // open: nQ
  RS_FF rs_ff_14 (.S(and_23_out[3]), .C(C), .R(bitextender_6_out[3]), .Q(rs_ff_11_q[3]));  // open: nQ
  and and_24 (M2_CMP, comparator_6_eq, rs_ff_9_q, inst_comp_3_a_new);
  and and_25 (M2_CLR, inst_comp_4_a_new, clr);
  and and_26 (M2_OLD, or_7_out[0], or_7_out[1], or_7_out[2], or_7_out[3]);
  or or_8 (or_8_out, M3_IE, M3_VO);
  and and_27 (and_27_out, M3_RS, ~M3_IE);  // And
  and and_28 (and_28_out, ~M3_RS, M3_DE);  // And
  and and_29 (and_29_out, or_10_out, ~M3_RS);  // And
  and and_30 (and_30_out, com2, M3_VO, comparator_15_eq);
  BitExtender #(.inputBits(1), .outputBits(4)) bitextender_7 (.in(or_8_out), .out(bitextender_7_out));
  assign and_31_out = {M4_IE, M3_IE, M2_IE, M1_IE} & bitextender_7_out & ~bitextender_8_out;  // And and_31, 4 bits wide
  assign or_9_out = {not_3_out[3], 1'b0, not_3_out[1:0]} | rs_ff_18_q;  // Or or_9, 4 bits wide
  BitExtender #(.inputBits(1), .outputBits(4)) bitextender_8 (.in(M3_RS), .out(bitextender_8_out));
  RS_FF rs_ff_15 (.S(M3_IE), .C(C), .R(and_27_out), .Q(M3_VO));  // open: nQ
  Comparator #(.Bits(32)) comparator_11 (.a(ld_addr), .b(M3_A), .eq(comparator_11_eq));  // open: gt, lt
  Register #(.Bits(32)) register_13 (.D(PA), .C(C), .en(M3_PE), .Q(M3_PA));
  Register #(.Bits(32)) register_14 (.D(A), .C(C), .en(M3_DE), .Q(M3_A));
  RS_FF rs_ff_16 (.S(and_28_out), .C(C), .R(M3_RS), .Q(rs_ff_16_q));  // open: nQ
  Register #(.Bits(32)) register_15 (.D(D), .C(C), .en(M3_DE), .Q(M3_D));
  Register #(.Bits(2)) register_16 (.D(MD), .C(C), .en(M3_DE), .Q(M3_MD));
  Comparator #(.Bits(4)) comparator_12 (.a(inst_WP), .b(M3_inst), .eq(comparator_12_eq));  // open: gt, lt
  and and_32 (M3_SELP, M3_VO, comparator_12_eq);
  Comparator #(.Bits(4)) comparator_13 (.a(M3_inst), .b(inst_W), .eq(comparator_13_eq));  // open: gt, lt
  and and_33 (M3_SEL, M3_VO, comparator_13_eq);
  RS_FF rs_ff_17 (.S(and_29_out), .C(C), .R(M3_RS), .Q(M3_COM));  // open: nQ
  or or_10 (or_10_out, and_30_out, and_34_out);
  and and_34 (and_34_out, comparator_14_eq, M3_VO, com1);
  Comparator #(.Bits(4)) comparator_14 (.a(M3_inst), .b(com1_id), .eq(comparator_14_eq));  // open: gt, lt
  Comparator #(.Bits(4)) comparator_15 (.a(M3_inst), .b(com2_id), .eq(comparator_15_eq));  // open: gt, lt
  Register #(.Bits(4)) register_17 (.D(inst), .C(C), .en(M3_IE), .Q(M3_inst));
  Register register_18 (.D(epoch), .C(C), .en(M3_IE), .Q(M3_epoch));
  inst_comp inst_comp_5 (.A_id(ld_id), .A_ep(ld_ep), .B_id(M3_inst), .B_ep(M3_epoch), .A_new(inst_comp_5_a_new));
  inst_comp inst_comp_6 (.A_id(M3_inst), .A_ep(M3_epoch), .B_id(clr_id), .B_ep(clr_ep), .A_new(inst_comp_6_a_new));
  and and_35 (M3_CLR, inst_comp_6_a_new, clr);
  and and_36 (M3_OLD, or_9_out[0], or_9_out[1], or_9_out[2], or_9_out[3]);
  RS_FF rs_ff_18 (.S(and_31_out[0]), .C(C), .R(bitextender_8_out[0]), .Q(rs_ff_18_q[0]));  // open: nQ
  RS_FF rs_ff_19 (.S(and_31_out[1]), .C(C), .R(bitextender_8_out[1]), .Q(rs_ff_18_q[1]));  // open: nQ
  RS_FF rs_ff_20 (.S(and_31_out[2]), .C(C), .R(bitextender_8_out[2]), .Q(rs_ff_18_q[2]));  // open: nQ
  RS_FF rs_ff_21 (.S(and_31_out[3]), .C(C), .R(bitextender_8_out[3]), .Q(rs_ff_18_q[3]));  // open: nQ
  and and_37 (M3_CMP, comparator_11_eq, rs_ff_16_q, inst_comp_5_a_new);
  and and_38 (and_38_out, M4_RS, ~M4_IE);  // And
  and and_39 (and_39_out, ~M4_RS, M4_DE);  // And
  and and_40 (and_40_out, or_13_out, ~M4_RS);  // And
  RS_FF rs_ff_22 (.S(M4_IE), .C(C), .R(and_38_out), .Q(M4_VO));  // open: nQ
  or or_11 (or_11_out, M4_IE, M4_VO);
  Comparator #(.Bits(32)) comparator_16 (.a(ld_addr), .b(M4_A), .eq(comparator_16_eq));  // open: gt, lt
  Register #(.Bits(32)) register_19 (.D(PA), .C(C), .en(M4_PE), .Q(M4_PA));
  Register #(.Bits(32)) register_20 (.D(A), .C(C), .en(M4_DE), .Q(M4_A));
  RS_FF rs_ff_23 (.S(and_39_out), .C(C), .R(M4_RS), .Q(rs_ff_23_q));  // open: nQ
  Register #(.Bits(32)) register_21 (.D(D), .C(C), .en(M4_DE), .Q(M4_D));
  Register #(.Bits(2)) register_22 (.D(MD), .C(C), .en(M4_DE), .Q(M4_MD));
  Comparator #(.Bits(4)) comparator_17 (.a(inst_WP), .b(M4_inst), .eq(comparator_17_eq));  // open: gt, lt
  Comparator #(.Bits(4)) comparator_18 (.a(M4_inst), .b(inst_W), .eq(comparator_18_eq));  // open: gt, lt
  RS_FF rs_ff_24 (.S(and_40_out), .C(C), .R(M4_RS), .Q(M4_COM));  // open: nQ
  and and_41 (and_41_out, com2, M4_VO, comparator_20_eq);
  Comparator #(.Bits(4)) comparator_19 (.a(M4_inst), .b(com1_id), .eq(comparator_19_eq));  // open: gt, lt
  Comparator #(.Bits(4)) comparator_20 (.a(M4_inst), .b(com2_id), .eq(comparator_20_eq));  // open: gt, lt
  Register #(.Bits(4)) register_23 (.D(inst), .C(C), .en(M4_IE), .Q(M4_inst));
  Register register_24 (.D(epoch), .C(C), .en(M4_IE), .Q(M4_epoch));
  inst_comp inst_comp_7 (.A_id(ld_id), .A_ep(ld_ep), .B_id(M4_inst), .B_ep(M4_epoch), .A_new(inst_comp_7_a_new));
  inst_comp inst_comp_8 (.A_id(M4_inst), .A_ep(M4_epoch), .B_id(clr_id), .B_ep(clr_ep), .A_new(inst_comp_8_a_new));
  BitExtender #(.inputBits(1), .outputBits(4)) bitextender_9 (.in(or_11_out), .out(bitextender_9_out));
  assign and_42_out = {M4_IE, M3_IE, M2_IE, M1_IE} & bitextender_9_out & ~bitextender_10_out;  // And and_42, 4 bits wide
  assign or_12_out = {1'b0, not_3_out[2:0]} | rs_ff_25_q;  // Or or_12, 4 bits wide
  RS_FF rs_ff_25 (.S(and_42_out[0]), .C(C), .R(bitextender_10_out[0]), .Q(rs_ff_25_q[0]));  // open: nQ
  RS_FF rs_ff_26 (.S(and_42_out[1]), .C(C), .R(bitextender_10_out[1]), .Q(rs_ff_25_q[1]));  // open: nQ
  BitExtender #(.inputBits(1), .outputBits(4)) bitextender_10 (.in(M4_RS), .out(bitextender_10_out));
  RS_FF rs_ff_27 (.S(and_42_out[2]), .C(C), .R(bitextender_10_out[2]), .Q(rs_ff_25_q[2]));  // open: nQ
  RS_FF rs_ff_28 (.S(and_42_out[3]), .C(C), .R(bitextender_10_out[3]), .Q(rs_ff_25_q[3]));  // open: nQ
  and and_43 (M4_CMP, comparator_16_eq, rs_ff_23_q, inst_comp_7_a_new);
  and and_44 (M4_SELP, M4_VO, comparator_17_eq);
  and and_45 (M4_SEL, M4_VO, comparator_18_eq);
  or or_13 (or_13_out, and_41_out, and_46_out);
  and and_46 (and_46_out, comparator_19_eq, M4_VO, com1);
  and and_47 (M4_CLR, inst_comp_8_a_new, clr);
  and and_48 (M4_OLD, or_12_out[0], or_12_out[1], or_12_out[2], or_12_out[3]);

  // Other names for the same wires on the sheet: clear = clr; comp_addr[31:0] = ld_addr; comp_ep = ld_ep;
  //   comp_id[3:0] = ld_id; ld_O[31:0] = ld_D; V_out = V
endmodule
