// Digital circuit store-buffer.dig as structural Verilog
module store_buffer (
  input  W_d,
  input  C,
  input  [31:0] D,
  input  [31:0] A,
  input  [3:0] inst,
  input  [3:0] com1_id,
  input  [3:0] com2_id,
  input  com1,
  input  com2,
  input  ld_ep,
  input  [3:0] ld_id,
  input  epoch,
  input  [31:0] ld_addr,
  input  W_id,
  input  [3:0] inst_W,
  input  LD,
  input  [1:0] MD,
  input  clr,
  input  [3:0] clr_id,
  input  clr_ep,
  output [31:0] D_O,
  output [31:0] A_O,
  output V,
  output full,
  output ld_V,
  output [31:0] ld_D,
  output [3:0] id_O,
  output ep_O,
  output [1:0] MD_O
);

  wire and_2_out, and_6_out, and_9_out, and_11_out, and_17_out, and_20_out, and_24_out, and_27_out,
       and_31_out, and_33_out, and_35_out, and_39_out, comparator_1_eq, comparator_2_eq, comparator_3_eq,
       comparator_4_eq, comparator_5_eq, comparator_6_eq, comparator_7_eq, comparator_8_eq, comparator_9_eq,
       comparator_10_eq, comparator_11_eq, comparator_12_eq, comparator_13_eq, comparator_14_eq,
       comparator_15_eq, comparator_16_eq, inst_comp_1_a_old, inst_comp_2_a_old, inst_comp_3_a_old,
       inst_comp_4_a_old, inst_comp_5_a_old, inst_comp_6_a_old, inst_comp_7_a_old, inst_comp_8_a_old, M1_CLR,
       M1_CMP, M1_COM, M1_DE, M1_epoch, M1_IE, M1_OLD, M1_RS, M1_SEL, M1_VO, M2_CLR, M2_CMP, M2_COM, M2_DE,
       M2_epoch, M2_IE, M2_OLD, M2_RS, M2_SEL, M2_VO, M3_CLR, M3_CMP, M3_COM, M3_DE, M3_epoch, M3_IE, M3_OLD,
       M3_RS, M3_SEL, M3_VO, M4_CLR, M4_CMP, M4_COM, M4_DE, M4_epoch, M4_IE, M4_OLD, M4_RS, M4_SEL, M4_VO,
       or_3_out, or_4_out, or_5_out, or_6_out, or_7_out, or_8_out, priorityencoder_2_any, rs_ff_3_q,
       rs_ff_4_q, rs_ff_5_q, rs_ff_6_q, rs_ff_9_q, rs_ff_10_q, rs_ff_11_q, rs_ff_12_q, rs_ff_15_q,
       rs_ff_16_q, rs_ff_17_q, rs_ff_18_q, rs_ff_21_q, rs_ff_22_q, rs_ff_23_q, rs_ff_24_q, V_t;
  wire [1:0] empty_id, M1_MD, M2_MD, M3_MD, M4_MD, priorityencoder_1_num, priorityencoder_3_num,
       register_21_q, register_23_q, register_26_q, register_28_q, sel_com;
  wire [3:0] and_3_out, and_12_out, and_16_out, and_22_out, and_29_out, and_32_out, and_34_out, and_36_out,
       and_37_out, and_38_out, bitextender_1_out, bitextender_2_out, bitextender_3_out, bitextender_4_out,
       bitextender_5_out, bitextender_6_out, bitextender_7_out, bitselector_1_out, bitselector_2_out,
       demultiplexer_2_out_0, fill_4_1_out1, M1_inst, M2_inst, M3_inst, M4_inst, mux1x4_1_out, not_1_out,
       not_3_out, not_4_out, or_2_out, or_9_out, or_10_out, priority_4_1_out1, register_22_q;
  wire [31:0] M1_A, M1_D, M2_A, M2_D, M3_A, M3_D, M4_A, M4_D;

  Multiplexer #(.Selector_Bits(2), .Bits(4)) multiplexer_1 (
    .sel(sel_com), .in_0(M1_inst), .in_1(M2_inst), .in_2(M3_inst), .in_3(M4_inst), .out(id_O));
  PriorityEncoder #(.Selector_Bits(2)) priorityencoder_1 (
    .in0(M1_CMP), .in1(M2_CMP), .in2(M3_CMP), .in3(M4_CMP), .num(priorityencoder_1_num), .any(ld_V));
  Multiplexer #(.Selector_Bits(2), .Bits(32)) multiplexer_2 (
    .sel(sel_com), .in_0(M1_D), .in_1(M2_D), .in_2(M3_D), .in_3(M4_D), .out(D_O));
  // Probe instM1 on M1_inst
  // Probe instM2 on M2_inst
  // Probe instM3 on M3_inst
  // Probe instM4 on M4_inst
  // Probe vM1 on M1_VO
  // Probe vM2 on M2_VO
  // Probe vM3 on M3_VO
  // Probe vM4 on M4_VO
  // Probe comM1 on M1_COM
  // Probe comM2 on M2_COM
  // Probe comM3 on M3_COM
  // Probe comM4 on M4_COM
  assign not_1_out = ~{M4_VO, M3_VO, M2_VO, M1_VO};  // Not not_1, 4 bits wide
  BitExtender #(.inputBits(1), .outputBits(4)) bitextender_1 (.in(W_d), .out(bitextender_1_out));
  PriorityEncoder #(.Selector_Bits(2)) priorityencoder_2 (
    .in0(not_1_out[0]), .in1(not_1_out[1]), .in2(not_1_out[2]), .in3(not_1_out[3]), .num(empty_id),
    .any(priorityencoder_2_any));
  assign {M4_DE, M3_DE, M2_DE, M1_DE} = {M4_SEL, M3_SEL, M2_SEL, M1_SEL} & bitextender_1_out;  // And and_1, 4 bits wide
  Multiplexer #(.Selector_Bits(2)) multiplexer_3 (
    .sel(sel_com), .in_0(M1_epoch), .in_1(M2_epoch), .in_2(M3_epoch), .in_3(M4_epoch), .out(ep_O));
  Multiplexer #(.Selector_Bits(2), .Bits(32)) multiplexer_4 (
    .sel(priorityencoder_1_num), .in_0(M1_D), .in_1(M2_D), .in_2(M3_D), .in_3(M4_D), .out(ld_D));
  not not_2 (full, priorityencoder_2_any);
  Multiplexer #(.Selector_Bits(2), .Bits(32)) multiplexer_5 (
    .sel(sel_com), .in_0(M1_A), .in_1(M2_A), .in_2(M3_A), .in_3(M4_A), .out(A_O));
  Demultiplexer #(.Selector_Bits(2)) demultiplexer_1 (
    .sel(empty_id), .in(W_id), .out_0(M1_IE), .out_1(M2_IE), .out_2(M3_IE), .out_3(M4_IE));
  Demultiplexer #(.Selector_Bits(2)) demultiplexer_2 (
    .sel(sel_com), .in(V_t), .out_0(demultiplexer_2_out_0[0]), .out_1(demultiplexer_2_out_0[1]),
    .out_2(demultiplexer_2_out_0[2]), .out_3(demultiplexer_2_out_0[3]));
  Multiplexer #(.Selector_Bits(2), .Bits(2)) multiplexer_6 (
    .sel(sel_com), .in_0(M1_MD), .in_1(M2_MD), .in_2(M3_MD), .in_3(M4_MD), .out(MD_O));
  assign {M4_RS, M3_RS, M2_RS, M1_RS} = {M4_CLR, M3_CLR, M2_CLR, M1_CLR} | demultiplexer_2_out_0;  // Or or_1, 4 bits wide
  assign or_2_out = {M4_IE, M3_IE, M2_IE, M1_IE} | {M4_RS, M3_RS, M2_RS, M1_RS};  // Or or_2, 4 bits wide
  RS_FF rs_ff_1 (.S(M1_IE), .C(C), .R(M1_RS), .Q(M1_VO));  // open: nQ
  Comparator #(.Bits(32)) comparator_1 (.a(ld_addr), .b(M1_A), .eq(comparator_1_eq));  // open: gt, lt
  Register #(.Bits(32)) register_1 (.D(A), .C(C), .en(M1_DE), .Q(M1_A));
  Register #(.Bits(32)) register_2 (.D(D), .C(C), .en(M1_DE), .Q(M1_D));
  Register #(.Bits(2)) register_3 (.D(MD), .C(C), .en(M1_DE), .Q(M1_MD));
  Comparator #(.Bits(4)) comparator_2 (.a(M1_inst), .b(inst_W), .eq(comparator_2_eq));  // open: gt, lt
  RS_FF rs_ff_2 (.S(or_3_out), .C(C), .R(M1_RS), .Q(M1_COM));  // open: nQ
  and and_2 (and_2_out, com2, M1_VO, comparator_4_eq);
  Comparator #(.Bits(4)) comparator_3 (.a(M1_inst), .b(com1_id), .eq(comparator_3_eq));  // open: gt, lt
  Comparator #(.Bits(4)) comparator_4 (.a(M1_inst), .b(com2_id), .eq(comparator_4_eq));  // open: gt, lt
  Register #(.Bits(4)) register_4 (.D(inst), .C(C), .en(M1_IE), .Q(M1_inst));
  Register register_5 (.D(epoch), .C(C), .en(M1_IE), .Q(M1_epoch));
  inst_comp inst_comp_1 (.A_id(ld_id), .A_ep(ld_ep), .B_id(M1_inst), .B_ep(M1_epoch), .A_old(inst_comp_1_a_old));
  inst_comp inst_comp_2 (.A_id(M1_inst), .A_ep(M1_epoch), .B_id(clr_id), .B_ep(clr_ep), .A_old(inst_comp_2_a_old));
  assign and_3_out = or_2_out & ~bitextender_2_out;  // And and_3, 4 bits wide
  and and_4 (M1_CMP, M1_VO, comparator_1_eq, inst_comp_1_a_old, 1'b1);
  and and_5 (M1_SEL, M1_VO, comparator_2_eq);
  or or_3 (or_3_out, and_2_out, and_6_out);
  and and_6 (and_6_out, comparator_3_eq, M1_VO, com1);
  and and_7 (M1_CLR, inst_comp_2_a_old, clr);
  BitExtender #(.inputBits(1), .outputBits(4)) bitextender_2 (.in(M1_RS), .out(bitextender_2_out));
  and and_8 (M1_OLD, rs_ff_3_q, rs_ff_4_q, rs_ff_5_q, rs_ff_6_q);
  RS_FF rs_ff_3 (.S(and_3_out[0]), .C(C), .R(bitextender_2_out[0]), .Q(rs_ff_3_q));  // open: nQ
  RS_FF rs_ff_4 (.S(and_3_out[1]), .C(C), .R(bitextender_2_out[1]), .Q(rs_ff_4_q));  // open: nQ
  RS_FF rs_ff_5 (.S(and_3_out[2]), .C(C), .R(bitextender_2_out[2]), .Q(rs_ff_5_q));  // open: nQ
  RS_FF rs_ff_6 (.S(and_3_out[3]), .C(C), .R(bitextender_2_out[3]), .Q(rs_ff_6_q));  // open: nQ
  and and_9 (and_9_out, com2, M2_VO, comparator_8_eq);
  RS_FF rs_ff_7 (.S(M2_IE), .C(C), .R(M2_RS), .Q(M2_VO));  // open: nQ
  Comparator #(.Bits(32)) comparator_5 (.a(ld_addr), .b(M2_A), .eq(comparator_5_eq));  // open: gt, lt
  Register #(.Bits(32)) register_6 (.D(A), .C(C), .en(M2_DE), .Q(M2_A));
  Register #(.Bits(32)) register_7 (.D(D), .C(C), .en(M2_DE), .Q(M2_D));
  Register #(.Bits(2)) register_8 (.D(MD), .C(C), .en(M2_DE), .Q(M2_MD));
  Comparator #(.Bits(4)) comparator_6 (.a(M2_inst), .b(inst_W), .eq(comparator_6_eq));  // open: gt, lt
  and and_10 (M2_SEL, M2_VO, comparator_6_eq);
  RS_FF rs_ff_8 (.S(or_4_out), .C(C), .R(M2_RS), .Q(M2_COM));  // open: nQ
  or or_4 (or_4_out, and_9_out, and_11_out);
  and and_11 (and_11_out, comparator_7_eq, M2_VO, com1);
  Comparator #(.Bits(4)) comparator_7 (.a(M2_inst), .b(com1_id), .eq(comparator_7_eq));  // open: gt, lt
  Comparator #(.Bits(4)) comparator_8 (.a(M2_inst), .b(com2_id), .eq(comparator_8_eq));  // open: gt, lt
  Register #(.Bits(4)) register_9 (.D(inst), .C(C), .en(M2_IE), .Q(M2_inst));
  Register register_10 (.D(epoch), .C(C), .en(M2_IE), .Q(M2_epoch));
  inst_comp inst_comp_3 (.A_id(ld_id), .A_ep(ld_ep), .B_id(M2_inst), .B_ep(M2_epoch), .A_old(inst_comp_3_a_old));
  inst_comp inst_comp_4 (.A_id(M2_inst), .A_ep(M2_epoch), .B_id(clr_id), .B_ep(clr_ep), .A_old(inst_comp_4_a_old));
  assign and_12_out = or_2_out & ~bitextender_3_out;  // And and_12, 4 bits wide
  RS_FF rs_ff_9 (.S(and_12_out[0]), .C(C), .R(bitextender_3_out[0]), .Q(rs_ff_9_q));  // open: nQ
  RS_FF rs_ff_10 (.S(and_12_out[1]), .C(C), .R(bitextender_3_out[1]), .Q(rs_ff_10_q));  // open: nQ
  RS_FF rs_ff_11 (.S(and_12_out[2]), .C(C), .R(bitextender_3_out[2]), .Q(rs_ff_11_q));  // open: nQ
  RS_FF rs_ff_12 (.S(and_12_out[3]), .C(C), .R(bitextender_3_out[3]), .Q(rs_ff_12_q));  // open: nQ
  and and_13 (M2_CMP, M2_VO, comparator_5_eq, inst_comp_3_a_old, 1'b1);
  and and_14 (M2_CLR, inst_comp_4_a_old, clr);
  BitExtender #(.inputBits(1), .outputBits(4)) bitextender_3 (.in(M2_RS), .out(bitextender_3_out));
  and and_15 (M2_OLD, rs_ff_9_q, rs_ff_10_q, rs_ff_11_q, rs_ff_12_q);
  assign and_16_out = ~{M4_CLR, M3_CLR, M2_CLR, M1_CLR} & {M4_OLD, M3_OLD, M2_OLD, M1_OLD} & {M4_COM, M3_COM, M2_COM, M1_COM};  // And and_16, 4 bits wide
  and and_17 (and_17_out, com2, M3_VO, comparator_12_eq);
  RS_FF rs_ff_13 (.S(M3_IE), .C(C), .R(M3_RS), .Q(M3_VO));  // open: nQ
  and and_18 (M3_CMP, M3_VO, comparator_9_eq, inst_comp_5_a_old, 1'b1);
  Comparator #(.Bits(32)) comparator_9 (.a(ld_addr), .b(M3_A), .eq(comparator_9_eq));  // open: gt, lt
  Register #(.Bits(32)) register_11 (.D(A), .C(C), .en(M3_DE), .Q(M3_A));
  Register #(.Bits(32)) register_12 (.D(D), .C(C), .en(M3_DE), .Q(M3_D));
  Register #(.Bits(2)) register_13 (.D(MD), .C(C), .en(M3_DE), .Q(M3_MD));
  Comparator #(.Bits(4)) comparator_10 (.a(M3_inst), .b(inst_W), .eq(comparator_10_eq));  // open: gt, lt
  and and_19 (M3_SEL, M3_VO, comparator_10_eq);
  RS_FF rs_ff_14 (.S(or_5_out), .C(C), .R(M3_RS), .Q(M3_COM));  // open: nQ
  or or_5 (or_5_out, and_17_out, and_20_out);
  and and_20 (and_20_out, comparator_11_eq, M3_VO, com1);
  Comparator #(.Bits(4)) comparator_11 (.a(M3_inst), .b(com1_id), .eq(comparator_11_eq));  // open: gt, lt
  Comparator #(.Bits(4)) comparator_12 (.a(M3_inst), .b(com2_id), .eq(comparator_12_eq));  // open: gt, lt
  Register #(.Bits(4)) register_14 (.D(inst), .C(C), .en(M3_IE), .Q(M3_inst));
  Register register_15 (.D(epoch), .C(C), .en(M3_IE), .Q(M3_epoch));
  inst_comp inst_comp_5 (.A_id(ld_id), .A_ep(ld_ep), .B_id(M3_inst), .B_ep(M3_epoch), .A_old(inst_comp_5_a_old));
  inst_comp inst_comp_6 (.A_id(M3_inst), .A_ep(M3_epoch), .B_id(clr_id), .B_ep(clr_ep), .A_old(inst_comp_6_a_old));
  and and_21 (M3_CLR, inst_comp_6_a_old, clr);
  assign and_22_out = or_2_out & ~bitextender_4_out;  // And and_22, 4 bits wide
  RS_FF rs_ff_15 (.S(and_22_out[0]), .C(C), .R(bitextender_4_out[0]), .Q(rs_ff_15_q));  // open: nQ
  RS_FF rs_ff_16 (.S(and_22_out[1]), .C(C), .R(bitextender_4_out[1]), .Q(rs_ff_16_q));  // open: nQ
  RS_FF rs_ff_17 (.S(and_22_out[2]), .C(C), .R(bitextender_4_out[2]), .Q(rs_ff_17_q));  // open: nQ
  RS_FF rs_ff_18 (.S(and_22_out[3]), .C(C), .R(bitextender_4_out[3]), .Q(rs_ff_18_q));  // open: nQ
  BitExtender #(.inputBits(1), .outputBits(4)) bitextender_4 (.in(M3_RS), .out(bitextender_4_out));
  and and_23 (M3_OLD, rs_ff_15_q, rs_ff_16_q, rs_ff_17_q, rs_ff_18_q);
  RS_FF rs_ff_19 (.S(M4_IE), .C(C), .R(M4_RS), .Q(M4_VO));  // open: nQ
  Comparator #(.Bits(32)) comparator_13 (.a(ld_addr), .b(M4_A), .eq(comparator_13_eq));  // open: gt, lt
  Register #(.Bits(32)) register_16 (.D(A), .C(C), .en(M4_DE), .Q(M4_A));
  Register #(.Bits(32)) register_17 (.D(D), .C(C), .en(M4_DE), .Q(M4_D));
  Register #(.Bits(2)) register_18 (.D(MD), .C(C), .en(M4_DE), .Q(M4_MD));
  Comparator #(.Bits(4)) comparator_14 (.a(M4_inst), .b(inst_W), .eq(comparator_14_eq));  // open: gt, lt
  RS_FF rs_ff_20 (.S(or_6_out), .C(C), .R(M4_RS), .Q(M4_COM));  // open: nQ
  and and_24 (and_24_out, com2, M4_VO, comparator_16_eq);
  Comparator #(.Bits(4)) comparator_15 (.a(M4_inst), .b(com1_id), .eq(comparator_15_eq));  // open: gt, lt
  Comparator #(.Bits(4)) comparator_16 (.a(M4_inst), .b(com2_id), .eq(comparator_16_eq));  // open: gt, lt
  Register #(.Bits(4)) register_19 (.D(inst), .C(C), .en(M4_IE), .Q(M4_inst));
  Register register_20 (.D(epoch), .C(C), .en(M4_IE), .Q(M4_epoch));
  inst_comp inst_comp_7 (.A_id(ld_id), .A_ep(ld_ep), .B_id(M4_inst), .B_ep(M4_epoch), .A_old(inst_comp_7_a_old));
  inst_comp inst_comp_8 (.A_id(M4_inst), .A_ep(M4_epoch), .B_id(clr_id), .B_ep(clr_ep), .A_old(inst_comp_8_a_old));
  and and_25 (M4_CMP, M4_VO, comparator_13_eq, inst_comp_7_a_old, 1'b1);
  and and_26 (M4_SEL, M4_VO, comparator_14_eq);
  or or_6 (or_6_out, and_24_out, and_27_out);
  and and_27 (and_27_out, comparator_15_eq, M4_VO, com1);
  and and_28 (M4_CLR, inst_comp_8_a_old, clr);
  assign and_29_out = or_2_out & ~bitextender_5_out;  // And and_29, 4 bits wide
  BitExtender #(.inputBits(1), .outputBits(4)) bitextender_5 (.in(M4_RS), .out(bitextender_5_out));
  RS_FF rs_ff_21 (.S(and_29_out[0]), .C(C), .R(bitextender_5_out[0]), .Q(rs_ff_21_q));  // open: nQ
  RS_FF rs_ff_22 (.S(and_29_out[1]), .C(C), .R(bitextender_5_out[1]), .Q(rs_ff_22_q));  // open: nQ
  RS_FF rs_ff_23 (.S(and_29_out[2]), .C(C), .R(bitextender_5_out[2]), .Q(rs_ff_23_q));  // open: nQ
  RS_FF rs_ff_24 (.S(and_29_out[3]), .C(C), .R(bitextender_5_out[3]), .Q(rs_ff_24_q));  // open: nQ
  and and_30 (M4_OLD, rs_ff_21_q, rs_ff_22_q, rs_ff_23_q, rs_ff_24_q);
  fill_4 fill_4_1 (
    .on(1'b0), .in1(not_3_out[0]), .in2(not_3_out[1]), .in3(not_3_out[2]), .in4(not_3_out[3]),
    .out1(fill_4_1_out1[3]), .out2(fill_4_1_out1[2]), .out3(fill_4_1_out1[1]), .out4(fill_4_1_out1[0]));  // open: v
  assign not_3_out = ~register_22_q;  // Not not_3, 4 bits wide
  or or_7 (or_7_out, M4_CLR, M3_CLR, M2_CLR, M1_CLR);
  or or_8 (or_8_out, LD, or_7_out);
  priority_4 priority_4_1 (
    .on(LD), .in1(and_36_out[0]), .in2(and_36_out[1]), .in3(and_36_out[2]), .in4(and_36_out[3]),
    .out1(priority_4_1_out1[3]), .out2(priority_4_1_out1[2]), .out3(priority_4_1_out1[1]),
    .out4(priority_4_1_out1[0]));  // open: v
  and and_31 (and_31_out, not_4_out[3], W_id);
  assign and_32_out = ~{M4_CLR, M3_CLR, M2_CLR, M1_CLR} & {M4_COM, M3_COM, M2_COM, M1_COM};  // And and_32, 4 bits wide
  Register #(.Bits(2)) register_21 (.D(empty_id), .C(C), .en(W_id), .Q(register_21_q));
  Register register_22 (.D(and_31_out), .C(C), .en(or_10_out[3]), .Q(register_22_q[0]));
  BitSelector #(.Selector_Bits(2)) bitselector_1 (.in(and_32_out), .sel(register_21_q), .out(bitselector_1_out[0]));
  BitSelector #(.Selector_Bits(2)) bitselector_2 (
    .in({M4_CLR, M3_CLR, M2_CLR, M1_CLR}), .sel(register_21_q), .out(bitselector_2_out[3]));
  assign or_9_out = priority_4_1_out1 | bitselector_2_out;  // Or or_9, 4 bits wide
  and and_33 (and_33_out, not_4_out[2], register_22_q[0]);
  Register #(.Bits(2)) register_23 (.D(register_21_q), .C(C), .en(W_id), .Q(register_23_q));
  BitExtender #(.inputBits(1), .outputBits(4)) bitextender_6 (.in(W_id), .out(bitextender_6_out));
  Register register_24 (.D(and_33_out), .C(C), .en(or_10_out[2]), .Q(register_22_q[1]));
  BitSelector #(.Selector_Bits(2)) bitselector_3 (.in(and_32_out), .sel(register_23_q), .out(bitselector_1_out[1]));
  BitSelector #(.Selector_Bits(2)) bitselector_4 (
    .in({M4_CLR, M3_CLR, M2_CLR, M1_CLR}), .sel(register_23_q), .out(bitselector_2_out[2]));
  mux1x4 mux1x4_1 (.A(or_9_out), .B({1'b0, or_9_out[3:1]}), .S(or_10_out), .out(mux1x4_1_out));
  BitExtender #(.inputBits(1), .outputBits(4)) bitextender_7 (.in(or_8_out), .out(bitextender_7_out));
  assign and_34_out = bitextender_6_out & fill_4_1_out1;  // And and_34, 4 bits wide
  and and_35 (and_35_out, not_4_out[1], register_22_q[1]);
  Register register_25 (.D(and_35_out), .C(C), .en(or_10_out[1]), .Q(register_22_q[2]));
  assign and_36_out = register_22_q & bitselector_1_out;  // And and_36, 4 bits wide
  Register #(.Bits(2)) register_26 (.D(register_23_q), .C(C), .en(W_id), .Q(register_26_q));
  assign and_37_out = mux1x4_1_out & bitextender_7_out;  // And and_37, 4 bits wide
  assign and_38_out = bitextender_7_out & or_9_out;  // And and_38, 4 bits wide
  and and_39 (and_39_out, not_4_out[0], register_22_q[2]);
  BitSelector #(.Selector_Bits(2)) bitselector_5 (.in(and_32_out), .sel(register_26_q), .out(bitselector_1_out[2]));
  BitSelector #(.Selector_Bits(2)) bitselector_6 (
    .in({M4_CLR, M3_CLR, M2_CLR, M1_CLR}), .sel(register_26_q), .out(bitselector_2_out[1]));
  assign not_4_out = ~and_37_out;  // Not not_4, 4 bits wide
  assign or_10_out = and_38_out | and_34_out;  // Or or_10, 4 bits wide
  Register register_27 (.D(and_39_out), .C(C), .en(or_10_out[0]), .Q(register_22_q[3]));
  PriorityEncoder #(.Selector_Bits(2)) priorityencoder_3 (
    .in0(and_36_out[0]), .in1(and_36_out[1]), .in2(and_36_out[2]), .in3(and_36_out[3]),
    .num(priorityencoder_3_num), .any(V));
  BitSelector #(.Selector_Bits(2)) bitselector_7 (.in(and_32_out), .sel(register_28_q), .out(bitselector_1_out[3]));
  Register #(.Bits(2)) register_28 (.D(register_26_q), .C(C), .en(W_id), .Q(register_28_q));
  BitSelector #(.Selector_Bits(2)) bitselector_8 (
    .in({M4_CLR, M3_CLR, M2_CLR, M1_CLR}), .sel(register_28_q), .out(bitselector_2_out[0]));
  Multiplexer #(.Selector_Bits(2), .Bits(2)) multiplexer_7 (
    .sel(priorityencoder_3_num), .in_0(register_21_q), .in_1(register_23_q), .in_2(register_26_q),
    .in_3(register_28_q), .out(sel_com));
  and and_40 (V_t, V, LD);

  // Other names for the same wires on the sheet: clear = clr; comp_addr[31:0] = ld_addr; comp_ep = ld_ep;
  //   comp_id[3:0] = ld_id; ld_O[31:0] = ld_D; V_out = V
endmodule
