// Digital circuit store-buffer8-debug.dig as structural Verilog
module store_buffer8_debug (
  input  W_d,
  input  C,
  input  [31:0] D,
  input  [31:0] A,
  input  [3:0] inst,
  input  [3:0] com1_id,
  input  [3:0] com2_id,
  input  com1,
  input  com2,
  input  ld_ep,
  input  [3:0] ld_id,
  input  epoch,
  input  [31:0] ld_addr,
  input  W_id,
  input  [3:0] inst_W,
  input  LD,
  input  [1:0] MD,
  input  clr,
  input  [3:0] clr_id,
  input  clr_ep,
  output [31:0] D_O,
  output [31:0] A_O,
  output V,
  output full,
  output ld_V,
  output [31:0] ld_D,
  output [3:0] id_O,
  output ep_O,
  output [1:0] MD_O
);

  wire and_4_out, and_5_out, and_6_out, and_7_out, and_11_out, and_14_out, and_15_out, and_16_out,
       and_17_out, and_21_out, and_24_out, and_25_out, and_26_out, and_27_out, and_31_out, and_34_out,
       and_35_out, and_36_out, and_37_out, and_41_out, and_44_out, and_45_out, and_46_out, and_47_out,
       and_51_out, and_54_out, and_55_out, and_56_out, and_57_out, and_61_out, and_64_out, and_65_out,
       and_66_out, and_67_out, and_71_out, and_74_out, and_75_out, and_76_out, and_77_out, and_81_out,
       comparator_1_eq, comparator_2_eq, comparator_3_eq, comparator_4_eq, comparator_5_eq, comparator_6_eq,
       comparator_7_eq, comparator_8_eq, comparator_9_eq, comparator_10_eq, comparator_11_eq,
       comparator_12_eq, comparator_13_eq, comparator_14_eq, comparator_15_eq, comparator_16_eq,
       comparator_17_eq, comparator_18_eq, comparator_19_eq, comparator_20_eq, comparator_21_eq,
       comparator_22_eq, comparator_23_eq, comparator_24_eq, comparator_25_eq, comparator_26_eq,
       comparator_27_eq, comparator_28_eq, comparator_29_eq, comparator_30_eq, comparator_31_eq,
       comparator_32_eq, inst_comp_1_a_new, inst_comp_2_a_new, inst_comp_3_a_new, inst_comp_4_a_new,
       inst_comp_5_a_new, inst_comp_6_a_new, inst_comp_7_a_new, inst_comp_8_a_new, inst_comp_9_a_new,
       inst_comp_10_a_new, inst_comp_11_a_new, inst_comp_12_a_new, inst_comp_13_a_new, inst_comp_14_a_new,
       inst_comp_15_a_new, inst_comp_16_a_new, M1_CLR, M1_CMP, M1_COM, M1_DE, M1_epoch, M1_IE, M1_OLD, M1_RS,
       M1_SEL, M1_VO, M2_CLR, M2_CMP, M2_COM, M2_DE, M2_epoch, M2_IE, M2_OLD, M2_RS, M2_SEL, M2_VO, M3_CLR,
       M3_CMP, M3_COM, M3_DE, M3_epoch, M3_IE, M3_OLD, M3_RS, M3_SEL, M3_VO, M4_CLR, M4_CMP, M4_COM, M4_DE,
       M4_epoch, M4_IE, M4_OLD, M4_RS, M4_SEL, M4_VO, M5_CLR, M5_CMP, M5_COM, M5_DE, M5_epoch, M5_IE, M5_OLD,
       M5_RS, M5_SEL, M5_VO, M6_CLR, M6_CMP, M6_COM, M6_DE, M6_epoch, M6_IE, M6_OLD, M6_RS, M6_SEL, M6_VO,
       M7_CLR, M7_CMP, M7_COM, M7_DE, M7_epoch, M7_IE, M7_OLD, M7_RS, M7_SEL, M7_VO, M8_CLR, M8_CMP, M8_COM,
       M8_DE, M8_epoch, M8_IE, M8_OLD, M8_RS, M8_SEL, M8_VO, or_2_out, or_4_out, or_5_out, or_7_out,
       or_8_out, or_10_out, or_11_out, or_13_out, or_14_out, or_16_out, or_17_out, or_19_out, or_20_out,
       or_22_out, or_23_out, or_25_out, priorityencoder_2_any, rs_ff_2_q, rs_ff_13_q, rs_ff_24_q, rs_ff_35_q,
       rs_ff_46_q, rs_ff_57_q, rs_ff_68_q, rs_ff_79_q, V_t;
  wire [1:0] M1_MD, M2_MD, M3_MD, M4_MD, M5_MD, M6_MD, M7_MD, M8_MD;
  wire [2:0] empty_id, priorityencoder_1_num, sel_com;
  wire [3:0] M1_inst, M2_inst, M3_inst, M4_inst, M5_inst, M6_inst, M7_inst, M8_inst;
  wire [7:0] and_1_out, and_8_out, and_18_out, and_28_out, and_38_out, and_48_out, and_58_out, and_68_out,
       and_78_out, bitextender_1_out, bitextender_2_out, bitextender_3_out, bitextender_4_out,
       bitextender_5_out, bitextender_6_out, bitextender_7_out, bitextender_8_out, bitextender_9_out,
       bitextender_10_out, bitextender_11_out, bitextender_12_out, bitextender_13_out, bitextender_14_out,
       bitextender_15_out, bitextender_16_out, bitextender_17_out, demultiplexer_2_out_0, not_1_out,
       not_3_out, or_3_out, or_6_out, or_9_out, or_12_out, or_15_out, or_18_out, or_21_out, or_24_out,
       rs_ff_4_q, rs_ff_15_q, rs_ff_26_q, rs_ff_37_q, rs_ff_48_q, rs_ff_59_q, rs_ff_70_q, rs_ff_81_q;
  wire [31:0] M1_A, M1_D, M2_A, M2_D, M3_A, M3_D, M4_A, M4_D, M5_A, M5_D, M6_A, M6_D, M7_A, M7_D, M8_A, M8_D;

  Multiplexer #(.Selector_Bits(3), .Bits(4)) multiplexer_1 (
    .sel(sel_com), .in_0(M1_inst), .in_1(M2_inst), .in_2(M3_inst), .in_3(M4_inst), .in_4(M5_inst),
    .in_5(M6_inst), .in_6(M7_inst), .in_7(M8_inst), .out(id_O));
  PriorityEncoder #(.Selector_Bits(3)) priorityencoder_1 (
    .in0(M1_CMP), .in1(M2_CMP), .in2(M3_CMP), .in3(M4_CMP), .in4(M5_CMP), .in5(M6_CMP), .in6(M7_CMP),
    .in7(M8_CMP), .num(priorityencoder_1_num), .any(ld_V));
  Multiplexer #(.Selector_Bits(3), .Bits(32)) multiplexer_2 (
    .sel(sel_com), .in_0(M1_D), .in_1(M2_D), .in_2(M3_D), .in_3(M4_D), .in_4(M5_D), .in_5(M6_D), .in_6(M7_D),
    .in_7(M8_D), .out(D_O));
  // Probe SIM1 on M1_inst
  // Probe SIM2 on M2_inst
  // Probe SIM3 on M3_inst
  // Probe SIM4 on M4_inst
  // Probe SIM5 on M5_inst
  // Probe SIM6 on M6_inst
  // Probe SIM7 on M7_inst
  // Probe SIM8 on M8_inst
  // Probe SVM1 on M1_VO
  // Probe SVM2 on M2_VO
  // Probe SVM3 on M3_VO
  // Probe SVM4 on M4_VO
  // Probe SVM5 on M5_VO
  // Probe SVM6 on M6_VO
  // Probe SVM7 on M7_VO
  // Probe SVM8 on M8_VO
  assign not_1_out = ~{M8_VO, M7_VO, M6_VO, M5_VO, M4_VO, M3_VO, M2_VO, M1_VO};  // Not not_1, 8 bits wide
  BitExtender #(.inputBits(1), .outputBits(8)) bitextender_1 (.in(W_d), .out(bitextender_1_out));
  assign and_1_out = ~{M8_CLR, M7_CLR, M6_CLR, M5_CLR, M4_CLR, M3_CLR, M2_CLR, M1_CLR} & {M8_OLD, M7_OLD, M6_OLD, M5_OLD, M4_OLD, M3_OLD, M2_OLD, M1_OLD} & {M8_COM, M7_COM, M6_COM, M5_COM, M4_COM, M3_COM, M2_COM, M1_COM};  // And and_1, 8 bits wide
  PriorityEncoder #(.Selector_Bits(3)) priorityencoder_2 (
    .in0(not_1_out[0]), .in1(not_1_out[1]), .in2(not_1_out[2]), .in3(not_1_out[3]), .in4(not_1_out[4]),
    .in5(not_1_out[5]), .in6(not_1_out[6]), .in7(not_1_out[7]), .num(empty_id), .any(priorityencoder_2_any));
  assign {M8_DE, M7_DE, M6_DE, M5_DE, M4_DE, M3_DE, M2_DE, M1_DE} = {M8_SEL, M7_SEL, M6_SEL, M5_SEL, M4_SEL, M3_SEL, M2_SEL, M1_SEL} & bitextender_1_out;  // And and_2, 8 bits wide
  Multiplexer #(.Selector_Bits(3)) multiplexer_3 (
    .sel(sel_com), .in_0(M1_epoch), .in_1(M2_epoch), .in_2(M3_epoch), .in_3(M4_epoch), .in_4(M5_epoch),
    .in_5(M6_epoch), .in_6(M7_epoch), .in_7(M8_epoch), .out(ep_O));
  Multiplexer #(.Selector_Bits(3), .Bits(32)) multiplexer_4 (
    .sel(priorityencoder_1_num), .in_0(M1_D), .in_1(M2_D), .in_2(M3_D), .in_3(M4_D), .in_4(M5_D),
    .in_5(M6_D), .in_6(M7_D), .in_7(M8_D), .out(ld_D));
  not not_2 (full, priorityencoder_2_any);
  Multiplexer #(.Selector_Bits(3), .Bits(32)) multiplexer_5 (
    .sel(sel_com), .in_0(M1_A), .in_1(M2_A), .in_2(M3_A), .in_3(M4_A), .in_4(M5_A), .in_5(M6_A), .in_6(M7_A),
    .in_7(M8_A), .out(A_O));
  PriorityEncoder #(.Selector_Bits(3)) priorityencoder_3 (
    .in0(and_1_out[0]), .in1(and_1_out[1]), .in2(and_1_out[2]), .in3(and_1_out[3]), .in4(and_1_out[4]),
    .in5(and_1_out[5]), .in6(and_1_out[6]), .in7(and_1_out[7]), .num(sel_com), .any(V));
  // Probe SCM1 on M1_COM
  // Probe SCM2 on M2_COM
  // Probe SCM3 on M3_COM
  // Probe SCM4 on M4_COM
  // Probe SCM5 on M5_COM
  // Probe SCM6 on M6_COM
  // Probe SCM7 on M7_COM
  // Probe SCM8 on M8_COM
  // Probe SAM1 on M1_A
  // Probe SAM2 on M2_A
  // Probe SAM3 on M3_A
  // Probe SAM4 on M4_A
  // Probe SAM5 on M5_A
  // Probe SAM6 on M6_A
  // Probe SAM7 on M7_A
  // Probe SAM8 on M8_A
  Demultiplexer #(.Selector_Bits(3)) demultiplexer_1 (
    .sel(empty_id), .in(W_id), .out_0(M1_IE), .out_1(M2_IE), .out_2(M3_IE), .out_3(M4_IE), .out_4(M5_IE),
    .out_5(M6_IE), .out_6(M7_IE), .out_7(M8_IE));
  Demultiplexer #(.Selector_Bits(3)) demultiplexer_2 (
    .sel(sel_com), .in(V_t), .out_0(demultiplexer_2_out_0[0]), .out_1(demultiplexer_2_out_0[1]),
    .out_2(demultiplexer_2_out_0[2]), .out_3(demultiplexer_2_out_0[3]), .out_4(demultiplexer_2_out_0[4]),
    .out_5(demultiplexer_2_out_0[5]), .out_6(demultiplexer_2_out_0[6]), .out_7(demultiplexer_2_out_0[7]));
  and and_3 (V_t, V, LD);
  Multiplexer #(.Selector_Bits(3), .Bits(2)) multiplexer_6 (
    .sel(sel_com), .in_0(M1_MD), .in_1(M2_MD), .in_2(M3_MD), .in_3(M4_MD), .in_4(M5_MD), .in_5(M6_MD),
    .in_6(M7_MD), .in_7(M8_MD), .out(MD_O));
  assign {M8_RS, M7_RS, M6_RS, M5_RS, M4_RS, M3_RS, M2_RS, M1_RS} = {M8_CLR, M7_CLR, M6_CLR, M5_CLR, M4_CLR, M3_CLR, M2_CLR, M1_CLR} | demultiplexer_2_out_0;  // Or or_1, 8 bits wide
  assign not_3_out = ~{M8_VO, M7_VO, M6_VO, M5_VO, M4_VO, M3_VO, M2_VO, M1_VO};  // Not not_3, 8 bits wide
  and and_4 (and_4_out, M1_RS, ~M1_IE);  // And
  and and_5 (and_5_out, ~M1_RS, M1_DE);  // And
  and and_6 (and_6_out, or_4_out, ~M1_RS);  // And
  BitExtender #(.inputBits(1), .outputBits(8)) bitextender_2 (.in(or_2_out), .out(bitextender_2_out));
  BitExtender #(.inputBits(1), .outputBits(8)) bitextender_3 (.in(M1_RS), .out(bitextender_3_out));
  RS_FF rs_ff_1 (.S(M1_IE), .C(C), .R(and_4_out), .Q(M1_VO));  // open: nQ
  or or_2 (or_2_out, M1_IE, M1_VO);
  Comparator #(.Bits(32)) comparator_1 (.a(ld_addr), .b(M1_A), .eq(comparator_1_eq));  // open: gt, lt
  Register #(.Bits(32)) register_1 (.D(A), .C(C), .en(M1_DE), .Q(M1_A));
  RS_FF rs_ff_2 (.S(and_5_out), .C(C), .R(M1_RS), .Q(rs_ff_2_q));  // open: nQ
  Register #(.Bits(32)) register_2 (.D(D), .C(C), .en(M1_DE), .Q(M1_D));
  Register #(.Bits(2)) register_3 (.D(MD), .C(C), .en(M1_DE), .Q(M1_MD));
  Comparator #(.Bits(4)) comparator_2 (.a(M1_inst), .b(inst_W), .eq(comparator_2_eq));  // open: gt, lt
  RS_FF rs_ff_3 (.S(and_6_out), .C(C), .R(M1_RS), .Q(M1_COM));  // open: nQ
  and and_7 (and_7_out, com2, M1_VO, comparator_4_eq);
  Comparator #(.Bits(4)) comparator_3 (.a(M1_inst), .b(com1_id), .eq(comparator_3_eq));  // open: gt, lt
  Comparator #(.Bits(4)) comparator_4 (.a(M1_inst), .b(com2_id), .eq(comparator_4_eq));  // open: gt, lt
  Register #(.Bits(4)) register_4 (.D(inst), .C(C), .en(M1_IE), .Q(M1_inst));
  Register register_5 (.D(epoch), .C(C), .en(M1_IE), .Q(M1_epoch));
  inst_comp inst_comp_1 (.A_id(ld_id), .A_ep(ld_ep), .B_id(M1_inst), .B_ep(M1_epoch), .A_new(inst_comp_1_a_new));
  inst_comp inst_comp_2 (.A_id(M1_inst), .A_ep(M1_epoch), .B_id(clr_id), .B_ep(clr_ep), .A_new(inst_comp_2_a_new));
  assign and_8_out = {M8_IE, M7_IE, M6_IE, M5_IE, M4_IE, M3_IE, M2_IE, M1_IE} & bitextender_2_out & ~bitextender_3_out;  // And and_8, 8 bits wide
  assign or_3_out = {not_3_out[7:1], 1'b0} | rs_ff_4_q;  // Or or_3, 8 bits wide
  RS_FF rs_ff_4 (.S(and_8_out[0]), .C(C), .R(bitextender_3_out[0]), .Q(rs_ff_4_q[0]));  // open: nQ
  RS_FF rs_ff_5 (.S(and_8_out[1]), .C(C), .R(bitextender_3_out[1]), .Q(rs_ff_4_q[1]));  // open: nQ
  RS_FF rs_ff_6 (.S(and_8_out[2]), .C(C), .R(bitextender_3_out[2]), .Q(rs_ff_4_q[2]));  // open: nQ
  RS_FF rs_ff_7 (.S(and_8_out[3]), .C(C), .R(bitextender_3_out[3]), .Q(rs_ff_4_q[3]));  // open: nQ
  RS_FF rs_ff_8 (.S(and_8_out[4]), .C(C), .R(bitextender_3_out[4]), .Q(rs_ff_4_q[4]));  // open: nQ
  RS_FF rs_ff_9 (.S(and_8_out[5]), .C(C), .R(bitextender_3_out[5]), .Q(rs_ff_4_q[5]));  // open: nQ
  RS_FF rs_ff_10 (.S(and_8_out[6]), .C(C), .R(bitextender_3_out[6]), .Q(rs_ff_4_q[6]));  // open: nQ
  RS_FF rs_ff_11 (.S(and_8_out[7]), .C(C), .R(bitextender_3_out[7]), .Q(rs_ff_4_q[7]));  // open: nQ
  and and_9 (M1_CMP, comparator_1_eq, rs_ff_2_q, inst_comp_1_a_new);
  and and_10 (M1_SEL, M1_VO, comparator_2_eq);
  or or_4 (or_4_out, and_7_out, and_11_out);
  and and_11 (and_11_out, comparator_3_eq, M1_VO, com1);
  and and_12 (M1_CLR, inst_comp_2_a_new, clr);
  and and_13 (M1_OLD, or_3_out[0], or_3_out[1], or_3_out[2], or_3_out[3], or_3_out[4], or_3_out[5], or_3_out[6], or_3_out[7]);
  and and_14 (and_14_out, M2_RS, ~M2_IE);  // And
  and and_15 (and_15_out, ~M2_RS, M2_DE);  // And
  and and_16 (and_16_out, or_7_out, ~M2_RS);  // And
  BitExtender #(.inputBits(1), .outputBits(8)) bitextender_4 (.in(or_5_out), .out(bitextender_4_out));
  BitExtender #(.inputBits(1), .outputBits(8)) bitextender_5 (.in(M2_RS), .out(bitextender_5_out));
  RS_FF rs_ff_12 (.S(M2_IE), .C(C), .R(and_14_out), .Q(M2_VO));  // open: nQ
  or or_5 (or_5_out, M2_IE, M2_VO);
  Comparator #(.Bits(32)) comparator_5 (.a(ld_addr), .b(M2_A), .eq(comparator_5_eq));  // open: gt, lt
  Register #(.Bits(32)) register_6 (.D(A), .C(C), .en(M2_DE), .Q(M2_A));
  RS_FF rs_ff_13 (.S(and_15_out), .C(C), .R(M2_RS), .Q(rs_ff_13_q));  // open: nQ
  Register #(.Bits(32)) register_7 (.D(D), .C(C), .en(M2_DE), .Q(M2_D));
  Register #(.Bits(2)) register_8 (.D(MD), .C(C), .en(M2_DE), .Q(M2_MD));
  Comparator #(.Bits(4)) comparator_6 (.a(M2_inst), .b(inst_W), .eq(comparator_6_eq));  // open: gt, lt
  RS_FF rs_ff_14 (.S(and_16_out), .C(C), .R(M2_RS), .Q(M2_COM));  // open: nQ
  and and_17 (and_17_out, com2, M2_VO, comparator_8_eq);
  Comparator #(.Bits(4)) comparator_7 (.a(M2_inst), .b(com1_id), .eq(comparator_7_eq));  // open: gt, lt
  Comparator #(.Bits(4)) comparator_8 (.a(M2_inst), .b(com2_id), .eq(comparator_8_eq));  // open: gt, lt
  Register #(.Bits(4)) register_9 (.D(inst), .C(C), .en(M2_IE), .Q(M2_inst));
  Register register_10 (.D(epoch), .C(C), .en(M2_IE), .Q(M2_epoch));
  inst_comp inst_comp_3 (.A_id(ld_id), .A_ep(ld_ep), .B_id(M2_inst), .B_ep(M2_epoch), .A_new(inst_comp_3_a_new));
  inst_comp inst_comp_4 (.A_id(M2_inst), .A_ep(M2_epoch), .B_id(clr_id), .B_ep(clr_ep), .A_new(inst_comp_4_a_new));
  assign and_18_out = {M8_IE, M7_IE, M6_IE, M5_IE, M4_IE, M3_IE, M2_IE, M1_IE} & bitextender_4_out & ~bitextender_5_out;  // And and_18, 8 bits wide
  assign or_6_out = {not_3_out[7:2], 1'b0, not_3_out[0]} | rs_ff_15_q;  // Or or_6, 8 bits wide
  RS_FF rs_ff_15 (.S(and_18_out[0]), .C(C), .R(bitextender_5_out[0]), .Q(rs_ff_15_q[0]));  // open: nQ
  RS_FF rs_ff_16 (.S(and_18_out[1]), .C(C), .R(bitextender_5_out[1]), .Q(rs_ff_15_q[1]));  // open: nQ
  RS_FF rs_ff_17 (.S(and_18_out[2]), .C(C), .R(bitextender_5_out[2]), .Q(rs_ff_15_q[2]));  // open: nQ
  RS_FF rs_ff_18 (.S(and_18_out[3]), .C(C), .R(bitextender_5_out[3]), .Q(rs_ff_15_q[3]));  // open: nQ
  RS_FF rs_ff_19 (.S(and_18_out[4]), .C(C), .R(bitextender_5_out[4]), .Q(rs_ff_15_q[4]));  // open: nQ
  RS_FF rs_ff_20 (.S(and_18_out[5]), .C(C), .R(bitextender_5_out[5]), .Q(rs_ff_15_q[5]));  // open: nQ
  RS_FF rs_ff_21 (.S(and_18_out[6]), .C(C), .R(bitextender_5_out[6]), .Q(rs_ff_15_q[6]));  // open: nQ
  RS_FF rs_ff_22 (.S(and_18_out[7]), .C(C), .R(bitextender_5_out[7]), .Q(rs_ff_15_q[7]));  // open: nQ
  and and_19 (M2_CMP, comparator_5_eq, rs_ff_13_q, inst_comp_3_a_new);
  and and_20 (M2_SEL, M2_VO, comparator_6_eq);
  or or_7 (or_7_out, and_17_out, and_21_out);
  and and_21 (and_21_out, comparator_7_eq, M2_VO, com1);
  and and_22 (M2_CLR, inst_comp_4_a_new, clr);
  and and_23 (M2_OLD, or_6_out[0], or_6_out[1], or_6_out[2], or_6_out[3], or_6_out[4], or_6_out[5], or_6_out[6], or_6_out[7]);
  and and_24 (and_24_out, M3_RS, ~M3_IE);  // And
  and and_25 (and_25_out, ~M3_RS, M3_DE);  // And
  and and_26 (and_26_out, or_10_out, ~M3_RS);  // And
  BitExtender #(.inputBits(1), .outputBits(8)) bitextender_6 (.in(or_8_out), .out(bitextender_6_out));
  BitExtender #(.inputBits(1), .outputBits(8)) bitextender_7 (.in(M3_RS), .out(bitextender_7_out));
  RS_FF rs_ff_23 (.S(M3_IE), .C(C), .R(and_24_out), .Q(M3_VO));  // open: nQ
  or or_8 (or_8_out, M3_IE, M3_VO);
  Comparator #(.Bits(32)) comparator_9 (.a(ld_addr), .b(M3_A), .eq(comparator_9_eq));  // open: gt, lt
  Register #(.Bits(32)) register_11 (.D(A), .C(C), .en(M3_DE), .Q(M3_A));
  RS_FF rs_ff_24 (.S(and_25_out), .C(C), .R(M3_RS), .Q(rs_ff_24_q));  // open: nQ
  Register #(.Bits(32)) register_12 (.D(D), .C(C), .en(M3_DE), .Q(M3_D));
  Register #(.Bits(2)) register_13 (.D(MD), .C(C), .en(M3_DE), .Q(M3_MD));
  Comparator #(.Bits(4)) comparator_10 (.a(M3_inst), .b(inst_W), .eq(comparator_10_eq));  // open: gt, lt
  RS_FF rs_ff_25 (.S(and_26_out), .C(C), .R(M3_RS), .Q(M3_COM));  // open: nQ
  and and_27 (and_27_out, com2, M3_VO, comparator_12_eq);
  Comparator #(.Bits(4)) comparator_11 (.a(M3_inst), .b(com1_id), .eq(comparator_11_eq));  // open: gt, lt
  Comparator #(.Bits(4)) comparator_12 (.a(M3_inst), .b(com2_id), .eq(comparator_12_eq));  // open: gt, lt
  Register #(.Bits(4)) register_14 (.D(inst), .C(C), .en(M3_IE), .Q(M3_inst));
  Register register_15 (.D(epoch), .C(C), .en(M3_IE), .Q(M3_epoch));
  inst_comp inst_comp_5 (.A_id(ld_id), .A_ep(ld_ep), .B_id(M3_inst), .B_ep(M3_epoch), .A_new(inst_comp_5_a_new));
  inst_comp inst_comp_6 (.A_id(M3_inst), .A_ep(M3_epoch), .B_id(clr_id), .B_ep(clr_ep), .A_new(inst_comp_6_a_new));
  assign and_28_out = {M8_IE, M7_IE, M6_IE, M5_IE, M4_IE, M3_IE, M2_IE, M1_IE} & bitextender_6_out & ~bitextender_7_out;  // And and_28, 8 bits wide
  assign or_9_out = {not_3_out[7:3], 1'b0, not_3_out[1:0]} | rs_ff_26_q;  // Or or_9, 8 bits wide
  RS_FF rs_ff_26 (.S(and_28_out[0]), .C(C), .R(bitextender_7_out[0]), .Q(rs_ff_26_q[0]));  // open: nQ
  RS_FF rs_ff_27 (.S(and_28_out[1]), .C(C), .R(bitextender_7_out[1]), .Q(rs_ff_26_q[1]));  // open: nQ
  RS_FF rs_ff_28 (.S(and_28_out[2]), .C(C), .R(bitextender_7_out[2]), .Q(rs_ff_26_q[2]));  // open: nQ
  RS_FF rs_ff_29 (.S(and_28_out[3]), .C(C), .R(bitextender_7_out[3]), .Q(rs_ff_26_q[3]));  // open: nQ
  RS_FF rs_ff_30 (.S(and_28_out[4]), .C(C), .R(bitextender_7_out[4]), .Q(rs_ff_26_q[4]));  // open: nQ
  RS_FF rs_ff_31 (.S(and_28_out[5]), .C(C), .R(bitextender_7_out[5]), .Q(rs_ff_26_q[5]));  // open: nQ
  RS_FF rs_ff_32 (.S(and_28_out[6]), .C(C), .R(bitextender_7_out[6]), .Q(rs_ff_26_q[6]));  // open: nQ
  RS_FF rs_ff_33 (.S(and_28_out[7]), .C(C), .R(bitextender_7_out[7]), .Q(rs_ff_26_q[7]));  // open: nQ
  and and_29 (M3_CMP, comparator_9_eq, rs_ff_24_q, inst_comp_5_a_new);
  and and_30 (M3_SEL, M3_VO, comparator_10_eq);
  or or_10 (or_10_out, and_27_out, and_31_out);
  and and_31 (and_31_out, comparator_11_eq, M3_VO, com1);
  and and_32 (M3_CLR, inst_comp_6_a_new, clr);
  and and_33 (M3_OLD, or_9_out[0], or_9_out[1], or_9_out[2], or_9_out[3], or_9_out[4], or_9_out[5], or_9_out[6], or_9_out[7]);
  and and_34 (and_34_out, M4_RS, ~M4_IE);  // And
  and and_35 (and_35_out, ~M4_RS, M4_DE);  // And
  and and_36 (and_36_out, or_13_out, ~M4_RS);  // And
  BitExtender #(.inputBits(1), .outputBits(8)) bitextender_8 (.in(or_11_out), .out(bitextender_8_out));
  BitExtender #(.inputBits(1), .outputBits(8)) bitextender_9 (.in(M4_RS), .out(bitextender_9_out));
  RS_FF rs_ff_34 (.S(M4_IE), .C(C), .R(and_34_out), .Q(M4_VO));  // open: nQ
  or or_11 (or_11_out, M4_IE, M4_VO);
  Comparator #(.Bits(32)) comparator_13 (.a(ld_addr), .b(M4_A), .eq(comparator_13_eq));  // open: gt, lt
  Register #(.Bits(32)) register_16 (.D(A), .C(C), .en(M4_DE), .Q(M4_A));
  RS_FF rs_ff_35 (.S(and_35_out), .C(C), .R(M4_RS), .Q(rs_ff_35_q));  // open: nQ
  Register #(.Bits(32)) register_17 (.D(D), .C(C), .en(M4_DE), .Q(M4_D));
  Register #(.Bits(2)) register_18 (.D(MD), .C(C), .en(M4_DE), .Q(M4_MD));
  Comparator #(.Bits(4)) comparator_14 (.a(M4_inst), .b(inst_W), .eq(comparator_14_eq));  // open: gt, lt
  RS_FF rs_ff_36 (.S(and_36_out), .C(C), .R(M4_RS), .Q(M4_COM));  // open: nQ
  and and_37 (and_37_out, com2, M4_VO, comparator_16_eq);
  Comparator #(.Bits(4)) comparator_15 (.a(M4_inst), .b(com1_id), .eq(comparator_15_eq));  // open: gt, lt
  Comparator #(.Bits(4)) comparator_16 (.a(M4_inst), .b(com2_id), .eq(comparator_16_eq));  // open: gt, lt
  Register #(.Bits(4)) register_19 (.D(inst), .C(C), .en(M4_IE), .Q(M4_inst));
  Register register_20 (.D(epoch), .C(C), .en(M4_IE), .Q(M4_epoch));
  inst_comp inst_comp_7 (.A_id(ld_id), .A_ep(ld_ep), .B_id(M4_inst), .B_ep(M4_epoch), .A_new(inst_comp_7_a_new));
  inst_comp inst_comp_8 (.A_id(M4_inst), .A_ep(M4_epoch), .B_id(clr_id), .B_ep(clr_ep), .A_new(inst_comp_8_a_new));
  assign and_38_out = {M8_IE, M7_IE, M6_IE, M5_IE, M4_IE, M3_IE, M2_IE, M1_IE} & bitextender_8_out & ~bitextender_9_out;  // And and_38, 8 bits wide
  assign or_12_out = {not_3_out[7:4], 1'b0, not_3_out[2:0]} | rs_ff_37_q;  // Or or_12, 8 bits wide
  RS_FF rs_ff_37 (.S(and_38_out[0]), .C(C), .R(bitextender_9_out[0]), .Q(rs_ff_37_q[0]));  // open: nQ
  RS_FF rs_ff_38 (.S(and_38_out[1]), .C(C), .R(bitextender_9_out[1]), .Q(rs_ff_37_q[1]));  // open: nQ
  RS_FF rs_ff_39 (.S(and_38_out[2]), .C(C), .R(bitextender_9_out[2]), .Q(rs_ff_37_q[2]));  // open: nQ
  RS_FF rs_ff_40 (.S(and_38_out[3]), .C(C), .R(bitextender_9_out[3]), .Q(rs_ff_37_q[3]));  // open: nQ
  RS_FF rs_ff_41 (.S(and_38_out[4]), .C(C), .R(bitextender_9_out[4]), .Q(rs_ff_37_q[4]));  // open: nQ
  RS_FF rs_ff_42 (.S(and_38_out[5]), .C(C), .R(bitextender_9_out[5]), .Q(rs_ff_37_q[5]));  // open: nQ
  RS_FF rs_ff_43 (.S(and_38_out[6]), .C(C), .R(bitextender_9_out[6]), .Q(rs_ff_37_q[6]));  // open: nQ
  RS_FF rs_ff_44 (.S(and_38_out[7]), .C(C), .R(bitextender_9_out[7]), .Q(rs_ff_37_q[7]));  // open: nQ
  and and_39 (M4_CMP, comparator_13_eq, rs_ff_35_q, inst_comp_7_a_new);
  and and_40 (M4_SEL, M4_VO, comparator_14_eq);
  or or_13 (or_13_out, and_37_out, and_41_out);
  and and_41 (and_41_out, comparator_15_eq, M4_VO, com1);
  and and_42 (M4_CLR, inst_comp_8_a_new, clr);
  and and_43 (M4_OLD, or_12_out[0], or_12_out[1], or_12_out[2], or_12_out[3], or_12_out[4], or_12_out[5], or_12_out[6], or_12_out[7]);
  and and_44 (and_44_out, M5_RS, ~M5_IE);  // And
  and and_45 (and_45_out, ~M5_RS, M5_DE);  // And
  and and_46 (and_46_out, or_16_out, ~M5_RS);  // And
  BitExtender #(.inputBits(1), .outputBits(8)) bitextender_10 (.in(or_14_out), .out(bitextender_10_out));
  BitExtender #(.inputBits(1), .outputBits(8)) bitextender_11 (.in(M5_RS), .out(bitextender_11_out));
  RS_FF rs_ff_45 (.S(M5_IE), .C(C), .R(and_44_out), .Q(M5_VO));  // open: nQ
  or or_14 (or_14_out, M5_IE, M5_VO);
  Comparator #(.Bits(32)) comparator_17 (.a(ld_addr), .b(M5_A), .eq(comparator_17_eq));  // open: gt, lt
  Register #(.Bits(32)) register_21 (.D(A), .C(C), .en(M5_DE), .Q(M5_A));
  RS_FF rs_ff_46 (.S(and_45_out), .C(C), .R(M5_RS), .Q(rs_ff_46_q));  // open: nQ
  Register #(.Bits(32)) register_22 (.D(D), .C(C), .en(M5_DE), .Q(M5_D));
  Register #(.Bits(2)) register_23 (.D(MD), .C(C), .en(M5_DE), .Q(M5_MD));
  Comparator #(.Bits(4)) comparator_18 (.a(M5_inst), .b(inst_W), .eq(comparator_18_eq));  // open: gt, lt
  RS_FF rs_ff_47 (.S(and_46_out), .C(C), .R(M5_RS), .Q(M5_COM));  // open: nQ
  and and_47 (and_47_out, com2, M5_VO, comparator_20_eq);
  Comparator #(.Bits(4)) comparator_19 (.a(M5_inst), .b(com1_id), .eq(comparator_19_eq));  // open: gt, lt
  Comparator #(.Bits(4)) comparator_20 (.a(M5_inst), .b(com2_id), .eq(comparator_20_eq));  // open: gt, lt
  Register #(.Bits(4)) register_24 (.D(inst), .C(C), .en(M5_IE), .Q(M5_inst));
  Register register_25 (.D(epoch), .C(C), .en(M5_IE), .Q(M5_epoch));
  inst_comp inst_comp_9 (.A_id(ld_id), .A_ep(ld_ep), .B_id(M5_inst), .B_ep(M5_epoch), .A_new(inst_comp_9_a_new));
  inst_comp inst_comp_10 (.A_id(M5_inst), .A_ep(M5_epoch), .B_id(clr_id), .B_ep(clr_ep), .A_new(inst_comp_10_a_new));
  assign and_48_out = {M8_IE, M7_IE, M6_IE, M5_IE, M4_IE, M3_IE, M2_IE, M1_IE} & bitextender_10_out & ~bitextender_11_out;  // And and_48, 8 bits wide
  assign or_15_out = {not_3_out[7:5], 1'b0, not_3_out[3:0]} | rs_ff_48_q;  // Or or_15, 8 bits wide
  RS_FF rs_ff_48 (.S(and_48_out[0]), .C(C), .R(bitextender_11_out[0]), .Q(rs_ff_48_q[0]));  // open: nQ
  RS_FF rs_ff_49 (.S(and_48_out[1]), .C(C), .R(bitextender_11_out[1]), .Q(rs_ff_48_q[1]));  // open: nQ
  RS_FF rs_ff_50 (.S(and_48_out[2]), .C(C), .R(bitextender_11_out[2]), .Q(rs_ff_48_q[2]));  // open: nQ
  RS_FF rs_ff_51 (.S(and_48_out[3]), .C(C), .R(bitextender_11_out[3]), .Q(rs_ff_48_q[3]));  // open: nQ
  RS_FF rs_ff_52 (.S(and_48_out[4]), .C(C), .R(bitextender_11_out[4]), .Q(rs_ff_48_q[4]));  // open: nQ
  RS_FF rs_ff_53 (.S(and_48_out[5]), .C(C), .R(bitextender_11_out[5]), .Q(rs_ff_48_q[5]));  // open: nQ
  RS_FF rs_ff_54 (.S(and_48_out[6]), .C(C), .R(bitextender_11_out[6]), .Q(rs_ff_48_q[6]));  // open: nQ
  RS_FF rs_ff_55 (.S(and_48_out[7]), .C(C), .R(bitextender_11_out[7]), .Q(rs_ff_48_q[7]));  // open: nQ
  and and_49 (M5_CMP, comparator_17_eq, rs_ff_46_q, inst_comp_9_a_new);
  and and_50 (M5_SEL, M5_VO, comparator_18_eq);
  or or_16 (or_16_out, and_47_out, and_51_out);
  and and_51 (and_51_out, comparator_19_eq, M5_VO, com1);
  and and_52 (M5_CLR, inst_comp_10_a_new, clr);
  and and_53 (M5_OLD, or_15_out[0], or_15_out[1], or_15_out[2], or_15_out[3], or_15_out[4], or_15_out[5], or_15_out[6], or_15_out[7]);
  and and_54 (and_54_out, M6_RS, ~M6_IE);  // And
  and and_55 (and_55_out, ~M6_RS, M6_DE);  // And
  and and_56 (and_56_out, or_19_out, ~M6_RS);  // And
  BitExtender #(.inputBits(1), .outputBits(8)) bitextender_12 (.in(or_17_out), .out(bitextender_12_out));
  BitExtender #(.inputBits(1), .outputBits(8)) bitextender_13 (.in(M6_RS), .out(bitextender_13_out));
  RS_FF rs_ff_56 (.S(M6_IE), .C(C), .R(and_54_out), .Q(M6_VO));  // open: nQ
  or or_17 (or_17_out, M6_IE, M6_VO);
  Comparator #(.Bits(32)) comparator_21 (.a(ld_addr), .b(M6_A), .eq(comparator_21_eq));  // open: gt, lt
  Register #(.Bits(32)) register_26 (.D(A), .C(C), .en(M6_DE), .Q(M6_A));
  RS_FF rs_ff_57 (.S(and_55_out), .C(C), .R(M6_RS), .Q(rs_ff_57_q));  // open: nQ
  Register #(.Bits(32)) register_27 (.D(D), .C(C), .en(M6_DE), .Q(M6_D));
  Register #(.Bits(2)) register_28 (.D(MD), .C(C), .en(M6_DE), .Q(M6_MD));
  Comparator #(.Bits(4)) comparator_22 (.a(M6_inst), .b(inst_W), .eq(comparator_22_eq));  // open: gt, lt
  RS_FF rs_ff_58 (.S(and_56_out), .C(C), .R(M6_RS), .Q(M6_COM));  // open: nQ
  and and_57 (and_57_out, com2, M6_VO, comparator_24_eq);
  Comparator #(.Bits(4)) comparator_23 (.a(M6_inst), .b(com1_id), .eq(comparator_23_eq));  // open: gt, lt
  Comparator #(.Bits(4)) comparator_24 (.a(M6_inst), .b(com2_id), .eq(comparator_24_eq));  // open: gt, lt
  Register #(.Bits(4)) register_29 (.D(inst), .C(C), .en(M6_IE), .Q(M6_inst));
  Register register_30 (.D(epoch), .C(C), .en(M6_IE), .Q(M6_epoch));
  inst_comp inst_comp_11 (.A_id(ld_id), .A_ep(ld_ep), .B_id(M6_inst), .B_ep(M6_epoch), .A_new(inst_comp_11_a_new));
  inst_comp inst_comp_12 (.A_id(M6_inst), .A_ep(M6_epoch), .B_id(clr_id), .B_ep(clr_ep), .A_new(inst_comp_12_a_new));
  assign and_58_out = {M8_IE, M7_IE, M6_IE, M5_IE, M4_IE, M3_IE, M2_IE, M1_IE} & bitextender_12_out & ~bitextender_13_out;  // And and_58, 8 bits wide
  assign or_18_out = {not_3_out[7:6], 1'b0, not_3_out[4:0]} | rs_ff_59_q;  // Or or_18, 8 bits wide
  RS_FF rs_ff_59 (.S(and_58_out[0]), .C(C), .R(bitextender_13_out[0]), .Q(rs_ff_59_q[0]));  // open: nQ
  RS_FF rs_ff_60 (.S(and_58_out[1]), .C(C), .R(bitextender_13_out[1]), .Q(rs_ff_59_q[1]));  // open: nQ
  RS_FF rs_ff_61 (.S(and_58_out[2]), .C(C), .R(bitextender_13_out[2]), .Q(rs_ff_59_q[2]));  // open: nQ
  RS_FF rs_ff_62 (.S(and_58_out[3]), .C(C), .R(bitextender_13_out[3]), .Q(rs_ff_59_q[3]));  // open: nQ
  RS_FF rs_ff_63 (.S(and_58_out[4]), .C(C), .R(bitextender_13_out[4]), .Q(rs_ff_59_q[4]));  // open: nQ
  RS_FF rs_ff_64 (.S(and_58_out[5]), .C(C), .R(bitextender_13_out[5]), .Q(rs_ff_59_q[5]));  // open: nQ
  RS_FF rs_ff_65 (.S(and_58_out[6]), .C(C), .R(bitextender_13_out[6]), .Q(rs_ff_59_q[6]));  // open: nQ
  RS_FF rs_ff_66 (.S(and_58_out[7]), .C(C), .R(bitextender_13_out[7]), .Q(rs_ff_59_q[7]));  // open: nQ
  and and_59 (M6_CMP, comparator_21_eq, rs_ff_57_q, inst_comp_11_a_new);
  and and_60 (M6_SEL, M6_VO, comparator_22_eq);
  or or_19 (or_19_out, and_57_out, and_61_out);
  and and_61 (and_61_out, comparator_23_eq, M6_VO, com1);
  and and_62 (M6_CLR, inst_comp_12_a_new, clr);
  and and_63 (M6_OLD, or_18_out[0], or_18_out[1], or_18_out[2], or_18_out[3], or_18_out[4], or_18_out[5], or_18_out[6], or_18_out[7]);
  and and_64 (and_64_out, M7_RS, ~M7_IE);  // And
  and and_65 (and_65_out, ~M7_RS, M7_DE);  // And
  and and_66 (and_66_out, or_22_out, ~M7_RS);  // And
  BitExtender #(.inputBits(1), .outputBits(8)) bitextender_14 (.in(or_20_out), .out(bitextender_14_out));
  BitExtender #(.inputBits(1), .outputBits(8)) bitextender_15 (.in(M7_RS), .out(bitextender_15_out));
  RS_FF rs_ff_67 (.S(M7_IE), .C(C), .R(and_64_out), .Q(M7_VO));  // open: nQ
  or or_20 (or_20_out, M7_IE, M7_VO);
  Comparator #(.Bits(32)) comparator_25 (.a(ld_addr), .b(M7_A), .eq(comparator_25_eq));  // open: gt, lt
  Register #(.Bits(32)) register_31 (.D(A), .C(C), .en(M7_DE), .Q(M7_A));
  RS_FF rs_ff_68 (.S(and_65_out), .C(C), .R(M7_RS), .Q(rs_ff_68_q));  // open: nQ
  Register #(.Bits(32)) register_32 (.D(D), .C(C), .en(M7_DE), .Q(M7_D));
  Register #(.Bits(2)) register_33 (.D(MD), .C(C), .en(M7_DE), .Q(M7_MD));
  Comparator #(.Bits(4)) comparator_26 (.a(M7_inst), .b(inst_W), .eq(comparator_26_eq));  // open: gt, lt
  RS_FF rs_ff_69 (.S(and_66_out), .C(C), .R(M7_RS), .Q(M7_COM));  // open: nQ
  and and_67 (and_67_out, com2, M7_VO, comparator_28_eq);
  Comparator #(.Bits(4)) comparator_27 (.a(M7_inst), .b(com1_id), .eq(comparator_27_eq));  // open: gt, lt
  Comparator #(.Bits(4)) comparator_28 (.a(M7_inst), .b(com2_id), .eq(comparator_28_eq));  // open: gt, lt
  Register #(.Bits(4)) register_34 (.D(inst), .C(C), .en(M7_IE), .Q(M7_inst));
  Register register_35 (.D(epoch), .C(C), .en(M7_IE), .Q(M7_epoch));
  inst_comp inst_comp_13 (.A_id(ld_id), .A_ep(ld_ep), .B_id(M7_inst), .B_ep(M7_epoch), .A_new(inst_comp_13_a_new));
  inst_comp inst_comp_14 (.A_id(M7_inst), .A_ep(M7_epoch), .B_id(clr_id), .B_ep(clr_ep), .A_new(inst_comp_14_a_new));
  assign and_68_out = {M8_IE, M7_IE, M6_IE, M5_IE, M4_IE, M3_IE, M2_IE, M1_IE} & bitextender_14_out & ~bitextender_15_out;  // And and_68, 8 bits wide
  assign or_21_out = {not_3_out[7], 1'b0, not_3_out[5:0]} | rs_ff_70_q;  // Or or_21, 8 bits wide
  RS_FF rs_ff_70 (.S(and_68_out[0]), .C(C), .R(bitextender_15_out[0]), .Q(rs_ff_70_q[0]));  // open: nQ
  RS_FF rs_ff_71 (.S(and_68_out[1]), .C(C), .R(bitextender_15_out[1]), .Q(rs_ff_70_q[1]));  // open: nQ
  RS_FF rs_ff_72 (.S(and_68_out[2]), .C(C), .R(bitextender_15_out[2]), .Q(rs_ff_70_q[2]));  // open: nQ
  RS_FF rs_ff_73 (.S(and_68_out[3]), .C(C), .R(bitextender_15_out[3]), .Q(rs_ff_70_q[3]));  // open: nQ
  RS_FF rs_ff_74 (.S(and_68_out[4]), .C(C), .R(bitextender_15_out[4]), .Q(rs_ff_70_q[4]));  // open: nQ
  RS_FF rs_ff_75 (.S(and_68_out[5]), .C(C), .R(bitextender_15_out[5]), .Q(rs_ff_70_q[5]));  // open: nQ
  RS_FF rs_ff_76 (.S(and_68_out[6]), .C(C), .R(bitextender_15_out[6]), .Q(rs_ff_70_q[6]));  // open: nQ
  RS_FF rs_ff_77 (.S(and_68_out[7]), .C(C), .R(bitextender_15_out[7]), .Q(rs_ff_70_q[7]));  // open: nQ
  and and_69 (M7_CMP, comparator_25_eq, rs_ff_68_q, inst_comp_13_a_new);
  and and_70 (M7_SEL, M7_VO, comparator_26_eq);
  or or_22 (or_22_out, and_67_out, and_71_out);
  and and_71 (and_71_out, comparator_27_eq, M7_VO, com1);
  and and_72 (M7_CLR, inst_comp_14_a_new, clr);
  and and_73 (M7_OLD, or_21_out[0], or_21_out[1], or_21_out[2], or_21_out[3], or_21_out[4], or_21_out[5], or_21_out[6], or_21_out[7]);
  and and_74 (and_74_out, M8_RS, ~M8_IE);  // And
  and and_75 (and_75_out, ~M8_RS, M8_DE);  // And
  and and_76 (and_76_out, or_25_out, ~M8_RS);  // And
  BitExtender #(.inputBits(1), .outputBits(8)) bitextender_16 (.in(or_23_out), .out(bitextender_16_out));
  BitExtender #(.inputBits(1), .outputBits(8)) bitextender_17 (.in(M8_RS), .out(bitextender_17_out));
  RS_FF rs_ff_78 (.S(M8_IE), .C(C), .R(and_74_out), .Q(M8_VO));  // open: nQ
  or or_23 (or_23_out, M8_IE, M8_VO);
  Comparator #(.Bits(32)) comparator_29 (.a(ld_addr), .b(M8_A), .eq(comparator_29_eq));  // open: gt, lt
  Register #(.Bits(32)) register_36 (.D(A), .C(C), .en(M8_DE), .Q(M8_A));
  RS_FF rs_ff_79 (.S(and_75_out), .C(C), .R(M8_RS), .Q(rs_ff_79_q));  // open: nQ
  Register #(.Bits(32)) register_37 (.D(D), .C(C), .en(M8_DE), .Q(M8_D));
  Register #(.Bits(2)) register_38 (.D(MD), .C(C), .en(M8_DE), .Q(M8_MD));
  Comparator #(.Bits(4)) comparator_30 (.a(M8_inst), .b(inst_W), .eq(comparator_30_eq));  // open: gt, lt
  RS_FF rs_ff_80 (.S(and_76_out), .C(C), .R(M8_RS), .Q(M8_COM));  // open: nQ
  and and_77 (and_77_out, com2, M8_VO, comparator_32_eq);
  Comparator #(.Bits(4)) comparator_31 (.a(M8_inst), .b(com1_id), .eq(comparator_31_eq));  // open: gt, lt
  Comparator #(.Bits(4)) comparator_32 (.a(M8_inst), .b(com2_id), .eq(comparator_32_eq));  // open: gt, lt
  Register #(.Bits(4)) register_39 (.D(inst), .C(C), .en(M8_IE), .Q(M8_inst));
  Register register_40 (.D(epoch), .C(C), .en(M8_IE), .Q(M8_epoch));
  inst_comp inst_comp_15 (.A_id(ld_id), .A_ep(ld_ep), .B_id(M8_inst), .B_ep(M8_epoch), .A_new(inst_comp_15_a_new));
  inst_comp inst_comp_16 (.A_id(M8_inst), .A_ep(M8_epoch), .B_id(clr_id), .B_ep(clr_ep), .A_new(inst_comp_16_a_new));
  assign and_78_out = {M8_IE, M7_IE, M6_IE, M5_IE, M4_IE, M3_IE, M2_IE, M1_IE} & bitextender_16_out & ~bitextender_17_out;  // And and_78, 8 bits wide
  assign or_24_out = {1'b0, not_3_out[6:0]} | rs_ff_81_q;  // Or or_24, 8 bits wide
  RS_FF rs_ff_81 (.S(and_78_out[0]), .C(C), .R(bitextender_17_out[0]), .Q(rs_ff_81_q[0]));  // open: nQ
  RS_FF rs_ff_82 (.S(and_78_out[1]), .C(C), .R(bitextender_17_out[1]), .Q(rs_ff_81_q[1]));  // open: nQ
  RS_FF rs_ff_83 (.S(and_78_out[2]), .C(C), .R(bitextender_17_out[2]), .Q(rs_ff_81_q[2]));  // open: nQ
  RS_FF rs_ff_84 (.S(and_78_out[3]), .C(C), .R(bitextender_17_out[3]), .Q(rs_ff_81_q[3]));  // open: nQ
  RS_FF rs_ff_85 (.S(and_78_out[4]), .C(C), .R(bitextender_17_out[4]), .Q(rs_ff_81_q[4]));  // open: nQ
  RS_FF rs_ff_86 (.S(and_78_out[5]), .C(C), .R(bitextender_17_out[5]), .Q(rs_ff_81_q[5]));  // open: nQ
  RS_FF rs_ff_87 (.S(and_78_out[6]), .C(C), .R(bitextender_17_out[6]), .Q(rs_ff_81_q[6]));  // open: nQ
  RS_FF rs_ff_88 (.S(and_78_out[7]), .C(C), .R(bitextender_17_out[7]), .Q(rs_ff_81_q[7]));  // open: nQ
  and and_79 (M8_CMP, comparator_29_eq, rs_ff_79_q, inst_comp_15_a_new);
  and and_80 (M8_SEL, M8_VO, comparator_30_eq);
  or or_25 (or_25_out, and_77_out, and_81_out);
  and and_81 (and_81_out, comparator_31_eq, M8_VO, com1);
  and and_82 (M8_CLR, inst_comp_16_a_new, clr);
  and and_83 (M8_OLD, or_24_out[0], or_24_out[1], or_24_out[2], or_24_out[3], or_24_out[4], or_24_out[5], or_24_out[6], or_24_out[7]);

  // Other names for the same wires on the sheet: clear = clr; comp_addr[31:0] = ld_addr; comp_ep = ld_ep;
  //   comp_id[3:0] = ld_id; ld_O[31:0] = ld_D; V_out = V
endmodule
