// Digital circuit store-controller-half.dig as structural Verilog
module store_controller_half (
  input  in1,
  input  C,
  input  in2,
  input  in3,
  input  in4,
  input  [3:0] clr,
  output out1,
  output out2,
  output out3,
  output out4,
  output ST2,
  output ST1,
  output [1:0] D2_sel,
  output [1:0] D1_sel,
  output [3:0] V
);

  wire bitselector_1_out, bitselector_2_out, bitselector_3_out, bitselector_4_out, E, not_2_out, not_3_out,
       not_5_out, not_6_out, or_1_out, or_2_out, priority_test4v_1_v, priority_test4v_2_v;
  wire [1:0] and_5_out, index_compressor_half_1_out0, index_compressor_half_1_out1,
       index_compressor_half_1_out2, index_compressor_half_1_out3, not_4_out, priorityencoder_1_num,
       register_1_q, register_2_q;
  wire [2:2] and_2_out, and_4_out, register_1_q_2, register_2_q_2;
  wire [3:0] and_1_out, bitextender_1_out, index_compressor_half_1_v, not_1_out, priority_test4v_1_out4,
       priority_test4v_2_out4, xor_1_out;
  wire [3:2] demultiplexer_1_out_0, demultiplexer_1_out_1, demultiplexer_1_out_2, demultiplexer_1_out_3;
  wire [11:0] multiplexer_1_out;

  DipSwitch #(.dipDefault("true")) dipswitch_1 (.out(E));
  assign not_1_out = ~clr;  // Not not_1, 4 bits wide
  priority_test4V priority_test4v_1 (
    .test(not_1_out), .on(1'b1), .in1(in4), .in2(in3), .in3(in2), .in4(in1),
    .out1(priority_test4v_1_out4[3]), .out2(priority_test4v_1_out4[2]), .out3(priority_test4v_1_out4[1]),
    .out4(priority_test4v_1_out4[0]), .v(priority_test4v_1_v));
  index_compressor_half index_compressor_half_1 (
    .in0(in1), .in1(in2), .in2(in3), .in3(in4), .out0(index_compressor_half_1_out0),
    .out1(index_compressor_half_1_out1), .out2(index_compressor_half_1_out2),
    .out3(index_compressor_half_1_out3), .V(index_compressor_half_1_v));
  not not_2 (not_2_out, and_5_out[0]);
  BitExtender #(.inputBits(1), .outputBits(4)) bitextender_1 (.in(not_2_out), .out(bitextender_1_out));
  assign and_1_out = bitextender_1_out & priority_test4v_1_out4;  // And and_1, 4 bits wide
  assign xor_1_out = {in4, in3, in2, in1} ^ priority_test4v_1_out4;  // XOr xor_1, 4 bits wide
  not not_3 (not_3_out, and_5_out[1]);
  priority_test4V priority_test4v_2 (
    .test(not_1_out), .on(not_3_out), .in1(xor_1_out[3]), .in2(xor_1_out[2]), .in3(xor_1_out[1]),
    .in4(xor_1_out[0]), .out1(priority_test4v_2_out4[3]), .out2(priority_test4v_2_out4[2]),
    .out3(priority_test4v_2_out4[1]), .out4(priority_test4v_2_out4[0]), .v(priority_test4v_2_v));
  PriorityEncoder #(.Selector_Bits(2)) priorityencoder_1 (
    .in0(1'b1), .in1(not_4_out[0]), .in2(not_4_out[1]), .in3(1'b0), .num(priorityencoder_1_num));  // open: any
  assign not_4_out = ~and_5_out;  // Not not_4, 2 bits wide
  Multiplexer #(.Selector_Bits(2), .Bits(12)) multiplexer_1 (
    .sel(priorityencoder_1_num),
    .in_0({index_compressor_half_1_v[3], index_compressor_half_1_out3, index_compressor_half_1_v[2], index_compressor_half_1_out2, index_compressor_half_1_v[1], index_compressor_half_1_out1, index_compressor_half_1_v[0], index_compressor_half_1_out0}),
    .in_1({3'b000, index_compressor_half_1_v[3], index_compressor_half_1_out3, index_compressor_half_1_v[2], index_compressor_half_1_out2, index_compressor_half_1_v[1], index_compressor_half_1_out1}),
    .in_2({{6{1'b0}}, index_compressor_half_1_v[3], index_compressor_half_1_out3, index_compressor_half_1_v[2], index_compressor_half_1_out2}),
    .in_3({12{1'b0}}), .out(multiplexer_1_out));
  BitSelector #(.Selector_Bits(2)) bitselector_1 (.in(clr), .sel(multiplexer_1_out[4:3]), .out(bitselector_1_out));
  and and_2 (and_2_out[2], ~bitselector_1_out, multiplexer_1_out[5]);  // And
  Register #(.Bits(3)) register_1 (
    .D({and_2_out[2], multiplexer_1_out[4:3]}), .C(C), .en(E), .Q({register_1_q_2[2], register_1_q}));
  BitSelector #(.Selector_Bits(2)) bitselector_2 (.in(clr), .sel(multiplexer_1_out[1:0]), .out(bitselector_2_out));
  BitSelector #(.Selector_Bits(2)) bitselector_3 (.in(clr), .sel(register_1_q), .out(bitselector_3_out));
  not not_5 (not_5_out, bitselector_3_out);
  and and_3 (and_5_out[0], not_5_out, register_1_q_2[2]);
  and and_4 (and_4_out[2], ~bitselector_2_out, multiplexer_1_out[2]);  // And
  Register #(.Bits(3)) register_2 (
    .D({and_4_out[2], multiplexer_1_out[1:0]}), .C(C), .en(E), .Q({register_2_q_2[2], register_2_q}));
  BitSelector #(.Selector_Bits(2)) bitselector_4 (.in(clr), .sel(register_2_q), .out(bitselector_4_out));
  not not_6 (not_6_out, bitselector_4_out);
  and and_5 (and_5_out[1], not_6_out, register_2_q_2[2]);
  Multiplexer #(.Bits(2)) multiplexer_2 (
    .sel(and_5_out[0]), .in_0(index_compressor_half_1_out1), .in_1(register_1_q), .out(D2_sel));
  Multiplexer #(.Bits(2)) multiplexer_3 (
    .sel(and_5_out[1]), .in_0(index_compressor_half_1_out0), .in_1(register_2_q), .out(D1_sel));
  or or_1 (or_1_out, priority_test4v_2_v, and_5_out[1]);
  or or_2 (or_2_out, priority_test4v_1_v, and_5_out[0]);
  Demultiplexer #(.Selector_Bits(2)) demultiplexer_1 (
    .sel(register_2_q), .in(and_5_out[1]), .out_0(demultiplexer_1_out_0[3]),
    .out_1(demultiplexer_1_out_1[3]), .out_2(demultiplexer_1_out_2[3]), .out_3(demultiplexer_1_out_3[3]));
  or or_3 (ST1, or_1_out, or_2_out);
  and and_6 (ST2, or_1_out, or_2_out);
  Demultiplexer #(.Selector_Bits(2)) demultiplexer_2 (
    .sel(register_1_q), .in(and_5_out[0]), .out_0(demultiplexer_1_out_0[2]),
    .out_1(demultiplexer_1_out_1[2]), .out_2(demultiplexer_1_out_2[2]), .out_3(demultiplexer_1_out_3[2]));
  or or_4 (V[0], demultiplexer_1_out_0[3], demultiplexer_1_out_0[2], priority_test4v_2_out4[0], and_1_out[0]);
  or or_5 (out1, clr[0], demultiplexer_1_out_0[3], demultiplexer_1_out_0[2], priority_test4v_2_out4[0], and_1_out[0]);
  or or_6 (V[1], demultiplexer_1_out_1[3], demultiplexer_1_out_1[2], priority_test4v_2_out4[1], and_1_out[1]);
  or or_7 (out2, clr[1], demultiplexer_1_out_1[3], demultiplexer_1_out_1[2], priority_test4v_2_out4[1], and_1_out[1]);
  or or_8 (V[2], demultiplexer_1_out_2[3], demultiplexer_1_out_2[2], priority_test4v_2_out4[2], and_1_out[2]);
  or or_9 (out3, clr[2], demultiplexer_1_out_2[3], demultiplexer_1_out_2[2], priority_test4v_2_out4[2], and_1_out[2]);
  or or_10 (V[3], demultiplexer_1_out_3[3], demultiplexer_1_out_3[2], priority_test4v_2_out4[3], and_1_out[3]);
  or or_11 (out4, clr[3], demultiplexer_1_out_3[3], demultiplexer_1_out_3[2], priority_test4v_2_out4[3], and_1_out[3]);

  // Other names for the same wires on the sheet: V_4[3:0] = V; clr_4[3:0] = clr; I1 = in1; I2 = in2; I3 = in3;
  //   I4 = in4; O1 = out1; O2 = out2; O3 = out3; O4 = out4
endmodule
