// Digital circuit store-controller.dig as structural Verilog
module store_controller (
  input  in1,
  input  C,
  input  in2,
  input  in3,
  input  in4,
  input  in5,
  input  in6,
  input  in7,
  input  in8,
  input  [7:0] clr,
  output out1,
  output out2,
  output out3,
  output out4,
  output out5,
  output out6,
  output out7,
  output out8,
  output ST2,
  output ST1,
  output [2:0] D2_sel,
  output [2:0] D1_sel,
  output [7:0] V
);

  wire bitselector_1_out, bitselector_2_out, bitselector_3_out, bitselector_4_out, bitselector_5_out,
       bitselector_6_out, bitselector_7_out, bitselector_8_out, bitselector_9_out, bitselector_10_out,
       bitselector_11_out, bitselector_12_out, E, not_2_out, not_3_out, not_5_out, not_6_out, not_7_out,
       not_8_out, not_9_out, not_10_out, or_1_out, or_2_out, priority_test8v_1_v, priority_test8v_2_v;
  wire [1:0] not_4_out, priorityencoder_1_num;
  wire [2:0] index_compressor_1_out0, index_compressor_1_out1, index_compressor_1_out2,
       index_compressor_1_out3, index_compressor_1_out4, index_compressor_1_out5, index_compressor_1_out6,
       index_compressor_1_out7, priorityencoder_2_num, register_1_q, register_2_q, register_3_q,
       register_4_q, register_5_q, register_6_q;
  wire [3:0] multiplexer_3_out, multiplexer_4_out, multiplexer_5_out, multiplexer_6_out;
  wire [3:2] demultiplexer_1_out_0, demultiplexer_1_out_1, demultiplexer_1_out_2, demultiplexer_1_out_3,
       demultiplexer_1_out_4, demultiplexer_1_out_5, demultiplexer_1_out_6, demultiplexer_1_out_7;
  wire [3:3] and_2_out, and_3_out, and_4_out, and_5_out, and_6_out, and_7_out, and_8_out, and_9_out,
       and_10_out, and_12_out, register_5_q_2, register_6_q_2;
  wire [5:0] and_11_out;
  wire [7:0] and_1_out, bitextender_1_out, index_compressor_1_v, not_1_out, priority_test8v_1_out8,
       priority_test8v_2_out8, xor_1_out;
  wire [31:0] multiplexer_1_out, multiplexer_2_out;

  DipSwitch #(.dipDefault("true")) dipswitch_1 (.out(E));
  assign not_1_out = ~clr;  // Not not_1, 8 bits wide
  not not_2 (not_2_out, and_11_out[4]);
  priority_test8V priority_test8v_1 (
    .test(not_1_out), .on(1'b1), .in1(in8), .in2(in7), .in3(in6), .in4(in5), .in5(in4), .in6(in3), .in7(in2),
    .in8(in1), .out1(priority_test8v_1_out8[7]), .out2(priority_test8v_1_out8[6]),
    .out3(priority_test8v_1_out8[5]), .out4(priority_test8v_1_out8[4]), .out5(priority_test8v_1_out8[3]),
    .out6(priority_test8v_1_out8[2]), .out7(priority_test8v_1_out8[1]), .out8(priority_test8v_1_out8[0]),
    .v(priority_test8v_1_v));
  index_compressor index_compressor_1 (
    .in0(in1), .in1(in2), .in2(in3), .in3(in4), .in4(in5), .in5(in6), .in6(in7), .in7(in8),
    .out0(index_compressor_1_out0), .out1(index_compressor_1_out1), .out2(index_compressor_1_out2),
    .out3(index_compressor_1_out3), .out4(index_compressor_1_out4), .out5(index_compressor_1_out5),
    .out6(index_compressor_1_out6), .out7(index_compressor_1_out7), .V(index_compressor_1_v));
  BitExtender #(.inputBits(1), .outputBits(8)) bitextender_1 (.in(not_2_out), .out(bitextender_1_out));
  assign and_1_out = bitextender_1_out & priority_test8v_1_out8;  // And and_1, 8 bits wide
  assign xor_1_out = {in8, in7, in6, in5, in4, in3, in2, in1} ^ priority_test8v_1_out8;  // XOr xor_1, 8 bits wide
  not not_3 (not_3_out, and_11_out[5]);
  priority_test8V priority_test8v_2 (
    .test(not_1_out), .on(not_3_out), .in1(xor_1_out[7]), .in2(xor_1_out[6]), .in3(xor_1_out[5]),
    .in4(xor_1_out[4]), .in5(xor_1_out[3]), .in6(xor_1_out[2]), .in7(xor_1_out[1]), .in8(xor_1_out[0]),
    .out1(priority_test8v_2_out8[7]), .out2(priority_test8v_2_out8[6]), .out3(priority_test8v_2_out8[5]),
    .out4(priority_test8v_2_out8[4]), .out5(priority_test8v_2_out8[3]), .out6(priority_test8v_2_out8[2]),
    .out7(priority_test8v_2_out8[1]), .out8(priority_test8v_2_out8[0]), .v(priority_test8v_2_v));
  PriorityEncoder #(.Selector_Bits(2)) priorityencoder_1 (
    .in0(1'b1), .in1(not_4_out[0]), .in2(not_4_out[1]), .in3(1'b0), .num(priorityencoder_1_num));  // open: any
  assign not_4_out = ~and_11_out[5:4];  // Not not_4, 2 bits wide
  Multiplexer #(.Selector_Bits(2), .Bits(32)) multiplexer_1 (
    .sel(priorityencoder_1_num),
    .in_0({index_compressor_1_v[7], index_compressor_1_out7, index_compressor_1_v[6], index_compressor_1_out6, index_compressor_1_v[5], index_compressor_1_out5, index_compressor_1_v[4], index_compressor_1_out4, index_compressor_1_v[3], index_compressor_1_out3, index_compressor_1_v[2], index_compressor_1_out2, index_compressor_1_v[1], index_compressor_1_out1, index_compressor_1_v[0], index_compressor_1_out0}),
    .in_1({4'b0000, index_compressor_1_v[7], index_compressor_1_out7, index_compressor_1_v[6], index_compressor_1_out6, index_compressor_1_v[5], index_compressor_1_out5, index_compressor_1_v[4], index_compressor_1_out4, index_compressor_1_v[3], index_compressor_1_out3, index_compressor_1_v[2], index_compressor_1_out2, index_compressor_1_v[1], index_compressor_1_out1}),
    .in_2({{8{1'b0}}, index_compressor_1_v[7], index_compressor_1_out7, index_compressor_1_v[6], index_compressor_1_out6, index_compressor_1_v[5], index_compressor_1_out5, index_compressor_1_v[4], index_compressor_1_out4, index_compressor_1_v[3], index_compressor_1_out3, index_compressor_1_v[2], index_compressor_1_out2}),
    .in_3({32{1'b0}}), .out(multiplexer_1_out));
  PriorityEncoder #(.Selector_Bits(3)) priorityencoder_2 (
    .in0(1'b1), .in1(and_11_out[3]), .in2(and_11_out[2]), .in3(and_11_out[1]), .in4(and_11_out[0]),
    .in5(1'b0), .in6(1'b0), .in7(1'b0), .num(priorityencoder_2_num));  // open: any
  Multiplexer #(.Selector_Bits(3), .Bits(32)) multiplexer_2 (
    .sel(priorityencoder_2_num), .in_0(multiplexer_1_out), .in_1({multiplexer_1_out[27:0], 4'b0000}),
    .in_2({multiplexer_1_out[23:0], {8{1'b0}}}), .in_3({multiplexer_1_out[19:0], {12{1'b0}}}),
    .in_4({multiplexer_1_out[15:0], {16{1'b0}}}), .in_5({multiplexer_1_out[11:0], {20{1'b0}}}),
    .in_6({32{1'b0}}), .in_7({32{1'b0}}), .out(multiplexer_2_out));
  BitSelector #(.Selector_Bits(3)) bitselector_1 (.in(clr), .sel(multiplexer_2_out[22:20]), .out(bitselector_1_out));
  and and_2 (and_2_out[3], ~bitselector_1_out, multiplexer_2_out[23]);  // And
  Register #(.Bits(4)) register_1 (
    .D({and_2_out[3], multiplexer_2_out[22:20]}), .C(C), .en(E), .Q({and_11_out[0], register_1_q}));
  BitSelector #(.Selector_Bits(3)) bitselector_2 (.in(clr), .sel(multiplexer_2_out[18:16]), .out(bitselector_2_out));
  BitSelector #(.Selector_Bits(3)) bitselector_3 (.in(clr), .sel(register_1_q), .out(bitselector_3_out));
  not not_5 (not_5_out, bitselector_3_out);
  and and_3 (and_3_out[3], not_5_out, and_11_out[0]);
  and and_4 (and_4_out[3], ~bitselector_2_out, multiplexer_2_out[19]);  // And
  BitSelector #(.Selector_Bits(3)) bitselector_4 (.in(clr), .sel(register_2_q), .out(bitselector_4_out));
  Register #(.Bits(4)) register_2 (
    .D({and_4_out[3], multiplexer_2_out[18:16]}), .C(C), .en(E), .Q({and_11_out[1], register_2_q}));
  BitSelector #(.Selector_Bits(3)) bitselector_5 (.in(clr), .sel(multiplexer_2_out[14:12]), .out(bitselector_5_out));
  Multiplexer #(.Bits(4)) multiplexer_3 (
    .sel(and_11_out[0]), .in_0({and_6_out[3], multiplexer_2_out[14:12]}),
    .in_1({and_3_out[3], register_1_q}), .out(multiplexer_3_out));
  not not_6 (not_6_out, bitselector_4_out);
  and and_5 (and_5_out[3], not_6_out, and_11_out[1]);
  and and_6 (and_6_out[3], ~bitselector_5_out, multiplexer_2_out[15]);  // And
  Register #(.Bits(4)) register_3 (.D(multiplexer_3_out), .C(C), .en(E), .Q({and_11_out[2], register_3_q}));
  BitSelector #(.Selector_Bits(3)) bitselector_6 (.in(clr), .sel(multiplexer_2_out[10:8]), .out(bitselector_6_out));
  BitSelector #(.Selector_Bits(3)) bitselector_7 (.in(clr), .sel(register_3_q), .out(bitselector_7_out));
  Multiplexer #(.Bits(4)) multiplexer_4 (
    .sel(and_11_out[1]), .in_0({and_8_out[3], multiplexer_2_out[10:8]}), .in_1({and_5_out[3], register_2_q}),
    .out(multiplexer_4_out));
  not not_7 (not_7_out, bitselector_7_out);
  and and_7 (and_7_out[3], not_7_out, and_11_out[2]);
  and and_8 (and_8_out[3], ~bitselector_6_out, multiplexer_2_out[11]);  // And
  Register #(.Bits(4)) register_4 (.D(multiplexer_4_out), .C(C), .en(E), .Q({and_11_out[3], register_4_q}));
  BitSelector #(.Selector_Bits(3)) bitselector_8 (.in(clr), .sel(multiplexer_2_out[6:4]), .out(bitselector_8_out));
  BitSelector #(.Selector_Bits(3)) bitselector_9 (.in(clr), .sel(register_4_q), .out(bitselector_9_out));
  not not_8 (not_8_out, bitselector_9_out);
  and and_9 (and_9_out[3], not_8_out, and_11_out[3]);
  and and_10 (and_10_out[3], ~bitselector_8_out, multiplexer_2_out[7]);  // And
  Multiplexer #(.Bits(4)) multiplexer_5 (
    .sel(and_11_out[2]), .in_0({and_10_out[3], multiplexer_2_out[6:4]}), .in_1({and_7_out[3], register_3_q}),
    .out(multiplexer_5_out));
  Register #(.Bits(4)) register_5 (.D(multiplexer_5_out), .C(C), .en(E), .Q({register_5_q_2[3], register_5_q}));
  BitSelector #(.Selector_Bits(3)) bitselector_10 (.in(clr), .sel(multiplexer_2_out[2:0]), .out(bitselector_10_out));
  BitSelector #(.Selector_Bits(3)) bitselector_11 (.in(clr), .sel(register_5_q), .out(bitselector_11_out));
  not not_9 (not_9_out, bitselector_11_out);
  and and_11 (and_11_out[4], not_9_out, register_5_q_2[3]);
  and and_12 (and_12_out[3], ~bitselector_10_out, multiplexer_2_out[3]);  // And
  Multiplexer #(.Bits(4)) multiplexer_6 (
    .sel(and_11_out[3]), .in_0({and_12_out[3], multiplexer_2_out[2:0]}), .in_1({and_9_out[3], register_4_q}),
    .out(multiplexer_6_out));
  BitSelector #(.Selector_Bits(3)) bitselector_12 (.in(clr), .sel(register_6_q), .out(bitselector_12_out));
  Register #(.Bits(4)) register_6 (.D(multiplexer_6_out), .C(C), .en(E), .Q({register_6_q_2[3], register_6_q}));
  Multiplexer #(.Bits(3)) multiplexer_7 (
    .sel(and_11_out[4]), .in_0(index_compressor_1_out1), .in_1(register_5_q), .out(D2_sel));
  Multiplexer #(.Bits(3)) multiplexer_8 (
    .sel(and_11_out[5]), .in_0(index_compressor_1_out0), .in_1(register_6_q), .out(D1_sel));
  not not_10 (not_10_out, bitselector_12_out);
  and and_13 (and_11_out[5], not_10_out, register_6_q_2[3]);
  or or_1 (or_1_out, priority_test8v_2_v, and_11_out[5]);
  or or_2 (or_2_out, priority_test8v_1_v, and_11_out[4]);
  Demultiplexer #(.Selector_Bits(3)) demultiplexer_1 (
    .sel(register_6_q), .in(and_11_out[5]), .out_0(demultiplexer_1_out_0[3]),
    .out_1(demultiplexer_1_out_1[3]), .out_2(demultiplexer_1_out_2[3]), .out_3(demultiplexer_1_out_3[3]),
    .out_4(demultiplexer_1_out_4[3]), .out_5(demultiplexer_1_out_5[3]), .out_6(demultiplexer_1_out_6[3]),
    .out_7(demultiplexer_1_out_7[3]));
  or or_3 (ST1, or_1_out, or_2_out);
  and and_14 (ST2, or_1_out, or_2_out);
  Demultiplexer #(.Selector_Bits(3)) demultiplexer_2 (
    .sel(register_5_q), .in(and_11_out[4]), .out_0(demultiplexer_1_out_0[2]),
    .out_1(demultiplexer_1_out_1[2]), .out_2(demultiplexer_1_out_2[2]), .out_3(demultiplexer_1_out_3[2]),
    .out_4(demultiplexer_1_out_4[2]), .out_5(demultiplexer_1_out_5[2]), .out_6(demultiplexer_1_out_6[2]),
    .out_7(demultiplexer_1_out_7[2]));
  or or_4 (V[0], demultiplexer_1_out_0[3], demultiplexer_1_out_0[2], priority_test8v_2_out8[0], and_1_out[0]);
  or or_5 (V[7], and_1_out[7], priority_test8v_2_out8[7], demultiplexer_1_out_7[2], demultiplexer_1_out_7[3]);
  or or_6 (out1, clr[0], demultiplexer_1_out_0[3], demultiplexer_1_out_0[2], priority_test8v_2_out8[0], and_1_out[0]);
  or or_7 (out8, and_1_out[7], priority_test8v_2_out8[7], demultiplexer_1_out_7[2], demultiplexer_1_out_7[3], clr[7]);
  or or_8 (V[1], demultiplexer_1_out_1[3], demultiplexer_1_out_1[2], priority_test8v_2_out8[1], and_1_out[1]);
  or or_9 (V[6], and_1_out[6], priority_test8v_2_out8[6], demultiplexer_1_out_6[2], demultiplexer_1_out_6[3]);
  or or_10 (out2, clr[1], demultiplexer_1_out_1[3], demultiplexer_1_out_1[2], priority_test8v_2_out8[1], and_1_out[1]);
  or or_11 (out7, and_1_out[6], priority_test8v_2_out8[6], demultiplexer_1_out_6[2], demultiplexer_1_out_6[3], clr[6]);
  or or_12 (V[2], demultiplexer_1_out_2[3], demultiplexer_1_out_2[2], priority_test8v_2_out8[2], and_1_out[2]);
  or or_13 (V[5], and_1_out[5], priority_test8v_2_out8[5], demultiplexer_1_out_5[2], demultiplexer_1_out_5[3]);
  or or_14 (out3, clr[2], demultiplexer_1_out_2[3], demultiplexer_1_out_2[2], priority_test8v_2_out8[2], and_1_out[2]);
  or or_15 (out6, and_1_out[5], priority_test8v_2_out8[5], demultiplexer_1_out_5[2], demultiplexer_1_out_5[3], clr[5]);
  or or_16 (V[3], demultiplexer_1_out_3[3], demultiplexer_1_out_3[2], priority_test8v_2_out8[3], and_1_out[3]);
  or or_17 (V[4], and_1_out[4], priority_test8v_2_out8[4], demultiplexer_1_out_4[2], demultiplexer_1_out_4[3]);
  or or_18 (out4, clr[3], demultiplexer_1_out_3[3], demultiplexer_1_out_3[2], priority_test8v_2_out8[3], and_1_out[3]);
  or or_19 (out5, and_1_out[4], priority_test8v_2_out8[4], demultiplexer_1_out_4[2], demultiplexer_1_out_4[3], clr[4]);

  // Other names for the same wires on the sheet: V_8[7:0] = V; clr_8[7:0] = clr; I1 = in1; I2 = in2; I3 = in3;
  //   I4 = in4; I5 = in5; I6 = in6; I7 = in7; I8 = in8; O1 = out1; O2 = out2; O3 = out3; O4 = out4; O5 = out5;
  //   O6 = out6; O7 = out7; O8 = out8
endmodule
