// Digital circuit alu rom testing.dig as structural Verilog
module alu_rom_testing (
  input  [4:0] in_1,
  output [10:0] out_2,
  output out_3
);

  wire and_1_out, and_2_out, and_3_out, and_4_out, and_5_out, and_7_out, and_8_out, and_9_out, and_10_out,
       and_11_out, and_12_out, and_13_out, and_14_out, and_15_out, and_16_out, and_17_out, and_18_out,
       and_19_out, and_20_out;
  wire [7:0] byte0_iv;

  assign byte0_iv = ~{3'b000, in_1};  // Not not_1, 8 bits wide
  and and_1 (and_1_out, in_1[3], in_1[0]);
  and and_2 (and_2_out, in_1[2], in_1[0]);
  and and_3 (and_3_out, byte0_iv[3], byte0_iv[2], in_1[1], byte0_iv[0]);
  and and_4 (and_4_out, byte0_iv[4], in_1[3], in_1[2], in_1[1]);
  and and_5 (and_5_out, in_1[4], byte0_iv[3], byte0_iv[2], in_1[1], in_1[0]);
  and and_6 (out_2[7], byte0_iv[4], in_1[3], in_1[2]);
  and and_7 (and_7_out, in_1[4], in_1[2], byte0_iv[1]);
  and and_8 (and_8_out, in_1[4], byte0_iv[3], byte0_iv[2]);
  and and_9 (and_9_out, byte0_iv[4], byte0_iv[3], byte0_iv[2]);
  and and_10 (and_10_out, byte0_iv[4], byte0_iv[3]);
  and and_11 (and_11_out, byte0_iv[4], in_1[3], byte0_iv[2], byte0_iv[1]);
  and and_12 (and_12_out, byte0_iv[4], in_1[3], byte0_iv[2]);
  and and_13 (and_13_out, in_1[4], in_1[3]);
  and and_14 (and_14_out, byte0_iv[4], byte0_iv[3], in_1[2], byte0_iv[1]);
  and and_15 (and_15_out, in_1[4], in_1[2], in_1[1]);
  and and_16 (and_16_out, byte0_iv[4], byte0_iv[3], byte0_iv[2], in_1[1], in_1[0]);
  and and_17 (and_17_out, byte0_iv[2], byte0_iv[0]);
  and and_18 (and_18_out, in_1[2], in_1[0]);
  and and_19 (and_19_out, in_1[1], in_1[2], in_1[4]);
  and and_20 (and_20_out, in_1[3], in_1[4]);
  or or_1 (out_2[10], and_1_out, and_2_out, and_3_out);
  or or_2 (out_2[6], and_7_out, and_4_out, and_5_out);
  or or_3 (out_2[5], out_2[7], and_7_out, and_8_out);
  or or_4 (out_2[4], and_14_out, and_15_out, and_9_out);
  or or_5 (out_2[3], and_10_out, and_15_out, and_11_out);
  or or_6 (out_2[2], and_12_out, and_13_out);
  or or_7 (out_2[1], and_14_out, and_15_out, and_16_out);
  or or_8 (out_2[0], in_1[3], in_1[1], and_17_out, and_18_out);
  nor nor_1 (out_3, and_19_out, and_20_out);

  assign out_2[9:8] = 2'b00;

  // Other names for the same wires on the sheet: byte0[4:0] = in_1
endmodule
