// Digital circuit compressor test.dig as structural Verilog
module compressor_test (
  input  I1,
  input  I2,
  input  I3,
  input  I4,
  input  I5,
  input  I6,
  input  I7,
  input  I8,
  input  [3:0] in_17,
  input  [3:0] in_18,
  input  [3:0] in_19,
  input  [3:0] in_20,
  input  [3:0] in_21,
  input  [3:0] in_22,
  input  [3:0] in_23,
  input  [3:0] in_24,
  output [3:0] out_9,
  output [3:0] out_10,
  output [3:0] out_11,
  output [3:0] out_12,
  output [3:0] out_13,
  output [3:0] out_14,
  output [3:0] out_15,
  output [3:0] out_16
);

  wire and_1_out, and_2_out, and_3_out, and_4_out, and_5_out, and_6_out, and_7_out, and_8_out, and_9_out,
       and_10_out, and_11_out, and_12_out, and_13_out, nand_1_out, nand_2_out, nor_1_out, nor_2_out,
       not_1_out, not_2_out, not_3_out, not_4_out, not_5_out, or_1_out, or_2_out, or_3_out, xnor_1_out,
       xnor_2_out, xnor_3_out, xor_1_out, xor_2_out;
  wire [3:0] multiplexer_1_out, multiplexer_2_out, multiplexer_3_out, multiplexer_4_out, multiplexer_5_out,
       multiplexer_6_out, multiplexer_7_out, multiplexer_8_out, multiplexer_9_out, multiplexer_10_out,
       multiplexer_11_out, multiplexer_12_out, multiplexer_13_out, multiplexer_14_out, multiplexer_15_out,
       multiplexer_16_out;

  xnor xnor_1 (xnor_1_out, I2, I3, I4, I5, I6, I7, I8);
  xnor xnor_2 (xnor_2_out, I4, I5, I6, I7, I8);
  xnor xnor_3 (xnor_3_out, I6, I7, I8);
  not not_1 (not_1_out, I8);
  Multiplexer #(.Bits(4)) multiplexer_1 (.sel(xnor_1_out), .in_0(in_17), .in_1(in_18), .out(multiplexer_1_out));
  Multiplexer #(.Bits(4)) multiplexer_2 (.sel(xnor_1_out), .in_0(in_18), .in_1(in_17), .out(multiplexer_2_out));
  Multiplexer #(.Bits(4)) multiplexer_3 (.sel(xnor_2_out), .in_0(in_19), .in_1(in_20), .out(multiplexer_3_out));
  Multiplexer #(.Bits(4)) multiplexer_4 (.sel(xnor_2_out), .in_0(in_20), .in_1(in_19), .out(multiplexer_4_out));
  Multiplexer #(.Bits(4)) multiplexer_5 (.sel(xnor_3_out), .in_0(in_21), .in_1(in_22), .out(multiplexer_5_out));
  Multiplexer #(.Bits(4)) multiplexer_6 (.sel(xnor_3_out), .in_0(in_22), .in_1(in_21), .out(multiplexer_6_out));
  Multiplexer #(.Bits(4)) multiplexer_7 (.sel(not_1_out), .in_0(in_23), .in_1(in_24), .out(multiplexer_7_out));
  Multiplexer #(.Bits(4)) multiplexer_8 (.sel(not_1_out), .in_0(in_24), .in_1(in_23), .out(multiplexer_8_out));
  and and_1 (and_1_out, or_3_out, not_2_out);
  nand nand_1 (nand_1_out, I3, I4);
  and and_2 (and_2_out, not_3_out, or_1_out);
  nor nor_1 (nor_1_out, I3, I4);
  xor xor_1 (xor_1_out, and_1_out, nand_1_out);
  xor xor_2 (xor_2_out, and_2_out, nor_1_out);
  nand nand_2 (nand_2_out, I7, I8);
  nor nor_2 (nor_2_out, I7, I8);
  Multiplexer #(.Bits(4)) multiplexer_9 (
    .sel(xor_2_out), .in_0(multiplexer_1_out), .in_1(multiplexer_3_out), .out(multiplexer_9_out));
  Multiplexer #(.Bits(4)) multiplexer_10 (
    .sel(xor_1_out), .in_0(multiplexer_2_out), .in_1(multiplexer_4_out), .out(multiplexer_10_out));
  Multiplexer #(.Bits(4)) multiplexer_11 (
    .sel(xor_2_out), .in_0(multiplexer_3_out), .in_1(multiplexer_1_out), .out(multiplexer_11_out));
  Multiplexer #(.Bits(4)) multiplexer_12 (
    .sel(xor_1_out), .in_0(multiplexer_4_out), .in_1(multiplexer_2_out), .out(multiplexer_12_out));
  Multiplexer #(.Bits(4)) multiplexer_13 (
    .sel(nand_2_out), .in_0(multiplexer_5_out), .in_1(multiplexer_7_out), .out(multiplexer_13_out));
  Multiplexer #(.Bits(4)) multiplexer_14 (
    .sel(nor_2_out), .in_0(multiplexer_6_out), .in_1(multiplexer_8_out), .out(multiplexer_14_out));
  Multiplexer #(.Bits(4)) multiplexer_15 (
    .sel(nand_2_out), .in_0(multiplexer_7_out), .in_1(multiplexer_5_out), .out(multiplexer_15_out));
  Multiplexer #(.Bits(4)) multiplexer_16 (
    .sel(nor_2_out), .in_0(multiplexer_8_out), .in_1(multiplexer_6_out), .out(multiplexer_16_out));
  and and_3 (and_3_out, I5, I6, I7, I8);
  and and_4 (and_4_out, I5, I6, I7);
  and and_5 (and_5_out, I6, I7, I8);
  and and_6 (and_6_out, I5, I7, I8);
  and and_7 (and_7_out, I5, I6, I8);
  and and_8 (and_8_out, I5, I6);
  and and_9 (and_9_out, I6, I7);
  and and_10 (and_10_out, I7, I8);
  and and_11 (and_11_out, I5, I8);
  and and_12 (and_12_out, I5, I7);
  and and_13 (and_13_out, I6, I8);
  or or_1 (or_1_out, I5, I6, I7, I8);
  or or_2 (or_2_out, and_4_out, and_5_out, and_6_out, and_7_out);
  or or_3 (or_3_out, and_8_out, and_9_out, and_10_out, and_11_out, and_12_out, and_13_out);
  not not_2 (not_2_out, and_3_out);
  not not_3 (not_3_out, or_2_out);
  not not_4 (not_4_out, or_3_out);
  not not_5 (not_5_out, or_1_out);
  Multiplexer #(.Bits(4)) multiplexer_17 (
    .sel(not_2_out), .in_0(multiplexer_9_out), .in_1(multiplexer_13_out), .out(out_9));
  Multiplexer #(.Bits(4)) multiplexer_18 (
    .sel(not_3_out), .in_0(multiplexer_10_out), .in_1(multiplexer_14_out), .out(out_10));
  Multiplexer #(.Bits(4)) multiplexer_19 (
    .sel(not_4_out), .in_0(multiplexer_11_out), .in_1(multiplexer_15_out), .out(out_11));
  Multiplexer #(.Bits(4)) multiplexer_20 (
    .sel(not_5_out), .in_0(multiplexer_12_out), .in_1(multiplexer_16_out), .out(out_12));
  Multiplexer #(.Bits(4)) multiplexer_21 (
    .sel(not_2_out), .in_0(multiplexer_13_out), .in_1(multiplexer_9_out), .out(out_13));
  Multiplexer #(.Bits(4)) multiplexer_22 (
    .sel(not_3_out), .in_0(multiplexer_14_out), .in_1(multiplexer_10_out), .out(out_14));
  Multiplexer #(.Bits(4)) multiplexer_23 (
    .sel(not_4_out), .in_0(multiplexer_15_out), .in_1(multiplexer_11_out), .out(out_15));
  Multiplexer #(.Bits(4)) multiplexer_24 (
    .sel(not_5_out), .in_0(multiplexer_16_out), .in_1(multiplexer_12_out), .out(out_16));

  // Notes on the sheet:
  //   in_17: default 1
  //   in_18: default 2
  //   in_19: default 3
  //   in_20: default 4
  //   in_21: default 5
  //   in_22: default 6
  //   in_23: default 7
  //   in_24: default 8
endmodule
