// Digital circuit new queue test.dig as structural Verilog
module new_queue_test (
  input  in_1,
  input  clk,
  input  in_3,
  input  in_5,
  input  [3:0] in_6,
  input  in_7,
  input  [3:0] in_8,
  input  in_9,
  output out_4
);

  wire and_1_out, and_2_out, inst_comp_1_a_old, inst_comp_2_a_old, inst_comp_3_a_old, MB_ep,
       multiplexer_1_out, multiplexer_3_out, multiplexer_4_out, multiplexer_6_out, multiplexer_7_out,
       multiplexer_8_out, multiplexer_10_out, not_1_out, not_3_out, not_4_out, or_1_out, or_2_out, or_3_out,
       register_2_q, register_6_q, STB_LD;
  wire [1:1] register_4_q;
  wire [2:0] and_3_out, multiplexer_2_out, nand_1_out, nand_2_out, not_2_out, register_3_q;
  wire [3:0] MB_id, multiplexer_5_out, multiplexer_9_out, register_1_q, register_5_q;

  DipSwitch dipswitch_1 (.out(STB_LD));
  not not_1 (not_1_out, in_9);
  not not_2 (not_2_out[0], register_3_q[0]);
  Multiplexer multiplexer_1 (.sel(and_3_out[2]), .in_0(nand_1_out[2]), .in_1(not_1_out), .out(multiplexer_1_out));
  and and_1 (and_1_out, multiplexer_1_out, in_1);
  xor xor_1 (not_2_out[1], register_3_q[0], register_3_q[1]);
  xor xor_2 (not_2_out[2], register_3_q[1], register_3_q[2]);
  Register #(.Bits(4)) register_1 (.D(in_6), .C(clk), .en(multiplexer_2_out[2]), .Q(register_1_q));
  Register register_2 (.D(in_5), .C(clk), .en(multiplexer_2_out[2]), .Q(register_2_q));
  Register register_3 (.D(and_1_out), .C(clk), .en(or_1_out), .Q(register_3_q[2]));
  not not_3 (not_3_out, multiplexer_1_out);
  or or_1 (or_1_out, not_3_out, multiplexer_2_out[2]);
  Multiplexer #(.Bits(3)) multiplexer_2 (.sel(or_2_out), .in_0(not_2_out), .in_1(and_3_out), .out(multiplexer_2_out));
  or or_2 (or_2_out, and_3_out[0], and_3_out[1], and_3_out[2]);
  Multiplexer multiplexer_3 (.sel(and_3_out[1]), .in_0(nand_1_out[1]), .in_1(nand_1_out[2]), .out(multiplexer_3_out));
  Multiplexer multiplexer_4 (.sel(register_3_q[2]), .in_0(in_1), .in_1(register_3_q[2]), .out(multiplexer_4_out));
  Multiplexer #(.Bits(4)) multiplexer_5 (
    .sel(register_3_q[2]), .in_0(in_6), .in_1(register_1_q), .out(multiplexer_5_out));
  inst_comp inst_comp_1 (.A_id(register_1_q), .A_ep(register_2_q), .B_id(in_8), .B_ep(in_7), .A_old(inst_comp_1_a_old));
  Multiplexer multiplexer_6 (.sel(register_3_q[2]), .in_0(in_5), .in_1(register_2_q), .out(multiplexer_6_out));
  and and_2 (and_2_out, multiplexer_3_out, multiplexer_4_out);
  Register register_4 (.D(and_2_out), .C(clk), .en(or_3_out), .Q(register_4_q[1]));
  not not_4 (not_4_out, multiplexer_3_out);
  or or_3 (or_3_out, not_4_out, multiplexer_2_out[1]);
  or or_4 (register_3_q[1], register_4_q[1], register_3_q[2]);
  nand nand_1 (nand_1_out[2], inst_comp_1_a_old, in_9);
  Register #(.Bits(4)) register_5 (.D(multiplexer_5_out), .C(clk), .en(multiplexer_2_out[1]), .Q(register_5_q));
  Register register_6 (.D(multiplexer_6_out), .C(clk), .en(multiplexer_2_out[1]), .Q(register_6_q));
  Multiplexer multiplexer_7 (.sel(and_3_out[0]), .in_0(nand_1_out[0]), .in_1(nand_1_out[1]), .out(multiplexer_7_out));
  Multiplexer multiplexer_8 (.sel(register_3_q[1]), .in_0(in_1), .in_1(register_4_q[1]), .out(multiplexer_8_out));
  or or_5 (register_3_q[0], in_3, register_4_q[1], register_3_q[2]);
  assign and_3_out = nand_2_out & register_3_q;  // And and_3, 3 bits wide
  Multiplexer #(.Bits(4)) multiplexer_9 (
    .sel(register_3_q[1]), .in_0(in_6), .in_1(register_5_q), .out(multiplexer_9_out));
  inst_comp inst_comp_2 (.A_id(register_5_q), .A_ep(register_6_q), .B_id(in_8), .B_ep(in_7), .A_old(inst_comp_2_a_old));
  Multiplexer multiplexer_10 (.sel(register_3_q[1]), .in_0(in_5), .in_1(register_6_q), .out(multiplexer_10_out));
  and and_4 (out_4, multiplexer_7_out, multiplexer_8_out);
  nand nand_2 (nand_2_out[2], in_3, register_4_q[1], register_3_q[2]);
  nand nand_3 (nand_1_out[1], inst_comp_2_a_old, in_9);
  Register #(.Bits(4)) register_7 (.D(multiplexer_9_out), .C(clk), .en(STB_LD), .Q(MB_id));
  Register register_8 (.D(multiplexer_10_out), .C(clk), .en(STB_LD), .Q(MB_ep));
  nand nand_4 (nand_2_out[1], in_3, register_4_q[1]);
  inst_comp inst_comp_3 (.A_id(MB_id), .A_ep(MB_ep), .B_id(in_8), .B_ep(in_7), .A_old(inst_comp_3_a_old));
  not not_5 (nand_2_out[0], in_3);
  nand nand_5 (nand_1_out[0], inst_comp_3_a_old, in_9);

  // Other names for the same wires on the sheet: B = in_3; C_ct = clk; clr = in_9; clr_ep = in_7; clr_id[3:0] = in_8;
  //   CT_FU__EPOCH = in_5; CT_FU__INST[3:0] = in_6; L = in_1; O = out_4
endmodule
