// Digital circuit compressor test 2.dig as structural Verilog
module compressor_test_2 (
  input  I1,
  input  I2,
  input  I3,
  input  I4,
  input  I5,
  input  I6,
  input  I7,
  input  I0,
  output [2:0] O0,
  output [2:0] O1,
  output [2:0] O2,
  output [2:0] O3,
  output [2:0] O4,
  output [2:0] O5,
  output [2:0] O6,
  output [2:0] O7
);

  wire [1:0] add_1_c_o, add_2_c_o, add_3_c_o, add_4_s, add_5_s, add_6_s;
  wire [2:0] add_7_s, add_8_s, add_9_s, and_1_out, and_2_out, and_3_out, and_4_out, and_5_out, and_6_out,
       and_7_out, bitextender_1_out, bitextender_2_out, bitextender_3_out, bitextender_4_out,
       bitextender_5_out, bitextender_6_out, bitextender_7_out, demultiplexer_1_out_0, demultiplexer_1_out_1,
       demultiplexer_2_out_0, demultiplexer_2_out_1, demultiplexer_2_out_2, demultiplexer_2_out_3,
       demultiplexer_2_out_4, demultiplexer_2_out_5, demultiplexer_2_out_6, demultiplexer_3_out_0,
       demultiplexer_3_out_1, demultiplexer_3_out_2, demultiplexer_4_out_0, demultiplexer_4_out_1,
       demultiplexer_4_out_2, demultiplexer_4_out_3, demultiplexer_4_out_4, demultiplexer_4_out_5,
       demultiplexer_4_out_6, demultiplexer_5_out_0, demultiplexer_5_out_1, demultiplexer_5_out_2,
       demultiplexer_5_out_3, demultiplexer_6_out_0, demultiplexer_6_out_1, demultiplexer_6_out_2,
       demultiplexer_6_out_3, demultiplexer_6_out_4, demultiplexer_6_out_5, demultiplexer_7_out_0,
       demultiplexer_7_out_1, demultiplexer_7_out_2, demultiplexer_7_out_3, demultiplexer_7_out_4;
  wire [2:2] add_5_c_o;

  Add add_1 (.a(I0), .b(I1), .c_i(1'b0), .s(add_1_c_o[0]), .c_o(add_1_c_o[1]));
  Add add_2 (.a(I2), .b(I3), .c_i(1'b0), .s(add_2_c_o[0]), .c_o(add_2_c_o[1]));
  Add add_3 (.a(I4), .b(I5), .c_i(1'b0), .s(add_3_c_o[0]), .c_o(add_3_c_o[1]));
  Add #(.Bits(2)) add_4 (.a(add_1_c_o), .b({1'b0, I2}), .c_i(1'b0), .s(add_4_s));  // open: c_o
  Add #(.Bits(2)) add_5 (.a(add_1_c_o), .b(add_2_c_o), .c_i(1'b0), .s(add_5_s), .c_o(add_5_c_o[2]));
  Add #(.Bits(2)) add_6 (.a(add_3_c_o), .b({1'b0, I6}), .c_i(1'b0), .s(add_6_s));  // open: c_o
  Add #(.Bits(3)) add_7 (.a({add_5_c_o[2], add_5_s}), .b({2'b00, I4}), .c_i(1'b0), .s(add_7_s));  // open: c_o
  Add #(.Bits(3)) add_8 (.a({add_5_c_o[2], add_5_s}), .b({1'b0, add_3_c_o}), .c_i(1'b0), .s(add_8_s));  // open: c_o
  Add #(.Bits(3)) add_9 (.a({add_5_c_o[2], add_5_s}), .b({1'b0, add_6_s}), .c_i(1'b0), .s(add_9_s));  // open: c_o
  BitExtender #(.inputBits(1), .outputBits(3)) bitextender_1 (.in(I1), .out(bitextender_1_out));
  BitExtender #(.inputBits(1), .outputBits(3)) bitextender_2 (.in(I7), .out(bitextender_2_out));
  assign and_1_out = 3'b001 & bitextender_1_out;  // And and_1, 3 bits wide
  assign and_2_out = 3'b111 & bitextender_2_out;  // And and_2, 3 bits wide
  Demultiplexer #(.Bits(3)) demultiplexer_1 (
    .sel(I0), .in(and_1_out), .out_0(demultiplexer_1_out_0), .out_1(demultiplexer_1_out_1));
  Demultiplexer #(.Bits(3), .Selector_Bits(3)) demultiplexer_2 (
    .sel(add_9_s), .in(and_2_out), .out_0(demultiplexer_2_out_0), .out_1(demultiplexer_2_out_1),
    .out_2(demultiplexer_2_out_2), .out_3(demultiplexer_2_out_3), .out_4(demultiplexer_2_out_4),
    .out_5(demultiplexer_2_out_5), .out_6(demultiplexer_2_out_6), .out_7(O7));
  BitExtender #(.inputBits(1), .outputBits(3)) bitextender_3 (.in(I2), .out(bitextender_3_out));
  BitExtender #(.inputBits(1), .outputBits(3)) bitextender_4 (.in(I6), .out(bitextender_4_out));
  assign and_3_out = 3'b010 & bitextender_3_out;  // And and_3, 3 bits wide
  assign and_4_out = 3'b110 & bitextender_4_out;  // And and_4, 3 bits wide
  Demultiplexer #(.Bits(3), .Selector_Bits(2)) demultiplexer_3 (
    .sel(add_1_c_o), .in(and_3_out), .out_0(demultiplexer_3_out_0), .out_1(demultiplexer_3_out_1),
    .out_2(demultiplexer_3_out_2));  // open: out_3
  Demultiplexer #(.Selector_Bits(3), .Bits(3)) demultiplexer_4 (
    .sel(add_8_s), .in(and_4_out), .out_0(demultiplexer_4_out_0), .out_1(demultiplexer_4_out_1),
    .out_2(demultiplexer_4_out_2), .out_3(demultiplexer_4_out_3), .out_4(demultiplexer_4_out_4),
    .out_5(demultiplexer_4_out_5), .out_6(demultiplexer_4_out_6));  // open: out_7
  BitExtender #(.inputBits(1), .outputBits(3)) bitextender_5 (.in(I3), .out(bitextender_5_out));
  BitExtender #(.inputBits(1), .outputBits(3)) bitextender_6 (.in(I5), .out(bitextender_6_out));
  assign and_5_out = 3'b011 & bitextender_5_out;  // And and_5, 3 bits wide
  assign and_6_out = 3'b101 & bitextender_6_out;  // And and_6, 3 bits wide
  Demultiplexer #(.Selector_Bits(2), .Bits(3)) demultiplexer_5 (
    .sel(add_4_s), .in(and_5_out), .out_0(demultiplexer_5_out_0), .out_1(demultiplexer_5_out_1),
    .out_2(demultiplexer_5_out_2), .out_3(demultiplexer_5_out_3));
  Demultiplexer #(.Selector_Bits(3), .Bits(3)) demultiplexer_6 (
    .sel(add_7_s), .in(and_6_out), .out_0(demultiplexer_6_out_0), .out_1(demultiplexer_6_out_1),
    .out_2(demultiplexer_6_out_2), .out_3(demultiplexer_6_out_3), .out_4(demultiplexer_6_out_4),
    .out_5(demultiplexer_6_out_5));  // open: out_6, out_7
  BitExtender #(.inputBits(1), .outputBits(3)) bitextender_7 (.in(I4), .out(bitextender_7_out));
  assign and_7_out = 3'b100 & bitextender_7_out;  // And and_7, 3 bits wide
  Demultiplexer #(.Selector_Bits(3), .Bits(3)) demultiplexer_7 (
    .sel({add_5_c_o[2], add_5_s}), .in(and_7_out), .out_0(demultiplexer_7_out_0),
    .out_1(demultiplexer_7_out_1), .out_2(demultiplexer_7_out_2), .out_3(demultiplexer_7_out_3),
    .out_4(demultiplexer_7_out_4));  // open: out_5, out_6, out_7
  assign O0 = demultiplexer_1_out_0 | demultiplexer_3_out_0 | demultiplexer_5_out_0 | demultiplexer_7_out_0 | demultiplexer_6_out_0 | demultiplexer_4_out_0 | demultiplexer_2_out_0;  // Or or_1, 3 bits wide
  assign O1 = demultiplexer_1_out_1 | demultiplexer_3_out_1 | demultiplexer_5_out_1 | demultiplexer_7_out_1 | demultiplexer_6_out_1 | demultiplexer_4_out_1 | demultiplexer_2_out_1;  // Or or_2, 3 bits wide
  assign O6 = demultiplexer_2_out_6 | demultiplexer_4_out_6;  // Or or_3, 3 bits wide
  assign O2 = demultiplexer_3_out_2 | demultiplexer_5_out_2 | demultiplexer_7_out_2 | demultiplexer_6_out_2 | demultiplexer_4_out_2 | demultiplexer_2_out_2;  // Or or_4, 3 bits wide
  assign O5 = demultiplexer_2_out_5 | demultiplexer_4_out_5 | demultiplexer_6_out_5;  // Or or_5, 3 bits wide
  assign O3 = demultiplexer_5_out_3 | demultiplexer_7_out_3 | demultiplexer_6_out_3 | demultiplexer_4_out_3 | demultiplexer_2_out_3;  // Or or_6, 3 bits wide
  assign O4 = demultiplexer_2_out_4 | demultiplexer_4_out_4 | demultiplexer_6_out_4 | demultiplexer_7_out_4;  // Or or_7, 3 bits wide
endmodule
