// Digital circuit computer-32.dig as structural Verilog
module computer_32 (
  input  C
);

  wire cpu_32_1_clk_str, cpu_32_1_csh_run, cpu_32_1_d_ld, cpu_32_1_d_st, cpu_32_1_dma_str, cpu_32_1_i_ld,
       cpu_32_1_int_out, cpu_32_1_int_str, cpu_32_1_mmu_str, dipswitch_1_out, dipswitch_2_out,
       dipswitch_3_out, dipswitch_4_out, dipswitch_5_out;
  wire [1:0] cpu_32_1_csh_mode, cpu_32_1_d_md, cpu_32_1_mmu_sel;
  wire [2:0] cpu_32_1_dma_sel;
  wire [31:0] driver_1_out, driver_2_out, ramdualaccess_1_d1, ramdualaccess_1_d2, undriven, undriven_2;

  cpu_32 cpu_32_1 (
    .C(C), .E(dipswitch_1_out), .bus_e(dipswitch_2_out), .run(dipswitch_3_out), .I_valid(1'b1),
    .I_D__bus(driver_2_out), .I_A__bus(undriven), .I_LD(cpu_32_1_i_ld), .D_valid(1'b1),
    .D_D__bus(driver_1_out), .D_A__bus(undriven_2), .D_LD(cpu_32_1_d_ld), .D_ST(cpu_32_1_d_st),
    .D_MD(cpu_32_1_d_md), .INT_nor(dipswitch_4_out), .INT_nmk(dipswitch_5_out), .INT_out(cpu_32_1_int_out),
    .INT_str(cpu_32_1_int_str), .CLK_str(cpu_32_1_clk_str), .CSH_run(cpu_32_1_csh_run),
    .CSH_mode(cpu_32_1_csh_mode), .DMA_str(cpu_32_1_dma_str), .DMA_sel(cpu_32_1_dma_sel),
    .MMU_str(cpu_32_1_mmu_str), .MMU_sel(cpu_32_1_mmu_sel));
  DipSwitch dipswitch_1 (.out(dipswitch_1_out));
  DipSwitch #(.dipDefault("true")) dipswitch_2 (.out(dipswitch_2_out));
  DipSwitch dipswitch_3 (.out(dipswitch_3_out));
  DipSwitch dipswitch_4 (.out(dipswitch_4_out));
  DipSwitch dipswitch_5 (.out(dipswitch_5_out));
  RAMDualAccess #(.AddrBits(24), .isProgramMemory("true"), .Bits(32)) ramdualaccess_1 (
    .str(cpu_32_1_d_st), .C(C), .ld(1'b1), .A1(undriven_2[25:2]), .Din1(driver_1_out), .A2(undriven[25:2]),
    .D1(ramdualaccess_1_d1), .D2(ramdualaccess_1_d2));
  assign driver_1_out = cpu_32_1_d_ld ? ramdualaccess_1_d1 : 32'bz;  // Driver driver_1
  assign driver_2_out = cpu_32_1_i_ld ? ramdualaccess_1_d2 : 32'bz;  // Driver driver_2

  // Notes on the sheet:
  //   C: Hz: 64
endmodule
