// Digital circuit cpu-32 test.dig as structural Verilog
module cpu_32_test (
  input  C,
  input  bus_e,
  input  E,
  input  [31:0] I_D__bus,
  input  [31:0] D_D__bus,
  input  [31:0] I_A__bus,
  input  [31:0] D_A__bus,
  input  INT_nor,
  input  INT_nmk,
  input  run,
  input  I_valid,
  input  D_valid,
  output I_LD,
  output D_LD,
  output D_ST,
  output [1:0] MMU_sel,
  output MMU_str,
  output [2:0] DMA_sel,
  output DMA_str,
  output INT_str,
  output CLK_str,
  output [1:0] CSH_mode,
  output CSH_run,
  output INT_out,
  output [1:0] D_MD
);

  wire add_4c32_1_c, alu_32_1_p6, alu_32_1_p9, ALU_A_DRD, ALU_A_FRD, ALU_A_LD, ALU_A_LRD, ALU_A_RE,
       ALU_A_STD, ALU_A_STF, ALU_B_DRD, ALU_B_FRD, ALU_B_LD, ALU_B_LRD, ALU_B_RE, ALU_B_STD, ALU_B_STF,
       ALU_busy, ALU_free, and_1_out, and_2_out, and_3_out, and_6_out, and_7_out, and_8_out, and_9_out,
       and_10_out, and_11_out, and_13_out, and_14_out, and_15_out, and_16_out, and_17_out, and_18_out,
       and_19_out, and_20_out, and_21_out, and_22_out, and_23_out, and_24_out, and_25_out, and_26_out,
       and_27_out, and_28_out, and_29_out, and_32_out, and_33_out, and_34_out, and_35_out, and_36_out,
       and_37_out, and_38_out, and_39_out, and_45_out, and_48_out, and_49_out, and_50_out, and_51_out,
       and_52_out, and_53_out, and_54_out, and_55_out, and_62_out, and_63_out, and_64_out, and_65_out,
       and_66_out, and_67_out, and_68_out, and_69_out, and_70_out, and_71_out, and_72_out, and_73_out,
       and_75_out, and_80_out, and_81_out, and_84_out, and_85_out, and_86_out, and_87_out, and_88_out,
       and_89_out, and_90_out, and_91_out, and_92_out, and_93_out, and_94_out, and_95_out, and_96_out,
       and_97_out, and_98_out, and_99_out, and_100_out, and_101_out, and_103_out, and_104_out, and_107_out,
       and_108_out, and_109_out, C_ct, C_dt, clr, clr_ep, cm_e, cm_e__bf, com1, com1_M, com2,
       comparator_1_gt, comparator_2_eq, comparator_3_gt, comparator_3_lt, comparator_4_eq, CT_ALU__LD,
       CT_ALU__M, CT_ALU__M2, CT_ALU__WD, CT_ALU__WF, CT_BUS__DAG, CT_BUS__DAM, CT_BUS__DAR, CT_BUS__DDG,
       CT_BUS__DDM, CT_BUS__DDR, CT_BUS__IAG, CT_BUS__IAR, CT_BUS__IDM, CT_BUS__IDR, CT_DEP__EA, CT_DEP__EB,
       CT_DIR__LD, CT_DIR__M, CT_DIR__MS, CT_DISP, CT_FL__W1, CT_FL__W2, CT_FU__EPOCH, CT_haz, CT_ISS__OFL,
       CT_ISS__OLDB, CT_ISS__ORC, CT_ISS__OSC, CT_ISS__OSTB, CT_ISS__UFL, CT_ISS__URA, CT_ISS__URB,
       CT_ISS__USC, CT_LDB__LD, CT_MVR, CT_RF__DM, CT_RF__E, CT_RF__FLS, CT_RF__PCAE, CT_RF__PCH, CT_RF__PCJ,
       CT_RF__PCR, CT_RF__PCSE, CT_RF__SCAE, CT_RF__SCAS, CT_RF__SCD, CT_RF__SCSE, CT_RF__W1, CT_RF__W2,
       CT_ROB__EX__E, CT_ROB__FL__STA, CT_ROB__FL__STB, CT_ROB__GEN__STA, CT_ROB__GEN__STB, CT_ROB__ST__E,
       CT_rollback, CT_SC__D1, CT_SC__D2, CT_SC__W1, CT_SC__W2, CT_STB__LD, DC_B_q, dc_e, DC_q,
       dipswitch_1_out, dipswitch_2_out, dipswitch_4_out, dipswitch_5_out, DIR_busy, DIR_free, DIR_LD,
       DIR_RD, DIR_ST, dp_e, ecm_e__bf, epoch_DP, epoch_IS, ex_e, ex_e__bf, ex_nop, ft_e, FT_q,
       halt_FT_DC_ISS, hlt, id_full, id_gen2_1_v, int_run, ISS_B_q, issue, kernel_inst, LD_ep, LDB_busy,
       LDB_free, LDB_LD, LDB_ldV, LDB_M__EP, LDB_M__V, load_buffer_1_p2, load_buffer_1_p3, load_buffer_1_p23,
       load_buffer_1_p24, load_buffer_1_p25, load_buffer_1_p31, MEM_LD, MEM_RD, mode, multiplexer_7_out,
       multiplexer_8_out, multiplexer_9_out, multiplexer_12_out, multiplexer_13_out, multiplexer_14_out,
       multiplexer_15_out, multiplexer_16_out, multiplexer_24_out, multiplexer_26_out, multiplexer_27_out,
       multiplexer_34_out, multiplexer_35_out, multiplexer_36_out, multiplexer_40_out, multiplexer_41_out,
       multiplexer_46_out, multiplexer_47_out, multiplexer_53_out, multiplexer_54_out, multiplexer_58_out,
       multiplexer_64_out, multiplexer_72_out, multiplexer_73_out, nand_1_out, nor_1_out, nor_2_out,
       nor_5_out, not_1_out, not_3_out, not_7_out, not_8_out, not_9_out, not_10_out, not_11_out, not_12_out,
       not_16_out, not_17_out, not_18_out, not_19_out, or_12_out, or_13_out, or_14_out, or_15_out, or_18_out,
       or_19_out, or_20_out, or_21_out, or_22_out, or_23_out, or_24_out, or_25_out, or_26_out, or_27_out,
       or_29_out, or_30_out, or_31_out, or_33_out, or_34_out, or_35_out, or_36_out, or_37_out, or_38_out,
       or_40_out, or_41_out, or_42_out, or_43_out, or_44_out, or_45_out, or_46_out, pc_ov, register_12_q,
       register_15_q, register_16_q, register_17_q, register_18_q, register_19_q, register_20_q,
       register_27_q, register_28_q, register_29_q, register_30_q, register_31_q, register_32_q,
       register_33_q, register_34_q, register_35_q, register_36_q, register_47_q, register_52_q,
       register_53_q, register_54_q, register_60_q, register_67_q, register_71_q, register_78_q,
       register_83_q, register_108_q, rf_e, rs_ff_1_nq, rs_ff_2_nq, rs_ff_3_nq, rs_ff_4_nq, rs_ff_5_nq,
       rs_ff_11_q, rs_ff_12_q, rs_ff_13_q, rs_ff_14_q, rs_ff_15_nq, RS_full, sc_ov, st, st_e__bf, ST_ep,
       STB_busy, STB_free, STB_LD, STB_M__EP, STB_M__V, xor_2_out, xor_3_out, xor_4_out, xor_5_out,
       xor_6_out, xor_7_out, xor_8_out, xor_9_out, xor_10_out, xor_11_out;
  wire [0:0] and_44_out, and_56_out, and_57_out;
  wire [1:0] and_30_out, and_58_out, and_60_out, CT_ALU__M_old, d_ff_1_q, d_ff_2_q, LDB_M__MD,
       multiplexer_45_out, multiplexer_52_out, multiplexer_63_out, multiplexer_68_out, multiplexer_75_out,
       register_51_q, register_59_q, register_76_q, register_82_q, register_97_q, register_103_q,
       register_111_q, STB_M__MD;
  wire [1:1] d_ff_3_q, d_ff_4_q;
  wire [2:0] ALU_A_RM, ALU_B_RM, and_41_out, and_43_out, CT_BUS__DASDN, CT_DEP__UMA, CT_DEP__UMB,
       CT_ISS__UFU, CT_RF__MA, CT_RF__MB, CT_RF__SCN, CT_RF__WM, CT_SC__O1, CT_SC__O2, multiplexer_25_out,
       register_10_q, register_11_q, register_13_q, register_14_q, store_controller_1_d1_sel,
       store_controller_1_d2_sel, store_controller_2_d1_sel, store_controller_2_d2_sel;
  wire [2:1] and_42_out;
  wire [3:0] ALU_A_INST, ALU_B_INST, clr_id, com1_inst, com2_inst, CT_FU__INST, DIR_INST, inst_DP, inst_EX,
       inst_EXT, inst_IS, inst_ST, LD_id, LDB_M__ID, multiplexer_6_out, multiplexer_22_out,
       multiplexer_33_out, multiplexer_39_out, multiplexer_44_out, multiplexer_51_out, multiplexer_57_out,
       multiplexer_62_out, multiplexer_67_out, multiplexer_70_out, pulldown_13_out, register_26_q,
       register_42_q, register_46_q, register_50_q, register_58_q, register_70_q, register_75_q,
       register_81_q, register_109_q, ROB_FL_INSTA, ROB_FL_INSTB, ROB_GEN_INSTA, ROB_GEN_INSTB, ST_id,
       STB_M__ID;
  wire [3:3] register_11_q_2;
  wire [4:0] CT_DEP__URA, CT_DEP__URB, CT_ISS__RA, CT_ISS__RB, CT_ISS__RC, CT_RF__RA, CT_RF__RB, CT_RF__WS;
  wire [7:0] ALU_A_F, ALU_A_FI, ALU_A_T__F, ALU_B_F, ALU_B_FI, ALU_B_T__F, bitextender_2_out, byte_D0,
       byte_D0_iv, byte_D1, byte_D1_ex, byte_D1_st, byte_D2, byte_D2_ex, byte_D3, byte_D3_ex, byte_I0,
       byte_I0_iv, byte_I1, byte_I2, byte_I3, CT_FL__D1, CT_FL__D2, CT_FU__WR, CT_RF__R1, CT_RF__R2, DIR_WR,
       fl_i, FU_free, multiplexer_4_out, multiplexer_19_out, multiplexer_21_out, multiplexer_30_out,
       multiplexer_32_out, multiplexer_38_out, multiplexer_56_out, register_23_q, register_25_q,
       register_39_q, register_41_q, register_45_q, register_69_q, ROB_FL_A, ROB_FL_B, ROB_GEN_WA,
       ROB_GEN_WB, xor_1_out;
  wire [7:3] ALU_A_WR, ALU_B_WR;
  wire [8:0] ALU_A_CT, ALU_B_CT, CT_ALU__CT, multiplexer_20_out, multiplexer_31_out, register_24_q,
       register_40_q;
  wire [9:0] and_12_out;
  wire [15:0] bitextender_3_out, multiplexer_43_out, multiplexer_50_out, multiplexer_61_out,
       multiplexer_66_out, register_49_q, register_57_q, register_74_q, register_80_q, register_95_q,
       register_101_q, V_inst;
  wire [31:0] add_1_s, add_4c32_1_s, alu_32_1_p8, alu_32_1_p11, alu_32_1_p12, alu_32_1_p14, ALU_A_A, ALU_A_B,
       ALU_A_R, ALU_A_T__R, ALU_B_A, ALU_B_B, ALU_B_R, ALU_B_T__R, bitextender_1_out, CT_RF__D1, CT_RF__D2,
       D_A__R_q, DIR, FL, I_A__R_q, I_D__R_q, LD_addr, LDB_ldD, LDB_M__A, multiplexer_2_out,
       multiplexer_3_out, multiplexer_10_out, multiplexer_17_out, multiplexer_18_out, multiplexer_23_out,
       multiplexer_28_out, multiplexer_29_out, multiplexer_37_out, multiplexer_42_out, multiplexer_48_out,
       multiplexer_49_out, multiplexer_55_out, multiplexer_59_out, multiplexer_60_out, multiplexer_65_out,
       multiplexer_69_out, multiplexer_74_out, mVec, OD_D__R_q, pc_read, PCA, pca_i, PCS, PCS_DC, PCS_FT,
       pcs_i, PCS_IS, pulldown_12_out, R_A, R_B, ramdualaccess_1_d1, ramdualaccess_1_d2, register_4_q,
       register_5_q, register_21_q, register_22_q, register_37_q, register_38_q, register_44_q,
       register_48_q, register_55_q, register_56_q, register_68_q, register_72_q, register_73_q,
       register_79_q, register_94_q, register_100_q, register_110_q, register_112_q, ROB_GEN_DA, ROB_GEN_DB,
       SCA, sca_i, SCS, scs_i, ST_addr, ST_data, STB_M__A, STB_M__D, sub_4c32_1_s;
  wire [31:24] res_station_1_p31;

  Comparator #(.Bits(32)) comparator_1 (.a(PCS), .b(mVec), .gt(comparator_1_gt));  // open: eq, lt
  BitExtender #(.inputBits(16), .outputBits(32)) bitextender_1 (.in({byte_D2_ex, byte_D3_ex}), .out(bitextender_1_out));
  and and_1 (and_1_out, FL[14], INT_nor);
  and and_2 (and_2_out, 1'b0, ~comparator_1_gt);  // And
  Add #(.Bits(32)) add_1 (.a(R_A), .b(bitextender_1_out), .c_i(1'b0), .s(add_1_s));  // open: c_o
  or or_1 (int_run, and_1_out, INT_nmk);
  PullDown pulldown_1 (.out(CT_haz));
  RS_FF u_mode (.S(and_2_out), .C(C_dt), .R(comparator_1_gt), .Q(mode));  // open: nQ
  Register #(.Bits(32)) MVR (.D(add_1_s), .C(C_dt), .en(CT_MVR), .Q(mVec));
  and and_3 (and_3_out, CT_haz, dp_e);
  assign CT_RF__PCSE = ft_e ? 1'b1 : 1'bz;  // Driver driver_1
  assign CT_BUS__IAR = ft_e ? 1'b1 : 1'bz;  // Driver driver_2
  assign CT_BUS__IAG = ft_e ? 1'b1 : 1'bz;  // Driver driver_3
  assign I_LD = ft_e ? 1'b1 : 1'bz;  // Driver driver_4
  id_gen2 id_gen2_1 (
    .C(C_ct), .\use (issue), .V_inst(V_inst), .epoch(epoch_IS), .id(inst_IS), .V(id_gen2_1_v), .com1(com1),
    .com1_id(com1_inst), .com2(com2), .com2_id(com2_inst));
  RS_FF FT (.S(run), .C(C_ct), .R(hlt), .Q(FT_q));  // open: nQ
  not not_1 (not_1_out, and_3_out);
  assign ex_nop = and_3_out ? 1'b1 : 1'bz;  // Driver driver_5
  not not_2 (id_full, id_gen2_1_v);
  and and_4 (ft_e, FT_q, not_1_out);
  Register DC_B (.D(FT_q), .C(C_dt), .en(1'b1), .Q(DC_B_q));
  Register #(.Bits(32)) register_1 (.D(PCS), .C(C_dt), .en(CT_RF__PCSE), .Q(PCS_FT));
  Register DC (.D(FT_q), .C(C_ct), .en(1'b1), .Q(DC_q));
  not not_3 (not_3_out, I_valid);
  and and_5 (dc_e, DC_q, not_1_out);
  Register ISS_B (.D(DC_B_q), .C(C_dt), .en(1'b1), .Q(ISS_B_q));
  Register #(.Bits(32)) register_2 (.D(PCS_FT), .C(C_dt), .en(CT_RF__PCSE), .Q(PCS_DC));
  assign CT_BUS__IDM = not_3_out ? 1'b1 : 1'bz;  // Driver driver_6
  Register ISS (.D(DC_q), .C(C_ct), .en(1'b1), .Q(dp_e));
  Register #(.Bits(4)) EX (.D(inst_DP), .C(C_dt), .en(dp_e), .Q(inst_EX));
  Register EX_B (.D(ISS_B_q), .C(C_dt), .en(1'b1), .Q(ex_e__bf));
  Register #(.Bits(32)) register_3 (.D(PCS_DC), .C(C_dt), .en(CT_RF__PCSE), .Q(PCS_IS));
  Register #(.Bits(4)) u_ST (.D(inst_EX), .C(C_dt), .en(ex_e), .Q(inst_ST));
  DipSwitch dipswitch_1 (.out(dipswitch_1_out));
  Multiplexer multiplexer_1 (.sel(dipswitch_2_out), .in_0(dipswitch_1_out), .in_1(C), .out(C_dt));
  DipSwitch dipswitch_2 (.out(dipswitch_2_out));
  not not_4 (C_ct, C_dt);
  Register EX_2 (.D(dp_e), .C(C_ct), .en(1'b1), .Q(ex_e));
  PullDown pulldown_2 (.out(CT_DISP));
  PullDown pulldown_3 (.out(CT_rollback));
  PullDown pulldown_4 (.out(com2));
  PullDown #(.Bits(4)) pulldown_5 (.out(com2_inst));
  PullDown pulldown_6 (.out(com1_M));
  PullDown pulldown_7 (.out(com1));
  PullDown #(.Bits(4)) pulldown_8 (.out(com1_inst));
  Multiplexer #(.Bits(32)) multiplexer_2 (.sel(CT_RF__DM), .in_0(ALU_A_T__R), .in_1(D_D__bus), .out(multiplexer_2_out));
  and and_6 (and_6_out, rf_e, CT_RF__E);
  Register ST_B (.D(ex_e__bf), .C(C_dt), .en(1'b1), .Q(st_e__bf));
  Register #(.Bits(4)) EXT (.D(inst_ST), .C(C_dt), .en(rf_e), .Q(inst_EXT));
  // Probe on multiplexer_2_out
  // Probe on CT_RF__WS
  // Probe on CT_RF__WM
  // Probe on CT_RF__RA
  // Probe on CT_RF__MA
  // Probe on CT_RF__RB
  // Probe on CT_RF__MB
  Register #(.Bits(32)) register_4 (.D(ALU_A_T__R), .C(C_dt), .en(CT_RF__E), .Q(register_4_q));
  Register ST_2 (.D(ex_e), .C(C_ct), .en(1'b1), .Q(rf_e));
  Register #(.Bits(32)) register_5 (.D(multiplexer_2_out), .C(C_dt), .en(and_6_out), .Q(register_5_q));
  // Probe on and_6_out
  // Probe M on CT_RF__WM
  // Probe REG st on register_4_q
  // Probe INST on {byte_I0, byte_I1, byte_I2, byte_I3}
  Register CM_B___EXT_B (.D(st_e__bf), .C(C_dt), .en(1'b1), .Q(cm_e__bf));
  // Probe on register_5_q
  // Probe S on CT_RF__WS
  assign byte_I0_iv = ~byte_I0;  // Not not_5, 8 bits wide
  assign byte_D0_iv = ~byte_D0;  // Not not_6, 8 bits wide
  Register CM___EXT (.D(rf_e), .C(C_ct), .en(1'b1), .Q(cm_e));
  // Probe inst on {byte_I0, byte_I1, byte_I2, byte_I3}
  // Probe R_A on R_A
  // Probe R_B on R_B
  // Probe PC on PCS
  // Probe SC on SCS
  // Probe FL on FL
  // Probe CT_BUS-_IDM on CT_BUS__IDM
  // Probe C_i on C_dt
  Register EXT_CM_B (.D(cm_e__bf), .C(C_dt), .en(1'b1), .Q(ecm_e__bf));
  or or_2 (halt_FT_DC_ISS, RS_full, id_full);
  // Probe com1_inst on com1_inst
  // Probe com2_inst on com2_inst
  // Probe inst_ST on inst_ST
  // Probe PC_inst on inst_IS
  // Probe inst_EX on inst_EX
  Register #(.Bits(8)) register_6 (.D(byte_D1), .C(C_ct), .en(ex_e__bf), .Q(byte_D1_ex));
  Register #(.Bits(8)) register_7 (.D(byte_D2), .C(C_ct), .en(ex_e__bf), .Q(byte_D2_ex));
  Register #(.Bits(8)) register_8 (.D(byte_D3), .C(C_ct), .en(ex_e__bf), .Q(byte_D3_ex));
  RAMDualAccess #(.AddrBits(24), .isProgramMemory("true"), .Bits(32)) ramdualaccess_1 (
    .str(D_ST), .C(C_dt), .ld(1'b1), .A1(D_A__bus[25:2]), .Din1(D_D__bus), .A2(I_A__bus[25:2]),
    .D1(ramdualaccess_1_d1), .D2(ramdualaccess_1_d2));
  assign D_D__bus = D_LD ? ramdualaccess_1_d1 : 32'bz;  // Driver driver_7
  assign I_D__bus = I_LD ? ramdualaccess_1_d2 : 32'bz;  // Driver driver_8
  Register #(.Bits(8)) register_9 (.D(byte_D1_ex), .C(C_ct), .en(st_e__bf), .Q(byte_D1_st));
  DipSwitch dipswitch_3 (.out(CT_rollback));
  sub_4c32 sub_4c32_1 (.a(SCS), .b({1'b0, CT_BUS__DASDN}), .s(sub_4c32_1_s));
  Multiplexer #(.Bits(32)) multiplexer_3 (
    .sel(CT_BUS__DAM), .in_0(ALU_A_T__R), .in_1(sub_4c32_1_s), .out(multiplexer_3_out));
  and and_7 (and_7_out, byte_D0[3], byte_D0[0]);
  and and_8 (and_8_out, byte_D0[2], byte_D0[0]);
  and and_9 (and_9_out, byte_D0_iv[3], byte_D0_iv[2], byte_D0[1], byte_D0_iv[0]);
  and and_10 (and_10_out, byte_D0_iv[4], byte_D0[3], byte_D0[2], byte_D0[1]);
  and and_11 (and_11_out, byte_D0[4], byte_D0_iv[3], byte_D0_iv[2], byte_D0[1], byte_D0[0]);
  and and_12 (and_12_out[7], byte_D0_iv[4], byte_D0[3], byte_D0[2]);
  and and_13 (and_13_out, byte_D0[4], byte_D0[2], byte_D0_iv[1]);
  and and_14 (and_14_out, byte_D0[4], byte_D0_iv[3], byte_D0_iv[2]);
  and and_15 (and_15_out, byte_D0_iv[4], byte_D0_iv[3], byte_D0_iv[2]);
  and and_16 (and_16_out, byte_D0_iv[4], byte_D0_iv[3]);
  and and_17 (and_17_out, byte_D0_iv[4], byte_D0[3], byte_D0_iv[2], byte_D0_iv[1]);
  and and_18 (and_18_out, byte_D0_iv[4], byte_D0[3], byte_D0_iv[2]);
  and and_19 (and_19_out, byte_D0[4], byte_D0[3]);
  and and_20 (and_20_out, byte_D0_iv[4], byte_D0_iv[3], byte_D0[2], byte_D0_iv[1]);
  and and_21 (and_21_out, byte_D0[4], byte_D0[2], byte_D0[1]);
  and and_22 (and_22_out, byte_D0_iv[4], byte_D0_iv[3], byte_D0_iv[2], byte_D0[1], byte_D0[0]);
  and and_23 (and_23_out, byte_D0_iv[2], byte_D0_iv[0]);
  and and_24 (and_24_out, byte_D0[2], byte_D0[0]);
  and and_25 (and_25_out, byte_D0[1], byte_D0[2], byte_D0[4]);
  and and_26 (and_26_out, byte_D0[3], byte_D0[4]);
  and and_27 (and_27_out, ft_e, CT_BUS__IAR);
  Multiplexer #(.Bits(8)) multiplexer_4 (
    .sel(CT_BUS__IDM), .in_0(I_D__bus[31:24]), .in_1(8'h72), .out(multiplexer_4_out));
  and and_28 (and_28_out, ex_e, CT_BUS__DAR);
  and and_29 (and_29_out, ex_e, CT_BUS__DDR);
  or or_3 (and_30_out[1], CT_RF__PCH, CT_RF__PCR);
  and and_30 (and_30_out[0], ~CT_RF__PCH, CT_RF__PCJ);  // And
  nor nor_1 (nor_1_out, CT_RF__PCR, CT_RF__PCJ);
  or or_4 (and_12_out[9], and_7_out, and_8_out, and_9_out);
  or or_5 (and_12_out[6], and_13_out, and_10_out, and_11_out);
  or or_6 (and_12_out[5], and_12_out[7], and_13_out, and_14_out);
  or or_7 (and_12_out[4], and_20_out, and_21_out, and_15_out);
  or or_8 (and_12_out[3], and_16_out, and_21_out, and_17_out);
  or or_9 (and_12_out[2], and_18_out, and_19_out);
  or or_10 (and_12_out[1], and_20_out, and_21_out, and_22_out);
  or or_11 (and_12_out[0], byte_D0[3], byte_D0[1], and_23_out, and_24_out);
  nor nor_2 (nor_2_out, and_25_out, and_26_out);
  add_4c32 add_4c32_1 (.a(PCS), .b(4'b0100), .s(add_4c32_1_s), .c(add_4c32_1_c));
  Register #(.Bits(32)) I_A__R (.D(PCS), .C(C_dt), .en(and_27_out), .Q(I_A__R_q));
  Register #(.Bits(32)) I_D__R (.D({multiplexer_4_out, I_D__bus[23:0]}), .C(C_dt), .en(dc_e), .Q(I_D__R_q));
  Register #(.Bits(32)) D_A__R (.D(multiplexer_3_out), .C(C_dt), .en(and_28_out), .Q(D_A__R_q));
  Register #(.Bits(32)) OD_D__R (.D(R_B), .C(C_dt), .en(and_29_out), .Q(OD_D__R_q));
  Multiplexer #(.Selector_Bits(2), .Bits(32)) multiplexer_5 (
    .sel(and_30_out), .in_0(add_4c32_1_s), .in_1(ALU_A_T__R), .in_2(PCA), .in_3(D_D__bus), .out(pcs_i));
  and and_31 (pc_ov, add_4c32_1_c, nor_1_out);
  assign I_A__bus = and_34_out ? I_A__R_q : 32'bz;  // Driver driver_9
  D_FF #(.Bits(32)) INST_3 (.D(I_D__R_q), .C(C_ct), .Q({byte_I0, byte_I1, byte_I2, byte_I3}));  // open: nQ
  assign D_A__bus = and_35_out ? D_A__R_q : 32'bz;  // Driver driver_10
  assign D_D__bus = and_36_out ? OD_D__R_q : 32'bz;  // Driver driver_11
  and and_32 (and_32_out, byte_D0_iv[0], byte_D0_iv[1], byte_D0[2], byte_D0[3], byte_D0[4], byte_D0_iv[5], byte_D0_iv[6], byte_D0_iv[7]);
  and and_33 (and_33_out, byte_D0[1], byte_D0_iv[2], byte_D0[3], byte_D0[4], byte_D0_iv[5], byte_D0_iv[6], byte_D0_iv[7]);
  and and_34 (and_34_out, CT_BUS__IAG, bus_e);
  and and_35 (and_35_out, CT_BUS__DAG, bus_e);
  and and_36 (and_36_out, CT_BUS__DDG, bus_e);
  and and_37 (and_37_out, byte_D0[4], byte_D0[3], byte_D0_iv[1], byte_D0_iv[2], byte_D0_iv[5], byte_D0_iv[6], byte_D0_iv[7]);
  or or_12 (or_12_out, and_32_out, and_33_out);
  and and_38 (and_38_out, byte_D0_iv[7], byte_D0_iv[6], byte_D0_iv[5], byte_D0_iv[4]);
  and and_39 (and_39_out, byte_D0_iv[7], byte_D0_iv[6], byte_D0_iv[5], byte_D0[4], byte_D0_iv[3]);
  assign {CT_RF__RA, CT_RF__MA} = or_13_out ? byte_D1 : 8'bz;  // Driver driver_12
  assign {CT_RF__RB, CT_RF__MB} = or_13_out ? byte_D2 : 8'bz;  // Driver driver_13
  assign CT_ALU__LD = or_13_out ? 1'b1 : 1'bz;  // Driver driver_14
  assign CT_ALU__CT = or_13_out ? {1'b0, and_12_out[7:0]} : 9'bz;  // Driver driver_15
  assign CT_ALU__M = or_13_out ? and_12_out[9] : 1'bz;  // Driver driver_16
  assign CT_FU__INST = or_13_out ? inst_DP : 4'bz;  // Driver driver_17
  assign CT_FU__WR = or_13_out ? byte_D1 : 8'bz;  // Driver driver_18
  assign CT_ALU__WD = or_13_out ? nor_2_out : 1'bz;  // Driver driver_19
  assign CT_ALU__WF = or_13_out ? 1'b1 : 1'bz;  // Driver driver_20
  assign {CT_RF__RB, CT_RF__MB} = or_12_out ? byte_D2 : 8'bz;  // Driver driver_21
  assign CT_DIR__LD = or_12_out ? 1'b1 : 1'bz;  // Driver driver_22
  assign CT_DIR__M = or_12_out ? and_33_out : 1'bz;  // Driver driver_23
  assign CT_DIR__MS = or_12_out ? byte_D0[0] : 1'bz;  // Driver driver_24
  assign CT_FU__INST = or_12_out ? inst_DP : 4'bz;  // Driver driver_25
  assign CT_FU__WR = or_12_out ? byte_D1 : 8'bz;  // Driver driver_26
  or or_13 (or_13_out, and_38_out, and_37_out, and_39_out);
  Multiplexer #(.Bits(4)) multiplexer_6 (.sel(com2), .in_0(com1_inst), .in_1(com2_inst), .out(multiplexer_6_out));
  BitExtender #(.inputBits(1), .outputBits(8)) bitextender_2 (.in(register_11_q_2[3]), .out(bitextender_2_out));
  ROB_gen rob_gen_1 (
    .D1_O(CT_RF__D1), .R1_O(CT_RF__R1), .W1_O(CT_RF__W1), .D2_O(CT_RF__D2), .R2_O(CT_RF__R2),
    .W2_O(CT_RF__W2), .C(C_dt), .E1(CT_ROB__GEN__STA), .E2(CT_ROB__GEN__STB), .D1(ROB_GEN_DA),
    .D2(ROB_GEN_DB), .R1(ROB_GEN_WA), .R2(ROB_GEN_WB), .inst1(ROB_GEN_INSTA), .inst2(ROB_GEN_INSTB),
    .com1(com1), .com2(com2), .com1_id(com1_inst), .com2_id(com2_inst));
  ROB_PC rob_pc_1 (
    .C(C_dt), .E(issue), .D(PCS_DC), .inst(inst_IS), .com_id(multiplexer_6_out), .read_id(inst_DP),
    .D1(pca_i), .D2(pc_read));
  ROB_SC rob_sc_1 (
    .C(C_dt), .E(CT_RF__SCSE), .dec(CT_RF__SCD), .off(CT_RF__SCN), .inst(inst_DP), .com1(com1), .com2(com2),
    .com1_id(com1_inst), .com2_id(com2_inst), .W1(CT_SC__W1), .dec1(CT_SC__D1), .off1(CT_SC__O1),
    .W2(CT_SC__W2), .dec2(CT_SC__D2), .off2(CT_SC__O2));
  ROB_FL rob_fl_1 (
    .C(C_dt), .E1(CT_ROB__FL__STA), .E2(CT_ROB__FL__STB), .D1(ALU_A_T__F), .D2(ALU_B_T__F),
    .inst1(ROB_FL_INSTA), .inst2(ROB_FL_INSTB), .com1(com1), .com2(com2), .com1_id(com1_inst),
    .com2_id(com2_inst), .W1_O(CT_FL__W1), .D1_O(CT_FL__D1), .W2_O(CT_FL__W2), .D2_O(CT_FL__D2));
  assign xor_1_out = FL[7:0] ^ bitextender_2_out;  // XOr xor_1, 8 bits wide
  not not_7 (not_7_out, byte_D1_ex[1]);
  or or_14 (or_14_out, byte_D1_ex[2], byte_D1_ex[0]);
  and and_40 (and_41_out[2], byte_D0_iv[7], byte_D0_iv[6], byte_D0[5]);
  and and_41 (and_41_out[1], byte_D0_iv[7], byte_D0[6], byte_D0_iv[5]);
  or or_15 (or_15_out, byte_D1_ex[0], byte_D1_ex[2]);
  Multiplexer #(.Selector_Bits(3)) multiplexer_7 (
    .sel(register_11_q), .in_0(xor_1_out[0]), .in_1(xor_1_out[1]), .in_2(xor_1_out[2]), .in_3(xor_1_out[3]),
    .in_4(xor_1_out[4]), .in_5(xor_1_out[5]), .in_6(xor_1_out[6]), .in_7(xor_1_out[7]),
    .out(multiplexer_7_out));
  and and_42 (and_42_out[1], not_7_out, or_14_out);
  nor nor_3 (and_42_out[2], byte_D1_ex[2], byte_D1_ex[1], byte_D1_ex[0]);
  not not_8 (not_8_out, byte_D1_ex[1]);
  not not_9 (not_9_out, byte_D0[0]);
  and and_43 (and_43_out[0], byte_D0[1], byte_D0[2], byte_D0[3], byte_D0[4], byte_D0_iv[5], byte_D0_iv[6], byte_D0_iv[7]);
  Register #(.Bits(3)) register_10 (.D({and_42_out, byte_D1_ex[1]}), .C(C_ct), .en(st_e__bf), .Q(register_10_q));
  or or_16 (and_41_out[0], and_41_out[2], and_41_out[1]);
  and and_44 (and_44_out[0], or_15_out, not_8_out);
  and and_45 (and_45_out, byte_D0_iv[4], byte_D0[5], byte_D0[6], byte_D0_iv[7]);
  Comparator #(.Bits(3)) comparator_2 (.a(byte_D0[2:0]), .b(3'b110), .eq(comparator_2_eq));  // open: gt, lt
  Register #(.Bits(4)) register_11 (.D(byte_D0[3:0]), .C(C_ct), .en(ex_e__bf), .Q({register_11_q_2[3], register_11_q}));
  Register register_12 (.D(xor_2_out), .C(C_ct), .en(st_e__bf), .Q(register_12_q));
  and and_46 (and_43_out[1], and_43_out[0], byte_D0[0]);
  and and_47 (and_43_out[2], not_9_out, and_43_out[0]);
  Multiplexer multiplexer_8 (.sel(ex_nop), .in_0(and_45_out), .in_1(1'b0), .out(multiplexer_8_out));
  assign st = register_12_q ? 1'b1 : 1'bz;  // Driver driver_27
  not not_10 (not_10_out, comparator_2_eq);
  xor xor_2 (xor_2_out, multiplexer_9_out, register_15_q);
  and and_48 (and_48_out, com1, CT_RF__W1);
  and and_49 (and_49_out, com2, CT_RF__W2);
  assign CT_BUS__DAM = and_43_out[0] ? 1'b1 : 1'bz;  // Driver driver_28
  assign CT_BUS__DAR = and_43_out[0] ? 1'b1 : 1'bz;  // Driver driver_29
  assign {CT_RF__RB, CT_RF__MB} = and_43_out[1] ? byte_D1_ex : 8'bz;  // Driver driver_30
  assign CT_BUS__DDR = and_43_out[1] ? 1'b1 : 1'bz;  // Driver driver_31
  Driver driver_32 (.in(1'b1), .en(and_43_out[2]));  // open: out
  assign CT_BUS__DASDN = and_43_out[2] ? {and_42_out, byte_D1_ex[1]} : 3'bz;  // Driver driver_33
  Register #(.Bits(3)) register_13 (.D(and_43_out), .C(C_ct), .en(st_e__bf), .Q(register_13_q));
  assign CT_BUS__DAG = register_13_q[0] ? 1'b1 : 1'bz;  // Driver driver_34
  assign CT_RF__SCSE = register_13_q[0] ? 1'b1 : 1'bz;  // Driver driver_35
  assign CT_RF__SCAS = register_13_q[0] ? 1'b1 : 1'bz;  // Driver driver_36
  assign D_ST = register_13_q[1] ? 1'b1 : 1'bz;  // Driver driver_37
  assign CT_RF__SCN = register_13_q[1] ? register_10_q : 3'bz;  // Driver driver_38
  assign CT_BUS__DDG = register_13_q[1] ? 1'b1 : 1'bz;  // Driver driver_39
  assign D_LD = register_13_q[2] ? 1'b1 : 1'bz;  // Driver driver_40
  assign CT_RF__SCD = register_13_q[2] ? 1'b1 : 1'bz;  // Driver driver_41
  assign CT_RF__SCN = register_13_q[2] ? register_10_q : 3'bz;  // Driver driver_42
  assign CT_RF__DM = register_13_q[2] ? 1'b1 : 1'bz;  // Driver driver_43
  assign {CT_RF__WS, CT_RF__WM} = register_13_q[2] ? byte_D1_st : 8'bz;  // Driver driver_44
  assign CT_RF__E = register_13_q[2] ? 1'b1 : 1'bz;  // Driver driver_45
  assign st = register_13_q[0] ? 1'b1 : 1'bz;  // Driver driver_46
  assign D_MD = and_41_out[0] ? {byte_D1_ex[1], and_44_out[0]} : 2'bz;  // Driver driver_47
  assign {CT_RF__RA, CT_RF__MA} = and_41_out[0] ? {byte_D0[4:0], 3'b000} : 8'bz;  // Driver driver_48
  assign CT_ALU__CT = and_41_out[0] ? 9'h19 : 9'bz;  // Driver driver_49
  assign CT_ALU__M_old = and_41_out[0] ? 2'b11 : 2'bz;  // Driver driver_50
  assign CT_BUS__DAR = and_41_out[0] ? 1'b1 : 1'bz;  // Driver driver_51
  assign {CT_RF__RB, CT_RF__MB} = and_41_out[1] ? byte_D1_ex : 8'bz;  // Driver driver_52
  assign CT_BUS__DDR = and_41_out[1] ? 1'b1 : 1'bz;  // Driver driver_53
  Driver driver_54 (.in(1'b1), .en(and_41_out[2]));  // open: out
  Register #(.Bits(3)) register_14 (.D(and_41_out), .C(C_ct), .en(st_e__bf), .Q(register_14_q));
  assign CT_BUS__DAG = register_14_q[0] ? 1'b1 : 1'bz;  // Driver driver_55
  assign D_ST = register_14_q[1] ? 1'b1 : 1'bz;  // Driver driver_56
  assign CT_BUS__DDG = register_14_q[1] ? 1'b1 : 1'bz;  // Driver driver_57
  assign D_LD = register_14_q[2] ? 1'b1 : 1'bz;  // Driver driver_58
  assign CT_RF__DM = register_14_q[2] ? 1'b1 : 1'bz;  // Driver driver_59
  assign {CT_RF__WS, CT_RF__WM} = register_14_q[2] ? byte_D1_st : 8'bz;  // Driver driver_60
  assign CT_RF__E = register_14_q[2] ? 1'b1 : 1'bz;  // Driver driver_61
  assign st = register_14_q[0] ? 1'b1 : 1'bz;  // Driver driver_62
  assign CT_DEP__EA = and_45_out ? 1'b1 : 1'bz;  // Driver driver_63
  assign {CT_DEP__URA, CT_DEP__UMA} = and_45_out ? byte_D1 : 8'bz;  // Driver driver_64
  assign CT_DEP__EB = and_45_out ? not_10_out : 1'bz;  // Driver driver_65
  assign {CT_DEP__URB, CT_DEP__UMB} = and_45_out ? 8'hf8 : 8'bz;  // Driver driver_66
  Register register_15 (.D(multiplexer_8_out), .C(C_ct), .en(ex_e__bf), .Q(register_15_q));
  assign ex_nop = multiplexer_9_out ? 1'b1 : 1'bz;  // Driver driver_67
  assign CT_BUS__IDM = multiplexer_9_out ? 1'b1 : 1'bz;  // Driver driver_68
  assign CT_ALU__CT = multiplexer_9_out ? 9'h19 : 9'bz;  // Driver driver_69
  assign CT_ALU__M_old = multiplexer_9_out ? 2'b11 : 2'bz;  // Driver driver_70
  assign {CT_RF__RA, CT_RF__MA} = multiplexer_9_out ? byte_D1_ex : 8'bz;  // Driver driver_71
  Register register_16 (.D(multiplexer_9_out), .C(C_ct), .en(st_e__bf), .Q(register_16_q));
  assign CT_RF__PCSE = register_16_q ? 1'b1 : 1'bz;  // Driver driver_72
  assign CT_RF__PCJ = register_16_q ? 1'b1 : 1'bz;  // Driver driver_73
  assign CT_BUS__IDM = register_16_q ? 1'b1 : 1'bz;  // Driver driver_74
  assign st = register_16_q ? 1'b1 : 1'bz;  // Driver driver_75
  Register register_17 (.D(register_16_q), .C(C_ct), .en(cm_e__bf), .Q(register_17_q));
  assign CT_BUS__IDM = register_17_q ? 1'b1 : 1'bz;  // Driver driver_76
  PullDown #(.Bits(16)) pulldown_9 (.out(V_inst));
  Multiplexer multiplexer_9 (.sel(multiplexer_7_out), .in_0(1'b0), .in_1(register_15_q), .out(multiplexer_9_out));
  regFile4 regfile4_1 (
    .C(C_dt), .E1(and_48_out), .E2(and_49_out), .D1(CT_RF__D1), .D2(CT_RF__D2), .RW1(CT_RF__R1[7:3]),
    .MW1(CT_RF__R1[2:0]), .RW2(CT_RF__R2[7:3]), .MW2(CT_RF__R2[2:0]), .RA(CT_RF__RA), .MA(CT_RF__MA),
    .RB(CT_RF__RB), .MB(CT_RF__MB), .PCS_i(pcs_i), .PCS_e(CT_RF__PCSE), .PCA_i(pca_i), .PCA_e(CT_RF__PCAE),
    .SCS_i(scs_i), .SCS_e(CT_RF__SCSE), .SCA_i(sca_i), .SCA_sel(CT_RF__SCAS), .SCA_e(CT_RF__SCAE),
    .FL_i({{24{1'b0}}, fl_i}), .FL_sel(CT_RF__FLS), .FL_e(4'b0001), .PC_read(pc_read), .R_A(R_A), .R_B(R_B),
    .PCS_O(PCS), .PCA_O(PCA), .SCS_O(SCS), .SCA_O(SCA), .FL_O(FL));
  PullDown pulldown_10 (.out(CT_RF__PCAE));
  PullDown pulldown_11 (.out(CT_RF__SCAE));
  and and_50 (and_50_out, com1, CT_SC__W1);
  and and_51 (and_51_out, com2, CT_SC__W2);
  and and_52 (and_52_out, byte_I0[0], byte_I0_iv[1], byte_I0_iv[2], byte_I0_iv[3], byte_I0[4], byte_I0[5], byte_I0[6], byte_I0_iv[7]);
  Multiplexer #(.Bits(32)) multiplexer_10 (
    .sel(CT_ALU__M), .in_0(R_B), .in_1({{16{1'b0}}, byte_D2_ex, byte_D3_ex}), .out(multiplexer_10_out));
  and and_53 (and_53_out, byte_D2_ex[7], CT_DIR__MS);
  BitExtender #(.inputBits(1)) bitextender_3 (.in(and_53_out), .out(bitextender_3_out));
  and and_54 (and_54_out, byte_I0_iv[0], byte_I0_iv[1], byte_I0_iv[2], byte_I0_iv[3], byte_I0[4], byte_I0[5], byte_I0[6], byte_I0_iv[7]);
  and and_55 (and_55_out, byte_I0[0], byte_I0[1], byte_I0_iv[2], byte_I0_iv[3], byte_I0[4], byte_I0[5], byte_I0[6], byte_I0_iv[7]);
  Multiplexer multiplexer_11 (.sel(ex_nop), .in_0(and_55_out), .in_1(1'b0));  // open: out
  or or_17 (CT_RF__SCAE, and_50_out, and_51_out);
  Register register_18 (.D(CT_ALU__LD), .C(C_ct), .en(multiplexer_12_out), .Q(register_18_q));
  Multiplexer multiplexer_12 (.sel(ALU_free), .in_0(xor_3_out), .in_1(register_18_q), .out(multiplexer_12_out));
  Register register_19 (.D(CT_ALU__WD), .C(C_ct), .en(multiplexer_12_out), .Q(register_19_q));
  Register register_20 (.D(CT_ALU__WF), .C(C_ct), .en(multiplexer_12_out), .Q(register_20_q));
  Register #(.Bits(32)) register_21 (.D(R_A), .C(C_dt), .en(multiplexer_12_out), .Q(register_21_q));
  Register #(.Bits(32)) register_22 (.D(multiplexer_10_out), .C(C_dt), .en(multiplexer_12_out), .Q(register_22_q));
  Register #(.Bits(8)) register_23 (.D(FL[7:0]), .C(C_dt), .en(multiplexer_12_out), .Q(register_23_q));
  Register #(.Bits(9)) register_24 (.D(CT_ALU__CT), .C(C_ct), .en(multiplexer_12_out), .Q(register_24_q));
  Register #(.Bits(8)) register_25 (.D(CT_FU__WR), .C(C_ct), .en(multiplexer_12_out), .Q(register_25_q));
  Register #(.Bits(4)) register_26 (.D(CT_FU__INST), .C(C_ct), .en(multiplexer_12_out), .Q(register_26_q));
  or or_18 (or_18_out, CT_FU__WR[0], CT_FU__WR[2]);
  not not_11 (not_11_out, CT_FU__WR[1]);
  Multiplexer multiplexer_13 (.sel(ex_nop), .in_0(and_54_out), .in_1(1'b0), .out(multiplexer_13_out));
  Multiplexer multiplexer_14 (.sel(ex_nop), .in_0(and_52_out), .in_1(1'b0), .out(multiplexer_14_out));
  xor xor_3 (xor_3_out, ALU_busy, register_18_q);
  Multiplexer multiplexer_15 (.sel(register_18_q), .in_0(CT_ALU__WD), .in_1(register_19_q), .out(multiplexer_15_out));
  Multiplexer multiplexer_16 (.sel(register_18_q), .in_0(CT_ALU__WF), .in_1(register_20_q), .out(multiplexer_16_out));
  Multiplexer #(.Bits(32)) multiplexer_17 (
    .sel(register_18_q), .in_0(R_A), .in_1(register_21_q), .out(multiplexer_17_out));
  Multiplexer #(.Bits(32)) multiplexer_18 (
    .sel(register_18_q), .in_0(multiplexer_10_out), .in_1(register_22_q), .out(multiplexer_18_out));
  Multiplexer #(.Bits(8)) multiplexer_19 (
    .sel(register_18_q), .in_0(FL[7:0]), .in_1(register_23_q), .out(multiplexer_19_out));
  Multiplexer #(.Bits(9)) multiplexer_20 (
    .sel(register_18_q), .in_0(CT_ALU__CT), .in_1(register_24_q), .out(multiplexer_20_out));
  Multiplexer #(.Bits(8)) multiplexer_21 (
    .sel(register_18_q), .in_0(CT_FU__WR), .in_1(register_25_q), .out(multiplexer_21_out));
  Multiplexer #(.Bits(4)) multiplexer_22 (
    .sel(register_18_q), .in_0(CT_FU__INST), .in_1(register_26_q), .out(multiplexer_22_out));
  Multiplexer #(.Bits(32)) multiplexer_23 (
    .sel(CT_DIR__M), .in_0(R_A), .in_1({bitextender_3_out, byte_D2_ex, byte_D3_ex}), .out(multiplexer_23_out));
  or or_19 (or_19_out, CT_FU__WR[0], CT_FU__WR[2]);
  not not_12 (not_12_out, CT_FU__WR[1]);
  and and_56 (and_56_out[0], or_18_out, not_11_out);
  assign CT_DEP__EA = and_54_out ? 1'b1 : 1'bz;  // Driver driver_77
  assign {CT_DEP__URA, CT_DEP__UMA} = and_54_out ? byte_I1 : 8'bz;  // Driver driver_78
  Register register_27 (.D(multiplexer_13_out), .C(C_ct), .en(ex_e__bf), .Q(register_27_q));
  assign ex_nop = register_27_q ? 1'b1 : 1'bz;  // Driver driver_79
  assign CT_BUS__IDM = register_27_q ? 1'b1 : 1'bz;  // Driver driver_80
  assign {CT_RF__RA, CT_RF__MA} = register_27_q ? byte_D1_ex : 8'bz;  // Driver driver_81
  assign CT_ALU__CT = register_27_q ? 9'h19 : 9'bz;  // Driver driver_82
  assign CT_ALU__M_old = register_27_q ? 2'b11 : 2'bz;  // Driver driver_83
  assign {CT_RF__RB, CT_RF__MB} = register_27_q ? 8'he8 : 8'bz;  // Driver driver_84
  assign CT_BUS__DAM = register_27_q ? 1'b1 : 1'bz;  // Driver driver_85
  assign CT_BUS__DAR = register_27_q ? 1'b1 : 1'bz;  // Driver driver_86
  assign CT_BUS__DDR = register_27_q ? 1'b1 : 1'bz;  // Driver driver_87
  Register register_28 (.D(register_27_q), .C(C_ct), .en(st_e__bf), .Q(register_28_q));
  assign CT_BUS__IDM = register_28_q ? 1'b1 : 1'bz;  // Driver driver_88
  assign CT_RF__SCSE = register_28_q ? 1'b1 : 1'bz;  // Driver driver_89
  assign CT_RF__SCAS = register_28_q ? 1'b1 : 1'bz;  // Driver driver_90
  assign CT_RF__SCN = register_28_q ? 3'b100 : 3'bz;  // Driver driver_91
  assign CT_RF__PCSE = register_28_q ? 1'b1 : 1'bz;  // Driver driver_92
  assign CT_RF__PCJ = register_28_q ? 1'b1 : 1'bz;  // Driver driver_93
  assign CT_BUS__DAG = register_28_q ? 1'b1 : 1'bz;  // Driver driver_94
  assign CT_BUS__DDG = register_28_q ? 1'b1 : 1'bz;  // Driver driver_95
  assign D_ST = register_28_q ? 1'b1 : 1'bz;  // Driver driver_96
  assign st = register_28_q ? 1'b1 : 1'bz;  // Driver driver_97
  Register register_29 (.D(register_28_q), .C(C_ct), .en(cm_e__bf), .Q(register_29_q));
  assign CT_BUS__IDM = register_29_q ? 1'b1 : 1'bz;  // Driver driver_98
  Register register_30 (.D(multiplexer_14_out), .C(C_ct), .en(ex_e__bf), .Q(register_30_q));
  assign ex_nop = register_30_q ? 1'b1 : 1'bz;  // Driver driver_99
  assign CT_BUS__IDM = register_30_q ? 1'b1 : 1'bz;  // Driver driver_100
  assign CT_BUS__DAM = register_30_q ? 1'b1 : 1'bz;  // Driver driver_101
  assign CT_BUS__DAR = register_30_q ? 1'b1 : 1'bz;  // Driver driver_102
  assign CT_BUS__DASDN = register_30_q ? 3'b100 : 3'bz;  // Driver driver_103
  Register register_31 (.D(register_30_q), .C(C_ct), .en(st_e__bf), .Q(register_31_q));
  assign CT_BUS__IDM = register_31_q ? 1'b1 : 1'bz;  // Driver driver_104
  assign D_LD = register_31_q ? 1'b1 : 1'bz;  // Driver driver_105
  assign CT_RF__SCSE = register_31_q ? 1'b1 : 1'bz;  // Driver driver_106
  assign CT_RF__SCD = register_31_q ? 1'b1 : 1'bz;  // Driver driver_107
  assign CT_RF__SCN = register_31_q ? 3'b100 : 3'bz;  // Driver driver_108
  assign CT_RF__SCAS = register_31_q ? 1'b1 : 1'bz;  // Driver driver_109
  assign CT_RF__PCSE = register_31_q ? 1'b1 : 1'bz;  // Driver driver_110
  assign CT_RF__PCJ = register_31_q ? 1'b1 : 1'bz;  // Driver driver_111
  assign CT_RF__PCR = register_31_q ? 1'b1 : 1'bz;  // Driver driver_112
  assign CT_BUS__DAG = register_31_q ? 1'b1 : 1'bz;  // Driver driver_113
  assign st = register_31_q ? 1'b1 : 1'bz;  // Driver driver_114
  Register register_32 (.D(register_31_q), .C(C_ct), .en(cm_e__bf), .Q(register_32_q));
  assign CT_BUS__IDM = register_32_q ? 1'b1 : 1'bz;  // Driver driver_115
  Register register_33 (.D(1'b0), .C(C_ct), .en(ex_e__bf), .Q(register_33_q));
  assign ex_nop = register_33_q ? 1'b1 : 1'bz;  // Driver driver_116
  assign hlt = register_33_q ? 1'b1 : 1'bz;  // Driver driver_117
  assign CT_BUS__IDM = register_33_q ? 1'b1 : 1'bz;  // Driver driver_118
  assign CT_BUS__IDM = register_33_q ? 1'b1 : 1'bz;  // Driver driver_119
  Register register_34 (.D(register_33_q), .C(C_ct), .en(st_e__bf), .Q(register_34_q));
  assign CT_RF__PCH = register_34_q ? 1'b1 : 1'bz;  // Driver driver_120
  assign CT_RF__PCSE = register_34_q ? 1'b1 : 1'bz;  // Driver driver_121
  assign CT_BUS__IDM = register_34_q ? 1'b1 : 1'bz;  // Driver driver_122
  assign st = register_34_q ? 1'b1 : 1'bz;  // Driver driver_123
  or or_20 (or_20_out, CT_ALU__LD, register_18_q);
  Multiplexer multiplexer_24 (.sel(ALU_free), .in_0(xor_4_out), .in_1(ALU_busy), .out(multiplexer_24_out));
  Register register_35 (.D(multiplexer_15_out), .C(C_ct), .en(multiplexer_24_out), .Q(register_35_q));
  Register register_36 (.D(multiplexer_16_out), .C(C_ct), .en(multiplexer_24_out), .Q(register_36_q));
  Register #(.Bits(32)) register_37 (.D(multiplexer_17_out), .C(C_dt), .en(multiplexer_24_out), .Q(register_37_q));
  Register #(.Bits(32)) register_38 (.D(multiplexer_18_out), .C(C_dt), .en(multiplexer_24_out), .Q(register_38_q));
  Register #(.Bits(8)) register_39 (.D(multiplexer_19_out), .C(C_dt), .en(multiplexer_24_out), .Q(register_39_q));
  Register #(.Bits(9)) register_40 (.D(multiplexer_20_out), .C(C_ct), .en(multiplexer_24_out), .Q(register_40_q));
  Register #(.Bits(8)) register_41 (.D(multiplexer_21_out), .C(C_ct), .en(multiplexer_24_out), .Q(register_41_q));
  Register #(.Bits(4)) register_42 (.D(multiplexer_22_out), .C(C_ct), .en(multiplexer_24_out), .Q(register_42_q));
  and and_57 (and_57_out[0], or_19_out, not_12_out);
  Multiplexer #(.Bits(3)) multiplexer_25 (
    .sel(and_51_out), .in_0(CT_SC__O1), .in_1(CT_SC__O2), .out(multiplexer_25_out));
  Register register_43 (.D(or_20_out), .C(C_ct), .en(multiplexer_24_out), .Q(ALU_busy));
  Multiplexer multiplexer_26 (.sel(ALU_busy), .in_0(CT_ALU__WD), .in_1(register_35_q), .out(multiplexer_26_out));
  Multiplexer multiplexer_27 (.sel(ALU_busy), .in_0(CT_ALU__WF), .in_1(register_36_q), .out(multiplexer_27_out));
  Multiplexer #(.Bits(32)) multiplexer_28 (.sel(ALU_busy), .in_0(R_A), .in_1(register_37_q), .out(multiplexer_28_out));
  Multiplexer #(.Bits(32)) multiplexer_29 (
    .sel(ALU_busy), .in_0(multiplexer_10_out), .in_1(register_38_q), .out(multiplexer_29_out));
  Multiplexer #(.Bits(8)) multiplexer_30 (
    .sel(ALU_busy), .in_0(FL[7:0]), .in_1(register_39_q), .out(multiplexer_30_out));
  Multiplexer #(.Bits(9)) multiplexer_31 (
    .sel(ALU_busy), .in_0(CT_ALU__CT), .in_1(register_40_q), .out(multiplexer_31_out));
  Multiplexer #(.Bits(8)) multiplexer_32 (
    .sel(ALU_busy), .in_0(CT_FU__WR), .in_1(register_41_q), .out(multiplexer_32_out));
  Multiplexer #(.Bits(4)) multiplexer_33 (
    .sel(ALU_busy), .in_0(CT_FU__INST), .in_1(register_42_q), .out(multiplexer_33_out));
  Multiplexer multiplexer_34 (.sel(DIR_free), .in_0(xor_5_out), .in_1(register_52_q), .out(multiplexer_34_out));
  Register #(.Bits(32)) register_44 (.D(multiplexer_23_out), .C(C_dt), .en(multiplexer_34_out), .Q(register_44_q));
  Register #(.Bits(8)) register_45 (.D(CT_FU__WR), .C(C_ct), .en(multiplexer_34_out), .Q(register_45_q));
  Register #(.Bits(4)) register_46 (.D(CT_FU__INST), .C(C_ct), .en(multiplexer_34_out), .Q(register_46_q));
  Multiplexer multiplexer_35 (.sel(LDB_free), .in_0(xor_6_out), .in_1(register_60_q), .out(multiplexer_35_out));
  Register register_47 (.D(CT_FU__EPOCH), .C(C_ct), .en(multiplexer_35_out), .Q(register_47_q));
  Register #(.Bits(32)) register_48 (.D(R_B), .C(C_dt), .en(multiplexer_35_out), .Q(register_48_q));
  Register #(.Bits(16)) register_49 (
    .D({byte_D2_ex, byte_D3_ex}), .C(C_dt), .en(multiplexer_35_out), .Q(register_49_q));
  Register #(.Bits(4)) register_50 (.D(CT_FU__INST), .C(C_ct), .en(multiplexer_35_out), .Q(register_50_q));
  Register #(.Bits(2)) register_51 (
    .D({CT_FU__WR[1], and_56_out[0]}), .C(C_ct), .en(multiplexer_35_out), .Q(register_51_q));
  Multiplexer multiplexer_36 (.sel(and_51_out), .in_0(CT_SC__D1), .in_1(CT_SC__D2), .out(multiplexer_36_out));
  or or_21 (or_21_out, CT_ALU__LD, ALU_busy);
  xor xor_4 (xor_4_out, ALU_busy, ALU_busy);
  Register register_52 (.D(CT_DIR__LD), .C(C_ct), .en(multiplexer_34_out), .Q(register_52_q));
  xor xor_5 (xor_5_out, register_67_q, register_52_q);
  Multiplexer #(.Bits(32)) multiplexer_37 (
    .sel(register_52_q), .in_0(multiplexer_23_out), .in_1(register_44_q), .out(multiplexer_37_out));
  Multiplexer #(.Bits(8)) multiplexer_38 (
    .sel(register_52_q), .in_0(CT_FU__WR), .in_1(register_45_q), .out(multiplexer_38_out));
  Multiplexer #(.Bits(4)) multiplexer_39 (
    .sel(register_52_q), .in_0(CT_FU__INST), .in_1(register_46_q), .out(multiplexer_39_out));
  Register register_53 (.D(CT_STB__LD), .C(C_ct), .en(multiplexer_40_out), .Q(register_53_q));
  Multiplexer multiplexer_40 (.sel(STB_free), .in_0(xor_7_out), .in_1(register_53_q), .out(multiplexer_40_out));
  Register register_54 (.D(CT_FU__EPOCH), .C(C_ct), .en(multiplexer_40_out), .Q(register_54_q));
  Register #(.Bits(32)) register_55 (.D(R_A), .C(C_dt), .en(multiplexer_40_out), .Q(register_55_q));
  Register #(.Bits(32)) register_56 (.D(R_B), .C(C_dt), .en(multiplexer_40_out), .Q(register_56_q));
  Register #(.Bits(16)) register_57 (
    .D({byte_D2_ex, byte_D3_ex}), .C(C_dt), .en(multiplexer_40_out), .Q(register_57_q));
  Register #(.Bits(4)) register_58 (.D(CT_FU__INST), .C(C_ct), .en(multiplexer_40_out), .Q(register_58_q));
  Register #(.Bits(2)) register_59 (
    .D({CT_FU__WR[1], and_57_out[0]}), .C(C_ct), .en(multiplexer_40_out), .Q(register_59_q));
  Register register_60 (.D(CT_LDB__LD), .C(C_ct), .en(multiplexer_35_out), .Q(register_60_q));
  xor xor_6 (xor_6_out, LDB_busy, register_60_q);
  Multiplexer multiplexer_41 (.sel(register_60_q), .in_0(CT_FU__EPOCH), .in_1(register_47_q), .out(multiplexer_41_out));
  Multiplexer #(.Bits(32)) multiplexer_42 (
    .sel(register_60_q), .in_0(R_B), .in_1(register_48_q), .out(multiplexer_42_out));
  Multiplexer #(.Bits(16)) multiplexer_43 (
    .sel(register_60_q), .in_0({byte_D2_ex, byte_D3_ex}), .in_1(register_49_q), .out(multiplexer_43_out));
  Multiplexer #(.Bits(4)) multiplexer_44 (
    .sel(register_60_q), .in_0(CT_FU__INST), .in_1(register_50_q), .out(multiplexer_44_out));
  Multiplexer #(.Bits(2)) multiplexer_45 (
    .sel(register_60_q), .in_0({CT_FU__WR[1], and_56_out[0]}), .in_1(register_51_q), .out(multiplexer_45_out));
  addsub_4c32 addsub_4c32_1 (.a(SCS), .b({1'b0, CT_RF__SCN}), .sub(CT_RF__SCD), .s(scs_i), .c(sc_ov));
  addsub_4c32 addsub_4c32_2 (.a(SCA), .b({1'b0, multiplexer_25_out}), .sub(multiplexer_36_out), .s(sca_i), .c(sc_ov));
  Register #(.Bits(32)) register_61 (.D(multiplexer_28_out), .C(C_dt), .en(ALU_A_LD), .Q(ALU_A_A));
  Register #(.Bits(32)) register_62 (.D(multiplexer_29_out), .C(C_dt), .en(ALU_A_LD), .Q(ALU_A_B));
  Register #(.Bits(8)) register_63 (.D(multiplexer_30_out), .C(C_dt), .en(ALU_A_LD), .Q(ALU_A_FI));
  Register #(.Bits(9)) register_64 (.D(multiplexer_31_out), .C(C_ct), .en(ALU_A_LD), .Q(ALU_A_CT));
  Register #(.Bits(8)) register_65 (.D(multiplexer_32_out), .C(C_ct), .en(ALU_A_LD), .Q({ALU_A_WR, ALU_A_RM}));
  Register #(.Bits(4)) register_66 (.D(multiplexer_33_out), .C(C_ct), .en(ALU_A_LD), .Q(ALU_A_INST));
  or or_22 (or_22_out, CT_DIR__LD, register_52_q);
  Multiplexer multiplexer_46 (.sel(DIR_free), .in_0(xor_8_out), .in_1(register_67_q), .out(multiplexer_46_out));
  xor xor_7 (xor_7_out, register_83_q, register_53_q);
  Multiplexer multiplexer_47 (.sel(register_53_q), .in_0(CT_FU__EPOCH), .in_1(register_54_q), .out(multiplexer_47_out));
  Multiplexer #(.Bits(32)) multiplexer_48 (
    .sel(register_53_q), .in_0(R_A), .in_1(register_55_q), .out(multiplexer_48_out));
  Multiplexer #(.Bits(32)) multiplexer_49 (
    .sel(register_53_q), .in_0(R_B), .in_1(register_56_q), .out(multiplexer_49_out));
  Multiplexer #(.Bits(16)) multiplexer_50 (
    .sel(register_53_q), .in_0({byte_D2_ex, byte_D3_ex}), .in_1(register_57_q), .out(multiplexer_50_out));
  Multiplexer #(.Bits(4)) multiplexer_51 (
    .sel(register_53_q), .in_0(CT_FU__INST), .in_1(register_58_q), .out(multiplexer_51_out));
  Multiplexer #(.Bits(2)) multiplexer_52 (
    .sel(register_53_q), .in_0({CT_FU__WR[1], and_57_out[0]}), .in_1(register_59_q), .out(multiplexer_52_out));
  or or_23 (or_23_out, CT_LDB__LD, register_60_q);
  Multiplexer multiplexer_53 (.sel(LDB_free), .in_0(xor_9_out), .in_1(LDB_busy), .out(multiplexer_53_out));
  and and_58 (and_58_out[0], ALU_A_LD, multiplexer_26_out);
  and and_59 (and_58_out[1], ALU_A_LD, multiplexer_27_out);
  and and_60 (and_60_out[0], ALU_B_LD, multiplexer_26_out);
  and and_61 (and_60_out[1], ALU_B_LD, multiplexer_27_out);
  Register register_67 (.D(or_22_out), .C(C_ct), .en(multiplexer_46_out), .Q(register_67_q));
  Register #(.Bits(32)) register_68 (.D(multiplexer_37_out), .C(C_dt), .en(multiplexer_46_out), .Q(register_68_q));
  Register #(.Bits(8)) register_69 (.D(multiplexer_38_out), .C(C_ct), .en(multiplexer_46_out), .Q(register_69_q));
  Register #(.Bits(4)) register_70 (.D(multiplexer_39_out), .C(C_ct), .en(multiplexer_46_out), .Q(register_70_q));
  or or_24 (or_24_out, CT_STB__LD, register_53_q);
  Multiplexer multiplexer_54 (.sel(STB_free), .in_0(xor_10_out), .in_1(register_83_q), .out(multiplexer_54_out));
  Register register_71 (.D(multiplexer_47_out), .C(C_ct), .en(multiplexer_54_out), .Q(register_71_q));
  Register #(.Bits(32)) register_72 (.D(multiplexer_48_out), .C(C_dt), .en(multiplexer_54_out), .Q(register_72_q));
  Register #(.Bits(32)) register_73 (.D(multiplexer_49_out), .C(C_dt), .en(multiplexer_54_out), .Q(register_73_q));
  Register #(.Bits(16)) register_74 (.D(multiplexer_50_out), .C(C_dt), .en(multiplexer_54_out), .Q(register_74_q));
  Register #(.Bits(4)) register_75 (.D(multiplexer_51_out), .C(C_ct), .en(multiplexer_54_out), .Q(register_75_q));
  Register #(.Bits(2)) register_76 (.D(multiplexer_52_out), .C(C_ct), .en(multiplexer_54_out), .Q(register_76_q));
  Register register_77 (.D(or_23_out), .C(C_ct), .en(multiplexer_53_out), .Q(LDB_busy));
  Register register_78 (.D(multiplexer_41_out), .C(C_ct), .en(multiplexer_53_out), .Q(register_78_q));
  Register #(.Bits(32)) register_79 (.D(multiplexer_42_out), .C(C_dt), .en(multiplexer_53_out), .Q(register_79_q));
  Register #(.Bits(16)) register_80 (.D(multiplexer_43_out), .C(C_dt), .en(multiplexer_53_out), .Q(register_80_q));
  Register #(.Bits(4)) register_81 (.D(multiplexer_44_out), .C(C_ct), .en(multiplexer_53_out), .Q(register_81_q));
  Register #(.Bits(2)) register_82 (.D(multiplexer_45_out), .C(C_ct), .en(multiplexer_53_out), .Q(register_82_q));
  or or_25 (or_25_out, CT_DIR__LD, register_67_q);
  xor xor_8 (xor_8_out, DIR_busy, register_67_q);
  Multiplexer #(.Bits(32)) multiplexer_55 (
    .sel(register_67_q), .in_0(multiplexer_23_out), .in_1(register_68_q), .out(multiplexer_55_out));
  Multiplexer #(.Bits(8)) multiplexer_56 (
    .sel(register_67_q), .in_0(CT_FU__WR), .in_1(register_69_q), .out(multiplexer_56_out));
  Multiplexer #(.Bits(4)) multiplexer_57 (
    .sel(register_67_q), .in_0(CT_FU__INST), .in_1(register_70_q), .out(multiplexer_57_out));
  Register register_83 (.D(or_24_out), .C(C_ct), .en(multiplexer_54_out), .Q(register_83_q));
  Multiplexer multiplexer_58 (.sel(register_83_q), .in_0(CT_FU__EPOCH), .in_1(register_71_q), .out(multiplexer_58_out));
  Multiplexer #(.Bits(32)) multiplexer_59 (
    .sel(register_83_q), .in_0(R_A), .in_1(register_72_q), .out(multiplexer_59_out));
  Multiplexer #(.Bits(32)) multiplexer_60 (
    .sel(register_83_q), .in_0(R_B), .in_1(register_73_q), .out(multiplexer_60_out));
  Multiplexer #(.Bits(16)) multiplexer_61 (
    .sel(register_83_q), .in_0({byte_D2_ex, byte_D3_ex}), .in_1(register_74_q), .out(multiplexer_61_out));
  Multiplexer #(.Bits(4)) multiplexer_62 (
    .sel(register_83_q), .in_0(CT_FU__INST), .in_1(register_75_q), .out(multiplexer_62_out));
  Multiplexer #(.Bits(2)) multiplexer_63 (
    .sel(register_83_q), .in_0({CT_FU__WR[1], and_57_out[0]}), .in_1(register_76_q), .out(multiplexer_63_out));
  or or_26 (or_26_out, CT_LDB__LD, LDB_busy);
  xor xor_9 (xor_9_out, LDB_busy, LDB_busy);
  Multiplexer multiplexer_64 (.sel(LDB_busy), .in_0(CT_FU__EPOCH), .in_1(register_78_q), .out(multiplexer_64_out));
  Multiplexer #(.Bits(32)) multiplexer_65 (.sel(LDB_busy), .in_0(R_B), .in_1(register_79_q), .out(multiplexer_65_out));
  Multiplexer #(.Bits(16)) multiplexer_66 (
    .sel(LDB_busy), .in_0({byte_D2_ex, byte_D3_ex}), .in_1(register_80_q), .out(multiplexer_66_out));
  Multiplexer #(.Bits(4)) multiplexer_67 (
    .sel(LDB_busy), .in_0(CT_FU__INST), .in_1(register_81_q), .out(multiplexer_67_out));
  Multiplexer #(.Bits(2)) multiplexer_68 (
    .sel(LDB_busy), .in_0({CT_FU__WR[1], and_56_out[0]}), .in_1(register_82_q), .out(multiplexer_68_out));
  and and_62 (and_62_out, ~and_58_out[0], ALU_A_STD);  // And
  and and_63 (and_63_out, ~and_58_out[1], ALU_A_STF);  // And
  and and_64 (and_64_out, ~and_60_out[0], ALU_A_STD);  // And
  and and_65 (and_65_out, ~and_60_out[1], ALU_A_STF);  // And
  Register #(.Bits(32)) register_84 (.D(multiplexer_28_out), .C(C_dt), .en(ALU_B_LD), .Q(ALU_B_A));
  Register #(.Bits(32)) register_85 (.D(multiplexer_29_out), .C(C_dt), .en(ALU_B_LD), .Q(ALU_B_B));
  Register #(.Bits(8)) register_86 (.D(multiplexer_30_out), .C(C_dt), .en(ALU_B_LD), .Q(ALU_B_FI));
  Register #(.Bits(9)) register_87 (.D(multiplexer_31_out), .C(C_ct), .en(ALU_A_LD), .Q(ALU_B_CT));
  Register #(.Bits(8)) register_88 (.D(multiplexer_32_out), .C(C_ct), .en(ALU_B_LD), .Q({ALU_B_WR, ALU_B_RM}));
  Register #(.Bits(4)) register_89 (.D(multiplexer_33_out), .C(C_ct), .en(ALU_B_LD), .Q(ALU_B_INST));
  Register #(.Bits(32)) register_90 (.D(multiplexer_55_out), .C(C_dt), .en(DIR_LD), .Q(DIR));
  Register #(.Bits(8)) register_91 (.D(multiplexer_56_out), .C(C_ct), .en(DIR_LD), .Q(DIR_WR));
  Register #(.Bits(4)) register_92 (.D(multiplexer_57_out), .C(C_ct), .en(DIR_LD), .Q(DIR_INST));
  or or_27 (or_27_out, CT_STB__LD, register_83_q);
  xor xor_10 (xor_10_out, STB_busy, register_83_q);
  Register register_93 (.D(multiplexer_64_out), .C(C_ct), .en(LDB_LD), .Q(LD_ep));
  Register #(.Bits(32)) register_94 (.D(multiplexer_65_out), .C(C_dt), .en(LDB_LD), .Q(register_94_q));
  Register #(.Bits(16)) register_95 (.D(multiplexer_66_out), .C(C_dt), .en(LDB_LD), .Q(register_95_q));
  Register #(.Bits(4)) register_96 (.D(multiplexer_67_out), .C(C_ct), .en(LDB_LD), .Q(LD_id));
  Register #(.Bits(2)) register_97 (.D(multiplexer_68_out), .C(C_ct), .en(LDB_LD), .Q(register_97_q));
  D_FF #(.Bits(2)) d_ff_1 (.D(and_58_out), .C(C_ct), .Q(d_ff_1_q));  // open: nQ
  RS_FF rs_ff_1 (.S(and_58_out[0]), .C(C_ct), .R(and_62_out), .nQ(rs_ff_1_nq));  // open: Q
  RS_FF rs_ff_2 (.S(and_58_out[1]), .C(C_ct), .R(and_63_out), .nQ(rs_ff_2_nq));  // open: Q
  D_FF #(.Bits(2)) d_ff_2 (.D(and_60_out), .C(C_ct), .Q(d_ff_2_q));  // open: nQ
  RS_FF rs_ff_3 (.S(and_60_out[0]), .C(C_ct), .R(and_64_out), .nQ(rs_ff_3_nq));  // open: Q
  RS_FF rs_ff_4 (.S(and_60_out[1]), .C(C_ct), .R(and_65_out), .nQ(rs_ff_4_nq));  // open: Q
  and and_66 (and_66_out, ~or_25_out, DIR_ST);  // And
  and and_67 (and_67_out, ~or_25_out, DIR_RD);  // And
  Register register_98 (.D(multiplexer_58_out), .C(C_ct), .en(STB_LD), .Q(ST_ep));
  Register #(.Bits(32)) register_99 (.D(multiplexer_59_out), .C(C_dt), .en(STB_LD), .Q(ST_data));
  Register #(.Bits(32)) register_100 (.D(multiplexer_60_out), .C(C_dt), .en(STB_LD), .Q(register_100_q));
  Register #(.Bits(16)) register_101 (.D(multiplexer_61_out), .C(C_dt), .en(STB_LD), .Q(register_101_q));
  Register #(.Bits(4)) register_102 (.D(multiplexer_62_out), .C(C_ct), .en(STB_LD), .Q(ST_id));
  Register #(.Bits(2)) register_103 (.D(multiplexer_63_out), .C(C_ct), .en(STB_LD), .Q(register_103_q));
  add_s16c32 add_s16c32_1 (.a(register_94_q), .b(register_95_q), .s(LD_addr));  // open: c
  D_FF #(.Bits(2)) d_ff_3 (.D(d_ff_1_q), .C(C_ct), .Q({d_ff_3_q[1], ALU_A_RE}));  // open: nQ
  D_FF #(.Bits(2)) d_ff_4 (.D(d_ff_2_q), .C(C_ct), .Q({d_ff_4_q[1], ALU_B_RE}));  // open: nQ
  RS_FF rs_ff_5 (.S(or_25_out), .C(C_ct), .R(and_66_out), .nQ(rs_ff_5_nq));  // open: Q
  RS_FF rs_ff_6 (.S(or_25_out), .C(C_ct), .R(and_67_out), .Q(DIR_RD));  // open: nQ
  add_s16c32 add_s16c32_2 (.a(register_100_q), .b(register_101_q), .s(ST_addr));  // open: c
  and and_68 (and_68_out, ALU_B_STD, ~and_75_out);  // And
  and and_69 (and_69_out, ALU_B_STF, ~and_75_out);  // And
  or or_28 (DIR_free, DIR_ST, rs_ff_5_nq);
  bus16_demux bus16_demux_1 (.bus(V_inst), .E(DIR_ST), .id(DIR_INST));
  and and_70 (and_70_out, or_26_out, STB_free);
  DipSwitch dipswitch_4 (.out(dipswitch_4_out));
  and and_71 (and_71_out, com1, CT_FL__W1);
  and and_72 (and_72_out, com2, CT_FL__W2);
  RS_FF rs_ff_7 (.S(ALU_A_RE), .C(C_ct), .R(ALU_A_FRD), .Q(ALU_A_DRD));  // open: nQ
  RS_FF rs_ff_8 (.S(d_ff_3_q[1]), .C(C_ct), .R(ALU_A_FRD), .Q(ALU_A_FRD));  // open: nQ
  RS_FF rs_ff_9 (.S(ALU_B_RE), .C(C_ct), .R(ALU_B_DRD), .Q(ALU_B_DRD));  // open: nQ
  RS_FF rs_ff_10 (.S(d_ff_4_q[1]), .C(C_ct), .R(ALU_B_FRD), .Q(ALU_B_FRD));  // open: nQ
  RS_FF rs_ff_11 (.S(and_68_out), .C(C_ct), .R(and_75_out), .Q(rs_ff_11_q));  // open: nQ
  RS_FF rs_ff_12 (.S(and_69_out), .C(C_ct), .R(and_75_out), .Q(rs_ff_12_q));  // open: nQ
  // alu_32 alu_32_1: pin names not known; wires that end beside it: ALU_A_A, ALU_A_B, ALU_A_FI, ALU_A_CT, ALU_A_RM, alu_32_1_p6, alu_32_1_p6, alu_32_1_p8, alu_32_1_p9, alu_32_1_p9, alu_32_1_p11, alu_32_1_p12, alu_32_1_p12, alu_32_1_p14, ALU_A_R, ALU_A_F
  alu_32 alu_32_2 (
    .A(ALU_B_A), .B(ALU_B_B), .F_I(ALU_B_FI), .CT(ALU_B_CT), .RM(ALU_B_RM), .E_A(alu_32_1_p8),
    .E_B(alu_32_1_p11), .E(alu_32_1_p14), .R_O(ALU_B_R), .F_O(ALU_B_F));
  and and_73 (and_73_out, or_27_out, STB_free);
  or or_29 (or_29_out, dipswitch_4_out, LDB_ldV);
  Multiplexer #(.Bits(32)) multiplexer_69 (
    .sel(LDB_ldV), .in_0(pulldown_12_out), .in_1(LDB_ldD), .out(multiplexer_69_out));
  PullDown #(.Bits(32)) pulldown_12 (.out(pulldown_12_out));
  Multiplexer #(.Bits(4)) multiplexer_70 (
    .sel(LDB_ldV), .in_0(pulldown_13_out), .in_1(LD_id), .out(multiplexer_70_out));
  PullDown #(.Bits(4)) pulldown_13 (.out(pulldown_13_out));
  or or_30 (or_30_out, ALU_B_STD, rs_ff_11_q);
  or or_31 (or_31_out, ALU_B_STF, rs_ff_12_q);
  PullDown #(.Bits(32)) pulldown_14 (.out(alu_32_1_p12));
  PullDown #(.Bits(32)) pulldown_15 (.out(alu_32_1_p14));
  and and_74 (DIR_LD, or_25_out, DIR_free);
  not not_13 (DIR_busy, DIR_free);
  bus16_demux bus16_demux_2 (.bus(V_inst), .E(and_73_out), .id(ST_id));
  DipSwitch dipswitch_5 (.out(dipswitch_5_out));
  or or_32 (CT_RF__FLS, and_71_out, and_72_out);
  or or_33 (or_33_out, ALU_A_STD, rs_ff_1_nq);
  or or_34 (or_34_out, ALU_A_STF, rs_ff_2_nq);
  or or_35 (or_35_out, ALU_B_STD, rs_ff_3_nq);
  or or_36 (or_36_out, ALU_B_STF, rs_ff_4_nq);
  and and_75 (and_75_out, or_30_out, or_31_out);
  bus16_demux bus16_demux_3 (.bus(V_inst), .E(and_75_out), .id(ALU_B_INST));
  store_buffer store_buffer_1 (
    .C(C_dt), .LD(dipswitch_5_out), .W_d(or_27_out), .inst_W(ST_id), .D(ST_data), .A(ST_addr),
    .MD(register_103_q), .W_id(CT_ISS__OSTB), .epoch(epoch_IS), .inst(inst_IS), .com1(com1), .com2(com2),
    .com1_id(com1_inst), .com2_id(com2_inst), .ld_ep(LD_ep), .ld_id(LD_id), .ld_addr(LD_addr),
    .full(STB_busy), .V(STB_M__V), .D_O(STB_M__D), .A_O(STB_M__A), .MD_O(STB_M__MD), .id_O(STB_M__ID),
    .ep_O(STB_M__EP), .ld_V(LDB_ldV), .ld_D(LDB_ldD));
  bus16_demux bus16_demux_4 (.bus(V_inst), .E(and_70_out), .id(ST_id));
  // load_buffer load_buffer_1: pin names not known; wires that end beside it: C_dt, load_buffer_1_p2, load_buffer_1_p3, or_29_out, multiplexer_70_out, multiplexer_69_out, or_26_out, LD_id, LD_addr, register_97_q, CT_ISS__OLDB, epoch_IS, inst_IS, com1, com2, com1_inst, com2_inst, ST_ep, ST_id, ST_addr, ST_data, LDB_busy, load_buffer_1_p23, load_buffer_1_p24, load_buffer_1_p25, LDB_M__V, LDB_M__A, LDB_M__MD, LDB_M__ID, LDB_M__EP, load_buffer_1_p31, load_buffer_1_p23, load_buffer_1_p24, load_buffer_1_p25
  DipSwitch dipswitch_6 (.out(load_buffer_1_p2));
  DipSwitch dipswitch_7 (.out(load_buffer_1_p3));
  and and_76 (ALU_A_LD, or_21_out, or_34_out, or_33_out);
  and and_77 (ALU_A_LRD, or_33_out, or_34_out);
  nand nand_1 (nand_1_out, or_33_out, or_34_out);
  and and_78 (ALU_B_LD, nand_1_out, CT_ALU__LD, or_36_out, or_35_out);
  and and_79 (ALU_B_LRD, or_35_out, or_36_out);
  and and_80 (and_80_out, ALU_A_STD, ~and_84_out);  // And
  and and_81 (and_81_out, ALU_A_STF, ~and_84_out);  // And
  Register #(.Bits(32)) register_104 (.D(ALU_A_R), .C(C_dt), .en(ALU_A_RE), .Q(ALU_A_T__R));
  Register #(.Bits(8)) register_105 (.D(ALU_A_F), .C(C_dt), .en(ALU_A_RE), .Q(ALU_A_T__F));
  Register #(.Bits(32)) register_106 (.D(ALU_B_R), .C(C_dt), .en(ALU_B_RE), .Q(ALU_B_T__R));
  Register #(.Bits(8)) register_107 (.D(ALU_B_F), .C(C_dt), .en(ALU_B_RE), .Q(ALU_B_T__F));
  not not_14 (STB_free, STB_busy);
  RS_FF rs_ff_13 (.S(and_80_out), .C(C_ct), .R(and_84_out), .Q(rs_ff_13_q));  // open: nQ
  RS_FF rs_ff_14 (.S(and_81_out), .C(C_ct), .R(and_84_out), .Q(rs_ff_14_q));  // open: nQ
  and and_82 (STB_LD, CT_STB__LD, STB_free);
  not not_15 (LDB_free, LDB_busy);
  Multiplexer #(.Bits(8)) multiplexer_71 (.sel(and_72_out), .in_0(CT_FL__D1), .in_1(CT_FL__D2), .out(fl_i));
  or or_37 (or_37_out, ALU_A_STD, rs_ff_13_q);
  or or_38 (or_38_out, ALU_A_STF, rs_ff_14_q);
  nor nor_4 (ALU_busy, ALU_A_LRD, ALU_B_LRD);
  or or_39 (ALU_free, ALU_A_LRD, ALU_B_LRD);
  and and_83 (LDB_LD, CT_STB__LD, LDB_free);
  and and_84 (and_84_out, or_37_out, or_38_out);
  bus16_demux bus16_demux_5 (.bus(V_inst), .E(and_84_out), .id(ALU_A_INST));
  and and_85 (and_85_out, byte_I0[3], byte_I0[0]);
  and and_86 (and_86_out, byte_I0[2], byte_I0[0]);
  and and_87 (and_87_out, byte_I0_iv[3], byte_I0_iv[2], byte_I0[1], byte_I0_iv[0]);
  and and_88 (and_88_out, byte_I0_iv[2], byte_I0_iv[0]);
  and and_89 (and_89_out, byte_I0[2], byte_I0[0]);
  and and_90 (and_90_out, byte_I0[1], byte_I0[2], byte_I0[4]);
  and and_91 (and_91_out, byte_I0[3], byte_I0[4]);
  and and_92 (and_92_out, byte_I0[4], byte_I0[3], byte_I0_iv[1], byte_I0_iv[2], byte_I0_iv[5], byte_I0_iv[6], byte_I0_iv[7]);
  or or_40 (or_40_out, and_85_out, and_86_out, and_87_out);
  or or_41 (or_41_out, byte_I0[3], byte_I0[1], and_88_out, and_89_out);
  nor nor_5 (nor_5_out, and_90_out, and_91_out);
  and and_93 (and_93_out, byte_I0_iv[7], byte_I0_iv[6], byte_I0[5]);
  and and_94 (and_94_out, byte_I0_iv[7], byte_I0[6], byte_I0_iv[5]);
  PullDown pulldown_16 (.out(CT_ALU__M));
  PullDown pulldown_17 (.out(CT_ALU__LD));
  PullDown pulldown_18 (.out(CT_ALU__WD));
  PullDown pulldown_19 (.out(CT_ALU__WF));
  PullDown pulldown_20 (.out(CT_FU__EPOCH));
  PullDown #(.Bits(4)) pulldown_21 (.out(CT_FU__INST));
  PullDown #(.Bits(8)) pulldown_22 (.out(CT_FU__WR));
  PullDown pulldown_23 (.out(CT_DIR__LD));
  PullDown pulldown_24 (.out(CT_DIR__M));
  PullDown pulldown_25 (.out(CT_DIR__MS));
  and and_95 (and_95_out, byte_I0_iv[0], byte_I0_iv[1], byte_I0[2], byte_I0[3], byte_I0[4], byte_I0_iv[5], byte_I0_iv[6], byte_I0_iv[7]);
  and and_96 (and_96_out, byte_I0[1], byte_I0_iv[2], byte_I0[3], byte_I0[4], byte_I0_iv[5], byte_I0_iv[6], byte_I0_iv[7]);
  and and_97 (and_97_out, byte_I0[1], byte_I0[2], byte_I0[3], byte_I0[4], byte_I0_iv[5], byte_I0_iv[6], byte_I0_iv[7]);
  or or_42 (or_42_out, and_93_out, and_94_out);
  and and_98 (and_98_out, byte_I0_iv[7], byte_I0_iv[6], byte_I0_iv[5], byte_I0_iv[4]);
  and and_99 (and_99_out, byte_I0_iv[7], byte_I0_iv[6], byte_I0_iv[5], byte_I0[4], byte_I0_iv[3]);
  or or_43 (or_43_out, and_95_out, and_96_out);
  not not_16 (not_16_out, byte_I0[0]);
  PullDown pulldown_26 (.out(D_valid));
  or or_44 (or_44_out, STB_M__V, LDB_M__V);
  RS_FF rs_ff_15 (.S(MEM_LD), .C(C_dt), .R(D_valid), .Q(MEM_RD), .nQ(rs_ff_15_nq));
  not not_17 (not_17_out, or_40_out);
  and and_100 (and_100_out, and_97_out, byte_I0[0]);
  and and_101 (and_101_out, not_16_out, and_97_out);
  or or_45 (or_45_out, rs_ff_15_nq, D_valid);
  or or_46 (or_46_out, and_98_out, and_92_out, and_99_out);
  assign issue = or_46_out ? dp_e : 1'bz;  // Driver driver_124
  assign CT_ISS__URA = or_46_out ? 1'b1 : 1'bz;  // Driver driver_125
  assign CT_ISS__URB = or_46_out ? not_17_out : 1'bz;  // Driver driver_126
  assign CT_ISS__RA = or_46_out ? byte_I1[7:3] : 5'bz;  // Driver driver_127
  assign CT_ISS__RB = or_46_out ? byte_I2[7:3] : 5'bz;  // Driver driver_128
  assign CT_ISS__UFL = or_46_out ? or_41_out : 1'bz;  // Driver driver_129
  assign CT_ISS__ORC = or_46_out ? nor_5_out : 1'bz;  // Driver driver_130
  assign CT_ISS__RC = or_46_out ? byte_I1[7:3] : 5'bz;  // Driver driver_131
  assign CT_ISS__OFL = or_46_out ? 1'b1 : 1'bz;  // Driver driver_132
  assign CT_ISS__UFU = or_46_out ? 3'b001 : 3'bz;  // Driver driver_133
  assign CT_ISS__URA = and_95_out ? 1'b1 : 1'bz;  // Driver driver_134
  assign CT_ISS__RA = and_95_out ? byte_I2[7:3] : 5'bz;  // Driver driver_135
  assign issue = or_43_out ? dp_e : 1'bz;  // Driver driver_136
  assign CT_ISS__ORC = or_43_out ? 1'b1 : 1'bz;  // Driver driver_137
  assign CT_ISS__RC = or_43_out ? byte_I1[7:3] : 5'bz;  // Driver driver_138
  assign CT_ISS__UFU = or_43_out ? 3'b010 : 3'bz;  // Driver driver_139
  assign issue = and_97_out ? dp_e : 1'bz;  // Driver driver_140
  assign CT_ISS__USC = and_97_out ? 1'b1 : 1'bz;  // Driver driver_141
  assign CT_ISS__OSC = and_97_out ? 1'b1 : 1'bz;  // Driver driver_142
  assign CT_ISS__URA = and_100_out ? 1'b1 : 1'bz;  // Driver driver_143
  assign CT_ISS__RA = and_100_out ? byte_I1[7:3] : 5'bz;  // Driver driver_144
  assign CT_ISS__UFU = and_100_out ? 3'b011 : 3'bz;  // Driver driver_145
  assign CT_ISS__ORC = and_101_out ? 1'b1 : 1'bz;  // Driver driver_146
  assign CT_ISS__RC = and_101_out ? byte_I1[7:3] : 5'bz;  // Driver driver_147
  assign CT_ISS__UFU = and_101_out ? 3'b100 : 3'bz;  // Driver driver_148
  assign issue = or_42_out ? dp_e : 1'bz;  // Driver driver_149
  assign CT_ISS__URA = or_42_out ? 1'b1 : 1'bz;  // Driver driver_150
  assign CT_ISS__RA = or_42_out ? byte_I0[4:0] : 5'bz;  // Driver driver_151
  assign CT_ISS__URB = and_94_out ? 1'b1 : 1'bz;  // Driver driver_152
  assign CT_ISS__RB = and_94_out ? byte_I1[7:3] : 5'bz;  // Driver driver_153
  assign CT_ISS__UFU = and_94_out ? 3'b011 : 3'bz;  // Driver driver_154
  assign CT_ISS__ORC = and_93_out ? 1'b1 : 1'bz;  // Driver driver_155
  assign CT_ISS__RC = and_93_out ? byte_I1[7:3] : 5'bz;  // Driver driver_156
  assign CT_ISS__UFU = and_93_out ? 3'b100 : 3'bz;  // Driver driver_157
  store_controller store_controller_1 (
    .C(C_ct), .in1(ALU_A_DRD), .in2(ALU_B_DRD), .in3(1'b0), .in4(1'b0), .in5(1'b0), .in6(DIR_RD), .in7(1'b0),
    .in8(1'b0), .D1_sel(store_controller_1_d1_sel), .D2_sel(store_controller_1_d2_sel),
    .ST1(CT_ROB__GEN__STA), .ST2(CT_ROB__GEN__STB), .out1(ALU_A_STD), .out2(ALU_B_STD), .out6(DIR_ST));  // open: out3, out4, out5, out7, out8
  store_controller store_controller_2 (
    .C(C_ct), .in1(ALU_B_FRD), .in2(ALU_A_FRD), .in3(1'b0), .in4(1'b0), .in5(1'b0), .in6(1'b0), .in7(1'b0),
    .in8(1'b0), .D1_sel(store_controller_2_d1_sel), .D2_sel(store_controller_2_d2_sel),
    .ST1(CT_ROB__FL__STA), .ST2(CT_ROB__FL__STB), .out1(ALU_A_STF), .out2(ALU_B_STF));  // open: out3, out4, out5, out6, out7, out8
  D_FF #(.Bits(8)) d_ff_5 (
    .D({3'b000, STB_free, LDB_free, DIR_free, ALU_free, 1'b1}), .C(C_ct), .Q(FU_free));  // open: nQ
  xor xor_11 (xor_11_out, STB_M__EP, LDB_M__EP);
  Comparator #(.Bits(4)) comparator_3 (
    .a(STB_M__ID), .b(LDB_M__ID), .gt(comparator_3_gt), .lt(comparator_3_lt));  // open: eq
  and and_102 (MEM_LD, or_44_out, or_45_out);
  and and_103 (and_103_out, STB_M__V, LDB_M__V);
  Multiplexer multiplexer_72 (
    .sel(xor_11_out), .in_0(comparator_3_gt), .in_1(comparator_3_lt), .out(multiplexer_72_out));
  Multiplexer multiplexer_73 (.sel(and_103_out), .in_0(STB_M__V), .in_1(multiplexer_72_out), .out(multiplexer_73_out));
  Multiplexer #(.Bits(32)) multiplexer_74 (
    .sel(multiplexer_73_out), .in_0(LDB_M__A), .in_1(STB_M__A), .out(multiplexer_74_out));
  Multiplexer #(.Bits(2)) multiplexer_75 (
    .sel(multiplexer_73_out), .in_0(LDB_M__MD), .in_1(STB_M__MD), .out(multiplexer_75_out));
  // data_select_32 data_select_32_1: pin names not known; wires that end beside it: store_controller_1_d1_sel, store_controller_1_d2_sel, ALU_A_T__R, ALU_B_T__R, {32{1'b0}}, {32{1'b0}}, {32{1'b0}}, DIR, {32{1'b0}}, {32{1'b0}}, ROB_GEN_DA, ROB_GEN_DB
  data_select_8 data_select_8_1 (
    .D1_sel(store_controller_2_d1_sel), .D2_sel(store_controller_2_d2_sel), .in1(ALU_A_T__F),
    .in2(ALU_B_T__F), .in3({8{1'b0}}), .in4({8{1'b0}}), .in5({8{1'b0}}), .in6({8{1'b0}}), .in7({8{1'b0}}),
    .in8({8{1'b0}}), .out1(ROB_FL_A), .out2(ROB_FL_B));
  Register register_108 (.D(multiplexer_73_out), .C(C_dt), .en(MEM_LD), .Q(register_108_q));
  Register #(.Bits(4)) register_109 (.D(LDB_M__ID), .C(C_dt), .en(MEM_LD), .Q(register_109_q));
  Register #(.Bits(32)) register_110 (.D(multiplexer_74_out), .C(C_dt), .en(MEM_LD), .Q(register_110_q));
  Register #(.Bits(2)) register_111 (.D(multiplexer_75_out), .C(C_dt), .en(MEM_LD), .Q(register_111_q));
  Register #(.Bits(32)) register_112 (.D(STB_M__D), .C(C_dt), .en(MEM_LD), .Q(register_112_q));
  and and_104 (and_104_out, byte_I0_iv[4], byte_I0[5], byte_I0[6], byte_I0_iv[7]);
  assign D_A__bus = MEM_RD ? register_110_q : 32'bz;  // Driver driver_158
  assign D_MD = MEM_RD ? register_111_q : 2'bz;  // Driver driver_159
  assign D_D__bus = MEM_RD ? register_112_q : 32'bz;  // Driver driver_160
  Comparator #(.Bits(3)) comparator_4 (.a(byte_I0[2:0]), .b(3'b110), .eq(comparator_4_eq));  // open: gt, lt
  and and_105 (D_LD, ~register_108_q, MEM_RD);  // And
  and and_106 (D_ST, MEM_RD, register_108_q);
  not not_18 (not_18_out, comparator_4_eq);
  and and_107 (and_107_out, byte_I0_iv[0], byte_I0_iv[1], byte_I0_iv[2], byte_I0_iv[3], byte_I0[4], byte_I0[5], byte_I0[6], byte_I0_iv[7]);
  and and_108 (and_108_out, byte_I0[0], byte_I0_iv[1], byte_I0_iv[2], byte_I0_iv[3], byte_I0[4], byte_I0[5], byte_I0[6], byte_I0_iv[7]);
  and and_109 (and_109_out, byte_I0[0], byte_I0[1], byte_I0_iv[2], byte_I0_iv[3], byte_I0[4], byte_I0[5], byte_I0[6], byte_I0_iv[7]);
  assign issue = and_104_out ? dp_e : 1'bz;  // Driver driver_161
  assign CT_ISS__URA = and_104_out ? 1'b1 : 1'bz;  // Driver driver_162
  assign CT_ISS__RA = and_104_out ? byte_I1[7:3] : 5'bz;  // Driver driver_163
  assign CT_ISS__UFL = and_104_out ? not_18_out : 1'bz;  // Driver driver_164
  assign issue = and_107_out ? dp_e : 1'bz;  // Driver driver_165
  assign CT_ISS__URA = and_107_out ? 1'b1 : 1'bz;  // Driver driver_166
  assign CT_ISS__RA = and_107_out ? byte_I1[7:3] : 5'bz;  // Driver driver_167
  assign CT_ISS__USC = and_107_out ? 1'b1 : 1'bz;  // Driver driver_168
  assign CT_ISS__OSC = and_107_out ? 1'b1 : 1'bz;  // Driver driver_169
  assign issue = and_108_out ? dp_e : 1'bz;  // Driver driver_170
  assign CT_ISS__USC = and_108_out ? 1'b1 : 1'bz;  // Driver driver_171
  assign CT_ISS__OSC = and_108_out ? 1'b1 : 1'bz;  // Driver driver_172
  assign issue = and_109_out ? dp_e : 1'bz;  // Driver driver_173
  data_select_8 data_select_8_2 (
    .D1_sel(store_controller_1_d1_sel), .D2_sel(store_controller_1_d2_sel), .in1({ALU_A_WR, ALU_A_RM}),
    .in2({ALU_B_WR, ALU_B_RM}), .in3({8{1'b0}}), .in4({8{1'b0}}), .in5({8{1'b0}}), .in6(DIR_WR),
    .in7({8{1'b0}}), .in8({8{1'b0}}), .out1(ROB_GEN_WA), .out2(ROB_GEN_WB));
  data_select_4 data_select_4_1 (
    .D1_sel(store_controller_2_d1_sel), .D2_sel(store_controller_2_d2_sel), .in1(ALU_A_INST),
    .in2(ALU_B_INST), .in3(4'b0000), .in4(4'b0000), .in5(4'b0000), .in6(4'b0000), .in7(4'b0000),
    .in8(4'b0000), .out1(ROB_FL_INSTA), .out2(ROB_FL_INSTB));
  PullDown pulldown_27 (.out(LD_ep));
  PullDown #(.Bits(4)) pulldown_28 (.out(LD_id));
  PullDown #(.Bits(32)) pulldown_29 (.out(LD_addr));
  PullDown pulldown_30 (.out(CT_STB__LD));
  PullDown pulldown_31 (.out(CT_LDB__LD));
  PullDown pulldown_32 (.out(CT_ISS__OLDB));
  data_select_4 data_select_4_2 (
    .D1_sel(store_controller_1_d1_sel), .D2_sel(store_controller_1_d2_sel), .in1(ALU_A_INST),
    .in2(ALU_B_INST), .in3(4'b0000), .in4(4'b0000), .in5(4'b0000), .in6(DIR_INST), .in7(4'b0000),
    .in8(4'b0000), .out1(ROB_GEN_INSTA), .out2(ROB_GEN_INSTB));
  not not_19 (not_19_out, E);
  PullDown pulldown_33 (.out(kernel_inst));
  PullDown pulldown_34 (.out(CT_RF__E));
  PullDown pulldown_35 (.out(CT_RF__DM));
  PullDown #(.Bits(5)) pulldown_36 (.out(CT_RF__WS));
  PullDown #(.Bits(3)) pulldown_37 (.out(CT_RF__WM));
  PullDown #(.Bits(5)) pulldown_38 (.out(CT_RF__RA));
  PullDown #(.Bits(3)) pulldown_39 (.out(CT_RF__MA));
  PullDown #(.Bits(5)) pulldown_40 (.out(CT_RF__RB));
  PullDown #(.Bits(3)) pulldown_41 (.out(CT_RF__MB));
  PullDown pulldown_42 (.out(CT_RF__PCSE));
  PullDown pulldown_43 (.out(CT_RF__PCJ));
  PullDown pulldown_44 (.out(CT_RF__PCR));
  PullDown #(.Bits(3)) pulldown_45 (.out(CT_RF__SCN));
  PullDown pulldown_46 (.out(CT_RF__SCD));
  PullDown pulldown_47 (.out(CT_RF__SCAS));
  PullDown pulldown_48 (.out(CT_RF__SCSE));
  PullDown pulldown_49 (.out(CT_RF__FLS));
  PullDown #(.Bits(4)) pulldown_50 (.out(4'b0001));
  PullDown #(.Bits(9)) pulldown_51 (.out(CT_ALU__CT));
  PullDown pulldown_52 (.out(CT_ALU__M));
  PullDown pulldown_53 (.out(CT_ALU__M2));
  PullDown pulldown_54 (.out(CT_BUS__IAR));
  PullDown pulldown_55 (.out(CT_BUS__IAG));
  PullDown pulldown_56 (.out(CT_BUS__IDR));
  PullDown pulldown_57 (.out(CT_BUS__IDM));
  PullDown pulldown_58 (.out(CT_BUS__DAR));
  PullDown pulldown_59 (.out(CT_BUS__DAM));
  PullDown pulldown_60 (.out(CT_BUS__DAG));
  PullDown pulldown_61 (.out(CT_BUS__DDR));
  PullDown pulldown_62 (.out(CT_BUS__DDG));
  PullDown pulldown_63 (.out(I_LD));
  PullDown pulldown_64 (.out(D_LD));
  PullDown pulldown_65 (.out(D_ST));
  PullDown #(.Bits(2)) pulldown_66 (.out(D_MD));
  PullDown pulldown_67 (.out(CT_MVR));
  // res_station res_station_1: pin names not known; wires that end beside it: C_ct, not_19_out, issue, {byte_I0, byte_I1, byte_I2, byte_I3}, epoch_IS, inst_IS, CT_ISS__URA, CT_ISS__URB, CT_ISS__RA, CT_ISS__RB, CT_ISS__USC, CT_ISS__UFL, CT_ISS__UFU, CT_ISS__ORC, CT_ISS__RC, CT_ISS__OSC, CT_ISS__OFL, com1, com2, com1_inst, com2_inst, CT_RF__R1[7:3], CT_RF__R2[7:3], CT_SC__W1, CT_SC__W2, CT_FL__W1, CT_FL__W2, clr, FU_free, CT_DISP, {res_station_1_p31, byte_D1, byte_D2, byte_D3}, epoch_DP, inst_DP, RS_full
  PullDown #(.Bits(3)) pulldown_68 (.out(CT_ISS__UFU));
  PullDown pulldown_69 (.out(CT_ISS__OSTB));
  Multiplexer #(.Bits(8)) multiplexer_76 (.sel(CT_DISP), .in_0(8'h72), .in_1(res_station_1_p31), .out(byte_D0));
  PullDown pulldown_70 (.out(clr));
  PullDown pulldown_71 (.out(clr_ep));
  PullDown #(.Bits(4)) pulldown_72 (.out(clr_id));
  PullDown pulldown_73 (.out(issue));
  PullDown pulldown_74 (.out(CT_ISS__URA));
  PullDown pulldown_75 (.out(CT_ISS__URB));
  PullDown #(.Bits(5)) pulldown_76 (.out(CT_ISS__RA));
  PullDown #(.Bits(5)) pulldown_77 (.out(CT_ISS__RB));
  PullDown pulldown_78 (.out(CT_ISS__USC));
  PullDown pulldown_79 (.out(CT_ISS__UFL));
  PullDown pulldown_80 (.out(CT_ISS__ORC));
  PullDown #(.Bits(5)) pulldown_81 (.out(CT_ISS__RC));
  PullDown pulldown_82 (.out(CT_ISS__OSC));
  PullDown pulldown_83 (.out(CT_ISS__OFL));
  PullDown pulldown_84 (.out(CT_ROB__EX__E));
  PullDown pulldown_85 (.out(CT_ROB__ST__E));
  PullDown #(.Bits(3)) pulldown_86 (.out(CT_BUS__DASDN));
  PullDown pulldown_87 (.out(CT_BUS__DDM));
  PullDown pulldown_88 (.out(CT_RF__PCH));
  PullDown pulldown_89 (.out(hlt));
  PullDown pulldown_90 (.out(ex_nop));

  assign CLK_str = 1'b0;
  assign CSH_mode = 2'b00;
  assign CSH_run = 1'b0;
  assign DMA_sel = 3'b000;
  assign DMA_str = 1'b0;
  assign INT_out = 1'b0;
  assign INT_str = 1'b0;
  assign MMU_sel = 2'b00;
  assign MMU_str = 1'b0;

  // Other names for the same wires on the sheet: disp_32[31:0] = {byte_D0, byte_D1, byte_D2, byte_D3};
  //   ALU_A_WR[2:0] = ALU_A_RM; ALU_B_WR[2:0] = ALU_B_RM; ALU_R[31:0] = ALU_A_T__R; ALU_T__R[31:0] = ALU_A_T__R;
  //   imm16_2_ex[15:0] = {byte_D2_ex, byte_D3_ex}; C_i = C_dt; ext_e = cm_e; ext_e__bf = cm_e__bf; int_proc = FL[14];
  //   trap = FL[15]; issue_32[31:0] = {byte_I0, byte_I1, byte_I2, byte_I3}; issue_e = dp_e; MEM_AC = D_valid;
  //   st_e = rf_e

  // Notes on the sheet:
  //   C: Hz: 4
  //   bus_e: default 1
  //   D_MD: 0:32
  //   1:16
  //   2:8
  //   3:u.u
  //   I_valid: default 1
  //   D_valid: default 1
  //   kernal mode system
  //   interrupt system
  //   pipeline controller
  //   inst id manager
  //   tests
  //   IO pins
  //   primeary signals
  //   decode circuit
  //   ALU
  //   register
  //   program counter controller
  //   bus system
  //   register system
  //   ROB
  //   stack
  //   RAM
  //   jump
  //   call
  //   return
  //   halt
  //   stack circuit
  //   ALU system
  //   dir circuit
  //   store circuit
  //   load circuit
  //   flag circuit
  //   issue circuit
  //   FU aribiter
  //   control bus
endmodule
