// Digital circuit cpu-32 test2.dig as structural Verilog
module cpu_32_test2 (
  input  C,
  input  bus_e,
  input  E,
  input  [31:0] I_D__bus,
  input  [31:0] D_D__bus,
  input  [31:0] I_A__bus,
  input  [31:0] D_A__bus,
  input  INT_nor,
  input  INT_nmk,
  input  run,
  input  I_valid,
  input  D_valid,
  output I_LD,
  output D_LD,
  output D_ST,
  output [1:0] MMU_sel,
  output MMU_str,
  output [2:0] DMA_sel,
  output DMA_str,
  output INT_str,
  output CLK_str,
  output [1:0] CSH_mode,
  output CSH_run,
  output INT_out,
  output [1:0] D_MD
);

  wire add_4c32_1_c, alu_32_1_p6, alu_32_1_p8, alu_e, and_1_out, and_3_out, and_4_out, and_5_out, and_6_out,
       and_9_out, and_10_out, and_11_out, and_12_out, and_13_out, and_14_out, and_17_out, and_18_out,
       and_19_out, and_20_out, and_21_out, and_22_out, and_24_out, and_25_out, and_26_out, and_27_out,
       and_28_out, and_29_out, and_30_out, and_31_out, and_32_out, and_33_out, and_34_out, and_35_out,
       and_36_out, and_37_out, and_38_out, and_41_out, and_42_out, and_44_out, and_45_out, and_46_out,
       and_47_out, and_48_out, and_50_out, and_51_out, and_60_out, and_61_out, and_62_out, and_63_out, C_ct,
       C_dt, comparator_1_gt, comparator_2_eq, CT_ALU__M2, CT_BUS__DAG, CT_BUS__DAM, CT_BUS__DAR,
       CT_BUS__DDG, CT_BUS__DDM, CT_BUS__DDR, CT_BUS__IAG, CT_BUS__IAR, CT_BUS__IDM, CT_BUS__IDR, CT_DEP__EA,
       CT_DEP__EB, CT_DEP__EOA, CT_DEP__OFLE, CT_DEP__OFLS, CT_DEP__OSCE, CT_DEP__OSCS, CT_DEP__STA,
       CT_DEP__STB, CT_MVR, CT_RAW, CT_RF__DE, CT_RF__DM, CT_RF__E, CT_RF__FLS, CT_RF__PCAE, CT_RF__PCH,
       CT_RF__PCJ, CT_RF__PCR, CT_RF__PCSE, CT_RF__SCD, CT_RF__SCDE, CT_RF__SCE, CT_RF__SCS, d_ff_1_q,
       d_ff_2_q, dc_e, dipswitch_1_out, dipswitch_2_out, dipswitch_3_out, dp_e, ex_e__bf, ex_nop, ext_e__bf,
       ft_e, hlt, int_run, kernel_inst, mode, multiplexer_5_out, multiplexer_8_out, multiplexer_9_out,
       multiplexer_14_out, multiplexer_15_out, multiplexer_16_out, multiplexer_17_out, multiplexer_18_out,
       multiplexer_19_out, nand_1_out, nand_2_out, nand_3_out, nand_4_out, nor_2_out, nor_4_out, nor_6_out,
       nor_7_out, nor_8_out, not_1_out, not_2_out, not_4_out, not_5_out, not_6_out, not_7_out, or_8_out,
       or_9_out, or_11_out, or_22_out, or_23_out, or_24_out, regfile2_1_p32, regfile2_1_p35, register_3_q,
       register_5_q, register_6_q, register_19_q, register_20_q, register_23_q, register_24_q, register_25_q,
       register_26_q, register_36_q, register_37_q, register_38_q, register_39_q, register_40_q,
       register_41_q, register_42_q, register_43_q, register_44_q, register_45_q, register_46_q, rf_e,
       rs_ff_1_q, rs_ff_as_1_nq, st_e__bf, xor_1_out, xor_2_out, xor_3_out, xor_4_out, xor_5_out;
  wire [0:0] and_57_out;
  wire [1:0] and_39_out, and_43_out, CT_ALU__M, register_22_q;
  wire [2:0] and_2_out, and_7_out, and_8_out, and_53_out, and_56_out, bitextender_1_out, CT_BUS__DASDN,
       CT_DEP__OFL, CT_DEP__OMA, CT_DEP__OMB, CT_DEP__OSC, CT_DEP__UMA, CT_DEP__UMB, CT_RF__DEM, CT_RF__MA,
       CT_RF__MB, CT_RF__SCN, CT_RF__WM, EOB_p18, EOB_p19, multiplexer_11_out, multiplexer_12_out, or_1_out,
       or_4_out, or_6_out, register_27_q, register_29_q, register_30_q, register_31_q, register_32_q,
       register_35_q;
  wire [2:1] and_54_out;
  wire [3:0] CT_RF__FLDE, CT_RF__FLE;
  wire [3:3] register_35_q_2;
  wire [4:0] CT_DEP__ORA, CT_DEP__ORB, CT_DEP__URA, CT_DEP__URB, CT_RF__DES, CT_RF__RA, CT_RF__RB, CT_RF__WS;
  wire [7:0] ALU_F, ALU_T__F, and_49_out, bitextender_3_out, bitextender_5_out, byte0, byte0_iv, byte1,
       byte1_ex, byte1_st, byte2, byte2_ex, byte3, byte3_ex, register_28_q, xor_6_out;
  wire [8:0] CT_ALU__A;
  wire [9:8] fl_i;
  wire [10:0] and_23_out, multiplexer_7_out, register_21_q;
  wire [23:0] inst_iv;
  wire [31:0] add_1_s, add_4c32_1_s, alu_32_1_p10, ALU_R, ALU_T__R, bitextender_2_out, bitextender_4_out,
       D_A__R_q, FL, I_A__R_q, I_D__R_q, multiplexer_1_out, multiplexer_3_out, multiplexer_4_out,
       multiplexer_10_out, multiplexer_13_out, mVec, OD_D__R_q, PCA, pca_i, PCS, PCS_d1, PCS_d2, pcs_i, R_A,
       R_B, ramdualaccess_1_d1, ramdualaccess_1_d2, register_1_q, register_2_q, SC, sc_i, sub_4c32_1_s;

  nor nor_1 (or_1_out[0], CT_DEP__OMA[0], CT_DEP__OMA[1]);
  nor nor_2 (nor_2_out, CT_DEP__OMA[0], CT_DEP__OMA[1], CT_DEP__OMA[2]);
  xor xor_1 (xor_1_out, CT_DEP__OMA[0], CT_DEP__OMA[1]);
  or or_1 (or_1_out[1], CT_DEP__OMA[0], nor_2_out);
  or or_2 (or_1_out[2], nor_2_out, xor_1_out);
  BitExtender #(.inputBits(1), .outputBits(3)) bitextender_1 (.in(CT_DEP__EOA), .out(bitextender_1_out));
  nor nor_3 (or_4_out[0], CT_DEP__UMA[0], CT_DEP__UMA[1]);
  nor nor_4 (nor_4_out, CT_DEP__UMA[0], CT_DEP__UMA[1], CT_DEP__UMA[2]);
  xor xor_2 (xor_2_out, CT_DEP__UMA[0], CT_DEP__UMA[1]);
  nor nor_5 (or_6_out[0], CT_DEP__UMB[0], CT_DEP__UMB[1]);
  nor nor_6 (nor_6_out, CT_DEP__UMB[0], CT_DEP__UMB[1], CT_DEP__UMB[2]);
  xor xor_3 (xor_3_out, CT_DEP__UMB[0], CT_DEP__UMB[1]);
  and and_1 (and_1_out, not_1_out, CT_DEP__STA, dp_e);
  not not_1 (not_1_out, ex_nop);
  assign and_2_out = bitextender_1_out & or_1_out;  // And and_2, 3 bits wide
  Comparator #(.Bits(32)) comparator_1 (.a(PCA), .b(mVec), .gt(comparator_1_gt));  // open: eq, lt
  or or_3 (or_4_out[1], CT_DEP__UMA[0], nor_4_out);
  or or_4 (or_4_out[2], nor_4_out, xor_2_out);
  or or_5 (or_6_out[1], CT_DEP__UMB[0], nor_6_out);
  or or_6 (or_6_out[2], nor_6_out, xor_3_out);
  // reg_scoreboard EOB: pin names not known; wires that end beside it: C_ct, and_1_out, CT_DEP__STB, and_2_out, CT_DEP__ORA, CT_DEP__ORB, CT_DEP__URA, CT_DEP__URB, 3'b000, 1'b0, 1'b0, CT_DEP__OSC, CT_DEP__OSCS, CT_DEP__OSCE, CT_DEP__OFL, CT_DEP__OFLS, CT_DEP__OFLE, EOB_p18, EOB_p19
  BitExtender #(.inputBits(16), .outputBits(32)) bitextender_2 (.in({byte2_ex, byte3_ex}), .out(bitextender_2_out));
  and and_3 (and_3_out, FL[14], INT_nor);
  and and_4 (and_4_out, CT_DEP__URA[0], CT_DEP__URA[1]);
  xor xor_4 (xor_4_out, CT_DEP__URA[2], CT_DEP__URA[3]);
  and and_5 (and_5_out, CT_DEP__URB[0], CT_DEP__URB[1]);
  xor xor_5 (xor_5_out, CT_DEP__URB[2], CT_DEP__URB[3]);
  and and_6 (and_6_out, 1'b0, ~comparator_1_gt);  // And
  Add #(.Bits(32)) add_1 (.a(R_A), .b(bitextender_2_out), .c_i(1'b0), .s(add_1_s));  // open: c_o
  or or_7 (int_run, and_3_out, INT_nmk);
  assign and_7_out = or_4_out & EOB_p18;  // And and_7, 3 bits wide
  assign and_8_out = EOB_p19 & or_6_out;  // And and_8, 3 bits wide
  nand nand_1 (nand_1_out, and_4_out, xor_4_out);
  nand nand_2 (nand_2_out, and_5_out, xor_5_out);
  RS_FF u_mode (.S(and_6_out), .C(C_dt), .R(comparator_1_gt), .Q(mode));  // open: nQ
  Register #(.Bits(32)) MVR (.D(add_1_s), .C(C_dt), .en(CT_MVR), .Q(mVec));
  or or_8 (or_8_out, and_7_out[0], and_7_out[1], and_7_out[2]);
  or or_9 (or_9_out, and_8_out[0], and_8_out[1], and_8_out[2]);
  and and_9 (and_9_out, nand_1_out, CT_DEP__EA);
  and and_10 (and_10_out, nand_2_out, CT_DEP__EB);
  and and_11 (and_11_out, or_8_out, and_9_out);
  and and_12 (and_12_out, or_9_out, and_10_out);
  or or_10 (CT_RAW, and_11_out, and_12_out);
  and and_13 (and_13_out, CT_RAW, dp_e);
  DipSwitch dipswitch_1 (.out(dipswitch_1_out));
  D_FF d_ff_1 (.D(dipswitch_1_out), .C(C_ct), .Q(d_ff_1_q));  // open: nQ
  Multiplexer #(.Bits(32)) multiplexer_1 (.sel(CT_RF__DM), .in_0(ALU_T__R), .in_1(D_D__bus), .out(multiplexer_1_out));
  and and_14 (and_14_out, rf_e, CT_RF__E);
  DipSwitch dipswitch_2 (.out(dipswitch_2_out));
  Multiplexer multiplexer_2 (.sel(dipswitch_3_out), .in_0(dipswitch_2_out), .in_1(C), .out(C_dt));
  DipSwitch dipswitch_3 (.out(dipswitch_3_out));
  RS_FF rs_ff_1 (.S(run), .C(C_ct), .R(hlt), .Q(rs_ff_1_q));  // open: nQ
  not not_2 (not_2_out, and_13_out);
  assign ex_nop = and_13_out ? 1'b1 : 1'bz;  // Driver driver_1
  or or_11 (or_11_out, hlt, d_ff_1_q);
  // Probe on multiplexer_1_out
  // Probe on CT_RF__WS
  // Probe on CT_RF__WM
  // Probe on CT_RF__RA
  // Probe on CT_RF__MA
  // Probe on CT_RF__RB
  // Probe on CT_RF__MB
  Register #(.Bits(32)) register_1 (.D(ALU_T__R), .C(C_dt), .en(CT_RF__E), .Q(register_1_q));
  not not_3 (C_ct, C_dt);
  D_FF d_ff_2 (.D(run), .C(C_ct), .Q(d_ff_2_q));  // open: nQ
  Register #(.Bits(32)) register_2 (.D(multiplexer_1_out), .C(C_dt), .en(and_14_out), .Q(register_2_q));
  // Probe on and_14_out
  // Probe M on CT_RF__WM
  // Probe REG st on register_1_q
  // Probe INST on {byte0, byte1, byte2, byte3}
  and and_15 (ft_e, rs_ff_1_q, not_2_out);
  Register register_3 (.D(rs_ff_1_q), .C(C_dt), .en(1'b1), .Q(register_3_q));
  Register #(.Bits(32)) register_4 (.D(PCS), .C(C_dt), .en(CT_RF__PCSE), .Q(PCS_d1));
  RS_FF_AS rs_ff_as_1 (.S(d_ff_2_q), .R(or_11_out), .nQ(rs_ff_as_1_nq));  // open: Q
  // Probe on register_2_q
  // Probe S on CT_RF__WS
  Register register_5 (.D(rs_ff_1_q), .C(C_ct), .en(1'b1), .Q(register_5_q));
  assign CT_BUS__IDM = rs_ff_as_1_nq ? 1'b1 : 1'bz;  // Driver driver_2
  // Probe inst on {byte0, byte1, byte2, byte3}
  // Probe R_A on R_A
  // Probe R_B on R_B
  // Probe PC on PCA
  // Probe SC on SC
  // Probe FL on FL
  // Probe CT_BUS-_IDM on CT_BUS__IDM
  // Probe C_i on C_dt
  and and_16 (dc_e, register_5_q, not_2_out);
  Register register_6 (.D(register_3_q), .C(C_dt), .en(1'b1), .Q(register_6_q));
  Register #(.Bits(32)) register_7 (.D(PCS_d1), .C(C_dt), .en(CT_RF__PCSE), .Q(PCS_d2));
  Register #(.Bits(8)) register_8 (.D(byte1), .C(C_ct), .en(ex_e__bf), .Q(byte1_ex));
  Register #(.Bits(8)) register_9 (.D(byte2), .C(C_ct), .en(ex_e__bf), .Q(byte2_ex));
  Register #(.Bits(8)) register_10 (.D(byte3), .C(C_ct), .en(ex_e__bf), .Q(byte3_ex));
  Register register_11 (.D(register_5_q), .C(C_ct), .en(1'b1), .Q(dp_e));
  assign CT_RF__PCSE = ft_e ? 1'b1 : 1'bz;  // Driver driver_3
  assign CT_BUS__IAR = ft_e ? 1'b1 : 1'bz;  // Driver driver_4
  assign CT_BUS__IAG = ft_e ? 1'b1 : 1'bz;  // Driver driver_5
  assign I_LD = ft_e ? 1'b1 : 1'bz;  // Driver driver_6
  Register register_12 (.D(register_6_q), .C(C_dt), .en(1'b1), .Q(ex_e__bf));
  Register #(.Bits(32)) register_13 (.D(PCS_d2), .C(C_dt), .en(CT_RF__PCSE), .Q(pca_i));
  Register register_14 (.D(dp_e), .C(C_ct), .en(1'b1), .Q(alu_e));
  Register #(.Bits(8)) register_15 (.D(byte1_ex), .C(C_ct), .en(st_e__bf), .Q(byte1_st));
  Register register_16 (.D(ex_e__bf), .C(C_dt), .en(1'b1), .Q(st_e__bf));
  RAMDualAccess #(.AddrBits(24), .isProgramMemory("true"), .Bits(32)) ramdualaccess_1 (
    .str(D_ST), .C(C_dt), .ld(1'b1), .A1(D_A__bus[25:2]), .Din1(D_D__bus), .A2(I_A__bus[25:2]),
    .D1(ramdualaccess_1_d1), .D2(ramdualaccess_1_d2));
  Register register_17 (.D(alu_e), .C(C_ct), .en(1'b1), .Q(rf_e));
  assign D_D__bus = D_LD ? ramdualaccess_1_d1 : 32'bz;  // Driver driver_7
  assign I_D__bus = I_LD ? ramdualaccess_1_d2 : 32'bz;  // Driver driver_8
  Register register_18 (.D(st_e__bf), .C(C_dt), .en(1'b1), .Q(ext_e__bf));
  sub_4c32 sub_4c32_1 (.a(SC), .b({1'b0, CT_BUS__DASDN}), .s(sub_4c32_1_s));
  and and_17 (and_17_out, byte0[3], byte0[0]);
  and and_18 (and_18_out, byte0_iv[4], byte0[2], byte0[0]);
  and and_19 (and_19_out, byte0_iv[3], byte0_iv[2], byte0[1], byte0_iv[0]);
  and and_20 (and_20_out, byte0_iv[3], byte0[2], byte0_iv[1], byte0[0]);
  and and_21 (and_21_out, byte0_iv[4], byte0[3], byte0[2], byte0[1]);
  and and_22 (and_22_out, byte0[4], byte0_iv[3], byte0_iv[2], byte0[1], byte0[0]);
  and and_23 (and_23_out[7], byte0_iv[4], byte0[3], byte0[2]);
  and and_24 (and_24_out, byte0[4], byte0[2], byte0_iv[1]);
  and and_25 (and_25_out, byte0[4], byte0_iv[3], byte0_iv[2]);
  and and_26 (and_26_out, byte0_iv[4], byte0_iv[3], byte0_iv[2]);
  and and_27 (and_27_out, byte0_iv[4], byte0_iv[3]);
  and and_28 (and_28_out, byte0[3], byte0_iv[2], byte0_iv[1]);
  and and_29 (and_29_out, byte0_iv[4], byte0[3], byte0_iv[2]);
  and and_30 (and_30_out, byte0[4], byte0[2], byte0[1], byte0[0]);
  and and_31 (and_31_out, byte0_iv[4], byte0_iv[3], byte0[2], byte0_iv[1]);
  and and_32 (and_32_out, byte0[4], byte0[2], byte0[1], byte0_iv[0]);
  and and_33 (and_33_out, byte0_iv[4], byte0_iv[3], byte0_iv[2], byte0[1], byte0[0]);
  and and_34 (and_34_out, byte0_iv[2], byte0_iv[0]);
  and and_35 (and_35_out, byte0[2], byte0[0]);
  nand nand_3 (nand_3_out, byte0[1], byte0[2], byte0_iv[3], byte0[4]);
  Multiplexer #(.Bits(32)) multiplexer_3 (
    .sel(CT_BUS__DAM), .in_0(ALU_R), .in_1(sub_4c32_1_s), .out(multiplexer_3_out));
  or or_12 (and_23_out[10], and_17_out, and_18_out, and_19_out, and_20_out);
  or or_13 (and_23_out[6], and_24_out, and_21_out, and_22_out);
  or or_14 (and_23_out[5], and_23_out[7], and_24_out, and_25_out);
  or or_15 (and_23_out[4], and_31_out, and_32_out, and_26_out);
  or or_16 (and_23_out[3], and_27_out, and_32_out, and_28_out);
  or or_17 (and_23_out[2], and_29_out, and_30_out);
  or or_18 (and_23_out[1], and_31_out, and_32_out, and_33_out);
  or or_19 (and_23_out[0], byte0[3], byte0[1], and_34_out, and_35_out);
  and and_36 (and_36_out, ft_e, CT_BUS__IAR);
  Multiplexer #(.Bits(32)) multiplexer_4 (
    .sel(CT_BUS__IDM), .in_0(I_D__bus), .in_1(32'h72000000), .out(multiplexer_4_out));
  and and_37 (and_37_out, alu_e, CT_BUS__DAR);
  and and_38 (and_38_out, alu_e, CT_BUS__DDR);
  or or_20 (and_39_out[1], CT_RF__PCH, CT_RF__PCR);
  and and_39 (and_39_out[0], ~CT_RF__PCH, CT_RF__PCJ);  // And
  nor nor_7 (nor_7_out, CT_RF__PCR, CT_RF__PCJ);
  add_4c32 add_4c32_1 (.a(PCS), .b(4'b0100), .s(add_4c32_1_s), .c(add_4c32_1_c));
  Register #(.Bits(32)) I_A__R (.D(PCS), .C(C_dt), .en(and_36_out), .Q(I_A__R_q));
  Register #(.Bits(32)) I_D__R (.D(multiplexer_4_out), .C(C_dt), .en(dc_e), .Q(I_D__R_q));
  Register #(.Bits(32)) D_A__R (.D(multiplexer_3_out), .C(C_dt), .en(and_37_out), .Q(D_A__R_q));
  Register #(.Bits(32)) OD_D__R (.D(R_B), .C(C_dt), .en(and_38_out), .Q(OD_D__R_q));
  Multiplexer multiplexer_5 (.sel(ex_nop), .in_0(nand_3_out), .in_1(1'b0), .out(multiplexer_5_out));
  Register register_19 (.D(multiplexer_5_out), .C(C_ct), .en(ex_e__bf), .Q(register_19_q));
  Register register_20 (.D(register_19_q), .C(C_ct), .en(st_e__bf), .Q(register_20_q));
  Multiplexer #(.Selector_Bits(2), .Bits(32)) multiplexer_6 (
    .sel(and_39_out), .in_0(add_4c32_1_s), .in_1(ALU_T__R), .in_2(pca_i), .in_3(D_D__bus), .out(pcs_i));
  and and_40 (fl_i[8], add_4c32_1_c, nor_7_out);
  assign I_A__bus = and_44_out ? I_A__R_q : 32'bz;  // Driver driver_9
  D_FF #(.Bits(32)) INST_3 (.D(I_D__R_q), .C(C_ct), .Q({byte0, byte1, byte2, byte3}), .nQ({byte0_iv, inst_iv}));
  assign D_A__bus = and_45_out ? D_A__R_q : 32'bz;  // Driver driver_10
  assign D_D__bus = and_46_out ? OD_D__R_q : 32'bz;  // Driver driver_11
  Multiplexer #(.Bits(11)) multiplexer_7 (
    .sel(ex_nop), .in_0({and_23_out[10], 2'b00, and_23_out[7:0]}), .in_1({11{1'b0}}), .out(multiplexer_7_out));
  BitExtender #(.inputBits(1), .outputBits(8)) bitextender_3 (.in(register_20_q), .out(bitextender_3_out));
  and and_41 (and_41_out, and_50_out, byte0[1]);
  and and_42 (and_42_out, and_50_out, ~byte0[1]);  // And
  and and_43 (and_43_out[0], byte0[0], byte0[1]);
  or or_21 (and_43_out[1], byte0[0], byte0[1]);
  and and_44 (and_44_out, CT_BUS__IAG, bus_e);
  and and_45 (and_45_out, CT_BUS__DAG, bus_e);
  and and_46 (and_46_out, CT_BUS__DDG, bus_e);
  and and_47 (and_47_out, byte0_iv[7], byte0_iv[6], byte0_iv[5], byte0_iv[4]);
  and and_48 (and_48_out, byte0_iv[7], byte0_iv[6], byte0_iv[5], byte0[4], byte0_iv[3]);
  Multiplexer multiplexer_8 (.sel(ex_nop), .in_0(or_22_out), .in_1(1'b0), .out(multiplexer_8_out));
  Register #(.Bits(11)) register_21 (.D(multiplexer_7_out), .C(C_ct), .en(ex_e__bf), .Q(register_21_q));
  assign and_49_out = byte1_st & bitextender_3_out;  // And and_49, 8 bits wide
  and and_50 (and_50_out, byte0_iv[2], byte0[3], byte0[4], byte0_iv[5], byte0_iv[6], byte0_iv[7]);
  Register #(.Bits(2)) register_22 (.D(and_43_out), .C(C_ct), .en(ex_e__bf), .Q(register_22_q));
  not not_4 (not_4_out, and_23_out[10]);
  nor nor_8 (nor_8_out, byte0[1], byte0[0]);
  Multiplexer multiplexer_9 (.sel(ex_nop), .in_0(and_50_out), .in_1(1'b0), .out(multiplexer_9_out));
  or or_22 (or_22_out, and_47_out, and_48_out);
  assign CT_DEP__STA = or_22_out ? nand_3_out : 1'bz;  // Driver driver_12
  assign CT_DEP__EA = or_22_out ? 1'b1 : 1'bz;  // Driver driver_13
  assign CT_DEP__EB = or_22_out ? not_4_out : 1'bz;  // Driver driver_14
  assign CT_DEP__EOA = or_22_out ? 1'b1 : 1'bz;  // Driver driver_15
  assign {CT_DEP__URA, CT_DEP__UMA} = or_22_out ? byte1 : 8'bz;  // Driver driver_16
  assign {CT_DEP__URB, CT_DEP__UMB} = or_22_out ? byte2 : 8'bz;  // Driver driver_17
  assign {CT_DEP__ORA, CT_DEP__OMA} = or_22_out ? byte1 : 8'bz;  // Driver driver_18
  assign CT_DEP__OFL = or_22_out ? 3'b001 : 3'bz;  // Driver driver_19
  assign CT_DEP__OFLS = or_22_out ? 1'b1 : 1'bz;  // Driver driver_20
  assign CT_DEP__OFLE = or_22_out ? 1'b1 : 1'bz;  // Driver driver_21
  Register register_23 (.D(multiplexer_8_out), .C(C_ct), .en(ex_e__bf), .Q(register_23_q));
  assign {CT_RF__RA, CT_RF__MA} = register_23_q ? byte1_ex : 8'bz;  // Driver driver_22
  assign {CT_RF__RB, CT_RF__MB} = register_23_q ? byte2_ex : 8'bz;  // Driver driver_23
  assign CT_ALU__A = register_23_q ? register_21_q[8:0] : 9'bz;  // Driver driver_24
  assign CT_ALU__M = register_23_q ? register_21_q[10:9] : 2'bz;  // Driver driver_25
  assign CT_DEP__STB = register_23_q ? register_19_q : 1'bz;  // Driver driver_26
  assign {CT_DEP__ORB, CT_DEP__OMB} = register_23_q ? byte1_ex : 8'bz;  // Driver driver_27
  assign CT_DEP__OFLS = register_23_q ? 1'b1 : 1'bz;  // Driver driver_28
  assign CT_DEP__OFLE = register_23_q ? 1'b1 : 1'bz;  // Driver driver_29
  Register register_24 (.D(register_23_q), .C(C_ct), .en(st_e__bf), .Q(register_24_q));
  assign {CT_RF__WS, CT_RF__WM} = register_24_q ? and_49_out : 8'bz;  // Driver driver_30
  assign CT_RF__E = register_24_q ? register_20_q : 1'bz;  // Driver driver_31
  assign CT_RF__FLS = register_24_q ? 1'b1 : 1'bz;  // Driver driver_32
  assign CT_RF__FLE = register_24_q ? 4'b0001 : 4'bz;  // Driver driver_33
  assign CT_DEP__STA = and_50_out ? 1'b1 : 1'bz;  // Driver driver_34
  assign CT_DEP__EA = and_50_out ? nor_8_out : 1'bz;  // Driver driver_35
  assign CT_DEP__EOA = and_50_out ? 1'b1 : 1'bz;  // Driver driver_36
  assign {CT_DEP__URA, CT_DEP__UMA} = and_50_out ? byte2 : 8'bz;  // Driver driver_37
  assign CT_DEP__OMA = and_41_out ? 3'b000 : 3'bz;  // Driver driver_38
  assign CT_DEP__OMA = and_42_out ? byte1[2:0] : 3'bz;  // Driver driver_39
  assign CT_DEP__ORA = and_50_out ? byte1[7:3] : 5'bz;  // Driver driver_40
  Register register_25 (.D(multiplexer_9_out), .C(C_ct), .en(ex_e__bf), .Q(register_25_q));
  assign CT_ALU__M = register_25_q ? register_22_q : 2'bz;  // Driver driver_41
  assign {CT_RF__RA, CT_RF__MA} = register_25_q ? 8'hd0 : 8'bz;  // Driver driver_42
  assign {CT_RF__RB, CT_RF__MB} = register_25_q ? byte2_ex : 8'bz;  // Driver driver_43
  assign CT_ALU__A = register_25_q ? 9'h9 : 9'bz;  // Driver driver_44
  assign CT_DEP__STB = register_25_q ? 1'b1 : 1'bz;  // Driver driver_45
  assign {CT_DEP__ORB, CT_DEP__OMB} = register_25_q ? byte1_ex : 8'bz;  // Driver driver_46
  Register register_26 (.D(register_25_q), .C(C_ct), .en(st_e__bf), .Q(register_26_q));
  assign {CT_RF__WS, CT_RF__WM} = register_26_q ? byte1_st : 8'bz;  // Driver driver_47
  assign CT_RF__E = register_26_q ? 1'b1 : 1'bz;  // Driver driver_48
  and and_51 (and_51_out, rf_e, CT_RF__E);
  Multiplexer #(.Bits(32)) multiplexer_10 (.sel(CT_RF__DM), .in_0(ALU_T__R), .in_1(D_D__bus), .out(multiplexer_10_out));
  // regFile2 regfile2_1: pin names not known; wires that end beside it: C_dt, and_51_out, multiplexer_10_out, CT_RF__WS, CT_RF__WM, CT_RF__RA, CT_RF__MA, CT_RF__RB, CT_RF__MB, {32{1'b0}}, 1'b0, 4'b0000, 4'b0000, pca_i, CT_RF__PCAE, pcs_i, CT_RF__PCSE, sc_i, CT_RF__SCS, CT_RF__SCE, CT_RF__SCDE, {FL[31:10], fl_i, ALU_T__F}, CT_RF__FLS, CT_RF__FLE, CT_RF__FLDE, CT_DEP__EA, CT_DEP__URA, CT_DEP__UMA, CT_DEP__EB, CT_DEP__URB, CT_DEP__UMB, regfile2_1_p32, CT_RF__DES, CT_RF__DEM, regfile2_1_p35, R_A, R_B, PCA, PCS, SC, FL, regfile2_1_p35
  not not_5 (not_5_out, byte1_ex[1]);
  or or_23 (or_23_out, byte1_ex[2], byte1_ex[0]);
  and and_52 (and_53_out[2], byte0_iv[7], byte0_iv[6], byte0[5]);
  and and_53 (and_53_out[1], byte0_iv[7], byte0[6], byte0_iv[5]);
  or or_24 (or_24_out, byte1_ex[0], byte1_ex[2]);
  and and_54 (and_54_out[1], not_5_out, or_23_out);
  nor nor_9 (and_54_out[2], byte1_ex[2], byte1_ex[1], byte1_ex[0]);
  not not_6 (not_6_out, byte1_ex[1]);
  and and_55 (regfile2_1_p32, alu_e, CT_RF__DE);
  not not_7 (not_7_out, byte0[0]);
  and and_56 (and_56_out[0], byte0[1], byte0[2], byte0[3], byte0[4], byte0_iv[5], byte0_iv[6], byte0_iv[7]);
  Register #(.Bits(3)) register_27 (.D({and_54_out, byte1_ex[1]}), .C(C_ct), .en(st_e__bf), .Q(register_27_q));
  or or_25 (and_53_out[0], and_53_out[2], and_53_out[1]);
  Register #(.Bits(8)) register_28 (.D({byte0[4:0], 3'b000}), .C(C_ct), .en(ex_e__bf), .Q(register_28_q));
  and and_57 (and_57_out[0], or_24_out, not_6_out);
  and and_58 (and_56_out[1], and_56_out[0], byte0[0]);
  and and_59 (and_56_out[2], not_7_out, and_56_out[0]);
  Multiplexer #(.Bits(3)) multiplexer_11 (.sel(ex_nop), .in_0(and_56_out), .in_1(3'b000), .out(multiplexer_11_out));
  Multiplexer #(.Bits(3)) multiplexer_12 (.sel(ex_nop), .in_0(and_53_out), .in_1(3'b000), .out(multiplexer_12_out));
  assign CT_DEP__EA = and_56_out[0] ? 1'b1 : 1'bz;  // Driver driver_49
  assign CT_DEP__EOA = and_56_out[0] ? 1'b1 : 1'bz;  // Driver driver_50
  assign {CT_DEP__ORA, CT_DEP__OMA} = and_56_out[0] ? byte1 : 8'bz;  // Driver driver_51
  assign {CT_DEP__URA, CT_DEP__UMA} = and_56_out[0] ? 8'hf0 : 8'bz;  // Driver driver_52
  assign CT_DEP__STA = and_56_out[2] ? 1'b1 : 1'bz;  // Driver driver_53
  assign CT_DEP__EB = and_56_out[1] ? 1'b1 : 1'bz;  // Driver driver_54
  assign {CT_DEP__URB, CT_DEP__UMB} = and_56_out[1] ? byte1 : 8'bz;  // Driver driver_55
  Register #(.Bits(3)) register_29 (.D(multiplexer_11_out), .C(C_ct), .en(ex_e__bf), .Q(register_29_q));
  assign CT_BUS__DAM = register_29_q[0] ? 1'b1 : 1'bz;  // Driver driver_56
  assign CT_BUS__DAR = register_29_q[0] ? 1'b1 : 1'bz;  // Driver driver_57
  assign {CT_RF__RB, CT_RF__MB} = register_29_q[1] ? byte1_ex : 8'bz;  // Driver driver_58
  assign CT_BUS__DDR = register_29_q[1] ? 1'b1 : 1'bz;  // Driver driver_59
  assign CT_DEP__STB = register_29_q[2] ? 1'b1 : 1'bz;  // Driver driver_60
  assign {CT_DEP__ORB, CT_DEP__OMB} = register_29_q[2] ? byte1_ex : 8'bz;  // Driver driver_61
  assign CT_BUS__DASDN = register_29_q[2] ? {and_54_out, byte1_ex[1]} : 3'bz;  // Driver driver_62
  Register #(.Bits(3)) register_30 (.D(register_29_q), .C(C_ct), .en(st_e__bf), .Q(register_30_q));
  assign CT_BUS__DAG = register_30_q[0] ? 1'b1 : 1'bz;  // Driver driver_63
  assign CT_RF__SCE = register_30_q[0] ? 1'b1 : 1'bz;  // Driver driver_64
  assign CT_RF__SCS = register_30_q[0] ? 1'b1 : 1'bz;  // Driver driver_65
  assign D_ST = register_30_q[1] ? 1'b1 : 1'bz;  // Driver driver_66
  assign CT_RF__SCN = register_30_q[1] ? register_27_q : 3'bz;  // Driver driver_67
  assign CT_BUS__DDG = register_30_q[1] ? 1'b1 : 1'bz;  // Driver driver_68
  assign D_LD = register_30_q[2] ? 1'b1 : 1'bz;  // Driver driver_69
  assign CT_RF__SCD = register_30_q[2] ? 1'b1 : 1'bz;  // Driver driver_70
  assign CT_RF__SCN = register_30_q[2] ? register_27_q : 3'bz;  // Driver driver_71
  assign CT_RF__DM = register_30_q[2] ? 1'b1 : 1'bz;  // Driver driver_72
  assign {CT_RF__WS, CT_RF__WM} = register_30_q[2] ? byte1_st : 8'bz;  // Driver driver_73
  assign CT_RF__E = register_30_q[2] ? 1'b1 : 1'bz;  // Driver driver_74
  assign CT_DEP__EA = and_53_out[0] ? 1'b1 : 1'bz;  // Driver driver_75
  assign {CT_DEP__URA, CT_DEP__UMA} = and_53_out[0] ? {byte0[4:0], 3'b000} : 8'bz;  // Driver driver_76
  assign CT_DEP__EB = and_53_out[1] ? 1'b1 : 1'bz;  // Driver driver_77
  assign {CT_DEP__URB, CT_DEP__UMB} = and_53_out[1] ? byte1 : 8'bz;  // Driver driver_78
  assign CT_DEP__STA = and_53_out[2] ? 1'b1 : 1'bz;  // Driver driver_79
  assign CT_DEP__EOA = and_53_out[2] ? 1'b1 : 1'bz;  // Driver driver_80
  assign {CT_DEP__ORA, CT_DEP__OMA} = and_53_out[2] ? byte1 : 8'bz;  // Driver driver_81
  assign D_MD = register_32_q[0] ? {byte1_ex[1], and_57_out[0]} : 2'bz;  // Driver driver_82
  assign {CT_RF__RA, CT_RF__MA} = register_32_q[0] ? register_28_q : 8'bz;  // Driver driver_83
  assign CT_ALU__A = register_32_q[0] ? 9'h19 : 9'bz;  // Driver driver_84
  assign CT_ALU__M = register_32_q[0] ? 2'b10 : 2'bz;  // Driver driver_85
  assign CT_BUS__DAR = register_32_q[0] ? 1'b1 : 1'bz;  // Driver driver_86
  assign {CT_RF__RB, CT_RF__MB} = register_32_q[1] ? byte1_ex : 8'bz;  // Driver driver_87
  assign CT_BUS__DDR = register_32_q[1] ? 1'b1 : 1'bz;  // Driver driver_88
  assign CT_DEP__STB = register_32_q[2] ? 1'b1 : 1'bz;  // Driver driver_89
  assign {CT_DEP__ORB, CT_DEP__OMB} = register_32_q[2] ? byte1_ex : 8'bz;  // Driver driver_90
  Register #(.Bits(3)) register_31 (.D(register_32_q), .C(C_ct), .en(st_e__bf), .Q(register_31_q));
  assign CT_BUS__DAG = register_31_q[0] ? 1'b1 : 1'bz;  // Driver driver_91
  assign D_ST = register_31_q[1] ? 1'b1 : 1'bz;  // Driver driver_92
  assign CT_BUS__DDG = register_31_q[1] ? 1'b1 : 1'bz;  // Driver driver_93
  assign D_LD = register_31_q[2] ? 1'b1 : 1'bz;  // Driver driver_94
  assign CT_RF__DM = register_31_q[2] ? 1'b1 : 1'bz;  // Driver driver_95
  assign {CT_RF__WS, CT_RF__WM} = register_31_q[2] ? byte1_st : 8'bz;  // Driver driver_96
  assign CT_RF__E = register_31_q[2] ? 1'b1 : 1'bz;  // Driver driver_97
  BitExtender #(.inputBits(16), .outputBits(32)) bitextender_4 (.in({byte2_ex, byte3_ex}), .out(bitextender_4_out));
  Register #(.Bits(3)) register_32 (.D(multiplexer_12_out), .C(C_ct), .en(ex_e__bf), .Q(register_32_q));
  Multiplexer #(.Selector_Bits(2), .Bits(32)) multiplexer_13 (
    .sel(CT_ALU__M), .in_0(R_B), .in_1({{24{1'b0}}, byte3_ex}), .in_2(bitextender_4_out),
    .in_3({{16{1'b0}}, byte2_ex, byte3_ex}), .out(multiplexer_13_out));
  Register #(.Bits(32)) register_33 (.D(ALU_R), .C(C_dt), .en(alu_e), .Q(ALU_T__R));
  Register #(.Bits(8)) register_34 (.D(ALU_F), .C(C_dt), .en(alu_e), .Q(ALU_T__F));
  // alu_32 alu_32_1: pin names not known; wires that end beside it: R_A, multiplexer_13_out, FL, CT_ALU__A, CT_RF__WM, alu_32_1_p6, alu_32_1_p6, alu_32_1_p8, alu_32_1_p8, alu_32_1_p10, alu_32_1_p10, ALU_R, ALU_F
  BitExtender #(.inputBits(1), .outputBits(8)) bitextender_5 (.in(register_35_q_2[3]), .out(bitextender_5_out));
  PullDown #(.Bits(32)) pulldown_1 (.out(alu_32_1_p10));
  addsub_4c32 addsub_4c32_1 (.a(SC), .b({1'b0, CT_RF__SCN}), .sub(CT_RF__SCD), .s(sc_i), .c(fl_i[9]));
  assign xor_6_out = FL[7:0] ^ bitextender_5_out;  // XOr xor_6, 8 bits wide
  and and_60 (and_60_out, byte0_iv[4], byte0[5], byte0[6], byte0_iv[7]);
  Comparator #(.Bits(3)) comparator_2 (.a(byte0[2:0]), .b(3'b110), .eq(comparator_2_eq));  // open: gt, lt
  Multiplexer #(.Selector_Bits(3)) multiplexer_14 (
    .sel(register_35_q), .in_0(xor_6_out[0]), .in_1(xor_6_out[1]), .in_2(xor_6_out[2]), .in_3(xor_6_out[3]),
    .in_4(xor_6_out[4]), .in_5(xor_6_out[5]), .in_6(xor_6_out[6]), .in_7(xor_6_out[7]),
    .out(multiplexer_14_out));
  Register #(.Bits(4)) register_35 (.D(byte0[3:0]), .C(C_ct), .en(ex_e__bf), .Q({register_35_q_2[3], register_35_q}));
  and and_61 (and_61_out, byte0[0], byte0_iv[1], byte0_iv[2], byte0_iv[3], byte0[4], byte0[5], byte0[6], byte0_iv[7]);
  nand nand_4 (nand_4_out, comparator_2_eq, and_60_out);
  Multiplexer multiplexer_15 (.sel(ex_nop), .in_0(and_60_out), .in_1(1'b0), .out(multiplexer_15_out));
  and and_62 (and_62_out, byte0_iv[0], byte0_iv[1], byte0_iv[2], byte0_iv[3], byte0[4], byte0[5], byte0[6], byte0_iv[7]);
  and and_63 (and_63_out, byte0[0], byte0[1], byte0_iv[2], byte0_iv[3], byte0[4], byte0[5], byte0[6], byte0_iv[7]);
  Multiplexer multiplexer_16 (.sel(ex_nop), .in_0(and_63_out), .in_1(1'b0), .out(multiplexer_16_out));
  PullDown pulldown_2 (.out(kernel_inst));
  PullDown pulldown_3 (.out(CT_RF__E));
  PullDown pulldown_4 (.out(CT_RF__DE));
  PullDown pulldown_5 (.out(CT_RF__DM));
  PullDown #(.Bits(5)) pulldown_6 (.out(CT_RF__WS));
  PullDown #(.Bits(3)) pulldown_7 (.out(CT_RF__WM));
  PullDown #(.Bits(5)) pulldown_8 (.out(CT_RF__DES));
  PullDown #(.Bits(3)) pulldown_9 (.out(CT_RF__DEM));
  PullDown #(.Bits(5)) pulldown_10 (.out(CT_RF__RA));
  PullDown #(.Bits(3)) pulldown_11 (.out(CT_RF__MA));
  PullDown #(.Bits(5)) pulldown_12 (.out(CT_RF__RB));
  PullDown #(.Bits(3)) pulldown_13 (.out(CT_RF__MB));
  PullDown pulldown_14 (.out(CT_RF__PCAE));
  PullDown pulldown_15 (.out(CT_RF__PCSE));
  PullDown pulldown_16 (.out(CT_RF__PCJ));
  PullDown pulldown_17 (.out(CT_RF__PCR));
  PullDown #(.Bits(3)) pulldown_18 (.out(CT_RF__SCN));
  PullDown pulldown_19 (.out(CT_RF__SCD));
  PullDown pulldown_20 (.out(CT_RF__SCS));
  PullDown pulldown_21 (.out(CT_RF__SCE));
  PullDown pulldown_22 (.out(CT_RF__SCDE));
  PullDown pulldown_23 (.out(CT_RF__FLS));
  PullDown #(.Bits(4)) pulldown_24 (.out(CT_RF__FLE));
  PullDown #(.Bits(4)) pulldown_25 (.out(CT_RF__FLDE));
  PullDown #(.Bits(9)) pulldown_26 (.out(CT_ALU__A));
  PullDown #(.Bits(2)) pulldown_27 (.out(CT_ALU__M));
  PullDown pulldown_28 (.out(CT_ALU__M2));
  PullDown pulldown_29 (.out(CT_BUS__IAR));
  PullDown pulldown_30 (.out(CT_BUS__IAG));
  PullDown pulldown_31 (.out(CT_BUS__IDR));
  PullDown pulldown_32 (.out(CT_BUS__IDM));
  PullDown pulldown_33 (.out(CT_BUS__DAR));
  PullDown pulldown_34 (.out(CT_BUS__DAM));
  PullDown pulldown_35 (.out(CT_BUS__DAG));
  PullDown pulldown_36 (.out(CT_BUS__DDR));
  PullDown pulldown_37 (.out(CT_BUS__DDG));
  PullDown pulldown_38 (.out(I_LD));
  PullDown pulldown_39 (.out(D_LD));
  PullDown pulldown_40 (.out(D_ST));
  PullDown #(.Bits(2)) pulldown_41 (.out(D_MD));
  PullDown pulldown_42 (.out(CT_MVR));
  Multiplexer multiplexer_17 (.sel(ex_nop), .in_0(and_62_out), .in_1(1'b0), .out(multiplexer_17_out));
  Multiplexer multiplexer_18 (.sel(ex_nop), .in_0(and_61_out), .in_1(1'b0), .out(multiplexer_18_out));
  assign CT_DEP__EA = and_60_out ? 1'b1 : 1'bz;  // Driver driver_98
  assign {CT_DEP__URA, CT_DEP__UMA} = and_60_out ? byte1 : 8'bz;  // Driver driver_99
  assign CT_DEP__EB = and_60_out ? nand_4_out : 1'bz;  // Driver driver_100
  assign {CT_DEP__URB, CT_DEP__UMB} = and_60_out ? 8'hf8 : 8'bz;  // Driver driver_101
  Register register_36 (.D(multiplexer_15_out), .C(C_ct), .en(ex_e__bf), .Q(register_36_q));
  assign ex_nop = multiplexer_19_out ? 1'b1 : 1'bz;  // Driver driver_102
  assign CT_BUS__IDM = multiplexer_19_out ? 1'b1 : 1'bz;  // Driver driver_103
  assign CT_ALU__A = multiplexer_19_out ? 9'h19 : 9'bz;  // Driver driver_104
  assign CT_ALU__M = multiplexer_19_out ? 2'b10 : 2'bz;  // Driver driver_105
  assign {CT_RF__RA, CT_RF__MA} = multiplexer_19_out ? byte1_ex : 8'bz;  // Driver driver_106
  Register register_37 (.D(multiplexer_19_out), .C(C_ct), .en(st_e__bf), .Q(register_37_q));
  assign CT_RF__PCSE = register_37_q ? 1'b1 : 1'bz;  // Driver driver_107
  assign CT_RF__PCJ = register_37_q ? 1'b1 : 1'bz;  // Driver driver_108
  assign CT_BUS__IDM = register_37_q ? 1'b1 : 1'bz;  // Driver driver_109
  Register register_38 (.D(register_37_q), .C(C_ct), .en(ext_e__bf), .Q(register_38_q));
  assign CT_BUS__IDM = register_38_q ? 1'b1 : 1'bz;  // Driver driver_110
  assign CT_DEP__EA = and_62_out ? 1'b1 : 1'bz;  // Driver driver_111
  assign {CT_DEP__URA, CT_DEP__UMA} = and_62_out ? byte1 : 8'bz;  // Driver driver_112
  Register register_39 (.D(multiplexer_17_out), .C(C_ct), .en(ex_e__bf), .Q(register_39_q));
  assign ex_nop = register_39_q ? 1'b1 : 1'bz;  // Driver driver_113
  assign CT_BUS__IDM = register_39_q ? 1'b1 : 1'bz;  // Driver driver_114
  assign {CT_RF__RA, CT_RF__MA} = register_39_q ? byte1_ex : 8'bz;  // Driver driver_115
  assign CT_ALU__A = register_39_q ? 9'h19 : 9'bz;  // Driver driver_116
  assign CT_ALU__M = register_39_q ? 2'b10 : 2'bz;  // Driver driver_117
  assign {CT_RF__RB, CT_RF__MB} = register_39_q ? 8'he8 : 8'bz;  // Driver driver_118
  assign CT_BUS__DAM = register_39_q ? 1'b1 : 1'bz;  // Driver driver_119
  assign CT_BUS__DAR = register_39_q ? 1'b1 : 1'bz;  // Driver driver_120
  assign CT_BUS__DDR = register_39_q ? 1'b1 : 1'bz;  // Driver driver_121
  Register register_40 (.D(register_39_q), .C(C_ct), .en(st_e__bf), .Q(register_40_q));
  assign CT_BUS__IDM = register_40_q ? 1'b1 : 1'bz;  // Driver driver_122
  assign CT_RF__SCE = register_40_q ? 1'b1 : 1'bz;  // Driver driver_123
  assign CT_RF__SCS = register_40_q ? 1'b1 : 1'bz;  // Driver driver_124
  assign CT_RF__SCN = register_40_q ? 3'b100 : 3'bz;  // Driver driver_125
  assign CT_RF__PCSE = register_40_q ? 1'b1 : 1'bz;  // Driver driver_126
  assign CT_RF__PCJ = register_40_q ? 1'b1 : 1'bz;  // Driver driver_127
  assign CT_BUS__DAG = register_40_q ? 1'b1 : 1'bz;  // Driver driver_128
  assign CT_BUS__DDG = register_40_q ? 1'b1 : 1'bz;  // Driver driver_129
  assign D_ST = register_40_q ? 1'b1 : 1'bz;  // Driver driver_130
  Register register_41 (.D(register_40_q), .C(C_ct), .en(ext_e__bf), .Q(register_41_q));
  assign CT_BUS__IDM = register_41_q ? 1'b1 : 1'bz;  // Driver driver_131
  Register register_42 (.D(multiplexer_18_out), .C(C_ct), .en(ex_e__bf), .Q(register_42_q));
  assign ex_nop = register_42_q ? 1'b1 : 1'bz;  // Driver driver_132
  assign CT_BUS__IDM = register_42_q ? 1'b1 : 1'bz;  // Driver driver_133
  assign CT_BUS__DAM = register_42_q ? 1'b1 : 1'bz;  // Driver driver_134
  assign CT_BUS__DAR = register_42_q ? 1'b1 : 1'bz;  // Driver driver_135
  assign CT_BUS__DASDN = register_42_q ? 3'b100 : 3'bz;  // Driver driver_136
  Register register_43 (.D(register_42_q), .C(C_ct), .en(st_e__bf), .Q(register_43_q));
  assign CT_BUS__IDM = register_43_q ? 1'b1 : 1'bz;  // Driver driver_137
  assign D_LD = register_43_q ? 1'b1 : 1'bz;  // Driver driver_138
  assign CT_RF__SCE = register_43_q ? 1'b1 : 1'bz;  // Driver driver_139
  assign CT_RF__SCD = register_43_q ? 1'b1 : 1'bz;  // Driver driver_140
  assign CT_RF__SCN = register_43_q ? 3'b100 : 3'bz;  // Driver driver_141
  assign CT_RF__SCS = register_43_q ? 1'b1 : 1'bz;  // Driver driver_142
  assign CT_RF__PCSE = register_43_q ? 1'b1 : 1'bz;  // Driver driver_143
  assign CT_RF__PCJ = register_43_q ? 1'b1 : 1'bz;  // Driver driver_144
  assign CT_RF__PCR = register_43_q ? 1'b1 : 1'bz;  // Driver driver_145
  assign CT_BUS__DAG = register_43_q ? 1'b1 : 1'bz;  // Driver driver_146
  Register register_44 (.D(register_43_q), .C(C_ct), .en(ext_e__bf), .Q(register_44_q));
  assign CT_BUS__IDM = register_44_q ? 1'b1 : 1'bz;  // Driver driver_147
  Register register_45 (.D(multiplexer_16_out), .C(C_ct), .en(ex_e__bf), .Q(register_45_q));
  assign ex_nop = register_45_q ? 1'b1 : 1'bz;  // Driver driver_148
  assign hlt = register_45_q ? 1'b1 : 1'bz;  // Driver driver_149
  assign CT_BUS__IDM = register_45_q ? 1'b1 : 1'bz;  // Driver driver_150
  assign CT_BUS__IDM = register_45_q ? 1'b1 : 1'bz;  // Driver driver_151
  Register register_46 (.D(register_45_q), .C(C_ct), .en(st_e__bf), .Q(register_46_q));
  assign CT_RF__PCH = register_46_q ? 1'b1 : 1'bz;  // Driver driver_152
  assign CT_RF__PCSE = register_46_q ? 1'b1 : 1'bz;  // Driver driver_153
  assign CT_BUS__IDM = register_46_q ? 1'b1 : 1'bz;  // Driver driver_154
  Multiplexer multiplexer_19 (.sel(multiplexer_14_out), .in_0(1'b0), .in_1(register_36_q), .out(multiplexer_19_out));
  PullDown pulldown_43 (.out(CT_DEP__STA));
  PullDown pulldown_44 (.out(CT_DEP__STB));
  PullDown pulldown_45 (.out(CT_DEP__EA));
  PullDown pulldown_46 (.out(CT_DEP__EB));
  PullDown pulldown_47 (.out(CT_DEP__EOA));
  PullDown #(.Bits(5)) pulldown_48 (.out(CT_DEP__URA));
  PullDown #(.Bits(3)) pulldown_49 (.out(CT_DEP__UMA));
  PullDown #(.Bits(5)) pulldown_50 (.out(CT_DEP__URB));
  PullDown #(.Bits(3)) pulldown_51 (.out(CT_DEP__UMB));
  PullDown #(.Bits(5)) pulldown_52 (.out(CT_DEP__ORA));
  PullDown #(.Bits(3)) pulldown_53 (.out(CT_DEP__OMA));
  PullDown #(.Bits(5)) pulldown_54 (.out(CT_DEP__ORB));
  PullDown #(.Bits(3)) pulldown_55 (.out(CT_DEP__OSC));
  PullDown pulldown_56 (.out(CT_DEP__OSCS));
  PullDown pulldown_57 (.out(CT_DEP__OSCE));
  PullDown #(.Bits(3)) pulldown_58 (.out(CT_DEP__OFL));
  PullDown pulldown_59 (.out(CT_DEP__OFLS));
  PullDown pulldown_60 (.out(CT_DEP__OFLE));
  PullDown #(.Bits(3)) pulldown_61 (.out(CT_BUS__DASDN));
  PullDown pulldown_62 (.out(CT_BUS__DDM));
  PullDown pulldown_63 (.out(CT_RF__PCH));
  PullDown pulldown_64 (.out(hlt));
  PullDown pulldown_65 (.out(ex_nop));

  assign CLK_str = 1'b0;
  assign CSH_mode = 2'b00;
  assign CSH_run = 1'b0;
  assign DMA_sel = 3'b000;
  assign DMA_str = 1'b0;
  assign INT_out = 1'b0;
  assign INT_str = 1'b0;
  assign MMU_sel = 2'b00;
  assign MMU_str = 1'b0;

  // Other names for the same wires on the sheet: fl_i (some bits) = {FL[31:10], ALU_T__F};
  //   imm16_2_ex[15:0] = {byte2_ex, byte3_ex}; C_i = C_dt; ex_e = alu_e; int_proc = FL[14]; trap = FL[15];
  //   inst[31:0] = {byte0, byte1, byte2, byte3}; inst_iv[31:24] = byte0_iv; pc_ov = fl_i[8]; PCS_d3[31:0] = pca_i;
  //   sc_ov = fl_i[9]; st_e = rf_e

  // Notes on the sheet:
  //   C: Hz: 64
  //   bus_e: default 1
  //   D_MD: 0:32
  //   1:16
  //   2:8
  //   3:u.u
  //   I_valid: default 1
  //   D_valid: default 1
  //   pipeline controller
  //   dependence circuit
  //   kernal mode system
  //   interrupt system
  //   tests
  //   IO pins
  //   primeary signals
  //   halt controller
  //   decode circuit
  //   ALU
  //   register
  //   program counter controller
  //   bus system
  //   register system
  //   stack
  //   RAM
  //   interrupt
  //   ALU system
  //   flag circuit
  //   stack circuit
  //   jump
  //   call
  //   return
  //   halt
  //   control bus
endmodule
