// Digital circuit fill-8.dig as structural Verilog
module fill_8 (
  input  in1,
  input  in2,
  input  in3,
  input  in4,
  input  in5,
  input  in6,
  input  in7,
  input  in8,
  input  on,
  output out1,
  output out2,
  output out3,
  output out4,
  output out5,
  output out6,
  output out7,
  output out8,
  output v
);

  or or_1 (out8, in8, on);
  or or_2 (out7, in7, on, in8);
  or or_3 (out6, in6, in7, on, in8);
  or or_4 (out5, in5, in6, on, in7, in8);
  or or_5 (out4, in4, in5, in6, on, in7, in8);
  or or_6 (out3, in3, in4, in5, on, in6, in7, in8);
  or or_7 (out2, in2, in3, in4, in5, on, in6, in7, in8);
  or or_8 (out1, in1, in2, in3, in4, on, in5, in6, in7, in8);
  or or_9 (v, in1, in2, in3, in4, in5, in6, in7, in8);
endmodule
