// Digital circuit history-queue-3s.dig as structural Verilog
module history_queue_3s (
  input  C,
  input  [4:0] S1,
  input  [4:0] S2,
  input  [4:0] S3,
  input  res,
  input  [4:0] R,
  input  [31:0] D,
  input  E,
  input  P1,
  input  P2,
  input  P3,
  output [31:0] D1,
  output [31:0] D2,
  output [31:0] D3
);

  wire and_4_out, and_5_out, and_6_out, and_8_out, and_14_out, and_18_out, and_24_out, and_29_out,
       and_34_out, and_38_out, and_44_out, and_49_out, and_54_out, and_58_out, and_64_out, and_69_out,
       and_74_out, and_78_out, and_84_out, comparator_1_eq, comparator_2_eq, comparator_3_eq,
       comparator_4_eq, comparator_5_eq, comparator_6_eq, comparator_7_eq, comparator_8_eq, comparator_9_eq,
       comparator_10_eq, comparator_11_eq, comparator_12_eq, comparator_13_eq, comparator_14_eq,
       comparator_15_eq, comparator_16_eq, comparator_17_eq, comparator_18_eq, comparator_19_eq,
       comparator_20_eq, comparator_21_eq, comparator_22_eq, comparator_23_eq, comparator_24_eq,
       comparator_25_eq, comparator_26_eq, comparator_27_eq, comparator_28_eq, comparator_29_eq,
       comparator_30_eq, comparator_31_eq, comparator_32_eq, comparator_33_eq, comparator_34_eq,
       comparator_35_eq, comparator_36_eq, comparator_37_eq, comparator_38_eq, comparator_39_eq,
       comparator_40_eq, comparator_41_eq, comparator_42_eq, comparator_43_eq, comparator_44_eq,
       comparator_45_eq, comparator_46_eq, comparator_47_eq, comparator_48_eq, or_2_out, res_t, V1, V2, V3,
       valid_2_q, valid_3_q, valid_4_q, valid_5_q, valid_6_q, valid_7_q, valid_8_q, valid_9_q, valid_10_q,
       valid_11_q, valid_12_q, valid_13_q, valid_14_q, valid_15_q, valid_16_q, valid_q;
  wire [3:0] priorityencoder_1_num, priorityencoder_2_num, priorityencoder_3_num;
  wire [4:0] id_2_q, id_3_q, id_4_q, id_5_q, id_6_q, id_7_q, id_8_q, id_9_q, id_10_q, id_11_q, id_12_q,
       id_13_q, id_14_q, id_15_q, id_16_q, id_q;
  wire [15:0] and_1_out, and_2_out, and_3_out, and_9_out, and_10_out, and_11_out, and_12_out,
       bitextender_1_out, bitextender_2_out, bitextender_3_out, bitextender_6_out, fill_16_1_out1, not_2_out,
       not_3_out, or_1_out, priority_16_1_out1;
  wire [31:0] and_7_out, and_13_out, and_19_out, and_23_out, and_28_out, and_33_out, and_39_out, and_43_out,
       and_48_out, and_53_out, and_59_out, and_63_out, and_68_out, and_73_out, and_79_out, and_83_out,
       bitextender_4_out, bitextender_5_out, bitextender_7_out, bitextender_8_out, bitextender_9_out,
       bitextender_10_out, bitextender_11_out, bitextender_12_out, bitextender_13_out, bitextender_14_out,
       bitextender_15_out, bitextender_16_out, bitextender_17_out, bitextender_18_out, bitextender_19_out,
       bitextender_20_out, data_2_q, data_3_q, data_4_q, data_5_q, data_6_q, data_7_q, data_8_q, data_9_q,
       data_10_q, data_11_q, data_12_q, data_13_q, data_14_q, data_15_q, data_16_q, data_q;

  not not_1 (res_t, res);
  BitExtender #(.inputBits(1)) bitextender_1 (.in(P1), .out(bitextender_1_out));
  BitExtender #(.inputBits(1)) bitextender_2 (.in(P2), .out(bitextender_2_out));
  assign and_1_out = and_10_out & bitextender_1_out;  // And and_1, 16 bits wide
  BitExtender #(.inputBits(1)) bitextender_3 (.in(P3), .out(bitextender_3_out));
  assign and_2_out = and_11_out & bitextender_2_out;  // And and_2, 16 bits wide
  assign or_1_out = and_3_out | and_2_out | and_1_out;  // Or or_1, 16 bits wide
  assign and_3_out = and_12_out & bitextender_3_out;  // And and_3, 16 bits wide
  priority_16 priority_16_1 (
    .in1(or_1_out[0]), .in2(or_1_out[1]), .in3(or_1_out[2]), .in4(or_1_out[3]), .in5(or_1_out[4]),
    .in6(or_1_out[5]), .in7(or_1_out[6]), .in8(or_1_out[7]), .in9(or_1_out[8]), .in10(or_1_out[9]),
    .in11(or_1_out[10]), .in12(or_1_out[11]), .in13(or_1_out[12]), .in14(or_1_out[13]), .in15(or_1_out[14]),
    .in16(or_1_out[15]), .out1(priority_16_1_out1[0]), .out2(priority_16_1_out1[1]),
    .out3(priority_16_1_out1[2]), .out4(priority_16_1_out1[3]), .out5(priority_16_1_out1[4]),
    .out6(priority_16_1_out1[5]), .out7(priority_16_1_out1[6]), .out8(priority_16_1_out1[7]),
    .out9(priority_16_1_out1[8]), .out10(priority_16_1_out1[9]), .out11(priority_16_1_out1[10]),
    .out12(priority_16_1_out1[11]), .out13(priority_16_1_out1[12]), .out14(priority_16_1_out1[13]),
    .out15(priority_16_1_out1[14]), .out16(priority_16_1_out1[15]));  // open: v
  assign not_2_out = ~priority_16_1_out1;  // Not not_2, 16 bits wide
  fill_16 fill_16_1 (
    .in1(or_1_out[0]), .in2(or_1_out[1]), .in3(or_1_out[2]), .in4(or_1_out[3]), .in5(or_1_out[4]),
    .in6(or_1_out[5]), .in7(or_1_out[6]), .in8(or_1_out[7]), .in9(or_1_out[8]), .in10(or_1_out[9]),
    .in11(or_1_out[10]), .in12(or_1_out[11]), .in13(or_1_out[12]), .in14(or_1_out[13]), .in15(or_1_out[14]),
    .in16(or_1_out[15]), .out1(fill_16_1_out1[0]), .out2(fill_16_1_out1[1]), .out3(fill_16_1_out1[2]),
    .out4(fill_16_1_out1[3]), .out5(fill_16_1_out1[4]), .out6(fill_16_1_out1[5]), .out7(fill_16_1_out1[6]),
    .out8(fill_16_1_out1[7]), .out9(fill_16_1_out1[8]), .out10(fill_16_1_out1[9]),
    .out11(fill_16_1_out1[10]), .out12(fill_16_1_out1[11]), .out13(fill_16_1_out1[12]),
    .out14(fill_16_1_out1[13]), .out15(fill_16_1_out1[14]), .out16(fill_16_1_out1[15]));
  assign not_3_out = ~fill_16_1_out1;  // Not not_3, 16 bits wide
  and and_4 (and_4_out, V1, P1);
  and and_5 (and_5_out, V2, P2);
  and and_6 (and_6_out, V3, P3);
  assign and_7_out = bitextender_4_out & D;  // And and_7, 32 bits wide
  BitExtender #(.inputBits(1), .outputBits(32)) bitextender_4 (.in(not_2_out[0]), .out(bitextender_4_out));
  or or_2 (or_2_out, E, and_4_out, and_5_out, and_6_out);
  PriorityEncoder #(.Selector_Bits(4)) priorityencoder_1 (
    .in0(and_10_out[0]), .in1(and_10_out[1]), .in2(and_10_out[2]), .in3(and_10_out[3]), .in4(and_10_out[4]),
    .in5(and_10_out[5]), .in6(and_10_out[6]), .in7(and_10_out[7]), .in8(and_10_out[8]), .in9(and_10_out[9]),
    .in10(and_10_out[10]), .in11(and_10_out[11]), .in12(and_10_out[12]), .in13(and_10_out[13]),
    .in14(and_10_out[14]), .in15(and_10_out[15]), .num(priorityencoder_1_num), .any(V1));
  PriorityEncoder #(.Selector_Bits(4)) priorityencoder_2 (
    .in0(and_11_out[0]), .in1(and_11_out[1]), .in2(and_11_out[2]), .in3(and_11_out[3]), .in4(and_11_out[4]),
    .in5(and_11_out[5]), .in6(and_11_out[6]), .in7(and_11_out[7]), .in8(and_11_out[8]), .in9(and_11_out[9]),
    .in10(and_11_out[10]), .in11(and_11_out[11]), .in12(and_11_out[12]), .in13(and_11_out[13]),
    .in14(and_11_out[14]), .in15(and_11_out[15]), .num(priorityencoder_2_num), .any(V2));
  PriorityEncoder #(.Selector_Bits(4)) priorityencoder_3 (
    .in0(and_12_out[0]), .in1(and_12_out[1]), .in2(and_12_out[2]), .in3(and_12_out[3]), .in4(and_12_out[4]),
    .in5(and_12_out[5]), .in6(and_12_out[6]), .in7(and_12_out[7]), .in8(and_12_out[8]), .in9(and_12_out[9]),
    .in10(and_12_out[10]), .in11(and_12_out[11]), .in12(and_12_out[12]), .in13(and_12_out[13]),
    .in14(and_12_out[14]), .in15(and_12_out[15]), .num(priorityencoder_3_num), .any(V3));
  Comparator #(.Bits(5)) comparator_1 (.a(S1), .b(id_q), .eq(comparator_1_eq));  // open: gt, lt
  Comparator #(.Bits(5)) comparator_2 (.a(S2), .b(id_q), .eq(comparator_2_eq));  // open: gt, lt
  Comparator #(.Bits(5)) comparator_3 (.a(S3), .b(id_q), .eq(comparator_3_eq));  // open: gt, lt
  and and_8 (and_8_out, E, not_2_out[0], res_t);
  Register valid (.D(and_8_out), .C(C), .en(and_9_out[0]), .Q(valid_q));
  Register #(.Bits(5)) id (.D(R), .C(C), .en(and_9_out[0]), .Q(id_q));
  Register #(.Bits(32)) data (.D(and_7_out), .C(C), .en(and_9_out[0]), .Q(data_q));
  assign and_9_out = not_3_out & bitextender_6_out;  // And and_9, 16 bits wide
  and and_10 (and_10_out[0], comparator_1_eq, valid_q);
  and and_11 (and_11_out[0], comparator_2_eq, valid_q);
  and and_12 (and_12_out[0], comparator_3_eq, valid_q);
  assign and_13_out = bitextender_5_out & data_q;  // And and_13, 32 bits wide
  BitExtender #(.inputBits(1), .outputBits(32)) bitextender_5 (.in(not_2_out[1]), .out(bitextender_5_out));
  BitExtender #(.inputBits(1)) bitextender_6 (.in(or_2_out), .out(bitextender_6_out));
  Comparator #(.Bits(5)) comparator_4 (.a(S1), .b(id_2_q), .eq(comparator_4_eq));  // open: gt, lt
  Comparator #(.Bits(5)) comparator_5 (.a(S2), .b(id_2_q), .eq(comparator_5_eq));  // open: gt, lt
  Comparator #(.Bits(5)) comparator_6 (.a(S3), .b(id_2_q), .eq(comparator_6_eq));  // open: gt, lt
  and and_14 (and_14_out, valid_q, not_2_out[1], res_t);
  Register valid_2 (.D(and_14_out), .C(C), .en(and_9_out[1]), .Q(valid_2_q));
  Register #(.Bits(5)) id_2 (.D(id_q), .C(C), .en(and_9_out[1]), .Q(id_2_q));
  Register #(.Bits(32)) data_2 (.D(and_13_out), .C(C), .en(and_9_out[1]), .Q(data_2_q));
  and and_15 (and_10_out[1], comparator_4_eq, valid_2_q);
  Comparator #(.Bits(5)) comparator_7 (.a(S1), .b(id_3_q), .eq(comparator_7_eq));  // open: gt, lt
  and and_16 (and_11_out[1], comparator_5_eq, valid_2_q);
  Comparator #(.Bits(5)) comparator_8 (.a(S2), .b(id_3_q), .eq(comparator_8_eq));  // open: gt, lt
  and and_17 (and_12_out[1], comparator_6_eq, valid_2_q);
  Comparator #(.Bits(5)) comparator_9 (.a(S3), .b(id_3_q), .eq(comparator_9_eq));  // open: gt, lt
  and and_18 (and_18_out, valid_2_q, not_2_out[2], res_t);
  Register valid_3 (.D(and_18_out), .C(C), .en(and_9_out[2]), .Q(valid_3_q));
  Register #(.Bits(5)) id_3 (.D(id_2_q), .C(C), .en(and_9_out[2]), .Q(id_3_q));
  assign and_19_out = bitextender_7_out & data_2_q;  // And and_19, 32 bits wide
  Register #(.Bits(32)) data_3 (.D(and_19_out), .C(C), .en(and_9_out[2]), .Q(data_3_q));
  BitExtender #(.inputBits(1), .outputBits(32)) bitextender_7 (.in(not_2_out[2]), .out(bitextender_7_out));
  and and_20 (and_10_out[2], comparator_7_eq, valid_3_q);
  and and_21 (and_11_out[2], comparator_8_eq, valid_3_q);
  and and_22 (and_12_out[2], comparator_9_eq, valid_3_q);
  assign and_23_out = bitextender_8_out & data_3_q;  // And and_23, 32 bits wide
  Comparator #(.Bits(5)) comparator_10 (.a(S1), .b(id_4_q), .eq(comparator_10_eq));  // open: gt, lt
  Comparator #(.Bits(5)) comparator_11 (.a(S2), .b(id_4_q), .eq(comparator_11_eq));  // open: gt, lt
  Comparator #(.Bits(5)) comparator_12 (.a(S3), .b(id_4_q), .eq(comparator_12_eq));  // open: gt, lt
  and and_24 (and_24_out, valid_3_q, not_2_out[3], res_t);
  Register valid_4 (.D(and_24_out), .C(C), .en(and_9_out[3]), .Q(valid_4_q));
  Register #(.Bits(5)) id_4 (.D(id_3_q), .C(C), .en(and_9_out[3]), .Q(id_4_q));
  Register #(.Bits(32)) data_4 (.D(and_23_out), .C(C), .en(and_9_out[3]), .Q(data_4_q));
  BitExtender #(.inputBits(1), .outputBits(32)) bitextender_8 (.in(not_2_out[3]), .out(bitextender_8_out));
  and and_25 (and_10_out[3], comparator_10_eq, valid_4_q);
  and and_26 (and_11_out[3], comparator_11_eq, valid_4_q);
  and and_27 (and_12_out[3], comparator_12_eq, valid_4_q);
  assign and_28_out = bitextender_9_out & data_4_q;  // And and_28, 32 bits wide
  BitExtender #(.inputBits(1), .outputBits(32)) bitextender_9 (.in(not_2_out[4]), .out(bitextender_9_out));
  Comparator #(.Bits(5)) comparator_13 (.a(S1), .b(id_5_q), .eq(comparator_13_eq));  // open: gt, lt
  Comparator #(.Bits(5)) comparator_14 (.a(S2), .b(id_5_q), .eq(comparator_14_eq));  // open: gt, lt
  Comparator #(.Bits(5)) comparator_15 (.a(S3), .b(id_5_q), .eq(comparator_15_eq));  // open: gt, lt
  and and_29 (and_29_out, valid_4_q, not_2_out[4], res_t);
  Register valid_5 (.D(and_29_out), .C(C), .en(and_9_out[4]), .Q(valid_5_q));
  Register #(.Bits(5)) id_5 (.D(id_4_q), .C(C), .en(and_9_out[4]), .Q(id_5_q));
  Register #(.Bits(32)) data_5 (.D(and_28_out), .C(C), .en(and_9_out[4]), .Q(data_5_q));
  and and_30 (and_10_out[4], comparator_13_eq, valid_5_q);
  and and_31 (and_11_out[4], comparator_14_eq, valid_5_q);
  and and_32 (and_12_out[4], comparator_15_eq, valid_5_q);
  assign and_33_out = bitextender_10_out & data_5_q;  // And and_33, 32 bits wide
  BitExtender #(.inputBits(1), .outputBits(32)) bitextender_10 (.in(not_2_out[5]), .out(bitextender_10_out));
  Comparator #(.Bits(5)) comparator_16 (.a(S1), .b(id_6_q), .eq(comparator_16_eq));  // open: gt, lt
  Comparator #(.Bits(5)) comparator_17 (.a(S2), .b(id_6_q), .eq(comparator_17_eq));  // open: gt, lt
  Comparator #(.Bits(5)) comparator_18 (.a(S3), .b(id_6_q), .eq(comparator_18_eq));  // open: gt, lt
  and and_34 (and_34_out, valid_5_q, not_2_out[5], res_t);
  Register valid_6 (.D(and_34_out), .C(C), .en(and_9_out[5]), .Q(valid_6_q));
  Register #(.Bits(5)) id_6 (.D(id_5_q), .C(C), .en(and_9_out[5]), .Q(id_6_q));
  Register #(.Bits(32)) data_6 (.D(and_33_out), .C(C), .en(and_9_out[5]), .Q(data_6_q));
  and and_35 (and_10_out[5], comparator_16_eq, valid_6_q);
  Comparator #(.Bits(5)) comparator_19 (.a(S1), .b(id_7_q), .eq(comparator_19_eq));  // open: gt, lt
  and and_36 (and_11_out[5], comparator_17_eq, valid_6_q);
  Comparator #(.Bits(5)) comparator_20 (.a(S2), .b(id_7_q), .eq(comparator_20_eq));  // open: gt, lt
  and and_37 (and_12_out[5], comparator_18_eq, valid_6_q);
  Comparator #(.Bits(5)) comparator_21 (.a(S3), .b(id_7_q), .eq(comparator_21_eq));  // open: gt, lt
  and and_38 (and_38_out, valid_6_q, not_2_out[6], res_t);
  Register valid_7 (.D(and_38_out), .C(C), .en(and_9_out[6]), .Q(valid_7_q));
  Register #(.Bits(5)) id_7 (.D(id_6_q), .C(C), .en(and_9_out[6]), .Q(id_7_q));
  assign and_39_out = bitextender_11_out & data_6_q;  // And and_39, 32 bits wide
  Register #(.Bits(32)) data_7 (.D(and_39_out), .C(C), .en(and_9_out[6]), .Q(data_7_q));
  BitExtender #(.inputBits(1), .outputBits(32)) bitextender_11 (.in(not_2_out[6]), .out(bitextender_11_out));
  and and_40 (and_10_out[6], comparator_19_eq, valid_7_q);
  and and_41 (and_11_out[6], comparator_20_eq, valid_7_q);
  and and_42 (and_12_out[6], comparator_21_eq, valid_7_q);
  assign and_43_out = bitextender_12_out & data_7_q;  // And and_43, 32 bits wide
  Comparator #(.Bits(5)) comparator_22 (.a(S1), .b(id_8_q), .eq(comparator_22_eq));  // open: gt, lt
  Comparator #(.Bits(5)) comparator_23 (.a(S2), .b(id_8_q), .eq(comparator_23_eq));  // open: gt, lt
  Comparator #(.Bits(5)) comparator_24 (.a(S3), .b(id_8_q), .eq(comparator_24_eq));  // open: gt, lt
  and and_44 (and_44_out, valid_7_q, not_2_out[7], res_t);
  Register valid_8 (.D(and_44_out), .C(C), .en(and_9_out[7]), .Q(valid_8_q));
  Register #(.Bits(5)) id_8 (.D(id_7_q), .C(C), .en(and_9_out[7]), .Q(id_8_q));
  Register #(.Bits(32)) data_8 (.D(and_43_out), .C(C), .en(and_9_out[7]), .Q(data_8_q));
  BitExtender #(.inputBits(1), .outputBits(32)) bitextender_12 (.in(not_2_out[7]), .out(bitextender_12_out));
  and and_45 (and_10_out[7], comparator_22_eq, valid_8_q);
  and and_46 (and_11_out[7], comparator_23_eq, valid_8_q);
  and and_47 (and_12_out[7], comparator_24_eq, valid_8_q);
  assign and_48_out = bitextender_13_out & data_8_q;  // And and_48, 32 bits wide
  BitExtender #(.inputBits(1), .outputBits(32)) bitextender_13 (.in(not_2_out[8]), .out(bitextender_13_out));
  Comparator #(.Bits(5)) comparator_25 (.a(S1), .b(id_9_q), .eq(comparator_25_eq));  // open: gt, lt
  Comparator #(.Bits(5)) comparator_26 (.a(S2), .b(id_9_q), .eq(comparator_26_eq));  // open: gt, lt
  Comparator #(.Bits(5)) comparator_27 (.a(S3), .b(id_9_q), .eq(comparator_27_eq));  // open: gt, lt
  and and_49 (and_49_out, valid_8_q, not_2_out[8], res_t);
  Register valid_9 (.D(and_49_out), .C(C), .en(and_9_out[8]), .Q(valid_9_q));
  Register #(.Bits(5)) id_9 (.D(id_8_q), .C(C), .en(and_9_out[8]), .Q(id_9_q));
  Register #(.Bits(32)) data_9 (.D(and_48_out), .C(C), .en(and_9_out[8]), .Q(data_9_q));
  and and_50 (and_10_out[8], comparator_25_eq, valid_9_q);
  and and_51 (and_11_out[8], comparator_26_eq, valid_9_q);
  and and_52 (and_12_out[8], comparator_27_eq, valid_9_q);
  assign and_53_out = bitextender_14_out & data_9_q;  // And and_53, 32 bits wide
  BitExtender #(.inputBits(1), .outputBits(32)) bitextender_14 (.in(not_2_out[9]), .out(bitextender_14_out));
  Comparator #(.Bits(5)) comparator_28 (.a(S1), .b(id_10_q), .eq(comparator_28_eq));  // open: gt, lt
  Comparator #(.Bits(5)) comparator_29 (.a(S2), .b(id_10_q), .eq(comparator_29_eq));  // open: gt, lt
  Comparator #(.Bits(5)) comparator_30 (.a(S3), .b(id_10_q), .eq(comparator_30_eq));  // open: gt, lt
  and and_54 (and_54_out, valid_9_q, not_2_out[9], res_t);
  Register valid_10 (.D(and_54_out), .C(C), .en(and_9_out[9]), .Q(valid_10_q));
  Register #(.Bits(5)) id_10 (.D(id_9_q), .C(C), .en(and_9_out[9]), .Q(id_10_q));
  Register #(.Bits(32)) data_10 (.D(and_53_out), .C(C), .en(and_9_out[9]), .Q(data_10_q));
  and and_55 (and_10_out[9], comparator_28_eq, valid_10_q);
  Comparator #(.Bits(5)) comparator_31 (.a(S1), .b(id_11_q), .eq(comparator_31_eq));  // open: gt, lt
  and and_56 (and_11_out[9], comparator_29_eq, valid_10_q);
  Comparator #(.Bits(5)) comparator_32 (.a(S2), .b(id_11_q), .eq(comparator_32_eq));  // open: gt, lt
  and and_57 (and_12_out[9], comparator_30_eq, valid_10_q);
  Comparator #(.Bits(5)) comparator_33 (.a(S3), .b(id_11_q), .eq(comparator_33_eq));  // open: gt, lt
  and and_58 (and_58_out, valid_10_q, not_2_out[10], res_t);
  Register valid_11 (.D(and_58_out), .C(C), .en(and_9_out[10]), .Q(valid_11_q));
  Register #(.Bits(5)) id_11 (.D(id_10_q), .C(C), .en(and_9_out[10]), .Q(id_11_q));
  assign and_59_out = bitextender_15_out & data_10_q;  // And and_59, 32 bits wide
  Register #(.Bits(32)) data_11 (.D(and_59_out), .C(C), .en(and_9_out[10]), .Q(data_11_q));
  BitExtender #(.inputBits(1), .outputBits(32)) bitextender_15 (.in(not_2_out[10]), .out(bitextender_15_out));
  and and_60 (and_10_out[10], comparator_31_eq, valid_11_q);
  and and_61 (and_11_out[10], comparator_32_eq, valid_11_q);
  and and_62 (and_12_out[10], comparator_33_eq, valid_11_q);
  assign and_63_out = bitextender_16_out & data_11_q;  // And and_63, 32 bits wide
  Comparator #(.Bits(5)) comparator_34 (.a(S1), .b(id_12_q), .eq(comparator_34_eq));  // open: gt, lt
  Comparator #(.Bits(5)) comparator_35 (.a(S2), .b(id_12_q), .eq(comparator_35_eq));  // open: gt, lt
  Comparator #(.Bits(5)) comparator_36 (.a(S3), .b(id_12_q), .eq(comparator_36_eq));  // open: gt, lt
  and and_64 (and_64_out, valid_11_q, not_2_out[11], res_t);
  Register valid_12 (.D(and_64_out), .C(C), .en(and_9_out[11]), .Q(valid_12_q));
  Register #(.Bits(5)) id_12 (.D(id_11_q), .C(C), .en(and_9_out[11]), .Q(id_12_q));
  Register #(.Bits(32)) data_12 (.D(and_63_out), .C(C), .en(and_9_out[11]), .Q(data_12_q));
  BitExtender #(.inputBits(1), .outputBits(32)) bitextender_16 (.in(not_2_out[11]), .out(bitextender_16_out));
  and and_65 (and_10_out[11], comparator_34_eq, valid_12_q);
  and and_66 (and_11_out[11], comparator_35_eq, valid_12_q);
  and and_67 (and_12_out[11], comparator_36_eq, valid_12_q);
  assign and_68_out = bitextender_17_out & data_12_q;  // And and_68, 32 bits wide
  BitExtender #(.inputBits(1), .outputBits(32)) bitextender_17 (.in(not_2_out[12]), .out(bitextender_17_out));
  Comparator #(.Bits(5)) comparator_37 (.a(S1), .b(id_13_q), .eq(comparator_37_eq));  // open: gt, lt
  Comparator #(.Bits(5)) comparator_38 (.a(S2), .b(id_13_q), .eq(comparator_38_eq));  // open: gt, lt
  Comparator #(.Bits(5)) comparator_39 (.a(S3), .b(id_13_q), .eq(comparator_39_eq));  // open: gt, lt
  and and_69 (and_69_out, valid_12_q, not_2_out[12], res_t);
  Register valid_13 (.D(and_69_out), .C(C), .en(and_9_out[12]), .Q(valid_13_q));
  Register #(.Bits(5)) id_13 (.D(id_12_q), .C(C), .en(and_9_out[12]), .Q(id_13_q));
  Register #(.Bits(32)) data_13 (.D(and_68_out), .C(C), .en(and_9_out[12]), .Q(data_13_q));
  and and_70 (and_10_out[12], comparator_37_eq, valid_13_q);
  and and_71 (and_11_out[12], comparator_38_eq, valid_13_q);
  and and_72 (and_12_out[12], comparator_39_eq, valid_13_q);
  assign and_73_out = bitextender_18_out & data_13_q;  // And and_73, 32 bits wide
  BitExtender #(.inputBits(1), .outputBits(32)) bitextender_18 (.in(not_2_out[13]), .out(bitextender_18_out));
  Comparator #(.Bits(5)) comparator_40 (.a(S1), .b(id_14_q), .eq(comparator_40_eq));  // open: gt, lt
  Comparator #(.Bits(5)) comparator_41 (.a(S2), .b(id_14_q), .eq(comparator_41_eq));  // open: gt, lt
  Comparator #(.Bits(5)) comparator_42 (.a(S3), .b(id_14_q), .eq(comparator_42_eq));  // open: gt, lt
  and and_74 (and_74_out, valid_13_q, not_2_out[13], res_t);
  Register valid_14 (.D(and_74_out), .C(C), .en(and_9_out[13]), .Q(valid_14_q));
  Register #(.Bits(5)) id_14 (.D(id_13_q), .C(C), .en(and_9_out[13]), .Q(id_14_q));
  Register #(.Bits(32)) data_14 (.D(and_73_out), .C(C), .en(and_9_out[13]), .Q(data_14_q));
  and and_75 (and_10_out[13], comparator_40_eq, valid_14_q);
  Comparator #(.Bits(5)) comparator_43 (.a(S1), .b(id_15_q), .eq(comparator_43_eq));  // open: gt, lt
  and and_76 (and_11_out[13], comparator_41_eq, valid_14_q);
  Comparator #(.Bits(5)) comparator_44 (.a(S2), .b(id_15_q), .eq(comparator_44_eq));  // open: gt, lt
  and and_77 (and_12_out[13], comparator_42_eq, valid_14_q);
  Comparator #(.Bits(5)) comparator_45 (.a(S3), .b(id_15_q), .eq(comparator_45_eq));  // open: gt, lt
  and and_78 (and_78_out, valid_14_q, not_2_out[14], res_t);
  Register valid_15 (.D(and_78_out), .C(C), .en(and_9_out[14]), .Q(valid_15_q));
  Register #(.Bits(5)) id_15 (.D(id_14_q), .C(C), .en(and_9_out[14]), .Q(id_15_q));
  assign and_79_out = bitextender_19_out & data_14_q;  // And and_79, 32 bits wide
  Register #(.Bits(32)) data_15 (.D(and_79_out), .C(C), .en(and_9_out[14]), .Q(data_15_q));
  BitExtender #(.inputBits(1), .outputBits(32)) bitextender_19 (.in(not_2_out[14]), .out(bitextender_19_out));
  and and_80 (and_10_out[14], comparator_43_eq, valid_15_q);
  and and_81 (and_11_out[14], comparator_44_eq, valid_15_q);
  and and_82 (and_12_out[14], comparator_45_eq, valid_15_q);
  assign and_83_out = bitextender_20_out & data_15_q;  // And and_83, 32 bits wide
  Comparator #(.Bits(5)) comparator_46 (.a(S1), .b(id_16_q), .eq(comparator_46_eq));  // open: gt, lt
  Comparator #(.Bits(5)) comparator_47 (.a(S2), .b(id_16_q), .eq(comparator_47_eq));  // open: gt, lt
  Comparator #(.Bits(5)) comparator_48 (.a(S3), .b(id_16_q), .eq(comparator_48_eq));  // open: gt, lt
  and and_84 (and_84_out, valid_15_q, not_2_out[15], res_t);
  Register valid_16 (.D(and_84_out), .C(C), .en(and_9_out[15]), .Q(valid_16_q));
  Register #(.Bits(5)) id_16 (.D(id_15_q), .C(C), .en(and_9_out[15]), .Q(id_16_q));
  Register #(.Bits(32)) data_16 (.D(and_83_out), .C(C), .en(and_9_out[15]), .Q(data_16_q));
  BitExtender #(.inputBits(1), .outputBits(32)) bitextender_20 (.in(not_2_out[15]), .out(bitextender_20_out));
  and and_85 (and_10_out[15], comparator_46_eq, valid_16_q);
  and and_86 (and_11_out[15], comparator_47_eq, valid_16_q);
  and and_87 (and_12_out[15], comparator_48_eq, valid_16_q);
  Multiplexer #(.Selector_Bits(4), .Bits(32)) multiplexer_1 (
    .sel(priorityencoder_1_num), .in_0(data_q), .in_1(data_2_q), .in_2(data_3_q), .in_3(data_4_q),
    .in_4(data_5_q), .in_5(data_6_q), .in_6(data_7_q), .in_7(data_8_q), .in_8(data_9_q), .in_9(data_10_q),
    .in_10(data_11_q), .in_11(data_12_q), .in_12(data_13_q), .in_13(data_14_q), .in_14(data_15_q),
    .in_15(data_16_q), .out(D1));
  Multiplexer #(.Selector_Bits(4), .Bits(32)) multiplexer_2 (
    .sel(priorityencoder_2_num), .in_0(data_q), .in_1(data_2_q), .in_2(data_3_q), .in_3(data_4_q),
    .in_4(data_5_q), .in_5(data_6_q), .in_6(data_7_q), .in_7(data_8_q), .in_8(data_9_q), .in_9(data_10_q),
    .in_10(data_11_q), .in_11(data_12_q), .in_12(data_13_q), .in_13(data_14_q), .in_14(data_15_q),
    .in_15(data_16_q), .out(D2));
  Multiplexer #(.Selector_Bits(4), .Bits(32)) multiplexer_3 (
    .sel(priorityencoder_3_num), .in_0(data_q), .in_1(data_2_q), .in_2(data_3_q), .in_3(data_4_q),
    .in_4(data_5_q), .in_5(data_6_q), .in_6(data_7_q), .in_7(data_8_q), .in_8(data_9_q), .in_9(data_10_q),
    .in_10(data_11_q), .in_11(data_12_q), .in_12(data_13_q), .in_13(data_14_q), .in_14(data_15_q),
    .in_15(data_16_q), .out(D3));
endmodule
