// Digital circuit history-queue3.dig as structural Verilog
module history_queue3 (
  input  C,
  input  res,
  input  [31:0] D,
  input  E,
  input  P1,
  input  [4:0] id,
  input  [4:0] com1_id,
  input  com1,
  input  [4:0] com2_id,
  input  com2,
  output [31:0] D1,
  output [4:0] I1,
  output V1,
  output full
);

  wire and_6_out, and_7_out, and_9_out, and_10_out, and_11_out, and_12_out, and_13_out, and_14_out,
       and_15_out, not_2_out, or_3_out;
  wire [2:0] priorityencoder_1_num;
  wire [4:0] id_2_q, id_3_q, id_4_q, id_5_q, id_6_q, id_7_q, id_8_q, id_q;
  wire [7:0] and_1_out, and_2_out, and_3_out, and_5_out, and_8_out, bitextender_1_out, bitextender_2_out,
       bitextender_3_out, bitextender_4_out, bitextender_5_out, comparator_1_eq, comparator_2_eq,
       fill_8_1_out1, not_1_out, not_3_out, or_1_out, or_2_out, priority_8_1_out1, valid_q;
  wire [31:0] data_2_q, data_3_q, data_4_q, data_5_q, data_6_q, data_7_q, data_8_q, data_q;

  assign not_1_out = ~valid_q;  // Not not_1, 8 bits wide
  BitExtender #(.inputBits(1), .outputBits(8)) bitextender_1 (.in(com2), .out(bitextender_1_out));
  assign and_1_out = comparator_1_eq & bitextender_1_out;  // And and_1, 8 bits wide
  priority_8 priority_8_1 (
    .on(1'b1), .in1(and_3_out[0]), .in2(and_3_out[1]), .in3(and_3_out[2]), .in4(and_3_out[3]),
    .in5(and_3_out[4]), .in6(and_3_out[5]), .in7(and_3_out[6]), .in8(and_3_out[7]),
    .out1(priority_8_1_out1[0]), .out2(priority_8_1_out1[1]), .out3(priority_8_1_out1[2]),
    .out4(priority_8_1_out1[3]), .out5(priority_8_1_out1[4]), .out6(priority_8_1_out1[5]),
    .out7(priority_8_1_out1[6]), .out8(priority_8_1_out1[7]));  // open: v
  BitExtender #(.inputBits(1), .outputBits(8)) bitextender_2 (.in(com1), .out(bitextender_2_out));
  assign and_2_out = comparator_2_eq & bitextender_2_out;  // And and_2, 8 bits wide
  BitExtender #(.inputBits(1), .outputBits(8)) bitextender_3 (.in(P1), .out(bitextender_3_out));
  assign and_3_out = valid_q & bitextender_3_out;  // And and_3, 8 bits wide
  assign or_1_out = and_2_out | and_1_out | priority_8_1_out1;  // Or or_1, 8 bits wide
  assign or_2_out = and_2_out | and_1_out | not_1_out | and_3_out;  // Or or_2, 8 bits wide
  and and_4 (full, valid_q[0], valid_q[1], valid_q[2], valid_q[3], valid_q[4], valid_q[5], valid_q[6], valid_q[7]);
  not not_2 (not_2_out, res);
  BitExtender #(.inputBits(1), .outputBits(8)) bitextender_4 (.in(not_2_out), .out(bitextender_4_out));
  assign not_3_out = ~or_1_out;  // Not not_3, 8 bits wide
  assign and_5_out = bitextender_4_out & not_3_out;  // And and_5, 8 bits wide
  fill_8 fill_8_1 (
    .on(1'b0), .in1(or_2_out[0]), .in2(or_2_out[1]), .in3(or_2_out[2]), .in4(or_2_out[3]), .in5(or_2_out[4]),
    .in6(or_2_out[5]), .in7(or_2_out[6]), .in8(or_2_out[7]), .out1(fill_8_1_out1[0]),
    .out2(fill_8_1_out1[1]), .out3(fill_8_1_out1[2]), .out4(fill_8_1_out1[3]), .out5(fill_8_1_out1[4]),
    .out6(fill_8_1_out1[5]), .out7(fill_8_1_out1[6]), .out8(fill_8_1_out1[7]));  // open: v
  and and_6 (and_6_out, V1, P1);
  or or_3 (or_3_out, E, and_6_out, com1, com2);
  PriorityEncoder #(.Selector_Bits(3)) priorityencoder_1 (
    .in0(valid_q[0]), .in1(valid_q[1]), .in2(valid_q[2]), .in3(valid_q[3]), .in4(valid_q[4]),
    .in5(valid_q[5]), .in6(valid_q[6]), .in7(valid_q[7]), .num(priorityencoder_1_num), .any(V1));
  Comparator #(.Bits(5)) comparator_1 (.a(com2_id), .b(id_q), .eq(comparator_1_eq[0]));  // open: gt, lt
  Comparator #(.Bits(5)) comparator_2 (.a(com1_id), .b(id_q), .eq(comparator_2_eq[0]));  // open: gt, lt
  Register #(.Bits(5)) u_id (.D(id), .C(C), .en(and_8_out[0]), .Q(id_q));
  and and_7 (and_7_out, E, and_5_out[0]);
  Register valid (.D(and_7_out), .C(C), .en(and_8_out[0]), .Q(valid_q[0]));
  Register #(.Bits(32)) data (.D(D), .C(C), .en(and_8_out[0]), .Q(data_q));
  assign and_8_out = fill_8_1_out1 & bitextender_5_out;  // And and_8, 8 bits wide
  BitExtender #(.inputBits(1), .outputBits(8)) bitextender_5 (.in(or_3_out), .out(bitextender_5_out));
  Comparator #(.Bits(5)) comparator_3 (.a(com2_id), .b(id_2_q), .eq(comparator_1_eq[1]));  // open: gt, lt
  Comparator #(.Bits(5)) comparator_4 (.a(com1_id), .b(id_2_q), .eq(comparator_2_eq[1]));  // open: gt, lt
  Register #(.Bits(5)) id_2 (.D(id_q), .C(C), .en(and_8_out[1]), .Q(id_2_q));
  and and_9 (and_9_out, valid_q[0], and_5_out[1]);
  Register valid_2 (.D(and_9_out), .C(C), .en(and_8_out[1]), .Q(valid_q[1]));
  Register #(.Bits(32)) data_2 (.D(data_q), .C(C), .en(and_8_out[1]), .Q(data_2_q));
  Comparator #(.Bits(5)) comparator_5 (.a(com2_id), .b(id_3_q), .eq(comparator_1_eq[2]));  // open: gt, lt
  Comparator #(.Bits(5)) comparator_6 (.a(com1_id), .b(id_3_q), .eq(comparator_2_eq[2]));  // open: gt, lt
  Register #(.Bits(5)) id_3 (.D(id_2_q), .C(C), .en(and_8_out[2]), .Q(id_3_q));
  and and_10 (and_10_out, valid_q[1], and_5_out[2]);
  Register valid_3 (.D(and_10_out), .C(C), .en(and_8_out[2]), .Q(valid_q[2]));
  Register #(.Bits(32)) data_3 (.D(data_2_q), .C(C), .en(and_8_out[2]), .Q(data_3_q));
  Comparator #(.Bits(5)) comparator_7 (.a(com2_id), .b(id_4_q), .eq(comparator_1_eq[3]));  // open: gt, lt
  Comparator #(.Bits(5)) comparator_8 (.a(com1_id), .b(id_4_q), .eq(comparator_2_eq[3]));  // open: gt, lt
  Register #(.Bits(5)) id_4 (.D(id_3_q), .C(C), .en(and_8_out[3]), .Q(id_4_q));
  and and_11 (and_11_out, valid_q[2], and_5_out[3]);
  Register valid_4 (.D(and_11_out), .C(C), .en(and_8_out[3]), .Q(valid_q[3]));
  Register #(.Bits(32)) data_4 (.D(data_3_q), .C(C), .en(and_8_out[3]), .Q(data_4_q));
  Comparator #(.Bits(5)) comparator_9 (.a(com2_id), .b(id_5_q), .eq(comparator_1_eq[4]));  // open: gt, lt
  Comparator #(.Bits(5)) comparator_10 (.a(com1_id), .b(id_5_q), .eq(comparator_2_eq[4]));  // open: gt, lt
  Register #(.Bits(5)) id_5 (.D(id_4_q), .C(C), .en(and_8_out[4]), .Q(id_5_q));
  and and_12 (and_12_out, valid_q[3], and_5_out[4]);
  Register valid_5 (.D(and_12_out), .C(C), .en(and_8_out[4]), .Q(valid_q[4]));
  Register #(.Bits(32)) data_5 (.D(data_4_q), .C(C), .en(and_8_out[4]), .Q(data_5_q));
  Comparator #(.Bits(5)) comparator_11 (.a(com2_id), .b(id_6_q), .eq(comparator_1_eq[5]));  // open: gt, lt
  Comparator #(.Bits(5)) comparator_12 (.a(com1_id), .b(id_6_q), .eq(comparator_2_eq[5]));  // open: gt, lt
  Register #(.Bits(5)) id_6 (.D(id_5_q), .C(C), .en(and_8_out[5]), .Q(id_6_q));
  and and_13 (and_13_out, valid_q[4], and_5_out[5]);
  Register valid_6 (.D(and_13_out), .C(C), .en(and_8_out[5]), .Q(valid_q[5]));
  Register #(.Bits(32)) data_6 (.D(data_5_q), .C(C), .en(and_8_out[5]), .Q(data_6_q));
  Comparator #(.Bits(5)) comparator_13 (.a(com2_id), .b(id_7_q), .eq(comparator_1_eq[6]));  // open: gt, lt
  Comparator #(.Bits(5)) comparator_14 (.a(com1_id), .b(id_7_q), .eq(comparator_2_eq[6]));  // open: gt, lt
  Register #(.Bits(5)) id_7 (.D(id_6_q), .C(C), .en(and_8_out[6]), .Q(id_7_q));
  and and_14 (and_14_out, valid_q[5], and_5_out[6]);
  Register valid_7 (.D(and_14_out), .C(C), .en(and_8_out[6]), .Q(valid_q[6]));
  Register #(.Bits(32)) data_7 (.D(data_6_q), .C(C), .en(and_8_out[6]), .Q(data_7_q));
  Comparator #(.Bits(5)) comparator_15 (.a(com2_id), .b(id_8_q), .eq(comparator_1_eq[7]));  // open: gt, lt
  Comparator #(.Bits(5)) comparator_16 (.a(com1_id), .b(id_8_q), .eq(comparator_2_eq[7]));  // open: gt, lt
  Register #(.Bits(5)) id_8 (.D(id_7_q), .C(C), .en(and_8_out[7]), .Q(id_8_q));
  and and_15 (and_15_out, valid_q[6], and_5_out[7]);
  Register valid_8 (.D(and_15_out), .C(C), .en(and_8_out[7]), .Q(valid_q[7]));
  Register #(.Bits(32)) data_8 (.D(data_7_q), .C(C), .en(and_8_out[7]), .Q(data_8_q));
  Multiplexer #(.Selector_Bits(3), .Bits(5)) multiplexer_1 (
    .sel(priorityencoder_1_num), .in_0(id_q), .in_1(id_2_q), .in_2(id_3_q), .in_3(id_4_q), .in_4(id_5_q),
    .in_5(id_6_q), .in_6(id_7_q), .in_7(id_8_q), .out(I1));
  Multiplexer #(.Selector_Bits(3), .Bits(32)) multiplexer_2 (
    .sel(priorityencoder_1_num), .in_0(data_q), .in_1(data_2_q), .in_2(data_3_q), .in_3(data_4_q),
    .in_4(data_5_q), .in_5(data_6_q), .in_6(data_7_q), .in_7(data_8_q), .out(D1));

  // Other names for the same wires on the sheet: cm1 = com1; cm1_id[4:0] = com1_id; cm2 = com2; cm2_id[4:0] = com2_id;
  //   OD1[31:0] = D1; OI1[4:0] = I1
endmodule
