// Digital circuit history.dig as structural Verilog
module history (
  input  [4:0] com1_id,
  input  com1,
  input  [4:0] com2_id,
  input  com2,
  input  [4:0] R,
  input  [31:0] D,
  input  E,
  input  [4:0] id,
  input  C,
  output [31:0] R1,
  output [31:0] R2,
  output [31:0] R3,
  output [31:0] R4,
  output [31:0] R5,
  output [31:0] R6,
  output [31:0] R7,
  output [31:0] R8,
  output [31:0] R9,
  output [31:0] R10,
  output [31:0] R11,
  output [31:0] R12,
  output [31:0] R13,
  output [31:0] R14,
  output [31:0] R15,
  output [31:0] R16,
  output [31:0] R17,
  output [31:0] R18,
  output [31:0] R19,
  output [31:0] R20,
  output [31:0] R21,
  output [31:0] R22,
  output [31:0] R23,
  output [31:0] R24,
  output [31:0] R25,
  output [31:0] R0,
  output [31:0] V
);

  wire and_1_out, and_2_out, and_3_out, and_5_out, and_6_out, and_7_out, cm_V1, cm_V2, direct,
       history_queue3_1_p14, history_queue3_1_p15, history_queue3_1_p16, history_queue3_1_p17, or_2_out,
       or_3_out;
  wire [4:0] cm_R1, cm_R2, history_queue3_1_p18, multiplexer_1_out, multiplexer_2_out, multiplexer_4_out;
  wire [31:0] and_4_out, buff_empty, commit32, demultiplexer_1_out_0, demultiplexer_2_out_0,
       demultiplexer_3_out_0, history_queue3_1_p19, history_queue3_1_p20, multiplexer_3_out;

  Demultiplexer #(.Selector_Bits(5)) demultiplexer_1 (
    .sel(R), .in(E), .out_0(demultiplexer_1_out_0[0]), .out_1(demultiplexer_1_out_0[1]),
    .out_2(demultiplexer_1_out_0[2]), .out_3(demultiplexer_1_out_0[3]), .out_4(demultiplexer_1_out_0[4]),
    .out_5(demultiplexer_1_out_0[5]), .out_6(demultiplexer_1_out_0[6]), .out_7(demultiplexer_1_out_0[7]),
    .out_8(demultiplexer_1_out_0[8]), .out_9(demultiplexer_1_out_0[9]), .out_10(demultiplexer_1_out_0[10]),
    .out_11(demultiplexer_1_out_0[11]), .out_12(demultiplexer_1_out_0[12]),
    .out_13(demultiplexer_1_out_0[13]), .out_14(demultiplexer_1_out_0[14]),
    .out_15(demultiplexer_1_out_0[15]), .out_16(demultiplexer_1_out_0[16]),
    .out_17(demultiplexer_1_out_0[17]), .out_18(demultiplexer_1_out_0[18]),
    .out_19(demultiplexer_1_out_0[19]), .out_20(demultiplexer_1_out_0[20]),
    .out_21(demultiplexer_1_out_0[21]), .out_22(demultiplexer_1_out_0[22]),
    .out_23(demultiplexer_1_out_0[23]), .out_24(demultiplexer_1_out_0[24]),
    .out_25(demultiplexer_1_out_0[25]), .out_26(demultiplexer_1_out_0[26]),
    .out_27(demultiplexer_1_out_0[27]), .out_28(demultiplexer_1_out_0[28]),
    .out_29(demultiplexer_1_out_0[29]), .out_30(demultiplexer_1_out_0[30]), .out_31(demultiplexer_1_out_0[31]));
  and and_1 (and_1_out, E, ~direct);  // And
  and and_2 (and_2_out, com1, cm_V1);
  and and_3 (and_3_out, com2, cm_V2);
  assign buff_empty = ~V;  // Not not_1, 32 bits wide
  assign and_4_out = buff_empty & demultiplexer_1_out_0;  // And and_4, 32 bits wide
  or or_1 (direct, and_4_out[0], and_4_out[1], and_4_out[2], and_4_out[3], and_4_out[4], and_4_out[5], and_4_out[6], and_4_out[7], and_4_out[8], and_4_out[9], and_4_out[10], and_4_out[11], and_4_out[12], and_4_out[13], and_4_out[14], and_4_out[15], and_4_out[16], and_4_out[17], and_4_out[18], and_4_out[19], and_4_out[20], and_4_out[21], and_4_out[22], and_4_out[23], and_4_out[24], and_4_out[25], and_4_out[26], and_4_out[27], and_4_out[28], and_4_out[29], and_4_out[30], and_4_out[31]);
  // history_queue3 history_queue3_1: pin names not known; wires that end beside it: C, and_1_out, id, R, D, and_2_out, and_3_out, cm_R1, cm_R2, com1, com1_id, com2, com2_id, history_queue3_1_p14, history_queue3_1_p15, history_queue3_1_p16, history_queue3_1_p17, history_queue3_1_p18, history_queue3_1_p19, history_queue3_1_p20
  DipSwitch dipswitch_1 (.out(history_queue3_1_p14));
  and and_5 (and_5_out, direct, E);
  Multiplexer #(.Bits(5)) multiplexer_1 (.sel(direct), .in_0(history_queue3_1_p18), .in_1(id), .out(multiplexer_1_out));
  and and_6 (and_6_out, cm_V1, com1);
  or or_2 (or_2_out, and_5_out, history_queue3_1_p16);
  Multiplexer #(.Bits(5)) multiplexer_2 (.sel(direct), .in_0(cm_R2), .in_1(R), .out(multiplexer_2_out));
  Demultiplexer #(.Selector_Bits(5)) demultiplexer_2 (
    .sel(cm_R1), .in(and_6_out), .out_0(demultiplexer_2_out_0[0]), .out_1(demultiplexer_2_out_0[1]),
    .out_2(demultiplexer_2_out_0[2]), .out_3(demultiplexer_2_out_0[3]), .out_4(demultiplexer_2_out_0[4]),
    .out_5(demultiplexer_2_out_0[5]), .out_6(demultiplexer_2_out_0[6]), .out_7(demultiplexer_2_out_0[7]),
    .out_8(demultiplexer_2_out_0[8]), .out_9(demultiplexer_2_out_0[9]), .out_10(demultiplexer_2_out_0[10]),
    .out_11(demultiplexer_2_out_0[11]), .out_12(demultiplexer_2_out_0[12]),
    .out_13(demultiplexer_2_out_0[13]), .out_14(demultiplexer_2_out_0[14]),
    .out_15(demultiplexer_2_out_0[15]), .out_16(demultiplexer_2_out_0[16]),
    .out_17(demultiplexer_2_out_0[17]), .out_18(demultiplexer_2_out_0[18]),
    .out_19(demultiplexer_2_out_0[19]), .out_20(demultiplexer_2_out_0[20]),
    .out_21(demultiplexer_2_out_0[21]), .out_22(demultiplexer_2_out_0[22]),
    .out_23(demultiplexer_2_out_0[23]), .out_24(demultiplexer_2_out_0[24]),
    .out_25(demultiplexer_2_out_0[25]), .out_26(demultiplexer_2_out_0[26]),
    .out_27(demultiplexer_2_out_0[27]), .out_28(demultiplexer_2_out_0[28]),
    .out_29(demultiplexer_2_out_0[29]), .out_30(demultiplexer_2_out_0[30]), .out_31(demultiplexer_2_out_0[31]));
  Multiplexer #(.Bits(32)) multiplexer_3 (.sel(direct), .in_0(history_queue3_1_p20), .in_1(D), .out(multiplexer_3_out));
  Multiplexer #(.Bits(5)) multiplexer_4 (.sel(direct), .in_0(cm_R2), .in_1(R), .out(multiplexer_4_out));
  or or_3 (or_3_out, and_3_out, direct);
  // map_inst2reg map_inst2reg_1: pin names not known; wires that end beside it: C, history_queue3_1_p15, or_2_out, history_queue3_1_p17, multiplexer_1_out, cm_R1, multiplexer_2_out, com1, com1_id, com2, com2_id, cm_V1, cm_R1, cm_V2, cm_R2
  register32x32 register32x32_1 (
    .valid(V), .R0(R0), .R1(R1), .R2(R2), .R3(R3), .R4(R4), .R5(R5), .R6(R6), .R7(R7), .R8(R8), .R9(R9),
    .R10(R10), .R11(R11), .R12(R12), .R13(R13), .R14(R14), .R15(R15), .R16(R16), .R17(R17), .R18(R18),
    .R19(R19), .R20(R20), .R21(R21), .R22(R22), .R23(R23), .R24(R24), .R25(R25), .C(C),
    .D1(history_queue3_1_p19), .D2(multiplexer_3_out), .S1(cm_R1), .S2(multiplexer_4_out), .E1(and_2_out),
    .E2(or_3_out), .Del(commit32));
  and and_7 (and_7_out, cm_V2, com2);
  Demultiplexer #(.Selector_Bits(5)) demultiplexer_3 (
    .sel(cm_R2), .in(and_7_out), .out_0(demultiplexer_3_out_0[0]), .out_1(demultiplexer_3_out_0[1]),
    .out_2(demultiplexer_3_out_0[2]), .out_3(demultiplexer_3_out_0[3]), .out_4(demultiplexer_3_out_0[4]),
    .out_5(demultiplexer_3_out_0[5]), .out_6(demultiplexer_3_out_0[6]), .out_7(demultiplexer_3_out_0[7]),
    .out_8(demultiplexer_3_out_0[8]), .out_9(demultiplexer_3_out_0[9]), .out_10(demultiplexer_3_out_0[10]),
    .out_11(demultiplexer_3_out_0[11]), .out_12(demultiplexer_3_out_0[12]),
    .out_13(demultiplexer_3_out_0[13]), .out_14(demultiplexer_3_out_0[14]),
    .out_15(demultiplexer_3_out_0[15]), .out_16(demultiplexer_3_out_0[16]),
    .out_17(demultiplexer_3_out_0[17]), .out_18(demultiplexer_3_out_0[18]),
    .out_19(demultiplexer_3_out_0[19]), .out_20(demultiplexer_3_out_0[20]),
    .out_21(demultiplexer_3_out_0[21]), .out_22(demultiplexer_3_out_0[22]),
    .out_23(demultiplexer_3_out_0[23]), .out_24(demultiplexer_3_out_0[24]),
    .out_25(demultiplexer_3_out_0[25]), .out_26(demultiplexer_3_out_0[26]),
    .out_27(demultiplexer_3_out_0[27]), .out_28(demultiplexer_3_out_0[28]),
    .out_29(demultiplexer_3_out_0[29]), .out_30(demultiplexer_3_out_0[30]), .out_31(demultiplexer_3_out_0[31]));
  assign commit32 = demultiplexer_2_out_0 | demultiplexer_3_out_0;  // Or or_4, 32 bits wide

  // Other names for the same wires on the sheet: buff_valid[31:0] = V; cm1 = com1; cm1_id[4:0] = com1_id; cm2 = com2;
  //   cm2_id[4:0] = com2_id
endmodule
