// Digital circuit history2.dig as structural Verilog
module history2 (
  input  [4:0] com1_id,
  input  com1,
  input  [4:0] com2_id,
  input  com2,
  input  [4:0] R,
  input  [31:0] D,
  input  E,
  input  [4:0] id,
  input  C,
  output [31:0] R1,
  output [31:0] R2,
  output [31:0] R3,
  output [31:0] R4,
  output [31:0] R5,
  output [31:0] R6,
  output [31:0] R7,
  output [31:0] R8,
  output [31:0] V,
  output full
);

  wire and_1_out, and_2_out, and_3_out, and_6_out, and_7_out, and_8_out, buff_full, cm_V1, cm_V2,
       dipswitch_1_out, direct, history_queue_1_v1, history_queue_1_v2, or_2_out, or_3_out, Q_full;
  wire [4:0] cm_R1, cm_R2, history_queue_1_i1, history_queue_1_i2, multiplexer_1_out, multiplexer_3_out,
       multiplexer_4_out;
  wire [7:0] and_4_out, buff_empty, buff_valid8, commit8, demultiplexer_1_out_0, demultiplexer_2_out_0,
       demultiplexer_3_out_0;
  wire [31:0] history_queue_1_d1, history_queue_1_d2, multiplexer_2_out;

  Demultiplexer #(.Selector_Bits(3)) demultiplexer_1 (
    .sel(R[2:0]), .in(E), .out_0(demultiplexer_1_out_0[0]), .out_1(demultiplexer_1_out_0[1]),
    .out_2(demultiplexer_1_out_0[2]), .out_3(demultiplexer_1_out_0[3]), .out_4(demultiplexer_1_out_0[4]),
    .out_5(demultiplexer_1_out_0[5]), .out_6(demultiplexer_1_out_0[6]), .out_7(demultiplexer_1_out_0[7]));
  and and_1 (and_1_out, E, ~direct);  // And
  and and_2 (and_2_out, com1, cm_V1);
  and and_3 (and_3_out, com2, cm_V2);
  assign buff_empty = ~buff_valid8;  // Not not_1, 8 bits wide
  assign and_4_out = buff_empty & demultiplexer_1_out_0;  // And and_4, 8 bits wide
  or or_1 (direct, and_4_out[0], and_4_out[1], and_4_out[2], and_4_out[3], and_4_out[4], and_4_out[5], and_4_out[6], and_4_out[7]);
  history_queue history_queue_1 (
    .C(C), .E(and_1_out), .id(id), .R(R), .D(D), .P1(and_2_out), .P2(and_3_out), .S1(cm_R1), .S2(cm_R2),
    .com1(com1), .com1_id(com1_id), .com2(com2), .com2_id(com2_id), .res(dipswitch_1_out),
    .V1(history_queue_1_v1), .V2(history_queue_1_v2), .I1(history_queue_1_i1), .I2(history_queue_1_i2),
    .D1(history_queue_1_d1), .D2(history_queue_1_d2), .full(Q_full));
  DipSwitch dipswitch_1 (.out(dipswitch_1_out));
  and and_5 (full, Q_full, buff_full);
  and and_6 (and_6_out, direct, E);
  Multiplexer #(.Bits(5)) multiplexer_1 (.sel(direct), .in_0(history_queue_1_i2), .in_1(id), .out(multiplexer_1_out));
  and and_7 (and_7_out, cm_V1, com1);
  or or_2 (or_2_out, and_6_out, history_queue_1_v2);
  Multiplexer #(.Bits(32)) multiplexer_2 (.sel(direct), .in_0(history_queue_1_d2), .in_1(D), .out(multiplexer_2_out));
  Multiplexer #(.Bits(5)) multiplexer_3 (.sel(direct), .in_0(cm_R2), .in_1(R), .out(multiplexer_3_out));
  Demultiplexer #(.Selector_Bits(3)) demultiplexer_2 (
    .sel(cm_R1[2:0]), .in(and_7_out), .out_0(demultiplexer_2_out_0[0]), .out_1(demultiplexer_2_out_0[1]),
    .out_2(demultiplexer_2_out_0[2]), .out_3(demultiplexer_2_out_0[3]), .out_4(demultiplexer_2_out_0[4]),
    .out_5(demultiplexer_2_out_0[5]), .out_6(demultiplexer_2_out_0[6]), .out_7(demultiplexer_2_out_0[7]));
  Multiplexer #(.Bits(5)) multiplexer_4 (.sel(direct), .in_0(cm_R2), .in_1(R), .out(multiplexer_4_out));
  map2_inst2reg map2_inst2reg_1 (
    .C(C), .E1(history_queue_1_v1), .E2(or_2_out), .I1(history_queue_1_i1), .I2(multiplexer_1_out),
    .R1(cm_R1), .R2(multiplexer_3_out), .com1(com1), .com1_id(com1_id), .com2(com2), .com2_id(com2_id),
    .V1(cm_V1), .O1(cm_R1), .V2(cm_V2), .O2(cm_R2));
  or or_3 (or_3_out, and_3_out, direct);
  and and_8 (and_8_out, cm_V2, com2);
  Demultiplexer #(.Selector_Bits(3)) demultiplexer_3 (
    .sel(cm_R2[2:0]), .in(and_8_out), .out_0(demultiplexer_3_out_0[0]), .out_1(demultiplexer_3_out_0[1]),
    .out_2(demultiplexer_3_out_0[2]), .out_3(demultiplexer_3_out_0[3]), .out_4(demultiplexer_3_out_0[4]),
    .out_5(demultiplexer_3_out_0[5]), .out_6(demultiplexer_3_out_0[6]), .out_7(demultiplexer_3_out_0[7]));
  register32x8 register32x8_1 (
    .C(C), .D1(history_queue_1_d1), .D2(multiplexer_2_out), .S1(cm_R1), .S2(multiplexer_4_out),
    .E1(and_2_out), .E2(or_3_out), .Del(commit8), .valid8(buff_valid8), .valid32(V), .R1(R1), .R2(R2),
    .R3(R3), .R4(R4), .R5(R5), .R6(R6), .R7(R7), .R8(R8));
  and and_9 (buff_full, buff_valid8[0], buff_valid8[1], buff_valid8[2], buff_valid8[3], buff_valid8[4], buff_valid8[5], buff_valid8[6], buff_valid8[7]);
  assign commit8 = demultiplexer_2_out_0 | demultiplexer_3_out_0;  // Or or_4, 8 bits wide

  // Other names for the same wires on the sheet: buff_valid32[31:0] = V; cm1 = com1; cm1_id[4:0] = com1_id;
  //   cm2 = com2; cm2_id[4:0] = com2_id
endmodule
