// Digital circuit id-gen2.dig as structural Verilog
module id_gen2 (
  input  \use ,
  input  C,
  input  [15:0] V_inst,
  output [3:0] id,
  output V,
  output com1,
  output com2,
  output [3:0] com2_id,
  output [3:0] com1_id,
  output epoch
);

  wire not_1_out, or_1_out, or_3_out, or_5_out, used, used1, used2, valid1, valid2;
  wire [0:0] and_1_out;
  wire [3:0] add_1_s;
  wire [4:0] add_2_s;
  wire [15:0] and_4_out, and_5_out, com1_16, com2_16, nor_1_out, or_2_out, or_4_out, use_16, used_q, valid_q;

  assign nor_1_out = ~(com2_16 | com1_16);  // NOr nor_1, 16 bits wide
  and and_1 (and_1_out[0], valid1, ~valid2);  // And
  and and_2 (com1, valid1, used1);
  and and_3 (com2, valid1, used1, valid2, used2);
  assign and_4_out = used_q & nor_1_out;  // And and_4, 16 bits wide
  not not_1 (not_1_out, used);
  or or_1 (or_1_out, com1, com2);
  assign and_5_out = valid_q & nor_1_out;  // And and_5, 16 bits wide
  Add #(.Bits(4)) add_1 (.a(com1_id), .b({2'b00, valid2, and_1_out[0]}), .c_i(1'b0), .s(add_1_s));  // open: c_o
  assign or_2_out = use_16 | and_4_out;  // Or or_2, 16 bits wide
  Add #(.Bits(5)) add_2 (.a({epoch, id}), .b({5{1'b0}}), .c_i(not_1_out), .s(add_2_s));  // open: c_o
  or or_3 (or_3_out, com1, com2, V_inst[0], V_inst[1], V_inst[2], V_inst[3], V_inst[4], V_inst[5], V_inst[6], V_inst[7], V_inst[8], V_inst[9], V_inst[10], V_inst[11], V_inst[12], V_inst[13], V_inst[14], V_inst[15]);
  assign or_4_out = V_inst | and_5_out;  // Or or_4, 16 bits wide
  or or_5 (or_5_out, com1, com2, \use );
  Register #(.Bits(4)) register_1 (.D(add_1_s), .C(C), .en(or_1_out), .Q(com1_id));
  Register #(.Bits(16)) u_used (.D(or_2_out), .C(C), .en(or_5_out), .Q(used_q));
  Register #(.Bits(5)) register_2 (.D(add_2_s), .C(C), .en(\use ), .Q({epoch, id}));
  Register #(.Bits(16)) valid (.D(or_4_out), .C(C), .en(or_3_out), .Q(valid_q));
  Add #(.Bits(4)) add_3 (.a(com1_id), .b(4'b0001), .c_i(1'b0), .s(com2_id));  // open: c_o
  BitSelector #(.Selector_Bits(4)) bitselector_1 (.in(used_q), .sel(com1_id), .out(used1));
  BitSelector #(.Selector_Bits(4)) bitselector_2 (.in(used_q), .sel(com2_id), .out(used2));
  BitSelector #(.Selector_Bits(4)) bitselector_3 (.in(used_q), .sel(id), .out(used));
  BitSelector #(.Selector_Bits(4)) bitselector_4 (.in(valid_q), .sel(com1_id), .out(valid1));
  BitSelector #(.Selector_Bits(4)) bitselector_5 (.in(valid_q), .sel(com2_id), .out(valid2));
  not not_2 (V, used);
  Demultiplexer #(.Selector_Bits(4)) demultiplexer_1 (
    .sel(com1_id), .in(com1), .out_0(com1_16[0]), .out_1(com1_16[1]), .out_2(com1_16[2]), .out_3(com1_16[3]),
    .out_4(com1_16[4]), .out_5(com1_16[5]), .out_6(com1_16[6]), .out_7(com1_16[7]), .out_8(com1_16[8]),
    .out_9(com1_16[9]), .out_10(com1_16[10]), .out_11(com1_16[11]), .out_12(com1_16[12]),
    .out_13(com1_16[13]), .out_14(com1_16[14]), .out_15(com1_16[15]));
  Demultiplexer #(.Selector_Bits(4)) demultiplexer_2 (
    .sel(com2_id), .in(com2), .out_0(com2_16[0]), .out_1(com2_16[1]), .out_2(com2_16[2]), .out_3(com2_16[3]),
    .out_4(com2_16[4]), .out_5(com2_16[5]), .out_6(com2_16[6]), .out_7(com2_16[7]), .out_8(com2_16[8]),
    .out_9(com2_16[9]), .out_10(com2_16[10]), .out_11(com2_16[11]), .out_12(com2_16[12]),
    .out_13(com2_16[13]), .out_14(com2_16[14]), .out_15(com2_16[15]));
  Demultiplexer #(.Selector_Bits(4)) demultiplexer_3 (
    .sel(id), .in(\use ), .out_0(use_16[0]), .out_1(use_16[1]), .out_2(use_16[2]), .out_3(use_16[3]),
    .out_4(use_16[4]), .out_5(use_16[5]), .out_6(use_16[6]), .out_7(use_16[7]), .out_8(use_16[8]),
    .out_9(use_16[9]), .out_10(use_16[10]), .out_11(use_16[11]), .out_12(use_16[12]), .out_13(use_16[13]),
    .out_14(use_16[14]), .out_15(use_16[15]));

  // Other names for the same wires on the sheet: store_16[15:0] = V_inst
endmodule
