// Digital circuit index-compressor.dig as structural Verilog
module index_compressor (
  input  in0,
  input  in1,
  input  in2,
  input  in3,
  input  in4,
  input  in5,
  input  in6,
  input  in7,
  output [2:0] out0,
  output [2:0] out1,
  output [2:0] out2,
  output [2:0] out3,
  output [2:0] out4,
  output [2:0] out5,
  output [2:0] out6,
  output [2:0] out7,
  output [7:0] V
);

  wire [1:0] add_1_c_o, add_2_c_o, add_3_s, add_4_s, add_5_s, add_h_1_c_o;
  wire [2:0] add_6_c_o;
  wire [2:2] add_3_c_o, add_4_c_o, add_5_c_o;
  wire [3:0] and_1_out, and_2_out, and_3_out, and_4_out, and_5_out, and_6_out, and_7_out, and_8_out,
       bitextender_1_out, bitextender_2_out, bitextender_3_out, bitextender_4_out, bitextender_5_out,
       bitextender_6_out, bitextender_7_out, bitextender_8_out, demultiplexer_1_out_0, demultiplexer_1_out_1,
       demultiplexer_2_out_0, demultiplexer_2_out_1, demultiplexer_2_out_2, demultiplexer_2_out_3,
       demultiplexer_2_out_4, demultiplexer_2_out_5, demultiplexer_2_out_6, demultiplexer_3_out_0,
       demultiplexer_3_out_1, demultiplexer_3_out_2, demultiplexer_4_out_0, demultiplexer_4_out_1,
       demultiplexer_4_out_2, demultiplexer_4_out_3, demultiplexer_4_out_4, demultiplexer_4_out_5,
       demultiplexer_4_out_6, demultiplexer_5_out_0, demultiplexer_5_out_1, demultiplexer_5_out_2,
       demultiplexer_5_out_3, demultiplexer_6_out_0, demultiplexer_6_out_1, demultiplexer_6_out_2,
       demultiplexer_6_out_3, demultiplexer_6_out_4, demultiplexer_6_out_5, demultiplexer_7_out_0,
       demultiplexer_7_out_1, demultiplexer_7_out_2, demultiplexer_7_out_3, demultiplexer_7_out_4;

  add_h add_h_1 (.a(in0), .b(in1), .s(add_h_1_c_o[0]), .c_o(add_h_1_c_o[1]));
  Add add_1 (.a(in0), .b(in1), .c_i(in2), .s(add_1_c_o[0]), .c_o(add_1_c_o[1]));
  Add add_2 (.a(in3), .b(in4), .c_i(in5), .s(add_2_c_o[0]), .c_o(add_2_c_o[1]));
  Add #(.Bits(2)) add_3 (.a(add_1_c_o), .b({1'b0, in3}), .c_i(1'b0), .s(add_3_s), .c_o(add_3_c_o[2]));
  Add #(.Bits(2)) add_4 (.a(add_1_c_o), .b({1'b0, in3}), .c_i(in4), .s(add_4_s), .c_o(add_4_c_o[2]));
  Add #(.Bits(2)) add_5 (.a(add_2_c_o), .b(add_1_c_o), .c_i(1'b0), .s(add_5_s), .c_o(add_5_c_o[2]));
  Add #(.Bits(2)) add_6 (.a(add_2_c_o), .b(add_1_c_o), .c_i(in6), .s(add_6_c_o[1:0]), .c_o(add_6_c_o[2]));
  BitExtender #(.inputBits(1), .outputBits(4)) bitextender_1 (.in(in0), .out(bitextender_1_out));
  BitExtender #(.inputBits(1), .outputBits(4)) bitextender_2 (.in(in1), .out(bitextender_2_out));
  BitExtender #(.inputBits(1), .outputBits(4)) bitextender_3 (.in(in7), .out(bitextender_3_out));
  assign and_1_out = 4'b1000 & bitextender_1_out;  // And and_1, 4 bits wide
  assign and_2_out = 4'b1001 & bitextender_2_out;  // And and_2, 4 bits wide
  assign and_3_out = 4'b1111 & bitextender_3_out;  // And and_3, 4 bits wide
  Demultiplexer #(.Bits(4)) demultiplexer_1 (
    .sel(in0), .in(and_2_out), .out_0(demultiplexer_1_out_0), .out_1(demultiplexer_1_out_1));
  Demultiplexer #(.Selector_Bits(3), .Bits(4)) demultiplexer_2 (
    .sel(add_6_c_o), .in(and_3_out), .out_0(demultiplexer_2_out_0), .out_1(demultiplexer_2_out_1),
    .out_2(demultiplexer_2_out_2), .out_3(demultiplexer_2_out_3), .out_4(demultiplexer_2_out_4),
    .out_5(demultiplexer_2_out_5), .out_6(demultiplexer_2_out_6), .out_7({V[7], out7}));
  BitExtender #(.inputBits(1), .outputBits(4)) bitextender_4 (.in(in2), .out(bitextender_4_out));
  BitExtender #(.inputBits(1), .outputBits(4)) bitextender_5 (.in(in6), .out(bitextender_5_out));
  assign and_4_out = 4'b1010 & bitextender_4_out;  // And and_4, 4 bits wide
  assign and_5_out = 4'b1110 & bitextender_5_out;  // And and_5, 4 bits wide
  Demultiplexer #(.Selector_Bits(2), .Bits(4)) demultiplexer_3 (
    .sel(add_h_1_c_o), .in(and_4_out), .out_0(demultiplexer_3_out_0), .out_1(demultiplexer_3_out_1),
    .out_2(demultiplexer_3_out_2));  // open: out_3
  Demultiplexer #(.Selector_Bits(3), .Bits(4)) demultiplexer_4 (
    .sel({add_5_c_o[2], add_5_s}), .in(and_5_out), .out_0(demultiplexer_4_out_0),
    .out_1(demultiplexer_4_out_1), .out_2(demultiplexer_4_out_2), .out_3(demultiplexer_4_out_3),
    .out_4(demultiplexer_4_out_4), .out_5(demultiplexer_4_out_5), .out_6(demultiplexer_4_out_6));  // open: out_7
  BitExtender #(.inputBits(1), .outputBits(4)) bitextender_6 (.in(in3), .out(bitextender_6_out));
  BitExtender #(.inputBits(1), .outputBits(4)) bitextender_7 (.in(in5), .out(bitextender_7_out));
  assign and_6_out = 4'b1011 & bitextender_6_out;  // And and_6, 4 bits wide
  assign and_7_out = 4'b1101 & bitextender_7_out;  // And and_7, 4 bits wide
  Demultiplexer #(.Selector_Bits(2), .Bits(4)) demultiplexer_5 (
    .sel(add_1_c_o), .in(and_6_out), .out_0(demultiplexer_5_out_0), .out_1(demultiplexer_5_out_1),
    .out_2(demultiplexer_5_out_2), .out_3(demultiplexer_5_out_3));
  Demultiplexer #(.Selector_Bits(3), .Bits(4)) demultiplexer_6 (
    .sel({add_4_c_o[2], add_4_s}), .in(and_7_out), .out_0(demultiplexer_6_out_0),
    .out_1(demultiplexer_6_out_1), .out_2(demultiplexer_6_out_2), .out_3(demultiplexer_6_out_3),
    .out_4(demultiplexer_6_out_4), .out_5(demultiplexer_6_out_5));  // open: out_6, out_7
  BitExtender #(.inputBits(1), .outputBits(4)) bitextender_8 (.in(in4), .out(bitextender_8_out));
  assign and_8_out = 4'b1100 & bitextender_8_out;  // And and_8, 4 bits wide
  Demultiplexer #(.Selector_Bits(3), .Bits(4)) demultiplexer_7 (
    .sel({add_3_c_o[2], add_3_s}), .in(and_8_out), .out_0(demultiplexer_7_out_0),
    .out_1(demultiplexer_7_out_1), .out_2(demultiplexer_7_out_2), .out_3(demultiplexer_7_out_3),
    .out_4(demultiplexer_7_out_4));  // open: out_5, out_6, out_7
  assign {V[0], out0} = and_1_out | demultiplexer_1_out_0 | demultiplexer_3_out_0 | demultiplexer_5_out_0 | demultiplexer_7_out_0 | demultiplexer_6_out_0 | demultiplexer_4_out_0 | demultiplexer_2_out_0;  // Or or_1, 4 bits wide
  assign {V[1], out1} = demultiplexer_1_out_1 | demultiplexer_3_out_1 | demultiplexer_5_out_1 | demultiplexer_7_out_1 | demultiplexer_6_out_1 | demultiplexer_4_out_1 | demultiplexer_2_out_1;  // Or or_2, 4 bits wide
  assign {V[6], out6} = demultiplexer_2_out_6 | demultiplexer_4_out_6;  // Or or_3, 4 bits wide
  assign {V[2], out2} = demultiplexer_3_out_2 | demultiplexer_5_out_2 | demultiplexer_7_out_2 | demultiplexer_6_out_2 | demultiplexer_4_out_2 | demultiplexer_2_out_2;  // Or or_4, 4 bits wide
  assign {V[5], out5} = demultiplexer_2_out_5 | demultiplexer_4_out_5 | demultiplexer_6_out_5;  // Or or_5, 4 bits wide
  assign {V[3], out3} = demultiplexer_5_out_3 | demultiplexer_7_out_3 | demultiplexer_6_out_3 | demultiplexer_4_out_3 | demultiplexer_2_out_3;  // Or or_6, 4 bits wide
  assign {V[4], out4} = demultiplexer_2_out_4 | demultiplexer_4_out_4 | demultiplexer_6_out_4 | demultiplexer_7_out_4;  // Or or_7, 4 bits wide

  // Other names for the same wires on the sheet: O7[2:0] = out7; O0[2:0] = out0; O6[2:0] = out6; O1[2:0] = out1;
  //   O2[2:0] = out2; O3[2:0] = out3; O4[2:0] = out4; O5[2:0] = out5; I0 = in0; I1 = in1; I2 = in2; I3 = in3;
  //   I4 = in4; I5 = in5; I6 = in6; I7 = in7
endmodule
