// Digital circuit inst-wfile.dig as structural Verilog
module inst_wfile (
  input  C,
  input  [4:0] SC_inst,
  input  [4:0] FL_inst,
  input  SC_sel,
  input  FL_sel,
  input  SC_e,
  input  FL_e,
  input  [3:0] Inst,
  input  [4:0] W,
  input  [4:0] RA,
  input  [4:0] RB,
  input  E1,
  input  [4:0] W_com1,
  input  com1,
  input  [4:0] W_com2,
  input  com2,
  input  [3:0] I_com1,
  input  [3:0] I_com2,
  input  res,
  output [4:0] R_A,
  output [4:0] R_B,
  output [4:0] SC_O,
  output [4:0] FL_O
);

  wire and_1_out, CE1, CE2, comparator_1_eq, comparator_2_eq, comparator_3_eq, FL_e_t, FL_M,
       multiplexer_25_out, multiplexer_26_out, R1_e, R1_M, R2_e, R2_M, R3_e, R3_M, R4_e, R4_M, R5_e, R5_M,
       R6_e, R6_M, R7_e, R7_M, R8_e, R8_M, R9_e, R9_M, R10_e, R10_M, R11_e, R11_M, R12_e, R12_M, R13_e,
       R13_M, R14_e, R14_M, R15_e, R15_M, R16_e, R16_M, R17_e, R17_M, R18_e, R18_M, R19_e, R19_M, R20_e,
       R20_M, R21_e, R21_M, R22_e, R22_M, R23_e, R23_M, R24_e, R24_M, R25_e, R25_M, SBP_e, SBP_M, SC_e_t,
       SC_M;
  wire [4:0] multiplexer_1_out, multiplexer_2_out, multiplexer_3_out, multiplexer_4_out, multiplexer_5_out,
       multiplexer_6_out, multiplexer_7_out, multiplexer_8_out, multiplexer_9_out, multiplexer_10_out,
       multiplexer_11_out, multiplexer_12_out, multiplexer_13_out, multiplexer_14_out, multiplexer_15_out,
       multiplexer_16_out, multiplexer_17_out, multiplexer_18_out, multiplexer_19_out, multiplexer_20_out,
       multiplexer_21_out, multiplexer_22_out, multiplexer_23_out, multiplexer_24_out, multiplexer_27_out,
       multiplexer_28_out, multiplexer_29_out, multiplexer_30_out, multiplexer_31_out, multiplexer_32_out,
       multiplexer_33_out, multiplexer_34_out, R1, R2, R3, R4, R5, R6, R7, R8, R9, R10, R11, R12, R13, R14,
       R15, R16, R17, R18, R19, R20, R21, R22, R23, R24, R25, SBP;
  wire [5:2] or_1_out, or_2_out;
  wire [31:0] bitextender_1_out, demultiplexer_1_out_5, demultiplexer_2_out_5, demultiplexer_3_out_5,
       not_1_out;

  Demultiplexer #(.Selector_Bits(5)) demultiplexer_1 (
    .sel(W), .in(E1), .out_0(demultiplexer_1_out_5[31]), .out_1(demultiplexer_1_out_5[30]),
    .out_2(demultiplexer_1_out_5[29]), .out_3(demultiplexer_1_out_5[28]), .out_4(demultiplexer_1_out_5[27]),
    .out_5(demultiplexer_1_out_5[26]), .out_6(demultiplexer_1_out_5[25]), .out_7(demultiplexer_1_out_5[24]),
    .out_8(demultiplexer_1_out_5[23]), .out_9(demultiplexer_1_out_5[22]), .out_10(demultiplexer_1_out_5[21]),
    .out_11(demultiplexer_1_out_5[20]), .out_12(demultiplexer_1_out_5[19]),
    .out_13(demultiplexer_1_out_5[18]), .out_14(demultiplexer_1_out_5[17]),
    .out_15(demultiplexer_1_out_5[16]), .out_16(demultiplexer_1_out_5[15]),
    .out_17(demultiplexer_1_out_5[14]), .out_18(demultiplexer_1_out_5[13]),
    .out_19(demultiplexer_1_out_5[12]), .out_20(demultiplexer_1_out_5[11]),
    .out_21(demultiplexer_1_out_5[10]), .out_22(demultiplexer_1_out_5[9]), .out_23(demultiplexer_1_out_5[8]),
    .out_24(demultiplexer_1_out_5[7]), .out_25(demultiplexer_1_out_5[6]), .out_26(demultiplexer_1_out_5[5]),
    .out_27(demultiplexer_1_out_5[4]), .out_28(demultiplexer_1_out_5[3]), .out_29(demultiplexer_1_out_5[2]),
    .out_30(demultiplexer_1_out_5[1]), .out_31(demultiplexer_1_out_5[0]));
  Demultiplexer #(.Selector_Bits(5)) demultiplexer_2 (
    .sel(W_com1), .in(CE1), .out_0(demultiplexer_2_out_5[31]), .out_1(demultiplexer_2_out_5[30]),
    .out_2(demultiplexer_2_out_5[29]), .out_3(demultiplexer_2_out_5[28]), .out_4(demultiplexer_2_out_5[27]),
    .out_5(demultiplexer_2_out_5[26]), .out_6(demultiplexer_2_out_5[25]), .out_7(demultiplexer_2_out_5[24]),
    .out_8(demultiplexer_2_out_5[23]), .out_9(demultiplexer_2_out_5[22]), .out_10(demultiplexer_2_out_5[21]),
    .out_11(demultiplexer_2_out_5[20]), .out_12(demultiplexer_2_out_5[19]),
    .out_13(demultiplexer_2_out_5[18]), .out_14(demultiplexer_2_out_5[17]),
    .out_15(demultiplexer_2_out_5[16]), .out_16(demultiplexer_2_out_5[15]),
    .out_17(demultiplexer_2_out_5[14]), .out_18(demultiplexer_2_out_5[13]),
    .out_19(demultiplexer_2_out_5[12]), .out_20(demultiplexer_2_out_5[11]),
    .out_21(demultiplexer_2_out_5[10]), .out_22(demultiplexer_2_out_5[9]), .out_23(demultiplexer_2_out_5[8]),
    .out_24(demultiplexer_2_out_5[7]), .out_25(demultiplexer_2_out_5[6]), .out_26(demultiplexer_2_out_5[5]),
    .out_27(demultiplexer_2_out_5[4]), .out_28(demultiplexer_2_out_5[3]), .out_29(demultiplexer_2_out_5[2]),
    .out_30(demultiplexer_2_out_5[1]), .out_31(demultiplexer_2_out_5[0]));
  Multiplexer #(.Bits(5)) multiplexer_1 (.sel(R1_M), .in_0({1'b0, Inst}), .in_1(5'b10000), .out(multiplexer_1_out));
  Register #(.Bits(5)) u_R1 (.D(multiplexer_1_out), .C(C), .en(R1_e), .Q(R1));
  Multiplexer #(.Bits(5)) multiplexer_2 (.sel(R5_M), .in_0({1'b0, Inst}), .in_1(5'b10000), .out(multiplexer_2_out));
  Register #(.Bits(5)) u_R5 (.D(multiplexer_2_out), .C(C), .en(R5_e), .Q(R5));
  Multiplexer #(.Bits(5)) multiplexer_3 (.sel(R9_M), .in_0({1'b0, Inst}), .in_1(5'b10000), .out(multiplexer_3_out));
  Register #(.Bits(5)) u_R9 (.D(multiplexer_3_out), .C(C), .en(R9_e), .Q(R9));
  Multiplexer #(.Bits(5)) multiplexer_4 (.sel(R13_M), .in_0({1'b0, Inst}), .in_1(5'b10000), .out(multiplexer_4_out));
  Register #(.Bits(5)) u_R13 (.D(multiplexer_4_out), .C(C), .en(R13_e), .Q(R13));
  Multiplexer #(.Bits(5)) multiplexer_5 (.sel(R17_M), .in_0({1'b0, Inst}), .in_1(5'b10000), .out(multiplexer_5_out));
  Register #(.Bits(5)) u_R17 (.D(multiplexer_5_out), .C(C), .en(R17_e), .Q(R17));
  Multiplexer #(.Bits(5)) multiplexer_6 (.sel(R21_M), .in_0({1'b0, Inst}), .in_1(5'b10000), .out(multiplexer_6_out));
  Register #(.Bits(5)) u_R21 (.D(multiplexer_6_out), .C(C), .en(R21_e), .Q(R21));
  Multiplexer #(.Bits(5)) multiplexer_7 (.sel(R25_M), .in_0({1'b0, Inst}), .in_1(5'b10000), .out(multiplexer_7_out));
  Register #(.Bits(5)) u_R25 (.D(multiplexer_7_out), .C(C), .en(R25_e), .Q(R25));
  Multiplexer #(.Bits(5)) multiplexer_8 (.sel(SBP_M), .in_0({1'b0, Inst}), .in_1(5'b10000), .out(multiplexer_8_out));
  Register #(.Bits(5)) u_SBP (.D(multiplexer_8_out), .C(C), .en(SBP_e), .Q(SBP));
  Demultiplexer #(.Selector_Bits(5)) demultiplexer_3 (
    .sel(W_com2), .in(CE2), .out_0(demultiplexer_3_out_5[31]), .out_1(demultiplexer_3_out_5[30]),
    .out_2(demultiplexer_3_out_5[29]), .out_3(demultiplexer_3_out_5[28]), .out_4(demultiplexer_3_out_5[27]),
    .out_5(demultiplexer_3_out_5[26]), .out_6(demultiplexer_3_out_5[25]), .out_7(demultiplexer_3_out_5[24]),
    .out_8(demultiplexer_3_out_5[23]), .out_9(demultiplexer_3_out_5[22]), .out_10(demultiplexer_3_out_5[21]),
    .out_11(demultiplexer_3_out_5[20]), .out_12(demultiplexer_3_out_5[19]),
    .out_13(demultiplexer_3_out_5[18]), .out_14(demultiplexer_3_out_5[17]),
    .out_15(demultiplexer_3_out_5[16]), .out_16(demultiplexer_3_out_5[15]),
    .out_17(demultiplexer_3_out_5[14]), .out_18(demultiplexer_3_out_5[13]),
    .out_19(demultiplexer_3_out_5[12]), .out_20(demultiplexer_3_out_5[11]),
    .out_21(demultiplexer_3_out_5[10]), .out_22(demultiplexer_3_out_5[9]), .out_23(demultiplexer_3_out_5[8]),
    .out_24(demultiplexer_3_out_5[7]), .out_25(demultiplexer_3_out_5[6]), .out_26(demultiplexer_3_out_5[5]),
    .out_27(demultiplexer_3_out_5[4]), .out_28(demultiplexer_3_out_5[3]), .out_29(demultiplexer_3_out_5[2]),
    .out_30(demultiplexer_3_out_5[1]), .out_31(demultiplexer_3_out_5[0]));
  BitExtender #(.inputBits(1), .outputBits(32)) bitextender_1 (.in(res), .out(bitextender_1_out));
  Multiplexer #(.Bits(5)) multiplexer_9 (.sel(R2_M), .in_0({1'b0, Inst}), .in_1(5'b10000), .out(multiplexer_9_out));
  Multiplexer #(.Bits(5)) multiplexer_10 (.sel(R6_M), .in_0({1'b0, Inst}), .in_1(5'b10000), .out(multiplexer_10_out));
  Multiplexer #(.Bits(5)) multiplexer_11 (.sel(R10_M), .in_0({1'b0, Inst}), .in_1(5'b10000), .out(multiplexer_11_out));
  Multiplexer #(.Bits(5)) multiplexer_12 (.sel(R14_M), .in_0({1'b0, Inst}), .in_1(5'b10000), .out(multiplexer_12_out));
  Multiplexer #(.Bits(5)) multiplexer_13 (.sel(R18_M), .in_0({1'b0, Inst}), .in_1(5'b10000), .out(multiplexer_13_out));
  Multiplexer #(.Bits(5)) multiplexer_14 (.sel(R22_M), .in_0({1'b0, Inst}), .in_1(5'b10000), .out(multiplexer_14_out));
  assign {R1_M, R2_M, R3_M, R4_M, R5_M, R6_M, R7_M, R8_M, R9_M, R10_M, R11_M, R12_M, R13_M, R14_M, R15_M, R16_M, R17_M, R18_M, R19_M, R20_M, R21_M, R22_M, R23_M, R24_M, R25_M, SBP_M, or_1_out, SC_M, FL_M} = not_1_out | bitextender_1_out;  // Or or_1, 32 bits wide
  assign not_1_out = ~demultiplexer_1_out_5;  // Not not_1, 32 bits wide
  Register #(.Bits(5)) u_R2 (.D(multiplexer_9_out), .C(C), .en(R2_e), .Q(R2));
  Register #(.Bits(5)) u_R6 (.D(multiplexer_10_out), .C(C), .en(R6_e), .Q(R6));
  Register #(.Bits(5)) u_R10 (.D(multiplexer_11_out), .C(C), .en(R10_e), .Q(R10));
  Register #(.Bits(5)) u_R14 (.D(multiplexer_12_out), .C(C), .en(R14_e), .Q(R14));
  Register #(.Bits(5)) u_R18 (.D(multiplexer_13_out), .C(C), .en(R18_e), .Q(R18));
  Register #(.Bits(5)) u_R22 (.D(multiplexer_14_out), .C(C), .en(R22_e), .Q(R22));
  assign {R1_e, R2_e, R3_e, R4_e, R5_e, R6_e, R7_e, R8_e, R9_e, R10_e, R11_e, R12_e, R13_e, R14_e, R15_e, R16_e, R17_e, R18_e, R19_e, R20_e, R21_e, R22_e, R23_e, R24_e, R25_e, SBP_e, or_2_out, SC_e_t, FL_e_t} = demultiplexer_3_out_5 | demultiplexer_2_out_5 | demultiplexer_1_out_5 | bitextender_1_out;  // Or or_2, 32 bits wide
  Multiplexer #(.Bits(5)) multiplexer_15 (.sel(SC_M), .in_0({1'b0, Inst}), .in_1(5'b10000), .out(multiplexer_15_out));
  Multiplexer #(.Bits(5)) multiplexer_16 (.sel(FL_M), .in_0({1'b0, Inst}), .in_1(5'b10000), .out(multiplexer_16_out));
  Comparator #(.Bits(5)) comparator_1 (.a({5{1'b1}}), .b(W), .eq(comparator_1_eq));  // open: gt, lt
  Multiplexer #(.Bits(5)) multiplexer_17 (.sel(R3_M), .in_0({1'b0, Inst}), .in_1(5'b10000), .out(multiplexer_17_out));
  Multiplexer #(.Bits(5)) multiplexer_18 (.sel(R7_M), .in_0({1'b0, Inst}), .in_1(5'b10000), .out(multiplexer_18_out));
  Multiplexer #(.Bits(5)) multiplexer_19 (.sel(R11_M), .in_0({1'b0, Inst}), .in_1(5'b10000), .out(multiplexer_19_out));
  Multiplexer #(.Bits(5)) multiplexer_20 (.sel(R15_M), .in_0({1'b0, Inst}), .in_1(5'b10000), .out(multiplexer_20_out));
  Multiplexer #(.Bits(5)) multiplexer_21 (.sel(R19_M), .in_0({1'b0, Inst}), .in_1(5'b10000), .out(multiplexer_21_out));
  Multiplexer #(.Bits(5)) multiplexer_22 (.sel(R23_M), .in_0({1'b0, Inst}), .in_1(5'b10000), .out(multiplexer_22_out));
  Multiplexer #(.Bits(5)) multiplexer_23 (
    .sel(SC_sel), .in_0(multiplexer_15_out), .in_1(SC_inst), .out(multiplexer_23_out));
  Multiplexer #(.Bits(5)) multiplexer_24 (
    .sel(and_1_out), .in_0(multiplexer_16_out), .in_1(FL_inst), .out(multiplexer_24_out));
  Register #(.Bits(5)) u_R3 (.D(multiplexer_17_out), .C(C), .en(R3_e), .Q(R3));
  Register #(.Bits(5)) u_R7 (.D(multiplexer_18_out), .C(C), .en(R7_e), .Q(R7));
  Register #(.Bits(5)) u_R11 (.D(multiplexer_19_out), .C(C), .en(R11_e), .Q(R11));
  Register #(.Bits(5)) u_R15 (.D(multiplexer_20_out), .C(C), .en(R15_e), .Q(R15));
  Register #(.Bits(5)) u_R19 (.D(multiplexer_21_out), .C(C), .en(R19_e), .Q(R19));
  Register #(.Bits(5)) u_R23 (.D(multiplexer_22_out), .C(C), .en(R23_e), .Q(R23));
  Multiplexer multiplexer_25 (.sel(SC_sel), .in_0(SC_e_t), .in_1(SC_e), .out(multiplexer_25_out));
  and and_1 (and_1_out, ~comparator_1_eq, FL_sel);  // And
  Multiplexer multiplexer_26 (.sel(and_1_out), .in_0(FL_e_t), .in_1(FL_e), .out(multiplexer_26_out));
  Multiplexer #(.Bits(5)) multiplexer_27 (.sel(R4_M), .in_0({1'b0, Inst}), .in_1(5'b10000), .out(multiplexer_27_out));
  Register #(.Bits(5)) u_R4 (.D(multiplexer_27_out), .C(C), .en(R4_e), .Q(R4));
  Multiplexer #(.Bits(5)) multiplexer_28 (.sel(R8_M), .in_0({1'b0, Inst}), .in_1(5'b10000), .out(multiplexer_28_out));
  Register #(.Bits(5)) u_R8 (.D(multiplexer_28_out), .C(C), .en(R8_e), .Q(R8));
  Multiplexer #(.Bits(5)) multiplexer_29 (.sel(R12_M), .in_0({1'b0, Inst}), .in_1(5'b10000), .out(multiplexer_29_out));
  Register #(.Bits(5)) u_R12 (.D(multiplexer_29_out), .C(C), .en(R12_e), .Q(R12));
  Multiplexer #(.Bits(5)) multiplexer_30 (.sel(R16_M), .in_0({1'b0, Inst}), .in_1(5'b10000), .out(multiplexer_30_out));
  Register #(.Bits(5)) u_R16 (.D(multiplexer_30_out), .C(C), .en(R16_e), .Q(R16));
  Multiplexer #(.Bits(5)) multiplexer_31 (.sel(R20_M), .in_0({1'b0, Inst}), .in_1(5'b10000), .out(multiplexer_31_out));
  Register #(.Bits(5)) u_R20 (.D(multiplexer_31_out), .C(C), .en(R20_e), .Q(R20));
  Multiplexer #(.Bits(5)) multiplexer_32 (.sel(R24_M), .in_0({1'b0, Inst}), .in_1(5'b10000), .out(multiplexer_32_out));
  Register #(.Bits(5)) u_R24 (.D(multiplexer_32_out), .C(C), .en(R24_e), .Q(R24));
  Register #(.Bits(5)) SC (.D(multiplexer_23_out), .C(C), .en(multiplexer_25_out), .Q(SC_O));
  Register #(.Bits(5)) FL (.D(multiplexer_24_out), .C(C), .en(multiplexer_26_out), .Q(FL_O));
  Multiplexer #(.Selector_Bits(5), .Bits(5)) multiplexer_33 (
    .sel(W_com1), .in_0(R1), .in_1(R2), .in_2(R3), .in_3(R4), .in_4(R5), .in_5(R6), .in_6(R7), .in_7(R8),
    .in_8(R9), .in_9(R10), .in_10(R11), .in_11(R12), .in_12(R13), .in_13(R14), .in_14(R15), .in_15(R16),
    .in_16(R17), .in_17(R18), .in_18(R19), .in_19(R20), .in_20(R21), .in_21(R22), .in_22(R23), .in_23(R24),
    .in_24(R25), .in_25(SBP), .in_26(5'b10000), .in_27(5'b10000), .in_28(5'b10000), .in_29(5'b10000),
    .in_30(SC_O), .in_31(FL_O), .out(multiplexer_33_out));
  Comparator #(.Bits(4)) comparator_2 (.a(I_com1), .b(multiplexer_33_out[3:0]), .eq(comparator_2_eq));  // open: gt, lt
  and and_2 (CE1, comparator_2_eq, ~multiplexer_33_out[4], com1);  // And
  Multiplexer #(.Selector_Bits(5), .Bits(5)) multiplexer_34 (
    .sel(W_com2), .in_0(R1), .in_1(R2), .in_2(R3), .in_3(R4), .in_4(R5), .in_5(R6), .in_6(R7), .in_7(R8),
    .in_8(R9), .in_9(R10), .in_10(R11), .in_11(R12), .in_12(R13), .in_13(R14), .in_14(R15), .in_15(R16),
    .in_16(R17), .in_17(R18), .in_18(R19), .in_19(R20), .in_20(R21), .in_21(R22), .in_22(R23), .in_23(R24),
    .in_24(R25), .in_25(SBP), .in_26(5'b10000), .in_27(5'b10000), .in_28(5'b10000), .in_29(5'b10000),
    .in_30(SC_O), .in_31(FL_O), .out(multiplexer_34_out));
  Comparator #(.Bits(4)) comparator_3 (.a(I_com2), .b(multiplexer_34_out[3:0]), .eq(comparator_3_eq));  // open: gt, lt
  and and_3 (CE2, comparator_3_eq, ~multiplexer_34_out[4], com2);  // And
  Multiplexer #(.Selector_Bits(5), .Bits(5)) multiplexer_35 (
    .sel(RA), .in_0(R1), .in_1(R2), .in_2(R3), .in_3(R4), .in_4(R5), .in_5(R6), .in_6(R7), .in_7(R8),
    .in_8(R9), .in_9(R10), .in_10(R11), .in_11(R12), .in_12(R13), .in_13(R14), .in_14(R15), .in_15(R16),
    .in_16(R17), .in_17(R18), .in_18(R19), .in_19(R20), .in_20(R21), .in_21(R22), .in_22(R23), .in_23(R24),
    .in_24(R25), .in_25(SBP), .in_26(5'b10000), .in_27(5'b10000), .in_28(5'b10000), .in_29(5'b10000),
    .in_30(SC_O), .in_31(FL_O), .out(R_A));
  Multiplexer #(.Selector_Bits(5), .Bits(5)) multiplexer_36 (
    .sel(RB), .in_0(R1), .in_1(R2), .in_2(R3), .in_3(R4), .in_4(R5), .in_5(R6), .in_6(R7), .in_7(R8),
    .in_8(R9), .in_9(R10), .in_10(R11), .in_11(R12), .in_12(R13), .in_13(R14), .in_14(R15), .in_15(R16),
    .in_16(R17), .in_17(R18), .in_18(R19), .in_19(R20), .in_20(R21), .in_21(R22), .in_22(R23), .in_23(R24),
    .in_24(R25), .in_25(SBP), .in_26(5'b10000), .in_27(5'b10000), .in_28(5'b10000), .in_29(5'b10000),
    .in_30(SC_O), .in_31(FL_O), .out(R_B));

  // Other names for the same wires on the sheet: E = E1; FL[4:0] = FL_O; FL_e__EX = FL_e; FL_i[4:0] = FL_inst;
  //   D_in[3:0] = Inst; inst_com1[3:0] = I_com1; inst_com2[3:0] = I_com2; RA_sel[4:0] = RA; RB_sel[4:0] = RB;
  //   RC1_sel[4:0] = W_com1; RC2_sel[4:0] = W_com2; reset = res; RW_sel[4:0] = W; SC[4:0] = SC_O; SC_e__EX = SC_e;
  //   SC_i[4:0] = SC_inst

  // Notes on the sheet:
  //   SC_inst: data input for SC
  //   FL_inst: data input for FL
  //   SC_sel: enable SC extern mode
  //   FL_sel: enable FL extern mode
  //   SC_e: SC register enable
  //   FL_e: FL register enable
  //   Inst: data in
  //   W: register to write:
  //   0~25: general
  //   26: zero
  //   27: one
  //   28: full
  //   29: program counter
  //   30: stack counter
  //   31: flag
  //   RA: register to read:
  //   0~25: general
  //   26: zero
  //   27: one
  //   28: full
  //   29: program counter
  //   30: stack counter
  //   31: flag
  //   RB: register to read:
  //   0~25: general
  //   26: zero
  //   27: one
  //   28: full
  //   29: program counter
  //   30: stack counter
  //   31: flag
  //   R_A: register out a
  //   R_B: register out b
  //   SC_O: SC out
  //   FL_O: FL out
  //   E1: enable
  //   W_com1: register to write:
  //   0~25: general
  //   26: zero
  //   27: one
  //   28: full
  //   29: program counter
  //   30: stack counter
  //   31: flag
  //   com1: enable
  //   W_com2: register to write:
  //   0~25: general
  //   26: zero
  //   27: one
  //   28: full
  //   29: program counter
  //   30: stack counter
  //   31: flag
  //   com2: enable
  //   I_com1: enable
  //   I_com2: enable
  //   res: reset
endmodule
