// Digital circuit load-buffer.dig as structural Verilog
module load_buffer (
  input  W_d,
  input  C,
  input  [31:0] D,
  input  [31:0] A,
  input  [3:0] inst,
  input  [3:0] com1_id,
  input  [3:0] com2_id,
  input  com1,
  input  com2,
  input  st_ep,
  input  [3:0] st_id,
  input  epoch,
  input  [31:0] st_addr,
  input  W_id,
  input  [3:0] inst_W,
  input  LD,
  input  [31:0] st_data,
  output [31:0] D_O,
  output [31:0] A_O,
  output V,
  output full,
  output ld_V,
  output [31:0] ld_D
);

  wire and_1_out, and_2_out, and_3_out, and_4_out, and_6_out, and_10_out, and_11_out, comparator_1_eq,
       comparator_2_eq, comparator_3_eq, comparator_4_eq, comparator_5_gt, comparator_5_lt, M1_AE, M1_AV,
       M1_CMP, M1_COM, M1_DE, M1_DV, M1_IE, M1_SEL, M1_VI, M1_VO, M1_WTN, M2_CMP, M2_COM, M2_DE, M2_IE,
       M2_SEL, M2_VI, M2_VO, M2_WTN, M3_CMP, M3_COM, M3_DE, M3_IE, M3_SEL, M3_VI, M3_VO, M3_WTN, M4_CMP,
       M4_COM, M4_DE, M4_IE, M4_SEL, M4_VI, M4_VO, M4_WTN, multiplexer_7_out, or_3_out,
       priorityencoder_2_any, priorityencoder_3_any, priorityencoder_4_any, register_12_q, xor_1_out;
  wire [1:0] empty_id, priorityencoder_1_num, priorityencoder_2_num, priorityencoder_4_num, register_2_q,
       register_3_q, register_5_q, register_8_q, sel_com;
  wire [3:0] and_5_out, bitextender_1_out, bitselector_1_out, demultiplexer_1_out_0, multiplexer_3_out,
       not_1_out, not_3_out, or_2_out, priority_4_1_out1, register_1_q, register_11_q;
  wire [31:0] M1_A, M1_D, M2_A, M2_D, M3_A, M3_D, M4_A, M4_D, multiplexer_6_out, st_D;

  PriorityEncoder #(.Selector_Bits(2)) priorityencoder_1 (
    .in0(M1_CMP), .in1(M2_CMP), .in2(M3_CMP), .in3(M4_CMP), .num(priorityencoder_1_num), .any(ld_V));
  PriorityEncoder #(.Selector_Bits(2)) priorityencoder_2 (
    .in0(M1_SEL), .in1(M2_SEL), .in2(M3_SEL), .in3(M4_SEL), .num(priorityencoder_2_num),
    .any(priorityencoder_2_any));
  Multiplexer #(.Selector_Bits(2), .Bits(32)) multiplexer_1 (
    .sel(sel_com), .in_0(M1_D), .in_1(M2_D), .in_2(M3_D), .in_3(M4_D), .out(D_O));
  priority_4 priority_4_1 (
    .on(1'b1), .in1(and_5_out[0]), .in2(and_5_out[1]), .in3(and_5_out[2]), .in4(and_5_out[3]),
    .out1(priority_4_1_out1[3]), .out2(priority_4_1_out1[2]), .out3(priority_4_1_out1[1]),
    .out4(priority_4_1_out1[0]));  // open: v
  and and_1 (and_1_out, not_3_out[3], 1'b1);
  assign not_1_out = ~{M4_VO, M3_VO, M2_VO, M1_VO};  // Not not_1, 4 bits wide
  Demultiplexer #(.Selector_Bits(2)) demultiplexer_1 (
    .sel(sel_com), .in(V), .out_0(demultiplexer_1_out_0[0]), .out_1(demultiplexer_1_out_0[1]),
    .out_2(demultiplexer_1_out_0[2]), .out_3(demultiplexer_1_out_0[3]));
  Demultiplexer #(.Selector_Bits(2)) demultiplexer_2 (
    .sel(empty_id), .in(W_id), .out_0(M1_VI), .out_1(M2_VI), .out_2(M3_VI), .out_3(M4_VI));
  Register register_1 (.D(and_1_out), .C(C), .en(or_2_out[3]), .Q(register_1_q[0]));
  BitSelector #(.Selector_Bits(2)) bitselector_1 (
    .in({M4_COM, M3_COM, M2_COM, M1_COM}), .sel(register_2_q), .out(bitselector_1_out[0]));
  Register #(.Bits(2)) register_2 (.D(empty_id), .C(C), .en(W_id), .Q(register_2_q));
  PriorityEncoder #(.Selector_Bits(2)) priorityencoder_3 (
    .in0(not_1_out[0]), .in1(not_1_out[1]), .in2(not_1_out[2]), .in3(not_1_out[3]), .num(empty_id),
    .any(priorityencoder_3_any));
  assign {M4_IE, M3_IE, M2_IE, M1_IE} = demultiplexer_1_out_0 | {M4_VI, M3_VI, M2_VI, M1_VI};  // Or or_1, 4 bits wide
  and and_2 (and_2_out, W_d, priorityencoder_2_any);
  and and_3 (and_3_out, not_3_out[2], register_1_q[0]);
  Register #(.Bits(2)) register_3 (.D(register_2_q), .C(C), .en(W_id), .Q(register_3_q));
  not not_2 (full, priorityencoder_3_any);
  Demultiplexer #(.Selector_Bits(2)) demultiplexer_3 (
    .sel(priorityencoder_2_num), .in(and_2_out), .out_0(M1_DE), .out_1(M2_DE), .out_2(M3_DE), .out_3(M4_DE));
  Multiplexer #(.Selector_Bits(2), .Bits(32)) multiplexer_2 (
    .sel(sel_com), .in_0(M1_A), .in_1(M2_A), .in_2(M3_A), .in_3(M4_A), .out(A_O));
  Multiplexer #(.Bits(4)) multiplexer_3 (
    .sel(W_id), .in_0(priority_4_1_out1), .in_1({1'b0, priority_4_1_out1[3:1]}), .out(multiplexer_3_out));
  Register register_4 (.D(and_3_out), .C(C), .en(or_2_out[2]), .Q(register_1_q[1]));
  BitSelector #(.Selector_Bits(2)) bitselector_2 (
    .in({M4_COM, M3_COM, M2_COM, M1_COM}), .sel(register_3_q), .out(bitselector_1_out[1]));
  Multiplexer #(.Selector_Bits(2), .Bits(32)) multiplexer_4 (
    .sel(priorityencoder_1_num), .in_0(M1_D), .in_1(M2_D), .in_2(M3_D), .in_3(M4_D), .out(ld_D));
  assign not_3_out = ~multiplexer_3_out;  // Not not_3, 4 bits wide
  BitExtender #(.inputBits(1), .outputBits(4)) bitextender_1 (.in(W_id), .out(bitextender_1_out));
  and and_4 (and_4_out, not_3_out[1], register_1_q[1]);
  Register #(.Bits(2)) register_5 (.D(register_3_q), .C(C), .en(W_id), .Q(register_5_q));
  Demultiplexer #(.Selector_Bits(2)) demultiplexer_4 (
    .sel(sel_com), .in(V), .out_0(M1_WTN), .out_1(M2_WTN), .out_2(M3_WTN), .out_3(M4_WTN));
  assign or_2_out = priority_4_1_out1 | bitextender_1_out;  // Or or_2, 4 bits wide
  Register register_6 (.D(and_4_out), .C(C), .en(or_2_out[1]), .Q(register_1_q[2]));
  assign and_5_out = register_1_q & bitselector_1_out;  // And and_5, 4 bits wide
  BitSelector #(.Selector_Bits(2)) bitselector_3 (
    .in({M4_COM, M3_COM, M2_COM, M1_COM}), .sel(register_5_q), .out(bitselector_1_out[2]));
  and and_6 (and_6_out, not_3_out[0], register_1_q[2]);
  Register register_7 (.D(and_6_out), .C(C), .en(or_2_out[0]), .Q(register_1_q[3]));
  Register #(.Bits(2)) register_8 (.D(register_5_q), .C(C), .en(W_id), .Q(register_8_q));
  PriorityEncoder #(.Selector_Bits(2)) priorityencoder_4 (
    .in0(and_5_out[0]), .in1(and_5_out[1]), .in2(and_5_out[2]), .in3(and_5_out[3]),
    .num(priorityencoder_4_num), .any(priorityencoder_4_any));
  BitSelector #(.Selector_Bits(2)) bitselector_4 (
    .in({M4_COM, M3_COM, M2_COM, M1_COM}), .sel(register_8_q), .out(bitselector_1_out[3]));
  Multiplexer #(.Selector_Bits(2), .Bits(2)) multiplexer_5 (
    .sel(priorityencoder_4_num), .in_0(register_2_q), .in_1(register_3_q), .in_2(register_5_q),
    .in_3(register_8_q), .out(sel_com));
  and and_7 (V, priorityencoder_4_any, LD);
  RS_FF rs_ff_1 (.S(M1_IE), .C(C), .R(or_3_out), .Q(M1_VO));  // open: nQ
  Comparator #(.Bits(32)) comparator_1 (.a(st_addr), .b(M1_A), .eq(comparator_1_eq));  // open: gt, lt
  Register #(.Bits(32)) register_9 (.D(A), .C(C), .en(M1_AE), .Q(M1_A));
  RS_FF rs_ff_2 (.S(M1_AE), .C(C), .R(or_3_out), .Q(M1_AV));  // open: nQ
  Register #(.Bits(32)) register_10 (.D(multiplexer_6_out), .C(C), .en(M1_DE), .Q(M1_D));
  RS_FF rs_ff_3 (.S(M1_DE), .C(C), .R(or_3_out), .Q(M1_DV));  // open: nQ
  Comparator #(.Bits(4)) comparator_2 (.a(register_11_q), .b(inst_W), .eq(comparator_2_eq));  // open: gt, lt
  Comparator #(.Bits(4)) comparator_3 (.a(register_11_q), .b(com1_id), .eq(comparator_3_eq));  // open: gt, lt
  Comparator #(.Bits(4)) comparator_4 (.a(register_11_q), .b(com2_id), .eq(comparator_4_eq));  // open: gt, lt
  Register #(.Bits(4)) register_11 (.D(inst), .C(C), .en(M1_IE), .Q(register_11_q));
  Register register_12 (.D(epoch), .C(C), .en(M1_IE), .Q(register_12_q));
  Comparator #(.Bits(4)) comparator_5 (
    .a(register_11_q), .b(st_id), .gt(comparator_5_gt), .lt(comparator_5_lt));  // open: eq
  xor xor_1 (xor_1_out, register_12_q, st_ep);
  and and_8 (M1_CMP, M1_VO, comparator_1_eq, multiplexer_7_out);
  Multiplexer #(.Bits(32)) multiplexer_6 (.sel(M1_CMP), .in_0(D), .in_1(st_D), .out(multiplexer_6_out));
  and and_9 (M1_SEL, M1_VO, comparator_2_eq);
  or or_3 (or_3_out, and_11_out, and_10_out);
  and and_10 (and_10_out, comparator_3_eq, com1);
  and and_11 (and_11_out, comparator_4_eq, com2);
  Multiplexer multiplexer_7 (.sel(xor_1_out), .in_0(comparator_5_gt), .in_1(comparator_5_lt), .out(multiplexer_7_out));

  // Other names for the same wires on the sheet: comp_addr[31:0] = st_addr; comp_ep = st_ep; comp_id[3:0] = st_id;
  //   ld_O[31:0] = ld_D
endmodule
