// Digital circuit map-inst2reg.dig as structural Verilog
module map_inst2reg (
  input  [4:0] I1,
  input  [4:0] I2,
  input  E1,
  input  E2,
  input  [4:0] R1,
  input  [4:0] R2,
  input  [4:0] com2_id,
  input  C,
  input  com1,
  input  com2,
  input  [4:0] com1_id,
  output [4:0] O1,
  output [4:0] O2,
  output V1,
  output V2
);

  wire [4:0] multiplexer_1_out, multiplexer_2_out, multiplexer_3_out, multiplexer_4_out, multiplexer_5_out,
       multiplexer_6_out, multiplexer_7_out, multiplexer_8_out, multiplexer_9_out, multiplexer_10_out,
       multiplexer_11_out, multiplexer_12_out, multiplexer_13_out, multiplexer_14_out, multiplexer_15_out,
       multiplexer_16_out, multiplexer_17_out, multiplexer_18_out, multiplexer_19_out, multiplexer_20_out,
       multiplexer_21_out, multiplexer_22_out, multiplexer_23_out, multiplexer_24_out, multiplexer_25_out,
       multiplexer_26_out;
  wire [5:0] register_1_q, register_2_q, register_3_q, register_4_q, register_5_q, register_6_q,
       register_7_q, register_8_q, register_9_q, register_10_q, register_11_q, register_12_q, register_13_q,
       register_14_q, register_15_q, register_16_q, register_17_q, register_18_q, register_19_q,
       register_20_q, register_21_q, register_22_q, register_23_q, register_24_q, register_25_q,
       register_26_q;
  wire [31:0] demultiplexer_1_out_8, demultiplexer_2_out_7, demultiplexer_3_out_5, demultiplexer_4_out_4,
       or_1_out, or_2_out;

  Demultiplexer #(.Selector_Bits(5)) demultiplexer_1 (
    .sel(com1_id), .in(com1), .out_0(demultiplexer_1_out_8[0]), .out_1(demultiplexer_1_out_8[1]),
    .out_2(demultiplexer_1_out_8[2]), .out_3(demultiplexer_1_out_8[3]), .out_4(demultiplexer_1_out_8[4]),
    .out_5(demultiplexer_1_out_8[5]), .out_6(demultiplexer_1_out_8[6]), .out_7(demultiplexer_1_out_8[7]),
    .out_8(demultiplexer_1_out_8[8]), .out_9(demultiplexer_1_out_8[9]), .out_10(demultiplexer_1_out_8[10]),
    .out_11(demultiplexer_1_out_8[11]), .out_12(demultiplexer_1_out_8[12]),
    .out_13(demultiplexer_1_out_8[13]), .out_14(demultiplexer_1_out_8[14]),
    .out_15(demultiplexer_1_out_8[15]), .out_16(demultiplexer_1_out_8[16]),
    .out_17(demultiplexer_1_out_8[17]), .out_18(demultiplexer_1_out_8[18]),
    .out_19(demultiplexer_1_out_8[19]), .out_20(demultiplexer_1_out_8[20]),
    .out_21(demultiplexer_1_out_8[21]), .out_22(demultiplexer_1_out_8[22]),
    .out_23(demultiplexer_1_out_8[23]), .out_24(demultiplexer_1_out_8[24]),
    .out_25(demultiplexer_1_out_8[25]), .out_26(demultiplexer_1_out_8[26]),
    .out_27(demultiplexer_1_out_8[27]), .out_28(demultiplexer_1_out_8[28]),
    .out_29(demultiplexer_1_out_8[29]), .out_30(demultiplexer_1_out_8[30]), .out_31(demultiplexer_1_out_8[31]));
  Demultiplexer #(.Selector_Bits(5)) demultiplexer_2 (
    .sel(com2_id), .in(com2), .out_0(demultiplexer_2_out_7[0]), .out_1(demultiplexer_2_out_7[1]),
    .out_2(demultiplexer_2_out_7[2]), .out_3(demultiplexer_2_out_7[3]), .out_4(demultiplexer_2_out_7[4]),
    .out_5(demultiplexer_2_out_7[5]), .out_6(demultiplexer_2_out_7[6]), .out_7(demultiplexer_2_out_7[7]),
    .out_8(demultiplexer_2_out_7[8]), .out_9(demultiplexer_2_out_7[9]), .out_10(demultiplexer_2_out_7[10]),
    .out_11(demultiplexer_2_out_7[11]), .out_12(demultiplexer_2_out_7[12]),
    .out_13(demultiplexer_2_out_7[13]), .out_14(demultiplexer_2_out_7[14]),
    .out_15(demultiplexer_2_out_7[15]), .out_16(demultiplexer_2_out_7[16]),
    .out_17(demultiplexer_2_out_7[17]), .out_18(demultiplexer_2_out_7[18]),
    .out_19(demultiplexer_2_out_7[19]), .out_20(demultiplexer_2_out_7[20]),
    .out_21(demultiplexer_2_out_7[21]), .out_22(demultiplexer_2_out_7[22]),
    .out_23(demultiplexer_2_out_7[23]), .out_24(demultiplexer_2_out_7[24]),
    .out_25(demultiplexer_2_out_7[25]), .out_26(demultiplexer_2_out_7[26]),
    .out_27(demultiplexer_2_out_7[27]), .out_28(demultiplexer_2_out_7[28]),
    .out_29(demultiplexer_2_out_7[29]), .out_30(demultiplexer_2_out_7[30]), .out_31(demultiplexer_2_out_7[31]));
  Demultiplexer #(.Selector_Bits(5)) demultiplexer_3 (
    .sel(I1), .in(E1), .out_0(demultiplexer_3_out_5[0]), .out_1(demultiplexer_3_out_5[1]),
    .out_2(demultiplexer_3_out_5[2]), .out_3(demultiplexer_3_out_5[3]), .out_4(demultiplexer_3_out_5[4]),
    .out_5(demultiplexer_3_out_5[5]), .out_6(demultiplexer_3_out_5[6]), .out_7(demultiplexer_3_out_5[7]),
    .out_8(demultiplexer_3_out_5[8]), .out_9(demultiplexer_3_out_5[9]), .out_10(demultiplexer_3_out_5[10]),
    .out_11(demultiplexer_3_out_5[11]), .out_12(demultiplexer_3_out_5[12]),
    .out_13(demultiplexer_3_out_5[13]), .out_14(demultiplexer_3_out_5[14]),
    .out_15(demultiplexer_3_out_5[15]), .out_16(demultiplexer_3_out_5[16]),
    .out_17(demultiplexer_3_out_5[17]), .out_18(demultiplexer_3_out_5[18]),
    .out_19(demultiplexer_3_out_5[19]), .out_20(demultiplexer_3_out_5[20]),
    .out_21(demultiplexer_3_out_5[21]), .out_22(demultiplexer_3_out_5[22]),
    .out_23(demultiplexer_3_out_5[23]), .out_24(demultiplexer_3_out_5[24]),
    .out_25(demultiplexer_3_out_5[25]), .out_26(demultiplexer_3_out_5[26]),
    .out_27(demultiplexer_3_out_5[27]), .out_28(demultiplexer_3_out_5[28]),
    .out_29(demultiplexer_3_out_5[29]), .out_30(demultiplexer_3_out_5[30]), .out_31(demultiplexer_3_out_5[31]));
  Demultiplexer #(.Selector_Bits(5)) demultiplexer_4 (
    .sel(I2), .in(E2), .out_0(demultiplexer_4_out_4[0]), .out_1(demultiplexer_4_out_4[1]),
    .out_2(demultiplexer_4_out_4[2]), .out_3(demultiplexer_4_out_4[3]), .out_4(demultiplexer_4_out_4[4]),
    .out_5(demultiplexer_4_out_4[5]), .out_6(demultiplexer_4_out_4[6]), .out_7(demultiplexer_4_out_4[7]),
    .out_8(demultiplexer_4_out_4[8]), .out_9(demultiplexer_4_out_4[9]), .out_10(demultiplexer_4_out_4[10]),
    .out_11(demultiplexer_4_out_4[11]), .out_12(demultiplexer_4_out_4[12]),
    .out_13(demultiplexer_4_out_4[13]), .out_14(demultiplexer_4_out_4[14]),
    .out_15(demultiplexer_4_out_4[15]), .out_16(demultiplexer_4_out_4[16]),
    .out_17(demultiplexer_4_out_4[17]), .out_18(demultiplexer_4_out_4[18]),
    .out_19(demultiplexer_4_out_4[19]), .out_20(demultiplexer_4_out_4[20]),
    .out_21(demultiplexer_4_out_4[21]), .out_22(demultiplexer_4_out_4[22]),
    .out_23(demultiplexer_4_out_4[23]), .out_24(demultiplexer_4_out_4[24]),
    .out_25(demultiplexer_4_out_4[25]), .out_26(demultiplexer_4_out_4[26]),
    .out_27(demultiplexer_4_out_4[27]), .out_28(demultiplexer_4_out_4[28]),
    .out_29(demultiplexer_4_out_4[29]), .out_30(demultiplexer_4_out_4[30]), .out_31(demultiplexer_4_out_4[31]));
  assign or_1_out = demultiplexer_3_out_5 | demultiplexer_4_out_4;  // Or or_1, 32 bits wide
  assign or_2_out = demultiplexer_1_out_8 | demultiplexer_2_out_7 | demultiplexer_3_out_5 | demultiplexer_4_out_4;  // Or or_2, 32 bits wide
  Multiplexer #(.Bits(5)) multiplexer_1 (.sel(demultiplexer_4_out_4[0]), .in_0(R1), .in_1(R2), .out(multiplexer_1_out));
  Multiplexer #(.Bits(5)) multiplexer_2 (.sel(demultiplexer_4_out_4[1]), .in_0(R1), .in_1(R2), .out(multiplexer_2_out));
  Multiplexer #(.Bits(5)) multiplexer_3 (.sel(demultiplexer_4_out_4[2]), .in_0(R1), .in_1(R2), .out(multiplexer_3_out));
  Multiplexer #(.Bits(5)) multiplexer_4 (.sel(demultiplexer_4_out_4[3]), .in_0(R1), .in_1(R2), .out(multiplexer_4_out));
  Multiplexer #(.Bits(5)) multiplexer_5 (.sel(demultiplexer_4_out_4[4]), .in_0(R1), .in_1(R2), .out(multiplexer_5_out));
  Multiplexer #(.Bits(5)) multiplexer_6 (.sel(demultiplexer_4_out_4[5]), .in_0(R1), .in_1(R2), .out(multiplexer_6_out));
  Multiplexer #(.Bits(5)) multiplexer_7 (.sel(demultiplexer_4_out_4[6]), .in_0(R1), .in_1(R2), .out(multiplexer_7_out));
  Multiplexer #(.Bits(5)) multiplexer_8 (.sel(demultiplexer_4_out_4[7]), .in_0(R1), .in_1(R2), .out(multiplexer_8_out));
  Multiplexer #(.Bits(5)) multiplexer_9 (.sel(demultiplexer_4_out_4[8]), .in_0(R1), .in_1(R2), .out(multiplexer_9_out));
  Multiplexer #(.Bits(5)) multiplexer_10 (
    .sel(demultiplexer_4_out_4[9]), .in_0(R1), .in_1(R2), .out(multiplexer_10_out));
  Multiplexer #(.Bits(5)) multiplexer_11 (
    .sel(demultiplexer_4_out_4[10]), .in_0(R1), .in_1(R2), .out(multiplexer_11_out));
  Multiplexer #(.Bits(5)) multiplexer_12 (
    .sel(demultiplexer_4_out_4[11]), .in_0(R1), .in_1(R2), .out(multiplexer_12_out));
  Multiplexer #(.Bits(5)) multiplexer_13 (
    .sel(demultiplexer_4_out_4[12]), .in_0(R1), .in_1(R2), .out(multiplexer_13_out));
  Multiplexer #(.Bits(5)) multiplexer_14 (
    .sel(demultiplexer_4_out_4[13]), .in_0(R1), .in_1(R2), .out(multiplexer_14_out));
  Multiplexer #(.Bits(5)) multiplexer_15 (
    .sel(demultiplexer_4_out_4[14]), .in_0(R1), .in_1(R2), .out(multiplexer_15_out));
  Multiplexer #(.Bits(5)) multiplexer_16 (
    .sel(demultiplexer_4_out_4[15]), .in_0(R1), .in_1(R2), .out(multiplexer_16_out));
  Multiplexer #(.Bits(5)) multiplexer_17 (
    .sel(demultiplexer_4_out_4[16]), .in_0(R1), .in_1(R2), .out(multiplexer_17_out));
  Multiplexer #(.Bits(5)) multiplexer_18 (
    .sel(demultiplexer_4_out_4[17]), .in_0(R1), .in_1(R2), .out(multiplexer_18_out));
  Multiplexer #(.Bits(5)) multiplexer_19 (
    .sel(demultiplexer_4_out_4[18]), .in_0(R1), .in_1(R2), .out(multiplexer_19_out));
  Multiplexer #(.Bits(5)) multiplexer_20 (
    .sel(demultiplexer_4_out_4[19]), .in_0(R1), .in_1(R2), .out(multiplexer_20_out));
  Multiplexer #(.Bits(5)) multiplexer_21 (
    .sel(demultiplexer_4_out_4[20]), .in_0(R1), .in_1(R2), .out(multiplexer_21_out));
  Multiplexer #(.Bits(5)) multiplexer_22 (
    .sel(demultiplexer_4_out_4[21]), .in_0(R1), .in_1(R2), .out(multiplexer_22_out));
  Multiplexer #(.Bits(5)) multiplexer_23 (
    .sel(demultiplexer_4_out_4[22]), .in_0(R1), .in_1(R2), .out(multiplexer_23_out));
  Multiplexer #(.Bits(5)) multiplexer_24 (
    .sel(demultiplexer_4_out_4[23]), .in_0(R1), .in_1(R2), .out(multiplexer_24_out));
  Multiplexer #(.Bits(5)) multiplexer_25 (
    .sel(demultiplexer_4_out_4[24]), .in_0(R1), .in_1(R2), .out(multiplexer_25_out));
  Multiplexer #(.Bits(5)) multiplexer_26 (
    .sel(demultiplexer_4_out_4[25]), .in_0(R1), .in_1(R2), .out(multiplexer_26_out));
  Register #(.Bits(6)) register_1 (.D({or_1_out[0], multiplexer_1_out}), .C(C), .en(or_2_out[0]), .Q(register_1_q));
  Register #(.Bits(6)) register_2 (.D({or_1_out[1], multiplexer_2_out}), .C(C), .en(or_2_out[1]), .Q(register_2_q));
  Register #(.Bits(6)) register_3 (.D({or_1_out[2], multiplexer_3_out}), .C(C), .en(or_2_out[2]), .Q(register_3_q));
  Register #(.Bits(6)) register_4 (.D({or_1_out[3], multiplexer_4_out}), .C(C), .en(or_2_out[3]), .Q(register_4_q));
  Register #(.Bits(6)) register_5 (.D({or_1_out[4], multiplexer_5_out}), .C(C), .en(or_2_out[4]), .Q(register_5_q));
  Register #(.Bits(6)) register_6 (.D({or_1_out[5], multiplexer_6_out}), .C(C), .en(or_2_out[5]), .Q(register_6_q));
  Register #(.Bits(6)) register_7 (.D({or_1_out[6], multiplexer_7_out}), .C(C), .en(or_2_out[6]), .Q(register_7_q));
  Register #(.Bits(6)) register_8 (.D({or_1_out[7], multiplexer_8_out}), .C(C), .en(or_2_out[7]), .Q(register_8_q));
  Register #(.Bits(6)) register_9 (.D({or_1_out[8], multiplexer_9_out}), .C(C), .en(or_2_out[8]), .Q(register_9_q));
  Register #(.Bits(6)) register_10 (.D({or_1_out[9], multiplexer_10_out}), .C(C), .en(or_2_out[9]), .Q(register_10_q));
  Register #(.Bits(6)) register_11 (
    .D({or_1_out[10], multiplexer_11_out}), .C(C), .en(or_2_out[10]), .Q(register_11_q));
  Register #(.Bits(6)) register_12 (
    .D({or_1_out[11], multiplexer_12_out}), .C(C), .en(or_2_out[11]), .Q(register_12_q));
  Register #(.Bits(6)) register_13 (
    .D({or_1_out[12], multiplexer_13_out}), .C(C), .en(or_2_out[12]), .Q(register_13_q));
  Register #(.Bits(6)) register_14 (
    .D({or_1_out[13], multiplexer_14_out}), .C(C), .en(or_2_out[13]), .Q(register_14_q));
  Register #(.Bits(6)) register_15 (
    .D({or_1_out[14], multiplexer_15_out}), .C(C), .en(or_2_out[14]), .Q(register_15_q));
  Register #(.Bits(6)) register_16 (
    .D({or_1_out[15], multiplexer_16_out}), .C(C), .en(or_2_out[15]), .Q(register_16_q));
  Register #(.Bits(6)) register_17 (
    .D({or_1_out[16], multiplexer_17_out}), .C(C), .en(or_2_out[16]), .Q(register_17_q));
  Register #(.Bits(6)) register_18 (
    .D({or_1_out[17], multiplexer_18_out}), .C(C), .en(or_2_out[17]), .Q(register_18_q));
  Register #(.Bits(6)) register_19 (
    .D({or_1_out[18], multiplexer_19_out}), .C(C), .en(or_2_out[18]), .Q(register_19_q));
  Register #(.Bits(6)) register_20 (
    .D({or_1_out[19], multiplexer_20_out}), .C(C), .en(or_2_out[19]), .Q(register_20_q));
  Register #(.Bits(6)) register_21 (
    .D({or_1_out[20], multiplexer_21_out}), .C(C), .en(or_2_out[20]), .Q(register_21_q));
  Register #(.Bits(6)) register_22 (
    .D({or_1_out[21], multiplexer_22_out}), .C(C), .en(or_2_out[21]), .Q(register_22_q));
  Register #(.Bits(6)) register_23 (
    .D({or_1_out[22], multiplexer_23_out}), .C(C), .en(or_2_out[22]), .Q(register_23_q));
  Register #(.Bits(6)) register_24 (
    .D({or_1_out[23], multiplexer_24_out}), .C(C), .en(or_2_out[23]), .Q(register_24_q));
  Register #(.Bits(6)) register_25 (
    .D({or_1_out[24], multiplexer_25_out}), .C(C), .en(or_2_out[24]), .Q(register_25_q));
  Register #(.Bits(6)) register_26 (
    .D({or_1_out[25], multiplexer_26_out}), .C(C), .en(or_2_out[25]), .Q(register_26_q));
  Multiplexer #(.Selector_Bits(5), .Bits(6)) multiplexer_27 (
    .sel(com1_id), .in_0(register_1_q), .in_1(register_2_q), .in_2(register_3_q), .in_3(register_4_q),
    .in_4(register_5_q), .in_5(register_6_q), .in_6(register_7_q), .in_7(register_8_q), .in_8(register_9_q),
    .in_9(register_10_q), .in_10(register_11_q), .in_11(register_12_q), .in_12(register_13_q),
    .in_13(register_14_q), .in_14(register_15_q), .in_15(register_16_q), .in_16(register_17_q),
    .in_17(register_18_q), .in_18(register_19_q), .in_19(register_20_q), .in_20(register_21_q),
    .in_21(register_22_q), .in_22(register_23_q), .in_23(register_24_q), .in_24(register_25_q),
    .in_25(register_26_q), .in_26({6{1'b0}}), .in_27({6{1'b0}}), .in_28({6{1'b0}}), .in_29({6{1'b0}}),
    .in_30({6{1'b0}}), .in_31({6{1'b0}}), .out({V1, O1}));
  Multiplexer #(.Selector_Bits(5), .Bits(6)) multiplexer_28 (
    .sel(com2_id), .in_0(register_1_q), .in_1(register_2_q), .in_2(register_3_q), .in_3(register_4_q),
    .in_4(register_5_q), .in_5(register_6_q), .in_6(register_7_q), .in_7(register_8_q), .in_8(register_9_q),
    .in_9(register_10_q), .in_10(register_11_q), .in_11(register_12_q), .in_12(register_13_q),
    .in_13(register_14_q), .in_14(register_15_q), .in_15(register_16_q), .in_16(register_17_q),
    .in_17(register_18_q), .in_18(register_19_q), .in_19(register_20_q), .in_20(register_21_q),
    .in_21(register_22_q), .in_22(register_23_q), .in_23(register_24_q), .in_24(register_25_q),
    .in_25(register_26_q), .in_26({6{1'b0}}), .in_27({6{1'b0}}), .in_28({6{1'b0}}), .in_29({6{1'b0}}),
    .in_30({6{1'b0}}), .in_31({6{1'b0}}), .out({V2, O2}));

  // Other names for the same wires on the sheet: cm1 = com1; cm1_id[4:0] = com1_id; cm2 = com2; cm2_id[4:0] = com2_id
endmodule
