// Digital circuit map2-inst2reg.dig as structural Verilog
module map2_inst2reg (
  input  [4:0] I1,
  input  [4:0] I2,
  input  E1,
  input  E2,
  input  [4:0] R1,
  input  [4:0] R2,
  input  [4:0] com2_id,
  input  C,
  input  com1,
  input  com2,
  input  [4:0] com1_id,
  output [4:0] O1,
  output [4:0] O2,
  output V1,
  output V2
);

  wire or_3_out, P1, P2;
  wire [2:0] priorityencoder_1_num, priorityencoder_2_num;
  wire [4:0] multiplexer_1_out, multiplexer_3_out, multiplexer_5_out, multiplexer_7_out, multiplexer_9_out,
       multiplexer_11_out, multiplexer_13_out, multiplexer_15_out, register_1_q, register_3_q, register_5_q,
       register_7_q, register_9_q, register_11_q, register_13_q, register_15_q;
  wire [5:0] and_2_out, and_5_out, and_6_out, and_7_out, and_8_out, and_9_out, and_10_out, and_11_out,
       bitextender_2_out, bitextender_3_out, bitextender_4_out, bitextender_5_out, bitextender_6_out,
       bitextender_7_out, bitextender_8_out, bitextender_9_out, multiplexer_2_out, multiplexer_4_out,
       multiplexer_6_out, multiplexer_8_out, multiplexer_10_out, multiplexer_12_out, multiplexer_14_out,
       multiplexer_16_out, register_2_q, register_4_q, register_6_q, register_8_q, register_10_q,
       register_12_q, register_14_q, register_16_q;
  wire [7:0] and_1_out, and_3_out, and_4_out, bitextender_1_out, comparator_1_eq, comparator_2_eq, not_1_out,
       or_1_out, or_2_out, priority_8_1_out8, priority_8_2_out8, priority_8_3_out8, priority_8_4_out8,
       xor_1_out;

  assign or_1_out = priority_8_1_out8 | priority_8_2_out8;  // Or or_1, 8 bits wide
  assign or_2_out = priority_8_1_out8 | priority_8_2_out8 | priority_8_3_out8 | priority_8_4_out8;  // Or or_2, 8 bits wide
  or or_3 (or_3_out, E1, E2);
  BitExtender #(.inputBits(1), .outputBits(8)) bitextender_1 (.in(or_3_out), .out(bitextender_1_out));
  assign and_1_out = or_2_out & bitextender_1_out;  // And and_1, 8 bits wide
  Multiplexer #(.Bits(5)) multiplexer_1 (.sel(priority_8_4_out8[0]), .in_0(I1), .in_1(I2), .out(multiplexer_1_out));
  Multiplexer #(.Bits(6)) multiplexer_2 (
    .sel(priority_8_4_out8[0]), .in_0({1'b1, R1}), .in_1({1'b1, R2}), .out(multiplexer_2_out));
  BitExtender #(.inputBits(1), .outputBits(6)) bitextender_2 (.in(or_1_out[0]), .out(bitextender_2_out));
  assign and_2_out = multiplexer_2_out & bitextender_2_out;  // And and_2, 6 bits wide
  assign and_3_out = comparator_1_eq & {register_16_q[5], register_14_q[5], register_12_q[5], register_10_q[5], register_8_q[5], register_6_q[5], register_4_q[5], register_2_q[5]};  // And and_3, 8 bits wide
  Register #(.Bits(5)) register_1 (.D(multiplexer_1_out), .C(C), .en(and_1_out[0]), .Q(register_1_q));
  Comparator #(.Bits(5)) comparator_1 (.a(register_1_q), .b(com1_id), .eq(comparator_1_eq[0]));  // open: gt, lt
  Comparator #(.Bits(5)) comparator_2 (.a(register_1_q), .b(com2_id), .eq(comparator_2_eq[0]));  // open: gt, lt
  Register #(.Bits(6)) register_2 (.D(and_2_out), .C(C), .en(and_1_out[0]), .Q(register_2_q));
  assign and_4_out = comparator_2_eq & {register_16_q[5], register_14_q[5], register_12_q[5], register_10_q[5], register_8_q[5], register_6_q[5], register_4_q[5], register_2_q[5]};  // And and_4, 8 bits wide
  priority_8 priority_8_1 (
    .on(com1), .in1(and_3_out[0]), .in2(and_3_out[1]), .in3(and_3_out[2]), .in4(and_3_out[3]),
    .in5(and_3_out[4]), .in6(and_3_out[5]), .in7(and_3_out[6]), .in8(and_3_out[7]),
    .out1(priority_8_1_out8[0]), .out2(priority_8_1_out8[1]), .out3(priority_8_1_out8[2]),
    .out4(priority_8_1_out8[3]), .out5(priority_8_1_out8[4]), .out6(priority_8_1_out8[5]),
    .out7(priority_8_1_out8[6]), .out8(priority_8_1_out8[7]), .v(V1));
  assign not_1_out = ~{register_16_q[5], register_14_q[5], register_12_q[5], register_10_q[5], register_8_q[5], register_6_q[5], register_4_q[5], register_2_q[5]};  // Not not_1, 8 bits wide
  Multiplexer #(.Bits(5)) multiplexer_3 (.sel(priority_8_4_out8[1]), .in_0(I1), .in_1(I2), .out(multiplexer_3_out));
  Multiplexer #(.Bits(6)) multiplexer_4 (
    .sel(priority_8_4_out8[1]), .in_0({1'b1, R1}), .in_1({1'b1, R2}), .out(multiplexer_4_out));
  BitExtender #(.inputBits(1), .outputBits(6)) bitextender_3 (.in(or_1_out[1]), .out(bitextender_3_out));
  assign and_5_out = multiplexer_4_out & bitextender_3_out;  // And and_5, 6 bits wide
  Register #(.Bits(5)) register_3 (.D(multiplexer_3_out), .C(C), .en(and_1_out[1]), .Q(register_3_q));
  Comparator #(.Bits(5)) comparator_3 (.a(register_3_q), .b(com1_id), .eq(comparator_1_eq[1]));  // open: gt, lt
  Comparator #(.Bits(5)) comparator_4 (.a(register_3_q), .b(com2_id), .eq(comparator_2_eq[1]));  // open: gt, lt
  Register #(.Bits(6)) register_4 (.D(and_5_out), .C(C), .en(and_1_out[1]), .Q(register_4_q));
  priority_8 priority_8_2 (
    .on(com2), .in1(and_4_out[0]), .in2(and_4_out[1]), .in3(and_4_out[2]), .in4(and_4_out[3]),
    .in5(and_4_out[4]), .in6(and_4_out[5]), .in7(and_4_out[6]), .in8(and_4_out[7]),
    .out1(priority_8_2_out8[0]), .out2(priority_8_2_out8[1]), .out3(priority_8_2_out8[2]),
    .out4(priority_8_2_out8[3]), .out5(priority_8_2_out8[4]), .out6(priority_8_2_out8[5]),
    .out7(priority_8_2_out8[6]), .out8(priority_8_2_out8[7]), .v(V2));
  Multiplexer #(.Bits(5)) multiplexer_5 (.sel(priority_8_4_out8[2]), .in_0(I1), .in_1(I2), .out(multiplexer_5_out));
  Multiplexer #(.Bits(6)) multiplexer_6 (
    .sel(priority_8_4_out8[2]), .in_0({1'b1, R1}), .in_1({1'b1, R2}), .out(multiplexer_6_out));
  assign and_6_out = multiplexer_6_out & bitextender_4_out;  // And and_6, 6 bits wide
  Register #(.Bits(5)) register_5 (.D(multiplexer_5_out), .C(C), .en(and_1_out[2]), .Q(register_5_q));
  Comparator #(.Bits(5)) comparator_5 (.a(register_5_q), .b(com1_id), .eq(comparator_1_eq[2]));  // open: gt, lt
  Comparator #(.Bits(5)) comparator_6 (.a(register_5_q), .b(com2_id), .eq(comparator_2_eq[2]));  // open: gt, lt
  BitExtender #(.inputBits(1), .outputBits(6)) bitextender_4 (.in(or_1_out[2]), .out(bitextender_4_out));
  Register #(.Bits(6)) register_6 (.D(and_6_out), .C(C), .en(and_1_out[2]), .Q(register_6_q));
  PriorityEncoder #(.Selector_Bits(3)) priorityencoder_1 (
    .in0(not_1_out[0]), .in1(not_1_out[1]), .in2(not_1_out[2]), .in3(not_1_out[3]), .in4(not_1_out[4]),
    .in5(not_1_out[5]), .in6(not_1_out[6]), .in7(not_1_out[7]), .num(priorityencoder_1_num));  // open: any
  priority_8 priority_8_3 (
    .on(1'b1), .in1(not_1_out[0]), .in2(not_1_out[1]), .in3(not_1_out[2]), .in4(not_1_out[3]),
    .in5(not_1_out[4]), .in6(not_1_out[5]), .in7(not_1_out[6]), .in8(not_1_out[7]),
    .out1(priority_8_3_out8[0]), .out2(priority_8_3_out8[1]), .out3(priority_8_3_out8[2]),
    .out4(priority_8_3_out8[3]), .out5(priority_8_3_out8[4]), .out6(priority_8_3_out8[5]),
    .out7(priority_8_3_out8[6]), .out8(priority_8_3_out8[7]), .v(P1));
  Multiplexer #(.Bits(5)) multiplexer_7 (.sel(priority_8_4_out8[3]), .in_0(I1), .in_1(I2), .out(multiplexer_7_out));
  Multiplexer #(.Bits(6)) multiplexer_8 (
    .sel(priority_8_4_out8[3]), .in_0({1'b1, R1}), .in_1({1'b1, R2}), .out(multiplexer_8_out));
  BitExtender #(.inputBits(1), .outputBits(6)) bitextender_5 (.in(or_1_out[3]), .out(bitextender_5_out));
  assign and_7_out = multiplexer_8_out & bitextender_5_out;  // And and_7, 6 bits wide
  assign xor_1_out = priority_8_3_out8 ^ not_1_out;  // XOr xor_1, 8 bits wide
  Register #(.Bits(5)) register_7 (.D(multiplexer_7_out), .C(C), .en(and_1_out[3]), .Q(register_7_q));
  Comparator #(.Bits(5)) comparator_7 (.a(register_7_q), .b(com1_id), .eq(comparator_1_eq[3]));  // open: gt, lt
  Comparator #(.Bits(5)) comparator_8 (.a(register_7_q), .b(com2_id), .eq(comparator_2_eq[3]));  // open: gt, lt
  Register #(.Bits(6)) register_8 (.D(and_7_out), .C(C), .en(and_1_out[3]), .Q(register_8_q));
  PriorityEncoder #(.Selector_Bits(3)) priorityencoder_2 (
    .in0(xor_1_out[0]), .in1(xor_1_out[1]), .in2(xor_1_out[2]), .in3(xor_1_out[3]), .in4(xor_1_out[4]),
    .in5(xor_1_out[5]), .in6(xor_1_out[6]), .in7(xor_1_out[7]), .num(priorityencoder_2_num));  // open: any
  priority_8 priority_8_4 (
    .on(1'b1), .in1(xor_1_out[0]), .in2(xor_1_out[1]), .in3(xor_1_out[2]), .in4(xor_1_out[3]),
    .in5(xor_1_out[4]), .in6(xor_1_out[5]), .in7(xor_1_out[6]), .in8(xor_1_out[7]),
    .out1(priority_8_4_out8[0]), .out2(priority_8_4_out8[1]), .out3(priority_8_4_out8[2]),
    .out4(priority_8_4_out8[3]), .out5(priority_8_4_out8[4]), .out6(priority_8_4_out8[5]),
    .out7(priority_8_4_out8[6]), .out8(priority_8_4_out8[7]), .v(P2));
  Multiplexer #(.Bits(5)) multiplexer_9 (.sel(priority_8_4_out8[4]), .in_0(I1), .in_1(I2), .out(multiplexer_9_out));
  Multiplexer #(.Bits(6)) multiplexer_10 (
    .sel(priority_8_4_out8[4]), .in_0({1'b1, R1}), .in_1({1'b1, R2}), .out(multiplexer_10_out));
  BitExtender #(.inputBits(1), .outputBits(6)) bitextender_6 (.in(or_1_out[4]), .out(bitextender_6_out));
  assign and_8_out = multiplexer_10_out & bitextender_6_out;  // And and_8, 6 bits wide
  Register #(.Bits(5)) register_9 (.D(multiplexer_9_out), .C(C), .en(and_1_out[4]), .Q(register_9_q));
  Comparator #(.Bits(5)) comparator_9 (.a(register_9_q), .b(com1_id), .eq(comparator_1_eq[4]));  // open: gt, lt
  Comparator #(.Bits(5)) comparator_10 (.a(register_9_q), .b(com2_id), .eq(comparator_2_eq[4]));  // open: gt, lt
  Register #(.Bits(6)) register_10 (.D(and_8_out), .C(C), .en(and_1_out[4]), .Q(register_10_q));
  Multiplexer #(.Bits(5)) multiplexer_11 (.sel(priority_8_4_out8[5]), .in_0(I1), .in_1(I2), .out(multiplexer_11_out));
  Multiplexer #(.Bits(6)) multiplexer_12 (
    .sel(priority_8_4_out8[5]), .in_0({1'b1, R1}), .in_1({1'b1, R2}), .out(multiplexer_12_out));
  BitExtender #(.inputBits(1), .outputBits(6)) bitextender_7 (.in(or_1_out[5]), .out(bitextender_7_out));
  assign and_9_out = multiplexer_12_out & bitextender_7_out;  // And and_9, 6 bits wide
  Register #(.Bits(5)) register_11 (.D(multiplexer_11_out), .C(C), .en(and_1_out[5]), .Q(register_11_q));
  Comparator #(.Bits(5)) comparator_11 (.a(register_11_q), .b(com1_id), .eq(comparator_1_eq[5]));  // open: gt, lt
  Comparator #(.Bits(5)) comparator_12 (.a(register_11_q), .b(com2_id), .eq(comparator_2_eq[5]));  // open: gt, lt
  Register #(.Bits(6)) register_12 (.D(and_9_out), .C(C), .en(and_1_out[5]), .Q(register_12_q));
  Multiplexer #(.Bits(5)) multiplexer_13 (.sel(priority_8_4_out8[6]), .in_0(I1), .in_1(I2), .out(multiplexer_13_out));
  Multiplexer #(.Bits(6)) multiplexer_14 (
    .sel(priority_8_4_out8[6]), .in_0({1'b1, R1}), .in_1({1'b1, R2}), .out(multiplexer_14_out));
  assign and_10_out = multiplexer_14_out & bitextender_8_out;  // And and_10, 6 bits wide
  Register #(.Bits(5)) register_13 (.D(multiplexer_13_out), .C(C), .en(and_1_out[6]), .Q(register_13_q));
  Comparator #(.Bits(5)) comparator_13 (.a(register_13_q), .b(com1_id), .eq(comparator_1_eq[6]));  // open: gt, lt
  Comparator #(.Bits(5)) comparator_14 (.a(register_13_q), .b(com2_id), .eq(comparator_2_eq[6]));  // open: gt, lt
  BitExtender #(.inputBits(1), .outputBits(6)) bitextender_8 (.in(or_1_out[6]), .out(bitextender_8_out));
  Register #(.Bits(6)) register_14 (.D(and_10_out), .C(C), .en(and_1_out[6]), .Q(register_14_q));
  Multiplexer #(.Bits(5)) multiplexer_15 (.sel(priority_8_4_out8[7]), .in_0(I1), .in_1(I2), .out(multiplexer_15_out));
  Multiplexer #(.Bits(6)) multiplexer_16 (
    .sel(priority_8_4_out8[7]), .in_0({1'b1, R1}), .in_1({1'b1, R2}), .out(multiplexer_16_out));
  BitExtender #(.inputBits(1), .outputBits(6)) bitextender_9 (.in(or_1_out[7]), .out(bitextender_9_out));
  assign and_11_out = multiplexer_16_out & bitextender_9_out;  // And and_11, 6 bits wide
  Register #(.Bits(5)) register_15 (.D(multiplexer_15_out), .C(C), .en(and_1_out[7]), .Q(register_15_q));
  Comparator #(.Bits(5)) comparator_15 (.a(register_15_q), .b(com1_id), .eq(comparator_1_eq[7]));  // open: gt, lt
  Comparator #(.Bits(5)) comparator_16 (.a(register_15_q), .b(com2_id), .eq(comparator_2_eq[7]));  // open: gt, lt
  Register #(.Bits(6)) register_16 (.D(and_11_out), .C(C), .en(and_1_out[7]), .Q(register_16_q));
  Multiplexer #(.Selector_Bits(3), .Bits(5)) multiplexer_17 (
    .sel(priorityencoder_1_num), .in_0(register_16_q[4:0]), .in_1(register_14_q[4:0]),
    .in_2(register_12_q[4:0]), .in_3(register_10_q[4:0]), .in_4(register_8_q[4:0]), .in_5(register_6_q[4:0]),
    .in_6(register_4_q[4:0]), .in_7(register_2_q[4:0]), .out(O1));
  Multiplexer #(.Selector_Bits(3), .Bits(5)) multiplexer_18 (
    .sel(priorityencoder_2_num), .in_0(register_16_q[4:0]), .in_1(register_14_q[4:0]),
    .in_2(register_12_q[4:0]), .in_3(register_10_q[4:0]), .in_4(register_8_q[4:0]), .in_5(register_6_q[4:0]),
    .in_6(register_4_q[4:0]), .in_7(register_2_q[4:0]), .out(O2));

  // Other names for the same wires on the sheet: cm1 = com1; cm1_id[4:0] = com1_id; cm2 = com2; cm2_id[4:0] = com2_id;
  //   D1[4:0] = R1; D2[4:0] = R2
endmodule
