// Digital circuit new queue test.dig as structural Verilog
module new_queue_test (
  input  in_1,
  input  clk,
  input  in_3,
  output out_4
);

  wire multiplexer_2_out, or_1_out;
  wire [1:1] register_2_q;
  wire [2:0] and_1_out, multiplexer_1_out, nand_1_out, register_1_q;

  Register register_1 (.D(in_1), .C(clk), .en(multiplexer_1_out[2]), .Q(register_1_q[2]));
  Multiplexer #(.Bits(3)) multiplexer_1 (
    .sel(or_1_out), .in_0({register_1_q[1:0], 1'b0}), .in_1(and_1_out), .out(multiplexer_1_out));
  or or_1 (or_1_out, and_1_out[0], and_1_out[1], and_1_out[2]);
  Multiplexer multiplexer_2 (.sel(register_1_q[2]), .in_0(in_1), .in_1(register_1_q[2]), .out(multiplexer_2_out));
  Register register_2 (.D(multiplexer_2_out), .C(clk), .en(multiplexer_1_out[1]), .Q(register_2_q[1]));
  or or_2 (register_1_q[1], register_2_q[1], register_1_q[2]);
  or or_3 (register_1_q[0], in_3, register_2_q[1], register_1_q[2]);
  assign and_1_out = nand_1_out & register_1_q;  // And and_1, 3 bits wide
  Multiplexer multiplexer_3 (.sel(register_1_q[1]), .in_0(in_1), .in_1(register_2_q[1]), .out(out_4));
  nand nand_1 (nand_1_out[2], in_3, register_2_q[1], register_1_q[2]);
  nand nand_2 (nand_1_out[1], in_3, register_2_q[1]);
  not not_1 (nand_1_out[0], in_3);

  // Other names for the same wires on the sheet: B = in_3; C = clk; L = in_1; O = out_4
endmodule
