// Digital circuit priority-16.dig as structural Verilog
module priority_16 (
  input  in1,
  input  in2,
  input  in3,
  input  in4,
  input  in5,
  input  in6,
  input  in7,
  input  in8,
  input  in9,
  input  in10,
  input  in11,
  input  in12,
  input  in13,
  input  in14,
  input  in15,
  input  in16,
  output out1,
  output out2,
  output out3,
  output out4,
  output out5,
  output out6,
  output out7,
  output out8,
  output out9,
  output out10,
  output out11,
  output out12,
  output out13,
  output out14,
  output out15,
  output out16,
  output v
);

  wire not_1_out, priority_8_1_v, priority_8_2_v;

  not not_1 (not_1_out, priority_8_2_v);
  priority_8 priority_8_1 (
    .on(not_1_out), .in1(in1), .in2(in2), .in3(in3), .in4(in4), .in5(in5), .in6(in6), .in7(in7), .in8(in8),
    .out1(out1), .out2(out2), .out3(out3), .out4(out4), .out5(out5), .out6(out6), .out7(out7), .out8(out8),
    .v(priority_8_1_v));
  priority_8 priority_8_2 (
    .on(1'b1), .in1(in9), .in2(in10), .in3(in11), .in4(in12), .in5(in13), .in6(in14), .in7(in15), .in8(in16),
    .out1(out9), .out2(out10), .out3(out11), .out4(out12), .out5(out13), .out6(out14), .out7(out15),
    .out8(out16), .v(priority_8_2_v));
  or or_1 (v, priority_8_1_v, priority_8_2_v);
endmodule
