// Digital circuit reg8x4.dig as structural Verilog
module reg8x4 (
  input  C,
  input  [3:0] E,
  input  [31:0] D,
  output [31:0] D_o
);

  Register #(.Bits(8)) R1 (.D(D[7:0]), .C(C), .en(E[0]), .Q(D_o[7:0]));
  Register #(.Bits(8)) R2 (.D(D[15:8]), .C(C), .en(E[1]), .Q(D_o[15:8]));
  Register #(.Bits(8)) R3 (.D(D[23:16]), .C(C), .en(E[2]), .Q(D_o[23:16]));
  Register #(.Bits(8)) R4 (.D(D[31:24]), .C(C), .en(E[3]), .Q(D_o[31:24]));

  // Other names for the same wires on the sheet: D1_i[7:0] = D[7:0]; D2_i[7:0] = D[15:8]; D3_i[7:0] = D[23:16];
  //   D4_i[7:0] = D[31:24]; E1 = E[0]; E2 = E[1]; E3 = E[2]; E4 = E[3]; R1[7:0] = D_o[7:0]; R2[7:0] = D_o[15:8];
  //   R3[7:0] = D_o[23:16]; R4[7:0] = D_o[31:24]

  // Notes on the sheet:
  //   E: enable
  //   D_o: data out
  //   D: data in
endmodule
