// Digital circuit regFile.dig as structural Verilog
module regFile (
  input  C,
  input  [31:0] PCA_i,
  input  [31:0] FL_i,
  input  FL_sel,
  input  PCA_e,
  input  [3:0] FL_e,
  input  [2:0] MW,
  input  [4:0] RW,
  input  [4:0] RA,
  input  [4:0] RB,
  input  [2:0] MA,
  input  [2:0] MB,
  input  E,
  input  [31:0] D,
  input  [31:0] PCS_i,
  input  PCS_e,
  input  SC_sel,
  input  SC_e,
  input  [31:0] SC_i,
  output [31:0] R_A,
  output [31:0] R_B,
  output [31:0] PCS_O,
  output [31:0] PCA_O,
  output [31:0] SC_O,
  output [31:0] FL_O
);

  wire a_mux_a1, a_mux_a2, a_mux_c2, a_mux_d1, a_mux_d2, and_1_out, and_8_out, and_9_out, and_11_out,
       and_12_out, and_13_out, and_14_out, b_mux_a1, b_mux_a2, b_mux_c2, b_mux_d1, b_mux_d2, comparator_1_eq,
       multiplexer_12_out, multiplexer_13_out, nor_3_out, not_3_out, not_4_out, not_5_out, not_6_out,
       or_3_out, R_HE, xor_1_out;
  wire [3:0] bitextender_1_out, bitextender_2_out, bitextender_3_out, FL_e_t, multiplexer_3_out,
       multiplexer_4_out, or_1_out, R1_e, R2_e, R3_e, R4_e, R5_e, R6_e, R7_e, R8_e, R9_e, R10_e, R11_e,
       R12_e, R13_e, R14_e, R15_e, R16_e, R17_e, R18_e, R19_e, R20_e, R21_e, R22_e, R23_e, R24_e, R25_e, R_e,
       SBP_e, SC_e_t;
  wire [6:6] FL_d_o;
  wire [7:0] and_16_out, and_17_out, and_18_out, and_19_out, and_20_out, and_21_out, bitextender_4_out,
       bitextender_5_out, bitextender_6_out, bitextender_7_out, bitextender_8_out, bitextender_9_out,
       bitextender_10_out, bitextender_11_out, multiplexer_5_out, multiplexer_6_out, multiplexer_7_out,
       multiplexer_8_out;
  wire [31:0] multiplexer_1_out, multiplexer_2_out, R1, R2, R3, R4, R5, R6, R7, R8, R9, R10, R11, R12, R13,
       R14, R15, R16, R17, R18, R19, R20, R21, R22, R23, R24, R25, R_A_t, R_B_t, register_1_q, register_2_q,
       SBP;
  wire [31:8] R_i;

  reg8x4 u_R1 (.C(C), .D({R_i, D[7:0]}), .E(R1_e), .D_o(R1));
  reg8x4 u_R5 (.C(C), .D({R_i, D[7:0]}), .E(R5_e), .D_o(R5));
  reg8x4 u_R9 (.C(C), .D({R_i, D[7:0]}), .E(R9_e), .D_o(R9));
  reg8x4 u_R13 (.C(C), .D({R_i, D[7:0]}), .E(R13_e), .D_o(R13));
  reg8x4 u_R17 (.C(C), .D({R_i, D[7:0]}), .E(R17_e), .D_o(R17));
  reg8x4 u_R21 (.C(C), .D({R_i, D[7:0]}), .E(R21_e), .D_o(R21));
  reg8x4 u_R25 (.C(C), .D({R_i, D[7:0]}), .E(R25_e), .D_o(R25));
  reg8x4 u_SBP (.C(C), .D({R_i, D[7:0]}), .E(SBP_e), .D_o(SBP));
  Comparator #(.Bits(5)) comparator_1 (.a({5{1'b1}}), .b(RW), .eq(comparator_1_eq));  // open: gt, lt
  Multiplexer #(.Bits(32)) multiplexer_1 (.sel(SC_sel), .in_0({R_i, D[7:0]}), .in_1(SC_i), .out(multiplexer_1_out));
  BitExtender #(.inputBits(1), .outputBits(4)) bitextender_1 (.in(SC_e), .out(bitextender_1_out));
  Multiplexer #(.Bits(32)) multiplexer_2 (.sel(and_1_out), .in_0({R_i, D[7:0]}), .in_1(FL_i), .out(multiplexer_2_out));
  and and_1 (and_1_out, ~comparator_1_eq, FL_sel);  // And
  BitExtender #(.inputBits(1), .outputBits(4)) bitextender_2 (.in(PCA_e), .out(bitextender_2_out));
  BitExtender #(.inputBits(1), .outputBits(4)) bitextender_3 (.in(PCS_e), .out(bitextender_3_out));
  Multiplexer #(.Bits(4)) multiplexer_3 (
    .sel(SC_sel), .in_0(SC_e_t), .in_1(bitextender_1_out), .out(multiplexer_3_out));
  Multiplexer #(.Bits(4)) multiplexer_4 (.sel(and_1_out), .in_0(FL_e_t), .in_1(FL_e), .out(multiplexer_4_out));
  reg8x4 u_R2 (.C(C), .D({R_i, D[7:0]}), .E(R2_e), .D_o(R2));
  reg8x4 u_R6 (.C(C), .D({R_i, D[7:0]}), .E(R6_e), .D_o(R6));
  reg8x4 u_R10 (.C(C), .D({R_i, D[7:0]}), .E(R10_e), .D_o(R10));
  reg8x4 u_R14 (.C(C), .D({R_i, D[7:0]}), .E(R14_e), .D_o(R14));
  reg8x4 u_R18 (.C(C), .D({R_i, D[7:0]}), .E(R18_e), .D_o(R18));
  reg8x4 u_R22 (.C(C), .D({R_i, D[7:0]}), .E(R22_e), .D_o(R22));
  reg8x4 PC (.C(C), .D(PCA_i), .E(bitextender_2_out), .D_o(PCA_O));
  reg8x4 PC_2 (.C(C), .D(PCS_i), .E(bitextender_3_out), .D_o(PCS_O));
  reg8x4 SC (.C(C), .D(multiplexer_1_out), .E(multiplexer_3_out), .D_o(SC_O));
  reg8x4 FL (.C(C), .D(multiplexer_2_out), .E(multiplexer_4_out), .D_o({FL_O[31:7], FL_d_o[6], FL_O[5:0]}));
  reg8x4 u_R3 (.C(C), .D({R_i, D[7:0]}), .E(R3_e), .D_o(R3));
  reg8x4 u_R7 (.C(C), .D({R_i, D[7:0]}), .E(R7_e), .D_o(R7));
  reg8x4 u_R11 (.C(C), .D({R_i, D[7:0]}), .E(R11_e), .D_o(R11));
  reg8x4 u_R15 (.C(C), .D({R_i, D[7:0]}), .E(R15_e), .D_o(R15));
  reg8x4 u_R19 (.C(C), .D({R_i, D[7:0]}), .E(R19_e), .D_o(R19));
  reg8x4 u_R23 (.C(C), .D({R_i, D[7:0]}), .E(R23_e), .D_o(R23));
  reg8x4 u_R4 (.C(C), .D({R_i, D[7:0]}), .E(R4_e), .D_o(R4));
  reg8x4 u_R8 (.C(C), .D({R_i, D[7:0]}), .E(R8_e), .D_o(R8));
  reg8x4 u_R12 (.C(C), .D({R_i, D[7:0]}), .E(R12_e), .D_o(R12));
  reg8x4 u_R16 (.C(C), .D({R_i, D[7:0]}), .E(R16_e), .D_o(R16));
  reg8x4 u_R20 (.C(C), .D({R_i, D[7:0]}), .E(R20_e), .D_o(R20));
  reg8x4 u_R24 (.C(C), .D({R_i, D[7:0]}), .E(R24_e), .D_o(R24));
  and and_2 (a_mux_c2, MA[2], MA[1]);
  nor nor_1 (a_mux_d1, MA[2], MA[1], MA[0]);
  and and_3 (b_mux_c2, MB[2], MB[1]);
  nor nor_2 (b_mux_d1, MB[2], MB[1], MB[0]);
  nor nor_3 (nor_3_out, MW[2], MW[1], MW[0]);
  and and_4 (a_mux_a1, MA[1], MA[0]);
  and and_5 (a_mux_a2, MA[2], ~MA[1], ~MA[0]);  // And
  not not_1 (a_mux_d2, MA[1]);
  and and_6 (b_mux_a1, MB[1], MB[0]);
  and and_7 (b_mux_a2, MB[2], ~MB[1], ~MB[0]);  // And
  not not_2 (b_mux_d2, MB[1]);
  xor xor_1 (xor_1_out, MW[0], MW[1]);
  nor nor_4 (or_1_out[3], MW[1], MW[0]);
  or or_1 (or_1_out[1], nor_3_out, MW[0]);
  or or_2 (or_1_out[0], xor_1_out, nor_3_out);
  Register #(.Bits(32)) register_1 (.D(PCS_O), .C(C), .en(PCS_e), .Q(register_1_q));
  Demultiplexer #(.Selector_Bits(5), .Bits(4)) demultiplexer_1 (
    .sel(RW), .in(R_e), .out_0(R1_e), .out_1(R2_e), .out_2(R3_e), .out_3(R4_e), .out_4(R5_e), .out_5(R6_e),
    .out_6(R7_e), .out_7(R8_e), .out_8(R9_e), .out_9(R10_e), .out_10(R11_e), .out_11(R12_e), .out_12(R13_e),
    .out_13(R14_e), .out_14(R15_e), .out_15(R16_e), .out_16(R17_e), .out_17(R18_e), .out_18(R19_e),
    .out_19(R20_e), .out_20(R21_e), .out_21(R22_e), .out_22(R23_e), .out_23(R24_e), .out_24(R25_e),
    .out_25(SBP_e), .out_30(SC_e_t), .out_31(FL_e_t));  // open: out_26, out_27, out_28, out_29
  not not_3 (not_3_out, RW[4]);
  not not_4 (not_4_out, RW[3]);
  not not_5 (not_5_out, RW[2]);
  not not_6 (not_6_out, RW[1]);
  Register #(.Bits(32)) register_2 (.D(register_1_q), .C(C), .en(PCS_e), .Q(register_2_q));
  and and_8 (and_8_out, RW[4], not_4_out);
  and and_9 (and_9_out, RW[4], RW[3], not_5_out, not_6_out);
  Multiplexer #(.Bits(8)) multiplexer_5 (
    .sel(a_mux_a2), .in_0(R_A_t[15:8]), .in_1(R_A_t[31:24]), .out(multiplexer_5_out));
  Multiplexer #(.Bits(8)) multiplexer_6 (
    .sel(a_mux_a1), .in_0(R_A_t[7:0]), .in_1(R_A_t[15:8]), .out(multiplexer_6_out));
  Multiplexer #(.Bits(8)) multiplexer_7 (
    .sel(b_mux_a2), .in_0(R_B_t[15:8]), .in_1(R_B_t[31:24]), .out(multiplexer_7_out));
  Multiplexer #(.Bits(8)) multiplexer_8 (
    .sel(b_mux_a1), .in_0(R_B_t[7:0]), .in_1(R_B_t[15:8]), .out(multiplexer_8_out));
  assign R_e = {{2{or_1_out[3]}}, or_1_out[1:0]} & {4{E}};  // And and_10, 4 bits wide
  Multiplexer #(.Bits(8)) multiplexer_9 (.sel(a_mux_a2), .in_0(multiplexer_6_out), .in_1(R_A_t[23:16]), .out(R_A[7:0]));
  Multiplexer #(.Bits(8)) multiplexer_10 (
    .sel(b_mux_a2), .in_0(multiplexer_8_out), .in_1(R_B_t[23:16]), .out(R_B[7:0]));
  Multiplexer #(.Selector_Bits(5), .Bits(32)) multiplexer_11 (
    .sel(RA), .in_0(R1), .in_1(R2), .in_2(R3), .in_3(R4), .in_4(R5), .in_5(R6), .in_6(R7), .in_7(R8),
    .in_8(R9), .in_9(R10), .in_10(R11), .in_11(R12), .in_12(R13), .in_13(R14), .in_14(R15), .in_15(R16),
    .in_16(R17), .in_17(R18), .in_18(R19), .in_19(R20), .in_20(R21), .in_21(R22), .in_22(R23), .in_23(R24),
    .in_24(R25), .in_25(SBP), .in_26({32{1'b0}}), .in_27(32'h1), .in_28({32{1'b1}}), .in_29(register_2_q),
    .in_30(SC_O), .in_31({FL_O[31:7], 1'b1, FL_O[5:0]}), .out(R_A_t));
  or or_3 (or_3_out, not_3_out, and_8_out, and_9_out);
  BitExtender #(.inputBits(1), .outputBits(8)) bitextender_4 (.in(a_mux_d1), .out(bitextender_4_out));
  and and_11 (and_11_out, MA[2], multiplexer_12_out);
  Multiplexer multiplexer_12 (.sel(MA[1]), .in_0(multiplexer_5_out[7]), .in_1(R_A[7]), .out(multiplexer_12_out));
  and and_12 (and_12_out, R_A[7], a_mux_c2);
  BitExtender #(.inputBits(1), .outputBits(8)) bitextender_5 (.in(b_mux_d1), .out(bitextender_5_out));
  and and_13 (and_13_out, MB[2], multiplexer_13_out);
  Multiplexer multiplexer_13 (.sel(MB[1]), .in_0(multiplexer_7_out[7]), .in_1(R_B[7]), .out(multiplexer_13_out));
  and and_14 (and_14_out, R_B[7], b_mux_c2);
  and and_15 (R_HE, E, or_3_out);
  assign and_16_out = bitextender_4_out & R_A_t[31:24];  // And and_16, 8 bits wide
  assign and_17_out = bitextender_4_out & R_A_t[23:16];  // And and_17, 8 bits wide
  BitExtender #(.inputBits(1), .outputBits(8)) bitextender_6 (.in(a_mux_d2), .out(bitextender_6_out));
  assign and_18_out = bitextender_5_out & R_B_t[31:24];  // And and_18, 8 bits wide
  assign and_19_out = bitextender_5_out & R_B_t[23:16];  // And and_19, 8 bits wide
  BitExtender #(.inputBits(1), .outputBits(8)) bitextender_7 (.in(b_mux_d2), .out(bitextender_7_out));
  Multiplexer #(.Bits(8)) multiplexer_14 (.sel(MW[2]), .in_0(D[31:24]), .in_1(D[15:8]), .out(R_i[31:24]));
  Multiplexer #(.Bits(8)) multiplexer_15 (.sel(MW[2]), .in_0(D[23:16]), .in_1(D[7:0]), .out(R_i[23:16]));
  Multiplexer #(.Bits(8)) multiplexer_16 (.sel(MW[1]), .in_0(D[15:8]), .in_1(D[7:0]), .out(R_i[15:8]));
  Multiplexer #(.Selector_Bits(5), .Bits(32)) multiplexer_17 (
    .sel(RB), .in_0(R1), .in_1(R2), .in_2(R3), .in_3(R4), .in_4(R5), .in_5(R6), .in_6(R7), .in_7(R8),
    .in_8(R9), .in_9(R10), .in_10(R11), .in_11(R12), .in_12(R13), .in_13(R14), .in_14(R15), .in_15(R16),
    .in_16(R17), .in_17(R18), .in_18(R19), .in_19(R20), .in_20(R21), .in_21(R22), .in_22(R23), .in_23(R24),
    .in_24(R25), .in_25(SBP), .in_26({32{1'b0}}), .in_27(32'h1), .in_28({32{1'b1}}), .in_29(register_2_q),
    .in_30(SC_O), .in_31({FL_O[31:7], 1'b1, FL_O[5:0]}), .out(R_B_t));
  BitExtender #(.inputBits(1), .outputBits(8)) bitextender_8 (.in(and_11_out), .out(bitextender_8_out));
  assign and_20_out = bitextender_6_out & multiplexer_5_out;  // And and_20, 8 bits wide
  BitExtender #(.inputBits(1), .outputBits(8)) bitextender_9 (.in(and_12_out), .out(bitextender_9_out));
  BitExtender #(.inputBits(1), .outputBits(8)) bitextender_10 (.in(and_13_out), .out(bitextender_10_out));
  assign and_21_out = bitextender_7_out & multiplexer_7_out;  // And and_21, 8 bits wide
  BitExtender #(.inputBits(1), .outputBits(8)) bitextender_11 (.in(and_14_out), .out(bitextender_11_out));
  assign R_A[31:24] = and_16_out | bitextender_8_out;  // Or or_4, 8 bits wide
  assign R_A[23:16] = and_17_out | bitextender_8_out;  // Or or_5, 8 bits wide
  assign R_A[15:8] = and_20_out | bitextender_9_out;  // Or or_6, 8 bits wide
  assign R_B[31:24] = and_18_out | bitextender_10_out;  // Or or_7, 8 bits wide
  assign R_B[23:16] = and_19_out | bitextender_10_out;  // Or or_8, 8 bits wide
  assign R_B[15:8] = and_21_out | bitextender_11_out;  // Or or_9, 8 bits wide

  assign FL_O[6] = 1'b1;

  // Other names for the same wires on the sheet: FL (some bits) = {FL_O[31:7], FL_O[5:0]}; D_A[31:0] = R_A;
  //   D_B[31:0] = R_B; A_mode[2:0] = MA; a_mux_b1 = MA[1]; a_mux_c1 = MA[2]; B_mode[2:0] = MB; b_mux_b1 = MB[1];
  //   b_mux_c1 = MB[2]; D_I[31:0] = D; R_i[7:0] = D[7:0]; FL_e__EX[3:0] = FL_e; PCA[31:0] = PCA_O; PCA_e__EX = PCA_e;
  //   PCS[31:0] = PCS_O; PCS_e__EX = PCS_e; PCS_HE = PCS_e; RA_sel[4:0] = RA; RB_sel[4:0] = RB; RW_sel[4:0] = RW;
  //   SC[31:0] = SC_O; SC_e__EX = SC_e; W_mode[2:0] = MW; w_mux_3 = MW[1]; w_mux_1 = MW[2]; w_mux_2 = MW[2]

  // Notes on the sheet:
  //   PCA_i: data input for arcitectural PC
  //   FL_i: data input for FL
  //   FL_sel: enable FL extern mode
  //   PCA_e: arcitectural PC register enable
  //   FL_e: FL register enable
  //   MW: write mode:
  //   0: 32
  //   1: 16L
  //   2: 8L
  //   3: 8H
  //   4: 16H
  //   5: S16L (=16L)
  //   6: S8L (=8L)
  //   7: S8H (=8H)
  //   RW: register to write:
  //   0~25: general
  //   26: zero
  //   27: one
  //   28: full
  //   29: program counter
  //   30: stack counter
  //   31: flag
  //   RA: register to read:
  //   0~25: general
  //   26: zero
  //   27: one
  //   28: full
  //   29: program counter
  //   30: stack counter
  //   31: flag
  //   RB: register to read:
  //   0~25: general
  //   26: zero
  //   27: one
  //   28: full
  //   29: program counter
  //   30: stack counter
  //   31: flag
  //   MA: read mode:
  //   0: 32
  //   1: 16L
  //   2: 8L
  //   3: 8H
  //   4: 16H
  //   5: S16L
  //   6: S8L
  //   7: S8H
  //   MB: read mode:
  //   0: 32
  //   1: 16L
  //   2: 8L
  //   3: 8H
  //   4: 16H
  //   5: S16L
  //   6: S8L
  //   7: S8H
  //   R_A: register out a
  //   R_B: register out b
  //   PCS_O: speculative PC out
  //   E: enable
  //   D: data in
  //   PCS_i: data input for speculative PC
  //   PCS_e: speculative PC register enable
  //   PCA_O: architectural PC out
  //   SC_O: SC out
  //   SC_sel: enable SC extern mode
  //   SC_e: SC register enable
  //   SC_i: data input for SC
  //   FL_O: FL out
endmodule
