// Digital circuit regFile2.dig as structural Verilog
module regFile2 (
  input  C,
  input  [31:0] PCA_i,
  input  [31:0] SC_i,
  input  [31:0] FL_i,
  input  SC_sel,
  input  FL_sel,
  input  PCA_e,
  input  SC_e,
  input  [3:0] FL_e,
  input  [2:0] MW,
  input  [4:0] RW,
  input  [4:0] RA,
  input  [4:0] RB,
  input  [2:0] MA,
  input  [2:0] MB,
  input  E,
  input  SC_de,
  input  [3:0] FL_de,
  input  [4:0] RD,
  input  [2:0] MD,
  input  DE,
  input  [31:0] D,
  input  [4:0] RDA,
  input  [2:0] RDAM,
  input  [4:0] RDB,
  input  [2:0] MDBM,
  input  RDAE,
  input  RDBE,
  input  [31:0] PCS_i,
  input  PCS_e,
  output [31:0] R_A,
  output [31:0] R_B,
  output [31:0] PCS_O,
  output [31:0] SC_O,
  output [31:0] FL_O,
  output NR,
  output [3:0] SC_RD,
  output [3:0] FL_RD,
  output [31:0] PCA_O
);

  wire a_mux_a1, a_mux_a2, a_mux_c2, a_mux_d1, a_mux_d2, and_1_out, and_9_out, and_10_out, and_11_out,
       and_12_out, and_22_out, and_23_out, b_mux_a1, b_mux_a2, b_mux_c2, b_mux_d1, b_mux_d2, comparator_1_eq,
       multiplexer_14_out, multiplexer_15_out, nor_3_out, nor_5_out, nor_7_out, nor_8_out, nor_11_out,
       nor_12_out, xor_1_out, xor_2_out, xor_3_out, xor_4_out;
  wire [3:0] and_20_out, and_21_out, bitextender_1_out, bitextender_2_out, bitextender_3_out,
       bitextender_4_out, FL_de_t, FL_e_t, multiplexer_3_out, multiplexer_4_out, multiplexer_5_out,
       multiplexer_6_out, multiplexer_20_out, multiplexer_21_out, or_1_out, or_3_out, or_11_out, or_13_out,
       R1_de, R1_e, R2_de, R2_e, R3_de, R3_e, R4_de, R4_e, R5_de, R5_e, R6_de, R6_e, R7_de, R7_e, R8_de,
       R8_e, R9_de, R9_e, R10_de, R10_e, R11_de, R11_e, R12_de, R12_e, R13_de, R13_e, R14_de, R14_e, R15_de,
       R15_e, R16_de, R16_e, R17_de, R17_e, R18_de, R18_e, R19_de, R19_e, R20_de, R20_e, R21_de, R21_e,
       R22_de, R22_e, R23_de, R23_e, R24_de, R24_e, R25_de, R25_e, R_de, R_e, RD1, RD2, RD3, RD4, RD5, RD6,
       RD7, RD8, RD9, RD10, RD11, RD12, RD13, RD14, RD15, RD16, RD17, RD18, RD19, RD20, RD21, RD22, RD23,
       RD24, RD25, RDSBP, SBP_de, SBP_e, SC_de_t, SC_e_t;
  wire [6:6] FL_d_o;
  wire [7:0] and_14_out, and_15_out, and_16_out, and_17_out, and_18_out, and_19_out, bitextender_5_out,
       bitextender_6_out, bitextender_7_out, bitextender_8_out, bitextender_9_out, bitextender_10_out,
       bitextender_11_out, bitextender_12_out, multiplexer_7_out, multiplexer_8_out, multiplexer_9_out,
       multiplexer_10_out;
  wire [31:0] multiplexer_1_out, multiplexer_2_out, R1, R2, R3, R4, R5, R6, R7, R8, R9, R10, R11, R12, R13,
       R14, R15, R16, R17, R18, R19, R20, R21, R22, R23, R24, R25, R_A_t, R_B_t, register_1_q, register_2_q,
       SBP;
  wire [31:8] R_i;

  Multiplexer #(.Bits(32)) multiplexer_1 (.sel(SC_sel), .in_0({R_i, D[7:0]}), .in_1(SC_i), .out(multiplexer_1_out));
  BitExtender #(.inputBits(1), .outputBits(4)) bitextender_1 (.in(SC_e), .out(bitextender_1_out));
  Multiplexer #(.Bits(32)) multiplexer_2 (.sel(and_1_out), .in_0({R_i, D[7:0]}), .in_1(FL_i), .out(multiplexer_2_out));
  Comparator #(.Bits(5)) comparator_1 (.a({5{1'b1}}), .b(RW), .eq(comparator_1_eq));  // open: gt, lt
  reg8x4_ready u_R1 (.C(C), .D_i({R_i, D[7:0]}), .E(R1_e), .D(R1_de), .D_o(R1), .R(RD1));
  reg8x4_ready u_R5 (.C(C), .D_i({R_i, D[7:0]}), .E(R5_e), .D(R5_de), .D_o(R5), .R(RD5));
  reg8x4_ready u_R9 (.C(C), .D_i({R_i, D[7:0]}), .E(R9_e), .D(R9_de), .D_o(R9), .R(RD9));
  reg8x4_ready u_R13 (.C(C), .D_i({R_i, D[7:0]}), .E(R13_e), .D(R13_de), .D_o(R13), .R(RD13));
  reg8x4_ready u_R17 (.C(C), .D_i({R_i, D[7:0]}), .E(R17_e), .D(R17_de), .D_o(R17), .R(RD17));
  reg8x4_ready u_R21 (.C(C), .D_i({R_i, D[7:0]}), .E(R21_e), .D(R21_de), .D_o(R21), .R(RD21));
  reg8x4_ready u_R25 (.C(C), .D_i({R_i, D[7:0]}), .E(R25_e), .D(R25_de), .D_o(R25), .R(RD25));
  Multiplexer #(.Bits(4)) multiplexer_3 (
    .sel(SC_sel), .in_0(SC_e_t), .in_1(bitextender_1_out), .out(multiplexer_3_out));
  and and_1 (and_1_out, ~comparator_1_eq, FL_sel);  // And
  Multiplexer #(.Bits(4)) multiplexer_4 (.sel(and_1_out), .in_0(FL_e_t), .in_1(FL_e), .out(multiplexer_4_out));
  BitExtender #(.inputBits(1), .outputBits(4)) bitextender_2 (.in(SC_de), .out(bitextender_2_out));
  reg8x4_ready u_R2 (.C(C), .D_i({R_i, D[7:0]}), .E(R2_e), .D(R2_de), .D_o(R2), .R(RD2));
  reg8x4_ready u_R6 (.C(C), .D_i({R_i, D[7:0]}), .E(R6_e), .D(R6_de), .D_o(R6), .R(RD6));
  reg8x4_ready u_R10 (.C(C), .D_i({R_i, D[7:0]}), .E(R10_e), .D(R10_de), .D_o(R10), .R(RD10));
  reg8x4_ready u_R14 (.C(C), .D_i({R_i, D[7:0]}), .E(R14_e), .D(R14_de), .D_o(R14), .R(RD14));
  reg8x4_ready u_R18 (.C(C), .D_i({R_i, D[7:0]}), .E(R18_e), .D(R18_de), .D_o(R18), .R(RD18));
  reg8x4_ready u_R22 (.C(C), .D_i({R_i, D[7:0]}), .E(R22_e), .D(R22_de), .D_o(R22), .R(RD22));
  BitExtender #(.inputBits(1), .outputBits(4)) bitextender_3 (.in(PCA_e), .out(bitextender_3_out));
  BitExtender #(.inputBits(1), .outputBits(4)) bitextender_4 (.in(PCS_e), .out(bitextender_4_out));
  Multiplexer #(.Bits(4)) multiplexer_5 (
    .sel(SC_sel), .in_0(SC_de_t), .in_1(bitextender_2_out), .out(multiplexer_5_out));
  Multiplexer #(.Bits(4)) multiplexer_6 (.sel(and_1_out), .in_0(FL_de_t), .in_1(FL_de), .out(multiplexer_6_out));
  reg8x4_ready u_SBP (.C(C), .D_i({R_i, D[7:0]}), .E(SBP_e), .D(SBP_de), .D_o(SBP), .R(RDSBP));
  reg8x4_ready PCA (.C(C), .D_i(PCA_i), .E(bitextender_3_out), .D(4'b0000), .D_o(PCA_O));  // open: R
  reg8x4_ready PCS (.C(C), .D_i(PCS_i), .E(bitextender_4_out), .D(4'b0000), .D_o(PCS_O));  // open: R
  reg8x4_ready SC (.C(C), .D_i(multiplexer_1_out), .E(multiplexer_3_out), .D(multiplexer_5_out), .D_o(SC_O), .R(SC_RD));
  reg8x4_ready FL (
    .C(C), .D_i(multiplexer_2_out), .E(multiplexer_4_out), .D(multiplexer_6_out),
    .D_o({FL_O[31:7], FL_d_o[6], FL_O[5:0]}), .R(FL_RD));
  reg8x4_ready u_R3 (.C(C), .D_i({R_i, D[7:0]}), .E(R3_e), .D(R3_de), .D_o(R3), .R(RD3));
  reg8x4_ready u_R7 (.C(C), .D_i({R_i, D[7:0]}), .E(R7_e), .D(R7_de), .D_o(R7), .R(RD7));
  reg8x4_ready u_R11 (.C(C), .D_i({R_i, D[7:0]}), .E(R11_e), .D(R11_de), .D_o(R11), .R(RD11));
  reg8x4_ready u_R15 (.C(C), .D_i({R_i, D[7:0]}), .E(R15_e), .D(R15_de), .D_o(R15), .R(RD15));
  reg8x4_ready u_R19 (.C(C), .D_i({R_i, D[7:0]}), .E(R19_e), .D(R19_de), .D_o(R19), .R(RD19));
  reg8x4_ready u_R23 (.C(C), .D_i({R_i, D[7:0]}), .E(R23_e), .D(R23_de), .D_o(R23), .R(RD23));
  reg8x4_ready u_R4 (.C(C), .D_i({R_i, D[7:0]}), .E(R4_e), .D(R4_de), .D_o(R4), .R(RD4));
  reg8x4_ready u_R8 (.C(C), .D_i({R_i, D[7:0]}), .E(R8_e), .D(R8_de), .D_o(R8), .R(RD8));
  reg8x4_ready u_R12 (.C(C), .D_i({R_i, D[7:0]}), .E(R12_e), .D(R12_de), .D_o(R12), .R(RD12));
  reg8x4_ready u_R16 (.C(C), .D_i({R_i, D[7:0]}), .E(R16_e), .D(R16_de), .D_o(R16), .R(RD16));
  reg8x4_ready u_R20 (.C(C), .D_i({R_i, D[7:0]}), .E(R20_e), .D(R20_de), .D_o(R20), .R(RD20));
  reg8x4_ready u_R24 (.C(C), .D_i({R_i, D[7:0]}), .E(R24_e), .D(R24_de), .D_o(R24), .R(RD24));
  and and_2 (a_mux_c2, MA[2], MA[1]);
  nor nor_1 (a_mux_d1, MA[2], MA[1], MA[0]);
  and and_3 (b_mux_c2, MB[2], MB[1]);
  nor nor_2 (b_mux_d1, MB[2], MB[1], MB[0]);
  nor nor_3 (nor_3_out, MW[2], MW[1], MW[0]);
  and and_4 (a_mux_a1, MA[1], MA[0]);
  and and_5 (a_mux_a2, MA[2], ~MA[1], ~MA[0]);  // And
  not not_1 (a_mux_d2, MA[1]);
  and and_6 (b_mux_a1, MB[1], MB[0]);
  and and_7 (b_mux_a2, MB[2], ~MB[1], ~MB[0]);  // And
  not not_2 (b_mux_d2, MB[1]);
  xor xor_1 (xor_1_out, MW[0], MW[1]);
  Register #(.Bits(32)) register_1 (.D(PCS_O), .C(C), .en(PCS_e), .Q(register_1_q));
  nor nor_4 (or_1_out[3], MW[1], MW[0]);
  or or_1 (or_1_out[1], nor_3_out, MW[0]);
  or or_2 (or_1_out[0], xor_1_out, nor_3_out);
  Demultiplexer #(.Selector_Bits(5), .Bits(4)) demultiplexer_1 (
    .sel(RW), .in(R_e), .out_0(R1_e), .out_1(R2_e), .out_2(R3_e), .out_3(R4_e), .out_4(R5_e), .out_5(R6_e),
    .out_6(R7_e), .out_7(R8_e), .out_8(R9_e), .out_9(R10_e), .out_10(R11_e), .out_11(R12_e), .out_12(R13_e),
    .out_13(R14_e), .out_14(R15_e), .out_15(R16_e), .out_16(R17_e), .out_17(R18_e), .out_18(R19_e),
    .out_19(R20_e), .out_20(R21_e), .out_21(R22_e), .out_22(R23_e), .out_23(R24_e), .out_24(R25_e),
    .out_25(SBP_e), .out_30(SC_e_t), .out_31(FL_e_t));  // open: out_26, out_27, out_28, out_29
  nor nor_5 (nor_5_out, MD[2], MD[1], MD[0]);
  Register #(.Bits(32)) register_2 (.D(register_1_q), .C(C), .en(PCS_e), .Q(register_2_q));
  xor xor_2 (xor_2_out, MD[0], MD[1]);
  nor nor_6 (or_3_out[3], MD[1], MD[0]);
  or or_3 (or_3_out[1], nor_5_out, MD[0]);
  or or_4 (or_3_out[0], xor_2_out, nor_5_out);
  Multiplexer #(.Bits(8)) multiplexer_7 (
    .sel(a_mux_a2), .in_0(R_A_t[15:8]), .in_1(R_A_t[31:24]), .out(multiplexer_7_out));
  Multiplexer #(.Bits(8)) multiplexer_8 (
    .sel(a_mux_a1), .in_0(R_A_t[7:0]), .in_1(R_A_t[15:8]), .out(multiplexer_8_out));
  Multiplexer #(.Bits(8)) multiplexer_9 (
    .sel(b_mux_a2), .in_0(R_B_t[15:8]), .in_1(R_B_t[31:24]), .out(multiplexer_9_out));
  Multiplexer #(.Bits(8)) multiplexer_10 (
    .sel(b_mux_a1), .in_0(R_B_t[7:0]), .in_1(R_B_t[15:8]), .out(multiplexer_10_out));
  assign R_e = {{2{or_1_out[3]}}, or_1_out[1:0]} & {4{E}};  // And and_8, 4 bits wide
  Multiplexer #(.Selector_Bits(5), .Bits(32)) multiplexer_11 (
    .sel(RA), .in_0(R1), .in_1(R2), .in_2(R3), .in_3(R4), .in_4(R5), .in_5(R6), .in_6(R7), .in_7(R8),
    .in_8(R9), .in_9(R10), .in_10(R11), .in_11(R12), .in_12(R13), .in_13(R14), .in_14(R15), .in_15(R16),
    .in_16(R17), .in_17(R18), .in_18(R19), .in_19(R20), .in_20(R21), .in_21(R22), .in_22(R23), .in_23(R24),
    .in_24(R25), .in_25(SBP), .in_26({32{1'b0}}), .in_27(32'h1), .in_28({32{1'b1}}), .in_29(register_2_q),
    .in_30(SC_O), .in_31({FL_O[31:7], 1'b1, FL_O[5:0]}), .out(R_A_t));
  Multiplexer #(.Bits(8)) multiplexer_12 (
    .sel(a_mux_a2), .in_0(multiplexer_8_out), .in_1(R_A_t[23:16]), .out(R_A[7:0]));
  Multiplexer #(.Bits(8)) multiplexer_13 (
    .sel(b_mux_a2), .in_0(multiplexer_10_out), .in_1(R_B_t[23:16]), .out(R_B[7:0]));
  BitExtender #(.inputBits(1), .outputBits(8)) bitextender_5 (.in(a_mux_d1), .out(bitextender_5_out));
  and and_9 (and_9_out, MA[2], multiplexer_14_out);
  Multiplexer multiplexer_14 (.sel(MA[1]), .in_0(multiplexer_7_out[7]), .in_1(R_A[7]), .out(multiplexer_14_out));
  and and_10 (and_10_out, R_A[7], a_mux_c2);
  BitExtender #(.inputBits(1), .outputBits(8)) bitextender_6 (.in(b_mux_d1), .out(bitextender_6_out));
  and and_11 (and_11_out, MB[2], multiplexer_15_out);
  Multiplexer multiplexer_15 (.sel(MB[1]), .in_0(multiplexer_9_out[7]), .in_1(R_B[7]), .out(multiplexer_15_out));
  and and_12 (and_12_out, R_B[7], b_mux_c2);
  Multiplexer #(.Selector_Bits(5), .Bits(32)) multiplexer_16 (
    .sel(RB), .in_0(R1), .in_1(R2), .in_2(R3), .in_3(R4), .in_4(R5), .in_5(R6), .in_6(R7), .in_7(R8),
    .in_8(R9), .in_9(R10), .in_10(R11), .in_11(R12), .in_12(R13), .in_13(R14), .in_14(R15), .in_15(R16),
    .in_16(R17), .in_17(R18), .in_18(R19), .in_19(R20), .in_20(R21), .in_21(R22), .in_22(R23), .in_23(R24),
    .in_24(R25), .in_25(SBP), .in_26({32{1'b0}}), .in_27(32'h1), .in_28({32{1'b1}}), .in_29(register_2_q),
    .in_30(SC_O), .in_31({FL_O[31:7], 1'b1, FL_O[5:0]}), .out(R_B_t));
  assign R_de = {{2{or_3_out[3]}}, or_3_out[1:0]} & {4{DE}};  // And and_13, 4 bits wide
  assign and_14_out = bitextender_5_out & R_A_t[31:24];  // And and_14, 8 bits wide
  assign and_15_out = bitextender_5_out & R_A_t[23:16];  // And and_15, 8 bits wide
  BitExtender #(.inputBits(1), .outputBits(8)) bitextender_7 (.in(a_mux_d2), .out(bitextender_7_out));
  assign and_16_out = bitextender_6_out & R_B_t[31:24];  // And and_16, 8 bits wide
  assign and_17_out = bitextender_6_out & R_B_t[23:16];  // And and_17, 8 bits wide
  BitExtender #(.inputBits(1), .outputBits(8)) bitextender_8 (.in(b_mux_d2), .out(bitextender_8_out));
  Multiplexer #(.Bits(8)) multiplexer_17 (.sel(MW[2]), .in_0(D[31:24]), .in_1(D[15:8]), .out(R_i[31:24]));
  Multiplexer #(.Bits(8)) multiplexer_18 (.sel(MW[2]), .in_0(D[23:16]), .in_1(D[7:0]), .out(R_i[23:16]));
  Multiplexer #(.Bits(8)) multiplexer_19 (.sel(MW[1]), .in_0(D[15:8]), .in_1(D[7:0]), .out(R_i[15:8]));
  BitExtender #(.inputBits(1), .outputBits(8)) bitextender_9 (.in(and_9_out), .out(bitextender_9_out));
  assign and_18_out = bitextender_7_out & multiplexer_7_out;  // And and_18, 8 bits wide
  BitExtender #(.inputBits(1), .outputBits(8)) bitextender_10 (.in(and_10_out), .out(bitextender_10_out));
  BitExtender #(.inputBits(1), .outputBits(8)) bitextender_11 (.in(and_11_out), .out(bitextender_11_out));
  assign and_19_out = bitextender_8_out & multiplexer_9_out;  // And and_19, 8 bits wide
  BitExtender #(.inputBits(1), .outputBits(8)) bitextender_12 (.in(and_12_out), .out(bitextender_12_out));
  assign R_A[31:24] = and_14_out | bitextender_9_out;  // Or or_5, 8 bits wide
  assign R_A[23:16] = and_15_out | bitextender_9_out;  // Or or_6, 8 bits wide
  assign R_A[15:8] = and_18_out | bitextender_10_out;  // Or or_7, 8 bits wide
  assign R_B[31:24] = and_16_out | bitextender_11_out;  // Or or_8, 8 bits wide
  assign R_B[23:16] = and_17_out | bitextender_11_out;  // Or or_9, 8 bits wide
  assign R_B[15:8] = and_19_out | bitextender_12_out;  // Or or_10, 8 bits wide
  Demultiplexer #(.Selector_Bits(5), .Bits(4)) demultiplexer_2 (
    .sel(RD), .in(R_de), .out_0(R1_de), .out_1(R2_de), .out_2(R3_de), .out_3(R4_de), .out_4(R5_de),
    .out_5(R6_de), .out_6(R7_de), .out_7(R8_de), .out_8(R9_de), .out_9(R10_de), .out_10(R11_de),
    .out_11(R12_de), .out_12(R13_de), .out_13(R14_de), .out_14(R15_de), .out_15(R16_de), .out_16(R17_de),
    .out_17(R18_de), .out_18(R19_de), .out_19(R20_de), .out_20(R21_de), .out_21(R22_de), .out_22(R23_de),
    .out_23(R24_de), .out_24(R25_de), .out_25(SBP_de), .out_30(SC_de_t), .out_31(FL_de_t));  // open: out_26, out_27, out_28, out_29
  Multiplexer #(.Selector_Bits(5), .Bits(4)) multiplexer_20 (
    .sel(RDA), .in_0(RD1), .in_1(RD2), .in_2(RD3), .in_3(RD4), .in_4(RD5), .in_5(RD6), .in_6(RD7),
    .in_7(RD8), .in_8(RD9), .in_9(RD10), .in_10(RD11), .in_11(RD12), .in_12(RD13), .in_13(RD14),
    .in_14(RD15), .in_15(RD16), .in_16(RD17), .in_17(RD18), .in_18(RD19), .in_19(RD20), .in_20(RD21),
    .in_21(RD22), .in_22(RD23), .in_23(RD24), .in_24(RD25), .in_25(RDSBP), .in_26(4'b1111), .in_27(4'b1111),
    .in_28(4'b1111), .in_29(4'b1111), .in_30(SC_RD), .in_31(FL_RD), .out(multiplexer_20_out));
  assign and_20_out = multiplexer_20_out & {{2{or_11_out[3]}}, or_11_out[1:0]};  // And and_20, 4 bits wide
  nor nor_7 (nor_7_out, RDAM[2], RDAM[1], RDAM[0]);
  xor xor_3 (xor_3_out, RDAM[0], RDAM[1]);
  nor nor_8 (nor_8_out, MDBM[2], MDBM[1], MDBM[0]);
  xor xor_4 (xor_4_out, MDBM[0], MDBM[1]);
  Multiplexer #(.Selector_Bits(5), .Bits(4)) multiplexer_21 (
    .sel(RDB), .in_0(RD1), .in_1(RD2), .in_2(RD3), .in_3(RD4), .in_4(RD5), .in_5(RD6), .in_6(RD7),
    .in_7(RD8), .in_8(RD9), .in_9(RD10), .in_10(RD11), .in_11(RD12), .in_12(RD13), .in_13(RD14),
    .in_14(RD15), .in_15(RD16), .in_16(RD17), .in_17(RD18), .in_18(RD19), .in_19(RD20), .in_20(RD21),
    .in_21(RD22), .in_22(RD23), .in_23(RD24), .in_24(RD25), .in_25(RDSBP), .in_26(4'b1111), .in_27(4'b1111),
    .in_28(4'b1111), .in_29(4'b1111), .in_30(SC_RD), .in_31(FL_RD), .out(multiplexer_21_out));
  nor nor_9 (or_11_out[3], RDAM[1], RDAM[0]);
  or or_11 (or_11_out[1], nor_7_out, RDAM[0]);
  or or_12 (or_11_out[0], xor_3_out, nor_7_out);
  nor nor_10 (or_13_out[3], MDBM[1], MDBM[0]);
  or or_13 (or_13_out[1], nor_8_out, MDBM[0]);
  or or_14 (or_13_out[0], xor_4_out, nor_8_out);
  assign and_21_out = multiplexer_21_out & {{2{or_13_out[3]}}, or_13_out[1:0]};  // And and_21, 4 bits wide
  nor nor_11 (nor_11_out, and_21_out[0], and_21_out[1], and_21_out[2], and_21_out[3]);
  nor nor_12 (nor_12_out, and_20_out[0], and_20_out[1], and_20_out[2], and_20_out[3]);
  and and_22 (and_22_out, nor_11_out, RDBE);
  and and_23 (and_23_out, RDAE, nor_12_out);
  or or_15 (NR, and_22_out, and_23_out);

  assign FL_O[6] = 1'b1;

  // Other names for the same wires on the sheet: FL (some bits) = {FL_O[31:7], FL_O[5:0]}; D_A[31:0] = R_A;
  //   D_B[31:0] = R_B; A_mode[2:0] = MA; a_mux_b1 = MA[1]; a_mux_c1 = MA[2]; B_mode[2:0] = MB; b_mux_b1 = MB[1];
  //   b_mux_c1 = MB[2]; D_I[31:0] = D; R_i[7:0] = D[7:0]; D_mode[2:0] = MD; FL_de__EX[3:0] = FL_de;
  //   FL_e__EX[3:0] = FL_e; PCA[31:0] = PCA_O; PCA_e__EX = PCA_e; PCS[31:0] = PCS_O; PCS_e__EX = PCS_e;
  //   RA_sel[4:0] = RA; RB_sel[4:0] = RB; RD_sel[4:0] = RD; RDA_e = RDAE; RDA_mode[2:0] = RDAM; RDA_sel[4:0] = RDA;
  //   RDB_e = RDBE; RDB_mode[2:0] = MDBM; RDB_sel[4:0] = RDB; RDFL[3:0] = FL_RD; RDSC[3:0] = SC_RD; RW_sel[4:0] = RW;
  //   SC[31:0] = SC_O; SC_de__EX = SC_de; SC_e__EX = SC_e; W_mode[2:0] = MW; w_mux_3 = MW[1]; w_mux_1 = MW[2];
  //   w_mux_2 = MW[2]

  // Notes on the sheet:
  //   PCA_i: data input for arcitectural PC
  //   SC_i: data input for SC
  //   FL_i: data input for FL
  //   SC_sel: enable SC extern mode
  //   FL_sel: enable FL extern mode
  //   PCA_e: arcitectural PC register enable
  //   SC_e: SC register enable
  //   FL_e: FL register enable
  //   MW: write mode:
  //   0: 32
  //   1: 16L
  //   2: 8L
  //   3: 8H
  //   4: 16H
  //   5: S16L (=16L)
  //   6: S8L (=8L)
  //   7: S8H (=8H)
  //   RW: register to write:
  //   0~25: general
  //   26: zero
  //   27: one
  //   28: full
  //   29: program counter
  //   30: stack counter
  //   31: flag
  //   RA: register to read:
  //   0~25: general
  //   26: zero
  //   27: one
  //   28: full
  //   29: program counter
  //   30: stack counter
  //   31: flag
  //   RB: register to read:
  //   0~25: general
  //   26: zero
  //   27: one
  //   28: full
  //   29: program counter
  //   30: stack counter
  //   31: flag
  //   MA: read mode:
  //   0: 32
  //   1: 16L
  //   2: 8L
  //   3: 8H
  //   4: 16H
  //   5: S16L
  //   6: S8L
  //   7: S8H
  //   MB: read mode:
  //   0: 32
  //   1: 16L
  //   2: 8L
  //   3: 8H
  //   4: 16H
  //   5: S16L
  //   6: S8L
  //   7: S8H
  //   R_A: register out a
  //   R_B: register out b
  //   PCS_O: speculative PC out
  //   SC_O: SC out
  //   FL_O: FL out
  //   E: enable
  //   SC_de: SC register disable
  //   FL_de: FL register disable
  //   NR: not ready
  //   SC_RD: SC ready
  //   FL_RD: FL ready
  //   RD: register to disable:
  //   0~25: general
  //   26: zero
  //   27: one
  //   28: full
  //   29: program counter
  //   30: stack counter
  //   31: flag
  //   MD: disable mode:
  //   0: 32
  //   1: 16L
  //   2: 8L
  //   3: 8H
  //   4: 16H
  //   5: S16L (=16L)
  //   6: S8L (=8L)
  //   7: S8H (=8H)
  //   DE: disable
  //   D: data in
  //   RDA: register to check ready:
  //   0~25: general
  //   26: zero
  //   27: one
  //   28: full
  //   29: program counter
  //   30: stack counter
  //   31: flag
  //   RDAM: check mode:
  //   0: 32
  //   1: 16L
  //   2: 8L
  //   3: 8H
  //   4: 16H
  //   5: S16L
  //   6: S8L
  //   7: S8H
  //   RDB: register to check ready:
  //   0~25: general
  //   26: zero
  //   27: one
  //   28: full
  //   29: program counter
  //   30: stack counter
  //   31: flag
  //   MDBM: check mode:
  //   0: 32
  //   1: 16L
  //   2: 8L
  //   3: 8H
  //   4: 16H
  //   5: S16L
  //   6: S8L
  //   7: S8H
  //   RDAE: enable ready check
  //   RDBE: enable ready check
  //   PCS_i: data input for speculative PC
  //   PCS_e: speculative PC register enable
  //   PCA_O: architectural PC out
endmodule
