// Digital circuit regFile3.dig as structural Verilog
module regFile3 (
  input  C,
  input  [31:0] FL_i,
  input  FL_sel,
  input  [3:0] FL_e,
  input  [2:0] MW,
  input  [4:0] RW,
  input  [4:0] RA,
  input  [4:0] RB,
  input  [2:0] MA,
  input  [2:0] MB,
  input  E,
  input  [31:0] D,
  input  [31:0] PCS_i,
  input  PCS_e,
  input  SCS_sel,
  input  SCS_e,
  input  [31:0] SCS_i,
  input  [4:0] com2_id,
  input  com2,
  input  [4:0] com1_id,
  input  com1,
  input  [4:0] GR_inst__id,
  input  [4:0] PC_inst__id,
  input  [4:0] SC_inst__id,
  input  [4:0] FL_inst__id,
  input  rollback,
  input  [31:0] PC_H,
  input  PC_HE,
  output [31:0] R_A,
  output [31:0] R_B,
  output [31:0] PCS_O,
  output [31:0] FL_O,
  output [31:0] SCS_O,
  output H_full
);

  wire a_mux_a1, a_mux_a2, a_mux_c2, a_mux_d1, a_mux_d2, and_2_out, and_3_out, and_4_out, and_12_out,
       and_13_out, and_15_out, and_16_out, and_17_out, and_18_out, b_mux_a1, b_mux_a2, b_mux_c2, b_mux_d1,
       b_mux_d2, comparator_1_eq, dipswitch_1_out, dipswitch_2_out, dipswitch_3_out, FL_HE, FL_sel__act,
       FLH_full, FLH_V, GH_full, MH1, MH2, MH3, MH4, MH5, MH6, MH7, MH8, MH9, MH10, MH11, MH12, MH13, MH14,
       MH15, MH16, MH17, MH18, MH19, MH20, MH21, MH22, MH23, MH24, MH25, MH26, MH27, MH28, MH29, MH30, MH31,
       MH32, multiplexer_43_out, multiplexer_44_out, nor_3_out, not_3_out, not_4_out, not_5_out, not_6_out,
       or_6_out, PCH_full, PCH_V, R_HE, SCH_full, SCH_V, SCS_HE, xor_1_out;
  wire [3:0] bitextender_2_out, bitextender_3_out, FL_e_t, multiplexer_22_out, multiplexer_23_out, or_4_out,
       R1_e, R2_e, R3_e, R4_e, R5_e, R6_e, R7_e, R8_e, R9_e, R10_e, R11_e, R12_e, R13_e, R14_e, R15_e, R16_e,
       R17_e, R18_e, R19_e, R20_e, R21_e, R22_e, R23_e, R24_e, R25_e, R_e, SBP_e, SCS_e_t;
  wire [4:0] multiplexer_1_out, multiplexer_2_out;
  wire [6:6] FL_d_o;
  wire [7:0] and_20_out, and_21_out, and_22_out, and_23_out, and_24_out, and_25_out, bitextender_4_out,
       bitextender_5_out, bitextender_6_out, bitextender_7_out, bitextender_8_out, bitextender_9_out,
       bitextender_10_out, bitextender_11_out, multiplexer_37_out, multiplexer_38_out, multiplexer_39_out,
       multiplexer_40_out;
  wire [31:0] bitextender_1_out, FLH, multiplexer_3_out, multiplexer_4_out, multiplexer_5_out,
       multiplexer_6_out, multiplexer_7_out, multiplexer_8_out, multiplexer_9_out, multiplexer_10_out,
       multiplexer_11_out, multiplexer_12_out, multiplexer_13_out, multiplexer_14_out, multiplexer_15_out,
       multiplexer_16_out, multiplexer_17_out, multiplexer_18_out, multiplexer_19_out, multiplexer_20_out,
       multiplexer_21_out, multiplexer_24_out, multiplexer_25_out, multiplexer_26_out, multiplexer_27_out,
       multiplexer_28_out, multiplexer_29_out, multiplexer_30_out, multiplexer_31_out, multiplexer_32_out,
       multiplexer_33_out, multiplexer_34_out, multiplexer_35_out, PCH, R1, R2, R3, R4, R5, R6, R7, R8, R9,
       R10, R11, R12, R13, R14, R15, R16, R17, R18, R19, R20, R21, R22, R23, R24, R25, R_A_t, R_B_t, R_H,
       register_1_q, register_2_q, RH1, RH2, RH3, RH4, RH5, RH6, RH7, RH8, RH9, RH10, RH11, RH12, RH13, RH14,
       RH15, RH16, RH17, RH18, RH19, RH20, RH21, RH22, RH23, RH24, RH25, RH26, RH27, RH28, RH29, RH30, RH31,
       RH32, RHV, SBP, SCH;
  wire [31:8] R_i;

  Multiplexer #(.Bits(5)) multiplexer_1 (
    .sel(SCS_sel), .in_0(GR_inst__id), .in_1(SC_inst__id), .out(multiplexer_1_out));
  Multiplexer #(.Bits(5)) multiplexer_2 (
    .sel(FL_sel__act), .in_0(GR_inst__id), .in_1(FL_inst__id), .out(multiplexer_2_out));
  DipSwitch dipswitch_1 (.out(dipswitch_1_out));
  DipSwitch dipswitch_2 (.out(dipswitch_2_out));
  DipSwitch dipswitch_3 (.out(dipswitch_3_out));
  history_queue2 history_queue2_1 (
    .C(C), .E(PC_HE), .id(PC_inst__id), .D(PC_H), .P1(rollback), .com1(com1), .com1_id(com1_id), .com2(com2),
    .com2_id(com2_id), .res(dipswitch_1_out), .V1(PCH_V), .D1(PCH), .full(PCH_full));  // open: I1
  history_queue3 history_queue3_1 (
    .C(C), .E(SCS_HE), .id(multiplexer_1_out), .D(SCS_O), .P1(rollback), .com1(com1), .com1_id(com1_id),
    .com2(com2), .com2_id(com2_id), .res(dipswitch_2_out), .V1(SCH_V), .D1(SCH), .full(SCH_full));  // open: I1
  history_queue3 history_queue3_2 (
    .C(C), .E(FL_HE), .id(multiplexer_2_out), .D({FL_O[31:7], 1'b1, FL_O[5:0]}), .P1(rollback), .com1(com1),
    .com1_id(com1_id), .com2(com2), .com2_id(com2_id), .res(dipswitch_3_out), .V1(FLH_V), .D1(FLH),
    .full(FLH_full));  // open: I1
  BitExtender #(.inputBits(1), .outputBits(32)) bitextender_1 (.in(rollback), .out(bitextender_1_out));
  history4 history4_1 (
    .C(C), .D(R_H), .R(RW), .inst(GR_inst__id), .push(R_HE), .valid(RHV), .out1(RH1), .out2(RH2), .out3(RH3),
    .out4(RH4), .out5(RH5), .out6(RH6), .out7(RH7), .out8(RH8), .out9(RH9), .out10(RH10), .out11(RH11),
    .out12(RH12), .out13(RH13), .out14(RH14), .out15(RH15), .out16(RH16), .out17(RH17), .out18(RH18),
    .out19(RH19), .out20(RH20), .out21(RH21), .out22(RH22), .out23(RH23), .out24(RH24), .out25(RH25),
    .out26(RH26), .out27(RH27), .out28(RH28), .out29(RH29), .out30(RH30), .out31(RH31), .out32(RH32));  // open: pop, RBP, halt
  assign {MH32, MH31, MH30, MH29, MH28, MH27, MH26, MH25, MH24, MH23, MH22, MH21, MH20, MH19, MH18, MH17, MH16, MH15, MH14, MH13, MH12, MH11, MH10, MH9, MH8, MH7, MH6, MH5, MH4, MH3, MH2, MH1} = bitextender_1_out & RHV;  // And and_1, 32 bits wide
  or or_1 (H_full, GH_full, PCH_full, SCH_full, FLH_full);
  Multiplexer #(.Bits(32)) multiplexer_3 (.sel(MH1), .in_0({R_i, D[7:0]}), .in_1(RH1), .out(multiplexer_3_out));
  Multiplexer #(.Bits(32)) multiplexer_4 (.sel(MH5), .in_0({R_i, D[7:0]}), .in_1(RH5), .out(multiplexer_4_out));
  Multiplexer #(.Bits(32)) multiplexer_5 (.sel(MH9), .in_0({R_i, D[7:0]}), .in_1(RH9), .out(multiplexer_5_out));
  Multiplexer #(.Bits(32)) multiplexer_6 (.sel(MH13), .in_0({R_i, D[7:0]}), .in_1(RH13), .out(multiplexer_6_out));
  Multiplexer #(.Bits(32)) multiplexer_7 (.sel(MH17), .in_0({R_i, D[7:0]}), .in_1(RH17), .out(multiplexer_7_out));
  Multiplexer #(.Bits(32)) multiplexer_8 (.sel(MH21), .in_0({R_i, D[7:0]}), .in_1(RH21), .out(multiplexer_8_out));
  Multiplexer #(.Bits(32)) multiplexer_9 (.sel(MH25), .in_0({R_i, D[7:0]}), .in_1(RH25), .out(multiplexer_9_out));
  Multiplexer #(.Bits(32)) multiplexer_10 (.sel(MH26), .in_0({R_i, D[7:0]}), .in_1(RH26), .out(multiplexer_10_out));
  reg8x4 u_R1 (.C(C), .D(multiplexer_3_out), .E(R1_e), .D_o(R1));
  reg8x4 u_R5 (.C(C), .D(multiplexer_4_out), .E(R5_e), .D_o(R5));
  reg8x4 u_R9 (.C(C), .D(multiplexer_5_out), .E(R9_e), .D_o(R9));
  reg8x4 u_R13 (.C(C), .D(multiplexer_6_out), .E(R13_e), .D_o(R13));
  reg8x4 u_R17 (.C(C), .D(multiplexer_7_out), .E(R17_e), .D_o(R17));
  reg8x4 u_R21 (.C(C), .D(multiplexer_8_out), .E(R21_e), .D_o(R21));
  reg8x4 u_R25 (.C(C), .D(multiplexer_9_out), .E(R25_e), .D_o(R25));
  reg8x4 u_SBP (.C(C), .D(multiplexer_10_out), .E(SBP_e), .D_o(SBP));
  and and_2 (and_2_out, rollback, PCH_V);
  and and_3 (and_3_out, rollback, SCH_V);
  and and_4 (and_4_out, rollback, FLH_V);
  Multiplexer #(.Bits(32)) multiplexer_11 (
    .sel(FL_sel__act), .in_0({R_i, D[7:0]}), .in_1(FL_i), .out(multiplexer_11_out));
  Comparator #(.Bits(5)) comparator_1 (.a({5{1'b1}}), .b(RW), .eq(comparator_1_eq));  // open: gt, lt
  Multiplexer #(.Bits(32)) multiplexer_12 (.sel(and_2_out), .in_0(PCS_i), .in_1(PCH), .out(multiplexer_12_out));
  Multiplexer #(.Bits(32)) multiplexer_13 (.sel(SCS_sel), .in_0({R_i, D[7:0]}), .in_1(SCS_i), .out(multiplexer_13_out));
  Multiplexer #(.Bits(32)) multiplexer_14 (
    .sel(and_3_out), .in_0(multiplexer_13_out), .in_1(SCH), .out(multiplexer_14_out));
  BitExtender #(.inputBits(1), .outputBits(4)) bitextender_2 (.in(SCS_e), .out(bitextender_2_out));
  Multiplexer #(.Bits(32)) multiplexer_15 (
    .sel(and_4_out), .in_0(multiplexer_11_out), .in_1(FLH), .out(multiplexer_15_out));
  and and_5 (FL_sel__act, ~comparator_1_eq, FL_sel);  // And
  Multiplexer #(.Bits(32)) multiplexer_16 (.sel(MH2), .in_0({R_i, D[7:0]}), .in_1(RH2), .out(multiplexer_16_out));
  Multiplexer #(.Bits(32)) multiplexer_17 (.sel(MH6), .in_0({R_i, D[7:0]}), .in_1(RH6), .out(multiplexer_17_out));
  Multiplexer #(.Bits(32)) multiplexer_18 (.sel(MH10), .in_0({R_i, D[7:0]}), .in_1(RH10), .out(multiplexer_18_out));
  Multiplexer #(.Bits(32)) multiplexer_19 (.sel(MH14), .in_0({R_i, D[7:0]}), .in_1(RH14), .out(multiplexer_19_out));
  Multiplexer #(.Bits(32)) multiplexer_20 (.sel(MH18), .in_0({R_i, D[7:0]}), .in_1(RH18), .out(multiplexer_20_out));
  Multiplexer #(.Bits(32)) multiplexer_21 (.sel(MH22), .in_0({R_i, D[7:0]}), .in_1(RH22), .out(multiplexer_21_out));
  BitExtender #(.inputBits(1), .outputBits(4)) bitextender_3 (.in(PCS_e), .out(bitextender_3_out));
  Multiplexer #(.Bits(4)) multiplexer_22 (
    .sel(SCS_sel), .in_0(SCS_e_t), .in_1(bitextender_2_out), .out(multiplexer_22_out));
  Multiplexer #(.Bits(4)) multiplexer_23 (.sel(FL_sel__act), .in_0(FL_e_t), .in_1(FL_e), .out(multiplexer_23_out));
  reg8x4 u_R2 (.C(C), .D(multiplexer_16_out), .E(R2_e), .D_o(R2));
  reg8x4 u_R6 (.C(C), .D(multiplexer_17_out), .E(R6_e), .D_o(R6));
  reg8x4 u_R10 (.C(C), .D(multiplexer_18_out), .E(R10_e), .D_o(R10));
  reg8x4 u_R14 (.C(C), .D(multiplexer_19_out), .E(R14_e), .D_o(R14));
  reg8x4 u_R18 (.C(C), .D(multiplexer_20_out), .E(R18_e), .D_o(R18));
  reg8x4 u_R22 (.C(C), .D(multiplexer_21_out), .E(R22_e), .D_o(R22));
  reg8x4 PC (.C(C), .D(multiplexer_12_out), .E(bitextender_3_out), .D_o(PCS_O));
  reg8x4 SC (.C(C), .D(multiplexer_14_out), .E(multiplexer_22_out), .D_o(SCS_O));
  reg8x4 FL (.C(C), .D(multiplexer_15_out), .E(multiplexer_23_out), .D_o({FL_O[31:7], FL_d_o[6], FL_O[5:0]}));
  or or_2 (SCS_HE, multiplexer_22_out[0], multiplexer_22_out[1], multiplexer_22_out[2], multiplexer_22_out[3]);
  or or_3 (FL_HE, multiplexer_23_out[0], multiplexer_23_out[1], multiplexer_23_out[2], multiplexer_23_out[3]);
  Multiplexer #(.Bits(32)) multiplexer_24 (.sel(MH3), .in_0({R_i, D[7:0]}), .in_1(RH3), .out(multiplexer_24_out));
  Multiplexer #(.Bits(32)) multiplexer_25 (.sel(MH7), .in_0({R_i, D[7:0]}), .in_1(RH7), .out(multiplexer_25_out));
  Multiplexer #(.Bits(32)) multiplexer_26 (.sel(MH11), .in_0({R_i, D[7:0]}), .in_1(RH11), .out(multiplexer_26_out));
  Multiplexer #(.Bits(32)) multiplexer_27 (.sel(MH15), .in_0({R_i, D[7:0]}), .in_1(RH15), .out(multiplexer_27_out));
  Multiplexer #(.Bits(32)) multiplexer_28 (.sel(MH19), .in_0({R_i, D[7:0]}), .in_1(RH19), .out(multiplexer_28_out));
  Multiplexer #(.Bits(32)) multiplexer_29 (.sel(MH23), .in_0({R_i, D[7:0]}), .in_1(RH23), .out(multiplexer_29_out));
  reg8x4 u_R3 (.C(C), .D(multiplexer_24_out), .E(R3_e), .D_o(R3));
  reg8x4 u_R7 (.C(C), .D(multiplexer_25_out), .E(R7_e), .D_o(R7));
  reg8x4 u_R11 (.C(C), .D(multiplexer_26_out), .E(R11_e), .D_o(R11));
  reg8x4 u_R15 (.C(C), .D(multiplexer_27_out), .E(R15_e), .D_o(R15));
  reg8x4 u_R19 (.C(C), .D(multiplexer_28_out), .E(R19_e), .D_o(R19));
  reg8x4 u_R23 (.C(C), .D(multiplexer_29_out), .E(R23_e), .D_o(R23));
  Multiplexer #(.Bits(32)) multiplexer_30 (.sel(MH4), .in_0({R_i, D[7:0]}), .in_1(RH4), .out(multiplexer_30_out));
  Multiplexer #(.Bits(32)) multiplexer_31 (.sel(MH8), .in_0({R_i, D[7:0]}), .in_1(RH8), .out(multiplexer_31_out));
  Multiplexer #(.Bits(32)) multiplexer_32 (.sel(MH12), .in_0({R_i, D[7:0]}), .in_1(RH12), .out(multiplexer_32_out));
  Multiplexer #(.Bits(32)) multiplexer_33 (.sel(MH16), .in_0({R_i, D[7:0]}), .in_1(RH16), .out(multiplexer_33_out));
  Multiplexer #(.Bits(32)) multiplexer_34 (.sel(MH20), .in_0({R_i, D[7:0]}), .in_1(RH20), .out(multiplexer_34_out));
  Multiplexer #(.Bits(32)) multiplexer_35 (.sel(MH24), .in_0({R_i, D[7:0]}), .in_1(RH24), .out(multiplexer_35_out));
  reg8x4 u_R4 (.C(C), .D(multiplexer_30_out), .E(R4_e), .D_o(R4));
  reg8x4 u_R8 (.C(C), .D(multiplexer_31_out), .E(R8_e), .D_o(R8));
  reg8x4 u_R12 (.C(C), .D(multiplexer_32_out), .E(R12_e), .D_o(R12));
  reg8x4 u_R16 (.C(C), .D(multiplexer_33_out), .E(R16_e), .D_o(R16));
  reg8x4 u_R20 (.C(C), .D(multiplexer_34_out), .E(R20_e), .D_o(R20));
  reg8x4 u_R24 (.C(C), .D(multiplexer_35_out), .E(R24_e), .D_o(R24));
  and and_6 (a_mux_c2, MA[2], MA[1]);
  nor nor_1 (a_mux_d1, MA[2], MA[1], MA[0]);
  and and_7 (b_mux_c2, MB[2], MB[1]);
  nor nor_2 (b_mux_d1, MB[2], MB[1], MB[0]);
  nor nor_3 (nor_3_out, MW[2], MW[1], MW[0]);
  and and_8 (a_mux_a1, MA[1], MA[0]);
  and and_9 (a_mux_a2, MA[2], ~MA[1], ~MA[0]);  // And
  not not_1 (a_mux_d2, MA[1]);
  and and_10 (b_mux_a1, MB[1], MB[0]);
  and and_11 (b_mux_a2, MB[2], ~MB[1], ~MB[0]);  // And
  not not_2 (b_mux_d2, MB[1]);
  xor xor_1 (xor_1_out, MW[0], MW[1]);
  nor nor_4 (or_4_out[3], MW[1], MW[0]);
  or or_4 (or_4_out[1], nor_3_out, MW[0]);
  or or_5 (or_4_out[0], xor_1_out, nor_3_out);
  Demultiplexer #(.Selector_Bits(5), .Bits(4)) demultiplexer_1 (
    .sel(RW), .in(R_e), .out_0(R1_e), .out_1(R2_e), .out_2(R3_e), .out_3(R4_e), .out_4(R5_e), .out_5(R6_e),
    .out_6(R7_e), .out_7(R8_e), .out_8(R9_e), .out_9(R10_e), .out_10(R11_e), .out_11(R12_e), .out_12(R13_e),
    .out_13(R14_e), .out_14(R15_e), .out_15(R16_e), .out_16(R17_e), .out_17(R18_e), .out_18(R19_e),
    .out_19(R20_e), .out_20(R21_e), .out_21(R22_e), .out_22(R23_e), .out_23(R24_e), .out_24(R25_e),
    .out_25(SBP_e), .out_30(SCS_e_t), .out_31(FL_e_t));  // open: out_26, out_27, out_28, out_29
  Register #(.Bits(32)) register_1 (.D(PCS_O), .C(C), .en(PCS_e), .Q(register_1_q));
  not not_3 (not_3_out, RW[4]);
  not not_4 (not_4_out, RW[3]);
  not not_5 (not_5_out, RW[2]);
  not not_6 (not_6_out, RW[1]);
  Multiplexer #(.Selector_Bits(5), .Bits(32)) multiplexer_36 (
    .sel(RW), .in_0(R1), .in_1(R2), .in_2(R3), .in_3(R4), .in_4(R5), .in_5(R6), .in_6(R7), .in_7(R8),
    .in_8(R9), .in_9(R10), .in_10(R11), .in_11(R12), .in_12(R13), .in_13(R14), .in_14(R15), .in_15(R16),
    .in_16(R17), .in_17(R18), .in_18(R19), .in_19(R20), .in_20(R21), .in_21(R22), .in_22(R23), .in_23(R24),
    .in_24(R25), .in_25(SBP), .in_26({32{1'b0}}), .in_27({32{1'b0}}), .in_28({32{1'b0}}), .in_29({32{1'b0}}),
    .in_30({32{1'b0}}), .in_31({32{1'b0}}), .out(R_H));
  Register #(.Bits(32)) register_2 (.D(register_1_q), .C(C), .en(PCS_e), .Q(register_2_q));
  and and_12 (and_12_out, RW[4], not_4_out);
  and and_13 (and_13_out, RW[4], RW[3], not_5_out, not_6_out);
  Multiplexer #(.Bits(8)) multiplexer_37 (
    .sel(a_mux_a2), .in_0(R_A_t[15:8]), .in_1(R_A_t[31:24]), .out(multiplexer_37_out));
  Multiplexer #(.Bits(8)) multiplexer_38 (
    .sel(a_mux_a1), .in_0(R_A_t[7:0]), .in_1(R_A_t[15:8]), .out(multiplexer_38_out));
  Multiplexer #(.Bits(8)) multiplexer_39 (
    .sel(b_mux_a2), .in_0(R_B_t[15:8]), .in_1(R_B_t[31:24]), .out(multiplexer_39_out));
  Multiplexer #(.Bits(8)) multiplexer_40 (
    .sel(b_mux_a1), .in_0(R_B_t[7:0]), .in_1(R_B_t[15:8]), .out(multiplexer_40_out));
  assign R_e = {{2{or_4_out[3]}}, or_4_out[1:0]} & {4{E}};  // And and_14, 4 bits wide
  Multiplexer #(.Bits(8)) multiplexer_41 (
    .sel(a_mux_a2), .in_0(multiplexer_38_out), .in_1(R_A_t[23:16]), .out(R_A[7:0]));
  Multiplexer #(.Bits(8)) multiplexer_42 (
    .sel(b_mux_a2), .in_0(multiplexer_40_out), .in_1(R_B_t[23:16]), .out(R_B[7:0]));
  or or_6 (or_6_out, not_3_out, and_12_out, and_13_out);
  BitExtender #(.inputBits(1), .outputBits(8)) bitextender_4 (.in(a_mux_d1), .out(bitextender_4_out));
  and and_15 (and_15_out, MA[2], multiplexer_43_out);
  Multiplexer multiplexer_43 (.sel(MA[1]), .in_0(multiplexer_37_out[7]), .in_1(R_A[7]), .out(multiplexer_43_out));
  and and_16 (and_16_out, R_A[7], a_mux_c2);
  BitExtender #(.inputBits(1), .outputBits(8)) bitextender_5 (.in(b_mux_d1), .out(bitextender_5_out));
  and and_17 (and_17_out, MB[2], multiplexer_44_out);
  Multiplexer multiplexer_44 (.sel(MB[1]), .in_0(multiplexer_39_out[7]), .in_1(R_B[7]), .out(multiplexer_44_out));
  and and_18 (and_18_out, R_B[7], b_mux_c2);
  Multiplexer #(.Selector_Bits(5), .Bits(32)) multiplexer_45 (
    .sel(RA), .in_0(R1), .in_1(R2), .in_2(R3), .in_3(R4), .in_4(R5), .in_5(R6), .in_6(R7), .in_7(R8),
    .in_8(R9), .in_9(R10), .in_10(R11), .in_11(R12), .in_12(R13), .in_13(R14), .in_14(R15), .in_15(R16),
    .in_16(R17), .in_17(R18), .in_18(R19), .in_19(R20), .in_20(R21), .in_21(R22), .in_22(R23), .in_23(R24),
    .in_24(R25), .in_25(SBP), .in_26({32{1'b0}}), .in_27(32'h1), .in_28({32{1'b1}}), .in_29(register_2_q),
    .in_30(SCS_O), .in_31({FL_O[31:7], 1'b1, FL_O[5:0]}), .out(R_A_t));
  and and_19 (R_HE, E, or_6_out);
  assign and_20_out = bitextender_4_out & R_A_t[31:24];  // And and_20, 8 bits wide
  assign and_21_out = bitextender_4_out & R_A_t[23:16];  // And and_21, 8 bits wide
  BitExtender #(.inputBits(1), .outputBits(8)) bitextender_6 (.in(a_mux_d2), .out(bitextender_6_out));
  assign and_22_out = bitextender_5_out & R_B_t[31:24];  // And and_22, 8 bits wide
  assign and_23_out = bitextender_5_out & R_B_t[23:16];  // And and_23, 8 bits wide
  BitExtender #(.inputBits(1), .outputBits(8)) bitextender_7 (.in(b_mux_d2), .out(bitextender_7_out));
  Multiplexer #(.Bits(8)) multiplexer_46 (.sel(MW[2]), .in_0(D[31:24]), .in_1(D[15:8]), .out(R_i[31:24]));
  Multiplexer #(.Bits(8)) multiplexer_47 (.sel(MW[2]), .in_0(D[23:16]), .in_1(D[7:0]), .out(R_i[23:16]));
  Multiplexer #(.Bits(8)) multiplexer_48 (.sel(MW[1]), .in_0(D[15:8]), .in_1(D[7:0]), .out(R_i[15:8]));
  BitExtender #(.inputBits(1), .outputBits(8)) bitextender_8 (.in(and_15_out), .out(bitextender_8_out));
  assign and_24_out = bitextender_6_out & multiplexer_37_out;  // And and_24, 8 bits wide
  BitExtender #(.inputBits(1), .outputBits(8)) bitextender_9 (.in(and_16_out), .out(bitextender_9_out));
  BitExtender #(.inputBits(1), .outputBits(8)) bitextender_10 (.in(and_17_out), .out(bitextender_10_out));
  assign and_25_out = bitextender_7_out & multiplexer_39_out;  // And and_25, 8 bits wide
  BitExtender #(.inputBits(1), .outputBits(8)) bitextender_11 (.in(and_18_out), .out(bitextender_11_out));
  Multiplexer #(.Selector_Bits(5), .Bits(32)) multiplexer_49 (
    .sel(RB), .in_0(R1), .in_1(R2), .in_2(R3), .in_3(R4), .in_4(R5), .in_5(R6), .in_6(R7), .in_7(R8),
    .in_8(R9), .in_9(R10), .in_10(R11), .in_11(R12), .in_12(R13), .in_13(R14), .in_14(R15), .in_15(R16),
    .in_16(R17), .in_17(R18), .in_18(R19), .in_19(R20), .in_20(R21), .in_21(R22), .in_22(R23), .in_23(R24),
    .in_24(R25), .in_25(SBP), .in_26({32{1'b0}}), .in_27(32'h1), .in_28({32{1'b1}}), .in_29(register_2_q),
    .in_30(SCS_O), .in_31({FL_O[31:7], 1'b1, FL_O[5:0]}), .out(R_B_t));
  assign R_A[31:24] = and_20_out | bitextender_8_out;  // Or or_7, 8 bits wide
  assign R_A[23:16] = and_21_out | bitextender_8_out;  // Or or_8, 8 bits wide
  assign R_A[15:8] = and_24_out | bitextender_9_out;  // Or or_9, 8 bits wide
  assign R_B[31:24] = and_22_out | bitextender_10_out;  // Or or_10, 8 bits wide
  assign R_B[23:16] = and_23_out | bitextender_10_out;  // Or or_11, 8 bits wide
  assign R_B[15:8] = and_25_out | bitextender_11_out;  // Or or_12, 8 bits wide

  assign FL_O[6] = 1'b1;

  // Other names for the same wires on the sheet: FL (some bits) = {FL_O[31:7], FL_O[5:0]}; D_A[31:0] = R_A;
  //   D_B[31:0] = R_B; A_mode[2:0] = MA; a_mux_b1 = MA[1]; a_mux_c1 = MA[2]; B_mode[2:0] = MB; b_mux_b1 = MB[1];
  //   b_mux_c1 = MB[2]; D_I[31:0] = D; R_i[7:0] = D[7:0]; FL_e__EX[3:0] = FL_e; PCS[31:0] = PCS_O; PCS_e__EX = PCS_e;
  //   PCS_H[31:0] = PC_H; PCS_HE = PC_HE; RA_sel[4:0] = RA; RB_sel[4:0] = RB; RW_sel[4:0] = RW; SCS[31:0] = SCS_O;
  //   SCS_e__EX = SCS_e; W_mode[2:0] = MW; w_mux_3 = MW[1]; w_mux_1 = MW[2]; w_mux_2 = MW[2]

  // Notes on the sheet:
  //   FL_i: data input for FL
  //   FL_sel: enable FL extern mode
  //   FL_e: FL register enable
  //   MW: write mode:
  //   0: 32
  //   1: 16L
  //   2: 8L
  //   3: 8H
  //   4: 16H
  //   5: S16L (=16L)
  //   6: S8L (=8L)
  //   7: S8H (=8H)
  //   RW: register to write:
  //   0~25: general
  //   26: zero
  //   27: one
  //   28: full
  //   29: program counter
  //   30: stack counter
  //   31: flag
  //   RA: register to read:
  //   0~25: general
  //   26: zero
  //   27: one
  //   28: full
  //   29: program counter
  //   30: stack counter
  //   31: flag
  //   RB: register to read:
  //   0~25: general
  //   26: zero
  //   27: one
  //   28: full
  //   29: program counter
  //   30: stack counter
  //   31: flag
  //   MA: read mode:
  //   0: 32
  //   1: 16L
  //   2: 8L
  //   3: 8H
  //   4: 16H
  //   5: S16L
  //   6: S8L
  //   7: S8H
  //   MB: read mode:
  //   0: 32
  //   1: 16L
  //   2: 8L
  //   3: 8H
  //   4: 16H
  //   5: S16L
  //   6: S8L
  //   7: S8H
  //   R_A: register out a
  //   R_B: register out b
  //   PCS_O: speculative PC out
  //   FL_O: FL out
  //   E: enable
  //   D: data in
  //   PCS_i: data input for speculative PC
  //   PCS_e: speculative PC register enable
  //   SCS_O: speculative SC out
  //   SCS_sel: enable speculative SC extern mode
  //   SCS_e: speculative SC register enable
  //   SCS_i: data input for speculative SC
  //   H_full: history buffer full
  //   GR_inst__id: general register instruction id
  //   PC_inst__id: program counter instruction id
  //   SC_inst__id: stack counter instruction id
  //   FL_inst__id: flag instruction id
  //   rollback: rollback
  //   PC_H: program counter history data
  //   PC_HE: program counter history store
endmodule
