// Digital circuit register32x32.dig as structural Verilog
module register32x32 (
  input  C,
  input  [31:0] D1,
  input  [31:0] D2,
  input  [4:0] S1,
  input  [4:0] S2,
  input  E1,
  input  E2,
  input  [31:0] Del,
  output [31:0] R0,
  output [31:0] R1,
  output [31:0] R2,
  output [31:0] R3,
  output [31:0] R4,
  output [31:0] R5,
  output [31:0] R6,
  output [31:0] R7,
  output [31:0] R8,
  output [31:0] R9,
  output [31:0] R10,
  output [31:0] R11,
  output [31:0] R12,
  output [31:0] R13,
  output [31:0] R14,
  output [31:0] R15,
  output [31:0] R16,
  output [31:0] R17,
  output [31:0] R18,
  output [31:0] R19,
  output [31:0] R20,
  output [31:0] R21,
  output [31:0] R22,
  output [31:0] R23,
  output [31:0] R24,
  output [31:0] R25,
  output [31:0] valid
);

  wire [31:0] and_1_out, demultiplexer_1_out_0, demultiplexer_2_out_0, multiplexer_1_out, multiplexer_2_out,
       multiplexer_3_out, multiplexer_4_out, multiplexer_5_out, multiplexer_6_out, multiplexer_7_out,
       multiplexer_8_out, multiplexer_9_out, multiplexer_10_out, multiplexer_11_out, multiplexer_12_out,
       multiplexer_13_out, multiplexer_14_out, multiplexer_15_out, multiplexer_16_out, multiplexer_17_out,
       multiplexer_18_out, multiplexer_19_out, multiplexer_20_out, multiplexer_21_out, multiplexer_22_out,
       multiplexer_23_out, multiplexer_24_out, multiplexer_25_out, multiplexer_26_out, not_1_out, or_1_out,
       or_2_out;

  Demultiplexer #(.Selector_Bits(5)) demultiplexer_1 (
    .sel(S1), .in(E1), .out_0(demultiplexer_1_out_0[0]), .out_1(demultiplexer_1_out_0[1]),
    .out_2(demultiplexer_1_out_0[2]), .out_3(demultiplexer_1_out_0[3]), .out_4(demultiplexer_1_out_0[4]),
    .out_5(demultiplexer_1_out_0[5]), .out_6(demultiplexer_1_out_0[6]), .out_7(demultiplexer_1_out_0[7]),
    .out_8(demultiplexer_1_out_0[8]), .out_9(demultiplexer_1_out_0[9]), .out_10(demultiplexer_1_out_0[10]),
    .out_11(demultiplexer_1_out_0[11]), .out_12(demultiplexer_1_out_0[12]),
    .out_13(demultiplexer_1_out_0[13]), .out_14(demultiplexer_1_out_0[14]),
    .out_15(demultiplexer_1_out_0[15]), .out_16(demultiplexer_1_out_0[16]),
    .out_17(demultiplexer_1_out_0[17]), .out_18(demultiplexer_1_out_0[18]),
    .out_19(demultiplexer_1_out_0[19]), .out_20(demultiplexer_1_out_0[20]),
    .out_21(demultiplexer_1_out_0[21]), .out_22(demultiplexer_1_out_0[22]),
    .out_23(demultiplexer_1_out_0[23]), .out_24(demultiplexer_1_out_0[24]),
    .out_25(demultiplexer_1_out_0[25]), .out_26(demultiplexer_1_out_0[26]),
    .out_27(demultiplexer_1_out_0[27]), .out_28(demultiplexer_1_out_0[28]),
    .out_29(demultiplexer_1_out_0[29]), .out_30(demultiplexer_1_out_0[30]), .out_31(demultiplexer_1_out_0[31]));
  Demultiplexer #(.Selector_Bits(5)) demultiplexer_2 (
    .sel(S2), .in(E2), .out_0(demultiplexer_2_out_0[0]), .out_1(demultiplexer_2_out_0[1]),
    .out_2(demultiplexer_2_out_0[2]), .out_3(demultiplexer_2_out_0[3]), .out_4(demultiplexer_2_out_0[4]),
    .out_5(demultiplexer_2_out_0[5]), .out_6(demultiplexer_2_out_0[6]), .out_7(demultiplexer_2_out_0[7]),
    .out_8(demultiplexer_2_out_0[8]), .out_9(demultiplexer_2_out_0[9]), .out_10(demultiplexer_2_out_0[10]),
    .out_11(demultiplexer_2_out_0[11]), .out_12(demultiplexer_2_out_0[12]),
    .out_13(demultiplexer_2_out_0[13]), .out_14(demultiplexer_2_out_0[14]),
    .out_15(demultiplexer_2_out_0[15]), .out_16(demultiplexer_2_out_0[16]),
    .out_17(demultiplexer_2_out_0[17]), .out_18(demultiplexer_2_out_0[18]),
    .out_19(demultiplexer_2_out_0[19]), .out_20(demultiplexer_2_out_0[20]),
    .out_21(demultiplexer_2_out_0[21]), .out_22(demultiplexer_2_out_0[22]),
    .out_23(demultiplexer_2_out_0[23]), .out_24(demultiplexer_2_out_0[24]),
    .out_25(demultiplexer_2_out_0[25]), .out_26(demultiplexer_2_out_0[26]),
    .out_27(demultiplexer_2_out_0[27]), .out_28(demultiplexer_2_out_0[28]),
    .out_29(demultiplexer_2_out_0[29]), .out_30(demultiplexer_2_out_0[30]), .out_31(demultiplexer_2_out_0[31]));
  assign or_1_out = demultiplexer_1_out_0 | demultiplexer_2_out_0;  // Or or_1, 32 bits wide
  assign not_1_out = ~Del;  // Not not_1, 32 bits wide
  assign and_1_out = not_1_out & or_1_out;  // And and_1, 32 bits wide
  assign or_2_out = Del | or_1_out;  // Or or_2, 32 bits wide
  Register V0 (.D(and_1_out[0]), .C(C), .en(or_2_out[0]), .Q(valid[0]));
  Multiplexer #(.Bits(32)) multiplexer_1 (
    .sel(demultiplexer_2_out_0[0]), .in_0(D1), .in_1(D2), .out(multiplexer_1_out));
  Register V1 (.D(and_1_out[1]), .C(C), .en(or_2_out[1]), .Q(valid[1]));
  Multiplexer #(.Bits(32)) multiplexer_2 (
    .sel(demultiplexer_2_out_0[1]), .in_0(D1), .in_1(D2), .out(multiplexer_2_out));
  Register V2 (.D(and_1_out[2]), .C(C), .en(or_2_out[2]), .Q(valid[2]));
  Multiplexer #(.Bits(32)) multiplexer_3 (
    .sel(demultiplexer_2_out_0[2]), .in_0(D1), .in_1(D2), .out(multiplexer_3_out));
  Register V3 (.D(and_1_out[3]), .C(C), .en(or_2_out[3]), .Q(valid[3]));
  Multiplexer #(.Bits(32)) multiplexer_4 (
    .sel(demultiplexer_2_out_0[3]), .in_0(D1), .in_1(D2), .out(multiplexer_4_out));
  Register V4 (.D(and_1_out[4]), .C(C), .en(or_2_out[4]), .Q(valid[4]));
  Multiplexer #(.Bits(32)) multiplexer_5 (
    .sel(demultiplexer_2_out_0[4]), .in_0(D1), .in_1(D2), .out(multiplexer_5_out));
  Register V5 (.D(and_1_out[5]), .C(C), .en(or_2_out[5]), .Q(valid[5]));
  Multiplexer #(.Bits(32)) multiplexer_6 (
    .sel(demultiplexer_2_out_0[5]), .in_0(D1), .in_1(D2), .out(multiplexer_6_out));
  Register V6 (.D(and_1_out[6]), .C(C), .en(or_2_out[6]), .Q(valid[6]));
  Multiplexer #(.Bits(32)) multiplexer_7 (
    .sel(demultiplexer_2_out_0[6]), .in_0(D1), .in_1(D2), .out(multiplexer_7_out));
  Register V7 (.D(and_1_out[7]), .C(C), .en(or_2_out[7]), .Q(valid[7]));
  Multiplexer #(.Bits(32)) multiplexer_8 (
    .sel(demultiplexer_2_out_0[7]), .in_0(D1), .in_1(D2), .out(multiplexer_8_out));
  Register V8 (.D(and_1_out[8]), .C(C), .en(or_2_out[8]), .Q(valid[8]));
  Multiplexer #(.Bits(32)) multiplexer_9 (
    .sel(demultiplexer_2_out_0[8]), .in_0(D1), .in_1(D2), .out(multiplexer_9_out));
  Register V9 (.D(and_1_out[9]), .C(C), .en(or_2_out[9]), .Q(valid[9]));
  Multiplexer #(.Bits(32)) multiplexer_10 (
    .sel(demultiplexer_2_out_0[9]), .in_0(D1), .in_1(D2), .out(multiplexer_10_out));
  Register V10 (.D(and_1_out[10]), .C(C), .en(or_2_out[10]), .Q(valid[10]));
  Multiplexer #(.Bits(32)) multiplexer_11 (
    .sel(demultiplexer_2_out_0[10]), .in_0(D1), .in_1(D2), .out(multiplexer_11_out));
  Register V11 (.D(and_1_out[11]), .C(C), .en(or_2_out[11]), .Q(valid[11]));
  Multiplexer #(.Bits(32)) multiplexer_12 (
    .sel(demultiplexer_2_out_0[11]), .in_0(D1), .in_1(D2), .out(multiplexer_12_out));
  Register V12 (.D(and_1_out[12]), .C(C), .en(or_2_out[12]), .Q(valid[12]));
  Multiplexer #(.Bits(32)) multiplexer_13 (
    .sel(demultiplexer_2_out_0[12]), .in_0(D1), .in_1(D2), .out(multiplexer_13_out));
  Register V13 (.D(and_1_out[13]), .C(C), .en(or_2_out[13]), .Q(valid[13]));
  Multiplexer #(.Bits(32)) multiplexer_14 (
    .sel(demultiplexer_2_out_0[13]), .in_0(D1), .in_1(D2), .out(multiplexer_14_out));
  Register V14 (.D(and_1_out[14]), .C(C), .en(or_2_out[14]), .Q(valid[14]));
  Multiplexer #(.Bits(32)) multiplexer_15 (
    .sel(demultiplexer_2_out_0[14]), .in_0(D1), .in_1(D2), .out(multiplexer_15_out));
  Register V15 (.D(and_1_out[15]), .C(C), .en(or_2_out[15]), .Q(valid[15]));
  Multiplexer #(.Bits(32)) multiplexer_16 (
    .sel(demultiplexer_2_out_0[15]), .in_0(D1), .in_1(D2), .out(multiplexer_16_out));
  Register V16 (.D(and_1_out[16]), .C(C), .en(or_2_out[16]), .Q(valid[16]));
  Multiplexer #(.Bits(32)) multiplexer_17 (
    .sel(demultiplexer_2_out_0[16]), .in_0(D1), .in_1(D2), .out(multiplexer_17_out));
  Register V17 (.D(and_1_out[17]), .C(C), .en(or_2_out[17]), .Q(valid[17]));
  Multiplexer #(.Bits(32)) multiplexer_18 (
    .sel(demultiplexer_2_out_0[17]), .in_0(D1), .in_1(D2), .out(multiplexer_18_out));
  Register V18 (.D(and_1_out[18]), .C(C), .en(or_2_out[18]), .Q(valid[18]));
  Multiplexer #(.Bits(32)) multiplexer_19 (
    .sel(demultiplexer_2_out_0[18]), .in_0(D1), .in_1(D2), .out(multiplexer_19_out));
  Register V19 (.D(and_1_out[19]), .C(C), .en(or_2_out[19]), .Q(valid[19]));
  Multiplexer #(.Bits(32)) multiplexer_20 (
    .sel(demultiplexer_2_out_0[19]), .in_0(D1), .in_1(D2), .out(multiplexer_20_out));
  Register V20 (.D(and_1_out[20]), .C(C), .en(or_2_out[20]), .Q(valid[20]));
  Multiplexer #(.Bits(32)) multiplexer_21 (
    .sel(demultiplexer_2_out_0[20]), .in_0(D1), .in_1(D2), .out(multiplexer_21_out));
  Register V21 (.D(and_1_out[21]), .C(C), .en(or_2_out[21]), .Q(valid[21]));
  Multiplexer #(.Bits(32)) multiplexer_22 (
    .sel(demultiplexer_2_out_0[21]), .in_0(D1), .in_1(D2), .out(multiplexer_22_out));
  Register V22 (.D(and_1_out[22]), .C(C), .en(or_2_out[22]), .Q(valid[22]));
  Multiplexer #(.Bits(32)) multiplexer_23 (
    .sel(demultiplexer_2_out_0[22]), .in_0(D1), .in_1(D2), .out(multiplexer_23_out));
  Register V23 (.D(and_1_out[23]), .C(C), .en(or_2_out[23]), .Q(valid[23]));
  Multiplexer #(.Bits(32)) multiplexer_24 (
    .sel(demultiplexer_2_out_0[23]), .in_0(D1), .in_1(D2), .out(multiplexer_24_out));
  Register V24 (.D(and_1_out[24]), .C(C), .en(or_2_out[24]), .Q(valid[24]));
  Multiplexer #(.Bits(32)) multiplexer_25 (
    .sel(demultiplexer_2_out_0[24]), .in_0(D1), .in_1(D2), .out(multiplexer_25_out));
  Register V25 (.D(and_1_out[25]), .C(C), .en(or_2_out[25]), .Q(valid[25]));
  Multiplexer #(.Bits(32)) multiplexer_26 (
    .sel(demultiplexer_2_out_0[25]), .in_0(D1), .in_1(D2), .out(multiplexer_26_out));
  Register #(.Bits(32)) u_R0 (.D(multiplexer_1_out), .C(C), .en(or_1_out[0]), .Q(R0));
  Register #(.Bits(32)) u_R1 (.D(multiplexer_2_out), .C(C), .en(or_1_out[1]), .Q(R1));
  Register #(.Bits(32)) u_R2 (.D(multiplexer_3_out), .C(C), .en(or_1_out[2]), .Q(R2));
  Register #(.Bits(32)) u_R3 (.D(multiplexer_4_out), .C(C), .en(or_1_out[3]), .Q(R3));
  Register #(.Bits(32)) u_R4 (.D(multiplexer_5_out), .C(C), .en(or_1_out[4]), .Q(R4));
  Register #(.Bits(32)) u_R5 (.D(multiplexer_6_out), .C(C), .en(or_1_out[5]), .Q(R5));
  Register #(.Bits(32)) u_R6 (.D(multiplexer_7_out), .C(C), .en(or_1_out[6]), .Q(R6));
  Register #(.Bits(32)) u_R7 (.D(multiplexer_8_out), .C(C), .en(or_1_out[7]), .Q(R7));
  Register #(.Bits(32)) u_R8 (.D(multiplexer_9_out), .C(C), .en(or_1_out[8]), .Q(R8));
  Register #(.Bits(32)) u_R9 (.D(multiplexer_10_out), .C(C), .en(or_1_out[9]), .Q(R9));
  Register #(.Bits(32)) u_R10 (.D(multiplexer_11_out), .C(C), .en(or_1_out[10]), .Q(R10));
  Register #(.Bits(32)) u_R11 (.D(multiplexer_12_out), .C(C), .en(or_1_out[11]), .Q(R11));
  Register #(.Bits(32)) u_R12 (.D(multiplexer_13_out), .C(C), .en(or_1_out[12]), .Q(R12));
  Register #(.Bits(32)) u_R13 (.D(multiplexer_14_out), .C(C), .en(or_1_out[13]), .Q(R13));
  Register #(.Bits(32)) u_R14 (.D(multiplexer_15_out), .C(C), .en(or_1_out[14]), .Q(R14));
  Register #(.Bits(32)) u_R15 (.D(multiplexer_16_out), .C(C), .en(or_1_out[15]), .Q(R15));
  Register #(.Bits(32)) u_R16 (.D(multiplexer_17_out), .C(C), .en(or_1_out[16]), .Q(R16));
  Register #(.Bits(32)) u_R17 (.D(multiplexer_18_out), .C(C), .en(or_1_out[17]), .Q(R17));
  Register #(.Bits(32)) u_R18 (.D(multiplexer_19_out), .C(C), .en(or_1_out[18]), .Q(R18));
  Register #(.Bits(32)) u_R19 (.D(multiplexer_20_out), .C(C), .en(or_1_out[19]), .Q(R19));
  Register #(.Bits(32)) u_R20 (.D(multiplexer_21_out), .C(C), .en(or_1_out[20]), .Q(R20));
  Register #(.Bits(32)) u_R21 (.D(multiplexer_22_out), .C(C), .en(or_1_out[21]), .Q(R21));
  Register #(.Bits(32)) u_R22 (.D(multiplexer_23_out), .C(C), .en(or_1_out[22]), .Q(R22));
  Register #(.Bits(32)) u_R23 (.D(multiplexer_24_out), .C(C), .en(or_1_out[23]), .Q(R23));
  Register #(.Bits(32)) u_R24 (.D(multiplexer_25_out), .C(C), .en(or_1_out[24]), .Q(R24));
  Register #(.Bits(32)) u_R25 (.D(multiplexer_26_out), .C(C), .en(or_1_out[25]), .Q(R25));

  assign valid[31:26] = {6{1'b0}};

  // Notes on the sheet:
  //   D1: data in
  //   D2: data in
  //   S1: register select
  //   S2: register select
  //   E1: store enable
  //   E2: store enable
  //   Del: delete
endmodule
