// Digital circuit register32x8.dig as structural Verilog
module register32x8 (
  input  C,
  input  [31:0] D1,
  input  [31:0] D2,
  input  [4:0] S1,
  input  [4:0] S2,
  input  E1,
  input  E2,
  input  [7:0] Del,
  output [31:0] R1,
  output [31:0] R2,
  output [31:0] R3,
  output [31:0] R4,
  output [31:0] R5,
  output [31:0] R6,
  output [31:0] R7,
  output [31:0] R8,
  output [31:0] valid32,
  output [7:0] valid8
);

  wire [1:0] multiplexer_9_out, multiplexer_10_out, multiplexer_11_out, multiplexer_12_out,
       multiplexer_13_out, multiplexer_14_out, multiplexer_15_out, multiplexer_16_out, Q1_q, Q2_q, Q3_q,
       Q4_q, Q5_q, Q6_q, Q7_q, Q8_q;
  wire [7:0] and_1_out, demultiplexer_1_out_0, demultiplexer_2_out_0, not_1_out, or_1_out, or_2_out;
  wire [31:0] multiplexer_1_out, multiplexer_2_out, multiplexer_3_out, multiplexer_4_out, multiplexer_5_out,
       multiplexer_6_out, multiplexer_7_out, multiplexer_8_out;

  Demultiplexer #(.Selector_Bits(3)) demultiplexer_1 (
    .sel(S1[2:0]), .in(E1), .out_0(demultiplexer_1_out_0[0]), .out_1(demultiplexer_1_out_0[1]),
    .out_2(demultiplexer_1_out_0[2]), .out_3(demultiplexer_1_out_0[3]), .out_4(demultiplexer_1_out_0[4]),
    .out_5(demultiplexer_1_out_0[5]), .out_6(demultiplexer_1_out_0[6]), .out_7(demultiplexer_1_out_0[7]));
  Demultiplexer #(.Selector_Bits(3)) demultiplexer_2 (
    .sel(S2[2:0]), .in(E2), .out_0(demultiplexer_2_out_0[0]), .out_1(demultiplexer_2_out_0[1]),
    .out_2(demultiplexer_2_out_0[2]), .out_3(demultiplexer_2_out_0[3]), .out_4(demultiplexer_2_out_0[4]),
    .out_5(demultiplexer_2_out_0[5]), .out_6(demultiplexer_2_out_0[6]), .out_7(demultiplexer_2_out_0[7]));
  assign or_1_out = demultiplexer_1_out_0 | demultiplexer_2_out_0;  // Or or_1, 8 bits wide
  assign not_1_out = ~Del;  // Not not_1, 8 bits wide
  assign and_1_out = not_1_out & or_1_out;  // And and_1, 8 bits wide
  assign or_2_out = Del | or_1_out;  // Or or_2, 8 bits wide
  Register V1 (.D(and_1_out[0]), .C(C), .en(or_2_out[0]), .Q(valid8[0]));
  Multiplexer #(.Bits(32)) multiplexer_1 (
    .sel(demultiplexer_2_out_0[0]), .in_0(D1), .in_1(D2), .out(multiplexer_1_out));
  Register V2 (.D(and_1_out[1]), .C(C), .en(or_2_out[1]), .Q(valid8[1]));
  Multiplexer #(.Bits(32)) multiplexer_2 (
    .sel(demultiplexer_2_out_0[1]), .in_0(D1), .in_1(D2), .out(multiplexer_2_out));
  Register V3 (.D(and_1_out[2]), .C(C), .en(or_2_out[2]), .Q(valid8[2]));
  Multiplexer #(.Bits(32)) multiplexer_3 (
    .sel(demultiplexer_2_out_0[2]), .in_0(D1), .in_1(D2), .out(multiplexer_3_out));
  Register V4 (.D(and_1_out[3]), .C(C), .en(or_2_out[3]), .Q(valid8[3]));
  Multiplexer #(.Bits(32)) multiplexer_4 (
    .sel(demultiplexer_2_out_0[3]), .in_0(D1), .in_1(D2), .out(multiplexer_4_out));
  Register V5 (.D(and_1_out[4]), .C(C), .en(or_2_out[4]), .Q(valid8[4]));
  Multiplexer #(.Bits(32)) multiplexer_5 (
    .sel(demultiplexer_2_out_0[4]), .in_0(D1), .in_1(D2), .out(multiplexer_5_out));
  Register V6 (.D(and_1_out[5]), .C(C), .en(or_2_out[5]), .Q(valid8[5]));
  Multiplexer #(.Bits(32)) multiplexer_6 (
    .sel(demultiplexer_2_out_0[5]), .in_0(D1), .in_1(D2), .out(multiplexer_6_out));
  Register V7 (.D(and_1_out[6]), .C(C), .en(or_2_out[6]), .Q(valid8[6]));
  Multiplexer #(.Bits(32)) multiplexer_7 (
    .sel(demultiplexer_2_out_0[6]), .in_0(D1), .in_1(D2), .out(multiplexer_7_out));
  Register V8 (.D(and_1_out[7]), .C(C), .en(or_2_out[7]), .Q(valid8[7]));
  Multiplexer #(.Bits(32)) multiplexer_8 (
    .sel(demultiplexer_2_out_0[7]), .in_0(D1), .in_1(D2), .out(multiplexer_8_out));
  Register #(.Bits(32)) u_R1 (.D(multiplexer_1_out), .C(C), .en(or_1_out[0]), .Q(R1));
  Register #(.Bits(32)) u_R2 (.D(multiplexer_2_out), .C(C), .en(or_1_out[1]), .Q(R2));
  Register #(.Bits(32)) u_R3 (.D(multiplexer_3_out), .C(C), .en(or_1_out[2]), .Q(R3));
  Register #(.Bits(32)) u_R4 (.D(multiplexer_4_out), .C(C), .en(or_1_out[3]), .Q(R4));
  Register #(.Bits(32)) u_R5 (.D(multiplexer_5_out), .C(C), .en(or_1_out[4]), .Q(R5));
  Register #(.Bits(32)) u_R6 (.D(multiplexer_6_out), .C(C), .en(or_1_out[5]), .Q(R6));
  Register #(.Bits(32)) u_R7 (.D(multiplexer_7_out), .C(C), .en(or_1_out[6]), .Q(R7));
  Register #(.Bits(32)) u_R8 (.D(multiplexer_8_out), .C(C), .en(or_1_out[7]), .Q(R8));
  Multiplexer #(.Bits(2)) multiplexer_9 (
    .sel(demultiplexer_2_out_0[0]), .in_0(S1[4:3]), .in_1(S2[4:3]), .out(multiplexer_9_out));
  Multiplexer #(.Bits(2)) multiplexer_10 (
    .sel(demultiplexer_2_out_0[1]), .in_0(S1[4:3]), .in_1(S2[4:3]), .out(multiplexer_10_out));
  Multiplexer #(.Bits(2)) multiplexer_11 (
    .sel(demultiplexer_2_out_0[2]), .in_0(S1[4:3]), .in_1(S2[4:3]), .out(multiplexer_11_out));
  Multiplexer #(.Bits(2)) multiplexer_12 (
    .sel(demultiplexer_2_out_0[3]), .in_0(S1[4:3]), .in_1(S2[4:3]), .out(multiplexer_12_out));
  Multiplexer #(.Bits(2)) multiplexer_13 (
    .sel(demultiplexer_2_out_0[4]), .in_0(S1[4:3]), .in_1(S2[4:3]), .out(multiplexer_13_out));
  Multiplexer #(.Bits(2)) multiplexer_14 (
    .sel(demultiplexer_2_out_0[5]), .in_0(S1[4:3]), .in_1(S2[4:3]), .out(multiplexer_14_out));
  Multiplexer #(.Bits(2)) multiplexer_15 (
    .sel(demultiplexer_2_out_0[6]), .in_0(S1[4:3]), .in_1(S2[4:3]), .out(multiplexer_15_out));
  Multiplexer #(.Bits(2)) multiplexer_16 (
    .sel(demultiplexer_2_out_0[7]), .in_0(S1[4:3]), .in_1(S2[4:3]), .out(multiplexer_16_out));
  Register #(.Bits(2)) Q1 (.D(multiplexer_9_out), .C(C), .en(or_1_out[0]), .Q(Q1_q));
  Register #(.Bits(2)) Q2 (.D(multiplexer_10_out), .C(C), .en(or_1_out[1]), .Q(Q2_q));
  Register #(.Bits(2)) Q3 (.D(multiplexer_11_out), .C(C), .en(or_1_out[2]), .Q(Q3_q));
  Register #(.Bits(2)) Q4 (.D(multiplexer_12_out), .C(C), .en(or_1_out[3]), .Q(Q4_q));
  Register #(.Bits(2)) Q5 (.D(multiplexer_13_out), .C(C), .en(or_1_out[4]), .Q(Q5_q));
  Register #(.Bits(2)) Q6 (.D(multiplexer_14_out), .C(C), .en(or_1_out[5]), .Q(Q6_q));
  Register #(.Bits(2)) Q7 (.D(multiplexer_15_out), .C(C), .en(or_1_out[6]), .Q(Q7_q));
  Register #(.Bits(2)) Q8 (.D(multiplexer_16_out), .C(C), .en(or_1_out[7]), .Q(Q8_q));
  Demultiplexer #(.Selector_Bits(2)) demultiplexer_3 (
    .sel(Q1_q), .in(valid8[0]), .out_0(valid32[0]), .out_1(valid32[8]), .out_2(valid32[16]),
    .out_3(valid32[24]));
  Demultiplexer #(.Selector_Bits(2)) demultiplexer_4 (
    .sel(Q2_q), .in(valid8[1]), .out_0(valid32[1]), .out_1(valid32[9]), .out_2(valid32[17]),
    .out_3(valid32[25]));
  Demultiplexer #(.Selector_Bits(2)) demultiplexer_5 (
    .sel(Q3_q), .in(valid8[2]), .out_0(valid32[2]), .out_1(valid32[10]), .out_2(valid32[18]),
    .out_3(valid32[26]));
  Demultiplexer #(.Selector_Bits(2)) demultiplexer_6 (
    .sel(Q4_q), .in(valid8[3]), .out_0(valid32[3]), .out_1(valid32[11]), .out_2(valid32[19]),
    .out_3(valid32[27]));
  Demultiplexer #(.Selector_Bits(2)) demultiplexer_7 (
    .sel(Q5_q), .in(valid8[4]), .out_0(valid32[4]), .out_1(valid32[12]), .out_2(valid32[20]),
    .out_3(valid32[28]));
  Demultiplexer #(.Selector_Bits(2)) demultiplexer_8 (
    .sel(Q6_q), .in(valid8[5]), .out_0(valid32[5]), .out_1(valid32[13]), .out_2(valid32[21]),
    .out_3(valid32[29]));
  Demultiplexer #(.Selector_Bits(2)) demultiplexer_9 (
    .sel(Q7_q), .in(valid8[6]), .out_0(valid32[6]), .out_1(valid32[14]), .out_2(valid32[22]),
    .out_3(valid32[30]));
  Demultiplexer #(.Selector_Bits(2)) demultiplexer_10 (
    .sel(Q8_q), .in(valid8[7]), .out_0(valid32[7]), .out_1(valid32[15]), .out_2(valid32[23]),
    .out_3(valid32[31]));

  // Other names for the same wires on the sheet: Q1[1:0] = S1[4:3]; Q2[1:0] = S2[4:3]

  // Notes on the sheet:
  //   D1: data in
  //   D2: data in
  //   S1: register select
  //   S2: register select
  //   E1: store enable
  //   E2: store enable
  //   Del: delete
endmodule
