// Digital circuit rotateL-4.dig as structural Verilog
module rotateL_4 (
  input  [3:0] in,
  input  [1:0] rot,
  output [3:0] out
);

  Multiplexer #(.Selector_Bits(2)) multiplexer_1 (
    .sel(rot), .in_0(in[0]), .in_1(in[3]), .in_2(in[2]), .in_3(in[1]), .out(out[0]));
  Multiplexer #(.Selector_Bits(2)) multiplexer_2 (
    .sel(rot), .in_0(in[1]), .in_1(in[0]), .in_2(in[3]), .in_3(in[2]), .out(out[1]));
  Multiplexer #(.Selector_Bits(2)) multiplexer_3 (
    .sel(rot), .in_0(in[2]), .in_1(in[1]), .in_2(in[0]), .in_3(in[3]), .out(out[2]));
  Multiplexer #(.Selector_Bits(2)) multiplexer_4 (
    .sel(rot), .in_0(in[3]), .in_1(in[2]), .in_2(in[1]), .in_3(in[0]), .out(out[3]));
endmodule
