// Digital circuit store-buffer.dig as structural Verilog
module store_buffer (
  input  W_d,
  input  C,
  input  [31:0] D,
  input  [31:0] A,
  input  [3:0] inst,
  input  [3:0] com1_id,
  input  [3:0] com2_id,
  input  com1,
  input  com2,
  input  ld_ep,
  input  [3:0] ld_id,
  input  epoch,
  input  [31:0] ld_addr,
  input  W_id,
  input  [3:0] inst_W,
  input  LD,
  input  [1:0] MD,
  output [31:0] D_O,
  output [31:0] A_O,
  output V,
  output full,
  output ld_V,
  output [31:0] ld_D,
  output [3:0] id_O,
  output ep_O,
  output [1:0] MD_O
);

  wire and_1_out, and_2_out, and_3_out, and_4_out, and_6_out, and_9_out, and_10_out, and_14_out, and_15_out,
       and_18_out, and_19_out, and_21_out, and_22_out, comparator_1_eq, comparator_2_eq, comparator_3_eq,
       comparator_4_eq, comparator_5_gt, comparator_5_lt, comparator_6_eq, comparator_7_eq, comparator_8_eq,
       comparator_9_eq, comparator_10_gt, comparator_10_lt, comparator_11_eq, comparator_12_eq,
       comparator_13_eq, comparator_14_eq, comparator_15_gt, comparator_15_lt, comparator_16_eq,
       comparator_17_eq, comparator_18_eq, comparator_19_eq, comparator_20_gt, comparator_20_lt, M1_CMP,
       M1_COM, M1_DE, M1_epoch, M1_IE, M1_RS, M1_SEL, M1_VO, M1_WTN, M2_CMP, M2_COM, M2_DE, M2_epoch, M2_IE,
       M2_RS, M2_SEL, M2_VO, M2_WTN, M3_CMP, M3_COM, M3_DE, M3_epoch, M3_IE, M3_RS, M3_SEL, M3_VO, M3_WTN,
       M4_CMP, M4_COM, M4_DE, M4_epoch, M4_IE, M4_RS, M4_SEL, M4_VO, M4_WTN, multiplexer_9_out,
       multiplexer_10_out, multiplexer_11_out, multiplexer_12_out, or_2_out, or_3_out, or_4_out, or_5_out,
       priorityencoder_2_any, priorityencoder_3_any, priorityencoder_4_any, xor_1_out, xor_2_out, xor_3_out,
       xor_4_out;
  wire [1:0] empty_id, M1_MD, M2_MD, M3_MD, M4_MD, priorityencoder_1_num, priorityencoder_2_num,
       priorityencoder_4_num, register_2_q, register_3_q, register_5_q, register_8_q, sel_com;
  wire [3:0] and_5_out, bitextender_1_out, bitselector_1_out, M1_inst, M2_inst, M3_inst, M4_inst,
       multiplexer_6_out, not_1_out, not_3_out, or_1_out, priority_4_1_out1, register_1_q;
  wire [31:0] M1_A, M1_D, M2_A, M2_D, M3_A, M3_D, M4_A, M4_D;

  Multiplexer #(.Selector_Bits(2), .Bits(4)) multiplexer_1 (
    .sel(sel_com), .in_0(M1_inst), .in_1(M2_inst), .in_2(M3_inst), .in_3(M4_inst), .out(id_O));
  PriorityEncoder #(.Selector_Bits(2)) priorityencoder_1 (
    .in0(M1_CMP), .in1(M2_CMP), .in2(M3_CMP), .in3(M4_CMP), .num(priorityencoder_1_num), .any(ld_V));
  PriorityEncoder #(.Selector_Bits(2)) priorityencoder_2 (
    .in0(M1_SEL), .in1(M2_SEL), .in2(M3_SEL), .in3(M4_SEL), .num(priorityencoder_2_num),
    .any(priorityencoder_2_any));
  Multiplexer #(.Selector_Bits(2), .Bits(32)) multiplexer_2 (
    .sel(sel_com), .in_0(M1_D), .in_1(M2_D), .in_2(M3_D), .in_3(M4_D), .out(D_O));
  priority_4 priority_4_1 (
    .on(1'b1), .in1(and_5_out[0]), .in2(and_5_out[1]), .in3(and_5_out[2]), .in4(and_5_out[3]),
    .out1(priority_4_1_out1[3]), .out2(priority_4_1_out1[2]), .out3(priority_4_1_out1[1]),
    .out4(priority_4_1_out1[0]));  // open: v
  and and_1 (and_1_out, not_3_out[3], 1'b1);
  assign not_1_out = ~{M4_VO, M3_VO, M2_VO, M1_VO};  // Not not_1, 4 bits wide
  Register register_1 (.D(and_1_out), .C(C), .en(or_1_out[3]), .Q(register_1_q[0]));
  BitSelector #(.Selector_Bits(2)) bitselector_1 (
    .in({M4_COM, M3_COM, M2_COM, M1_COM}), .sel(register_2_q), .out(bitselector_1_out[0]));
  Register #(.Bits(2)) register_2 (.D(empty_id), .C(C), .en(W_id), .Q(register_2_q));
  PriorityEncoder #(.Selector_Bits(2)) priorityencoder_3 (
    .in0(not_1_out[0]), .in1(not_1_out[1]), .in2(not_1_out[2]), .in3(not_1_out[3]), .num(empty_id),
    .any(priorityencoder_3_any));
  and and_2 (and_2_out, W_d, priorityencoder_2_any);
  and and_3 (and_3_out, not_3_out[2], register_1_q[0]);
  Register #(.Bits(2)) register_3 (.D(register_2_q), .C(C), .en(W_id), .Q(register_3_q));
  Multiplexer #(.Selector_Bits(2)) multiplexer_3 (
    .sel(sel_com), .in_0(M1_epoch), .in_1(M2_epoch), .in_2(M3_epoch), .in_3(M4_epoch), .out(ep_O));
  Multiplexer #(.Selector_Bits(2), .Bits(32)) multiplexer_4 (
    .sel(priorityencoder_1_num), .in_0(M1_D), .in_1(M2_D), .in_2(M3_D), .in_3(M4_D), .out(ld_D));
  not not_2 (full, priorityencoder_3_any);
  Demultiplexer #(.Selector_Bits(2)) demultiplexer_1 (
    .sel(priorityencoder_2_num), .in(and_2_out), .out_0(M1_DE), .out_1(M2_DE), .out_2(M3_DE), .out_3(M4_DE));
  Multiplexer #(.Selector_Bits(2), .Bits(32)) multiplexer_5 (
    .sel(sel_com), .in_0(M1_A), .in_1(M2_A), .in_2(M3_A), .in_3(M4_A), .out(A_O));
  Multiplexer #(.Bits(4)) multiplexer_6 (
    .sel(W_id), .in_0(priority_4_1_out1), .in_1({1'b0, priority_4_1_out1[3:1]}), .out(multiplexer_6_out));
  Register register_4 (.D(and_3_out), .C(C), .en(or_1_out[2]), .Q(register_1_q[1]));
  BitSelector #(.Selector_Bits(2)) bitselector_2 (
    .in({M4_COM, M3_COM, M2_COM, M1_COM}), .sel(register_3_q), .out(bitselector_1_out[1]));
  assign not_3_out = ~multiplexer_6_out;  // Not not_3, 4 bits wide
  BitExtender #(.inputBits(1), .outputBits(4)) bitextender_1 (.in(W_id), .out(bitextender_1_out));
  and and_4 (and_4_out, not_3_out[1], register_1_q[1]);
  Register #(.Bits(2)) register_5 (.D(register_3_q), .C(C), .en(W_id), .Q(register_5_q));
  Demultiplexer #(.Selector_Bits(2)) demultiplexer_2 (
    .sel(empty_id), .in(W_id), .out_0(M1_IE), .out_1(M2_IE), .out_2(M3_IE), .out_3(M4_IE));
  Demultiplexer #(.Selector_Bits(2)) demultiplexer_3 (
    .sel(sel_com), .in(V), .out_0(M1_RS), .out_1(M2_RS), .out_2(M3_RS), .out_3(M4_RS));
  Demultiplexer #(.Selector_Bits(2)) demultiplexer_4 (
    .sel(sel_com), .in(V), .out_0(M1_WTN), .out_1(M2_WTN), .out_2(M3_WTN), .out_3(M4_WTN));
  assign or_1_out = priority_4_1_out1 | bitextender_1_out;  // Or or_1, 4 bits wide
  Register register_6 (.D(and_4_out), .C(C), .en(or_1_out[1]), .Q(register_1_q[2]));
  assign and_5_out = register_1_q & bitselector_1_out;  // And and_5, 4 bits wide
  BitSelector #(.Selector_Bits(2)) bitselector_3 (
    .in({M4_COM, M3_COM, M2_COM, M1_COM}), .sel(register_5_q), .out(bitselector_1_out[2]));
  Multiplexer #(.Selector_Bits(2), .Bits(2)) multiplexer_7 (
    .sel(sel_com), .in_0(M1_MD), .in_1(M2_MD), .in_2(M3_MD), .in_3(M4_MD), .out(MD_O));
  and and_6 (and_6_out, not_3_out[0], register_1_q[2]);
  Register register_7 (.D(and_6_out), .C(C), .en(or_1_out[0]), .Q(register_1_q[3]));
  Register #(.Bits(2)) register_8 (.D(register_5_q), .C(C), .en(W_id), .Q(register_8_q));
  PriorityEncoder #(.Selector_Bits(2)) priorityencoder_4 (
    .in0(and_5_out[0]), .in1(and_5_out[1]), .in2(and_5_out[2]), .in3(and_5_out[3]),
    .num(priorityencoder_4_num), .any(priorityencoder_4_any));
  BitSelector #(.Selector_Bits(2)) bitselector_4 (
    .in({M4_COM, M3_COM, M2_COM, M1_COM}), .sel(register_8_q), .out(bitselector_1_out[3]));
  Multiplexer #(.Selector_Bits(2), .Bits(2)) multiplexer_8 (
    .sel(priorityencoder_4_num), .in_0(register_2_q), .in_1(register_3_q), .in_2(register_5_q),
    .in_3(register_8_q), .out(sel_com));
  RS_FF rs_ff_1 (.S(M1_IE), .C(C), .R(M1_RS), .Q(M1_VO));  // open: nQ
  and and_7 (M1_CMP, M1_VO, comparator_1_eq, multiplexer_9_out, M1_COM);
  Comparator #(.Bits(32)) comparator_1 (.a(ld_addr), .b(M1_A), .eq(comparator_1_eq));  // open: gt, lt
  Register #(.Bits(32)) register_9 (.D(A), .C(C), .en(M1_DE), .Q(M1_A));
  Register #(.Bits(32)) register_10 (.D(D), .C(C), .en(M1_DE), .Q(M1_D));
  Register #(.Bits(2)) register_11 (.D(MD), .C(C), .en(M1_DE), .Q(M1_MD));
  Comparator #(.Bits(4)) comparator_2 (.a(M1_inst), .b(inst_W), .eq(comparator_2_eq));  // open: gt, lt
  and and_8 (M1_SEL, M1_VO, comparator_2_eq);
  RS_FF rs_ff_2 (.S(or_2_out), .C(C), .R(M1_WTN), .Q(M1_COM));  // open: nQ
  or or_2 (or_2_out, and_10_out, and_9_out);
  and and_9 (and_9_out, comparator_3_eq, com1);
  Comparator #(.Bits(4)) comparator_3 (.a(M1_inst), .b(com1_id), .eq(comparator_3_eq));  // open: gt, lt
  and and_10 (and_10_out, comparator_4_eq, com2);
  Comparator #(.Bits(4)) comparator_4 (.a(M1_inst), .b(com2_id), .eq(comparator_4_eq));  // open: gt, lt
  Register #(.Bits(4)) register_12 (.D(inst), .C(C), .en(M1_IE), .Q(M1_inst));
  Register register_13 (.D(epoch), .C(C), .en(M1_IE), .Q(M1_epoch));
  Comparator #(.Bits(4)) comparator_5 (.a(ld_id), .b(M1_inst), .gt(comparator_5_gt), .lt(comparator_5_lt));  // open: eq
  xor xor_1 (xor_1_out, M1_epoch, ld_ep);
  and and_11 (V, priorityencoder_4_any, LD);
  Multiplexer multiplexer_9 (.sel(xor_1_out), .in_0(comparator_5_gt), .in_1(comparator_5_lt), .out(multiplexer_9_out));
  RS_FF rs_ff_3 (.S(M2_IE), .C(C), .R(M2_RS), .Q(M2_VO));  // open: nQ
  Comparator #(.Bits(32)) comparator_6 (.a(ld_addr), .b(M2_A), .eq(comparator_6_eq));  // open: gt, lt
  Register #(.Bits(32)) register_14 (.D(A), .C(C), .en(M2_DE), .Q(M2_A));
  Register #(.Bits(32)) register_15 (.D(D), .C(C), .en(M2_DE), .Q(M2_D));
  Register #(.Bits(2)) register_16 (.D(MD), .C(C), .en(M2_DE), .Q(M2_MD));
  Comparator #(.Bits(4)) comparator_7 (.a(M2_inst), .b(inst_W), .eq(comparator_7_eq));  // open: gt, lt
  RS_FF rs_ff_4 (.S(or_3_out), .C(C), .R(M2_WTN), .Q(M2_COM));  // open: nQ
  Comparator #(.Bits(4)) comparator_8 (.a(M2_inst), .b(com1_id), .eq(comparator_8_eq));  // open: gt, lt
  Comparator #(.Bits(4)) comparator_9 (.a(M2_inst), .b(com2_id), .eq(comparator_9_eq));  // open: gt, lt
  Register #(.Bits(4)) register_17 (.D(inst), .C(C), .en(M2_IE), .Q(M2_inst));
  Register register_18 (.D(epoch), .C(C), .en(M2_IE), .Q(M2_epoch));
  Comparator #(.Bits(4)) comparator_10 (
    .a(ld_id), .b(M2_inst), .gt(comparator_10_gt), .lt(comparator_10_lt));  // open: eq
  xor xor_2 (xor_2_out, M2_epoch, ld_ep);
  and and_12 (M2_CMP, M2_VO, comparator_6_eq, multiplexer_10_out, M2_COM);
  and and_13 (M2_SEL, M2_VO, comparator_7_eq);
  or or_3 (or_3_out, and_15_out, and_14_out);
  and and_14 (and_14_out, comparator_8_eq, com1);
  and and_15 (and_15_out, comparator_9_eq, com2);
  Multiplexer multiplexer_10 (
    .sel(xor_2_out), .in_0(comparator_10_gt), .in_1(comparator_10_lt), .out(multiplexer_10_out));
  RS_FF rs_ff_5 (.S(M3_IE), .C(C), .R(M3_RS), .Q(M3_VO));  // open: nQ
  Comparator #(.Bits(32)) comparator_11 (.a(ld_addr), .b(M3_A), .eq(comparator_11_eq));  // open: gt, lt
  Register #(.Bits(32)) register_19 (.D(A), .C(C), .en(M3_DE), .Q(M3_A));
  Register #(.Bits(32)) register_20 (.D(D), .C(C), .en(M3_DE), .Q(M3_D));
  Register #(.Bits(2)) register_21 (.D(MD), .C(C), .en(M3_DE), .Q(M3_MD));
  Comparator #(.Bits(4)) comparator_12 (.a(M3_inst), .b(inst_W), .eq(comparator_12_eq));  // open: gt, lt
  RS_FF rs_ff_6 (.S(or_4_out), .C(C), .R(M3_WTN), .Q(M3_COM));  // open: nQ
  Comparator #(.Bits(4)) comparator_13 (.a(M3_inst), .b(com1_id), .eq(comparator_13_eq));  // open: gt, lt
  Comparator #(.Bits(4)) comparator_14 (.a(M3_inst), .b(com2_id), .eq(comparator_14_eq));  // open: gt, lt
  Register #(.Bits(4)) register_22 (.D(inst), .C(C), .en(M3_IE), .Q(M3_inst));
  Register register_23 (.D(epoch), .C(C), .en(M3_IE), .Q(M3_epoch));
  Comparator #(.Bits(4)) comparator_15 (
    .a(ld_id), .b(M3_inst), .gt(comparator_15_gt), .lt(comparator_15_lt));  // open: eq
  xor xor_3 (xor_3_out, M3_epoch, ld_ep);
  and and_16 (M3_CMP, M3_VO, comparator_11_eq, multiplexer_11_out, M3_COM);
  and and_17 (M3_SEL, M3_VO, comparator_12_eq);
  or or_4 (or_4_out, and_19_out, and_18_out);
  and and_18 (and_18_out, comparator_13_eq, com1);
  and and_19 (and_19_out, comparator_14_eq, com2);
  Multiplexer multiplexer_11 (
    .sel(xor_3_out), .in_0(comparator_15_gt), .in_1(comparator_15_lt), .out(multiplexer_11_out));
  RS_FF rs_ff_7 (.S(M4_IE), .C(C), .R(M4_RS), .Q(M4_VO));  // open: nQ
  Comparator #(.Bits(32)) comparator_16 (.a(ld_addr), .b(M4_A), .eq(comparator_16_eq));  // open: gt, lt
  Register #(.Bits(32)) register_24 (.D(A), .C(C), .en(M4_DE), .Q(M4_A));
  Register #(.Bits(32)) register_25 (.D(D), .C(C), .en(M4_DE), .Q(M4_D));
  Register #(.Bits(2)) register_26 (.D(MD), .C(C), .en(M4_DE), .Q(M4_MD));
  Comparator #(.Bits(4)) comparator_17 (.a(M4_inst), .b(inst_W), .eq(comparator_17_eq));  // open: gt, lt
  and and_20 (M4_SEL, M4_VO, comparator_17_eq);
  RS_FF rs_ff_8 (.S(or_5_out), .C(C), .R(M4_WTN), .Q(M4_COM));  // open: nQ
  or or_5 (or_5_out, and_22_out, and_21_out);
  and and_21 (and_21_out, comparator_18_eq, com1);
  Comparator #(.Bits(4)) comparator_18 (.a(M4_inst), .b(com1_id), .eq(comparator_18_eq));  // open: gt, lt
  and and_22 (and_22_out, comparator_19_eq, com2);
  Comparator #(.Bits(4)) comparator_19 (.a(M4_inst), .b(com2_id), .eq(comparator_19_eq));  // open: gt, lt
  Register #(.Bits(4)) register_27 (.D(inst), .C(C), .en(M4_IE), .Q(M4_inst));
  Register register_28 (.D(epoch), .C(C), .en(M4_IE), .Q(M4_epoch));
  Comparator #(.Bits(4)) comparator_20 (
    .a(ld_id), .b(M4_inst), .gt(comparator_20_gt), .lt(comparator_20_lt));  // open: eq
  xor xor_4 (xor_4_out, M4_epoch, ld_ep);
  and and_23 (M4_CMP, M4_VO, comparator_16_eq, multiplexer_12_out, M4_COM);
  Multiplexer multiplexer_12 (
    .sel(xor_4_out), .in_0(comparator_20_gt), .in_1(comparator_20_lt), .out(multiplexer_12_out));

  // Other names for the same wires on the sheet: comp_addr[31:0] = ld_addr; comp_ep = ld_ep; comp_id[3:0] = ld_id;
  //   ld_O[31:0] = ld_D
endmodule
