// Digital circuit sub-4c32.dig as structural Verilog
module sub_4c32 (
  input  [3:0] b,
  input  [31:0] a,
  output [31:0] s
);

  wire add_1_c_o, not_3_out;
  wire [3:0] not_1_out;
  wire [27:0] lcgp_28_1_c, not_2_out;

  assign not_1_out = ~b;  // Not not_1, 4 bits wide
  Add #(.Bits(4)) add_1 (.a(a[3:0]), .b(not_1_out), .c_i(1'b1), .s(s[3:0]), .c_o(add_1_c_o));
  LCGP_28 lcgp_28_1 (.P(not_2_out), .C_n(not_3_out), .C(lcgp_28_1_c));  // open: P_o, C_o
  assign not_2_out = ~a[31:4];  // Not not_2, 28 bits wide
  not not_3 (not_3_out, add_1_c_o);
  assign s[31:4] = lcgp_28_1_c ^ a[31:4];  // XOr xor_1, 28 bits wide

  // Notes on the sheet:
  //   b: second input to add
  //   a: first input to add
  //   s: the result of the addition
endmodule
